// Digital circuit 1 of 24 decoder.dig as structural Verilog
module _1_of_24_decoder (
  input  clk
);

  wire _74138_1_pin7, _74138_1_pin9, _74138_1_pin10, _74138_1_pin11, _74138_1_pin12, _74138_1_pin13,
       _74138_1_pin14, _74138_1_pin15, _74138_2_pin7, _74138_2_pin9, _74138_2_pin10, _74138_2_pin11,
       _74138_2_pin12, _74138_2_pin13, _74138_2_pin14, _74138_2_pin15, _74138_3_pin7, _74138_3_pin9,
       _74138_3_pin10, _74138_3_pin11, _74138_3_pin13, _74138_3_pin14, _74138_3_pin15, _74163_1_pin14,
       and_1_out, U7_pin1, U7_pin11, U7_pin12, U7_pin13, U7_pin14, U7_pin15;

  _74163 U7 (
    .pin1(U7_pin1), .pin2(clk), .pin3(1'b0), .pin4(1'b0), .pin5(1'b0), .pin6(1'b0), .pin7(1'b1), .pin8(1'b0),
    .pin9(1'b1), .pin10(1'b1), .pin11(U7_pin11), .pin12(U7_pin12), .pin13(U7_pin13), .pin14(U7_pin14),
    .pin15(U7_pin15), .pin16(1'b1));
  _74163 _74163_1 (
    .pin1(U7_pin1), .pin2(clk), .pin3(1'b0), .pin4(1'b0), .pin5(1'b0), .pin6(1'b0), .pin7(1'b1), .pin8(1'b0),
    .pin9(1'b1), .pin10(U7_pin15), .pin14(_74163_1_pin14), .pin16(1'b1));  // open: pin11, pin12, pin13, pin15
  LED led_1 (.in(_74163_1_pin14));
  LED led_2 (.in(U7_pin12));
  LED led_3 (.in(U7_pin11));
  and and_1 (and_1_out, U7_pin11, _74163_1_pin14);
  LED led_4 (.in(U7_pin14));
  LED led_5 (.in(U7_pin13));
  _74138 _74138_1 (
    .pin1(U7_pin14), .pin2(U7_pin13), .pin3(U7_pin12), .pin4(U7_pin11), .pin5(_74163_1_pin14), .pin6(1'b1),
    .pin7(_74138_1_pin7), .pin8(1'b0), .pin9(_74138_1_pin9), .pin10(_74138_1_pin10), .pin11(_74138_1_pin11),
    .pin12(_74138_1_pin12), .pin13(_74138_1_pin13), .pin14(_74138_1_pin14), .pin15(_74138_1_pin15),
    .pin16(1'b1));
  _74138 _74138_2 (
    .pin1(U7_pin14), .pin2(U7_pin13), .pin3(U7_pin12), .pin4(_74163_1_pin14), .pin5(_74163_1_pin14),
    .pin6(U7_pin11), .pin7(_74138_2_pin7), .pin8(1'b0), .pin9(_74138_2_pin9), .pin10(_74138_2_pin10),
    .pin11(_74138_2_pin11), .pin12(_74138_2_pin12), .pin13(_74138_2_pin13), .pin14(_74138_2_pin14),
    .pin15(_74138_2_pin15), .pin16(1'b1));
  _74138 _74138_3 (
    .pin1(U7_pin14), .pin2(U7_pin13), .pin3(U7_pin12), .pin4(and_1_out), .pin5(and_1_out),
    .pin6(_74163_1_pin14), .pin7(_74138_3_pin7), .pin8(1'b0), .pin9(_74138_3_pin9), .pin10(_74138_3_pin10),
    .pin11(_74138_3_pin11), .pin12(U7_pin1), .pin13(_74138_3_pin13), .pin14(_74138_3_pin14),
    .pin15(_74138_3_pin15), .pin16(1'b1));
  LED led_6 (.in(_74138_1_pin15));
  LED led_7 (.in(_74138_1_pin14));
  LED led_8 (.in(_74138_1_pin13));
  LED led_9 (.in(_74138_1_pin12));
  LED led_10 (.in(_74138_1_pin11));
  LED led_11 (.in(_74138_1_pin10));
  LED led_12 (.in(_74138_1_pin9));
  LED led_13 (.in(_74138_1_pin7));
  LED led_14 (.in(_74138_2_pin15));
  LED led_15 (.in(_74138_2_pin14));
  LED led_16 (.in(_74138_2_pin13));
  LED led_17 (.in(_74138_2_pin12));
  LED led_18 (.in(_74138_2_pin11));
  LED led_19 (.in(_74138_2_pin10));
  LED led_20 (.in(_74138_2_pin9));
  LED led_21 (.in(_74138_2_pin7));
  LED led_22 (.in(_74138_3_pin15));
  LED led_23 (.in(_74138_3_pin14));
  LED led_24 (.in(_74138_3_pin13));
  LED led_25 (.in(U7_pin1));
  LED led_26 (.in(_74138_3_pin11));
  LED led_27 (.in(_74138_3_pin10));
  LED led_28 (.in(_74138_3_pin9));
  LED led_29 (.in(_74138_3_pin7));

  // Notes on the sheet:
  //   clk: Hz: 8
endmodule
