// Digital circuit 1 of 24 decoder_4.dig as structural Verilog
module _1_of_24_decoder_4 (
  input  clk
);

  wire _74139_1_pin4, _74139_1_pin5, _74139_1_pin6, _74139_1_pin9, _74139_1_pin10, _74139_1_pin11,
       _74139_1_pin12, _74163_1_pin14, diodeforward_1_out, nand_1_out, nand_2_out, nand_3_out, U7_pin1,
       U7_pin11, U7_pin12, U7_pin13, U7_pin14, U7_pin15;

  _74163 U7 (
    .pin1(U7_pin1), .pin2(clk), .pin3(1'b0), .pin4(1'b0), .pin5(1'b0), .pin6(1'b0), .pin7(1'b1), .pin8(1'b0),
    .pin9(1'b1), .pin10(1'b1), .pin11(U7_pin11), .pin12(U7_pin12), .pin13(U7_pin13), .pin14(U7_pin14),
    .pin15(U7_pin15), .pin16(1'b1));
  _74163 _74163_1 (
    .pin1(U7_pin1), .pin2(clk), .pin3(1'b0), .pin4(1'b0), .pin5(1'b0), .pin6(1'b0), .pin7(1'b1), .pin8(1'b0),
    .pin9(1'b1), .pin10(U7_pin15), .pin14(_74163_1_pin14), .pin16(1'b1));  // open: pin11, pin12, pin13, pin15
  LED led_1 (.in(_74163_1_pin14));
  LED led_2 (.in(U7_pin12));
  LED led_3 (.in(U7_pin11));
  LED led_4 (.in(U7_pin14));
  LED led_5 (.in(U7_pin13));
  nand nand_1 (nand_1_out, _74163_1_pin14, U7_pin12);
  DiodeForward diodeforward_1 (.in(U7_pin12), .out(diodeforward_1_out));
  DiodeForward diodeforward_2 (.in(U7_pin11), .out(diodeforward_1_out));
  DiodeForward diodeforward_3 (.in(_74163_1_pin14), .out(diodeforward_1_out));
  PullDown pulldown_1 (.out(diodeforward_1_out));
  nand nand_2 (nand_2_out, diodeforward_1_out, diodeforward_1_out);
  nand nand_3 (nand_3_out, nand_2_out, nand_2_out);
  _74139 _74139_1 (
    .pin1(nand_1_out), .pin2(U7_pin14), .pin3(U7_pin13), .pin4(_74139_1_pin4), .pin5(_74139_1_pin5),
    .pin6(_74139_1_pin6), .pin7(U7_pin1), .pin8(1'b0), .pin9(_74139_1_pin9), .pin10(_74139_1_pin10),
    .pin11(_74139_1_pin11), .pin12(_74139_1_pin12), .pin13(U7_pin13), .pin14(U7_pin14), .pin15(nand_3_out),
    .pin16(1'b1));
  LED led_6 (.in(_74139_1_pin12));
  LED led_7 (.in(_74139_1_pin11));
  LED led_8 (.in(_74139_1_pin10));
  LED led_9 (.in(_74139_1_pin9));
  LED led_10 (.in(_74139_1_pin4));
  LED led_11 (.in(_74139_1_pin5));
  LED led_12 (.in(_74139_1_pin6));
  LED led_13 (.in(U7_pin1));

  // Notes on the sheet:
  //   TP0
  //   TP1
  //   TP2
  //   TP3
  //   TP20
  //   TP21
  //   TP22
  //   TP23
endmodule
