// Digital circuit 1 of 24 decoder_6.dig as structural Verilog
module _1_of_24_decoder_6 (
  input  clk,
  output CLK_2,
  output GATED_CLK
);

  wire _74138_1_pin7, _74138_1_pin9, _74138_1_pin10, _74138_1_pin11, _74138_1_pin12, _74138_1_pin13,
       _74138_1_pin14, _74138_1_pin15, _74161_1_pin12, _74161_1_pin13, _74161_1_pin14, _74161_1_pin15,
       not_1_out, nRST, or_1_out, Q3, Q4, T0;

  _74161 _74161_1 (
    .pin1(nRST), .pin2(clk), .pin3(1'b0), .pin4(1'b0), .pin5(1'b0), .pin6(1'b0), .pin7(1'b1), .pin8(1'b0),
    .pin9(1'b1), .pin10(1'b1), .pin11(Q3), .pin12(_74161_1_pin12), .pin13(_74161_1_pin13),
    .pin14(_74161_1_pin14), .pin15(_74161_1_pin15), .pin16(1'b1));
  _74161 _74161_2 (
    .pin1(nRST), .pin2(clk), .pin3(1'b0), .pin4(1'b0), .pin5(1'b0), .pin6(1'b0), .pin7(1'b1), .pin8(1'b0),
    .pin9(1'b1), .pin10(_74161_1_pin15), .pin14(Q4), .pin16(1'b1));  // open: pin11, pin12, pin13, pin15
  nand nand_1 (nRST, Q3, Q4);
  _74138 _74138_1 (
    .pin1(_74161_1_pin14), .pin2(_74161_1_pin13), .pin3(_74161_1_pin12), .pin4(Q3), .pin5(Q4), .pin6(1'b1),
    .pin7(_74138_1_pin7), .pin8(1'b0), .pin9(_74138_1_pin9), .pin10(_74138_1_pin10), .pin11(_74138_1_pin11),
    .pin12(_74138_1_pin12), .pin13(_74138_1_pin13), .pin14(_74138_1_pin14), .pin15(_74138_1_pin15),
    .pin16(1'b1));
  not not_1 (not_1_out, clk);
  or or_1 (or_1_out, Q3, Q4);
  not not_2 (T0, nRST);
  and and_1 (GATED_CLK, not_1_out, or_1_out);
  LED TP0 (.in(_74138_1_pin15));
  LED TP1 (.in(_74138_1_pin14));
  LED TP2 (.in(_74138_1_pin13));
  LED TP3 (.in(_74138_1_pin12));
  LED TP4 (.in(_74138_1_pin11));
  LED TP5 (.in(_74138_1_pin10));
  LED TP6 (.in(_74138_1_pin9));
  LED TP7 (.in(_74138_1_pin7));
  LED led_1 (.in(GATED_CLK));

  assign CLK_2 = clk;

  // Other names for the same wires on the sheet: GCLK = GATED_CLK

  // Notes on the sheet:
  //   clk: Hz: 2
endmodule
