// Digital circuit 1-bit ALU_Adder.dig as structural Verilog
module _1_bit_ALU_Adder (
);

  wire and_1_out, and_2_out, and_3_out, and_4_out, dipswitch_1_out, dipswitch_2_out, dipswitch_3_out,
       dipswitch_4_out, dipswitch_5_out, dipswitch_6_out, or_1_out, or_2_out, xor_1_out, xor_2_out;

  DipSwitch dipswitch_1 (.out(dipswitch_1_out));
  DipSwitch dipswitch_2 (.out(dipswitch_2_out));
  DipSwitch dipswitch_3 (.out(dipswitch_3_out));
  DipSwitch dipswitch_4 (.out(dipswitch_4_out));
  DipSwitch dipswitch_5 (.out(dipswitch_5_out));
  xor xor_1 (xor_1_out, dipswitch_1_out, dipswitch_2_out);
  and and_1 (and_1_out, dipswitch_1_out, dipswitch_4_out, dipswitch_2_out);
  and and_2 (and_2_out, dipswitch_1_out, dipswitch_5_out, dipswitch_2_out);
  DipSwitch dipswitch_6 (.out(dipswitch_6_out));
  xor xor_2 (xor_2_out, xor_1_out, dipswitch_6_out);
  and and_3 (and_3_out, dipswitch_6_out, dipswitch_5_out, xor_1_out);
  and and_4 (and_4_out, xor_2_out, dipswitch_3_out);
  or or_1 (or_1_out, and_3_out, and_2_out);
  or or_2 (or_2_out, and_4_out, and_1_out);

  // Notes on the sheet:
  //   ^
  //   E
  //   0
  //   AND
  //   1
  //   XOR
  //   OR
  //   ADD
  //   &
  //   A
  //   B
  //   X
  //   XOR ^
  //   AND &
  //   Carry-Enable E
  //   I
  //   S
  //   C
  //   Combined Logic and Adder ALU. Uses 2.25 74xx chips per bit
  //   No extra carry propogation delay compared to a regular ripple-carry adder.
  //   Carry-In I
  //   NOT
  //   ?*
  //   <- basically just using XOR
  //   with a constant 1 on the B input
  //   <- *extra unused mode shown for completeness
  //   S is A & B
  //   C is A | B
  //   C Carry-Out
  //   S SUM
endmodule
