// Digital circuit 1-bit ALU_Adder_wTests.dig as structural Verilog
module _1_bit_ALU_Adder_wTests (
  input  A,
  input  B,
  input  K,
  input  N,
  input  E,
  input  I,
  output S,
  output C
);

  wire and_1_out, and_2_out, and_3_out, and_4_out, xor_1_out, xor_2_out;

  xor xor_1 (xor_1_out, A, B);
  and and_1 (and_1_out, A, N, B);
  and and_2 (and_2_out, A, E, B);
  xor xor_2 (xor_2_out, xor_1_out, I);
  and and_3 (and_3_out, I, E, xor_1_out);
  and and_4 (and_4_out, xor_2_out, K);
  or or_1 (C, and_3_out, and_2_out);
  or or_2 (S, and_4_out, and_1_out);

  // Notes on the sheet:
  //   ^
  //   E
  //   0
  //   AND
  //   1
  //   XOR
  //   OR
  //   ADD
  //   &
  //   A
  //   B
  //   X
  //   XOR ^
  //   AND &
  //   Carry-Enable E
  //   I
  //   S
  //   C
  //   Combined Logic and Adder ALU. Uses 2.25 74xx chips per bit
  //   No extra carry propagation delay compared to a regular ripple-carry adder.
  //   Carry-In I
  //   NOT
  //   <- basically just using XOR
  //   with a constant 1 on the B input
  //   C Carry-Out
  //   S SUM
endmodule

/* Test case ALU Test:
            E  K  N  A             B             I          S                                    C
            0  0  0  x             x             x          0                                    0
repeat(2)   0  1  0  bits(1,n)     1             0          bits(1,!(n&1))                       0
repeat(4)   0  0  1  bits(1,n>>1)  bits(1,n)     x          bits(1,(n>>1)&(n&1))                 0
repeat(4)   0  1  0  bits(1,n>>1)  bits(1,n)     0          bits(1,(n>>1)^(n&1))                 0
repeat(4)   0  1  1  bits(1,n>>1)  bits(1,n)     0          bits(1,(n>>1)|(n&1))                 0
repeat(8)   1  1  0  bits(1,n>>2)  bits(1,n>>1)  bits(1,n)  bits(1,((n>>2)&1)+((n>>1)&1)+(n&1))  bits(1,(((n>>2)&1)+((n>>1)&1)+(n&1))>>1)
*/
