// Digital circuit 10-clock sequencer.dig as structural Verilog
module _10_clock_sequencer (
  input  clk,
  output GCLK,
  output T5,
  output T1,
  output T0,
  output T2,
  output T3,
  output T4,
  output T7,
  output T6,
  output T8,
  output T9
);

  wire GATE, MR, nand_2_out, nand_4_out, not_1_out, not_2_out, T0_t, T1_t, T2_t, T3_t, T4_t, T5_t, T6_t,
       T7_t, T8_t;

  _744017 U16 (
    .pin1(T5_t), .pin2(T1_t), .pin3(T0_t), .pin4(T2_t), .pin5(T6_t), .pin6(T7_t), .pin7(T3_t), .pin8(1'b0),
    .pin9(T8_t), .pin10(T4_t), .pin11(MR), .pin13(1'b0), .pin14(clk), .pin15(MR), .pin16(1'b1));  // open: pin12
  not not_1 (not_1_out, T1_t);
  not not_2 (not_2_out, MR);
  nand nand_1 (GCLK, GATE, nand_2_out);
  nand nand_2 (nand_2_out, clk, clk);
  nand nand_3 (GATE, not_1_out, nand_4_out);
  nand nand_4 (nand_4_out, GATE, not_2_out);
  not not_3 (T0, T0_t);
  not not_4 (T1, T1_t);
  not not_5 (T2, T2_t);
  not not_6 (T3, T3_t);
  not not_7 (T4, T4_t);
  not not_8 (T5, T5_t);
  not not_9 (T6, T6_t);
  not not_10 (T7, T7_t);
  not not_11 (T8, T8_t);
  not not_12 (T9, MR);

  // Other names for the same wires on the sheet: T9_t = MR

  // Notes on the sheet:
  //   Clock Sequencer (5 ICs)
endmodule
