// Digital circuit 16-bit accumulator.dig as structural Verilog
module _16_bit_accumulator (
);

  wire and_1_out, Aout, CLR, Fout, GCLK, nCLRPC;
  wire [3:0] U13_pin5, U13_pin12, U14_pin6;
  wire [3:1] U14_pin12;

  and and_1 (and_1_out, CLR, nCLRPC);
  _74164 U13 (
    .pin1(1'b1), .pin2(Fout), .pin3(U13_pin5[3]), .pin4(U13_pin5[2]), .pin5(U13_pin5[1]), .pin6(U13_pin5[0]),
    .pin7(1'b0), .pin8(GCLK), .pin9(and_1_out), .pin10(U13_pin12[3]), .pin11(U13_pin12[2]),
    .pin12(U13_pin12[1]), .pin13(U13_pin12[0]), .pin14(1'b1));
  Seven_Seg_Hex seven_seg_hex_1 (.d(U13_pin5), .dp(1'b0));
  Seven_Seg_Hex seven_seg_hex_2 (.d(U13_pin12), .dp(1'b0));
  Seven_Seg_Hex seven_seg_hex_3 (.d(U14_pin6), .dp(1'b0));
  Seven_Seg_Hex seven_seg_hex_4 (.d({U14_pin12, Aout}), .dp(1'b0));
  _74164 U14 (
    .pin1(1'b1), .pin2(U13_pin12[0]), .pin3(U14_pin6[3]), .pin4(U14_pin6[2]), .pin5(U14_pin6[1]),
    .pin6(U14_pin6[0]), .pin7(1'b0), .pin8(GCLK), .pin9(and_1_out), .pin10(U14_pin12[3]),
    .pin11(U14_pin12[2]), .pin12(U14_pin12[1]), .pin13(Aout), .pin14(1'b1));

  // Notes on the sheet:
  //   ACCUMULATOR
  //   U35B
endmodule
