// Digital circuit 161_clock_sequencer.dig as structural Verilog
module _161_clock_sequencer (
  input  clk,
  output T0,
  output T1,
  output T2,
  output T3,
  output T4,
  output T5,
  output T6,
  output T7,
  output nFRONT,
  output nREAR
);

  wire _74161_1_pin12, _74161_1_pin13, _74161_1_pin14, n1SD, nand_1_out, nand_3_out, nRES, RES, U7_pin15;

  _74161 _74161_1 (
    .pin1(1'b1), .pin2(clk), .pin3(1'b1), .pin4(1'b1), .pin5(1'b1), .pin6(1'b1), .pin7(1'b1), .pin8(1'b0),
    .pin9(1'b1), .pin10(1'b1), .pin12(_74161_1_pin12), .pin13(_74161_1_pin13), .pin14(_74161_1_pin14),
    .pin16(1'b1));  // open: pin11, pin15
  _74138 _74138_1 (
    .pin1(_74161_1_pin14), .pin2(_74161_1_pin13), .pin3(_74161_1_pin12), .pin4(1'b0), .pin5(1'b0),
    .pin6(1'b1), .pin7(T7), .pin8(1'b0), .pin9(T6), .pin10(T5), .pin11(T4), .pin12(T3), .pin13(T2),
    .pin14(T1), .pin15(T0), .pin16(1'b1));
  nand nand_1 (nand_1_out, T0, nFRONT);
  nand nand_2 (nFRONT, nand_1_out, T3);
  nand nand_3 (nand_3_out, T5, nREAR);
  nand nand_4 (nREAR, nand_3_out, T7);
  _74161 U7 (
    .pin2(clk), .pin3(1'b0), .pin4(1'b0), .pin5(1'b0), .pin6(1'b0), .pin7(1'b1), .pin8(1'b0), .pin9(1'b1),
    .pin10(1'b1), .pin15(U7_pin15), .pin16(1'b1));  // open: pin1, pin11, pin12, pin13, pin14
  Reset reset_1 (.out(n1SD));
  _7474 U9 (
    .pin1(1'b1), .pin2(U7_pin15), .pin3(clk), .pin4(n1SD), .pin5(RES), .pin6(nRES), .pin7(1'b0),
    .pin10(1'b1), .pin11(1'b1), .pin12(1'b1), .pin13(1'b1), .pin14(1'b1));  // open: pin8, pin9

  // Notes on the sheet:
  //   clk: Hz: 2
  //   Clock Sequencer
  //   Carry FF
endmodule
