// Digital circuit 16_bit_program counter_40_pin.dig as structural Verilog
module _16_bit_program_counter_40_pin (
  input  DATA_0,
  input  CK,
  input  nLD_COUNT,
  input  DATA_1,
  input  DATA_2,
  input  DATA_3,
  input  RES,
  input  INC,
  input  DATA_4,
  input  DATA_5,
  input  DATA_6,
  input  DATA_7,
  input  DATA_8,
  input  DATA_9,
  input  DATA_10,
  input  DATA_11,
  input  DATA_12,
  input  DATA_13,
  input  DATA_14,
  input  DATA_15,
  input  VDD,
  input  GND,
  input  VSS,
  output Q0,
  output Q1,
  output Q2,
  output Q3,
  output Q4,
  output Q5,
  output Q6,
  output Q7,
  output Q8,
  output Q9,
  output Q10,
  output Q11,
  output Q12,
  output Q13,
  output Q14,
  output Q15,
  output TCO
);

  wire nand_1_out, nand_2_out, nand_3_out, nand_4_out, nand_5_out, nand_6_out, nand_7_out, nand_8_out,
       nand_9_out, nand_10_out, nand_11_out, nand_12_out, nand_13_out, nand_14_out, nand_15_out, nand_16_out,
       nand_17_out, nand_18_out, nand_19_out, nand_20_out, nand_21_out, nand_22_out, nand_23_out,
       nand_24_out, nand_25_out, nand_26_out, nand_27_out, nand_28_out, nand_29_out, nand_30_out,
       nand_31_out, nand_32_out, nand_33_out, nand_34_out, nand_35_out, nand_36_out, nand_37_out,
       nand_38_out, nand_39_out, nand_40_out, nand_41_out, nand_42_out, nand_43_out, nand_44_out,
       nand_45_out, nand_46_out, nand_47_out, nand_48_out, nand_49_out, nand_50_out, nand_51_out,
       nand_52_out, nand_53_out, nand_54_out, nand_55_out, nand_56_out, nand_57_out, nand_58_out,
       nand_59_out, nand_60_out, nand_61_out, nand_62_out, nand_63_out, nand_65_out, nand_66_out,
       nand_67_out, nand_68_out, nand_69_out, nand_70_out, nand_71_out, nand_72_out, nand_73_out,
       nand_74_out, nand_75_out, nand_76_out, nand_77_out, nand_78_out, nand_79_out, nand_80_out,
       nand_81_out, nand_82_out, nand_83_out, nand_84_out, nand_85_out, nand_86_out, nand_87_out,
       nand_88_out, nand_89_out, nand_90_out, nand_91_out, nand_92_out, nand_93_out, nand_94_out,
       nand_95_out, nand_96_out, nand_97_out, nand_98_out, nand_99_out, nand_100_out, nand_101_out,
       nand_102_out, nand_103_out, nand_104_out, nand_105_out, nand_106_out, nand_107_out, nand_108_out,
       nand_109_out, nand_110_out, nand_111_out, nand_112_out, nand_113_out, nand_114_out, nand_115_out,
       nand_116_out, nand_117_out, nand_118_out, nand_119_out, nand_120_out, nand_121_out, nand_122_out,
       nand_123_out, nand_124_out, nand_125_out, nand_126_out, nand_127_out, nand_128_out, nand_129_out,
       nand_130_out, nand_131_out, nand_132_out, nand_133_out, nand_134_out, nand_135_out, nand_136_out,
       nand_137_out, nand_138_out, nand_139_out, nand_140_out, nand_141_out, nand_142_out, nand_143_out,
       nand_144_out, nand_145_out, nand_146_out, nand_147_out, nand_148_out, nand_149_out, nand_150_out,
       nand_151_out, nand_152_out, nand_153_out, nand_154_out, nand_155_out, nand_156_out, nand_157_out,
       nand_158_out, nand_159_out, nand_160_out, nand_161_out, nand_162_out, nand_163_out, nand_164_out,
       nand_165_out, nand_166_out, nand_167_out, nand_168_out, nand_169_out, nand_170_out, nand_171_out,
       nand_172_out, nand_173_out, nand_174_out, nand_175_out, nand_176_out, nand_177_out, nand_178_out,
       nand_179_out, nand_180_out, nand_181_out, nand_182_out, nand_183_out, nand_184_out, nand_185_out,
       nand_186_out, nand_187_out, nand_188_out, nand_189_out, nand_190_out, nand_191_out, nand_192_out,
       nand_193_out, nand_194_out, nand_195_out, nand_196_out, nand_197_out, nand_198_out, nand_199_out,
       nand_200_out, nand_201_out, nand_202_out, nand_203_out, nand_204_out, nand_205_out, nand_206_out,
       nand_207_out, nand_208_out, nand_209_out, nand_210_out, nand_211_out, nand_212_out, nand_213_out,
       nand_214_out, nand_215_out, nand_216_out, nand_217_out, nand_218_out, nand_219_out, nand_220_out,
       nand_221_out, nand_222_out, nand_223_out, nand_224_out, nand_225_out, nand_226_out, nand_227_out,
       nand_228_out, nand_229_out, nand_230_out, nand_231_out, nand_232_out, nand_233_out, nand_234_out,
       nand_235_out, nand_236_out, nand_237_out, nand_238_out, nand_239_out, nand_240_out, nand_241_out,
       nand_242_out, nand_243_out, nand_244_out, nand_245_out, nand_246_out, nand_247_out, nand_248_out,
       nand_249_out, nand_250_out, nand_251_out, nand_252_out, nand_253_out, nand_254_out, nand_255_out,
       nand_256_out, nand_257_out, nand_258_out, nand_259_out, nand_260_out, nand_261_out, nand_262_out,
       nand_263_out, nand_264_out, nand_265_out, nand_266_out, nand_267_out, nand_268_out, nand_269_out,
       nand_270_out, nand_271_out, nand_272_out, nand_273_out, nand_274_out, nand_275_out, nand_276_out,
       nand_277_out, nand_278_out, nand_279_out, nand_280_out, nand_281_out, nand_282_out, nand_283_out,
       nand_284_out, nand_285_out, nand_286_out, nand_287_out, nand_288_out, nand_289_out, nand_290_out,
       nand_291_out, nand_292_out, nand_293_out, nand_294_out, nand_295_out, nand_296_out, nand_297_out,
       nand_298_out, nand_299_out, nand_300_out, nand_301_out, nand_302_out, nand_303_out, nand_304_out,
       nand_306_out, nand_308_out, nand_310_out, nand_312_out, nand_314_out, nand_316_out, nand_318_out,
       nand_320_out, nand_322_out, nand_324_out, nand_326_out, nand_328_out, nand_330_out, nand_332_out,
       nand_334_out, nand_336_out;

  PowerSupply powersupply_1 (.VDD(VDD), .GND(GND));
  nand nand_1 (nand_1_out, INC, Q0);
  nand nand_2 (nand_2_out, nand_19_out, Q1);
  nand nand_3 (nand_3_out, nand_22_out, Q2);
  nand nand_4 (nand_4_out, nand_25_out, Q3);
  nand nand_5 (nand_5_out, nand_28_out, Q4);
  nand nand_6 (nand_6_out, nand_31_out, Q5);
  nand nand_7 (nand_7_out, nand_34_out, Q6);
  nand nand_8 (nand_8_out, nand_37_out, Q7);
  nand nand_9 (nand_9_out, nand_40_out, Q8);
  nand nand_10 (nand_10_out, nand_43_out, Q9);
  nand nand_11 (nand_11_out, nand_46_out, Q10);
  nand nand_12 (nand_12_out, nand_49_out, Q11);
  nand nand_13 (nand_13_out, nand_52_out, Q12);
  nand nand_14 (nand_14_out, nand_55_out, Q13);
  nand nand_15 (nand_15_out, nand_58_out, Q14);
  nand nand_16 (nand_16_out, nand_61_out, Q15);
  nand nand_17 (nand_17_out, INC, nand_1_out);
  nand nand_18 (nand_18_out, nand_1_out, Q0);
  nand nand_19 (nand_19_out, nand_1_out, nand_1_out);
  nand nand_20 (nand_20_out, nand_19_out, nand_2_out);
  nand nand_21 (nand_21_out, nand_2_out, Q1);
  nand nand_22 (nand_22_out, nand_2_out, nand_2_out);
  nand nand_23 (nand_23_out, nand_22_out, nand_3_out);
  nand nand_24 (nand_24_out, nand_3_out, Q2);
  nand nand_25 (nand_25_out, nand_3_out, nand_3_out);
  nand nand_26 (nand_26_out, nand_25_out, nand_4_out);
  nand nand_27 (nand_27_out, nand_4_out, Q3);
  nand nand_28 (nand_28_out, nand_4_out, nand_4_out);
  nand nand_29 (nand_29_out, nand_28_out, nand_5_out);
  nand nand_30 (nand_30_out, nand_5_out, Q4);
  nand nand_31 (nand_31_out, nand_5_out, nand_5_out);
  nand nand_32 (nand_32_out, nand_31_out, nand_6_out);
  nand nand_33 (nand_33_out, nand_6_out, Q5);
  nand nand_34 (nand_34_out, nand_6_out, nand_6_out);
  nand nand_35 (nand_35_out, nand_34_out, nand_7_out);
  nand nand_36 (nand_36_out, nand_7_out, Q6);
  nand nand_37 (nand_37_out, nand_7_out, nand_7_out);
  nand nand_38 (nand_38_out, nand_37_out, nand_8_out);
  nand nand_39 (nand_39_out, nand_8_out, Q7);
  nand nand_40 (nand_40_out, nand_8_out, nand_8_out);
  nand nand_41 (nand_41_out, nand_40_out, nand_9_out);
  nand nand_42 (nand_42_out, nand_9_out, Q8);
  nand nand_43 (nand_43_out, nand_9_out, nand_9_out);
  nand nand_44 (nand_44_out, nand_43_out, nand_10_out);
  nand nand_45 (nand_45_out, nand_10_out, Q9);
  nand nand_46 (nand_46_out, nand_10_out, nand_10_out);
  nand nand_47 (nand_47_out, nand_46_out, nand_11_out);
  nand nand_48 (nand_48_out, nand_11_out, Q10);
  nand nand_49 (nand_49_out, nand_11_out, nand_11_out);
  nand nand_50 (nand_50_out, nand_49_out, nand_12_out);
  nand nand_51 (nand_51_out, nand_12_out, Q11);
  nand nand_52 (nand_52_out, nand_12_out, nand_12_out);
  nand nand_53 (nand_53_out, nand_52_out, nand_13_out);
  nand nand_54 (nand_54_out, nand_13_out, Q12);
  nand nand_55 (nand_55_out, nand_13_out, nand_13_out);
  nand nand_56 (nand_56_out, nand_55_out, nand_14_out);
  nand nand_57 (nand_57_out, nand_14_out, Q13);
  nand nand_58 (nand_58_out, nand_14_out, nand_14_out);
  nand nand_59 (nand_59_out, nand_58_out, nand_15_out);
  nand nand_60 (nand_60_out, nand_15_out, Q14);
  nand nand_61 (nand_61_out, nand_15_out, nand_15_out);
  nand nand_62 (nand_62_out, nand_61_out, nand_16_out);
  nand nand_63 (nand_63_out, nand_16_out, Q15);
  nand nand_64 (TCO, nand_16_out, nand_16_out);
  nand nand_65 (nand_65_out, nand_17_out, nand_18_out);
  nand nand_66 (nand_66_out, nand_20_out, nand_21_out);
  nand nand_67 (nand_67_out, nand_23_out, nand_24_out);
  nand nand_68 (nand_68_out, nand_26_out, nand_27_out);
  nand nand_69 (nand_69_out, nand_29_out, nand_30_out);
  nand nand_70 (nand_70_out, nand_32_out, nand_33_out);
  nand nand_71 (nand_71_out, nand_35_out, nand_36_out);
  nand nand_72 (nand_72_out, nand_38_out, nand_39_out);
  nand nand_73 (nand_73_out, nand_41_out, nand_42_out);
  nand nand_74 (nand_74_out, nand_44_out, nand_45_out);
  nand nand_75 (nand_75_out, nand_47_out, nand_48_out);
  nand nand_76 (nand_76_out, nand_50_out, nand_51_out);
  nand nand_77 (nand_77_out, nand_53_out, nand_54_out);
  nand nand_78 (nand_78_out, nand_56_out, nand_57_out);
  nand nand_79 (nand_79_out, nand_59_out, nand_60_out);
  nand nand_80 (nand_80_out, nand_62_out, nand_63_out);
  nand nand_81 (nand_81_out, RES, DATA_0);
  nand nand_82 (nand_82_out, RES, DATA_1);
  nand nand_83 (nand_83_out, RES, DATA_2);
  nand nand_84 (nand_84_out, RES, DATA_3);
  nand nand_85 (nand_85_out, RES, DATA_4);
  nand nand_86 (nand_86_out, RES, DATA_5);
  nand nand_87 (nand_87_out, RES, DATA_6);
  nand nand_88 (nand_88_out, RES, DATA_7);
  nand nand_89 (nand_89_out, RES, DATA_8);
  nand nand_90 (nand_90_out, RES, DATA_9);
  nand nand_91 (nand_91_out, RES, DATA_10);
  nand nand_92 (nand_92_out, RES, DATA_11);
  nand nand_93 (nand_93_out, RES, DATA_12);
  nand nand_94 (nand_94_out, RES, DATA_13);
  nand nand_95 (nand_95_out, RES, DATA_14);
  nand nand_96 (nand_96_out, RES, DATA_15);
  nand nand_97 (nand_97_out, nLD_COUNT, nLD_COUNT);
  nand nand_98 (nand_98_out, nand_81_out, nand_81_out);
  nand nand_99 (nand_99_out, nLD_COUNT, nLD_COUNT);
  nand nand_100 (nand_100_out, nand_82_out, nand_82_out);
  nand nand_101 (nand_101_out, nLD_COUNT, nLD_COUNT);
  nand nand_102 (nand_102_out, nand_83_out, nand_83_out);
  nand nand_103 (nand_103_out, nLD_COUNT, nLD_COUNT);
  nand nand_104 (nand_104_out, nand_84_out, nand_84_out);
  nand nand_105 (nand_105_out, nLD_COUNT, nLD_COUNT);
  nand nand_106 (nand_106_out, nand_85_out, nand_85_out);
  nand nand_107 (nand_107_out, nLD_COUNT, nLD_COUNT);
  nand nand_108 (nand_108_out, nand_86_out, nand_86_out);
  nand nand_109 (nand_109_out, nLD_COUNT, nLD_COUNT);
  nand nand_110 (nand_110_out, nand_87_out, nand_87_out);
  nand nand_111 (nand_111_out, nLD_COUNT, nLD_COUNT);
  nand nand_112 (nand_112_out, nand_88_out, nand_88_out);
  nand nand_113 (nand_113_out, nLD_COUNT, nLD_COUNT);
  nand nand_114 (nand_114_out, nand_89_out, nand_89_out);
  nand nand_115 (nand_115_out, nLD_COUNT, nLD_COUNT);
  nand nand_116 (nand_116_out, nand_90_out, nand_90_out);
  nand nand_117 (nand_117_out, nLD_COUNT, nLD_COUNT);
  nand nand_118 (nand_118_out, nand_91_out, nand_91_out);
  nand nand_119 (nand_119_out, nLD_COUNT, nLD_COUNT);
  nand nand_120 (nand_120_out, nand_92_out, nand_92_out);
  nand nand_121 (nand_121_out, nLD_COUNT, nLD_COUNT);
  nand nand_122 (nand_122_out, nand_93_out, nand_93_out);
  nand nand_123 (nand_123_out, nLD_COUNT, nLD_COUNT);
  nand nand_124 (nand_124_out, nand_94_out, nand_94_out);
  nand nand_125 (nand_125_out, nLD_COUNT, nLD_COUNT);
  nand nand_126 (nand_126_out, nand_95_out, nand_95_out);
  nand nand_127 (nand_127_out, nLD_COUNT, nLD_COUNT);
  nand nand_128 (nand_128_out, nand_96_out, nand_96_out);
  nand nand_129 (nand_129_out, nand_65_out, nLD_COUNT);
  nand nand_130 (nand_130_out, nand_97_out, nand_98_out);
  nand nand_131 (nand_131_out, nand_66_out, nLD_COUNT);
  nand nand_132 (nand_132_out, nand_99_out, nand_100_out);
  nand nand_133 (nand_133_out, nand_67_out, nLD_COUNT);
  nand nand_134 (nand_134_out, nand_101_out, nand_102_out);
  nand nand_135 (nand_135_out, nand_68_out, nLD_COUNT);
  nand nand_136 (nand_136_out, nand_103_out, nand_104_out);
  nand nand_137 (nand_137_out, nand_69_out, nLD_COUNT);
  nand nand_138 (nand_138_out, nand_105_out, nand_106_out);
  nand nand_139 (nand_139_out, nand_70_out, nLD_COUNT);
  nand nand_140 (nand_140_out, nand_107_out, nand_108_out);
  nand nand_141 (nand_141_out, nand_71_out, nLD_COUNT);
  nand nand_142 (nand_142_out, nand_109_out, nand_110_out);
  nand nand_143 (nand_143_out, nand_72_out, nLD_COUNT);
  nand nand_144 (nand_144_out, nand_111_out, nand_112_out);
  nand nand_145 (nand_145_out, nand_73_out, nLD_COUNT);
  nand nand_146 (nand_146_out, nand_113_out, nand_114_out);
  nand nand_147 (nand_147_out, nand_74_out, nLD_COUNT);
  nand nand_148 (nand_148_out, nand_115_out, nand_116_out);
  nand nand_149 (nand_149_out, nand_75_out, nLD_COUNT);
  nand nand_150 (nand_150_out, nand_117_out, nand_118_out);
  nand nand_151 (nand_151_out, nand_76_out, nLD_COUNT);
  nand nand_152 (nand_152_out, nand_119_out, nand_120_out);
  nand nand_153 (nand_153_out, nand_77_out, nLD_COUNT);
  nand nand_154 (nand_154_out, nand_121_out, nand_122_out);
  nand nand_155 (nand_155_out, nand_78_out, nLD_COUNT);
  nand nand_156 (nand_156_out, nand_123_out, nand_124_out);
  nand nand_157 (nand_157_out, nand_79_out, nLD_COUNT);
  nand nand_158 (nand_158_out, nand_125_out, nand_126_out);
  nand nand_159 (nand_159_out, nand_80_out, nLD_COUNT);
  nand nand_160 (nand_160_out, nand_127_out, nand_128_out);
  nand nand_161 (nand_161_out, nand_129_out, nand_130_out);
  nand nand_162 (nand_162_out, nand_131_out, nand_132_out);
  nand nand_163 (nand_163_out, nand_133_out, nand_134_out);
  nand nand_164 (nand_164_out, nand_135_out, nand_136_out);
  nand nand_165 (nand_165_out, nand_137_out, nand_138_out);
  nand nand_166 (nand_166_out, nand_139_out, nand_140_out);
  nand nand_167 (nand_167_out, nand_141_out, nand_142_out);
  nand nand_168 (nand_168_out, nand_143_out, nand_144_out);
  nand nand_169 (nand_169_out, nand_145_out, nand_146_out);
  nand nand_170 (nand_170_out, nand_147_out, nand_148_out);
  nand nand_171 (nand_171_out, nand_149_out, nand_150_out);
  nand nand_172 (nand_172_out, nand_151_out, nand_152_out);
  nand nand_173 (nand_173_out, nand_153_out, nand_154_out);
  nand nand_174 (nand_174_out, nand_155_out, nand_156_out);
  nand nand_175 (nand_175_out, nand_157_out, nand_158_out);
  nand nand_176 (nand_176_out, nand_159_out, nand_160_out);
  nand nand_177 (nand_177_out, CK, CK);
  nand nand_178 (nand_178_out, nand_161_out, nand_161_out);
  nand nand_179 (nand_179_out, CK, CK);
  nand nand_180 (nand_180_out, nand_162_out, nand_162_out);
  nand nand_181 (nand_181_out, CK, CK);
  nand nand_182 (nand_182_out, nand_163_out, nand_163_out);
  nand nand_183 (nand_183_out, CK, CK);
  nand nand_184 (nand_184_out, nand_164_out, nand_164_out);
  nand nand_185 (nand_185_out, CK, CK);
  nand nand_186 (nand_186_out, nand_165_out, nand_165_out);
  nand nand_187 (nand_187_out, CK, CK);
  nand nand_188 (nand_188_out, nand_166_out, nand_166_out);
  nand nand_189 (nand_189_out, CK, CK);
  nand nand_190 (nand_190_out, nand_167_out, nand_167_out);
  nand nand_191 (nand_191_out, CK, CK);
  nand nand_192 (nand_192_out, nand_168_out, nand_168_out);
  nand nand_193 (nand_193_out, CK, CK);
  nand nand_194 (nand_194_out, nand_169_out, nand_169_out);
  nand nand_195 (nand_195_out, CK, CK);
  nand nand_196 (nand_196_out, nand_170_out, nand_170_out);
  nand nand_197 (nand_197_out, CK, CK);
  nand nand_198 (nand_198_out, nand_171_out, nand_171_out);
  nand nand_199 (nand_199_out, CK, CK);
  nand nand_200 (nand_200_out, nand_172_out, nand_172_out);
  nand nand_201 (nand_201_out, CK, CK);
  nand nand_202 (nand_202_out, nand_173_out, nand_173_out);
  nand nand_203 (nand_203_out, CK, CK);
  nand nand_204 (nand_204_out, nand_174_out, nand_174_out);
  nand nand_205 (nand_205_out, CK, CK);
  nand nand_206 (nand_206_out, nand_175_out, nand_175_out);
  nand nand_207 (nand_207_out, CK, CK);
  nand nand_208 (nand_208_out, nand_176_out, nand_176_out);
  nand nand_209 (nand_209_out, nand_161_out, nand_177_out);
  nand nand_210 (nand_210_out, nand_177_out, nand_178_out);
  nand nand_211 (nand_211_out, nand_162_out, nand_179_out);
  nand nand_212 (nand_212_out, nand_179_out, nand_180_out);
  nand nand_213 (nand_213_out, nand_163_out, nand_181_out);
  nand nand_214 (nand_214_out, nand_181_out, nand_182_out);
  nand nand_215 (nand_215_out, nand_164_out, nand_183_out);
  nand nand_216 (nand_216_out, nand_183_out, nand_184_out);
  nand nand_217 (nand_217_out, nand_165_out, nand_185_out);
  nand nand_218 (nand_218_out, nand_185_out, nand_186_out);
  nand nand_219 (nand_219_out, nand_166_out, nand_187_out);
  nand nand_220 (nand_220_out, nand_187_out, nand_188_out);
  nand nand_221 (nand_221_out, nand_167_out, nand_189_out);
  nand nand_222 (nand_222_out, nand_189_out, nand_190_out);
  nand nand_223 (nand_223_out, nand_168_out, nand_191_out);
  nand nand_224 (nand_224_out, nand_191_out, nand_192_out);
  nand nand_225 (nand_225_out, nand_169_out, nand_193_out);
  nand nand_226 (nand_226_out, nand_193_out, nand_194_out);
  nand nand_227 (nand_227_out, nand_170_out, nand_195_out);
  nand nand_228 (nand_228_out, nand_195_out, nand_196_out);
  nand nand_229 (nand_229_out, nand_171_out, nand_197_out);
  nand nand_230 (nand_230_out, nand_197_out, nand_198_out);
  nand nand_231 (nand_231_out, nand_172_out, nand_199_out);
  nand nand_232 (nand_232_out, nand_199_out, nand_200_out);
  nand nand_233 (nand_233_out, nand_173_out, nand_201_out);
  nand nand_234 (nand_234_out, nand_201_out, nand_202_out);
  nand nand_235 (nand_235_out, nand_174_out, nand_203_out);
  nand nand_236 (nand_236_out, nand_203_out, nand_204_out);
  nand nand_237 (nand_237_out, nand_175_out, nand_205_out);
  nand nand_238 (nand_238_out, nand_205_out, nand_206_out);
  nand nand_239 (nand_239_out, nand_176_out, nand_207_out);
  nand nand_240 (nand_240_out, nand_207_out, nand_208_out);
  nand nand_241 (nand_241_out, nand_209_out, nand_242_out);
  nand nand_242 (nand_242_out, nand_241_out, nand_210_out);
  nand nand_243 (nand_243_out, nand_211_out, nand_244_out);
  nand nand_244 (nand_244_out, nand_243_out, nand_212_out);
  nand nand_245 (nand_245_out, nand_213_out, nand_246_out);
  nand nand_246 (nand_246_out, nand_245_out, nand_214_out);
  nand nand_247 (nand_247_out, nand_215_out, nand_248_out);
  nand nand_248 (nand_248_out, nand_247_out, nand_216_out);
  nand nand_249 (nand_249_out, nand_217_out, nand_250_out);
  nand nand_250 (nand_250_out, nand_249_out, nand_218_out);
  nand nand_251 (nand_251_out, nand_219_out, nand_252_out);
  nand nand_252 (nand_252_out, nand_251_out, nand_220_out);
  nand nand_253 (nand_253_out, nand_221_out, nand_254_out);
  nand nand_254 (nand_254_out, nand_253_out, nand_222_out);
  nand nand_255 (nand_255_out, nand_223_out, nand_256_out);
  nand nand_256 (nand_256_out, nand_255_out, nand_224_out);
  nand nand_257 (nand_257_out, nand_225_out, nand_258_out);
  nand nand_258 (nand_258_out, nand_257_out, nand_226_out);
  nand nand_259 (nand_259_out, nand_227_out, nand_260_out);
  nand nand_260 (nand_260_out, nand_259_out, nand_228_out);
  nand nand_261 (nand_261_out, nand_229_out, nand_262_out);
  nand nand_262 (nand_262_out, nand_261_out, nand_230_out);
  nand nand_263 (nand_263_out, nand_231_out, nand_264_out);
  nand nand_264 (nand_264_out, nand_263_out, nand_232_out);
  nand nand_265 (nand_265_out, nand_233_out, nand_266_out);
  nand nand_266 (nand_266_out, nand_265_out, nand_234_out);
  nand nand_267 (nand_267_out, nand_235_out, nand_268_out);
  nand nand_268 (nand_268_out, nand_267_out, nand_236_out);
  nand nand_269 (nand_269_out, nand_237_out, nand_270_out);
  nand nand_270 (nand_270_out, nand_269_out, nand_238_out);
  nand nand_271 (nand_271_out, nand_239_out, nand_272_out);
  nand nand_272 (nand_272_out, nand_271_out, nand_240_out);
  nand nand_273 (nand_273_out, nand_241_out, CK);
  nand nand_274 (nand_274_out, CK, nand_242_out);
  nand nand_275 (nand_275_out, nand_243_out, CK);
  nand nand_276 (nand_276_out, CK, nand_244_out);
  nand nand_277 (nand_277_out, nand_245_out, CK);
  nand nand_278 (nand_278_out, CK, nand_246_out);
  nand nand_279 (nand_279_out, nand_247_out, CK);
  nand nand_280 (nand_280_out, CK, nand_248_out);
  nand nand_281 (nand_281_out, nand_249_out, CK);
  nand nand_282 (nand_282_out, CK, nand_250_out);
  nand nand_283 (nand_283_out, nand_251_out, CK);
  nand nand_284 (nand_284_out, CK, nand_252_out);
  nand nand_285 (nand_285_out, nand_253_out, CK);
  nand nand_286 (nand_286_out, CK, nand_254_out);
  nand nand_287 (nand_287_out, nand_255_out, CK);
  nand nand_288 (nand_288_out, CK, nand_256_out);
  nand nand_289 (nand_289_out, nand_257_out, CK);
  nand nand_290 (nand_290_out, CK, nand_258_out);
  nand nand_291 (nand_291_out, nand_259_out, CK);
  nand nand_292 (nand_292_out, CK, nand_260_out);
  nand nand_293 (nand_293_out, nand_261_out, CK);
  nand nand_294 (nand_294_out, CK, nand_262_out);
  nand nand_295 (nand_295_out, nand_263_out, CK);
  nand nand_296 (nand_296_out, CK, nand_264_out);
  nand nand_297 (nand_297_out, nand_265_out, CK);
  nand nand_298 (nand_298_out, CK, nand_266_out);
  nand nand_299 (nand_299_out, nand_267_out, CK);
  nand nand_300 (nand_300_out, CK, nand_268_out);
  nand nand_301 (nand_301_out, nand_269_out, CK);
  nand nand_302 (nand_302_out, CK, nand_270_out);
  nand nand_303 (nand_303_out, nand_271_out, CK);
  nand nand_304 (nand_304_out, CK, nand_272_out);
  nand nand_305 (Q0, nand_273_out, nand_306_out);
  nand nand_306 (nand_306_out, Q0, nand_274_out);
  nand nand_307 (Q1, nand_275_out, nand_308_out);
  nand nand_308 (nand_308_out, Q1, nand_276_out);
  nand nand_309 (Q2, nand_277_out, nand_310_out);
  nand nand_310 (nand_310_out, Q2, nand_278_out);
  nand nand_311 (Q3, nand_279_out, nand_312_out);
  nand nand_312 (nand_312_out, Q3, nand_280_out);
  nand nand_313 (Q4, nand_281_out, nand_314_out);
  nand nand_314 (nand_314_out, Q4, nand_282_out);
  nand nand_315 (Q5, nand_283_out, nand_316_out);
  nand nand_316 (nand_316_out, Q5, nand_284_out);
  nand nand_317 (Q6, nand_285_out, nand_318_out);
  nand nand_318 (nand_318_out, Q6, nand_286_out);
  nand nand_319 (Q7, nand_287_out, nand_320_out);
  nand nand_320 (nand_320_out, Q7, nand_288_out);
  nand nand_321 (Q8, nand_289_out, nand_322_out);
  nand nand_322 (nand_322_out, Q8, nand_290_out);
  nand nand_323 (Q9, nand_291_out, nand_324_out);
  nand nand_324 (nand_324_out, Q9, nand_292_out);
  nand nand_325 (Q10, nand_293_out, nand_326_out);
  nand nand_326 (nand_326_out, Q10, nand_294_out);
  nand nand_327 (Q11, nand_295_out, nand_328_out);
  nand nand_328 (nand_328_out, Q11, nand_296_out);
  nand nand_329 (Q12, nand_297_out, nand_330_out);
  nand nand_330 (nand_330_out, Q12, nand_298_out);
  nand nand_331 (Q13, nand_299_out, nand_332_out);
  nand nand_332 (nand_332_out, Q13, nand_300_out);
  nand nand_333 (Q14, nand_301_out, nand_334_out);
  nand nand_334 (nand_334_out, Q14, nand_302_out);
  nand nand_335 (Q15, nand_303_out, nand_336_out);
  nand nand_336 (nand_336_out, Q15, nand_304_out);

  assign VSS = GND;

  // Notes on the sheet:
  //   DATA_0: pin 39
  //   CK: pin 18
  //   nLD_COUNT: pin 19
  //   DATA_1: pin 38
  //   DATA_2: pin 37
  //   DATA_3: pin 36
  //   RES: pin 22
  //   INC: pin 20
  //   DATA_4: pin 35
  //   DATA_5: pin 34
  //   DATA_6: pin 33
  //   DATA_7: pin 32
  //   Q0: pin 1
  //   Q1: pin 2
  //   Q2: pin 3
  //   Q3: pin 4
  //   Q4: pin 5
  //   Q5: pin 6
  //   Q6: pin 7
  //   Q7: pin 8
  //   DATA_8: pin 31
  //   DATA_9: pin 29
  //   DATA_10: pin 28
  //   DATA_11: pin 27
  //   DATA_12: pin 26
  //   DATA_13: pin 25
  //   DATA_14: pin 24
  //   DATA_15: pin 23
  //   Q8: pin 9
  //   Q9: pin 11
  //   Q10: pin 12
  //   Q11: pin 13
  //   Q12: pin 14
  //   Q13: pin 15
  //   Q14: pin 16
  //   Q15: pin 17
  //   TCO: pin 21
  //   VDD: pin 40, default 1
  //   GND: pin 11
  //   VSS: pin 30
  //   16-bit Program Counter Slice in 336 Gates
endmodule
