// Digital circuit 1802_registers.dig as structural Verilog
module _1802_registers (
  input  D,
  input  U,
  input  D7,
  input  D6,
  input  D5,
  input  D4,
  input  D3,
  input  D2,
  input  D1,
  input  D0,
  input  CLR,
  input  D15,
  input  D14,
  input  D13,
  input  D12,
  input  D11,
  input  D10,
  input  D9,
  input  D8,
  input  nLD,
  input  in_23,
  input  in_24,
  input  in_25,
  input  in_26,
  input  in_27,
  input  in_28,
  input  in_29,
  input  A_B,
  input  nEN,
  input  in_32,
  input  CLK,
  input  in_34,
  output B,
  output C
);

  wire _74173_1_pin11, _74173_1_pin12, _74173_1_pin13, _74173_1_pin14, _74173_2_pin11, _74173_2_pin12,
       _74173_2_pin13, _74173_2_pin14, _74173_3_pin11, _74173_3_pin12, _74173_3_pin13, _74173_3_pin14,
       _74173_4_pin11, _74173_4_pin12, _74173_4_pin13, _74173_4_pin14, _74193_1_pin12, _74193_1_pin13,
       _74193_2_pin12, _74193_2_pin13, _74193_3_pin12, _74193_3_pin13, A0, A1, A2, A3, A4, A5, A6, A7, A8,
       A9, A10, A11, A12, A13, A14, A15, D0_t, D1_t, D2_t, D3_t, D4_t, D5_t, D6_t, D7_t, D8_t, D9_t, D10_t,
       D11_t, D12_t, D13_t, D14_t, D15_t, Q0, Q1, Q2, Q3, Q4, Q5, Q6, Q7, Q8, Q9, Q10, Q11, Q12, Q13, Q14,
       Q15;

  Seven_Seg_Hex seven_seg_hex_1 (.d({A15, A14, A13, A12}), .dp(1'b0));
  Seven_Seg_Hex seven_seg_hex_2 (.d({A11, A10, A9, A8}), .dp(1'b0));
  Seven_Seg_Hex seven_seg_hex_3 (.d({A7, A6, A5, A4}), .dp(1'b0));
  Seven_Seg_Hex seven_seg_hex_4 (.d({A3, A2, A1, A0}), .dp(1'b0));
  Seven_Seg_Hex seven_seg_hex_5 (.d({D15, D14, D13, D12}), .dp(1'b0));
  Seven_Seg_Hex seven_seg_hex_6 (.d({D11, D10, D9, D8}), .dp(1'b0));
  Seven_Seg_Hex seven_seg_hex_7 (.d({D7, D6, D5, D4}), .dp(1'b0));
  Seven_Seg_Hex seven_seg_hex_8 (.d({D3, D2, D1, D0}), .dp(1'b0));
  Seven_Seg_Hex seven_seg_hex_9 (.d(4'b0000), .dp(1'b0));
  Seven_Seg_Hex seven_seg_hex_10 (.d({in_26, in_25, in_24, in_23}), .dp(1'b0));
  Seven_Seg_Hex seven_seg_hex_11 (.d({Q15, Q14, Q13, Q12}), .dp(1'b0));
  Seven_Seg_Hex seven_seg_hex_12 (.d({Q11, Q10, Q9, Q8}), .dp(1'b0));
  Seven_Seg_Hex seven_seg_hex_13 (.d({Q7, Q6, Q5, Q4}), .dp(1'b0));
  Seven_Seg_Hex seven_seg_hex_14 (.d({Q3, Q2, Q1, Q0}), .dp(1'b0));
  Seven_Seg_Hex seven_seg_hex_15 (.d({D15_t, D14_t, D13_t, D12_t}), .dp(1'b0));
  Seven_Seg_Hex seven_seg_hex_16 (.d({D11_t, D10_t, D9_t, D8_t}), .dp(1'b0));
  Seven_Seg_Hex seven_seg_hex_17 (.d({D7_t, D6_t, D5_t, D4_t}), .dp(1'b0));
  Seven_Seg_Hex seven_seg_hex_18 (.d({D3_t, D2_t, D1_t, D0_t}), .dp(1'b0));
  _74193 _74193_1 (
    .pin1(A1), .pin2(Q1), .pin3(Q0), .pin4(D), .pin5(U), .pin6(Q2), .pin7(Q3), .pin8(1'b0), .pin9(A3),
    .pin10(A2), .pin11(nLD), .pin12(_74193_1_pin12), .pin13(_74193_1_pin13), .pin14(CLR), .pin15(A0),
    .pin16(1'b1));
  _74193 _74193_2 (
    .pin1(A5), .pin2(Q5), .pin3(Q4), .pin4(_74193_1_pin13), .pin5(_74193_1_pin12), .pin6(Q6), .pin7(Q7),
    .pin8(1'b0), .pin9(A7), .pin10(A6), .pin11(nLD), .pin12(_74193_2_pin12), .pin13(_74193_2_pin13),
    .pin14(CLR), .pin15(A4), .pin16(1'b1));
  _74193 _74193_3 (
    .pin1(A9), .pin2(Q9), .pin3(Q8), .pin4(_74193_2_pin13), .pin5(_74193_2_pin12), .pin6(Q10), .pin7(Q11),
    .pin8(1'b0), .pin9(A11), .pin10(A10), .pin11(nLD), .pin12(_74193_3_pin12), .pin13(_74193_3_pin13),
    .pin14(CLR), .pin15(A8), .pin16(1'b1));
  _74193 _74193_4 (
    .pin1(A13), .pin2(Q13), .pin3(Q12), .pin4(_74193_3_pin13), .pin5(_74193_3_pin12), .pin6(Q14), .pin7(Q15),
    .pin8(1'b0), .pin9(A15), .pin10(A14), .pin11(nLD), .pin12(C), .pin13(B), .pin14(CLR), .pin15(A12),
    .pin16(1'b1));
  _74173 _74173_1 (
    .pin1(in_29), .pin2(in_29), .pin3(A0), .pin4(A1), .pin5(A2), .pin6(A3), .pin7(CLK), .pin8(1'b0),
    .pin9(nEN), .pin10(nEN), .pin11(_74173_1_pin11), .pin12(_74173_1_pin12), .pin13(_74173_1_pin13),
    .pin14(_74173_1_pin14), .pin15(in_32), .pin16(1'b1));
  _74173 _74173_2 (
    .pin1(in_29), .pin2(in_29), .pin3(A4), .pin4(A5), .pin5(A6), .pin6(A7), .pin7(CLK), .pin8(1'b0),
    .pin9(nEN), .pin10(nEN), .pin11(_74173_2_pin11), .pin12(_74173_2_pin12), .pin13(_74173_2_pin13),
    .pin14(_74173_2_pin14), .pin15(in_32), .pin16(1'b1));
  _74173 _74173_3 (
    .pin1(in_29), .pin2(in_29), .pin3(A8), .pin4(A9), .pin5(A10), .pin6(A11), .pin7(CLK), .pin8(1'b0),
    .pin9(nEN), .pin10(nEN), .pin11(_74173_3_pin11), .pin12(_74173_3_pin12), .pin13(_74173_3_pin13),
    .pin14(_74173_3_pin14), .pin15(in_32), .pin16(1'b1));
  _74173 _74173_4 (
    .pin1(in_29), .pin2(in_29), .pin3(A12), .pin4(A13), .pin5(A14), .pin6(A15), .pin7(CLK), .pin8(1'b0),
    .pin9(nEN), .pin10(nEN), .pin11(_74173_4_pin11), .pin12(_74173_4_pin12), .pin13(_74173_4_pin13),
    .pin14(_74173_4_pin14), .pin15(in_32), .pin16(1'b1));
  _74219 _74219_1 (
    .pin1(in_23), .pin2(in_28), .pin3(in_27), .pin4(D0_t), .pin5(_74173_1_pin14), .pin6(D1_t),
    .pin7(_74173_1_pin13), .pin8(1'b0), .pin9(_74173_1_pin12), .pin10(D2_t), .pin11(_74173_1_pin11),
    .pin12(D3_t), .pin13(in_26), .pin14(in_25), .pin15(in_24), .pin16(1'b1));
  _74219 _74219_2 (
    .pin1(in_23), .pin2(in_28), .pin3(in_27), .pin4(D4_t), .pin5(_74173_2_pin14), .pin6(D5_t),
    .pin7(_74173_2_pin13), .pin8(1'b0), .pin9(_74173_2_pin12), .pin10(D6_t), .pin11(_74173_2_pin11),
    .pin12(D7_t), .pin13(in_26), .pin14(in_25), .pin15(in_24), .pin16(1'b1));
  _74219 _74219_3 (
    .pin1(in_23), .pin2(in_28), .pin3(in_27), .pin4(D8_t), .pin5(_74173_3_pin14), .pin6(D9_t),
    .pin7(_74173_3_pin13), .pin8(1'b0), .pin9(_74173_3_pin12), .pin10(D10_t), .pin11(_74173_3_pin11),
    .pin12(D11_t), .pin13(in_26), .pin14(in_25), .pin15(in_24), .pin16(1'b1));
  _74219 _74219_4 (
    .pin1(in_23), .pin2(in_28), .pin3(in_27), .pin4(D12_t), .pin5(_74173_4_pin14), .pin6(D13_t),
    .pin7(_74173_4_pin13), .pin8(1'b0), .pin9(_74173_4_pin12), .pin10(D14_t), .pin11(_74173_4_pin11),
    .pin12(D15_t), .pin13(in_26), .pin14(in_25), .pin15(in_24), .pin16(1'b1));
  _74157 _74157_1 (
    .pin1(A_B), .pin2(Q0), .pin3(D0), .pin4(D0_t), .pin5(Q1), .pin6(D1), .pin7(D1_t), .pin8(1'b0),
    .pin9(D2_t), .pin10(D2), .pin11(Q2), .pin12(D3_t), .pin13(D3), .pin14(Q3), .pin15(in_34), .pin16(1'b1));
  _74157 _74157_2 (
    .pin1(A_B), .pin2(Q4), .pin3(D4), .pin4(D4_t), .pin5(Q5), .pin6(D5), .pin7(D5_t), .pin8(1'b0),
    .pin9(D6_t), .pin10(D6), .pin11(Q6), .pin12(D7_t), .pin13(D7), .pin14(Q7), .pin15(in_34), .pin16(1'b1));
  _74157 _74157_3 (
    .pin1(A_B), .pin2(Q8), .pin3(D8), .pin4(D8_t), .pin5(Q9), .pin6(D9), .pin7(D9_t), .pin8(1'b0),
    .pin9(D10_t), .pin10(D10), .pin11(Q10), .pin12(D11_t), .pin13(D11), .pin14(Q11), .pin15(in_34),
    .pin16(1'b1));
  _74157 _74157_4 (
    .pin1(A_B), .pin2(Q12), .pin3(D12), .pin4(D12_t), .pin5(Q13), .pin6(D13), .pin7(D13_t), .pin8(1'b0),
    .pin9(D14_t), .pin10(D14), .pin11(Q14), .pin12(D15_t), .pin13(D15), .pin14(Q15), .pin15(in_34),
    .pin16(1'b1));

  // Other names for the same wires on the sheet: B0 = D0; B1 = D1; B2 = D2; B3 = D3; B4 = D4; B5 = D5; B6 = D6;
  //   B7 = D7; B8 = D8; B9 = D9; B10 = D10; B11 = D11; B12 = D12; B13 = D13; B14 = D14; B15 = D15; S0 = in_23;
  //   S1 = in_24; S2 = in_25; S3 = in_26

  // Notes on the sheet:
  //   RAM ADDRESS
  //   BUS DATA
  //   REG
  //   COUNTER OUTPUT
  //   DATA
  //   U/D COUNTER
  //   ADDRESS REGISTER
  //   16 x 16-BIT RAM
  //   2 WAY MUX
endmodule
