// Digital circuit 1_bit_ALU_1.dig as structural Verilog
module _1_bit_ALU_1 (
  input  Cin,
  input  A,
  input  B,
  input  XOR,
  input  AND,
  input  Cen,
  output SUM,
  output Cout
);

  wire and_1_out, and_2_out, and_3_out, and_4_out, xor_1_out, xor_2_out;

  xor xor_1 (xor_1_out, A, B);
  and and_1 (and_1_out, A, AND, B);
  and and_2 (and_2_out, A, Cen, B);
  xor xor_2 (xor_2_out, xor_1_out, Cin);
  and and_3 (and_3_out, Cin, Cen, xor_1_out);
  and and_4 (and_4_out, xor_2_out, XOR);
  or or_1 (Cout, and_3_out, and_2_out);
  or or_2 (SUM, and_4_out, and_1_out);

  // Notes on the sheet:
  //   ^
  //   E
  //   0
  //   AND
  //   1
  //   XOR
  //   OR
  //   ADD
  //   A
  //   B
  //   XOR ^
  //   AND &
  //   Carry-Enable E
  //   &
  //   X
  //   I
  //   S
  //   C
  //   Combined Logic and Adder ALU. Uses 2.25 74xx chips per bit
  //   No extra carry propogation delay compared to a regular ripple-carry adder.
  //   Carry-In I
  //   NOT
  //   ?*
  //   <- basically just using XOR
  //   with a constant 1 on the B input
  //   <- *extra unused mode shown for completeness
  //   S is A & B
  //   C is A | B
  //   C Carry-Out
  //   S SUM
endmodule
