// Digital circuit 1bit_multi_gate.dig as structural Verilog
module _1bit_multi_gate (
  input  A0,
  input  B0,
  input  I0,
  input  I1,
  input  I0_2,
  input  B0_2,
  input  A0_2,
  input  S0,
  input  S1,
  input  A0_3,
  input  nE1,
  input  A1,
  input  A2,
  input  A3,
  input  A,
  input  B,
  input  Cin,
  input  Cin_2,
  input  I1_2,
  input  A4,
  input  B1,
  input  Cin_3,
  input  A_2,
  input  B_2,
  input  I0_3,
  input  nE2,
  input  I1_3,
  input  I2,
  input  I3,
  input  Cin_4,
  input  A0_4,
  input  B0_3,
  input  I0_4,
  input  I1_4,
  input  Cin_5,
  input  SC,
  input  I2_2,
  input  A0_5,
  input  B0_4,
  input  C0,
  input  SEL,
  input  OE,
  input  clk,
  input  SC_2,
  input  A0_6,
  input  B0_5,
  input  I0_5,
  input  I1_5,
  input  A_3,
  input  B_3,
  input  A_4,
  input  B_4,
  output Fout,
  output out_13,
  output CARRY,
  output SUM,
  output Fout_2,
  output SUM_2,
  output Cout,
  output Fout_3,
  output Cout_2,
  output SUM_3,
  output Cout_3,
  output Cout_4,
  output Sum_4,
  output out_54,
  output out_55,
  output Cout_5,
  output Fout_4,
  output Fout_5,
  output Sum_5,
  output Carry_2
);

  wire and_3_out, diodebackward_21_out, diodebackward_44_out, diodebackward_48_out, diodebackward_51_out,
       diodebackward_53_out, diodebackward_55_out, diodebackward_57_out, diodebackward_59_out,
       diodebackward_61_out, diodebackward_63_out, diodebackward_65_out, diodebackward_89_out, nand_1_out,
       nand_2_out, nand_3_out, nand_4_out, nand_5_out, nand_6_out, nand_7_out, nand_8_out, nand_9_out,
       nand_10_out, nand_11_out, nand_12_out, nand_13_out, nand_14_out, nand_15_out, nand_16_out,
       nand_17_out, nand_18_out, nand_20_out, nand_21_out, nand_22_out, nand_23_out, nand_24_out,
       nand_26_out, nand_27_out, nand_28_out, nand_29_out, nand_30_out, nand_32_out, nand_33_out,
       nand_37_out, nand_38_out, nand_40_out, nand_41_out, nor_1_out, not_1_out, not_2_out, not_3_out,
       not_4_out, not_5_out, not_6_out, not_7_out, not_9_out, not_10_out, not_11_out, not_12_out, not_13_out,
       not_14_out, not_15_out, not_16_out, not_17_out, not_18_out, not_19_out, not_20_out, not_21_out,
       not_24_out, not_25_out, not_26_out, not_27_out, not_28_out, not_29_out, not_30_out, not_31_out,
       not_33_out, not_34_out, not_35_out, not_36_out, not_37_out, not_38_out, not_39_out, not_40_out,
       not_41_out, not_42_out, not_43_out, not_44_out, not_45_out, not_46_out, not_47_out, pullup_1_out,
       pullup_2_out, pullup_3_out, pullup_4_out, pullup_5_out, pullup_7_out, pullup_8_out, pullup_9_out,
       pullup_10_out, pullup_11_out, pullup_12_out, pullup_13_out, pullup_14_out, pullup_15_out,
       pullup_16_out, pullup_28_out, pullup_29_out, pullup_30_out, pullup_31_out, pullup_32_out,
       pullup_34_out, pullup_35_out, pullup_36_out, pullup_37_out, xor_1_out, xor_3_out;

  not not_1 (not_1_out, S0);
  not not_2 (not_2_out, S1);
  not not_3 (not_3_out, nE1);
  PullUp pullup_1 (.out(pullup_1_out));
  DiodeBackward diodebackward_1 (.in(not_1_out), .out(pullup_1_out));
  not not_4 (not_4_out, pullup_1_out);
  DiodeBackward diodebackward_2 (.in(not_2_out), .out(pullup_1_out));
  DiodeBackward diodebackward_3 (.in(A0_3), .out(pullup_1_out));
  DiodeBackward diodebackward_4 (.in(not_3_out), .out(pullup_1_out));
  PullUp pullup_2 (.out(pullup_2_out));
  DiodeBackward diodebackward_5 (.in(S0), .out(pullup_2_out));
  not not_5 (not_5_out, pullup_2_out);
  DiodeBackward diodebackward_6 (.in(not_2_out), .out(pullup_2_out));
  DiodeBackward diodebackward_7 (.in(A1), .out(pullup_2_out));
  DiodeBackward diodebackward_8 (.in(not_3_out), .out(pullup_2_out));
  PullUp pullup_3 (.out(pullup_3_out));
  DiodeBackward diodebackward_9 (.in(not_1_out), .out(pullup_3_out));
  not not_6 (not_6_out, pullup_3_out);
  DiodeBackward diodebackward_10 (.in(S1), .out(pullup_3_out));
  DiodeBackward diodebackward_11 (.in(A2), .out(pullup_3_out));
  DiodeBackward diodebackward_12 (.in(not_3_out), .out(pullup_3_out));
  PullUp pullup_4 (.out(pullup_4_out));
  DiodeBackward diodebackward_13 (.in(S0), .out(pullup_4_out));
  not not_7 (not_7_out, pullup_4_out);
  DiodeBackward diodebackward_14 (.in(S1), .out(pullup_4_out));
  DiodeBackward diodebackward_15 (.in(A3), .out(pullup_4_out));
  DiodeBackward diodebackward_16 (.in(not_3_out), .out(pullup_4_out));
  PullUp pullup_5 (.out(pullup_5_out));
  DiodeBackward diodebackward_17 (.in(not_4_out), .out(pullup_5_out));
  DiodeBackward diodebackward_18 (.in(not_5_out), .out(pullup_5_out));
  DiodeBackward diodebackward_19 (.in(not_6_out), .out(pullup_5_out));
  DiodeBackward diodebackward_20 (.in(not_7_out), .out(pullup_5_out));
  not not_8 (out_13, pullup_5_out);
  nand nand_1 (nand_1_out, A0, B0);
  nand nand_2 (nand_2_out, A0_4, B0_3);
  DiodeBackward diodebackward_21 (.in(A0_2), .out(diodebackward_21_out));
  DiodeBackward diodebackward_22 (.in(B0_2), .out(diodebackward_21_out));
  PullUp pullup_6 (.out(diodebackward_21_out));
  not not_9 (not_9_out, diodebackward_21_out);
  xor xor_1 (xor_1_out, A0_5, B0_4);
  nand nand_3 (nand_3_out, A4, B1);
  nand nand_4 (nand_4_out, A0, nand_1_out);
  nand nand_5 (nand_5_out, nand_1_out, B0);
  nand nand_6 (nand_6_out, nand_1_out, nand_1_out);
  nand nand_7 (nand_7_out, A0_4, nand_2_out);
  nand nand_8 (nand_8_out, nand_2_out, B0_3);
  nand nand_9 (nand_9_out, nand_2_out, nand_2_out);
  nand nand_10 (nand_10_out, I2_2, Cin_5);
  nand nand_11 (nand_11_out, 1'b0, SC);
  PullUp pullup_7 (.out(pullup_7_out));
  DiodeBackward diodebackward_23 (.in(A0_2), .out(pullup_7_out));
  not not_10 (not_10_out, pullup_7_out);
  DiodeBackward diodebackward_24 (.in(not_9_out), .out(pullup_7_out));
  PullUp pullup_8 (.out(pullup_8_out));
  DiodeBackward diodebackward_25 (.in(not_9_out), .out(pullup_8_out));
  not not_11 (not_11_out, pullup_8_out);
  DiodeBackward diodebackward_26 (.in(B0_2), .out(pullup_8_out));
  PullUp pullup_9 (.out(pullup_9_out));
  DiodeBackward diodebackward_27 (.in(A), .out(pullup_9_out));
  DiodeBackward diodebackward_28 (.in(not_26_out), .out(pullup_9_out));
  PullUp pullup_10 (.out(pullup_10_out));
  DiodeBackward diodebackward_29 (.in(not_26_out), .out(pullup_10_out));
  DiodeBackward diodebackward_30 (.in(B), .out(pullup_10_out));
  PullUp pullup_11 (.out(pullup_11_out));
  DiodeBackward diodebackward_31 (.in(not_26_out), .out(pullup_11_out));
  DiodeBackward diodebackward_32 (.in(Cin), .out(pullup_11_out));
  PullUp pullup_12 (.out(pullup_12_out));
  DiodeBackward diodebackward_33 (.in(B), .out(pullup_12_out));
  DiodeBackward diodebackward_34 (.in(A), .out(pullup_12_out));
  DiodeBackward diodebackward_35 (.in(Cin), .out(pullup_12_out));
  PullUp pullup_13 (.out(pullup_13_out));
  DiodeBackward diodebackward_36 (.in(Cin), .out(pullup_13_out));
  DiodeBackward diodebackward_37 (.in(B), .out(pullup_13_out));
  PullUp pullup_14 (.out(pullup_14_out));
  DiodeBackward diodebackward_38 (.in(A), .out(pullup_14_out));
  DiodeBackward diodebackward_39 (.in(B), .out(pullup_14_out));
  PullUp pullup_15 (.out(pullup_15_out));
  DiodeBackward diodebackward_40 (.in(A), .out(pullup_15_out));
  DiodeBackward diodebackward_41 (.in(Cin), .out(pullup_15_out));
  not not_12 (not_12_out, SEL);
  xor xor_2 (Sum_4, xor_1_out, C0);
  nand nand_12 (nand_12_out, xor_1_out, C0);
  nand nand_13 (nand_13_out, A0_5, B0_4);
  nand nand_14 (nand_14_out, A4, nand_3_out);
  nand nand_15 (nand_15_out, nand_3_out, B1);
  nand nand_16 (nand_16_out, nand_4_out, nand_5_out);
  nand nand_17 (nand_17_out, nand_7_out, nand_8_out);
  nand nand_18 (nand_18_out, nand_10_out, nand_11_out);
  not not_13 (not_13_out, pullup_9_out);
  not not_14 (not_14_out, pullup_10_out);
  not not_15 (not_15_out, pullup_11_out);
  not not_16 (not_16_out, pullup_12_out);
  not not_17 (not_17_out, pullup_13_out);
  not not_18 (not_18_out, pullup_14_out);
  not not_19 (not_19_out, pullup_15_out);
  and and_1 (out_54, ~OE, ~SEL);  // And
  and and_2 (out_55, ~OE, ~not_12_out);  // And
  PullUp pullup_16 (.out(pullup_16_out));
  DiodeBackward diodebackward_42 (.in(not_10_out), .out(pullup_16_out));
  not not_20 (not_20_out, pullup_16_out);
  DiodeBackward diodebackward_43 (.in(not_11_out), .out(pullup_16_out));
  not not_21 (not_21_out, not_9_out);
  nand nand_19 (Cout_4, nand_12_out, nand_13_out);
  nand nand_20 (nand_20_out, nand_14_out, nand_15_out);
  nand nand_21 (nand_21_out, nand_16_out, I0);
  nand nand_22 (nand_22_out, I1, nand_6_out);
  nand nand_23 (nand_23_out, nand_17_out, I0_4);
  nand nand_24 (nand_24_out, I1_4, nand_9_out);
  DiodeBackward diodebackward_44 (.in(not_13_out), .out(diodebackward_44_out));
  DiodeBackward diodebackward_45 (.in(not_14_out), .out(diodebackward_44_out));
  DiodeBackward diodebackward_46 (.in(not_15_out), .out(diodebackward_44_out));
  DiodeBackward diodebackward_47 (.in(not_16_out), .out(diodebackward_44_out));
  DiodeBackward diodebackward_48 (.in(not_17_out), .out(diodebackward_48_out));
  DiodeBackward diodebackward_49 (.in(not_18_out), .out(diodebackward_48_out));
  DiodeBackward diodebackward_50 (.in(not_19_out), .out(diodebackward_48_out));
  PullUp pullup_17 (.out(diodebackward_44_out));
  not not_22 (SUM, diodebackward_44_out);
  PullUp pullup_18 (.out(diodebackward_48_out));
  nand nand_25 (Fout, nand_21_out, nand_22_out);
  nand nand_26 (nand_26_out, nand_23_out, nand_24_out);
  DiodeBackward diodebackward_51 (.in(not_20_out), .out(diodebackward_51_out));
  DiodeBackward diodebackward_52 (.in(I0_2), .out(diodebackward_51_out));
  DiodeBackward diodebackward_53 (.in(not_21_out), .out(diodebackward_53_out));
  DiodeBackward diodebackward_54 (.in(I1_2), .out(diodebackward_53_out));
  not not_23 (CARRY, diodebackward_48_out);
  nand nand_27 (nand_27_out, nand_20_out, Cin_3);
  PullUp pullup_19 (.out(diodebackward_51_out));
  not not_24 (not_24_out, diodebackward_51_out);
  PullUp pullup_20 (.out(diodebackward_53_out));
  not not_25 (not_25_out, diodebackward_53_out);
  not not_26 (not_26_out, CARRY);
  nand nand_28 (nand_28_out, nand_26_out, nand_18_out);
  DiodeBackward diodebackward_55 (.in(not_24_out), .out(diodebackward_55_out));
  DiodeBackward diodebackward_56 (.in(not_25_out), .out(diodebackward_55_out));
  nand nand_29 (nand_29_out, nand_20_out, nand_27_out);
  nand nand_30 (nand_30_out, nand_27_out, Cin_3);
  nand nand_31 (Cout, nand_3_out, nand_27_out);
  PullUp pullup_21 (.out(diodebackward_55_out));
  not not_27 (not_27_out, diodebackward_55_out);
  nand nand_32 (nand_32_out, nand_26_out, nand_28_out);
  nand nand_33 (nand_33_out, nand_28_out, nand_18_out);
  nand nand_34 (Cout_3, nand_2_out, nand_28_out);
  nand nand_35 (SUM_2, nand_29_out, nand_30_out);
  DiodeBackward diodebackward_57 (.in(not_27_out), .out(diodebackward_57_out));
  DiodeBackward diodebackward_58 (.in(Cin_2), .out(diodebackward_57_out));
  nand nand_36 (SUM_3, nand_32_out, nand_33_out);
  PullUp pullup_22 (.out(diodebackward_57_out));
  not not_28 (not_28_out, diodebackward_57_out);
  DiodeBackward diodebackward_59 (.in(not_27_out), .out(diodebackward_59_out));
  DiodeBackward diodebackward_60 (.in(not_28_out), .out(diodebackward_59_out));
  DiodeBackward diodebackward_61 (.in(not_28_out), .out(diodebackward_61_out));
  DiodeBackward diodebackward_62 (.in(Cin_2), .out(diodebackward_61_out));
  DiodeBackward diodebackward_63 (.in(not_28_out), .out(diodebackward_63_out));
  DiodeBackward diodebackward_64 (.in(not_9_out), .out(diodebackward_63_out));
  PullUp pullup_23 (.out(diodebackward_59_out));
  not not_29 (not_29_out, diodebackward_59_out);
  PullUp pullup_24 (.out(diodebackward_61_out));
  not not_30 (not_30_out, diodebackward_61_out);
  PullUp pullup_25 (.out(diodebackward_63_out));
  not not_31 (not_31_out, diodebackward_63_out);
  xor xor_3 (xor_3_out, A0_6, B0_5);
  and and_3 (and_3_out, A0_6, B0_5);
  DiodeBackward diodebackward_65 (.in(not_29_out), .out(diodebackward_65_out));
  DiodeBackward diodebackward_66 (.in(not_30_out), .out(diodebackward_65_out));
  PullUp pullup_26 (.out(diodebackward_65_out));
  not not_32 (Fout_2, diodebackward_65_out);
  PullUp pullup_27 (.out(Cout_5));
  DiodeBackward diodebackward_67 (.in(not_31_out), .out(Cout_5));
  DiodeBackward diodebackward_68 (.in(SC_2), .out(Cout_5));
  not not_33 (not_33_out, A_2);
  not not_34 (not_34_out, B_2);
  not not_35 (not_35_out, nE2);
  nand nand_37 (nand_37_out, I0_5, xor_3_out);
  nand nand_38 (nand_38_out, and_3_out, I1_5);
  nand nand_39 (Fout_4, nand_37_out, nand_38_out);
  PullUp pullup_28 (.out(pullup_28_out));
  DiodeBackward diodebackward_69 (.in(not_33_out), .out(pullup_28_out));
  not not_36 (not_36_out, pullup_28_out);
  DiodeBackward diodebackward_70 (.in(not_34_out), .out(pullup_28_out));
  DiodeBackward diodebackward_71 (.in(I0_3), .out(pullup_28_out));
  DiodeBackward diodebackward_72 (.in(not_35_out), .out(pullup_28_out));
  PullUp pullup_29 (.out(pullup_29_out));
  DiodeBackward diodebackward_73 (.in(A_2), .out(pullup_29_out));
  not not_37 (not_37_out, pullup_29_out);
  DiodeBackward diodebackward_74 (.in(not_34_out), .out(pullup_29_out));
  DiodeBackward diodebackward_75 (.in(I1_3), .out(pullup_29_out));
  DiodeBackward diodebackward_76 (.in(not_35_out), .out(pullup_29_out));
  PullUp pullup_30 (.out(pullup_30_out));
  DiodeBackward diodebackward_77 (.in(not_33_out), .out(pullup_30_out));
  not not_38 (not_38_out, pullup_30_out);
  DiodeBackward diodebackward_78 (.in(B_2), .out(pullup_30_out));
  DiodeBackward diodebackward_79 (.in(I2), .out(pullup_30_out));
  DiodeBackward diodebackward_80 (.in(not_35_out), .out(pullup_30_out));
  PullUp pullup_31 (.out(pullup_31_out));
  DiodeBackward diodebackward_81 (.in(A_2), .out(pullup_31_out));
  not not_39 (not_39_out, pullup_31_out);
  DiodeBackward diodebackward_82 (.in(B_2), .out(pullup_31_out));
  DiodeBackward diodebackward_83 (.in(I3), .out(pullup_31_out));
  DiodeBackward diodebackward_84 (.in(not_35_out), .out(pullup_31_out));
  PullUp pullup_32 (.out(pullup_32_out));
  DiodeBackward diodebackward_85 (.in(not_36_out), .out(pullup_32_out));
  DiodeBackward diodebackward_86 (.in(not_37_out), .out(pullup_32_out));
  DiodeBackward diodebackward_87 (.in(not_38_out), .out(pullup_32_out));
  DiodeBackward diodebackward_88 (.in(not_39_out), .out(pullup_32_out));
  not not_40 (not_40_out, pullup_32_out);
  DiodeBackward diodebackward_89 (.in(not_40_out), .out(diodebackward_89_out));
  DiodeBackward diodebackward_90 (.in(Cin_4), .out(diodebackward_89_out));
  PullUp pullup_33 (.out(diodebackward_89_out));
  not not_41 (not_41_out, diodebackward_89_out);
  not not_42 (not_42_out, A_3);
  not not_43 (not_43_out, B_3);
  not not_44 (not_44_out, A_4);
  not not_45 (not_45_out, B_4);
  PullUp pullup_34 (.out(pullup_34_out));
  DiodeBackward diodebackward_91 (.in(not_40_out), .out(pullup_34_out));
  not not_46 (not_46_out, pullup_34_out);
  DiodeBackward diodebackward_92 (.in(not_41_out), .out(pullup_34_out));
  PullUp pullup_35 (.out(pullup_35_out));
  DiodeBackward diodebackward_93 (.in(not_41_out), .out(pullup_35_out));
  not not_47 (not_47_out, pullup_35_out);
  DiodeBackward diodebackward_94 (.in(Cin_4), .out(pullup_35_out));
  PullUp pullup_36 (.out(pullup_36_out));
  DiodeBackward diodebackward_95 (.in(not_41_out), .out(pullup_36_out));
  not not_48 (Cout_2, pullup_36_out);
  nor nor_1 (nor_1_out, A_4, B_4);
  nor nor_2 (Carry_2, not_44_out, not_45_out);
  nand nand_40 (nand_40_out, A_3, not_43_out);
  nand nand_41 (nand_41_out, not_42_out, B_3);
  PullUp pullup_37 (.out(pullup_37_out));
  DiodeBackward diodebackward_96 (.in(not_46_out), .out(pullup_37_out));
  not not_49 (Fout_3, pullup_37_out);
  DiodeBackward diodebackward_97 (.in(not_47_out), .out(pullup_37_out));
  and and_4 (Sum_5, ~nor_1_out, ~Carry_2);  // And
  nand nand_42 (Fout_5, nand_40_out, nand_41_out);

  // Other names for the same wires on the sheet: AL = SC

  // Notes on the sheet:
  //   4 input Multiplexer in 8 gates
  //   1-bit Zero, XOR, AND, OR Gate
  //   Half Adder
  //   Full Adder (74xx80) 10 gates
  //   1-bit Full Adder
  //   CARRY SUPPRESS
  //   Load/Count Multiplexer
  //   Suppress Carry
  //   Alternative Half Adder
  //   Alternative XOR gate
endmodule
