// Digital circuit 2_3_gate_Inst_Dec_ALU.dig as structural Verilog
module _2_3_gate_Inst_Dec_ALU (
  input  A,
  input  B,
  input  Cin,
  input  SETC,
  input  LD,
  input  IR6,
  input  IR5,
  input  IR4,
  output Cout,
  output CLC,
  output CtoFF,
  output Fout,
  output CLR
);

  wire and_1_out, and_2_out, and_3_out, and_4_out, and_5_out, and_6_out, and_7_out, and_8_out, and_9_out,
       and_10_out, and_11_out, and_12_out, and_13_out, and_14_out, and_15_out, and_16_out, and_17_out,
       and_18_out, and_19_out, and_20_out, and_21_out, and_22_out, and_23_out, and_24_out, and_25_out,
       and_26_out, and_27_out, and_28_out, and_29_out, and_30_out, and_31_out, and_32_out, and_33_out,
       and_34_out, and_35_out, and_36_out, and_37_out, and_38_out, and_39_out, and_40_out, and_41_out,
       and_42_out, and_43_out, and_44_out, and_45_out, not_1_out, not_2_out, not_3_out, not_4_out, not_5_out,
       not_6_out, not_7_out, not_8_out, or_1_out, or_3_out, or_4_out, or_7_out, or_8_out, or_9_out,
       or_11_out, or_12_out, or_13_out, or_14_out, or_16_out;

  not not_1 (not_1_out, IR4);
  not not_2 (not_2_out, IR5);
  not not_3 (not_3_out, IR6);
  not not_4 (not_4_out, LD);
  not not_5 (not_5_out, SETC);
  not not_6 (not_6_out, Cin);
  not not_7 (not_7_out, B);
  not not_8 (not_8_out, A);
  and and_1 (and_1_out, A, not_7_out, and_2_out);
  and and_2 (and_2_out, IR4, not_2_out, IR6);
  or or_1 (or_1_out, and_1_out, and_3_out);
  and and_3 (and_3_out, A, Cin, and_4_out);
  and and_4 (and_4_out, not_1_out, not_2_out);
  and and_5 (and_5_out, A, B, and_6_out);
  and and_6 (and_6_out, not_1_out, not_2_out);
  or or_2 (Cout, or_1_out, or_3_out, or_4_out);
  or or_3 (or_3_out, and_5_out, and_7_out);
  and and_7 (and_7_out, A, Cin, and_8_out);
  and and_8 (and_8_out, not_2_out, IR6);
  and and_9 (and_9_out, not_7_out, Cin, and_10_out);
  and and_10 (and_10_out, IR4, not_2_out, IR6);
  or or_4 (or_4_out, and_9_out, and_11_out);
  and and_11 (and_11_out, B, Cin, and_12_out);
  and and_12 (and_12_out, not_1_out, not_2_out);
  and and_13 (and_13_out, IR4, not_2_out, IR6);
  or or_5 (CLC, and_13_out, not_4_out);
  or or_6 (CtoFF, not_1_out, IR5, or_7_out);
  or or_7 (or_7_out, not_3_out, not_5_out);
  and and_14 (and_14_out, not_8_out, not_7_out);
  and and_15 (and_15_out, and_14_out, and_16_out, and_17_out);
  and and_16 (and_16_out, not_6_out, IR4);
  and and_17 (and_17_out, not_2_out, IR6);
  or or_8 (or_8_out, and_15_out, and_18_out, or_9_out);
  and and_18 (and_18_out, not_8_out, B, and_19_out);
  and and_19 (and_19_out, Cin, IR4, not_2_out);
  and and_20 (and_20_out, A, not_7_out, and_21_out);
  and and_21 (and_21_out, Cin, IR4, not_2_out);
  or or_9 (or_9_out, and_20_out, and_22_out, and_24_out);
  and and_22 (and_22_out, A, B, and_23_out);
  and and_23 (and_23_out, not_6_out, IR4, not_2_out);
  and and_24 (and_24_out, not_8_out, not_7_out, and_25_out);
  and and_25 (and_25_out, Cin, not_1_out);
  and and_26 (and_26_out, not_8_out, B, and_27_out);
  and and_27 (and_27_out, not_6_out, not_1_out);
  or or_10 (Fout, or_8_out, or_11_out, or_13_out);
  or or_11 (or_11_out, and_26_out, and_28_out, or_12_out);
  and and_28 (and_28_out, A, not_7_out, and_29_out);
  and and_29 (and_29_out, not_6_out, not_1_out);
  and and_30 (and_30_out, A, B, and_31_out);
  and and_31 (and_31_out, Cin, not_1_out);
  or or_12 (or_12_out, and_30_out, and_32_out, and_34_out);
  and and_32 (and_32_out, not_8_out, not_7_out, and_33_out);
  and and_33 (and_33_out, Cin, IR5);
  and and_34 (and_34_out, not_8_out, B, and_35_out);
  and and_35 (and_35_out, not_6_out, IR5);
  and and_36 (and_36_out, A, not_7_out, and_37_out);
  and and_37 (and_37_out, not_6_out, IR5);
  or or_13 (or_13_out, and_36_out, and_38_out, or_14_out);
  and and_38 (and_38_out, A, B, and_39_out);
  and and_39 (and_39_out, Cin, IR5);
  and and_40 (and_40_out, B, Cin, and_41_out);
  and and_41 (and_41_out, IR4, not_2_out, not_3_out);
  or or_14 (or_14_out, and_40_out, and_42_out, and_44_out);
  and and_42 (and_42_out, B, not_1_out, and_43_out);
  and and_43 (and_43_out, IR5, not_3_out);
  and and_44 (and_44_out, Cin, not_1_out, and_45_out);
  and and_45 (and_45_out, IR5, not_3_out);
  or or_15 (CLR, IR4, IR5, or_16_out);
  or or_16 (or_16_out, IR6, not_4_out);
endmodule
