// Digital circuit 32_pulse_clock_generator.dig as structural Verilog
module _32_pulse_clock_generator (
  input  clk,
  output CLK_2
);

  wire _74161_1_pin15, button_1_out, GCLK, IX, LD, nand_1_out, nand_3_out, nLOAD, nRES, Q4, Q5, RCO, RST,
       SETC, T0;
  wire [3:0] _74161_1_pin11;

  Monoflop monoflop_1 (.C(nLOAD), .R(1'b0), .Q(SETC), .nQ(nRES));
  Monoflop monoflop_2 (.C(button_1_out), .R(1'b0), .Q(LD), .nQ(nLOAD));
  Button button_1 (.out(button_1_out));
  _74161 _74161_1 (
    .pin1(RST), .pin2(clk), .pin3(1'b0), .pin4(1'b0), .pin5(1'b0), .pin6(1'b0), .pin7(1'b1), .pin8(1'b0),
    .pin9(1'b1), .pin10(1'b1), .pin11(_74161_1_pin11[3]), .pin12(_74161_1_pin11[2]),
    .pin13(_74161_1_pin11[1]), .pin14(_74161_1_pin11[0]), .pin15(_74161_1_pin15), .pin16(1'b1));
  _74161 _74161_2 (
    .pin1(RST), .pin2(clk), .pin3(1'b0), .pin4(1'b0), .pin5(1'b0), .pin6(1'b0), .pin7(1'b1), .pin8(1'b0),
    .pin9(1'b1), .pin10(_74161_1_pin15), .pin13(Q5), .pin14(Q4), .pin16(1'b1));  // open: pin11, pin12, pin15
  Seven_Seg_Hex seven_seg_hex_1 (.d({3'b000, Q4}), .dp(1'b0));
  Seven_Seg_Hex seven_seg_hex_2 (.d(_74161_1_pin11), .dp(1'b0));
  and and_1 (RCO, _74161_1_pin11[0], _74161_1_pin11[1], _74161_1_pin11[2], _74161_1_pin11[3], Q4);
  nand nand_1 (nand_1_out, clk, clk);
  nand nand_2 (RST, nRES, nand_3_out);
  nand nand_3 (nand_3_out, RST, T0);
  nand nand_4 (GCLK, nand_1_out, RST);
  _7474 _7474_1 (
    .pin1(1'b1), .pin2(1'b1), .pin3(1'b1), .pin4(1'b1), .pin7(1'b0), .pin8(T0), .pin9(IX), .pin10(1'b1),
    .pin11(clk), .pin12(RCO), .pin13(1'b1), .pin14(1'b1));  // open: pin5, pin6

  assign CLK_2 = clk;

  // Notes on the sheet:
  //   clk: Hz: 16
  //   STEP/RUN
  //   Clock Sequencer
  //   # Clock
  //   Carry FF
endmodule
