// Digital circuit 3_4_5_input_nand_gates.dig as structural Verilog
module _3_4_5_input_nand_gates (
  input  A,
  input  B,
  input  D,
  input  C,
  input  A_2,
  input  B_2,
  input  D_2,
  input  C_2,
  input  E,
  input  A_3,
  input  B_3,
  input  C_3,
  input  in_16,
  input  in_17,
  output out_5,
  output out_10,
  output out_15,
  output out_18
);

  wire nand_1_out, nand_2_out, nand_3_out, nand_4_out, nand_5_out, nand_6_out, nand_7_out, nand_8_out,
       nand_9_out, nand_10_out, nand_11_out, nand_14_out;

  nand nand_1 (nand_1_out, A_3, B_3);
  nand nand_2 (nand_2_out, A, B);
  nand nand_3 (nand_3_out, C, D);
  nand nand_4 (nand_4_out, A_2, B_2);
  nand nand_5 (nand_5_out, C_2, D_2);
  or or_1 (out_18, ~in_16, ~in_17);  // Or
  nand nand_6 (nand_6_out, nand_1_out, nand_1_out);
  nand nand_7 (nand_7_out, nand_2_out, nand_2_out);
  nand nand_8 (nand_8_out, nand_3_out, nand_3_out);
  nand nand_9 (nand_9_out, nand_4_out, nand_4_out);
  nand nand_10 (nand_10_out, nand_5_out, nand_5_out);
  nand nand_11 (nand_11_out, nand_9_out, nand_10_out);
  nand nand_12 (out_15, nand_6_out, C_3);
  nand nand_13 (out_5, nand_7_out, nand_8_out);
  nand nand_14 (nand_14_out, nand_11_out, nand_11_out);
  nand nand_15 (out_10, nand_14_out, E);

  // Notes on the sheet:
  //   3 input NAND
  //   4 Input NAND
  //   5 Input NAND
endmodule
