// Digital circuit 3_pack_ALU.dig as structural Verilog
module _3_pack_ALU (
  input  A,
  input  B,
  input  I0,
  input  I1,
  input  Cin,
  input  I2,
  input  I3,
  output Sum,
  output Cout
);

  wire nand_1_out, nand_2_out, nand_3_out, nand_4_out, nand_5_out, nand_6_out, nand_7_out, xor_1_out,
       xor_2_out, xor_3_out;

  xor xor_1 (xor_1_out, B, I2);
  xor xor_2 (xor_2_out, A, xor_1_out);
  nand nand_1 (nand_1_out, A, xor_1_out);
  xor xor_3 (xor_3_out, 1'b1, nand_1_out);
  nand nand_2 (nand_2_out, I0, xor_2_out);
  nand nand_3 (nand_3_out, xor_3_out, I1);
  nand nand_4 (nand_4_out, nand_2_out, nand_3_out);
  xor xor_4 (Sum, nand_4_out, Cin);
  nand nand_5 (nand_5_out, nand_4_out, Cin);
  nand nand_6 (nand_6_out, nand_5_out, nand_1_out);
  nand nand_7 (nand_7_out, nand_6_out, I3);
  nand nand_8 (Cout, nand_7_out, nand_7_out);

  // Notes on the sheet:
  //   Suppress Carry
  //   Invert B
  //   XOR
  //   AND
  //   Half Adder 1
  //   3-chip ALU bitslice
  //   2 Input MUX
  //   Half Adder 2
endmodule
