// Digital circuit 4017_8-bit_sequencer.dig as structural Verilog
module _4017_8_bit_sequencer (
  input  clk,
  output GCLK,
  output T5,
  output T1,
  output T0,
  output T2,
  output T3,
  output T4,
  output T7,
  output T6,
  output T8,
  output T9
);

  wire GATE, MR, nor_2_out, nor_4_out, T0_t, T1_t, T2_t, T3_t, T4_t, T5_t, T6_t, T7_t, T8_t;

  _744017 U16 (
    .pin1(T5_t), .pin2(T1_t), .pin3(T0_t), .pin4(T2_t), .pin5(T6_t), .pin6(T7_t), .pin7(T3_t), .pin8(1'b0),
    .pin9(T8_t), .pin10(T4_t), .pin11(MR), .pin13(1'b0), .pin14(clk), .pin15(MR), .pin16(1'b1));  // open: pin12
  nor nor_1 (GCLK, GATE, nor_2_out);
  nor nor_2 (nor_2_out, clk, clk);
  nor nor_3 (GATE, T1_t, nor_4_out);
  nor nor_4 (nor_4_out, GATE, MR);
  not not_1 (T0, T0_t);
  not not_2 (T1, T1_t);
  not not_3 (T2, T2_t);
  not not_4 (T3, T3_t);
  not not_5 (T4, T4_t);
  not not_6 (T5, T5_t);
  not not_7 (T6, T6_t);
  not not_8 (T7, T7_t);
  not not_9 (T8, T8_t);
  not not_10 (T9, MR);

  // Other names for the same wires on the sheet: T9_t = MR

  // Notes on the sheet:
  //   8 pulse Clock Sequencer (2 ICs)
endmodule
