// Digital circuit 4017_clock_sequencer.dig as structural Verilog
module _4017_clock_sequencer (
  input  clk,
  output GCLK,
  output T0,
  output T1,
  output T2,
  output T3,
  output T4,
  output T5,
  output T6,
  output T7,
  output nRES,
  output HOLD,
  output MR,
  output H
);

  wire EN2, GATE, n1SD, nand_2_out, nand_10_out, nEN1, nGATE, nH, nHOLD, not_1_out, not_3_out, Q0, Q1, Q2,
       Q3, QA, QB, QC, RCO, RES;

  Seven_Seg_Hex seven_seg_hex_1 (.d({Q3, Q2, Q1, Q0}), .dp(1'b0));
  _74HC4520 _74hc4520_1 (
    .pin1(clk), .pin2(nEN1), .pin3(Q0), .pin4(Q1), .pin5(Q2), .pin6(Q3), .pin7(RES), .pin8(1'b0), .pin9(clk),
    .pin10(EN2), .pin11(QA), .pin12(QB), .pin13(QC), .pin15(MR), .pin16(1'b1));  // open: pin14
  PullUp pullup_1 (.out(RCO));
  DiodeBackward diodebackward_1 (.in(Q3), .out(RCO));
  DiodeBackward diodebackward_2 (.in(Q2), .out(RCO));
  DiodeBackward diodebackward_3 (.in(Q1), .out(RCO));
  DiodeBackward diodebackward_4 (.in(Q0), .out(RCO));
  nand nand_1 (nEN1, nRES, nand_2_out);
  nand nand_2 (nand_2_out, nEN1, T7);
  _74138 _74138_1 (
    .pin1(QA), .pin2(QB), .pin3(QC), .pin4(1'b0), .pin5(1'b0), .pin6(1'b1), .pin7(T7), .pin8(1'b0),
    .pin9(T6), .pin10(T5), .pin11(T4), .pin12(T3), .pin13(T2), .pin14(T1), .pin15(T0), .pin16(1'b1));
  not not_1 (not_1_out, T7);
  nand nand_3 (MR, T7, n1SD);
  nand nand_4 (H, T4, T5, T6, T7);
  not not_2 (nH, H);
  or or_1 (EN2, nH, nHOLD);
  nand nand_5 (HOLD, nGATE, nHOLD);
  nand nand_6 (nHOLD, HOLD, nRES);
  not not_3 (not_3_out, T3);
  nand nand_7 (GATE, T3, nGATE);
  nand nand_8 (nGATE, GATE, nRES);
  nand nand_9 (GCLK, not_3_out, nand_10_out);
  nand nand_10 (nand_10_out, clk, clk);
  Reset reset_1 (.out(n1SD));
  _7474 U9 (
    .pin1(1'b1), .pin2(RCO), .pin3(clk), .pin4(n1SD), .pin5(RES), .pin6(nRES), .pin7(1'b0), .pin10(1'b1),
    .pin11(1'b1), .pin12(1'b1), .pin13(1'b1), .pin14(1'b1));  // open: pin8, pin9

  // Other names for the same wires on the sheet: nSET = T3

  // Notes on the sheet:
  //   clk: Hz: 2
  //   U10
  //   Clock Sequencer
  //   U8
  //   U13
  //   Carry FF
endmodule
