// Digital circuit 4017_sequencer_2.dig as structural Verilog
module _4017_sequencer_2 (
  input  clk,
  output GCLK,
  output T0,
  output T1,
  output T2,
  output T3,
  output T4,
  output T5,
  output T6,
  output T7,
  output nRES,
  output HOLD,
  output MR
);

  wire GATE, n1SD, nand_6_out, nGATE, nHOLD, nSET, RCO, RES, T8, T9;
  wire [3:0] U7_pin14;

  not not_1 (nSET, T2);
  nand nand_1 (HOLD, nGATE, nHOLD);
  nand nand_2 (nHOLD, HOLD, nRES);
  nand nand_3 (GATE, nSET, nGATE);
  nand nand_4 (nGATE, GATE, nRES);
  nand nand_5 (GCLK, GATE, nand_6_out);
  nand nand_6 (nand_6_out, clk, clk);
  _7474 U9 (
    .pin1(1'b1), .pin2(RCO), .pin3(clk), .pin4(n1SD), .pin5(RES), .pin6(nRES), .pin7(1'b0), .pin10(1'b1),
    .pin11(1'b1), .pin12(1'b1), .pin13(1'b1), .pin14(1'b1));  // open: pin8, pin9
  Reset reset_1 (.out(n1SD));
  _74161 U7 (
    .pin1(GATE), .pin2(clk), .pin3(1'b0), .pin4(1'b0), .pin5(1'b0), .pin6(1'b0), .pin7(1'b1), .pin8(1'b0),
    .pin9(1'b1), .pin10(1'b1), .pin11(U7_pin14[3]), .pin12(U7_pin14[2]), .pin13(U7_pin14[1]),
    .pin14(U7_pin14[0]), .pin15(RCO), .pin16(1'b1));
  _744017 _744017_1 (
    .pin1(MR), .pin2(T1), .pin3(T0), .pin4(T2), .pin5(T6), .pin6(T7), .pin7(T3), .pin8(1'b0), .pin9(T8),
    .pin10(T4), .pin11(T9), .pin13(HOLD), .pin14(clk), .pin15(MR), .pin16(1'b1));  // open: pin12
  Seven_Seg_Hex seven_seg_hex_1 (.d(U7_pin14), .dp(1'b0));

  assign T5 = MR;

  // Other names for the same wires on the sheet: RST = GATE

  // Notes on the sheet:
  //   clk: Hz: 2
  //   Clock Sequencer
  //   U8
  //   U10
  //   U13
  //   Carry FF
  //   # Clock
endmodule
