// Digital circuit 4017_sequencer_3.dig as structural Verilog
module _4017_sequencer_3 (
  input  clk,
  output GCLK,
  output nLD,
  output T5,
  output T1,
  output T0,
  output T2,
  output T3,
  output T4
);

  wire GATE, HOLD, LD, MR, n2SD, nand_4_out, nGATE, nHOLD, nR, nRES, nSET, R, RCO, SETC, T2_t, T3_t, T4_t,
       T6, T7, T8, T9;
  wire [3:0] U17_pin11;

  Reset reset_1 (.out(n2SD));
  not not_1 (nSET, T2_t);
  not not_2 (nRES, SETC);
  not not_3 (nLD, LD);
  nand nand_1 (GATE, nSET, nGATE);
  nand nand_2 (nGATE, GATE, nR);
  nand nand_3 (GCLK, GATE, nand_4_out);
  nand nand_4 (nand_4_out, clk, clk);
  _744017 U16 (
    .pin1(MR), .pin2(SETC), .pin3(LD), .pin4(T2_t), .pin5(T6), .pin6(T7), .pin7(T3_t), .pin8(1'b0),
    .pin9(T8), .pin10(T4_t), .pin11(T9), .pin13(HOLD), .pin14(clk), .pin15(MR), .pin16(1'b1));  // open: pin12
  nand nand_5 (HOLD, nGATE, nHOLD);
  nand nand_6 (nHOLD, HOLD, nR);
  _74161 U17 (
    .pin1(GATE), .pin2(clk), .pin3(1'b0), .pin4(1'b0), .pin5(1'b0), .pin6(1'b0), .pin7(1'b1), .pin8(1'b0),
    .pin9(1'b1), .pin10(1'b1), .pin11(U17_pin11[3]), .pin12(U17_pin11[2]), .pin13(U17_pin11[1]),
    .pin14(U17_pin11[0]), .pin15(RCO), .pin16(1'b1));
  _7474 U9 (
    .pin1(1'b1), .pin2(1'b1), .pin3(1'b1), .pin4(1'b1), .pin7(1'b0), .pin8(nR), .pin9(R), .pin10(n2SD),
    .pin11(clk), .pin12(RCO), .pin13(1'b1), .pin14(1'b1));  // open: pin5, pin6
  Seven_Seg_Hex seven_seg_hex_1 (.d(U17_pin11), .dp(1'b0));
  not not_4 (T0, LD);
  not not_5 (T1, SETC);
  not not_6 (T2, T2_t);
  not not_7 (T3, T3_t);
  not not_8 (T4, T4_t);
  not not_9 (T5, MR);

  // Other names for the same wires on the sheet: nAEN = GATE; T0_t = LD; T1_t = SETC; T5_t = MR

  // Notes on the sheet:
  //   Clock Sequencer (5 ICs)
  //   U11
  //   U19
  //   Carry FF
  //   # Clock
endmodule
