// Digital circuit 4017_state_generator.dig as structural Verilog
module _4017_state_generator (
  input  clk,
  output nLD,
  output GCLK,
  output SETC,
  output GATE,
  output ST
);

  wire button_1_out, LD, monoflop_1_nq, MR, nGATE, nor_1_out, PC_INC, T2, T3, T4, T5, T6, T7, T8;

  _744017 U16 (
    .pin1(T5), .pin2(SETC), .pin3(LD), .pin4(T2), .pin5(T6), .pin6(T7), .pin7(T3), .pin8(1'b0), .pin9(T8),
    .pin10(T4), .pin11(ST), .pin13(MR), .pin14(clk), .pin15(MR), .pin16(1'b1));  // open: pin12
  nor nor_1 (nor_1_out, GATE, clk);
  nor nor_2 (GATE, SETC, nGATE);
  nor nor_3 (nGATE, GATE, ST);
  not not_1 (nLD, LD);
  not not_2 (PC_INC, T8);
  Button button_1 (.out(button_1_out));
  Monoflop monoflop_1 (.C(button_1_out), .R(1'b0), .nQ(monoflop_1_nq));  // open: Q
  nor nor_4 (GCLK, nor_1_out, nor_1_out);
  _7474 _7474_1 (
    .pin1(monoflop_1_nq), .pin2(1'b1), .pin3(clk), .pin4(nGATE), .pin6(MR), .pin7(1'b0), .pin10(1'b1),
    .pin11(1'b1), .pin12(1'b1), .pin13(1'b1), .pin14(1'b1));  // open: pin5, pin8, pin9

  // Other names for the same wires on the sheet: nLOAD = nLD; RCLK = PC_INC; T0 = LD; T1 = SETC; T9 = ST

  // Notes on the sheet:
  //   clk: Hz: 10
endmodule
