// Digital circuit 4520_clock_sequencer.dig as structural Verilog
module _4520_clock_sequencer (
  input  clk,
  output GCLK,
  output T0,
  output T1,
  output T2,
  output T3,
  output T4,
  output T5,
  output T6,
  output T7,
  output nRES,
  output GATE,
  output nHOLD
);

  wire _74hc4520_1_pin11, _74hc4520_1_pin12, _74hc4520_1_pin13, END, HOLD, n1SD, nand_7_out, nGATE, Q0, Q1,
       Q2, Q3, RCO, RES;

  Seven_Seg_Hex seven_seg_hex_1 (.d({Q3, Q2, Q1, Q0}), .dp(1'b0));
  _74HC4520 _74hc4520_1 (
    .pin1(clk), .pin2(1'b1), .pin3(Q0), .pin4(Q1), .pin5(Q2), .pin6(Q3), .pin7(RES), .pin8(1'b0), .pin9(clk),
    .pin10(nGATE), .pin11(_74hc4520_1_pin11), .pin12(_74hc4520_1_pin12), .pin13(_74hc4520_1_pin13),
    .pin15(END), .pin16(1'b1));  // open: pin14
  _74138 _74138_1 (
    .pin1(_74hc4520_1_pin11), .pin2(_74hc4520_1_pin12), .pin3(_74hc4520_1_pin13), .pin4(1'b0), .pin5(1'b0),
    .pin6(nGATE), .pin7(T7), .pin8(1'b0), .pin9(T6), .pin10(T5), .pin11(T4), .pin12(T3), .pin13(T2),
    .pin14(T1), .pin15(T0), .pin16(1'b1));
  Reset reset_1 (.out(n1SD));
  DiodeBackward diodebackward_1 (.in(Q3), .out(RCO));
  DiodeBackward diodebackward_2 (.in(Q2), .out(RCO));
  DiodeBackward diodebackward_3 (.in(Q1), .out(RCO));
  DiodeBackward diodebackward_4 (.in(Q0), .out(RCO));
  PullUp pullup_1 (.out(RCO));
  nand nand_1 (END, T7, T7);
  _7474 U9 (
    .pin1(1'b1), .pin2(RCO), .pin3(clk), .pin4(n1SD), .pin5(RES), .pin6(nRES), .pin7(1'b0), .pin10(1'b1),
    .pin11(1'b1), .pin12(1'b1), .pin13(1'b1), .pin14(1'b1));  // open: pin8, pin9
  nand nand_2 (HOLD, nGATE, nHOLD);
  nand nand_3 (nHOLD, HOLD, nRES);
  nand nand_4 (GATE, T3, nGATE);
  nand nand_5 (nGATE, GATE, nRES);
  nand nand_6 (GCLK, GATE, nand_7_out);
  nand nand_7 (nand_7_out, clk, clk);

  // Notes on the sheet:
  //   clk: Hz: 2
  //   Clock Sequencer
  //   Carry FF
  //   U9
  //   U10
  //   U13
endmodule
