// Digital circuit 4520_clock_sequencer_2.dig as structural Verilog
module _4520_clock_sequencer_2 (
  input  clk,
  output GCLK,
  output T0,
  output T1,
  output T2,
  output T3,
  output T4,
  output T5,
  output T6,
  output T7,
  output nRES,
  output GATE,
  output nSET
);

  wire _74hc4520_1_pin11, _74hc4520_1_pin12, _74hc4520_1_pin13, END, HOLD, nand_6_out, nGATE, nHOLD, Q0, Q1,
       Q2, Q3;

  Seven_Seg_Hex seven_seg_hex_1 (.d({Q3, Q2, Q1, Q0}), .dp(1'b0));
  _74HC4520 _74hc4520_1 (
    .pin1(clk), .pin2(T4), .pin3(Q0), .pin4(Q1), .pin5(Q2), .pin6(Q3), .pin7(nGATE), .pin8(1'b0), .pin9(clk),
    .pin10(nHOLD), .pin11(_74hc4520_1_pin11), .pin12(_74hc4520_1_pin12), .pin13(_74hc4520_1_pin13),
    .pin15(END), .pin16(1'b1));  // open: pin14
  nand nand_1 (HOLD, nGATE, nHOLD);
  nand nand_2 (nHOLD, HOLD, nRES);
  nand nand_3 (GATE, nSET, nGATE);
  nand nand_4 (nGATE, GATE, nRES);
  nand nand_5 (GCLK, GATE, nand_6_out);
  nand nand_6 (nand_6_out, clk, clk);
  _74138 _74138_1 (
    .pin1(_74hc4520_1_pin11), .pin2(_74hc4520_1_pin12), .pin3(_74hc4520_1_pin13), .pin4(1'b0), .pin5(1'b0),
    .pin6(nHOLD), .pin7(T7), .pin8(1'b0), .pin9(T6), .pin10(T5), .pin11(T4), .pin12(nSET), .pin13(T2),
    .pin14(T1), .pin15(T0), .pin16(1'b1));
  DiodeForward diodeforward_1 (.in(Q3), .out(nRES));
  DiodeForward diodeforward_2 (.in(Q2), .out(nRES));
  DiodeForward diodeforward_3 (.in(Q1), .out(nRES));
  DiodeForward diodeforward_4 (.in(Q0), .out(nRES));
  nand nand_7 (END, T7, T7);
  PullDown pulldown_1 (.out(nRES));

  assign T3 = nSET;

  // Other names for the same wires on the sheet: nLD = T0; Z = nRES

  // Notes on the sheet:
  //   clk: Hz: 2
  //   Clock Sequencer
  //   U8
  //   U10
endmodule
