// Digital circuit 4520_clock_sequencer_3.dig as structural Verilog
module _4520_clock_sequencer_3 (
  input  clk,
  input  in_12,
  input  in_13,
  output T0,
  output T1,
  output T2,
  output T3,
  output T4,
  output T5,
  output T6,
  output T7,
  output nFRONT,
  output nREAR,
  output nRES
);

  wire n1SD, nF, nR, Q0, Q1, Q2, Q3, QA, QB, RCO, RES;

  Seven_Seg_Hex seven_seg_hex_1 (.d({Q3, Q2, Q1, Q0}), .dp(1'b0));
  _74HC4520 _74hc4520_1 (
    .pin1(clk), .pin2(nF), .pin3(Q0), .pin4(Q1), .pin5(Q2), .pin6(Q3), .pin7(RES), .pin8(1'b0), .pin9(clk),
    .pin10(in_12), .pin11(QA), .pin12(QB), .pin15(in_13), .pin16(1'b1));  // open: pin13, pin14
  nand nand_1 (nF, T0, nFRONT);
  nand nand_2 (nFRONT, nF, T3);
  nand nand_3 (nR, T5, nREAR);
  nand nand_4 (nREAR, nR, T7);
  _74139 _74139_1 (
    .pin1(nF), .pin2(QA), .pin3(QB), .pin4(T4), .pin5(T5), .pin6(T6), .pin7(T7), .pin8(1'b0), .pin9(T3),
    .pin10(T2), .pin11(T1), .pin12(T0), .pin13(QB), .pin14(QA), .pin15(nR), .pin16(1'b1));
  Reset reset_1 (.out(n1SD));
  _7474 U9 (
    .pin1(1'b1), .pin2(RCO), .pin3(clk), .pin4(n1SD), .pin5(RES), .pin6(nRES), .pin7(1'b0), .pin10(1'b1),
    .pin11(1'b1), .pin12(1'b1), .pin13(1'b1), .pin14(1'b1));  // open: pin8, pin9
  PullUp pullup_1 (.out(RCO));
  DiodeBackward diodebackward_1 (.in(Q3), .out(RCO));
  DiodeBackward diodebackward_2 (.in(Q2), .out(RCO));
  DiodeBackward diodebackward_3 (.in(Q1), .out(RCO));
  DiodeBackward diodebackward_4 (.in(Q0), .out(RCO));

  // Notes on the sheet:
  //   clk: Hz: 2
  //   in_12: default 1
  //   Clock Sequencer
  //   Carry FF
endmodule
