// Digital circuit 4_bit_ALU_3_chip.dig as structural Verilog
module _4_bit_ALU_3_chip (
  input  I0,
  input  I1,
  input  I2,
  input  I3,
  input  Cin,
  input  CLK,
  input  B1,
  input  B2,
  input  B3,
  input  B0,
  input  A,
  input  B,
  input  Cin_2,
  input  I4,
  input  I5,
  input  nSC,
  input  CMP_A,
  input  INV_B,
  output Cout,
  output A0,
  output A1,
  output A2,
  output A3,
  output Fout,
  output Cout_2
);

  wire F0, F1, F2, F3, nand_1_out, nand_2_out, nand_3_out, nand_4_out, nand_5_out, nand_6_out, nand_7_out,
       nand_8_out, nand_9_out, nand_10_out, nand_11_out, nand_12_out, nand_13_out, nand_14_out, nand_15_out,
       nand_16_out, nand_17_out, nand_18_out, nand_19_out, nand_20_out, nand_21_out, nand_22_out,
       nand_23_out, nand_24_out, nand_25_out, nand_26_out, nand_29_out, nand_30_out, nand_31_out,
       nand_32_out, nand_33_out, nand_34_out, nand_35_out, nand_36_out, nand_38_out, nand_39_out,
       nand_40_out, nand_41_out, nand_42_out, nand_43_out, nand_44_out, nand_45_out, nand_46_out,
       nand_47_out, nand_48_out, nand_49_out, nand_50_out, nand_51_out, nand_52_out, nand_53_out,
       nand_54_out, nand_55_out, nand_56_out, nand_57_out, nand_58_out, nand_59_out, nand_60_out,
       nand_61_out, nand_62_out, nand_63_out, nand_64_out, nand_65_out, nand_67_out, nand_69_out,
       nand_71_out, nand_73_out, xor_1_out, xor_2_out, xor_3_out, xor_4_out, xor_5_out, xor_6_out, xor_7_out,
       xor_8_out, xor_9_out, xor_10_out, xor_11_out, xor_12_out, xor_13_out, xor_14_out, xor_15_out,
       xor_16_out;

  Seven_Seg_Hex seven_seg_hex_1 (.d({F3, F2, F1, F0}), .dp(1'b0));
  Seven_Seg_Hex seven_seg_hex_2 (.d({A3, A2, A1, A0}), .dp(1'b0));
  Seven_Seg_Hex seven_seg_hex_3 (.d({B3, B2, B1, B0}), .dp(1'b0));
  xor xor_1 (xor_1_out, B3, I2);
  xor xor_2 (xor_2_out, B2, I2);
  xor xor_3 (xor_3_out, B1, I2);
  xor xor_4 (xor_4_out, B0, I2);
  xor xor_5 (xor_5_out, A, CMP_A);
  xor xor_6 (xor_6_out, INV_B, B);
  xor xor_7 (xor_7_out, A3, xor_1_out);
  nand nand_1 (nand_1_out, A3, xor_1_out);
  xor xor_8 (xor_8_out, A2, xor_2_out);
  nand nand_2 (nand_2_out, A2, xor_2_out);
  xor xor_9 (xor_9_out, A1, xor_3_out);
  nand nand_3 (nand_3_out, A1, xor_3_out);
  xor xor_10 (xor_10_out, A0, xor_4_out);
  nand nand_4 (nand_4_out, A0, xor_4_out);
  xor xor_11 (xor_11_out, xor_5_out, xor_6_out);
  xor xor_12 (xor_12_out, 1'b1, nand_1_out);
  xor xor_13 (xor_13_out, 1'b1, nand_2_out);
  xor xor_14 (xor_14_out, 1'b1, nand_3_out);
  xor xor_15 (xor_15_out, 1'b1, nand_4_out);
  xor xor_16 (xor_16_out, xor_11_out, Cin_2);
  nand nand_5 (nand_5_out, xor_11_out, Cin_2);
  nand nand_6 (nand_6_out, xor_5_out, xor_6_out);
  nand nand_7 (nand_7_out, I0, xor_7_out);
  nand nand_8 (nand_8_out, xor_12_out, I1);
  nand nand_9 (nand_9_out, I0, xor_8_out);
  nand nand_10 (nand_10_out, xor_13_out, I1);
  nand nand_11 (nand_11_out, I0, xor_9_out);
  nand nand_12 (nand_12_out, xor_14_out, I1);
  nand nand_13 (nand_13_out, I0, xor_10_out);
  nand nand_14 (nand_14_out, xor_15_out, I1);
  nand nand_15 (nand_15_out, nand_5_out, nand_6_out);
  nand nand_16 (nand_16_out, nand_7_out, nand_8_out);
  nand nand_17 (nand_17_out, nand_9_out, nand_10_out);
  nand nand_18 (nand_18_out, nand_11_out, nand_12_out);
  nand nand_19 (nand_19_out, nand_13_out, nand_14_out);
  nand nand_20 (nand_20_out, xor_16_out, I4);
  nand nand_21 (nand_21_out, I5, nand_15_out);
  nand nand_22 (nand_22_out, nand_15_out, nSC);
  xor xor_17 (F3, nand_16_out, nand_38_out);
  nand nand_23 (nand_23_out, nand_16_out, nand_38_out);
  xor xor_18 (F2, nand_17_out, nand_39_out);
  nand nand_24 (nand_24_out, nand_17_out, nand_39_out);
  xor xor_19 (F1, nand_18_out, nand_40_out);
  nand nand_25 (nand_25_out, nand_18_out, nand_40_out);
  xor xor_20 (F0, nand_19_out, Cin);
  nand nand_26 (nand_26_out, nand_19_out, Cin);
  nand nand_27 (Fout, nand_20_out, nand_21_out);
  nand nand_28 (Cout_2, nand_22_out, nand_22_out);
  nand nand_29 (nand_29_out, nand_23_out, nand_1_out);
  nand nand_30 (nand_30_out, nand_24_out, nand_2_out);
  nand nand_31 (nand_31_out, nand_25_out, nand_3_out);
  nand nand_32 (nand_32_out, nand_26_out, nand_4_out);
  nand nand_33 (nand_33_out, nand_29_out, I3);
  nand nand_34 (nand_34_out, nand_30_out, I3);
  nand nand_35 (nand_35_out, nand_31_out, I3);
  nand nand_36 (nand_36_out, nand_32_out, I3);
  nand nand_37 (Cout, nand_33_out, nand_33_out);
  nand nand_38 (nand_38_out, nand_34_out, nand_34_out);
  nand nand_39 (nand_39_out, nand_35_out, nand_35_out);
  nand nand_40 (nand_40_out, nand_36_out, nand_36_out);
  nand nand_41 (nand_41_out, CLK, CLK);
  nand nand_42 (nand_42_out, F3, nand_41_out);
  nand nand_43 (nand_43_out, nand_42_out, nand_41_out);
  nand nand_44 (nand_44_out, F2, nand_41_out);
  nand nand_45 (nand_45_out, nand_44_out, nand_41_out);
  nand nand_46 (nand_46_out, F1, nand_41_out);
  nand nand_47 (nand_47_out, nand_46_out, nand_41_out);
  nand nand_48 (nand_48_out, F0, nand_41_out);
  nand nand_49 (nand_49_out, nand_48_out, nand_41_out);
  nand nand_50 (nand_50_out, nand_42_out, nand_51_out);
  nand nand_51 (nand_51_out, nand_50_out, nand_43_out);
  nand nand_52 (nand_52_out, nand_44_out, nand_53_out);
  nand nand_53 (nand_53_out, nand_52_out, nand_45_out);
  nand nand_54 (nand_54_out, nand_46_out, nand_55_out);
  nand nand_55 (nand_55_out, nand_54_out, nand_47_out);
  nand nand_56 (nand_56_out, nand_48_out, nand_57_out);
  nand nand_57 (nand_57_out, nand_56_out, nand_49_out);
  nand nand_58 (nand_58_out, nand_50_out, CLK);
  nand nand_59 (nand_59_out, nand_58_out, CLK);
  nand nand_60 (nand_60_out, nand_52_out, CLK);
  nand nand_61 (nand_61_out, nand_60_out, CLK);
  nand nand_62 (nand_62_out, nand_54_out, CLK);
  nand nand_63 (nand_63_out, nand_62_out, CLK);
  nand nand_64 (nand_64_out, nand_56_out, CLK);
  nand nand_65 (nand_65_out, nand_64_out, CLK);
  nand nand_66 (A3, nand_58_out, nand_67_out);
  nand nand_67 (nand_67_out, A3, nand_59_out);
  nand nand_68 (A2, nand_60_out, nand_69_out);
  nand nand_69 (nand_69_out, A2, nand_61_out);
  nand nand_70 (A1, nand_62_out, nand_71_out);
  nand nand_71 (nand_71_out, A1, nand_63_out);
  nand nand_72 (A0, nand_64_out, nand_73_out);
  nand nand_73 (nand_73_out, A0, nand_65_out);

  // Notes on the sheet:
  //   ALU
  //   ACC
  //   BUS
  //   Suppress Carry
  //   Invert B
  //   XOR
  //   AND
  //   Half Adder 1
  //   3-chip ALU bitslice
  //   Partial Sum
  //   2 Input MUX
  //   Half Adder 2
  //   Master Slave FF using gated D-type latches
endmodule
