// Digital circuit 7480_DTL_full_adder.dig as structural Verilog
module _7480_DTL_full_adder (
  input  A,
  input  B,
  input  Cin,
  output Sum,
  output Cout
);

  wire diodebackward_3_out, diodebackward_5_out, diodebackward_7_out, diodebackward_12_out,
       diodebackward_14_out, diodeforward_1_out, diodeforward_5_out, not_1_out, not_2_out, pullup_1_out,
       pullup_2_out;

  PullUp pullup_1 (.out(pullup_1_out));
  DiodeBackward diodebackward_1 (.in(A), .out(pullup_1_out));
  DiodeBackward diodebackward_2 (.in(not_2_out), .out(pullup_1_out));
  DiodeBackward diodebackward_3 (.in(B), .out(diodebackward_3_out));
  DiodeBackward diodebackward_4 (.in(not_2_out), .out(diodebackward_3_out));
  DiodeBackward diodebackward_5 (.in(Cin), .out(diodebackward_5_out));
  DiodeBackward diodebackward_6 (.in(not_2_out), .out(diodebackward_5_out));
  DiodeBackward diodebackward_7 (.in(A), .out(diodebackward_7_out));
  DiodeBackward diodebackward_8 (.in(B), .out(diodebackward_7_out));
  DiodeBackward diodebackward_9 (.in(Cin), .out(diodebackward_7_out));
  PullUp pullup_2 (.out(pullup_2_out));
  DiodeBackward diodebackward_10 (.in(A), .out(pullup_2_out));
  DiodeBackward diodebackward_11 (.in(B), .out(pullup_2_out));
  DiodeBackward diodebackward_12 (.in(A), .out(diodebackward_12_out));
  DiodeBackward diodebackward_13 (.in(Cin), .out(diodebackward_12_out));
  DiodeBackward diodebackward_14 (.in(B), .out(diodebackward_14_out));
  DiodeBackward diodebackward_15 (.in(Cin), .out(diodebackward_14_out));
  PullUp pullup_3 (.out(diodebackward_3_out));
  PullUp pullup_4 (.out(diodebackward_5_out));
  PullUp pullup_5 (.out(diodebackward_12_out));
  PullUp pullup_6 (.out(diodebackward_14_out));
  PullUp pullup_7 (.out(diodebackward_7_out));
  DiodeForward diodeforward_1 (.in(pullup_1_out), .out(diodeforward_1_out));
  DiodeForward diodeforward_2 (.in(diodebackward_3_out), .out(diodeforward_1_out));
  DiodeForward diodeforward_3 (.in(diodebackward_5_out), .out(diodeforward_1_out));
  DiodeForward diodeforward_4 (.in(diodebackward_7_out), .out(diodeforward_1_out));
  DiodeForward diodeforward_5 (.in(pullup_2_out), .out(diodeforward_5_out));
  DiodeForward diodeforward_6 (.in(diodebackward_12_out), .out(diodeforward_5_out));
  DiodeForward diodeforward_7 (.in(diodebackward_14_out), .out(diodeforward_5_out));
  PullDown pulldown_1 (.out(diodeforward_1_out));
  PullDown pulldown_2 (.out(diodeforward_5_out));
  not not_1 (not_1_out, diodeforward_1_out);
  not not_2 (not_2_out, diodeforward_5_out);
  not not_3 (Sum, not_1_out);
  not not_4 (Cout, not_2_out);

  // Notes on the sheet:
  //   DTL Adder using AND-OR-INVERT
  //   ~S=(A.C)+(B.C)+(Cin.C)+(A.B.Cin)
  //   C=(A.B)+(A.Cin)+(B.Cin)
endmodule
