// Digital circuit 74HC219_up_down_counter.dig as structural Verilog
module _74HC219_up_down_counter (
  input  nCS,
  input  nWE,
  input  A0,
  input  A1,
  input  A2,
  input  A3,
  input  in_7,
  input  in_8,
  input  in_9,
  input  in_10
);

  wire _74173_1_pin1, _74173_1_pin3, _74173_1_pin4, _74173_1_pin5, _74173_1_pin6, _74173_1_pin11,
       _74173_1_pin12, _74173_1_pin13, _74173_1_pin14, _74173_2_pin3, _74173_2_pin4, _74173_2_pin5,
       _74173_2_pin6, _74173_2_pin11, _74173_2_pin12, _74173_2_pin13, _74173_2_pin14, _74173_3_pin3,
       _74173_3_pin4, _74173_3_pin5, _74173_3_pin6, _74173_3_pin11, _74173_3_pin12, _74173_3_pin13,
       _74173_3_pin14, _74173_4_pin3, _74173_4_pin4, _74173_4_pin5, _74173_4_pin6, _74173_4_pin11,
       _74173_4_pin12, _74173_4_pin13, _74173_4_pin14, _74193_1_pin12, _74193_1_pin13, _74193_2_pin12,
       _74193_2_pin13, _74193_3_pin12, _74193_3_pin13, A0_t, A1_t, A2_t, A3_t, A4, A5, A6, A7, A8, A9, A10,
       A11, A12, A13, A14, A15, BUS0, BUS1, BUS2, BUS3, BUS4, BUS5, BUS6, BUS7, BUS8, BUS9, BUS10, BUS11,
       BUS12, BUS13, BUS14, BUS15, button_1_out, button_2_out, button_3_out, button_4_out, button_5_out,
       button_6_out, button_7_out, button_8_out, button_9_out, button_10_out, button_11_out, button_12_out,
       button_13_out, button_14_out, button_15_out, button_16_out, D0, D1, D2, D3, D4, D5, D6, D7, D8, D9,
       D10, D11, D12, D13, D14, D15, d_ff_1_nq, d_ff_2_nq, d_ff_3_nq, d_ff_4_nq, d_ff_5_nq, d_ff_6_nq,
       d_ff_7_nq, d_ff_8_nq, d_ff_9_nq, d_ff_10_nq, d_ff_11_nq, d_ff_12_nq, IC16_2_nq, IC16_nq, IC17_2_nq,
       IC17_nq;

  LED led_1 (.in(D15));
  LED led_2 (.in(D14));
  D_FF IC17 (.D(IC17_nq), .C(button_1_out), .Q(D15), .nQ(IC17_nq));
  Button button_1 (.out(button_1_out));
  LED led_3 (.in(D13));
  D_FF d_ff_1 (.D(d_ff_1_nq), .C(button_2_out), .Q(D14), .nQ(d_ff_1_nq));
  Button button_2 (.out(button_2_out));
  _74219 _74219_1 (
    .pin1(A0), .pin2(nCS), .pin3(nWE), .pin4(D12), .pin5(BUS12), .pin6(D13), .pin7(BUS13), .pin8(1'b0),
    .pin9(BUS14), .pin10(D14), .pin11(BUS15), .pin12(D15), .pin13(A3), .pin14(A2), .pin15(A1), .pin16(1'b1));
  LED led_4 (.in(D12));
  D_FF d_ff_2 (.D(d_ff_2_nq), .C(button_3_out), .Q(D13), .nQ(d_ff_2_nq));
  Button button_3 (.out(button_3_out));
  LED led_5 (.in(D11));
  D_FF d_ff_3 (.D(d_ff_3_nq), .C(button_4_out), .Q(D12), .nQ(d_ff_3_nq));
  Button button_4 (.out(button_4_out));
  LED led_6 (.in(D10));
  D_FF d_ff_4 (.D(d_ff_4_nq), .C(button_5_out), .Q(D11), .nQ(d_ff_4_nq));
  Button button_5 (.out(button_5_out));
  LED led_7 (.in(D9));
  D_FF d_ff_5 (.D(d_ff_5_nq), .C(button_6_out), .Q(D10), .nQ(d_ff_5_nq));
  Button button_6 (.out(button_6_out));
  LED led_8 (.in(D8));
  D_FF d_ff_6 (.D(d_ff_6_nq), .C(button_7_out), .Q(D9), .nQ(d_ff_6_nq));
  Button button_7 (.out(button_7_out));
  _74219 _74219_2 (
    .pin1(A0), .pin2(nCS), .pin3(nWE), .pin4(D8), .pin5(BUS8), .pin6(D9), .pin7(BUS9), .pin8(1'b0),
    .pin9(BUS10), .pin10(D10), .pin11(BUS11), .pin12(D11), .pin13(A3), .pin14(A2), .pin15(A1), .pin16(1'b1));
  D_FF IC17_2 (.D(IC17_2_nq), .C(button_8_out), .Q(D8), .nQ(IC17_2_nq));
  Button button_8 (.out(button_8_out));
  Seven_Seg_Hex seven_seg_hex_1 (.d({BUS15, BUS14, BUS13, BUS12}), .dp(1'b0));
  Seven_Seg_Hex seven_seg_hex_2 (.d({D15, D14, D13, D12}), .dp(1'b0));
  Seven_Seg_Hex seven_seg_hex_3 (.d({BUS11, BUS10, BUS9, BUS8}), .dp(1'b0));
  Seven_Seg_Hex seven_seg_hex_4 (.d({D11, D10, D9, D8}), .dp(1'b0));
  Seven_Seg_Hex seven_seg_hex_5 (.d({BUS7, BUS6, BUS5, BUS4}), .dp(1'b0));
  LED led_9 (.in(D7));
  D_FF IC16 (.D(IC16_nq), .C(button_9_out), .Q(D7), .nQ(IC16_nq));
  Seven_Seg_Hex seven_seg_hex_6 (.d({BUS3, BUS2, BUS1, BUS0}), .dp(1'b0));
  LED led_10 (.in(D6));
  D_FF d_ff_7 (.D(d_ff_7_nq), .C(button_10_out), .Q(D6), .nQ(d_ff_7_nq));
  Button button_9 (.out(button_9_out));
  _74219 _74219_3 (
    .pin1(A0), .pin2(nCS), .pin3(nWE), .pin4(D4), .pin5(BUS4), .pin6(D5), .pin7(BUS5), .pin8(1'b0),
    .pin9(BUS6), .pin10(D6), .pin11(BUS7), .pin12(D7), .pin13(A3), .pin14(A2), .pin15(A1), .pin16(1'b1));
  LED led_11 (.in(D5));
  D_FF d_ff_8 (.D(d_ff_8_nq), .C(button_11_out), .Q(D5), .nQ(d_ff_8_nq));
  Button button_10 (.out(button_10_out));
  Seven_Seg_Hex seven_seg_hex_7 (.d({A15, A14, A13, A12}), .dp(1'b0));
  LED led_12 (.in(D4));
  D_FF d_ff_9 (.D(d_ff_9_nq), .C(button_12_out), .Q(D4), .nQ(d_ff_9_nq));
  Button button_11 (.out(button_11_out));
  Seven_Seg_Hex seven_seg_hex_8 (.d({A11, A10, A9, A8}), .dp(1'b0));
  LED led_13 (.in(D3));
  D_FF d_ff_10 (.D(d_ff_10_nq), .C(button_13_out), .Q(D3), .nQ(d_ff_10_nq));
  Button button_12 (.out(button_12_out));
  Seven_Seg_Hex seven_seg_hex_9 (.d({A7, A6, A5, A4}), .dp(1'b0));
  LED led_14 (.in(D2));
  D_FF d_ff_11 (.D(d_ff_11_nq), .C(button_14_out), .Q(D2), .nQ(d_ff_11_nq));
  Button button_13 (.out(button_13_out));
  Seven_Seg_Hex seven_seg_hex_10 (.d({A3_t, A2_t, A1_t, A0_t}), .dp(1'b0));
  LED led_15 (.in(D1));
  D_FF d_ff_12 (.D(d_ff_12_nq), .C(button_15_out), .Q(D1), .nQ(d_ff_12_nq));
  Button button_14 (.out(button_14_out));
  _74219 _74219_4 (
    .pin1(A0), .pin2(nCS), .pin3(nWE), .pin4(D0), .pin5(BUS0), .pin6(D1), .pin7(BUS1), .pin8(1'b0),
    .pin9(BUS2), .pin10(D2), .pin11(BUS3), .pin12(D3), .pin13(A3), .pin14(A2), .pin15(A1), .pin16(1'b1));
  LED led_16 (.in(D0));
  D_FF IC16_2 (.D(IC16_2_nq), .C(button_16_out), .Q(D0), .nQ(IC16_2_nq));
  Button button_15 (.out(button_15_out));
  Seven_Seg_Hex seven_seg_hex_11 (.d({D7, D6, D5, D4}), .dp(1'b0));
  Button button_16 (.out(button_16_out));
  Seven_Seg_Hex seven_seg_hex_12 (.d({D3, D2, D1, D0}), .dp(1'b0));
  _74173 _74173_1 (
    .pin1(_74173_1_pin1), .pin2(_74173_1_pin1), .pin3(_74173_1_pin3), .pin4(_74173_1_pin4),
    .pin5(_74173_1_pin5), .pin6(_74173_1_pin6), .pin8(1'b0), .pin11(_74173_1_pin11), .pin12(_74173_1_pin12),
    .pin13(_74173_1_pin13), .pin14(_74173_1_pin14), .pin16(1'b1));  // open: pin7, pin9, pin10, pin15
  _74173 _74173_2 (
    .pin1(_74173_1_pin1), .pin2(_74173_1_pin1), .pin3(_74173_2_pin3), .pin4(_74173_2_pin4),
    .pin5(_74173_2_pin5), .pin6(_74173_2_pin6), .pin8(1'b0), .pin11(_74173_2_pin11), .pin12(_74173_2_pin12),
    .pin13(_74173_2_pin13), .pin14(_74173_2_pin14), .pin16(1'b1));  // open: pin7, pin9, pin10, pin15
  _74173 _74173_3 (
    .pin1(_74173_1_pin1), .pin2(_74173_1_pin1), .pin3(_74173_3_pin3), .pin4(_74173_3_pin4),
    .pin5(_74173_3_pin5), .pin6(_74173_3_pin6), .pin8(1'b0), .pin11(_74173_3_pin11), .pin12(_74173_3_pin12),
    .pin13(_74173_3_pin13), .pin14(_74173_3_pin14), .pin16(1'b1));  // open: pin7, pin9, pin10, pin15
  _74173 _74173_4 (
    .pin1(_74173_1_pin1), .pin2(_74173_1_pin1), .pin3(_74173_4_pin3), .pin4(_74173_4_pin4),
    .pin5(_74173_4_pin5), .pin6(_74173_4_pin6), .pin8(1'b0), .pin11(_74173_4_pin11), .pin12(_74173_4_pin12),
    .pin13(_74173_4_pin13), .pin14(_74173_4_pin14), .pin16(1'b1));  // open: pin7, pin9, pin10, pin15
  _74193 _74193_1 (
    .pin1(BUS1), .pin2(A1_t), .pin3(A0_t), .pin4(in_8), .pin5(in_7), .pin6(A2_t), .pin7(A3_t), .pin8(1'b0),
    .pin9(BUS3), .pin10(BUS2), .pin11(in_10), .pin12(_74193_1_pin12), .pin13(_74193_1_pin13), .pin14(in_9),
    .pin15(BUS0), .pin16(1'b1));
  _74193 _74193_2 (
    .pin1(BUS5), .pin2(A5), .pin3(A4), .pin4(_74193_1_pin13), .pin5(_74193_1_pin12), .pin6(A6), .pin7(A7),
    .pin8(1'b0), .pin9(BUS7), .pin10(BUS6), .pin11(in_10), .pin12(_74193_2_pin12), .pin13(_74193_2_pin13),
    .pin14(in_9), .pin15(BUS4), .pin16(1'b1));
  _74193 _74193_3 (
    .pin1(BUS9), .pin2(A9), .pin3(A8), .pin4(_74193_2_pin13), .pin5(_74193_2_pin12), .pin6(A10), .pin7(A11),
    .pin8(1'b0), .pin9(BUS11), .pin10(BUS10), .pin11(in_10), .pin12(_74193_3_pin12), .pin13(_74193_3_pin13),
    .pin14(in_9), .pin15(BUS8), .pin16(1'b1));
  _74193 _74193_4 (
    .pin1(BUS13), .pin2(A13), .pin3(A12), .pin4(_74193_3_pin13), .pin5(_74193_3_pin12), .pin6(A14),
    .pin7(A15), .pin8(1'b0), .pin9(BUS15), .pin10(BUS14), .pin11(in_10), .pin14(in_9), .pin15(BUS12),
    .pin16(1'b1));  // open: pin12, pin13

  // Other names for the same wires on the sheet: DN = in_8; nLD = in_10; RES = in_9; UP = in_7

  // Notes on the sheet:
  //   nWE: default 1
  //   ENTER H
  //   Data Input
  //   BUS DATA
  //   ENTER L
  //   PROGRAM COUNTER
endmodule
