// Digital circuit 74HC670_register_file.dig as structural Verilog
module _74HC670_register_file (
);

  wire _74193_1_pin12, _74193_1_pin13, _74193_1_pin14, _74193_2_pin12, _74193_2_pin13, _74670_1_pin1,
       _74670_1_pin2, _74670_1_pin3, _74670_1_pin6, _74670_1_pin7, _74670_1_pin9, _74670_1_pin10,
       _74670_1_pin15, _74670_2_pin1, _74670_2_pin2, _74670_2_pin3, _74670_2_pin6, _74670_2_pin7,
       _74670_2_pin9, _74670_2_pin10, _74670_2_pin15, A0, A1, A2, A3, A4, A5, A6, A7, D0, D1, D2, D3, D4, D5,
       D6, D7, DN, nLD, Q0, Q1, Q2, Q3, Q4, Q5, Q6, Q7, RA, RB, UP, WA, WB;

  _74193 _74193_1 (
    .pin1(D1), .pin2(Q1), .pin3(Q0), .pin4(DN), .pin5(UP), .pin6(Q2), .pin7(Q3), .pin8(1'b0), .pin9(D3),
    .pin10(D2), .pin11(nLD), .pin12(_74193_1_pin12), .pin13(_74193_1_pin13), .pin14(_74193_1_pin14),
    .pin15(D0), .pin16(1'b1));
  _74193 _74193_2 (
    .pin1(D5), .pin2(Q5), .pin3(Q4), .pin4(_74193_1_pin13), .pin5(_74193_1_pin12), .pin6(Q6), .pin7(Q7),
    .pin8(1'b0), .pin9(D7), .pin10(D6), .pin11(nLD), .pin12(_74193_2_pin12), .pin13(_74193_2_pin13),
    .pin14(_74193_1_pin14), .pin15(D4), .pin16(1'b1));
  Seven_Seg_Hex seven_seg_hex_1 (.d({A7, A6, A5, A4}), .dp(1'b0));
  Seven_Seg_Hex seven_seg_hex_2 (.d({A3, A2, A1, A0}), .dp(1'b0));
  Seven_Seg_Hex seven_seg_hex_3 (.d({D7, D6, D5, D4}), .dp(1'b0));
  Seven_Seg_Hex seven_seg_hex_4 (.d({D3, D2, D1, D0}), .dp(1'b0));
  _74670 _74670_1 (
    .pin1(_74670_1_pin1), .pin2(_74670_1_pin2), .pin3(_74670_1_pin3), .pin4(RB), .pin5(RA),
    .pin6(_74670_1_pin6), .pin7(_74670_1_pin7), .pin8(1'b0), .pin9(_74670_1_pin9), .pin10(_74670_1_pin10),
    .pin13(WB), .pin14(WA), .pin15(_74670_1_pin15), .pin16(1'b1));  // open: pin11, pin12
  _74670 _74670_2 (
    .pin1(_74670_2_pin1), .pin2(_74670_2_pin2), .pin3(_74670_2_pin3), .pin4(RB), .pin5(RA),
    .pin6(_74670_2_pin6), .pin7(_74670_2_pin7), .pin8(1'b0), .pin9(_74670_2_pin9), .pin10(_74670_2_pin10),
    .pin13(WB), .pin14(WA), .pin15(_74670_2_pin15), .pin16(1'b1));  // open: pin11, pin12

  // Notes on the sheet:
  //   8-bit U/D COUNTER
  //   ADDRESS
  //   DATA
endmodule
