// Digital circuit 8_bit_2_1_mux.dig as structural Verilog
module _8_bit_2_1_mux (
  input  in_1,
  input  in_2,
  input  in_3,
  input  in_4,
  input  in_5,
  input  in_6,
  input  in_7,
  input  in_8,
  input  in_9,
  input  in_10,
  input  in_11,
  input  in_12,
  input  in_13,
  input  in_14,
  input  in_15,
  input  in_16,
  input  S1,
  input  S0,
  output out_17,
  output out_18,
  output out_19,
  output out_20,
  output out_21,
  output out_22,
  output out_23,
  output out_24
);

  wire nand_1_out, nand_2_out, nand_3_out, nand_4_out, nand_5_out, nand_6_out, nand_7_out, nand_8_out,
       nand_9_out, nand_10_out, nand_11_out, nand_12_out, nand_13_out, nand_14_out, nand_15_out, nand_16_out;

  nand nand_1 (nand_1_out, in_12, S0);
  nand nand_2 (nand_2_out, in_8, S1);
  nand nand_3 (nand_3_out, in_11, S0);
  nand nand_4 (nand_4_out, in_7, S1);
  nand nand_5 (nand_5_out, in_10, S0);
  nand nand_6 (nand_6_out, in_6, S1);
  nand nand_7 (nand_7_out, in_9, S0);
  nand nand_8 (nand_8_out, in_5, S1);
  nand nand_9 (nand_9_out, in_13, S0);
  nand nand_10 (nand_10_out, in_4, S1);
  nand nand_11 (nand_11_out, in_14, S0);
  nand nand_12 (nand_12_out, in_3, S1);
  nand nand_13 (nand_13_out, in_15, S0);
  nand nand_14 (nand_14_out, in_2, S1);
  nand nand_15 (nand_15_out, in_16, S0);
  nand nand_16 (nand_16_out, in_1, S1);
  nand nand_17 (out_17, nand_1_out, nand_2_out);
  nand nand_18 (out_18, nand_3_out, nand_4_out);
  nand nand_19 (out_19, nand_5_out, nand_6_out);
  nand nand_20 (out_20, nand_7_out, nand_8_out);
  nand nand_21 (out_21, nand_9_out, nand_10_out);
  nand nand_22 (out_22, nand_11_out, nand_12_out);
  nand nand_23 (out_23, nand_13_out, nand_14_out);
  nand nand_24 (out_24, nand_15_out, nand_16_out);
endmodule
