// Digital circuit 8_bit_ALU_ACC_PC_1.dig as structural Verilog
module _8_bit_ALU_ACC_PC_1 (
  input  D0,
  input  CLK,
  input  I1,
  input  I0,
  input  NEG,
  input  Cin,
  input  D1,
  input  D2,
  input  D3,
  input  D4,
  input  D5,
  input  D6,
  input  D7,
  input  PCin,
  input  Sel_Data,
  input  Sel_PC,
  input  in_38,
  input  in_39,
  input  in_40,
  input  in_41,
  input  in_42,
  input  in_43,
  input  in_44,
  input  in_45,
  input  in_46,
  input  in_47,
  input  in_48,
  input  in_49,
  output Q0,
  output Q1,
  output Q2,
  output Q3,
  output Q4,
  output Q5,
  output Q6,
  output Q7,
  output Cout,
  output A3,
  output A2,
  output A1,
  output A0,
  output A5,
  output A4,
  output A7,
  output A6,
  output A9,
  output A8,
  output A11,
  output A10
);

  wire AL, AR0, AR1, AR2, AR3, diodebackward_1_out, diodebackward_3_out, diodebackward_6_out,
       diodebackward_11_out, diodebackward_15_out, F0, F1, F2, F3, F4, F5, F6, F7, nand_1_out, nand_2_out,
       nand_3_out, nand_4_out, nand_5_out, nand_6_out, nand_7_out, nand_8_out, nand_9_out, nand_10_out,
       nand_11_out, nand_12_out, nand_13_out, nand_14_out, nand_15_out, nand_16_out, nand_17_out,
       nand_18_out, nand_19_out, nand_20_out, nand_21_out, nand_22_out, nand_23_out, nand_24_out,
       nand_25_out, nand_34_out, nand_35_out, nand_37_out, nand_38_out, nand_39_out, nand_40_out,
       nand_41_out, nand_42_out, nand_43_out, nand_44_out, nand_45_out, nand_46_out, nand_47_out,
       nand_48_out, nand_49_out, nand_50_out, nand_51_out, nand_52_out, nand_53_out, nand_54_out,
       nand_55_out, nand_56_out, nand_57_out, nand_58_out, nand_59_out, nand_60_out, nand_61_out,
       nand_62_out, nand_63_out, nand_64_out, nand_65_out, nand_66_out, nand_67_out, nand_68_out,
       nand_69_out, nand_70_out, nand_71_out, nand_72_out, nand_73_out, nand_74_out, nand_75_out,
       nand_76_out, nand_77_out, nand_78_out, nand_79_out, nand_80_out, nand_81_out, nand_82_out,
       nand_83_out, nand_84_out, nand_85_out, nand_86_out, nand_87_out, nand_88_out, nand_89_out,
       nand_90_out, nand_91_out, nand_92_out, nand_93_out, nand_94_out, nand_95_out, nand_96_out,
       nand_97_out, nand_98_out, nand_99_out, nand_100_out, nand_101_out, nand_102_out, nand_103_out,
       nand_104_out, nand_105_out, nand_106_out, nand_107_out, nand_108_out, nand_109_out, nand_110_out,
       nand_111_out, nand_112_out, nand_113_out, nand_114_out, nand_115_out, nand_116_out, nand_117_out,
       nand_118_out, nand_119_out, nand_120_out, nand_121_out, nand_122_out, nand_123_out, nand_124_out,
       nand_125_out, nand_126_out, nand_127_out, nand_128_out, nand_129_out, nand_130_out, nand_131_out,
       nand_132_out, nand_133_out, nand_134_out, nand_135_out, nand_136_out, nand_137_out, nand_138_out,
       nand_139_out, nand_140_out, nand_141_out, nand_142_out, nand_143_out, nand_144_out, nand_145_out,
       nand_146_out, nand_147_out, nand_148_out, nand_149_out, nand_150_out, nand_151_out, nand_152_out,
       nand_153_out, nand_154_out, nand_155_out, nand_156_out, nand_157_out, nand_158_out, nand_159_out,
       nand_160_out, nand_161_out, nand_162_out, nand_163_out, nand_164_out, nand_165_out, nand_166_out,
       nand_168_out, nand_170_out, nand_173_out, nand_175_out, nand_177_out, nand_180_out, nand_182_out,
       nand_183_out, nand_184_out, nand_185_out, nand_186_out, nand_187_out, nand_188_out, nand_189_out,
       nand_190_out, nand_191_out, nand_192_out, nand_193_out, nand_194_out, nand_195_out, nand_196_out,
       nand_197_out, nand_198_out, nand_199_out, nand_200_out, nand_201_out, nand_202_out, nand_203_out,
       nand_204_out, nand_205_out, nand_206_out, nand_207_out, nand_208_out, nand_209_out, nand_210_out,
       nand_211_out, nand_212_out, nand_213_out, nand_214_out, nand_215_out, nand_216_out, nand_217_out,
       nand_218_out, nand_219_out, nand_220_out, nand_221_out, nand_222_out, nand_223_out, nand_224_out,
       nand_225_out, nand_226_out, nand_227_out, nand_228_out, nand_229_out, nand_230_out, nand_231_out,
       nand_232_out, nand_233_out, nand_234_out, nand_235_out, nand_236_out, nand_237_out, nand_239_out,
       nand_241_out, nand_243_out, nand_245_out, nand_247_out, nand_249_out, nand_251_out, nand_253_out,
       nand_254_out, nand_255_out, nand_256_out, nand_257_out, nand_258_out, nand_259_out, nand_260_out,
       nand_261_out, nand_262_out, nand_263_out, nand_264_out, nand_265_out, nand_266_out, nand_267_out,
       nand_268_out, nand_269_out, nand_270_out, nand_271_out, nand_272_out, nand_273_out, nand_274_out,
       nand_275_out, nand_276_out, nand_277_out, nand_278_out, nand_279_out, nand_280_out, nand_281_out,
       nand_282_out, nand_283_out, nand_284_out, nand_285_out, nand_286_out, nand_287_out, nand_288_out,
       nand_289_out, nand_290_out, nand_291_out, nand_292_out, nand_293_out, nand_294_out, nand_295_out,
       nand_296_out, nand_297_out, nand_298_out, nand_299_out, nand_300_out, nand_301_out, nand_302_out,
       nand_303_out, nand_304_out, nand_305_out, nand_306_out, nand_307_out, nand_308_out, nand_309_out,
       nand_310_out, nand_311_out, nand_312_out, nand_313_out, nand_314_out, nand_315_out, nand_316_out,
       nand_317_out, nand_318_out, nand_319_out, nand_320_out, nand_321_out, nand_322_out, nand_323_out,
       nand_324_out, nand_325_out, nand_326_out, nand_327_out, nand_328_out, nand_329_out, nand_330_out,
       nand_331_out, nand_332_out, nand_333_out, nand_334_out, nand_335_out, nand_336_out, nand_337_out,
       nand_338_out, nand_339_out, nand_340_out, nand_341_out, nand_342_out, nand_343_out, nand_344_out,
       nand_345_out, nand_346_out, nand_347_out, nand_348_out, nand_349_out, nand_350_out, nand_351_out,
       nand_352_out, nand_353_out, nand_354_out, nand_355_out, nand_356_out, nand_357_out, nand_358_out,
       nand_359_out, nand_360_out, nand_361_out, nand_362_out, nand_363_out, nand_364_out, nand_365_out,
       nand_366_out, nand_367_out, nand_368_out, nand_369_out, nand_370_out, nand_371_out, nand_372_out,
       nand_373_out, nand_374_out, nand_375_out, nand_376_out, nand_377_out, nand_378_out, nand_379_out,
       nand_380_out, nand_381_out, nand_382_out, nand_383_out, nand_384_out, nand_385_out, nand_386_out,
       nand_387_out, nand_388_out, nand_389_out, nand_390_out, nand_391_out, nand_392_out, nand_393_out,
       nand_394_out, nand_395_out, nand_396_out, nand_397_out, nand_398_out, nand_399_out, nand_400_out,
       nand_401_out, nand_402_out, nand_403_out, nand_404_out, nand_405_out, nand_406_out, nand_407_out,
       nand_408_out, nand_409_out, nand_410_out, nand_411_out, nand_412_out, nand_413_out, nand_414_out,
       nand_415_out, nand_416_out, nand_417_out, nand_418_out, nand_419_out, nand_420_out, nand_421_out,
       nand_423_out, nand_425_out, nand_427_out, nand_429_out, nand_431_out, nand_433_out, nand_435_out,
       nand_437_out, nand_439_out, nand_441_out, nand_443_out, nand_445_out, nJMP, nW, W;

  nand nand_1 (nand_1_out, in_39, in_39);
  nand nand_2 (nand_2_out, in_40, in_40);
  nand nand_3 (nand_3_out, in_41, in_41);
  nand nand_4 (nand_4_out, nand_1_out, nand_2_out);
  nand nand_5 (nand_5_out, in_39, nand_2_out);
  nand nand_6 (nand_6_out, nand_1_out, in_40);
  nand nand_7 (nand_7_out, in_39, in_40);
  nand nand_8 (nand_8_out, nand_1_out, nand_2_out);
  nand nand_9 (nand_9_out, in_39, nand_2_out);
  nand nand_10 (nand_10_out, nand_1_out, in_40);
  nand nand_11 (nand_11_out, in_39, in_40);
  nand nand_12 (nand_12_out, in_38, nand_4_out);
  nand nand_13 (nand_13_out, in_38, nand_5_out);
  nand nand_14 (nand_14_out, in_38, nand_6_out);
  nand nand_15 (nand_15_out, in_38, nand_7_out);
  nand nand_16 (nand_16_out, in_38, nand_8_out);
  nand nand_17 (nand_17_out, in_38, nand_9_out);
  nand nand_18 (nand_18_out, in_38, nand_10_out);
  nand nand_19 (nand_19_out, in_38, nand_11_out);
  nand nand_20 (nand_20_out, nand_12_out, nand_3_out);
  nand nand_21 (nand_21_out, nand_13_out, nand_3_out);
  nand nand_22 (nand_22_out, nand_14_out, nand_3_out);
  nand nand_23 (nand_23_out, nand_15_out, nand_3_out);
  nand nand_24 (nand_24_out, nand_16_out, in_41);
  nand nand_25 (nand_25_out, nand_17_out, in_41);
  nand nand_26 (nW, nand_18_out, in_41);
  nand nand_27 (nJMP, nand_19_out, in_41);
  DiodeBackward diodebackward_1 (.in(nJMP), .out(diodebackward_1_out));
  DiodeBackward diodebackward_2 (.in(in_41), .out(diodebackward_1_out));
  PullUp pullup_1 (.out(diodebackward_1_out));
  DiodeBackward diodebackward_3 (.in(nand_20_out), .out(diodebackward_3_out));
  DiodeBackward diodebackward_4 (.in(nand_21_out), .out(diodebackward_3_out));
  DiodeBackward diodebackward_5 (.in(nand_22_out), .out(diodebackward_3_out));
  nand nand_28 (AL, diodebackward_1_out, diodebackward_1_out);
  PullUp pullup_2 (.out(diodebackward_3_out));
  DiodeBackward diodebackward_6 (.in(nand_20_out), .out(diodebackward_6_out));
  DiodeBackward diodebackward_7 (.in(nand_22_out), .out(diodebackward_6_out));
  DiodeBackward diodebackward_8 (.in(nand_23_out), .out(diodebackward_6_out));
  DiodeBackward diodebackward_9 (.in(nand_24_out), .out(diodebackward_6_out));
  DiodeBackward diodebackward_10 (.in(nJMP), .out(diodebackward_6_out));
  nand nand_29 (AR3, diodebackward_3_out, diodebackward_3_out);
  PullUp pullup_3 (.out(diodebackward_6_out));
  DiodeBackward diodebackward_11 (.in(nand_22_out), .out(diodebackward_11_out));
  DiodeBackward diodebackward_12 (.in(nand_23_out), .out(diodebackward_11_out));
  DiodeBackward diodebackward_13 (.in(nand_24_out), .out(diodebackward_11_out));
  DiodeBackward diodebackward_14 (.in(nand_25_out), .out(diodebackward_11_out));
  nand nand_30 (AR2, diodebackward_6_out, diodebackward_6_out);
  PullUp pullup_4 (.out(diodebackward_11_out));
  DiodeBackward diodebackward_15 (.in(nand_25_out), .out(diodebackward_15_out));
  DiodeBackward diodebackward_16 (.in(nJMP), .out(diodebackward_15_out));
  nand nand_31 (AR1, diodebackward_11_out, diodebackward_11_out);
  PullUp pullup_5 (.out(diodebackward_15_out));
  nand nand_32 (AR0, diodebackward_15_out, diodebackward_15_out);
  nand nand_33 (W, nW, nW);
  nand nand_34 (nand_34_out, 1'b0, 1'b0);
  LED led_1 (.in(nand_20_out));
  LED led_2 (.in(nand_21_out));
  LED led_3 (.in(nand_22_out));
  LED led_4 (.in(nand_23_out));
  LED led_5 (.in(nand_24_out));
  LED led_6 (.in(nand_25_out));
  LED led_7 (.in(nW));
  LED led_8 (.in(nJMP));
  nand nand_35 (nand_35_out, 1'b0, 1'b0);
  Seven_Seg_Hex seven_seg_hex_1 (.d({A7, A6, A5, A4}), .dp(1'b0));
  Seven_Seg_Hex seven_seg_hex_2 (.d({3'b000, AL}), .dp(1'b0));
  Seven_Seg_Hex seven_seg_hex_3 (.d({A3, A2, A1, A0}), .dp(1'b0));
  Seven_Seg_Hex seven_seg_hex_4 (.d({AR3, AR2, AR1, AR0}), .dp(1'b0));
  Seven_Seg_Hex seven_seg_hex_5 (.d({F7, F6, F5, F4}), .dp(1'b0));
  Seven_Seg_Hex seven_seg_hex_6 (.d({F3, F2, F1, F0}), .dp(1'b0));
  Seven_Seg_Hex seven_seg_hex_7 (.d({Q7, Q6, Q5, Q4}), .dp(1'b0));
  Seven_Seg_Hex seven_seg_hex_8 (.d({Q3, Q2, Q1, Q0}), .dp(1'b0));
  Seven_Seg_Hex seven_seg_hex_9 (.d({D7, D6, D5, D4}), .dp(1'b0));
  Seven_Seg_Hex seven_seg_hex_10 (.d({D3, D2, D1, D0}), .dp(1'b0));
  nand nand_36 (AL, I1, I1);
  nand nand_37 (nand_37_out, D7, NEG);
  nand nand_38 (nand_38_out, D6, NEG);
  nand nand_39 (nand_39_out, D5, NEG);
  nand nand_40 (nand_40_out, D4, NEG);
  nand nand_41 (nand_41_out, D3, NEG);
  nand nand_42 (nand_42_out, D2, NEG);
  nand nand_43 (nand_43_out, D1, NEG);
  nand nand_44 (nand_44_out, D0, NEG);
  nand nand_45 (nand_45_out, D7, nand_37_out);
  nand nand_46 (nand_46_out, nand_37_out, NEG);
  nand nand_47 (nand_47_out, D6, nand_38_out);
  nand nand_48 (nand_48_out, nand_38_out, NEG);
  nand nand_49 (nand_49_out, D5, nand_39_out);
  nand nand_50 (nand_50_out, nand_39_out, NEG);
  nand nand_51 (nand_51_out, D4, nand_40_out);
  nand nand_52 (nand_52_out, nand_40_out, NEG);
  nand nand_53 (nand_53_out, D3, nand_41_out);
  nand nand_54 (nand_54_out, nand_41_out, NEG);
  nand nand_55 (nand_55_out, D2, nand_42_out);
  nand nand_56 (nand_56_out, nand_42_out, NEG);
  nand nand_57 (nand_57_out, D1, nand_43_out);
  nand nand_58 (nand_58_out, nand_43_out, NEG);
  nand nand_59 (nand_59_out, D0, nand_44_out);
  nand nand_60 (nand_60_out, nand_44_out, NEG);
  nand nand_61 (nand_61_out, nand_45_out, nand_46_out);
  nand nand_62 (nand_62_out, nand_47_out, nand_48_out);
  nand nand_63 (nand_63_out, nand_49_out, nand_50_out);
  nand nand_64 (nand_64_out, nand_51_out, nand_52_out);
  nand nand_65 (nand_65_out, nand_53_out, nand_54_out);
  nand nand_66 (nand_66_out, nand_55_out, nand_56_out);
  nand nand_67 (nand_67_out, nand_57_out, nand_58_out);
  nand nand_68 (nand_68_out, nand_59_out, nand_60_out);
  nand nand_69 (nand_69_out, Q7, nand_61_out);
  nand nand_70 (nand_70_out, Q6, nand_62_out);
  nand nand_71 (nand_71_out, Q5, nand_63_out);
  nand nand_72 (nand_72_out, Q4, nand_64_out);
  nand nand_73 (nand_73_out, Q3, nand_65_out);
  nand nand_74 (nand_74_out, Q2, nand_66_out);
  nand nand_75 (nand_75_out, Q1, nand_67_out);
  nand nand_76 (nand_76_out, Q0, nand_68_out);
  nand nand_77 (nand_77_out, Q7, nand_69_out);
  nand nand_78 (nand_78_out, nand_69_out, nand_69_out);
  nand nand_79 (nand_79_out, nand_69_out, nand_61_out);
  nand nand_80 (nand_80_out, Q6, nand_70_out);
  nand nand_81 (nand_81_out, nand_70_out, nand_70_out);
  nand nand_82 (nand_82_out, nand_70_out, nand_62_out);
  nand nand_83 (nand_83_out, Q5, nand_71_out);
  nand nand_84 (nand_84_out, nand_71_out, nand_71_out);
  nand nand_85 (nand_85_out, nand_71_out, nand_63_out);
  nand nand_86 (nand_86_out, Q4, nand_72_out);
  nand nand_87 (nand_87_out, nand_72_out, nand_72_out);
  nand nand_88 (nand_88_out, nand_72_out, nand_64_out);
  nand nand_89 (nand_89_out, Q3, nand_73_out);
  nand nand_90 (nand_90_out, nand_73_out, nand_73_out);
  nand nand_91 (nand_91_out, nand_73_out, nand_65_out);
  nand nand_92 (nand_92_out, Q2, nand_74_out);
  nand nand_93 (nand_93_out, nand_74_out, nand_74_out);
  nand nand_94 (nand_94_out, nand_74_out, nand_66_out);
  nand nand_95 (nand_95_out, Q1, nand_75_out);
  nand nand_96 (nand_96_out, nand_75_out, nand_75_out);
  nand nand_97 (nand_97_out, nand_75_out, nand_67_out);
  nand nand_98 (nand_98_out, Q0, nand_76_out);
  nand nand_99 (nand_99_out, nand_76_out, nand_76_out);
  nand nand_100 (nand_100_out, nand_76_out, nand_68_out);
  nand nand_101 (nand_101_out, nand_77_out, nand_79_out);
  nand nand_102 (nand_102_out, nand_80_out, nand_82_out);
  nand nand_103 (nand_103_out, nand_83_out, nand_85_out);
  nand nand_104 (nand_104_out, nand_86_out, nand_88_out);
  nand nand_105 (nand_105_out, nand_89_out, nand_91_out);
  nand nand_106 (nand_106_out, nand_92_out, nand_94_out);
  nand nand_107 (nand_107_out, nand_95_out, nand_97_out);
  nand nand_108 (nand_108_out, nand_98_out, nand_100_out);
  nand nand_109 (nand_109_out, nand_78_out, I1);
  nand nand_110 (nand_110_out, nand_101_out, I0);
  nand nand_111 (nand_111_out, nand_81_out, I1);
  nand nand_112 (nand_112_out, nand_102_out, I0);
  nand nand_113 (nand_113_out, nand_84_out, I1);
  nand nand_114 (nand_114_out, nand_103_out, I0);
  nand nand_115 (nand_115_out, nand_87_out, I1);
  nand nand_116 (nand_116_out, nand_104_out, I0);
  nand nand_117 (nand_117_out, nand_90_out, I1);
  nand nand_118 (nand_118_out, nand_105_out, I0);
  nand nand_119 (nand_119_out, nand_93_out, I1);
  nand nand_120 (nand_120_out, nand_106_out, I0);
  nand nand_121 (nand_121_out, nand_96_out, I1);
  nand nand_122 (nand_122_out, nand_107_out, I0);
  nand nand_123 (nand_123_out, nand_99_out, I1);
  nand nand_124 (nand_124_out, nand_108_out, I0);
  nand nand_125 (nand_125_out, nand_109_out, nand_110_out);
  nand nand_126 (nand_126_out, nand_111_out, nand_112_out);
  nand nand_127 (nand_127_out, nand_113_out, nand_114_out);
  nand nand_128 (nand_128_out, nand_115_out, nand_116_out);
  nand nand_129 (nand_129_out, nand_117_out, nand_118_out);
  nand nand_130 (nand_130_out, nand_119_out, nand_120_out);
  nand nand_131 (nand_131_out, nand_121_out, nand_122_out);
  nand nand_132 (nand_132_out, nand_123_out, nand_124_out);
  nand nand_133 (nand_133_out, nand_125_out, nand_182_out);
  nand nand_134 (nand_134_out, nand_126_out, nand_183_out);
  nand nand_135 (nand_135_out, nand_127_out, nand_184_out);
  nand nand_136 (nand_136_out, nand_128_out, nand_185_out);
  nand nand_137 (nand_137_out, nand_129_out, nand_186_out);
  nand nand_138 (nand_138_out, nand_130_out, nand_187_out);
  nand nand_139 (nand_139_out, nand_131_out, nand_188_out);
  nand nand_140 (nand_140_out, nand_132_out, Cin);
  nand nand_141 (nand_141_out, nand_125_out, nand_133_out);
  nand nand_142 (nand_142_out, nand_133_out, nand_182_out);
  nand nand_143 (nand_143_out, nand_133_out, nand_69_out);
  nand nand_144 (nand_144_out, nand_126_out, nand_134_out);
  nand nand_145 (nand_145_out, nand_134_out, nand_183_out);
  nand nand_146 (nand_146_out, nand_134_out, nand_70_out);
  nand nand_147 (nand_147_out, nand_127_out, nand_135_out);
  nand nand_148 (nand_148_out, nand_135_out, nand_184_out);
  nand nand_149 (nand_149_out, nand_135_out, nand_71_out);
  nand nand_150 (nand_150_out, nand_128_out, nand_136_out);
  nand nand_151 (nand_151_out, nand_136_out, nand_185_out);
  nand nand_152 (nand_152_out, nand_136_out, nand_72_out);
  nand nand_153 (nand_153_out, nand_129_out, nand_137_out);
  nand nand_154 (nand_154_out, nand_137_out, nand_186_out);
  nand nand_155 (nand_155_out, nand_137_out, nand_73_out);
  nand nand_156 (nand_156_out, nand_130_out, nand_138_out);
  nand nand_157 (nand_157_out, nand_138_out, nand_187_out);
  nand nand_158 (nand_158_out, nand_138_out, nand_74_out);
  nand nand_159 (nand_159_out, nand_131_out, nand_139_out);
  nand nand_160 (nand_160_out, nand_139_out, nand_188_out);
  nand nand_161 (nand_161_out, nand_139_out, nand_75_out);
  nand nand_162 (nand_162_out, nand_132_out, nand_140_out);
  nand nand_163 (nand_163_out, nand_140_out, Cin);
  nand nand_164 (nand_164_out, nand_140_out, nand_76_out);
  nand nand_165 (nand_165_out, nand_149_out, AL);
  nand nand_166 (nand_166_out, nand_161_out, AL);
  nand nand_167 (F7, nand_141_out, nand_142_out);
  nand nand_168 (nand_168_out, nand_143_out, AL);
  nand nand_169 (F6, nand_144_out, nand_145_out);
  nand nand_170 (nand_170_out, nand_146_out, AL);
  nand nand_171 (F5, nand_147_out, nand_148_out);
  nand nand_172 (F4, nand_150_out, nand_151_out);
  nand nand_173 (nand_173_out, nand_152_out, AL);
  nand nand_174 (F3, nand_153_out, nand_154_out);
  nand nand_175 (nand_175_out, nand_155_out, AL);
  nand nand_176 (F2, nand_156_out, nand_157_out);
  nand nand_177 (nand_177_out, nand_158_out, AL);
  nand nand_178 (F1, nand_159_out, nand_160_out);
  nand nand_179 (F0, nand_162_out, nand_163_out);
  nand nand_180 (nand_180_out, nand_164_out, AL);
  nand nand_181 (Cout, nand_168_out, nand_168_out);
  nand nand_182 (nand_182_out, nand_170_out, nand_170_out);
  nand nand_183 (nand_183_out, nand_165_out, nand_165_out);
  nand nand_184 (nand_184_out, nand_173_out, nand_173_out);
  nand nand_185 (nand_185_out, nand_175_out, nand_175_out);
  nand nand_186 (nand_186_out, nand_177_out, nand_177_out);
  nand nand_187 (nand_187_out, nand_166_out, nand_166_out);
  nand nand_188 (nand_188_out, nand_180_out, nand_180_out);
  nand nand_189 (nand_189_out, CLK, CLK);
  nand nand_190 (nand_190_out, F7, nand_189_out);
  nand nand_191 (nand_191_out, nand_190_out, nand_189_out);
  nand nand_192 (nand_192_out, F6, nand_189_out);
  nand nand_193 (nand_193_out, nand_192_out, nand_189_out);
  nand nand_194 (nand_194_out, F5, nand_189_out);
  nand nand_195 (nand_195_out, nand_194_out, nand_189_out);
  nand nand_196 (nand_196_out, F4, nand_189_out);
  nand nand_197 (nand_197_out, nand_196_out, nand_189_out);
  nand nand_198 (nand_198_out, F3, nand_189_out);
  nand nand_199 (nand_199_out, nand_198_out, nand_189_out);
  nand nand_200 (nand_200_out, F2, nand_189_out);
  nand nand_201 (nand_201_out, nand_200_out, nand_189_out);
  nand nand_202 (nand_202_out, F1, nand_189_out);
  nand nand_203 (nand_203_out, nand_202_out, nand_189_out);
  nand nand_204 (nand_204_out, F0, nand_189_out);
  nand nand_205 (nand_205_out, nand_204_out, nand_189_out);
  nand nand_206 (nand_206_out, nand_190_out, nand_207_out);
  nand nand_207 (nand_207_out, nand_206_out, nand_191_out);
  nand nand_208 (nand_208_out, nand_192_out, nand_209_out);
  nand nand_209 (nand_209_out, nand_208_out, nand_193_out);
  nand nand_210 (nand_210_out, nand_194_out, nand_211_out);
  nand nand_211 (nand_211_out, nand_210_out, nand_195_out);
  nand nand_212 (nand_212_out, nand_196_out, nand_213_out);
  nand nand_213 (nand_213_out, nand_212_out, nand_197_out);
  nand nand_214 (nand_214_out, nand_198_out, nand_215_out);
  nand nand_215 (nand_215_out, nand_214_out, nand_199_out);
  nand nand_216 (nand_216_out, nand_200_out, nand_217_out);
  nand nand_217 (nand_217_out, nand_216_out, nand_201_out);
  nand nand_218 (nand_218_out, nand_202_out, nand_219_out);
  nand nand_219 (nand_219_out, nand_218_out, nand_203_out);
  nand nand_220 (nand_220_out, nand_204_out, nand_221_out);
  nand nand_221 (nand_221_out, nand_220_out, nand_205_out);
  nand nand_222 (nand_222_out, nand_206_out, CLK);
  nand nand_223 (nand_223_out, nand_222_out, CLK);
  nand nand_224 (nand_224_out, nand_208_out, CLK);
  nand nand_225 (nand_225_out, nand_224_out, CLK);
  nand nand_226 (nand_226_out, nand_210_out, CLK);
  nand nand_227 (nand_227_out, nand_226_out, CLK);
  nand nand_228 (nand_228_out, nand_212_out, CLK);
  nand nand_229 (nand_229_out, nand_228_out, CLK);
  nand nand_230 (nand_230_out, nand_214_out, CLK);
  nand nand_231 (nand_231_out, nand_230_out, CLK);
  nand nand_232 (nand_232_out, nand_216_out, CLK);
  nand nand_233 (nand_233_out, nand_232_out, CLK);
  nand nand_234 (nand_234_out, nand_218_out, CLK);
  nand nand_235 (nand_235_out, nand_234_out, CLK);
  nand nand_236 (nand_236_out, nand_220_out, CLK);
  nand nand_237 (nand_237_out, nand_236_out, CLK);
  nand nand_238 (Q7, nand_222_out, nand_239_out);
  nand nand_239 (nand_239_out, Q7, nand_223_out);
  nand nand_240 (Q6, nand_224_out, nand_241_out);
  nand nand_241 (nand_241_out, Q6, nand_225_out);
  nand nand_242 (Q5, nand_226_out, nand_243_out);
  nand nand_243 (nand_243_out, Q5, nand_227_out);
  nand nand_244 (Q4, nand_228_out, nand_245_out);
  nand nand_245 (nand_245_out, Q4, nand_229_out);
  nand nand_246 (Q3, nand_230_out, nand_247_out);
  nand nand_247 (nand_247_out, Q3, nand_231_out);
  nand nand_248 (Q2, nand_232_out, nand_249_out);
  nand nand_249 (nand_249_out, Q2, nand_233_out);
  nand nand_250 (Q1, nand_234_out, nand_251_out);
  nand nand_251 (nand_251_out, Q1, nand_235_out);
  nand nand_252 (Q0, nand_236_out, nand_253_out);
  nand nand_253 (nand_253_out, Q0, nand_237_out);
  nand nand_254 (nand_254_out, nand_255_out, A11);
  nand nand_255 (nand_255_out, nand_256_out, nand_256_out);
  nand nand_256 (nand_256_out, nand_278_out, A10);
  nand nand_257 (nand_257_out, nand_258_out, A9);
  nand nand_258 (nand_258_out, nand_259_out, nand_259_out);
  nand nand_259 (nand_259_out, nand_283_out, A8);
  nand nand_260 (nand_260_out, nand_261_out, A7);
  nand nand_261 (nand_261_out, nand_262_out, nand_262_out);
  nand nand_262 (nand_262_out, nand_288_out, A6);
  nand nand_263 (nand_263_out, nand_264_out, A5);
  nand nand_264 (nand_264_out, nand_265_out, nand_265_out);
  nand nand_265 (nand_265_out, nand_266_out, A4);
  nand nand_266 (nand_266_out, nand_267_out, nand_267_out);
  nand nand_267 (nand_267_out, nand_268_out, A3);
  nand nand_268 (nand_268_out, nand_269_out, nand_269_out);
  nand nand_269 (nand_269_out, nand_270_out, A2);
  nand nand_270 (nand_270_out, nand_271_out, nand_271_out);
  nand nand_271 (nand_271_out, nand_272_out, A1);
  nand nand_272 (nand_272_out, nand_273_out, nand_273_out);
  nand nand_273 (nand_273_out, PCin, A0);
  nand nand_274 (nand_274_out, nand_255_out, nand_254_out);
  nand nand_275 (nand_275_out, nand_254_out, A11);
  nand nand_276 (nand_276_out, nand_278_out, nand_256_out);
  nand nand_277 (nand_277_out, nand_256_out, A10);
  nand nand_278 (nand_278_out, nand_257_out, nand_257_out);
  nand nand_279 (nand_279_out, nand_258_out, nand_257_out);
  nand nand_280 (nand_280_out, nand_257_out, A9);
  nand nand_281 (nand_281_out, nand_283_out, nand_259_out);
  nand nand_282 (nand_282_out, nand_259_out, A8);
  nand nand_283 (nand_283_out, nand_260_out, nand_260_out);
  nand nand_284 (nand_284_out, nand_261_out, nand_260_out);
  nand nand_285 (nand_285_out, nand_260_out, A7);
  nand nand_286 (nand_286_out, nand_288_out, nand_262_out);
  nand nand_287 (nand_287_out, nand_262_out, A6);
  nand nand_288 (nand_288_out, nand_263_out, nand_263_out);
  nand nand_289 (nand_289_out, nand_264_out, nand_263_out);
  nand nand_290 (nand_290_out, nand_263_out, A5);
  nand nand_291 (nand_291_out, nand_266_out, nand_265_out);
  nand nand_292 (nand_292_out, nand_265_out, A4);
  nand nand_293 (nand_293_out, nand_268_out, nand_267_out);
  nand nand_294 (nand_294_out, nand_267_out, A3);
  nand nand_295 (nand_295_out, nand_270_out, nand_269_out);
  nand nand_296 (nand_296_out, nand_269_out, A2);
  nand nand_297 (nand_297_out, nand_272_out, nand_271_out);
  nand nand_298 (nand_298_out, nand_271_out, A1);
  nand nand_299 (nand_299_out, PCin, nand_273_out);
  nand nand_300 (nand_300_out, nand_273_out, A0);
  nand nand_301 (nand_301_out, nand_274_out, nand_275_out);
  nand nand_302 (nand_302_out, nand_276_out, nand_277_out);
  nand nand_303 (nand_303_out, nand_279_out, nand_280_out);
  nand nand_304 (nand_304_out, nand_281_out, nand_282_out);
  nand nand_305 (nand_305_out, nand_284_out, nand_285_out);
  nand nand_306 (nand_306_out, nand_286_out, nand_287_out);
  nand nand_307 (nand_307_out, nand_289_out, nand_290_out);
  nand nand_308 (nand_308_out, nand_291_out, nand_292_out);
  nand nand_309 (nand_309_out, nand_293_out, nand_294_out);
  nand nand_310 (nand_310_out, nand_295_out, nand_296_out);
  nand nand_311 (nand_311_out, nand_297_out, nand_298_out);
  nand nand_312 (nand_312_out, nand_299_out, nand_300_out);
  nand nand_313 (nand_313_out, Cin, Cin);
  nand nand_314 (nand_314_out, nand_301_out, nand_313_out);
  nand nand_315 (nand_315_out, nand_314_out, nand_313_out);
  nand nand_316 (nand_316_out, nand_302_out, nand_313_out);
  nand nand_317 (nand_317_out, nand_316_out, nand_313_out);
  nand nand_318 (nand_318_out, nand_303_out, nand_313_out);
  nand nand_319 (nand_319_out, nand_318_out, nand_313_out);
  nand nand_320 (nand_320_out, nand_304_out, nand_313_out);
  nand nand_321 (nand_321_out, nand_320_out, nand_313_out);
  nand nand_322 (nand_322_out, nand_305_out, nand_313_out);
  nand nand_323 (nand_323_out, nand_322_out, nand_313_out);
  nand nand_324 (nand_324_out, nand_306_out, nand_313_out);
  nand nand_325 (nand_325_out, nand_324_out, nand_313_out);
  nand nand_326 (nand_326_out, nand_307_out, nand_313_out);
  nand nand_327 (nand_327_out, nand_326_out, nand_313_out);
  nand nand_328 (nand_328_out, nand_308_out, nand_313_out);
  nand nand_329 (nand_329_out, nand_328_out, nand_313_out);
  nand nand_330 (nand_330_out, nand_309_out, nand_313_out);
  nand nand_331 (nand_331_out, nand_330_out, nand_313_out);
  nand nand_332 (nand_332_out, nand_310_out, nand_313_out);
  nand nand_333 (nand_333_out, nand_332_out, nand_313_out);
  nand nand_334 (nand_334_out, nand_311_out, nand_313_out);
  nand nand_335 (nand_335_out, nand_334_out, nand_313_out);
  nand nand_336 (nand_336_out, nand_312_out, nand_313_out);
  nand nand_337 (nand_337_out, nand_336_out, nand_313_out);
  nand nand_338 (nand_338_out, nand_314_out, nand_339_out);
  nand nand_339 (nand_339_out, nand_338_out, nand_315_out);
  nand nand_340 (nand_340_out, nand_316_out, nand_341_out);
  nand nand_341 (nand_341_out, nand_340_out, nand_317_out);
  nand nand_342 (nand_342_out, nand_318_out, nand_343_out);
  nand nand_343 (nand_343_out, nand_342_out, nand_319_out);
  nand nand_344 (nand_344_out, nand_320_out, nand_345_out);
  nand nand_345 (nand_345_out, nand_344_out, nand_321_out);
  nand nand_346 (nand_346_out, nand_322_out, nand_347_out);
  nand nand_347 (nand_347_out, nand_346_out, nand_323_out);
  nand nand_348 (nand_348_out, nand_324_out, nand_349_out);
  nand nand_349 (nand_349_out, nand_348_out, nand_325_out);
  nand nand_350 (nand_350_out, nand_326_out, nand_351_out);
  nand nand_351 (nand_351_out, nand_350_out, nand_327_out);
  nand nand_352 (nand_352_out, nand_328_out, nand_353_out);
  nand nand_353 (nand_353_out, nand_352_out, nand_329_out);
  nand nand_354 (nand_354_out, nand_330_out, nand_355_out);
  nand nand_355 (nand_355_out, nand_354_out, nand_331_out);
  nand nand_356 (nand_356_out, nand_332_out, nand_357_out);
  nand nand_357 (nand_357_out, nand_356_out, nand_333_out);
  nand nand_358 (nand_358_out, nand_334_out, nand_359_out);
  nand nand_359 (nand_359_out, nand_358_out, nand_335_out);
  nand nand_360 (nand_360_out, nand_336_out, nand_361_out);
  nand nand_361 (nand_361_out, nand_360_out, nand_337_out);
  nand nand_362 (nand_362_out, 1'b1, Sel_Data);
  nand nand_363 (nand_363_out, nand_338_out, Sel_PC);
  nand nand_364 (nand_364_out, 1'b1, Sel_Data);
  nand nand_365 (nand_365_out, nand_340_out, Sel_PC);
  nand nand_366 (nand_366_out, 1'b1, Sel_Data);
  nand nand_367 (nand_367_out, nand_342_out, Sel_PC);
  nand nand_368 (nand_368_out, 1'b1, Sel_Data);
  nand nand_369 (nand_369_out, nand_344_out, Sel_PC);
  nand nand_370 (nand_370_out, in_42, Sel_Data);
  nand nand_371 (nand_371_out, nand_346_out, Sel_PC);
  nand nand_372 (nand_372_out, in_43, Sel_Data);
  nand nand_373 (nand_373_out, nand_348_out, Sel_PC);
  nand nand_374 (nand_374_out, in_44, Sel_Data);
  nand nand_375 (nand_375_out, nand_350_out, Sel_PC);
  nand nand_376 (nand_376_out, in_45, Sel_Data);
  nand nand_377 (nand_377_out, nand_352_out, Sel_PC);
  nand nand_378 (nand_378_out, in_46, Sel_Data);
  nand nand_379 (nand_379_out, nand_354_out, Sel_PC);
  nand nand_380 (nand_380_out, in_47, Sel_Data);
  nand nand_381 (nand_381_out, nand_356_out, Sel_PC);
  nand nand_382 (nand_382_out, in_48, Sel_Data);
  nand nand_383 (nand_383_out, nand_358_out, Sel_PC);
  nand nand_384 (nand_384_out, in_49, Sel_Data);
  nand nand_385 (nand_385_out, nand_360_out, Sel_PC);
  nand nand_386 (nand_386_out, nand_362_out, nand_363_out);
  nand nand_387 (nand_387_out, nand_364_out, nand_365_out);
  nand nand_388 (nand_388_out, nand_366_out, nand_367_out);
  nand nand_389 (nand_389_out, nand_368_out, nand_369_out);
  nand nand_390 (nand_390_out, nand_370_out, nand_371_out);
  nand nand_391 (nand_391_out, nand_372_out, nand_373_out);
  nand nand_392 (nand_392_out, nand_374_out, nand_375_out);
  nand nand_393 (nand_393_out, nand_376_out, nand_377_out);
  nand nand_394 (nand_394_out, nand_378_out, nand_379_out);
  nand nand_395 (nand_395_out, nand_380_out, nand_381_out);
  nand nand_396 (nand_396_out, nand_382_out, nand_383_out);
  nand nand_397 (nand_397_out, nand_384_out, nand_385_out);
  nand nand_398 (nand_398_out, nand_386_out, Cin);
  nand nand_399 (nand_399_out, nand_398_out, Cin);
  nand nand_400 (nand_400_out, nand_387_out, Cin);
  nand nand_401 (nand_401_out, nand_400_out, Cin);
  nand nand_402 (nand_402_out, nand_388_out, Cin);
  nand nand_403 (nand_403_out, nand_402_out, Cin);
  nand nand_404 (nand_404_out, nand_389_out, Cin);
  nand nand_405 (nand_405_out, nand_404_out, Cin);
  nand nand_406 (nand_406_out, nand_390_out, Cin);
  nand nand_407 (nand_407_out, nand_406_out, Cin);
  nand nand_408 (nand_408_out, nand_391_out, Cin);
  nand nand_409 (nand_409_out, nand_408_out, Cin);
  nand nand_410 (nand_410_out, nand_392_out, Cin);
  nand nand_411 (nand_411_out, nand_410_out, Cin);
  nand nand_412 (nand_412_out, nand_393_out, Cin);
  nand nand_413 (nand_413_out, nand_412_out, Cin);
  nand nand_414 (nand_414_out, nand_394_out, Cin);
  nand nand_415 (nand_415_out, nand_414_out, Cin);
  nand nand_416 (nand_416_out, nand_395_out, Cin);
  nand nand_417 (nand_417_out, nand_416_out, Cin);
  nand nand_418 (nand_418_out, nand_396_out, Cin);
  nand nand_419 (nand_419_out, nand_418_out, Cin);
  nand nand_420 (nand_420_out, nand_397_out, Cin);
  nand nand_421 (nand_421_out, nand_420_out, Cin);
  nand nand_422 (A11, nand_398_out, nand_423_out);
  nand nand_423 (nand_423_out, A11, nand_399_out);
  nand nand_424 (A10, nand_400_out, nand_425_out);
  nand nand_425 (nand_425_out, A10, nand_401_out);
  nand nand_426 (A9, nand_402_out, nand_427_out);
  nand nand_427 (nand_427_out, A9, nand_403_out);
  nand nand_428 (A8, nand_404_out, nand_429_out);
  nand nand_429 (nand_429_out, A8, nand_405_out);
  nand nand_430 (A7, nand_406_out, nand_431_out);
  nand nand_431 (nand_431_out, A7, nand_407_out);
  nand nand_432 (A6, nand_408_out, nand_433_out);
  nand nand_433 (nand_433_out, A6, nand_409_out);
  nand nand_434 (A5, nand_410_out, nand_435_out);
  nand nand_435 (nand_435_out, A5, nand_411_out);
  nand nand_436 (A4, nand_412_out, nand_437_out);
  nand nand_437 (nand_437_out, A4, nand_413_out);
  nand nand_438 (A3, nand_414_out, nand_439_out);
  nand nand_439 (nand_439_out, A3, nand_415_out);
  nand nand_440 (A2, nand_416_out, nand_441_out);
  nand nand_441 (nand_441_out, A2, nand_417_out);
  nand nand_442 (A1, nand_418_out, nand_443_out);
  nand nand_443 (nand_443_out, A1, nand_419_out);
  nand nand_444 (A0, nand_420_out, nand_445_out);
  nand nand_445 (nand_445_out, A0, nand_421_out);

  // Other names for the same wires on the sheet: AC0 = Q0; AC1 = Q1; AC2 = Q2; AC3 = Q3; AC4 = Q4; AC5 = Q5; AC6 = Q6;
  //   AC7 = Q7; CLK_t = Cin; ID0 = in_49; ID1 = in_48; ID2 = in_47; ID3 = in_46; ID4 = in_45; ID5 = in_44;
  //   ID6 = in_43; ID7 = in_42; IR5 = in_39; IR6 = in_40; IR7 = in_41

  // Notes on the sheet:
  //   CLK: Hz: 2147483647
  //   A3: pin 28
  //   A2: pin 27
  //   A1: pin 26
  //   A0: pin 25
  //   A5: pin 30
  //   A4: pin 29
  //   A7: pin 32
  //   A6: pin 31
  //   A9: pin 34
  //   A8: pin 33
  //   A11: pin 36
  //   A10: pin 35
  //   PCin: pin 37
  //   Sel_Data: pin 38
  //   Sel_PC: pin 39
  //   in_38: default 1
  //   CONTROL UNIT
  //   3 to 8 Instruction decoder - 27 Gates
  //   Octal Inverter/Driver
  //   LOAD
  //   AND
  //   OR
  //   XOR
  //   ADD
  //   SUB
  //   STORE
  //   JMP
  //   INSTRUCTION
  //   PC
  //   ALU
  //   ACC
  //   BUS
  //   I1    I0      NEG   Cin    SC
  //   LD
  //   AND	1      0                           0		
  //   OR	1      1                           0
  //   XOR                     0      1                           0
  //   ADD                     0      1                           1
  //   SUB                     0      1       1      1         1
  //   ST
  //   JMP
  //   8-bit ALU and Accumulator 224 gates
  //   Master Slave arrangement using gated D-type latches
  //   12 bit program counter 192 gates
  //   Half Adder
  //   PC Latch
  //   MUX
  //   ADDR Latch
endmodule
