// Digital circuit 8_bit_UD_counter.dig as structural Verilog
module _8_bit_UD_counter (
  input  D,
  input  U,
  input  D7,
  input  D6,
  input  D5,
  input  D4,
  input  D3,
  input  D2,
  input  D1,
  input  D0,
  input  nLD,
  input  CLR,
  output Q7,
  output Q6,
  output Q5,
  output Q4,
  output Q3,
  output Q2,
  output Q1,
  output Q0,
  output B,
  output C
);

  wire _74193_1_pin12, _74193_1_pin13;

  _74193 _74193_1 (
    .pin1(D1), .pin2(Q1), .pin3(Q0), .pin4(D), .pin5(U), .pin6(Q2), .pin7(Q3), .pin8(1'b0), .pin9(D3),
    .pin10(D2), .pin11(nLD), .pin12(_74193_1_pin12), .pin13(_74193_1_pin13), .pin14(CLR), .pin15(D0),
    .pin16(1'b1));
  _74193 _74193_2 (
    .pin1(D5), .pin2(Q5), .pin3(Q4), .pin4(_74193_1_pin13), .pin5(_74193_1_pin12), .pin6(Q6), .pin7(Q7),
    .pin8(1'b0), .pin9(D7), .pin10(D6), .pin11(nLD), .pin12(C), .pin13(B), .pin14(CLR), .pin15(D4),
    .pin16(1'b1));

  // Notes on the sheet:
  //   8-bit Binary Up/Down Counter
endmodule
