// Digital circuit 8_bit_adder.dig as structural Verilog
module _8_bit_adder (
  input  in_1,
  input  in_2,
  input  in_3,
  input  in_4,
  input  in_5,
  input  in_6,
  input  in_7,
  input  in_8,
  input  in_9,
  input  in_10,
  input  nINC,
  input  nDEC
);

  wire _74283_1_pin9, _74540_1_pin19, A0, A1, A2, A3, A4, A5, A6, A7, B0, B1, B2, B3, B4, B5, B6, B7,
       diodebackward_1_out, diodebackward_5_out, diodebackward_6_out, diodebackward_9_out, nLD, pullup_2_out,
       pullup_3_out, pullup_6_out, pullup_7_out, S0, S1, S2, S3, S4, S5, S6, S7;

  DiodeBackward diodebackward_1 (.in(nINC), .out(diodebackward_1_out));
  DiodeBackward diodebackward_2 (.in(nDEC), .out(diodebackward_1_out));
  PullUp pullup_1 (.out(diodebackward_1_out));
  PullUp pullup_2 (.out(pullup_2_out));
  DiodeBackward diodebackward_3 (.in(nDEC), .out(pullup_2_out));
  PullUp pullup_3 (.out(pullup_3_out));
  DiodeBackward diodebackward_4 (.in(nDEC), .out(pullup_3_out));
  DiodeBackward diodebackward_5 (.in(nDEC), .out(diodebackward_5_out));
  PullUp pullup_4 (.out(diodebackward_5_out));
  DiodeBackward diodebackward_6 (.in(nDEC), .out(diodebackward_6_out));
  PullUp pullup_5 (.out(diodebackward_6_out));
  PullUp pullup_6 (.out(pullup_6_out));
  DiodeBackward diodebackward_7 (.in(nDEC), .out(pullup_6_out));
  PullUp pullup_7 (.out(pullup_7_out));
  DiodeBackward diodebackward_8 (.in(nDEC), .out(pullup_7_out));
  DiodeBackward diodebackward_9 (.in(nDEC), .out(diodebackward_9_out));
  PullUp pullup_8 (.out(diodebackward_9_out));
  nand nand_1 (nLD, nINC, nDEC);
  _74540 _74540_1 (
    .pin1(1'b0), .pin2(diodebackward_9_out), .pin3(pullup_7_out), .pin4(pullup_6_out),
    .pin5(diodebackward_6_out), .pin6(diodebackward_5_out), .pin7(pullup_3_out), .pin8(pullup_2_out),
    .pin9(diodebackward_1_out), .pin10(1'b0), .pin11(B0), .pin12(B1), .pin13(B2), .pin14(B3), .pin15(B4),
    .pin16(B5), .pin17(B6), .pin18(B7), .pin19(_74540_1_pin19), .pin20(1'b1));
  _74541 _74541_1 (
    .pin1(nLD), .pin2(in_1), .pin3(in_2), .pin4(in_3), .pin5(in_4), .pin6(in_5), .pin7(in_6), .pin8(in_7),
    .pin9(in_8), .pin10(1'b0), .pin11(B0), .pin12(B1), .pin13(B2), .pin14(B3), .pin15(B4), .pin16(B5),
    .pin17(B6), .pin18(B7), .pin19(1'b0), .pin20(1'b1));
  not not_1 (_74540_1_pin19, nLD);
  _74283 _74283_1 (
    .pin1(S1), .pin2(B1), .pin3(A1), .pin4(S0), .pin5(A0), .pin6(B0), .pin7(1'b0), .pin8(1'b0),
    .pin9(_74283_1_pin9), .pin10(S3), .pin11(B3), .pin12(A3), .pin13(S2), .pin14(A2), .pin15(B2), .pin16(1'b1));
  _74283 _74283_2 (
    .pin1(S5), .pin2(B5), .pin3(A5), .pin4(S4), .pin5(A4), .pin6(B4), .pin7(_74283_1_pin9), .pin8(1'b0),
    .pin10(S7), .pin11(A7), .pin12(B7), .pin13(S6), .pin14(A6), .pin15(B6), .pin16(1'b1));  // open: pin9
  _74173 _74173_1 (
    .pin1(1'b0), .pin2(1'b0), .pin3(A0), .pin4(A1), .pin5(A2), .pin6(A3), .pin7(in_10), .pin8(1'b0),
    .pin9(1'b0), .pin10(1'b0), .pin11(S3), .pin12(S2), .pin13(S1), .pin14(S0), .pin15(in_9), .pin16(1'b1));
  _74173 _74173_2 (
    .pin1(1'b0), .pin2(1'b0), .pin3(A4), .pin4(A5), .pin5(A6), .pin6(A7), .pin7(in_10), .pin8(1'b0),
    .pin9(1'b0), .pin10(1'b0), .pin11(S7), .pin12(S6), .pin13(S5), .pin14(S4), .pin15(in_9), .pin16(1'b1));
  Seven_Seg_Hex seven_seg_hex_1 (.d({A7, A6, A5, A4}), .dp(1'b0));
  Seven_Seg_Hex seven_seg_hex_2 (.d({A3, A2, A1, A0}), .dp(1'b0));

  // Other names for the same wires on the sheet: CLK = in_10; RES = in_9

  // Notes on the sheet:
  //   Constant Input
  //   8-bit adder
  //   Register
  //   OUTPUT
endmodule
