// Digital circuit 8_bit_register.dig as structural Verilog
module _8_bit_register (
  input  CK,
  input  in_10,
  input  in_11,
  input  in_12,
  input  in_13,
  input  in_14,
  input  in_15,
  input  in_16,
  input  in_17,
  input  in_18,
  input  in_19,
  output A8,
  output A9,
  output A10,
  output A11,
  output A12,
  output A13,
  output A14,
  output A15
);

  wire nand_1_out, nand_2_out, nand_3_out, nand_4_out, nand_5_out, nand_6_out, nand_7_out, nand_8_out,
       nand_9_out, nand_10_out, nand_11_out, nand_12_out, nand_13_out, nand_14_out, nand_15_out, nand_16_out,
       nand_17_out, nand_18_out, nand_19_out, nand_20_out, nand_21_out, nand_22_out, nand_23_out,
       nand_24_out, nand_25_out, nand_26_out, nand_27_out, nand_28_out, nand_29_out, nand_30_out,
       nand_31_out, nand_32_out, nand_33_out, nand_34_out, nand_35_out, nand_36_out, nand_37_out,
       nand_38_out, nand_39_out, nand_40_out, nand_41_out, nand_42_out, nand_43_out, nand_44_out,
       nand_45_out, nand_46_out, nand_47_out, nand_48_out, nand_49_out, nand_50_out, nand_51_out,
       nand_52_out, nand_53_out, nand_54_out, nand_55_out, nand_56_out, nand_57_out, nand_58_out,
       nand_59_out, nand_60_out, nand_61_out, nand_62_out, nand_63_out, nand_64_out, nand_65_out,
       nand_66_out, nand_67_out, nand_68_out, nand_69_out, nand_70_out, nand_71_out, nand_72_out,
       nand_73_out, nand_75_out, nand_77_out, nand_79_out, nand_81_out, nand_83_out, nand_85_out,
       nand_87_out, nand_89_out;

  nand nand_1 (nand_1_out, A15, in_19);
  nand nand_2 (nand_2_out, in_17, in_18);
  nand nand_3 (nand_3_out, A14, in_19);
  nand nand_4 (nand_4_out, in_16, in_18);
  nand nand_5 (nand_5_out, A13, in_19);
  nand nand_6 (nand_6_out, in_15, in_18);
  nand nand_7 (nand_7_out, A12, in_19);
  nand nand_8 (nand_8_out, in_14, in_18);
  nand nand_9 (nand_9_out, A11, in_19);
  nand nand_10 (nand_10_out, in_13, in_18);
  nand nand_11 (nand_11_out, A10, in_19);
  nand nand_12 (nand_12_out, in_12, in_18);
  nand nand_13 (nand_13_out, A9, in_19);
  nand nand_14 (nand_14_out, in_11, in_18);
  nand nand_15 (nand_15_out, A8, in_19);
  nand nand_16 (nand_16_out, in_10, in_18);
  nand nand_17 (nand_17_out, nand_1_out, nand_2_out);
  nand nand_18 (nand_18_out, nand_3_out, nand_4_out);
  nand nand_19 (nand_19_out, nand_5_out, nand_6_out);
  nand nand_20 (nand_20_out, nand_7_out, nand_8_out);
  nand nand_21 (nand_21_out, nand_9_out, nand_10_out);
  nand nand_22 (nand_22_out, nand_11_out, nand_12_out);
  nand nand_23 (nand_23_out, nand_13_out, nand_14_out);
  nand nand_24 (nand_24_out, nand_15_out, nand_16_out);
  nand nand_25 (nand_25_out, CK, CK);
  nand nand_26 (nand_26_out, nand_17_out, nand_25_out);
  nand nand_27 (nand_27_out, nand_26_out, nand_25_out);
  nand nand_28 (nand_28_out, nand_18_out, nand_25_out);
  nand nand_29 (nand_29_out, nand_28_out, nand_25_out);
  nand nand_30 (nand_30_out, nand_19_out, nand_25_out);
  nand nand_31 (nand_31_out, nand_30_out, nand_25_out);
  nand nand_32 (nand_32_out, nand_20_out, nand_25_out);
  nand nand_33 (nand_33_out, nand_32_out, nand_25_out);
  nand nand_34 (nand_34_out, nand_21_out, nand_25_out);
  nand nand_35 (nand_35_out, nand_34_out, nand_25_out);
  nand nand_36 (nand_36_out, nand_22_out, nand_25_out);
  nand nand_37 (nand_37_out, nand_36_out, nand_25_out);
  nand nand_38 (nand_38_out, nand_23_out, nand_25_out);
  nand nand_39 (nand_39_out, nand_38_out, nand_25_out);
  nand nand_40 (nand_40_out, nand_24_out, nand_25_out);
  nand nand_41 (nand_41_out, nand_40_out, nand_25_out);
  nand nand_42 (nand_42_out, nand_26_out, nand_43_out);
  nand nand_43 (nand_43_out, nand_42_out, nand_27_out);
  nand nand_44 (nand_44_out, nand_28_out, nand_45_out);
  nand nand_45 (nand_45_out, nand_44_out, nand_29_out);
  nand nand_46 (nand_46_out, nand_30_out, nand_47_out);
  nand nand_47 (nand_47_out, nand_46_out, nand_31_out);
  nand nand_48 (nand_48_out, nand_32_out, nand_49_out);
  nand nand_49 (nand_49_out, nand_48_out, nand_33_out);
  nand nand_50 (nand_50_out, nand_34_out, nand_51_out);
  nand nand_51 (nand_51_out, nand_50_out, nand_35_out);
  nand nand_52 (nand_52_out, nand_36_out, nand_53_out);
  nand nand_53 (nand_53_out, nand_52_out, nand_37_out);
  nand nand_54 (nand_54_out, nand_38_out, nand_55_out);
  nand nand_55 (nand_55_out, nand_54_out, nand_39_out);
  nand nand_56 (nand_56_out, nand_40_out, nand_57_out);
  nand nand_57 (nand_57_out, nand_56_out, nand_41_out);
  nand nand_58 (nand_58_out, nand_42_out, CK);
  nand nand_59 (nand_59_out, nand_58_out, CK);
  nand nand_60 (nand_60_out, nand_44_out, CK);
  nand nand_61 (nand_61_out, nand_60_out, CK);
  nand nand_62 (nand_62_out, nand_46_out, CK);
  nand nand_63 (nand_63_out, nand_62_out, CK);
  nand nand_64 (nand_64_out, nand_48_out, CK);
  nand nand_65 (nand_65_out, nand_64_out, CK);
  nand nand_66 (nand_66_out, nand_50_out, CK);
  nand nand_67 (nand_67_out, nand_66_out, CK);
  nand nand_68 (nand_68_out, nand_52_out, CK);
  nand nand_69 (nand_69_out, nand_68_out, CK);
  nand nand_70 (nand_70_out, nand_54_out, CK);
  nand nand_71 (nand_71_out, nand_70_out, CK);
  nand nand_72 (nand_72_out, nand_56_out, CK);
  nand nand_73 (nand_73_out, nand_72_out, CK);
  nand nand_74 (A15, nand_58_out, nand_75_out);
  nand nand_75 (nand_75_out, A15, nand_59_out);
  nand nand_76 (A14, nand_60_out, nand_77_out);
  nand nand_77 (nand_77_out, A14, nand_61_out);
  nand nand_78 (A13, nand_62_out, nand_79_out);
  nand nand_79 (nand_79_out, A13, nand_63_out);
  nand nand_80 (A12, nand_64_out, nand_81_out);
  nand nand_81 (nand_81_out, A12, nand_65_out);
  nand nand_82 (A11, nand_66_out, nand_83_out);
  nand nand_83 (nand_83_out, A11, nand_67_out);
  nand nand_84 (A10, nand_68_out, nand_85_out);
  nand nand_85 (nand_85_out, A10, nand_69_out);
  nand nand_86 (A9, nand_70_out, nand_87_out);
  nand nand_87 (nand_87_out, A9, nand_71_out);
  nand nand_88 (A8, nand_72_out, nand_89_out);
  nand nand_89 (nand_89_out, A8, nand_73_out);

  // Other names for the same wires on the sheet: HLD = in_19; SET = in_18

  // Notes on the sheet:
  //   8-bit Register
endmodule
