// Digital circuit 8_bit_register_1.dig as structural Verilog
module _8_bit_register_1 (
  input  P0,
  input  CLK,
  input  P1,
  input  P2,
  input  P3,
  input  LD,
  input  INC,
  input  in_12,
  input  P4,
  input  P5,
  input  P6,
  input  P7,
  input  INV,
  output A0,
  output A1,
  output A2,
  output A3,
  output A4,
  output A5,
  output A6,
  output A7
);

  wire nand_1_out, nand_2_out, nand_3_out, nand_4_out, nand_5_out, nand_6_out, nand_7_out, nand_8_out,
       nand_9_out, nand_10_out, nand_11_out, nand_12_out, nand_13_out, nand_14_out, nand_15_out, nand_16_out,
       nand_17_out, nand_18_out, nand_19_out, nand_20_out, nand_21_out, nand_22_out, nand_23_out,
       nand_24_out, nand_25_out, nand_26_out, nand_27_out, nand_28_out, nand_29_out, nand_30_out,
       nand_31_out, nand_32_out, nand_33_out, nand_34_out, nand_35_out, nand_36_out, nand_37_out,
       nand_38_out, nand_39_out, nand_40_out, nand_41_out, nand_42_out, nand_43_out, nand_44_out,
       nand_45_out, nand_46_out, nand_47_out, nand_48_out, nand_49_out, nand_50_out, nand_51_out,
       nand_52_out, nand_53_out, nand_54_out, nand_55_out, nand_56_out, nand_57_out, nand_58_out,
       nand_59_out, nand_60_out, nand_61_out, nand_62_out, nand_63_out, nand_64_out, nand_65_out,
       nand_66_out, nand_67_out, nand_68_out, nand_69_out, nand_70_out, nand_71_out, nand_72_out,
       nand_73_out, nand_74_out, nand_75_out, nand_76_out, nand_77_out, nand_78_out, nand_79_out,
       nand_80_out, nand_81_out, nand_82_out, nand_83_out, nand_84_out, nand_85_out, nand_86_out,
       nand_87_out, nand_88_out, nand_89_out, nand_90_out, nand_91_out, nand_92_out, nand_93_out,
       nand_94_out, nand_95_out, nand_96_out, nand_97_out, nand_98_out, nand_99_out, nand_100_out,
       nand_101_out, nand_102_out, nand_103_out, nand_104_out, nand_105_out, nand_106_out, nand_107_out,
       nand_108_out, nand_109_out, nand_110_out, nand_111_out, nand_112_out, nand_113_out, nand_114_out,
       nand_115_out, nand_116_out, nand_117_out, nand_118_out, nand_119_out, nand_120_out, nand_121_out,
       nand_122_out, nand_123_out, nand_124_out, nand_125_out, nand_126_out, nand_127_out, nand_128_out,
       nand_129_out, nand_130_out, nand_131_out, nand_132_out, nand_133_out, nand_134_out, nand_135_out,
       nand_136_out, nand_137_out, nand_138_out, nand_139_out, nand_140_out, nand_141_out, nand_142_out,
       nand_143_out, nand_144_out, nand_145_out, nand_147_out, nand_149_out, nand_151_out, nand_153_out,
       nand_155_out, nand_157_out, nand_159_out, nand_161_out;

  nand nand_1 (nand_1_out, P7, INV);
  nand nand_2 (nand_2_out, P6, INV);
  nand nand_3 (nand_3_out, P5, INV);
  nand nand_4 (nand_4_out, P4, INV);
  nand nand_5 (nand_5_out, P3, INV);
  nand nand_6 (nand_6_out, P2, INV);
  nand nand_7 (nand_7_out, P1, INV);
  nand nand_8 (nand_8_out, P0, INV);
  nand nand_9 (nand_9_out, P7, nand_1_out);
  nand nand_10 (nand_10_out, nand_1_out, INV);
  nand nand_11 (nand_11_out, P6, nand_2_out);
  nand nand_12 (nand_12_out, nand_2_out, INV);
  nand nand_13 (nand_13_out, P5, nand_3_out);
  nand nand_14 (nand_14_out, nand_3_out, INV);
  nand nand_15 (nand_15_out, P4, nand_4_out);
  nand nand_16 (nand_16_out, nand_4_out, INV);
  nand nand_17 (nand_17_out, P3, nand_5_out);
  nand nand_18 (nand_18_out, nand_5_out, INV);
  nand nand_19 (nand_19_out, P2, nand_6_out);
  nand nand_20 (nand_20_out, nand_6_out, INV);
  nand nand_21 (nand_21_out, P1, nand_7_out);
  nand nand_22 (nand_22_out, nand_7_out, INV);
  nand nand_23 (nand_23_out, P0, nand_8_out);
  nand nand_24 (nand_24_out, nand_8_out, INV);
  Seven_Seg_Hex seven_seg_hex_1 (.d({A7, A6, A5, A4}), .dp(1'b0));
  nand nand_25 (nand_25_out, nand_9_out, nand_10_out);
  nand nand_26 (nand_26_out, nand_11_out, nand_12_out);
  nand nand_27 (nand_27_out, nand_13_out, nand_14_out);
  nand nand_28 (nand_28_out, nand_15_out, nand_16_out);
  nand nand_29 (nand_29_out, nand_17_out, nand_18_out);
  nand nand_30 (nand_30_out, nand_19_out, nand_20_out);
  nand nand_31 (nand_31_out, nand_21_out, nand_22_out);
  nand nand_32 (nand_32_out, nand_23_out, nand_24_out);
  Seven_Seg_Hex seven_seg_hex_2 (.d({A3, A2, A1, A0}), .dp(1'b0));
  nand nand_33 (nand_33_out, A7, nand_45_out);
  nand nand_34 (nand_34_out, A6, nand_48_out);
  nand nand_35 (nand_35_out, A5, nand_51_out);
  nand nand_36 (nand_36_out, A4, nand_54_out);
  nand nand_37 (nand_37_out, A3, nand_57_out);
  nand nand_38 (nand_38_out, A2, nand_60_out);
  nand nand_39 (nand_39_out, A1, nand_63_out);
  nand nand_40 (nand_40_out, A0, in_12);
  nand nand_41 (nand_41_out, A7, nand_33_out);
  nand nand_42 (nand_42_out, nand_33_out, nand_33_out);
  nand nand_43 (nand_43_out, nand_33_out, nand_45_out);
  nand nand_44 (nand_44_out, A6, nand_34_out);
  nand nand_45 (nand_45_out, nand_34_out, nand_34_out);
  nand nand_46 (nand_46_out, nand_34_out, nand_48_out);
  nand nand_47 (nand_47_out, A5, nand_35_out);
  nand nand_48 (nand_48_out, nand_35_out, nand_35_out);
  nand nand_49 (nand_49_out, nand_35_out, nand_51_out);
  nand nand_50 (nand_50_out, A4, nand_36_out);
  nand nand_51 (nand_51_out, nand_36_out, nand_36_out);
  nand nand_52 (nand_52_out, nand_36_out, nand_54_out);
  nand nand_53 (nand_53_out, A3, nand_37_out);
  nand nand_54 (nand_54_out, nand_37_out, nand_37_out);
  nand nand_55 (nand_55_out, nand_37_out, nand_57_out);
  nand nand_56 (nand_56_out, A2, nand_38_out);
  nand nand_57 (nand_57_out, nand_38_out, nand_38_out);
  nand nand_58 (nand_58_out, nand_38_out, nand_60_out);
  nand nand_59 (nand_59_out, A1, nand_39_out);
  nand nand_60 (nand_60_out, nand_39_out, nand_39_out);
  nand nand_61 (nand_61_out, nand_39_out, nand_63_out);
  nand nand_62 (nand_62_out, A0, nand_40_out);
  nand nand_63 (nand_63_out, nand_40_out, nand_40_out);
  nand nand_64 (nand_64_out, nand_40_out, in_12);
  nand nand_65 (nand_65_out, nand_41_out, nand_43_out);
  nand nand_66 (nand_66_out, nand_44_out, nand_46_out);
  nand nand_67 (nand_67_out, nand_47_out, nand_49_out);
  nand nand_68 (nand_68_out, nand_50_out, nand_52_out);
  nand nand_69 (nand_69_out, nand_53_out, nand_55_out);
  nand nand_70 (nand_70_out, nand_56_out, nand_58_out);
  nand nand_71 (nand_71_out, nand_59_out, nand_61_out);
  nand nand_72 (nand_72_out, nand_62_out, nand_64_out);
  nand nand_73 (nand_73_out, nand_25_out, LD);
  nand nand_74 (nand_74_out, nand_65_out, INC);
  nand nand_75 (nand_75_out, nand_26_out, LD);
  nand nand_76 (nand_76_out, nand_66_out, INC);
  nand nand_77 (nand_77_out, nand_27_out, LD);
  nand nand_78 (nand_78_out, nand_67_out, INC);
  nand nand_79 (nand_79_out, nand_28_out, LD);
  nand nand_80 (nand_80_out, nand_68_out, INC);
  nand nand_81 (nand_81_out, nand_29_out, LD);
  nand nand_82 (nand_82_out, nand_69_out, INC);
  nand nand_83 (nand_83_out, nand_30_out, LD);
  nand nand_84 (nand_84_out, nand_70_out, INC);
  nand nand_85 (nand_85_out, nand_31_out, LD);
  nand nand_86 (nand_86_out, nand_71_out, INC);
  nand nand_87 (nand_87_out, nand_32_out, LD);
  nand nand_88 (nand_88_out, nand_72_out, INC);
  nand nand_89 (nand_89_out, nand_73_out, nand_74_out);
  nand nand_90 (nand_90_out, nand_75_out, nand_76_out);
  nand nand_91 (nand_91_out, nand_77_out, nand_78_out);
  nand nand_92 (nand_92_out, nand_79_out, nand_80_out);
  nand nand_93 (nand_93_out, nand_81_out, nand_82_out);
  nand nand_94 (nand_94_out, nand_83_out, nand_84_out);
  nand nand_95 (nand_95_out, nand_85_out, nand_86_out);
  nand nand_96 (nand_96_out, nand_87_out, nand_88_out);
  nand nand_97 (nand_97_out, CLK, CLK);
  nand nand_98 (nand_98_out, nand_89_out, nand_97_out);
  nand nand_99 (nand_99_out, nand_98_out, nand_97_out);
  nand nand_100 (nand_100_out, nand_90_out, nand_97_out);
  nand nand_101 (nand_101_out, nand_100_out, nand_97_out);
  nand nand_102 (nand_102_out, nand_91_out, nand_97_out);
  nand nand_103 (nand_103_out, nand_102_out, nand_97_out);
  nand nand_104 (nand_104_out, nand_92_out, nand_97_out);
  nand nand_105 (nand_105_out, nand_104_out, nand_97_out);
  nand nand_106 (nand_106_out, nand_93_out, nand_97_out);
  nand nand_107 (nand_107_out, nand_106_out, nand_97_out);
  nand nand_108 (nand_108_out, nand_94_out, nand_97_out);
  nand nand_109 (nand_109_out, nand_108_out, nand_97_out);
  nand nand_110 (nand_110_out, nand_95_out, nand_97_out);
  nand nand_111 (nand_111_out, nand_110_out, nand_97_out);
  nand nand_112 (nand_112_out, nand_96_out, nand_97_out);
  nand nand_113 (nand_113_out, nand_112_out, nand_97_out);
  nand nand_114 (nand_114_out, nand_98_out, nand_115_out);
  nand nand_115 (nand_115_out, nand_114_out, nand_99_out);
  nand nand_116 (nand_116_out, nand_100_out, nand_117_out);
  nand nand_117 (nand_117_out, nand_116_out, nand_101_out);
  nand nand_118 (nand_118_out, nand_102_out, nand_119_out);
  nand nand_119 (nand_119_out, nand_118_out, nand_103_out);
  nand nand_120 (nand_120_out, nand_104_out, nand_121_out);
  nand nand_121 (nand_121_out, nand_120_out, nand_105_out);
  nand nand_122 (nand_122_out, nand_106_out, nand_123_out);
  nand nand_123 (nand_123_out, nand_122_out, nand_107_out);
  nand nand_124 (nand_124_out, nand_108_out, nand_125_out);
  nand nand_125 (nand_125_out, nand_124_out, nand_109_out);
  nand nand_126 (nand_126_out, nand_110_out, nand_127_out);
  nand nand_127 (nand_127_out, nand_126_out, nand_111_out);
  nand nand_128 (nand_128_out, nand_112_out, nand_129_out);
  nand nand_129 (nand_129_out, nand_128_out, nand_113_out);
  nand nand_130 (nand_130_out, nand_114_out, CLK);
  nand nand_131 (nand_131_out, nand_130_out, CLK);
  nand nand_132 (nand_132_out, nand_116_out, CLK);
  nand nand_133 (nand_133_out, nand_132_out, CLK);
  nand nand_134 (nand_134_out, nand_118_out, CLK);
  nand nand_135 (nand_135_out, nand_134_out, CLK);
  nand nand_136 (nand_136_out, nand_120_out, CLK);
  nand nand_137 (nand_137_out, nand_136_out, CLK);
  nand nand_138 (nand_138_out, nand_122_out, CLK);
  nand nand_139 (nand_139_out, nand_138_out, CLK);
  nand nand_140 (nand_140_out, nand_124_out, CLK);
  nand nand_141 (nand_141_out, nand_140_out, CLK);
  nand nand_142 (nand_142_out, nand_126_out, CLK);
  nand nand_143 (nand_143_out, nand_142_out, CLK);
  nand nand_144 (nand_144_out, nand_128_out, CLK);
  nand nand_145 (nand_145_out, nand_144_out, CLK);
  nand nand_146 (A7, nand_130_out, nand_147_out);
  nand nand_147 (nand_147_out, A7, nand_131_out);
  nand nand_148 (A6, nand_132_out, nand_149_out);
  nand nand_149 (nand_149_out, A6, nand_133_out);
  nand nand_150 (A5, nand_134_out, nand_151_out);
  nand nand_151 (nand_151_out, A5, nand_135_out);
  nand nand_152 (A4, nand_136_out, nand_153_out);
  nand nand_153 (nand_153_out, A4, nand_137_out);
  nand nand_154 (A3, nand_138_out, nand_155_out);
  nand nand_155 (nand_155_out, A3, nand_139_out);
  nand nand_156 (A2, nand_140_out, nand_157_out);
  nand nand_157 (nand_157_out, A2, nand_141_out);
  nand nand_158 (A1, nand_142_out, nand_159_out);
  nand nand_159 (nand_159_out, A1, nand_143_out);
  nand nand_160 (A0, nand_144_out, nand_161_out);
  nand nand_161 (nand_161_out, A0, nand_145_out);

  // Notes on the sheet:
  //   CLK: Hz: 2147483647
  //   ADDRESS
  //   8-bit presettable counter
  //   16 Gates per bit (4 x 74xx00)
  //   Master Slave arrangement using gated D-type latches
endmodule
