// Digital circuit 8_bit_sequencer.dig as structural Verilog
module _8_bit_sequencer (
  input  clk,
  output GCLK,
  output nLD,
  output T0,
  output T9,
  output CLK_2
);

  wire GATE, LD, MR, n2SD, nand_4_out, nGATE, nR, nRES, nSET, SETC, T2, T3, T4, T5, T6, T7, T8;

  Reset reset_1 (.out(n2SD));
  not not_1 (nR, MR);
  not not_2 (nSET, T2);
  not not_3 (nRES, SETC);
  not not_4 (nLD, LD);
  not not_5 (T0, LD);
  not not_6 (T9, MR);
  _744017 U16 (
    .pin1(T5), .pin2(SETC), .pin3(LD), .pin4(T2), .pin5(T6), .pin6(T7), .pin7(T3), .pin8(1'b0), .pin9(T8),
    .pin10(T4), .pin11(MR), .pin13(1'b0), .pin14(clk), .pin15(1'b0), .pin16(1'b1));  // open: pin12
  nand nand_1 (GATE, nLD, nGATE);
  nand nand_2 (nGATE, GATE, nR);
  nand nand_3 (GCLK, GATE, nand_4_out);
  nand nand_4 (nand_4_out, clk, clk);

  assign CLK_2 = clk;

  // Other names for the same wires on the sheet: nAEN = GATE; T0_t = LD; T1 = SETC; T9_t = MR

  // Notes on the sheet:
  //   Clock Sequencer (3 ICs)
  //   U11
endmodule
