// Digital circuit ALU_1.dig as structural Verilog
module ALU_1 (
  input  Fn,
  input  Cin,
  input  nB,
  input  nA,
  input  I1,
  input  I0,
  input  Ain,
  input  Bin,
  output Fout,
  output Cout
);

  wire nand_1_out, nand_2_out, nand_3_out, nand_4_out, nand_5_out, nand_6_out, xor_1_out, xor_2_out,
       xor_3_out, xor_4_out;

  xor xor_1 (xor_1_out, Ain, nA);
  xor xor_2 (xor_2_out, nB, Bin);
  xor xor_3 (xor_3_out, xor_1_out, xor_2_out);
  xor xor_4 (xor_4_out, xor_3_out, Cin);
  nand nand_1 (nand_1_out, xor_3_out, Cin);
  nand nand_2 (nand_2_out, xor_1_out, xor_2_out);
  nand nand_3 (nand_3_out, nand_1_out, nand_2_out);
  nand nand_4 (nand_4_out, xor_4_out, I0);
  nand nand_5 (nand_5_out, I1, nand_3_out);
  nand nand_6 (nand_6_out, nand_3_out, Fn);
  nand nand_7 (Fout, nand_4_out, nand_5_out);
  nand nand_8 (Cout, nand_6_out, nand_6_out);

  // Other names for the same wires on the sheet: Aout = Ain; Bout = Bin; F = Fn

  // Notes on the sheet:
  //   3 chip (12 gate ) bit serial ALU
  //   Suppress Carry
endmodule
