// Digital circuit ALU_NAND_slice.dig as structural Verilog
module ALU_NAND_slice (
  input  I1,
  input  I0,
  input  CI,
  input  SC,
  input  B,
  input  A,
  input  I2,
  input  I4,
  input  I3,
  input  CI_2,
  input  SC_2,
  input  B_2,
  input  A_2,
  input  I5,
  output F,
  output CO,
  output F_2,
  output CO_2
);

  wire and_1_out, and_2_out, and_3_out, nand_1_out, nand_2_out, nand_3_out, nand_4_out, nand_5_out,
       nand_6_out, nand_7_out, nand_8_out, nand_9_out, nand_10_out, nand_11_out, nand_12_out, nand_13_out,
       nand_14_out, nand_15_out, nand_16_out, nand_17_out, nand_18_out, nand_19_out, nand_21_out, xor_1_out,
       xor_2_out;

  nand nand_1 (nand_1_out, B, I2);
  xor xor_1 (xor_1_out, B_2, I5);
  nand nand_2 (nand_2_out, B, nand_1_out);
  nand nand_3 (nand_3_out, nand_1_out, I2);
  nand nand_4 (nand_4_out, nand_2_out, nand_3_out);
  nand nand_5 (nand_5_out, A, nand_4_out);
  and and_1 (and_1_out, A_2, xor_1_out);
  xor xor_2 (xor_2_out, A_2, xor_1_out);
  nand nand_6 (nand_6_out, A, nand_5_out);
  nand nand_7 (nand_7_out, nand_5_out, nand_5_out);
  nand nand_8 (nand_8_out, nand_5_out, nand_4_out);
  nand nand_9 (nand_9_out, nand_6_out, nand_8_out);
  nand nand_10 (nand_10_out, nand_7_out, I1);
  nand nand_11 (nand_11_out, nand_9_out, I0);
  nand nand_12 (nand_12_out, and_1_out, I1);
  nand nand_13 (nand_13_out, xor_2_out, I0);
  nand nand_14 (nand_14_out, nand_10_out, nand_11_out);
  nand nand_15 (nand_15_out, nand_12_out, nand_13_out);
  nand nand_16 (nand_16_out, nand_14_out, CI);
  xor xor_3 (F_2, nand_15_out, CI_2);
  and and_2 (and_2_out, nand_15_out, CI_2);
  nand nand_17 (nand_17_out, nand_14_out, nand_16_out);
  nand nand_18 (nand_18_out, nand_16_out, CI);
  nand nand_19 (nand_19_out, nand_16_out, nand_5_out);
  nand nand_20 (F, nand_17_out, nand_18_out);
  nand nand_21 (nand_21_out, nand_19_out, SC);
  and and_3 (and_3_out, and_2_out, and_1_out);
  nand nand_22 (CO, nand_21_out, nand_21_out);
  and and_4 (CO_2, and_3_out, SC);

  assign I3 = I0;
  assign I4 = I1;
  assign SC_2 = SC;

  // Other names for the same wires on the sheet: AL = SC
endmodule
