// Digital circuit ALU_bitslice.dig as structural Verilog
module ALU_bitslice (
  input  I1,
  input  I0,
  input  I2_NEG,
  input  Cin,
  input  I3_SC,
  input  A0,
  input  B0,
  output Cout,
  output Fout
);

  wire nand_1_out, nand_2_out, nand_3_out, nand_4_out, nand_5_out, nand_6_out, nand_7_out, nand_8_out,
       nand_9_out, nand_10_out, nand_11_out, nand_12_out, nand_13_out, nand_14_out, nand_15_out, nand_16_out,
       nand_18_out;

  nand nand_1 (nand_1_out, B0, I2_NEG);
  nand nand_2 (nand_2_out, B0, nand_1_out);
  nand nand_3 (nand_3_out, nand_1_out, I2_NEG);
  nand nand_4 (nand_4_out, nand_2_out, nand_3_out);
  nand nand_5 (nand_5_out, A0, nand_4_out);
  nand nand_6 (nand_6_out, A0, nand_5_out);
  nand nand_7 (nand_7_out, nand_5_out, nand_5_out);
  nand nand_8 (nand_8_out, nand_5_out, nand_4_out);
  nand nand_9 (nand_9_out, nand_6_out, nand_8_out);
  nand nand_10 (nand_10_out, nand_7_out, I1);
  nand nand_11 (nand_11_out, nand_9_out, I0);
  nand nand_12 (nand_12_out, nand_10_out, nand_11_out);
  nand nand_13 (nand_13_out, nand_12_out, Cin);
  nand nand_14 (nand_14_out, nand_12_out, nand_13_out);
  nand nand_15 (nand_15_out, nand_13_out, Cin);
  nand nand_16 (nand_16_out, nand_13_out, nand_5_out);
  nand nand_17 (Fout, nand_14_out, nand_15_out);
  nand nand_18 (nand_18_out, nand_16_out, I3_SC);
  nand nand_19 (Cout, nand_18_out, nand_18_out);

  // Other names for the same wires on the sheet: AL = I3_SC

  // Notes on the sheet:
  //   ALU bitslice with ADD, SUB, AND, OR, XOR
endmodule
