// Digital circuit ALU_slice_2.dig as structural Verilog
module ALU_slice_2 (
  input  I1,
  input  I0,
  input  Cin,
  input  I3,
  input  B,
  input  A,
  input  I2,
  output Fout,
  output Cout
);

  wire and_1_out, nand_1_out, nand_2_out, nand_3_out, nand_4_out, nand_5_out, nand_6_out, xor_1_out,
       xor_2_out;

  xor xor_1 (xor_1_out, B, I2);
  and and_1 (and_1_out, A, xor_1_out);
  xor xor_2 (xor_2_out, A, xor_1_out);
  nand nand_1 (nand_1_out, A, xor_1_out);
  nand nand_2 (nand_2_out, and_1_out, I1);
  nand nand_3 (nand_3_out, xor_2_out, I0);
  nand nand_4 (nand_4_out, nand_2_out, nand_3_out);
  xor xor_3 (Fout, nand_4_out, Cin);
  nand nand_5 (nand_5_out, nand_4_out, Cin);
  nand nand_6 (nand_6_out, nand_5_out, nand_1_out);
  and and_2 (Cout, nand_6_out, I3);

  // Other names for the same wires on the sheet: AL = I3

  // Notes on the sheet:
  //   ADD
  //   INV
  //   AND
  //   XOR
  //   Invert B
  //   Half Adder 1
  //   1st Carry
  //   ALU Bitslice
  //   MUX
  //   Half Adder 2
  //   2nd Carry
  //   "OR" Carries
  //   Suppress Carry
endmodule
