// Digital circuit AND_OR_BS_ALU.dig as structural Verilog
module AND_OR_BS_ALU (
  input  A,
  input  nA,
  input  nB,
  input  B,
  input  Cin,
  input  F,
  input  SETC,
  input  C,
  input  I1,
  input  I0,
  input  CLA,
  input  LD,
  output Cout,
  output CLC,
  output CtoFF,
  output Fout,
  output CLR
);

  wire and_1_out, and_2_out, and_3_out, and_4_out, and_5_out, and_6_out, and_7_out, and_8_out, and_9_out,
       and_10_out, and_11_out, and_12_out, and_13_out, and_14_out, and_15_out, and_16_out, and_17_out,
       and_18_out, and_19_out, and_20_out, and_21_out, and_22_out, and_23_out, and_24_out, and_25_out,
       and_26_out, and_27_out, and_28_out, and_29_out, and_30_out, and_31_out, and_32_out, and_33_out,
       and_34_out, and_35_out, and_36_out, and_37_out, and_38_out, and_39_out, and_40_out, and_41_out,
       and_42_out, and_43_out, and_44_out, and_45_out, and_46_out, and_47_out, and_48_out, and_49_out,
       and_50_out, and_51_out, and_52_out, and_53_out, and_54_out, and_55_out, and_56_out, and_57_out,
       and_58_out, and_59_out, and_60_out, and_61_out, and_62_out, and_63_out, and_64_out, and_65_out,
       and_66_out, and_67_out, and_68_out, and_69_out, and_70_out, and_71_out, and_72_out, and_73_out,
       and_74_out, and_75_out, and_76_out, and_77_out, and_78_out, and_79_out, and_80_out, and_81_out,
       and_82_out, and_83_out, and_84_out, and_85_out, and_86_out, and_87_out, and_88_out, and_89_out,
       and_90_out, and_91_out, and_92_out, and_93_out, and_94_out, and_95_out, and_96_out, and_97_out,
       and_98_out, and_99_out, and_100_out, and_101_out, and_102_out, and_103_out, and_104_out, and_105_out,
       and_106_out, and_107_out, and_108_out, and_109_out, and_110_out, and_111_out, and_112_out,
       and_113_out, and_114_out, and_115_out, and_116_out, and_117_out, and_118_out, and_119_out,
       and_120_out, and_121_out, and_122_out, and_123_out, and_124_out, and_125_out, and_126_out,
       and_127_out, and_128_out, and_129_out, and_130_out, and_131_out, and_132_out, and_133_out,
       and_134_out, and_135_out, and_136_out, not_1_out, not_2_out, not_3_out, not_4_out, not_5_out,
       not_6_out, not_7_out, not_8_out, not_9_out, or_1_out, or_2_out, or_3_out, or_5_out, or_6_out,
       or_7_out, or_10_out, or_11_out, or_12_out, or_13_out, or_14_out, or_15_out, or_16_out, or_17_out,
       or_18_out, or_19_out, or_20_out, or_22_out, or_23_out, or_24_out, or_25_out, or_26_out, or_27_out,
       or_28_out, or_29_out, or_30_out, or_31_out, or_32_out;

  and and_1 (and_1_out, not_9_out, B);
  not not_1 (not_1_out, LD);
  not not_2 (not_2_out, CLA);
  not not_3 (not_3_out, C);
  not not_4 (not_4_out, SETC);
  not not_5 (not_5_out, Cin);
  not not_6 (not_6_out, B);
  not not_7 (not_7_out, nB);
  not not_8 (not_8_out, nA);
  not not_9 (not_9_out, A);
  and and_2 (and_2_out, and_3_out, and_4_out);
  and and_3 (and_3_out, and_1_out, F);
  and and_4 (and_4_out, nA, not_7_out);
  or or_1 (or_1_out, and_2_out, and_7_out);
  and and_5 (and_5_out, and_6_out, F);
  and and_6 (and_6_out, not_9_out, not_6_out);
  and and_7 (and_7_out, and_5_out, and_8_out);
  and and_8 (and_8_out, nA, nB);
  or or_2 (or_2_out, or_1_out, or_3_out);
  and and_9 (and_9_out, A, B);
  and and_10 (and_10_out, and_11_out, and_12_out);
  and and_11 (and_11_out, and_9_out, F);
  and and_12 (and_12_out, not_8_out, not_7_out);
  or or_3 (or_3_out, and_10_out, and_15_out);
  and and_13 (and_13_out, and_14_out, F);
  and and_14 (and_14_out, A, not_6_out);
  and and_15 (and_15_out, and_13_out, and_16_out);
  and and_16 (and_16_out, not_8_out, nB);
  or or_4 (Cout, or_2_out, or_6_out);
  and and_17 (and_17_out, not_9_out, Cin);
  and and_18 (and_18_out, and_17_out, and_19_out);
  and and_19 (and_19_out, F, nA);
  or or_5 (or_5_out, and_18_out, and_21_out);
  and and_20 (and_20_out, A, Cin);
  and and_21 (and_21_out, and_20_out, and_22_out);
  and and_22 (and_22_out, F, not_8_out);
  or or_6 (or_6_out, or_5_out, or_7_out);
  and and_23 (and_23_out, B, Cin);
  and and_24 (and_24_out, and_23_out, and_25_out);
  and and_25 (and_25_out, F, not_7_out);
  or or_7 (or_7_out, and_24_out, and_27_out);
  and and_26 (and_26_out, not_6_out, Cin);
  and and_27 (and_27_out, and_26_out, and_28_out);
  and and_28 (and_28_out, F, nB);
  or or_8 (CLC, C, not_1_out);
  or or_9 (CtoFF, not_3_out, not_4_out);
  and and_29 (and_29_out, not_9_out, not_6_out);
  and and_30 (and_30_out, and_29_out, Cin);
  and and_31 (and_31_out, and_30_out, and_32_out);
  and and_32 (and_32_out, and_33_out, not_7_out);
  and and_33 (and_33_out, I0, not_8_out);
  or or_10 (or_10_out, and_31_out, and_36_out);
  and and_34 (and_34_out, not_9_out, B);
  and and_35 (and_35_out, and_34_out, not_5_out);
  or or_11 (or_11_out, or_10_out, and_41_out);
  and and_36 (and_36_out, and_35_out, and_37_out);
  and and_37 (and_37_out, and_38_out, not_7_out);
  and and_38 (and_38_out, I0, not_8_out);
  and and_39 (and_39_out, not_9_out, not_6_out);
  and and_40 (and_40_out, and_39_out, not_5_out);
  and and_41 (and_41_out, and_40_out, and_42_out);
  and and_42 (and_42_out, and_43_out, nB);
  and and_43 (and_43_out, I0, not_8_out);
  and and_44 (and_44_out, not_9_out, B);
  or or_12 (or_12_out, or_11_out, or_14_out);
  and and_45 (and_45_out, and_44_out, Cin);
  and and_46 (and_46_out, and_45_out, and_47_out);
  and and_47 (and_47_out, and_48_out, nB);
  and and_48 (and_48_out, I0, not_8_out);
  or or_13 (or_13_out, and_46_out, and_51_out);
  and and_49 (and_49_out, not_9_out, not_6_out);
  and and_50 (and_50_out, and_49_out, not_5_out);
  or or_14 (or_14_out, or_13_out, and_56_out);
  and and_51 (and_51_out, and_50_out, and_52_out);
  and and_52 (and_52_out, and_53_out, not_7_out);
  and and_53 (and_53_out, I0, nA);
  and and_54 (and_54_out, not_9_out, B);
  and and_55 (and_55_out, and_54_out, Cin);
  and and_56 (and_56_out, and_55_out, and_57_out);
  and and_57 (and_57_out, and_58_out, not_7_out);
  and and_58 (and_58_out, I0, nA);
  and and_59 (and_59_out, not_9_out, not_6_out);
  or or_15 (or_15_out, or_12_out, or_18_out);
  and and_60 (and_60_out, and_59_out, Cin);
  and and_61 (and_61_out, and_60_out, and_62_out);
  and and_62 (and_62_out, and_63_out, nB);
  and and_63 (and_63_out, I0, nA);
  or or_16 (or_16_out, and_61_out, and_66_out);
  and and_64 (and_64_out, not_9_out, B);
  and and_65 (and_65_out, and_64_out, not_5_out);
  or or_17 (or_17_out, or_16_out, and_71_out);
  and and_66 (and_66_out, and_65_out, and_67_out);
  and and_67 (and_67_out, and_68_out, nB);
  and and_68 (and_68_out, I0, nA);
  and and_69 (and_69_out, A, not_6_out);
  and and_70 (and_70_out, and_69_out, not_5_out);
  and and_71 (and_71_out, and_70_out, and_72_out);
  and and_72 (and_72_out, and_73_out, not_7_out);
  and and_73 (and_73_out, I0, not_8_out);
  and and_74 (and_74_out, A, B);
  or or_18 (or_18_out, or_17_out, or_20_out);
  and and_75 (and_75_out, and_74_out, Cin);
  and and_76 (and_76_out, and_75_out, and_77_out);
  and and_77 (and_77_out, and_78_out, not_7_out);
  and and_78 (and_78_out, I0, not_8_out);
  or or_19 (or_19_out, and_76_out, and_81_out);
  and and_79 (and_79_out, A, not_6_out);
  and and_80 (and_80_out, and_79_out, Cin);
  or or_20 (or_20_out, or_19_out, and_86_out);
  and and_81 (and_81_out, and_80_out, and_82_out);
  and and_82 (and_82_out, and_83_out, nB);
  and and_83 (and_83_out, I0, not_8_out);
  and and_84 (and_84_out, A, B);
  and and_85 (and_85_out, and_84_out, not_5_out);
  and and_86 (and_86_out, and_85_out, and_87_out);
  and and_87 (and_87_out, and_88_out, nB);
  and and_88 (and_88_out, I0, not_8_out);
  or or_21 (Fout, or_15_out, or_27_out);
  and and_89 (and_89_out, A, not_6_out);
  and and_90 (and_90_out, and_89_out, Cin);
  and and_91 (and_91_out, and_90_out, and_92_out);
  and and_92 (and_92_out, and_93_out, not_7_out);
  and and_93 (and_93_out, I0, nA);
  or or_22 (or_22_out, and_91_out, and_96_out);
  and and_94 (and_94_out, A, B);
  and and_95 (and_95_out, and_94_out, not_5_out);
  or or_23 (or_23_out, or_22_out, and_101_out);
  and and_96 (and_96_out, and_95_out, and_97_out);
  and and_97 (and_97_out, and_98_out, not_7_out);
  and and_98 (and_98_out, I0, nA);
  and and_99 (and_99_out, A, not_6_out);
  and and_100 (and_100_out, and_99_out, not_5_out);
  and and_101 (and_101_out, and_100_out, and_102_out);
  and and_102 (and_102_out, and_103_out, nB);
  and and_103 (and_103_out, I0, nA);
  and and_104 (and_104_out, A, B);
  or or_24 (or_24_out, or_23_out, or_26_out);
  and and_105 (and_105_out, and_104_out, Cin);
  and and_106 (and_106_out, and_105_out, and_107_out);
  and and_107 (and_107_out, and_108_out, nB);
  and and_108 (and_108_out, I0, nA);
  or or_25 (or_25_out, and_106_out, and_110_out);
  and and_109 (and_109_out, not_9_out, B);
  and and_110 (and_110_out, and_111_out, and_112_out);
  and and_111 (and_111_out, and_109_out, I1);
  or or_26 (or_26_out, or_25_out, and_115_out);
  and and_112 (and_112_out, nA, not_7_out);
  and and_113 (and_113_out, and_114_out, I1);
  and and_114 (and_114_out, not_9_out, not_6_out);
  and and_115 (and_115_out, and_113_out, and_116_out);
  and and_116 (and_116_out, nA, nB);
  or or_27 (or_27_out, or_24_out, or_30_out);
  and and_117 (and_117_out, A, B);
  and and_118 (and_118_out, and_119_out, and_120_out);
  and and_119 (and_119_out, and_117_out, I1);
  and and_120 (and_120_out, not_8_out, not_7_out);
  or or_28 (or_28_out, and_118_out, and_123_out);
  and and_121 (and_121_out, and_122_out, I1);
  and and_122 (and_122_out, A, not_6_out);
  or or_29 (or_29_out, or_28_out, and_126_out);
  and and_123 (and_123_out, and_121_out, and_124_out);
  and and_124 (and_124_out, not_8_out, nB);
  and and_125 (and_125_out, not_9_out, Cin);
  and and_126 (and_126_out, and_125_out, and_127_out);
  and and_127 (and_127_out, I1, nA);
  or or_30 (or_30_out, or_29_out, or_32_out);
  and and_128 (and_128_out, A, Cin);
  and and_129 (and_129_out, and_128_out, and_130_out);
  and and_130 (and_130_out, I1, not_8_out);
  or or_31 (or_31_out, and_129_out, and_132_out);
  and and_131 (and_131_out, B, Cin);
  or or_32 (or_32_out, or_31_out, and_135_out);
  and and_132 (and_132_out, and_131_out, and_133_out);
  and and_133 (and_133_out, I1, not_7_out);
  and and_134 (and_134_out, not_6_out, Cin);
  and and_135 (and_135_out, and_134_out, and_136_out);
  and and_136 (and_136_out, I1, nB);
  or or_33 (CLR, not_2_out, not_1_out);
endmodule
