// Digital circuit Address_Latch.dig as structural Verilog
module Address_Latch (
  input  H,
  input  LD,
  input  D,
  input  CK,
  input  in_6,
  input  Hold,
  input  Load,
  input  Data,
  input  CK_2,
  input  H_2,
  input  LD_2,
  input  CK_3,
  input  Din,
  output A8,
  output A8_2,
  output A8_3
);

  wire nand_1_out, nand_2_out, nand_3_out, nand_4_out, nand_5_out, nand_6_out, nand_7_out, nand_8_out,
       nand_9_out, nand_10_out, nand_11_out, nand_12_out, nand_13_out, nand_14_out, nand_15_out, nand_16_out,
       nand_17_out, nand_18_out, nand_19_out, nand_20_out, nand_21_out, nand_22_out, nand_23_out,
       nand_24_out, nand_25_out, nand_26_out, nand_27_out, nand_28_out, nand_29_out, nand_30_out,
       nand_31_out, nand_32_out, nand_33_out, nand_35_out, nand_37_out, nand_39_out;

  nand nand_1 (nand_1_out, A8_3, Din);
  nand nand_2 (nand_2_out, A8, in_6);
  nand nand_3 (nand_3_out, A8_3, nand_1_out);
  nand nand_4 (nand_4_out, nand_1_out, Din);
  nand nand_5 (nand_5_out, A8, nand_2_out);
  nand nand_6 (nand_6_out, nand_2_out, in_6);
  nand nand_7 (nand_7_out, nand_3_out, nand_4_out);
  nand nand_8 (nand_8_out, nand_5_out, nand_6_out);
  nand nand_9 (nand_9_out, CK_3, CK_3);
  nand nand_10 (nand_10_out, CK, CK);
  nand nand_11 (nand_11_out, nand_7_out, nand_9_out);
  nand nand_12 (nand_12_out, nand_11_out, nand_9_out);
  nand nand_13 (nand_13_out, nand_8_out, nand_10_out);
  nand nand_14 (nand_14_out, nand_13_out, nand_10_out);
  nand nand_15 (nand_15_out, nand_11_out, nand_16_out);
  nand nand_16 (nand_16_out, nand_15_out, nand_12_out);
  nand nand_17 (nand_17_out, nand_13_out, nand_18_out);
  nand nand_18 (nand_18_out, nand_17_out, nand_14_out);
  nand nand_19 (nand_19_out, H_2, A8_3);
  nand nand_20 (nand_20_out, LD_2, nand_15_out);
  nand nand_21 (nand_21_out, H, A8);
  nand nand_22 (nand_22_out, LD, D);
  nand nand_23 (nand_23_out, A8_2, Hold);
  nand nand_24 (nand_24_out, Load, Data);
  nand nand_25 (nand_25_out, nand_19_out, nand_20_out);
  nand nand_26 (nand_26_out, nand_21_out, nand_22_out);
  nand nand_27 (nand_27_out, nand_23_out, nand_24_out);
  nand nand_28 (nand_28_out, nand_25_out, CK_3);
  nand nand_29 (nand_29_out, nand_28_out, CK_3);
  nand nand_30 (nand_30_out, nand_26_out, CK);
  nand nand_31 (nand_31_out, nand_30_out, CK);
  nand nand_32 (nand_32_out, nand_27_out, CK_2);
  nand nand_33 (nand_33_out, nand_32_out, CK_2);
  nand nand_34 (A8_3, nand_28_out, nand_35_out);
  nand nand_35 (nand_35_out, A8_3, nand_29_out);
  nand nand_36 (A8, nand_30_out, nand_37_out);
  nand nand_37 (nand_37_out, A8, nand_31_out);
  nand nand_38 (A8_2, nand_32_out, nand_39_out);
  nand nand_39 (nand_39_out, A8_2, nand_33_out);

  // Notes on the sheet:
  //   A8: pin 36
  //   A8_2: pin 36
  //   A8_3: pin 36
  //   PC
  //   Address Latch
  //   ADDR Latch
endmodule
