// Digital circuit Address_Latch_2.dig as structural Verilog
module Address_Latch_2 (
  input  Load_Hold,
  input  D8,
  input  CK,
  input  D9,
  input  D10,
  input  D11,
  input  D12,
  input  D13,
  input  D14,
  input  D15,
  output A8,
  output A9,
  output A10,
  output A11,
  output A12,
  output A13,
  output A14,
  output A15
);

  wire nand_1_out, nand_2_out, nand_3_out, nand_4_out, nand_5_out, nand_6_out, nand_7_out, nand_8_out,
       nand_9_out, nand_10_out, nand_11_out, nand_12_out, nand_13_out, nand_14_out, nand_15_out, nand_16_out,
       nand_17_out, nand_18_out, nand_19_out, nand_20_out, nand_21_out, nand_22_out, nand_23_out,
       nand_24_out, nand_25_out, nand_26_out, nand_27_out, nand_28_out, nand_29_out, nand_30_out,
       nand_31_out, nand_32_out, nand_33_out, nand_34_out, nand_35_out, nand_36_out, nand_37_out,
       nand_38_out, nand_39_out, nand_40_out, nand_41_out, nand_43_out, nand_45_out, nand_47_out,
       nand_49_out, nand_51_out, nand_53_out, nand_55_out, nand_57_out;

  nand nand_1 (nand_1_out, Load_Hold, Load_Hold);
  nand nand_2 (nand_2_out, A15, nand_1_out);
  nand nand_3 (nand_3_out, Load_Hold, D15);
  nand nand_4 (nand_4_out, A14, nand_1_out);
  nand nand_5 (nand_5_out, Load_Hold, D14);
  nand nand_6 (nand_6_out, A13, nand_1_out);
  nand nand_7 (nand_7_out, Load_Hold, D13);
  nand nand_8 (nand_8_out, A12, nand_1_out);
  nand nand_9 (nand_9_out, Load_Hold, D12);
  nand nand_10 (nand_10_out, A11, nand_1_out);
  nand nand_11 (nand_11_out, Load_Hold, D11);
  nand nand_12 (nand_12_out, A10, nand_1_out);
  nand nand_13 (nand_13_out, Load_Hold, D10);
  nand nand_14 (nand_14_out, A9, nand_1_out);
  nand nand_15 (nand_15_out, Load_Hold, D9);
  nand nand_16 (nand_16_out, A8, nand_1_out);
  nand nand_17 (nand_17_out, Load_Hold, D8);
  nand nand_18 (nand_18_out, nand_2_out, nand_3_out);
  nand nand_19 (nand_19_out, nand_4_out, nand_5_out);
  nand nand_20 (nand_20_out, nand_6_out, nand_7_out);
  nand nand_21 (nand_21_out, nand_8_out, nand_9_out);
  nand nand_22 (nand_22_out, nand_10_out, nand_11_out);
  nand nand_23 (nand_23_out, nand_12_out, nand_13_out);
  nand nand_24 (nand_24_out, nand_14_out, nand_15_out);
  nand nand_25 (nand_25_out, nand_16_out, nand_17_out);
  nand nand_26 (nand_26_out, nand_18_out, CK);
  nand nand_27 (nand_27_out, nand_26_out, CK);
  nand nand_28 (nand_28_out, nand_19_out, CK);
  nand nand_29 (nand_29_out, nand_28_out, CK);
  nand nand_30 (nand_30_out, nand_20_out, CK);
  nand nand_31 (nand_31_out, nand_30_out, CK);
  nand nand_32 (nand_32_out, nand_21_out, CK);
  nand nand_33 (nand_33_out, nand_32_out, CK);
  nand nand_34 (nand_34_out, nand_22_out, CK);
  nand nand_35 (nand_35_out, nand_34_out, CK);
  nand nand_36 (nand_36_out, nand_23_out, CK);
  nand nand_37 (nand_37_out, nand_36_out, CK);
  nand nand_38 (nand_38_out, nand_24_out, CK);
  nand nand_39 (nand_39_out, nand_38_out, CK);
  nand nand_40 (nand_40_out, nand_25_out, CK);
  nand nand_41 (nand_41_out, nand_40_out, CK);
  nand nand_42 (A15, nand_26_out, nand_43_out);
  nand nand_43 (nand_43_out, A15, nand_27_out);
  nand nand_44 (A14, nand_28_out, nand_45_out);
  nand nand_45 (nand_45_out, A14, nand_29_out);
  nand nand_46 (A13, nand_30_out, nand_47_out);
  nand nand_47 (nand_47_out, A13, nand_31_out);
  nand nand_48 (A12, nand_32_out, nand_49_out);
  nand nand_49 (nand_49_out, A12, nand_33_out);
  nand nand_50 (A11, nand_34_out, nand_51_out);
  nand nand_51 (nand_51_out, A11, nand_35_out);
  nand nand_52 (A10, nand_36_out, nand_53_out);
  nand nand_53 (nand_53_out, A10, nand_37_out);
  nand nand_54 (A9, nand_38_out, nand_55_out);
  nand nand_55 (nand_55_out, A9, nand_39_out);
  nand nand_56 (A8, nand_40_out, nand_57_out);
  nand nand_57 (nand_57_out, A8, nand_41_out);

  // Notes on the sheet:
  //   Address Latch
endmodule
