// Digital circuit BS_ALU.dig as structural Verilog
module BS_ALU (
  input  Aout,
  input  nA,
  input  nB,
  input  Bout,
  input  Cin,
  input  F,
  input  X0,
  input  X1,
  output Fout,
  output Cout
);

  wire nand_1_out, nand_2_out, nand_3_out, nand_4_out, nand_5_out, nand_6_out, xor_1_out, xor_2_out,
       xor_3_out, xor_4_out;

  xor xor_1 (xor_1_out, Aout, nA);
  xor xor_2 (xor_2_out, nB, Bout);
  xor xor_3 (xor_3_out, xor_1_out, xor_2_out);
  xor xor_4 (xor_4_out, xor_3_out, Cin);
  nand nand_1 (nand_1_out, xor_3_out, Cin);
  nand nand_2 (nand_2_out, xor_1_out, xor_2_out);
  nand nand_3 (nand_3_out, nand_1_out, nand_2_out);
  nand nand_4 (nand_4_out, xor_4_out, X0);
  nand nand_5 (nand_5_out, X1, nand_3_out);
  nand nand_6 (nand_6_out, nand_3_out, F);
  nand nand_7 (Fout, nand_4_out, nand_5_out);
  nand nand_8 (Cout, nand_6_out, nand_6_out);

  // Notes on the sheet:
  //   U24A
  //   U24B
  //   Bit Serial ALU
  //   U24C
  //   U24D
  //   U25D
  //   U25C
  //   U25B
  //   U26B
  //   U26C
  //   U26A
  //   U26D
  //   U25A
endmodule
