// Digital circuit BS_ALU_and Switches.dig as structural Verilog
module BS_ALU_and_Switches (
  input  Aout,
  input  nA,
  input  nB,
  input  Bout,
  input  Cin,
  input  F,
  input  X0,
  input  X1,
  input  in_11,
  output Fout,
  output Cout
);

  wire BUS0, BUS1, BUS2, BUS3, BUS4, BUS5, BUS6, BUS7, BUS8, BUS9, BUS10, BUS11, BUS12, BUS13, BUS14, BUS15,
       button_1_out, button_2_out, button_3_out, button_4_out, button_5_out, button_6_out, button_7_out,
       button_8_out, button_9_out, button_10_out, button_11_out, button_12_out, button_13_out, button_14_out,
       button_15_out, button_16_out, D0, D1, D2, D3, D4, D5, D6, D7, D8, D9, D10, D11, D12, D13, D14, D15,
       d_ff_1_nq, d_ff_2_nq, d_ff_3_nq, d_ff_4_nq, d_ff_5_nq, d_ff_6_nq, d_ff_7_nq, d_ff_8_nq, d_ff_9_nq,
       d_ff_10_nq, d_ff_11_nq, d_ff_12_nq, IC16_2_nq, IC16_nq, IC17_2_nq, IC17_nq, nand_1_out, nand_2_out,
       nand_3_out, nand_4_out, nand_5_out, nand_6_out, xor_1_out, xor_2_out, xor_3_out, xor_4_out;

  LED led_1 (.in(D15));
  LED led_2 (.in(D14));
  D_FF IC17 (.D(IC17_nq), .C(button_1_out), .Q(D15), .nQ(IC17_nq));
  Button button_1 (.out(button_1_out));
  _74541 _74541_1 (
    .pin1(in_11), .pin2(D12), .pin3(D13), .pin4(D14), .pin5(D15), .pin6(D11), .pin7(D10), .pin8(D9),
    .pin9(D8), .pin10(1'b0), .pin11(BUS8), .pin12(BUS9), .pin13(BUS10), .pin14(BUS11), .pin15(BUS12),
    .pin16(BUS13), .pin17(BUS14), .pin18(BUS15), .pin19(in_11), .pin20(1'b1));
  LED led_3 (.in(D13));
  D_FF d_ff_1 (.D(d_ff_1_nq), .C(button_2_out), .Q(D14), .nQ(d_ff_1_nq));
  Button button_2 (.out(button_2_out));
  LED led_4 (.in(D12));
  D_FF d_ff_2 (.D(d_ff_2_nq), .C(button_3_out), .Q(D13), .nQ(d_ff_2_nq));
  Button button_3 (.out(button_3_out));
  LED led_5 (.in(D11));
  D_FF d_ff_3 (.D(d_ff_3_nq), .C(button_4_out), .Q(D12), .nQ(d_ff_3_nq));
  Button button_4 (.out(button_4_out));
  xor xor_1 (xor_1_out, Aout, nA);
  xor xor_2 (xor_2_out, nB, Bout);
  LED led_6 (.in(D10));
  D_FF d_ff_4 (.D(d_ff_4_nq), .C(button_5_out), .Q(D11), .nQ(d_ff_4_nq));
  Button button_5 (.out(button_5_out));
  LED led_7 (.in(D9));
  D_FF d_ff_5 (.D(d_ff_5_nq), .C(button_6_out), .Q(D10), .nQ(d_ff_5_nq));
  Button button_6 (.out(button_6_out));
  xor xor_3 (xor_3_out, xor_1_out, xor_2_out);
  LED led_8 (.in(D8));
  D_FF d_ff_6 (.D(d_ff_6_nq), .C(button_7_out), .Q(D9), .nQ(d_ff_6_nq));
  Button button_7 (.out(button_7_out));
  Seven_Seg_Hex seven_seg_hex_1 (.d({D15, D14, D13, D12}), .dp(1'b0));
  D_FF IC17_2 (.D(IC17_2_nq), .C(button_8_out), .Q(D8), .nQ(IC17_2_nq));
  Button button_8 (.out(button_8_out));
  xor xor_4 (xor_4_out, xor_3_out, Cin);
  nand nand_1 (nand_1_out, xor_3_out, Cin);
  nand nand_2 (nand_2_out, xor_1_out, xor_2_out);
  Seven_Seg_Hex seven_seg_hex_2 (.d({D11, D10, D9, D8}), .dp(1'b0));
  nand nand_3 (nand_3_out, nand_1_out, nand_2_out);
  LED led_9 (.in(D7));
  D_FF IC16 (.D(IC16_nq), .C(button_9_out), .Q(D7), .nQ(IC16_nq));
  Button button_9 (.out(button_9_out));
  LED led_10 (.in(D6));
  D_FF d_ff_7 (.D(d_ff_7_nq), .C(button_10_out), .Q(D6), .nQ(d_ff_7_nq));
  Button button_10 (.out(button_10_out));
  _74541 _74541_2 (
    .pin1(in_11), .pin2(D7), .pin3(D6), .pin4(D5), .pin5(D4), .pin6(D3), .pin7(D2), .pin8(D1), .pin9(D0),
    .pin10(1'b0), .pin11(BUS0), .pin12(BUS1), .pin13(BUS2), .pin14(BUS3), .pin15(BUS4), .pin16(BUS5),
    .pin17(BUS6), .pin18(BUS7), .pin19(in_11), .pin20(1'b1));
  LED led_11 (.in(D5));
  D_FF d_ff_8 (.D(d_ff_8_nq), .C(button_11_out), .Q(D5), .nQ(d_ff_8_nq));
  Button button_11 (.out(button_11_out));
  nand nand_4 (nand_4_out, xor_4_out, X0);
  nand nand_5 (nand_5_out, X1, nand_3_out);
  nand nand_6 (nand_6_out, nand_3_out, F);
  LED led_12 (.in(D4));
  D_FF d_ff_9 (.D(d_ff_9_nq), .C(button_12_out), .Q(D4), .nQ(d_ff_9_nq));
  Button button_12 (.out(button_12_out));
  LED led_13 (.in(D3));
  D_FF d_ff_10 (.D(d_ff_10_nq), .C(button_13_out), .Q(D3), .nQ(d_ff_10_nq));
  Button button_13 (.out(button_13_out));
  nand nand_7 (Fout, nand_4_out, nand_5_out);
  nand nand_8 (Cout, nand_6_out, nand_6_out);
  LED led_14 (.in(D2));
  D_FF d_ff_11 (.D(d_ff_11_nq), .C(button_14_out), .Q(D2), .nQ(d_ff_11_nq));
  Button button_14 (.out(button_14_out));
  LED led_15 (.in(D1));
  D_FF d_ff_12 (.D(d_ff_12_nq), .C(button_15_out), .Q(D1), .nQ(d_ff_12_nq));
  Button button_15 (.out(button_15_out));
  LED led_16 (.in(D0));
  D_FF IC16_2 (.D(IC16_2_nq), .C(button_16_out), .Q(D0), .nQ(IC16_2_nq));
  Button button_16 (.out(button_16_out));
  Seven_Seg_Hex seven_seg_hex_3 (.d({D7, D6, D5, D4}), .dp(1'b0));
  Seven_Seg_Hex seven_seg_hex_4 (.d({D3, D2, D1, D0}), .dp(1'b0));

  // Other names for the same wires on the sheet: nSE = in_11

  // Notes on the sheet:
  //   ENTER H
  //   SW to BUS HI
  //   U24A
  //   U24B
  //   Bit Serial ALU
  //   U24C
  //   Data Input
  //   U24D
  //   U25D
  //   U25C
  //   U25B
  //   U26B
  //   U26C
  //   U26A
  //   ENTER L
  //   U26D
  //   U25A
  //   SW to BUS LO
endmodule
