// Digital circuit Bit_serial_fibonacci_2.dig as structural Verilog
module Bit_serial_fibonacci_2 (
  input  clk,
  input  in_2,
  input  in_3,
  input  in_4,
  input  A,
  input  in_11,
  output LD,
  output RES,
  output GCLK,
  output T0,
  output RST
);

  wire _74153_1_pin7, ADD, AND, Aout, Bout, button_1_out, button_2_out, C, Cin, CLA, CLR, Cout, D0, D1, D2,
       D3, D4, D5, D6, D7, D8, D9, D10, D11, D12, D13, D14, D15, diodebackward_1_out, diodebackward_2_out,
       diodebackward_9_out, F, Fout, I0, I1, IX, LD_t, LOAD, nA, nand_1_out, nand_2_out, nand_4_out,
       nand_5_out, nand_6_out, nand_7_out, nand_8_out, nand_10_out, nand_11_out, nand_12_out, nand_13_out,
       nB, nCLRPC, nJMP, OR, pullup_2_out, pullup_4_out, pullup_5_out, pullup_7_out, RCO, SETC, ST, SUB,
       U3_pin9, U8_pin9, U9_pin9, XOR, xor_1_out, xor_2_out, xor_3_out, xor_4_out;
  wire [3:0] U5_pin3, U5_pin10, U6_pin5, U7_pin11;
  wire [3:1] U6_pin10;

  _74165 U3 (
    .pin1(LD), .pin2(GCLK), .pin3(D11), .pin4(D10), .pin5(D9), .pin6(D8), .pin8(1'b0), .pin9(U3_pin9),
    .pin10(1'b0), .pin11(D15), .pin12(D14), .pin13(D13), .pin14(D12), .pin15(1'b0), .pin16(1'b1));  // open: pin7
  Monoflop monoflop_1 (.C(LD), .R(1'b0), .Q(SETC), .nQ(RES));
  Monoflop monoflop_2 (.C(button_1_out), .R(1'b0), .Q(LD_t), .nQ(LD));
  Button button_1 (.out(button_1_out));
  _74138 U1 (
    .pin1(in_2), .pin2(in_3), .pin3(in_4), .pin4(1'b0), .pin5(1'b0), .pin6(1'b1), .pin7(nJMP), .pin8(1'b0),
    .pin9(ST), .pin10(SUB), .pin11(ADD), .pin12(XOR), .pin13(OR), .pin14(AND), .pin15(LOAD), .pin16(1'b1));
  DiodeBackward diodebackward_1 (.in(LOAD), .out(diodebackward_1_out));
  Monoflop monoflop_3 (.C(button_2_out), .R(1'b0), .nQ(nCLRPC));  // open: Q
  Button button_2 (.out(button_2_out));
  PullUp pullup_1 (.out(diodebackward_1_out));
  DiodeBackward diodebackward_2 (.in(LOAD), .out(diodebackward_2_out));
  DiodeBackward diodebackward_3 (.in(ADD), .out(diodebackward_2_out));
  DiodeBackward diodebackward_4 (.in(SUB), .out(diodebackward_2_out));
  DiodeBackward diodebackward_5 (.in(nJMP), .out(diodebackward_2_out));
  PullUp pullup_2 (.out(pullup_2_out));
  PullUp pullup_3 (.out(diodebackward_2_out));
  DiodeBackward diodebackward_6 (.in(SUB), .out(pullup_2_out));
  DiodeBackward diodebackward_7 (.in(ST), .out(pullup_2_out));
  _74165 U4 (
    .pin1(LD), .pin2(GCLK), .pin3(D3), .pin4(D2), .pin5(D1), .pin6(D0), .pin8(1'b0), .pin9(Bout),
    .pin10(U3_pin9), .pin11(D7), .pin12(D6), .pin13(D5), .pin14(D4), .pin15(1'b0), .pin16(1'b1));  // open: pin7
  PullUp pullup_4 (.out(pullup_4_out));
  DiodeBackward diodebackward_8 (.in(SUB), .out(pullup_4_out));
  PullUp pullup_5 (.out(pullup_5_out));
  DiodeBackward diodebackward_9 (.in(AND), .out(diodebackward_9_out));
  DiodeBackward diodebackward_10 (.in(OR), .out(diodebackward_9_out));
  PullUp pullup_6 (.out(diodebackward_9_out));
  PullUp pullup_7 (.out(pullup_7_out));
  DiodeBackward diodebackward_11 (.in(LOAD), .out(pullup_7_out));
  DiodeBackward diodebackward_12 (.in(OR), .out(pullup_7_out));
  DiodeBackward diodebackward_13 (.in(XOR), .out(pullup_7_out));
  DiodeBackward diodebackward_14 (.in(ADD), .out(pullup_7_out));
  DiodeBackward diodebackward_15 (.in(SUB), .out(pullup_7_out));
  DiodeBackward diodebackward_16 (.in(ST), .out(pullup_7_out));
  _74540 U2 (
    .pin1(1'b0), .pin2(pullup_7_out), .pin3(diodebackward_9_out), .pin4(pullup_5_out), .pin5(pullup_4_out),
    .pin6(pullup_2_out), .pin7(diodebackward_2_out), .pin8(diodebackward_1_out), .pin9(1'b0), .pin10(1'b0),
    .pin12(CLA), .pin13(F), .pin14(C), .pin15(nB), .pin16(nA), .pin17(I1), .pin18(I0), .pin19(1'b0),
    .pin20(1'b1));  // open: pin11
  _74153 _74153_1 (
    .pin1(1'b0), .pin2(in_4), .pin3(1'b0), .pin4(Fout), .pin5(SETC), .pin6(in_11), .pin7(_74153_1_pin7),
    .pin8(1'b0), .pin10(1'b0), .pin11(1'b0), .pin12(1'b0), .pin13(1'b0), .pin14(A), .pin15(1'b1), .pin16(1'b1));  // open: pin9
  _74164 U5 (
    .pin1(1'b1), .pin2(Bout), .pin3(U5_pin3[3]), .pin4(U5_pin3[2]), .pin5(U5_pin3[1]), .pin6(U5_pin3[0]),
    .pin7(1'b0), .pin8(GCLK), .pin9(CLR), .pin10(U5_pin10[3]), .pin11(U5_pin10[2]), .pin12(U5_pin10[1]),
    .pin13(U5_pin10[0]), .pin14(1'b1));
  _74595 U8 (
    .pin1(D14), .pin2(D13), .pin3(D12), .pin4(D11), .pin5(D10), .pin6(D9), .pin7(D8), .pin8(1'b0),
    .pin9(U8_pin9), .pin10(RES), .pin11(GCLK), .pin12(T0), .pin13(1'b0), .pin14(_74153_1_pin7), .pin15(D15),
    .pin16(1'b1));
  Seven_Seg_Hex seven_seg_hex_1 (.d(U5_pin3), .dp(1'b0));
  Seven_Seg_Hex seven_seg_hex_2 (.d(U5_pin10), .dp(1'b0));
  Seven_Seg_Hex seven_seg_hex_3 (.d(U6_pin5), .dp(1'b0));
  Seven_Seg_Hex seven_seg_hex_4 (.d({U6_pin10, Aout}), .dp(1'b0));
  _74595 U9 (
    .pin1(D6), .pin2(D5), .pin3(D4), .pin4(D3), .pin5(D2), .pin6(D1), .pin7(D0), .pin8(1'b0), .pin9(U9_pin9),
    .pin10(RES), .pin11(GCLK), .pin12(T0), .pin13(1'b0), .pin14(U8_pin9), .pin15(D7), .pin16(1'b1));
  _74164 U6 (
    .pin1(1'b1), .pin2(U5_pin10[0]), .pin3(U6_pin5[3]), .pin4(U6_pin5[2]), .pin5(U6_pin5[1]),
    .pin6(U6_pin5[0]), .pin7(1'b0), .pin8(GCLK), .pin9(CLR), .pin10(U6_pin10[3]), .pin11(U6_pin10[2]),
    .pin12(U6_pin10[1]), .pin13(Aout), .pin14(1'b1));
  Seven_Seg_Hex seven_seg_hex_5 (.d({D15, D14, D13, D12}), .dp(1'b0));
  Seven_Seg_Hex seven_seg_hex_6 (.d({D15, D14, D13, D12}), .dp(1'b0));
  Seven_Seg_Hex seven_seg_hex_7 (.d({D11, D10, D9, D8}), .dp(1'b0));
  Seven_Seg_Hex seven_seg_hex_8 (.d({D11, D10, D9, D8}), .dp(1'b0));
  Seven_Seg_Hex seven_seg_hex_9 (.d({D7, D6, D5, D4}), .dp(1'b0));
  Seven_Seg_Hex seven_seg_hex_10 (.d({D7, D6, D5, D4}), .dp(1'b0));
  Seven_Seg_Hex seven_seg_hex_11 (.d({D3, D2, D1, D0}), .dp(1'b0));
  Seven_Seg_Hex seven_seg_hex_12 (.d({D3, D2, D1, D0}), .dp(1'b0));
  xor xor_1 (xor_1_out, Aout, nA);
  xor xor_2 (xor_2_out, nB, Bout);
  nand nand_1 (nand_1_out, SETC, C);
  nand nand_2 (nand_2_out, C, C);
  nand nand_3 (CLR, CLA, LD_t);
  xor xor_3 (xor_3_out, xor_1_out, xor_2_out);
  nand nand_4 (nand_4_out, nand_2_out, LD_t);
  xor xor_4 (xor_4_out, xor_3_out, Cin);
  nand nand_5 (nand_5_out, xor_3_out, Cin);
  nand nand_6 (nand_6_out, xor_1_out, xor_2_out);
  nand nand_7 (nand_7_out, nand_5_out, nand_6_out);
  nand nand_8 (nand_8_out, clk, clk);
  nand nand_9 (RST, RES, nand_10_out);
  nand nand_10 (nand_10_out, RST, T0);
  nand nand_11 (nand_11_out, xor_4_out, I0);
  nand nand_12 (nand_12_out, I1, nand_7_out);
  nand nand_13 (nand_13_out, nand_7_out, F);
  nand nand_14 (GCLK, nand_8_out, RST);
  nand nand_15 (Fout, nand_11_out, nand_12_out);
  nand nand_16 (Cout, nand_13_out, nand_13_out);
  _74161 U7 (
    .pin1(RST), .pin2(clk), .pin3(1'b0), .pin4(1'b0), .pin5(1'b0), .pin6(1'b0), .pin7(1'b1), .pin8(1'b0),
    .pin9(1'b1), .pin10(1'b1), .pin11(U7_pin11[3]), .pin12(U7_pin11[2]), .pin13(U7_pin11[1]),
    .pin14(U7_pin11[0]), .pin15(RCO), .pin16(1'b1));
  _7474 _7474_1 (
    .pin1(nand_4_out), .pin2(Cout), .pin3(GCLK), .pin4(nand_1_out), .pin5(Cin), .pin7(1'b0), .pin8(T0),
    .pin9(IX), .pin10(1'b1), .pin11(clk), .pin12(RCO), .pin13(1'b1), .pin14(1'b1));  // open: pin6
  LED led_1 (.in(Cin));
  Seven_Seg_Hex seven_seg_hex_13 (.d(U7_pin11), .dp(1'b0));

  // Other names for the same wires on the sheet: nCC = in_4; nLOAD = LD; nRES = RES

  // Notes on the sheet:
  //   clk: Hz: 2147483647
  //   Fibonacci 1
  //   Instruction Input
  //   STEP/RUN
  //   16 bit Shift Register B
  //   CLR PC
  //   Instruction Decode
  //   CLA
  //   C
  //   F
  //   ~B
  //   ~A
  //   I0
  //   I1
  //   LOAD
  //   AND
  //   OR
  //   XOR
  //   ADD
  //   SUB
  //   STORE
  //   JMP
  //   Bit serial Fibonacci Generator
  //   16 bit Shift Register A
  //   16 bit Shift Register C
  //   (n-1)
  //   C REGISTER
  //   (n)
  //   ALU
  //   CLR ACC
  //   Carry is only set before Bit 0 of an operation
  //   Any residual carry is cleared before an operation
  //   Clock Sequencer
  //   Suppress Carry
  //   Carry FF
  //   CARRY
  //   # Clock
endmodule
