// Digital circuit Brent_Kung_adder_w_carry_in.dig as structural Verilog
module Brent_Kung_adder_w_carry_in (
  input  [7:0] Din_A,
  input  [7:0] Din_B,
  input  Cin,
  output [7:0] Dout,
  output Cout
);

  wire and_1_out, and_2_out, and_3_out, and_4_out, and_5_out, and_6_out, and_7_out, and_8_out, and_9_out,
       and_10_out, and_11_out, and_12_out, and_13_out, and_14_out, and_15_out, and_16_out, and_17_out,
       and_18_out, and_19_out, and_20_out, and_21_out, and_22_out, and_23_out, and_24_out, or_1_out,
       or_2_out, or_3_out, or_4_out, or_5_out, or_6_out, or_7_out, or_9_out, or_10_out, or_11_out, or_12_out,
       xor_1_out, xor_2_out, xor_3_out, xor_4_out, xor_5_out, xor_6_out, xor_7_out, xor_8_out;

  xor xor_1 (xor_1_out, Din_A[0], Din_B[0]);
  and and_1 (and_1_out, Din_A[0], Din_B[0]);
  xor xor_2 (xor_2_out, Din_A[1], Din_B[1]);
  and and_2 (and_2_out, Din_A[1], Din_B[1]);
  xor xor_3 (xor_3_out, Din_A[2], Din_B[2]);
  and and_3 (and_3_out, Din_A[2], Din_B[2]);
  xor xor_4 (xor_4_out, Din_A[3], Din_B[3]);
  and and_4 (and_4_out, Din_A[3], Din_B[3]);
  xor xor_5 (xor_5_out, Din_A[4], Din_B[4]);
  and and_5 (and_5_out, Din_A[4], Din_B[4]);
  xor xor_6 (xor_6_out, Din_A[5], Din_B[5]);
  and and_6 (and_6_out, Din_A[5], Din_B[5]);
  xor xor_7 (xor_7_out, Din_A[6], Din_B[6]);
  and and_7 (and_7_out, Din_A[6], Din_B[6]);
  xor xor_8 (xor_8_out, Din_A[7], Din_B[7]);
  and and_8 (and_8_out, Din_A[7], Din_B[7]);
  and and_9 (and_9_out, xor_2_out, or_9_out);
  and and_10 (and_10_out, xor_3_out, xor_4_out);
  and and_11 (and_11_out, xor_4_out, and_3_out);
  and and_12 (and_12_out, xor_5_out, xor_6_out);
  and and_13 (and_13_out, xor_6_out, and_5_out);
  and and_14 (and_14_out, xor_7_out, xor_8_out);
  and and_15 (and_15_out, xor_8_out, and_7_out);
  or or_1 (or_1_out, and_9_out, and_2_out);
  or or_2 (or_2_out, and_11_out, and_4_out);
  or or_3 (or_3_out, and_13_out, and_6_out);
  or or_4 (or_4_out, and_15_out, and_8_out);
  and and_16 (and_16_out, or_1_out, and_10_out);
  and and_17 (and_17_out, and_12_out, and_14_out);
  and and_18 (and_18_out, and_14_out, or_3_out);
  or or_5 (or_5_out, and_16_out, or_2_out);
  or or_6 (or_6_out, and_18_out, or_4_out);
  and and_19 (and_19_out, or_5_out, and_12_out);
  and and_20 (and_20_out, or_5_out, and_17_out);
  or or_7 (or_7_out, and_19_out, or_3_out);
  or or_8 (Cout, and_20_out, or_6_out);
  and and_21 (and_21_out, xor_1_out, Cin);
  and and_22 (and_22_out, xor_3_out, or_1_out);
  and and_23 (and_23_out, xor_5_out, or_5_out);
  and and_24 (and_24_out, xor_7_out, or_7_out);
  or or_9 (or_9_out, and_21_out, and_1_out);
  or or_10 (or_10_out, and_22_out, and_3_out);
  or or_11 (or_11_out, and_23_out, and_5_out);
  or or_12 (or_12_out, and_24_out, and_7_out);
  xor xor_9 (Dout[0], Cin, xor_1_out);
  xor xor_10 (Dout[1], or_9_out, xor_2_out);
  xor xor_11 (Dout[2], or_1_out, xor_3_out);
  xor xor_12 (Dout[3], or_10_out, xor_4_out);
  xor xor_13 (Dout[4], or_5_out, xor_5_out);
  xor xor_14 (Dout[5], or_11_out, xor_6_out);
  xor xor_15 (Dout[6], or_7_out, xor_7_out);
  xor xor_16 (Dout[7], or_12_out, xor_8_out);
endmodule
