// Digital circuit DTL_ALU.dig as structural Verilog
module DTL_ALU (
  input  A,
  input  B,
  input  Cin,
  input  SETC,
  input  LD,
  input  IR6,
  input  IR5,
  input  IR4,
  output Cout,
  output CLC,
  output CtoFF,
  output Fout,
  output CLR
);

  wire diodebackward_6_out, diodebackward_10_out, diodebackward_44_out, diodebackward_74_out,
       diodebackward_84_out, diodebackward_108_out, diodebackward_121_out, not_1_out, not_2_out, not_3_out,
       not_4_out, not_5_out, not_6_out, not_7_out, not_8_out, not_9_out, not_11_out, not_12_out, not_13_out,
       not_14_out, not_18_out, not_19_out, not_20_out, not_21_out, not_22_out, not_23_out, not_24_out,
       not_26_out, not_27_out, not_28_out, not_29_out, not_30_out, not_31_out, not_32_out, not_33_out,
       pullup_1_out, pullup_3_out, pullup_5_out, pullup_6_out, pullup_7_out, pullup_8_out, pullup_9_out,
       pullup_10_out, pullup_11_out, pullup_13_out, pullup_14_out, pullup_15_out, pullup_16_out,
       pullup_17_out, pullup_18_out, pullup_21_out, pullup_22_out, pullup_23_out, pullup_25_out,
       pullup_26_out;

  not not_1 (not_1_out, IR4);
  not not_2 (not_2_out, IR5);
  not not_3 (not_3_out, IR6);
  not not_4 (not_4_out, B);
  not not_5 (not_5_out, A);
  not not_6 (not_6_out, Cin);
  PullUp pullup_1 (.out(pullup_1_out));
  DiodeBackward diodebackward_1 (.in(A), .out(pullup_1_out));
  DiodeBackward diodebackward_2 (.in(not_4_out), .out(pullup_1_out));
  DiodeBackward diodebackward_3 (.in(IR4), .out(pullup_1_out));
  not not_7 (not_7_out, pullup_1_out);
  DiodeBackward diodebackward_4 (.in(not_2_out), .out(pullup_1_out));
  DiodeBackward diodebackward_5 (.in(IR6), .out(pullup_1_out));
  DiodeBackward diodebackward_6 (.in(A), .out(diodebackward_6_out));
  not not_8 (not_8_out, diodebackward_6_out);
  PullUp pullup_2 (.out(diodebackward_6_out));
  DiodeBackward diodebackward_7 (.in(Cin), .out(diodebackward_6_out));
  DiodeBackward diodebackward_8 (.in(not_1_out), .out(diodebackward_6_out));
  DiodeBackward diodebackward_9 (.in(not_2_out), .out(diodebackward_6_out));
  DiodeBackward diodebackward_10 (.in(not_7_out), .out(diodebackward_10_out));
  not not_9 (not_9_out, pullup_3_out);
  PullUp pullup_3 (.out(pullup_3_out));
  DiodeBackward diodebackward_11 (.in(A), .out(pullup_3_out));
  DiodeBackward diodebackward_12 (.in(B), .out(pullup_3_out));
  DiodeBackward diodebackward_13 (.in(not_1_out), .out(pullup_3_out));
  DiodeBackward diodebackward_14 (.in(not_2_out), .out(pullup_3_out));
  not not_10 (Cout, diodebackward_10_out);
  PullUp pullup_4 (.out(diodebackward_10_out));
  DiodeBackward diodebackward_15 (.in(not_8_out), .out(diodebackward_10_out));
  DiodeBackward diodebackward_16 (.in(not_9_out), .out(diodebackward_10_out));
  DiodeBackward diodebackward_17 (.in(not_11_out), .out(diodebackward_10_out));
  DiodeBackward diodebackward_18 (.in(not_12_out), .out(diodebackward_10_out));
  PullUp pullup_5 (.out(pullup_5_out));
  DiodeBackward diodebackward_19 (.in(A), .out(pullup_5_out));
  DiodeBackward diodebackward_20 (.in(Cin), .out(pullup_5_out));
  DiodeBackward diodebackward_21 (.in(not_2_out), .out(pullup_5_out));
  DiodeBackward diodebackward_22 (.in(not_13_out), .out(diodebackward_10_out));
  PullUp pullup_6 (.out(pullup_6_out));
  not not_11 (not_11_out, pullup_5_out);
  DiodeBackward diodebackward_23 (.in(IR6), .out(pullup_5_out));
  DiodeBackward diodebackward_24 (.in(not_4_out), .out(pullup_6_out));
  DiodeBackward diodebackward_25 (.in(Cin), .out(pullup_6_out));
  not not_12 (not_12_out, pullup_6_out);
  DiodeBackward diodebackward_26 (.in(IR4), .out(pullup_6_out));
  DiodeBackward diodebackward_27 (.in(not_2_out), .out(pullup_6_out));
  DiodeBackward diodebackward_28 (.in(IR6), .out(pullup_6_out));
  not not_13 (not_13_out, pullup_7_out);
  PullUp pullup_7 (.out(pullup_7_out));
  DiodeBackward diodebackward_29 (.in(B), .out(pullup_7_out));
  DiodeBackward diodebackward_30 (.in(Cin), .out(pullup_7_out));
  DiodeBackward diodebackward_31 (.in(not_1_out), .out(pullup_7_out));
  DiodeBackward diodebackward_32 (.in(not_2_out), .out(pullup_7_out));
  PullUp pullup_8 (.out(pullup_8_out));
  DiodeBackward diodebackward_33 (.in(not_14_out), .out(pullup_8_out));
  not not_14 (not_14_out, pullup_9_out);
  PullUp pullup_9 (.out(pullup_9_out));
  DiodeBackward diodebackward_34 (.in(IR4), .out(pullup_9_out));
  DiodeBackward diodebackward_35 (.in(not_2_out), .out(pullup_9_out));
  DiodeBackward diodebackward_36 (.in(IR6), .out(pullup_9_out));
  not not_15 (CLC, pullup_8_out);
  DiodeBackward diodebackward_37 (.in(LD), .out(pullup_8_out));
  not not_16 (CLR, pullup_10_out);
  PullUp pullup_10 (.out(pullup_10_out));
  DiodeBackward diodebackward_38 (.in(not_1_out), .out(pullup_10_out));
  DiodeBackward diodebackward_39 (.in(not_2_out), .out(pullup_10_out));
  DiodeBackward diodebackward_40 (.in(not_3_out), .out(pullup_10_out));
  PullUp pullup_11 (.out(pullup_11_out));
  DiodeBackward diodebackward_41 (.in(LD), .out(pullup_10_out));
  DiodeBackward diodebackward_42 (.in(IR4), .out(pullup_11_out));
  DiodeBackward diodebackward_43 (.in(not_2_out), .out(pullup_11_out));
  not not_17 (CtoFF, pullup_11_out);
  DiodeBackward diodebackward_44 (.in(not_5_out), .out(diodebackward_44_out));
  DiodeBackward diodebackward_45 (.in(IR6), .out(pullup_11_out));
  DiodeBackward diodebackward_46 (.in(SETC), .out(pullup_11_out));
  not not_18 (not_18_out, diodebackward_44_out);
  PullUp pullup_12 (.out(diodebackward_44_out));
  DiodeBackward diodebackward_47 (.in(not_4_out), .out(diodebackward_44_out));
  DiodeBackward diodebackward_48 (.in(not_6_out), .out(diodebackward_44_out));
  DiodeBackward diodebackward_49 (.in(IR4), .out(diodebackward_44_out));
  DiodeBackward diodebackward_50 (.in(not_2_out), .out(diodebackward_44_out));
  PullUp pullup_13 (.out(pullup_13_out));
  DiodeBackward diodebackward_51 (.in(IR6), .out(diodebackward_44_out));
  DiodeBackward diodebackward_52 (.in(not_5_out), .out(pullup_13_out));
  DiodeBackward diodebackward_53 (.in(B), .out(pullup_13_out));
  not not_19 (not_19_out, pullup_13_out);
  DiodeBackward diodebackward_54 (.in(Cin), .out(pullup_13_out));
  DiodeBackward diodebackward_55 (.in(IR4), .out(pullup_13_out));
  DiodeBackward diodebackward_56 (.in(not_2_out), .out(pullup_13_out));
  not not_20 (not_20_out, pullup_14_out);
  PullUp pullup_14 (.out(pullup_14_out));
  DiodeBackward diodebackward_57 (.in(A), .out(pullup_14_out));
  DiodeBackward diodebackward_58 (.in(not_4_out), .out(pullup_14_out));
  DiodeBackward diodebackward_59 (.in(Cin), .out(pullup_14_out));
  DiodeBackward diodebackward_60 (.in(IR4), .out(pullup_14_out));
  PullUp pullup_15 (.out(pullup_15_out));
  DiodeBackward diodebackward_61 (.in(not_2_out), .out(pullup_14_out));
  DiodeBackward diodebackward_62 (.in(A), .out(pullup_15_out));
  DiodeBackward diodebackward_63 (.in(B), .out(pullup_15_out));
  not not_21 (not_21_out, pullup_15_out);
  DiodeBackward diodebackward_64 (.in(not_6_out), .out(pullup_15_out));
  DiodeBackward diodebackward_65 (.in(IR4), .out(pullup_15_out));
  DiodeBackward diodebackward_66 (.in(not_2_out), .out(pullup_15_out));
  not not_22 (not_22_out, pullup_16_out);
  PullUp pullup_16 (.out(pullup_16_out));
  DiodeBackward diodebackward_67 (.in(not_5_out), .out(pullup_16_out));
  DiodeBackward diodebackward_68 (.in(not_4_out), .out(pullup_16_out));
  DiodeBackward diodebackward_69 (.in(Cin), .out(pullup_16_out));
  DiodeBackward diodebackward_70 (.in(not_1_out), .out(pullup_16_out));
  PullUp pullup_17 (.out(pullup_17_out));
  DiodeBackward diodebackward_71 (.in(not_5_out), .out(pullup_17_out));
  DiodeBackward diodebackward_72 (.in(B), .out(pullup_17_out));
  DiodeBackward diodebackward_73 (.in(not_6_out), .out(pullup_17_out));
  DiodeBackward diodebackward_74 (.in(not_18_out), .out(diodebackward_74_out));
  PullUp pullup_18 (.out(pullup_18_out));
  not not_23 (not_23_out, pullup_17_out);
  DiodeBackward diodebackward_75 (.in(A), .out(pullup_18_out));
  DiodeBackward diodebackward_76 (.in(not_4_out), .out(pullup_18_out));
  DiodeBackward diodebackward_77 (.in(not_1_out), .out(pullup_17_out));
  DiodeBackward diodebackward_78 (.in(not_19_out), .out(diodebackward_74_out));
  DiodeBackward diodebackward_79 (.in(not_20_out), .out(diodebackward_74_out));
  DiodeBackward diodebackward_80 (.in(not_21_out), .out(diodebackward_74_out));
  DiodeBackward diodebackward_81 (.in(not_22_out), .out(diodebackward_74_out));
  not not_24 (not_24_out, pullup_18_out);
  DiodeBackward diodebackward_82 (.in(not_6_out), .out(pullup_18_out));
  DiodeBackward diodebackward_83 (.in(not_1_out), .out(pullup_18_out));
  DiodeBackward diodebackward_84 (.in(A), .out(diodebackward_84_out));
  not not_25 (Fout, diodebackward_74_out);
  PullUp pullup_19 (.out(diodebackward_74_out));
  DiodeBackward diodebackward_85 (.in(not_27_out), .out(diodebackward_74_out));
  DiodeBackward diodebackward_86 (.in(not_23_out), .out(diodebackward_74_out));
  DiodeBackward diodebackward_87 (.in(not_24_out), .out(diodebackward_74_out));
  DiodeBackward diodebackward_88 (.in(not_26_out), .out(diodebackward_74_out));
  not not_26 (not_26_out, diodebackward_84_out);
  PullUp pullup_20 (.out(diodebackward_84_out));
  DiodeBackward diodebackward_89 (.in(B), .out(diodebackward_84_out));
  DiodeBackward diodebackward_90 (.in(Cin), .out(diodebackward_84_out));
  DiodeBackward diodebackward_91 (.in(not_1_out), .out(diodebackward_84_out));
  DiodeBackward diodebackward_92 (.in(not_28_out), .out(diodebackward_74_out));
  DiodeBackward diodebackward_93 (.in(not_29_out), .out(diodebackward_74_out));
  DiodeBackward diodebackward_94 (.in(not_30_out), .out(diodebackward_74_out));
  DiodeBackward diodebackward_95 (.in(not_31_out), .out(diodebackward_74_out));
  not not_27 (not_27_out, pullup_21_out);
  PullUp pullup_21 (.out(pullup_21_out));
  DiodeBackward diodebackward_96 (.in(not_5_out), .out(pullup_21_out));
  DiodeBackward diodebackward_97 (.in(not_4_out), .out(pullup_21_out));
  DiodeBackward diodebackward_98 (.in(Cin), .out(pullup_21_out));
  DiodeBackward diodebackward_99 (.in(IR5), .out(pullup_21_out));
  DiodeBackward diodebackward_100 (.in(not_33_out), .out(diodebackward_74_out));
  DiodeBackward diodebackward_101 (.in(not_32_out), .out(diodebackward_74_out));
  PullUp pullup_22 (.out(pullup_22_out));
  DiodeBackward diodebackward_102 (.in(not_5_out), .out(pullup_22_out));
  DiodeBackward diodebackward_103 (.in(B), .out(pullup_22_out));
  DiodeBackward diodebackward_104 (.in(not_6_out), .out(pullup_22_out));
  not not_28 (not_28_out, pullup_22_out);
  PullUp pullup_23 (.out(pullup_23_out));
  DiodeBackward diodebackward_105 (.in(IR5), .out(pullup_22_out));
  DiodeBackward diodebackward_106 (.in(A), .out(pullup_23_out));
  DiodeBackward diodebackward_107 (.in(not_4_out), .out(pullup_23_out));
  not not_29 (not_29_out, pullup_23_out);
  DiodeBackward diodebackward_108 (.in(A), .out(diodebackward_108_out));
  DiodeBackward diodebackward_109 (.in(not_6_out), .out(pullup_23_out));
  DiodeBackward diodebackward_110 (.in(IR5), .out(pullup_23_out));
  not not_30 (not_30_out, diodebackward_108_out);
  PullUp pullup_24 (.out(diodebackward_108_out));
  DiodeBackward diodebackward_111 (.in(B), .out(diodebackward_108_out));
  DiodeBackward diodebackward_112 (.in(Cin), .out(diodebackward_108_out));
  DiodeBackward diodebackward_113 (.in(IR5), .out(diodebackward_108_out));
  not not_31 (not_31_out, pullup_25_out);
  PullUp pullup_25 (.out(pullup_25_out));
  DiodeBackward diodebackward_114 (.in(B), .out(pullup_25_out));
  DiodeBackward diodebackward_115 (.in(Cin), .out(pullup_25_out));
  DiodeBackward diodebackward_116 (.in(IR4), .out(pullup_25_out));
  DiodeBackward diodebackward_117 (.in(not_2_out), .out(pullup_25_out));
  PullUp pullup_26 (.out(pullup_26_out));
  DiodeBackward diodebackward_118 (.in(not_3_out), .out(pullup_25_out));
  DiodeBackward diodebackward_119 (.in(B), .out(pullup_26_out));
  DiodeBackward diodebackward_120 (.in(not_1_out), .out(pullup_26_out));
  not not_32 (not_32_out, pullup_26_out);
  DiodeBackward diodebackward_121 (.in(Cin), .out(diodebackward_121_out));
  DiodeBackward diodebackward_122 (.in(IR5), .out(pullup_26_out));
  DiodeBackward diodebackward_123 (.in(not_3_out), .out(pullup_26_out));
  not not_33 (not_33_out, diodebackward_121_out);
  PullUp pullup_27 (.out(diodebackward_121_out));
  DiodeBackward diodebackward_124 (.in(not_1_out), .out(diodebackward_121_out));
  DiodeBackward diodebackward_125 (.in(IR5), .out(diodebackward_121_out));
  DiodeBackward diodebackward_126 (.in(not_3_out), .out(diodebackward_121_out));

  // Notes on the sheet:
  //   DTL BIT SERIAL ALU.
  //   33 Inverters
  //   33 pull-up resistors
  //   130 diodes
endmodule
