// Digital circuit DTL_Inst_Dec_ALU.dig as structural Verilog
module DTL_Inst_Dec_ALU (
  input  A,
  input  B,
  input  Cin,
  input  SETC,
  input  LD,
  input  IR6,
  input  IR5,
  input  IR4,
  output Cout,
  output CLC,
  output CtoFF,
  output Fout,
  output CLR
);

  wire ADD, AND, C, CLA, diodebackward_26_out, diodebackward_29_out, diodebackward_31_out,
       diodebackward_33_out, F, I0, I1, LOAD, nA, nand_1_out, nand_2_out, nand_3_out, nand_4_out, nand_5_out,
       nand_6_out, nand_7_out, nand_8_out, nand_9_out, nand_10_out, nand_11_out, nand_12_out, nand_14_out,
       nand_17_out, nand_18_out, nand_19_out, nand_20_out, nand_21_out, nand_22_out, nand_23_out, nB, nJMP,
       not_1_out, not_2_out, not_3_out, not_19_out, OR, pullup_1_out, pullup_2_out, pullup_3_out,
       pullup_4_out, pullup_5_out, pullup_6_out, pullup_7_out, pullup_8_out, pullup_9_out, pullup_12_out,
       pullup_13_out, ST, SUB, XOR;

  not not_1 (not_1_out, IR4);
  not not_2 (not_2_out, IR5);
  not not_3 (not_3_out, IR6);
  PullUp pullup_1 (.out(pullup_1_out));
  DiodeBackward diodebackward_1 (.in(not_1_out), .out(pullup_1_out));
  not not_4 (LOAD, pullup_1_out);
  DiodeBackward diodebackward_2 (.in(not_2_out), .out(pullup_1_out));
  DiodeBackward diodebackward_3 (.in(not_3_out), .out(pullup_1_out));
  PullUp pullup_2 (.out(pullup_2_out));
  DiodeBackward diodebackward_4 (.in(IR4), .out(pullup_2_out));
  not not_5 (AND, pullup_2_out);
  DiodeBackward diodebackward_5 (.in(not_2_out), .out(pullup_2_out));
  DiodeBackward diodebackward_6 (.in(not_3_out), .out(pullup_2_out));
  PullUp pullup_3 (.out(pullup_3_out));
  DiodeBackward diodebackward_7 (.in(not_1_out), .out(pullup_3_out));
  not not_6 (OR, pullup_3_out);
  DiodeBackward diodebackward_8 (.in(IR5), .out(pullup_3_out));
  DiodeBackward diodebackward_9 (.in(not_3_out), .out(pullup_3_out));
  PullUp pullup_4 (.out(pullup_4_out));
  DiodeBackward diodebackward_10 (.in(IR4), .out(pullup_4_out));
  not not_7 (XOR, pullup_4_out);
  DiodeBackward diodebackward_11 (.in(IR5), .out(pullup_4_out));
  DiodeBackward diodebackward_12 (.in(not_3_out), .out(pullup_4_out));
  PullUp pullup_5 (.out(pullup_5_out));
  DiodeBackward diodebackward_13 (.in(not_1_out), .out(pullup_5_out));
  not not_8 (ADD, pullup_5_out);
  DiodeBackward diodebackward_14 (.in(not_2_out), .out(pullup_5_out));
  DiodeBackward diodebackward_15 (.in(IR6), .out(pullup_5_out));
  PullUp pullup_6 (.out(pullup_6_out));
  DiodeBackward diodebackward_16 (.in(IR4), .out(pullup_6_out));
  not not_9 (SUB, pullup_6_out);
  DiodeBackward diodebackward_17 (.in(not_2_out), .out(pullup_6_out));
  DiodeBackward diodebackward_18 (.in(IR6), .out(pullup_6_out));
  PullUp pullup_7 (.out(pullup_7_out));
  DiodeBackward diodebackward_19 (.in(not_1_out), .out(pullup_7_out));
  not not_10 (ST, pullup_7_out);
  DiodeBackward diodebackward_20 (.in(IR5), .out(pullup_7_out));
  DiodeBackward diodebackward_21 (.in(IR6), .out(pullup_7_out));
  PullUp pullup_8 (.out(pullup_8_out));
  DiodeBackward diodebackward_22 (.in(IR4), .out(pullup_8_out));
  not not_11 (nJMP, pullup_8_out);
  DiodeBackward diodebackward_23 (.in(IR5), .out(pullup_8_out));
  DiodeBackward diodebackward_24 (.in(IR6), .out(pullup_8_out));
  PullUp pullup_9 (.out(pullup_9_out));
  DiodeBackward diodebackward_25 (.in(LOAD), .out(pullup_9_out));
  DiodeBackward diodebackward_26 (.in(LOAD), .out(diodebackward_26_out));
  DiodeBackward diodebackward_27 (.in(ADD), .out(diodebackward_26_out));
  DiodeBackward diodebackward_28 (.in(SUB), .out(diodebackward_26_out));
  PullUp pullup_10 (.out(diodebackward_26_out));
  DiodeBackward diodebackward_29 (.in(SUB), .out(diodebackward_29_out));
  nand nand_1 (nand_1_out, A, nA);
  nand nand_2 (nand_2_out, B, nB);
  PullUp pullup_11 (.out(diodebackward_29_out));
  PullUp pullup_12 (.out(pullup_12_out));
  DiodeBackward diodebackward_30 (.in(SUB), .out(pullup_12_out));
  PullUp pullup_13 (.out(pullup_13_out));
  DiodeBackward diodebackward_31 (.in(AND), .out(diodebackward_31_out));
  DiodeBackward diodebackward_32 (.in(OR), .out(diodebackward_31_out));
  nand nand_3 (nand_3_out, A, nand_1_out);
  nand nand_4 (nand_4_out, nand_1_out, nA);
  nand nand_5 (nand_5_out, B, nand_2_out);
  nand nand_6 (nand_6_out, nand_2_out, nB);
  PullUp pullup_14 (.out(diodebackward_31_out));
  DiodeBackward diodebackward_33 (.in(LOAD), .out(diodebackward_33_out));
  DiodeBackward diodebackward_34 (.in(OR), .out(diodebackward_33_out));
  DiodeBackward diodebackward_35 (.in(XOR), .out(diodebackward_33_out));
  DiodeBackward diodebackward_36 (.in(ADD), .out(diodebackward_33_out));
  DiodeBackward diodebackward_37 (.in(SUB), .out(diodebackward_33_out));
  DiodeBackward diodebackward_38 (.in(ST), .out(diodebackward_33_out));
  DiodeBackward diodebackward_39 (.in(nJMP), .out(diodebackward_33_out));
  PullUp pullup_15 (.out(diodebackward_33_out));
  not not_12 (I0, diodebackward_33_out);
  not not_13 (I1, diodebackward_31_out);
  not not_14 (nA, pullup_13_out);
  not not_15 (nB, pullup_12_out);
  not not_16 (C, diodebackward_29_out);
  not not_17 (F, diodebackward_26_out);
  not not_18 (CLA, pullup_9_out);
  nand nand_7 (nand_7_out, nand_3_out, nand_4_out);
  nand nand_8 (nand_8_out, nand_5_out, nand_6_out);
  nand nand_9 (nand_9_out, nand_7_out, nand_8_out);
  nand nand_10 (nand_10_out, nand_7_out, nand_9_out);
  nand nand_11 (nand_11_out, nand_9_out, nand_8_out);
  nand nand_12 (nand_12_out, nand_10_out, nand_11_out);
  nand nand_13 (CtoFF, SETC, C);
  not not_19 (not_19_out, C);
  nand nand_14 (nand_14_out, nand_12_out, Cin);
  nand nand_15 (CLC, not_19_out, LD);
  nand nand_16 (CLR, LD, CLA);
  nand nand_17 (nand_17_out, nand_12_out, nand_14_out);
  nand nand_18 (nand_18_out, nand_14_out, Cin);
  nand nand_19 (nand_19_out, nand_17_out, nand_18_out);
  nand nand_20 (nand_20_out, nand_14_out, nand_9_out);
  nand nand_21 (nand_21_out, nand_19_out, I0);
  nand nand_22 (nand_22_out, I1, nand_20_out);
  nand nand_23 (nand_23_out, nand_20_out, F);
  nand nand_24 (Fout, nand_21_out, nand_22_out);
  not not_20 (Cout, nand_23_out);

  // Other names for the same wires on the sheet: Ain = A; Bin = B; Y7 = nJMP; Y0 = LOAD; Y1 = AND; Y2 = OR; Y3 = XOR;
  //   Y4 = ADD; Y5 = SUB; Y6 = ST

  // Notes on the sheet:
  //   ALU
  //   Instruction Input
  //   Serial Data Inputs
  //   3 to 8 line decoder
  //   CLA
  //   F
  //   ~B
  //   C
  //   ~A
  //   I1
  //   I0
  //   LOAD
  //   AND
  //   OR
  //   XOR
  //   ADD
  //   SUB
  //   STORE
  //   JMP
  //   Carry is only set before Bit 0 of an operation
  //   Any residual carry is cleared before an operation
  //   Suppress Carry
endmodule
