// Digital circuit DTL_menagerie.dig as structural Verilog
module DTL_menagerie (
  input  A,
  input  B,
  input  C,
  input  nE,
  input  S0,
  input  S1,
  input  A0,
  input  nE1,
  input  A1,
  input  A2,
  input  A3,
  input  nE2,
  input  B1,
  input  B2,
  input  B3,
  input  B0,
  input  A_2,
  input  B_2,
  input  Cin,
  input  in_33,
  input  in_34,
  input  in_35,
  input  in_36,
  input  D,
  input  CLK,
  input  CLK_2,
  input  D_2,
  input  CLK_3,
  input  nSET,
  input  nRESET,
  input  DATA,
  input  nSET_2,
  input  nRESET_2,
  input  B_3,
  input  A_3,
  input  I0,
  input  I1,
  input  I2,
  input  I3,
  input  Cin_2,
  input  I0_2,
  input  I1_2,
  input  I2_2,
  input  I3_2,
  input  A_4,
  input  B_4,
  input  Cin_3,
  input  I0_3,
  input  I1_3,
  input  S0_2,
  input  S1_2,
  input  D0,
  input  S2,
  input  D1,
  input  D2,
  input  D3,
  input  D4,
  input  D5,
  input  D6,
  input  D7,
  input  CLK_4,
  input  nRES,
  input  A_5,
  input  B_5,
  input  A_6,
  input  B_6,
  input  Cin_4,
  input  A_7,
  input  B_7,
  input  C_2,
  input  D_3,
  input  A3_2,
  input  B3_2,
  input  A2_2,
  input  B2_2,
  input  A1_2,
  input  B1_2,
  input  A0_2,
  input  B0_2,
  input  Cin_5,
  input  S1_3,
  input  S0_3,
  input  D_4,
  input  C_3,
  input  B_8,
  input  A_8,
  input  EN,
  input  D8,
  input  D9,
  input  D10,
  input  D11,
  input  D12,
  input  D13,
  input  D14,
  input  D15,
  input  D0_2,
  input  D1_2,
  input  D2_2,
  input  D3_2,
  input  D4_2,
  input  D5_2,
  input  D6_2,
  input  D7_2,
  input  I4,
  input  I5,
  input  nSET_3,
  input  nRESET_3,
  input  A_9,
  input  B_9,
  input  C_4,
  input  nE_2,
  input  A0_3,
  input  B0_3,
  input  A1_3,
  input  B1_3,
  input  A2_3,
  input  B2_3,
  input  A3_3,
  input  B3_3,
  input  I0_4,
  input  I1_4,
  input  CLK_5,
  input  nSET_4,
  input  nRESET_4,
  input  DATA_2,
  input  nLD_COUNT,
  input  RES,
  input  INC,
  input  clk_6,
  input  D16,
  input  D17,
  input  D18,
  input  D19,
  input  clk_7,
  input  D20,
  input  D21,
  input  D22,
  input  D23,
  input  CLK_8,
  input  D_5,
  input  I0_5,
  input  I1_5,
  input  M,
  input  A_10,
  input  B_10,
  input  Cin_6,
  output out_1,
  output out_2,
  output out_3,
  output out_4,
  output out_5,
  output out_6,
  output out_7,
  output out_8,
  output out_17,
  output out_18,
  output CARRY,
  output SUM,
  output out_32,
  output Q,
  output nQ,
  output Q_2,
  output nQ_2,
  output Q_3,
  output nQ_3,
  output Q_4,
  output nQ_4,
  output out_58,
  output out_64,
  output CARRY_2,
  output Fout,
  output out_78,
  output out_91,
  output SUM_2,
  output Cout,
  output out_97,
  output SUM2,
  output SUM1,
  output SUM0,
  output out_117,
  output out_138,
  output CARRY_3,
  output Fout_2,
  output nQ_5,
  output out_146,
  output out_147,
  output out_148,
  output out_149,
  output out_150,
  output out_151,
  output out_152,
  output out_153,
  output F0,
  output F1,
  output F2,
  output F3,
  output Q_5,
  output nQ_6,
  output Q_6,
  output Q_7,
  output Q_8,
  output Q_9,
  output Q_10,
  output Q_11,
  output Q_12,
  output Q_13,
  output Fout_3,
  output Sum_3,
  output Cout_2
);

  wire A0_t, A1_t, A2_t, A3_t, A4, A5, A6, A7, A8, A9, A10, A11, A12, A13, A14, A15, C0, C1, C2, C3, Cin_t,
       diodebackward_1_out, diodebackward_3_out, diodebackward_5_out, diodebackward_7_out,
       diodebackward_9_out, diodebackward_11_out, diodebackward_13_out, diodebackward_15_out,
       diodebackward_17_out, diodebackward_19_out, diodebackward_21_out, diodebackward_23_out,
       diodebackward_25_out, diodebackward_27_out, diodebackward_29_out, diodebackward_31_out,
       diodebackward_101_out, diodebackward_103_out, diodebackward_106_out, diodebackward_108_out,
       diodebackward_111_out, diodebackward_113_out, diodebackward_116_out, diodebackward_118_out,
       diodebackward_121_out, diodebackward_123_out, diodebackward_125_out, diodebackward_127_out,
       diodebackward_153_out, diodebackward_155_out, diodebackward_157_out, diodebackward_159_out,
       diodebackward_161_out, diodebackward_163_out, diodebackward_165_out, diodebackward_167_out,
       diodebackward_169_out, diodebackward_171_out, diodebackward_173_out, diodebackward_175_out,
       diodebackward_177_out, diodebackward_179_out, diodebackward_181_out, diodebackward_183_out,
       diodebackward_186_out, diodebackward_188_out, diodebackward_190_out, diodebackward_256_out,
       diodebackward_260_out, diodebackward_264_out, diodebackward_268_out, diodebackward_272_out,
       diodebackward_276_out, diodebackward_280_out, diodebackward_284_out, diodebackward_288_out,
       diodebackward_292_out, diodebackward_296_out, diodebackward_300_out, diodebackward_304_out,
       diodebackward_308_out, diodebackward_312_out, diodebackward_316_out, diodebackward_320_out,
       diodebackward_328_out, diodebackward_336_out, diodebackward_338_out, diodebackward_340_out,
       diodebackward_392_out, diodebackward_394_out, diodebackward_438_out, diodebackward_440_out,
       diodebackward_443_out, diodebackward_446_out, diodebackward_449_out, diodebackward_451_out,
       diodebackward_454_out, diodebackward_457_out, diodebackward_472_out, diodebackward_474_out,
       diodebackward_477_out, diodebackward_479_out, diodebackward_497_out, diodebackward_499_out,
       diodebackward_502_out, diodebackward_505_out, diodebackward_533_out, diodebackward_535_out,
       diodebackward_538_out, diodebackward_649_out, diodebackward_651_out, diodebackward_653_out,
       diodebackward_655_out, diodebackward_658_out, diodebackward_660_out, diodebackward_662_out,
       diodebackward_664_out, diodebackward_666_out, diodebackward_668_out, diodebackward_670_out,
       diodebackward_684_out, diodebackward_688_out, diodebackward_692_out, diodebackward_696_out,
       diodebackward_700_out, diodebackward_704_out, diodebackward_708_out, diodebackward_712_out,
       diodebackward_728_out, diodebackward_730_out, diodebackward_736_out, diodebackward_738_out,
       diodebackward_748_out, diodebackward_750_out, diodebackward_753_out, diodebackward_756_out,
       diodebackward_761_out, diodebackward_763_out, diodebackward_766_out, diodebackward_768_out,
       diodebackward_770_out, diodebackward_776_out, diodebackward_778_out, diodebackward_781_out,
       diodebackward_784_out, diodebackward_787_out, diodebackward_789_out, diodebackward_792_out,
       diodebackward_795_out, diodebackward_798_out, diodebackward_801_out, diodebackward_803_out,
       diodebackward_805_out, diodebackward_807_out, diodebackward_810_out, diodebackward_812_out,
       diodebackward_814_out, diodebackward_816_out, diodebackward_819_out, diodebackward_822_out,
       diodebackward_825_out, diodebackward_828_out, diodebackward_832_out, diodebackward_834_out,
       diodebackward_837_out, diodebackward_848_out, diodebackward_851_out, diodebackward_878_out,
       diodebackward_880_out, diodebackward_901_out, diodebackward_903_out, diodebackward_905_out,
       diodebackward_907_out, diodebackward_909_out, diodebackward_911_out, diodebackward_924_out,
       diodebackward_928_out, diodebackward_944_out, diodebackward_946_out, diodebackward_948_out,
       diodebackward_950_out, diodebackward_953_out, diodebackward_956_out, diodebackward_959_out,
       diodebackward_961_out, diodebackward_963_out, diodebackward_966_out, diodebackward_969_out,
       diodebackward_972_out, diodebackward_975_out, diodebackward_978_out, diodebackward_980_out,
       diodebackward_983_out, diodebackward_986_out, diodebackward_989_out, diodebackward_992_out,
       diodebackward_995_out, diodebackward_997_out, diodebackward_1024_out, diodebackward_1026_out,
       diodebackward_1028_out, diodebackward_1030_out, diodebackward_1032_out, diodebackward_1034_out,
       diodebackward_1036_out, diodebackward_1038_out, diodebackward_1040_out, diodebackward_1042_out,
       diodebackward_1044_out, diodebackward_1046_out, diodebackward_1048_out, diodebackward_1050_out,
       diodebackward_1053_out, diodebackward_1056_out, diodebackward_1059_out, diodebackward_1061_out,
       diodebackward_1063_out, diodebackward_1065_out, diodebackward_1067_out, diodebackward_1069_out,
       diodebackward_1071_out, diodebackward_1073_out, diodebackward_1075_out, diodebackward_1077_out,
       diodebackward_1079_out, diodebackward_1081_out, diodebackward_1083_out, diodebackward_1085_out,
       diodebackward_1087_out, diodebackward_1089_out, diodebackward_1091_out, diodebackward_1093_out,
       diodebackward_1096_out, diodebackward_1098_out, diodebackward_1100_out, diodebackward_1102_out,
       diodebackward_1104_out, diodebackward_1106_out, diodebackward_1109_out, diodebackward_1112_out,
       diodebackward_1115_out, diodebackward_1117_out, diodebackward_1120_out, diodebackward_1122_out,
       diodebackward_1125_out, diodebackward_1143_out, diodebackward_1145_out, diodebackward_1148_out,
       diodebackward_1151_out, diodebackward_1154_out, diodebackward_1158_out, diodebackward_1162_out,
       diodebackward_1166_out, diodebackward_1170_out, diodebackward_1174_out, diodebackward_1178_out,
       diodebackward_1182_out, diodebackward_1186_out, diodebackward_1194_out, diodebackward_1196_out,
       diodebackward_1199_out, diodebackward_1207_out, diodebackward_1215_out, diodebackward_1223_out,
       diodebackward_1231_out, diodebackward_1239_out, diodebackward_1247_out, diodeforward_1_out,
       diodeforward_5_out, INC_t, not_1_out, not_2_out, not_3_out, not_4_out, not_5_out, not_6_out,
       not_7_out, not_8_out, not_9_out, not_10_out, not_11_out, not_12_out, not_13_out, not_14_out,
       not_15_out, not_16_out, not_17_out, not_18_out, not_19_out, not_20_out, not_21_out, not_22_out,
       not_23_out, not_24_out, not_25_out, not_26_out, not_27_out, not_28_out, not_29_out, not_30_out,
       not_31_out, not_32_out, not_33_out, not_34_out, not_35_out, not_36_out, not_37_out, not_38_out,
       not_39_out, not_40_out, not_41_out, not_42_out, not_43_out, not_44_out, not_45_out, not_46_out,
       not_47_out, not_48_out, not_49_out, not_50_out, not_51_out, not_52_out, not_54_out, not_56_out,
       not_58_out, not_60_out, not_61_out, not_62_out, not_63_out, not_64_out, not_65_out, not_66_out,
       not_67_out, not_69_out, not_70_out, not_71_out, not_72_out, not_73_out, not_74_out, not_75_out,
       not_76_out, not_77_out, not_78_out, not_79_out, not_80_out, not_81_out, not_82_out, not_83_out,
       not_84_out, not_85_out, not_86_out, not_87_out, not_88_out, not_89_out, not_90_out, not_91_out,
       not_92_out, not_93_out, not_94_out, not_95_out, not_96_out, not_97_out, not_98_out, not_100_out,
       not_101_out, not_102_out, not_103_out, not_104_out, not_105_out, not_106_out, not_107_out,
       not_108_out, not_109_out, not_110_out, not_111_out, not_112_out, not_113_out, not_114_out,
       not_115_out, not_118_out, not_120_out, not_122_out, not_124_out, not_125_out, not_126_out,
       not_127_out, not_128_out, not_129_out, not_130_out, not_131_out, not_132_out, not_133_out,
       not_134_out, not_135_out, not_136_out, not_137_out, not_138_out, not_139_out, not_140_out,
       not_141_out, not_142_out, not_143_out, not_144_out, not_146_out, not_147_out, not_148_out,
       not_149_out, not_150_out, not_151_out, not_152_out, not_153_out, not_154_out, not_159_out,
       not_160_out, not_161_out, not_162_out, not_163_out, not_164_out, not_165_out, not_166_out,
       not_167_out, not_168_out, not_169_out, not_170_out, not_171_out, not_172_out, not_173_out,
       not_174_out, not_176_out, not_179_out, not_180_out, not_181_out, not_182_out, not_183_out,
       not_184_out, not_185_out, not_186_out, not_187_out, not_188_out, not_189_out, not_190_out,
       not_192_out, not_193_out, not_194_out, not_195_out, not_196_out, not_197_out, not_201_out,
       not_202_out, not_203_out, not_204_out, not_205_out, not_206_out, not_207_out, not_208_out,
       not_209_out, not_210_out, not_211_out, not_212_out, not_213_out, not_214_out, not_215_out,
       not_216_out, not_217_out, not_218_out, not_219_out, not_220_out, not_221_out, not_222_out,
       not_223_out, not_227_out, not_237_out, not_238_out, not_239_out, not_240_out, not_241_out,
       not_242_out, not_243_out, not_244_out, not_245_out, not_246_out, not_247_out, not_248_out,
       not_249_out, not_250_out, not_255_out, not_256_out, not_258_out, not_259_out, not_260_out,
       not_261_out, not_262_out, not_263_out, not_264_out, not_265_out, not_266_out, not_267_out,
       not_268_out, not_269_out, not_270_out, not_271_out, not_272_out, not_273_out, not_274_out,
       not_275_out, not_276_out, not_277_out, not_278_out, not_279_out, not_280_out, not_281_out,
       not_282_out, not_283_out, not_284_out, not_285_out, not_286_out, not_287_out, not_288_out,
       not_289_out, not_290_out, not_291_out, not_292_out, not_293_out, not_294_out, not_296_out,
       not_301_out, not_305_out, not_306_out, not_307_out, not_308_out, not_309_out, not_310_out,
       not_313_out, not_314_out, not_315_out, not_316_out, not_317_out, not_318_out, not_319_out,
       not_320_out, not_321_out, not_322_out, not_323_out, not_324_out, not_325_out, not_326_out,
       not_327_out, not_328_out, not_329_out, not_330_out, not_331_out, not_332_out, not_333_out,
       not_334_out, not_335_out, not_336_out, not_337_out, not_338_out, not_339_out, not_340_out,
       not_341_out, not_344_out, not_346_out, not_347_out, not_354_out, not_355_out, not_356_out,
       not_357_out, not_358_out, not_360_out, not_361_out, not_362_out, not_363_out, not_364_out,
       not_365_out, not_366_out, not_367_out, not_368_out, not_369_out, not_370_out, not_371_out,
       not_372_out, not_377_out, not_378_out, not_379_out, not_380_out, not_381_out, not_382_out,
       not_383_out, not_384_out, not_386_out, not_387_out, not_389_out, not_390_out, not_391_out,
       not_394_out, not_395_out, not_396_out, not_397_out, not_400_out, not_401_out, not_402_out,
       not_403_out, not_404_out, not_405_out, not_406_out, not_407_out, not_408_out, not_412_out,
       not_413_out, not_414_out, not_415_out, not_416_out, not_417_out, not_418_out, not_419_out,
       not_420_out, not_422_out, not_423_out, not_424_out, not_425_out, not_426_out, not_427_out,
       not_428_out, not_429_out, not_430_out, not_431_out, not_432_out, not_433_out, not_434_out,
       not_435_out, not_436_out, not_437_out, not_438_out, not_439_out, not_440_out, not_441_out,
       not_442_out, not_443_out, not_444_out, not_446_out, not_447_out, not_449_out, not_450_out,
       not_452_out, not_453_out, not_456_out, not_457_out, not_461_out, not_462_out, not_463_out,
       not_464_out, not_465_out, not_466_out, not_468_out, not_470_out, not_471_out, not_472_out,
       not_473_out, not_475_out, not_476_out, not_477_out, not_478_out, not_479_out, not_480_out,
       not_481_out, not_482_out, not_483_out, not_494_out, nQ0, nQ1, nQ2, nQ3, pullup_17_out, pullup_18_out,
       pullup_19_out, pullup_20_out, pullup_21_out, pullup_22_out, pullup_23_out, pullup_24_out,
       pullup_25_out, pullup_26_out, pullup_27_out, pullup_28_out, pullup_29_out, pullup_30_out,
       pullup_31_out, pullup_32_out, pullup_33_out, pullup_34_out, pullup_35_out, pullup_36_out,
       pullup_37_out, pullup_38_out, pullup_39_out, pullup_40_out, pullup_41_out, pullup_42_out,
       pullup_43_out, pullup_44_out, pullup_57_out, pullup_58_out, pullup_59_out, pullup_60_out,
       pullup_61_out, pullup_62_out, pullup_63_out, pullup_64_out, pullup_65_out, pullup_66_out,
       pullup_67_out, pullup_68_out, pullup_88_out, pullup_89_out, pullup_90_out, pullup_91_out,
       pullup_92_out, pullup_93_out, pullup_94_out, pullup_95_out, pullup_96_out, pullup_97_out,
       pullup_98_out, pullup_99_out, pullup_100_out, pullup_101_out, pullup_102_out, pullup_103_out,
       pullup_104_out, pullup_105_out, pullup_106_out, pullup_107_out, pullup_108_out, pullup_109_out,
       pullup_110_out, pullup_111_out, pullup_133_out, pullup_134_out, pullup_135_out, pullup_136_out,
       pullup_137_out, pullup_138_out, pullup_139_out, pullup_140_out, pullup_141_out, pullup_142_out,
       pullup_143_out, pullup_144_out, pullup_145_out, pullup_146_out, pullup_147_out, pullup_148_out,
       pullup_149_out, pullup_150_out, pullup_151_out, pullup_152_out, pullup_153_out, pullup_154_out,
       pullup_155_out, pullup_156_out, pullup_157_out, pullup_158_out, pullup_161_out, pullup_162_out,
       pullup_163_out, pullup_164_out, pullup_165_out, pullup_166_out, pullup_167_out, pullup_168_out,
       pullup_173_out, pullup_178_out, pullup_179_out, pullup_184_out, pullup_185_out, pullup_186_out,
       pullup_187_out, pullup_188_out, pullup_189_out, pullup_194_out, pullup_195_out, pullup_196_out,
       pullup_197_out, pullup_198_out, pullup_199_out, pullup_200_out, pullup_201_out, pullup_204_out,
       pullup_205_out, pullup_206_out, pullup_207_out, pullup_208_out, pullup_209_out, pullup_210_out,
       pullup_211_out, pullup_212_out, pullup_213_out, pullup_214_out, pullup_215_out, pullup_216_out,
       pullup_217_out, pullup_219_out, pullup_220_out, pullup_221_out, pullup_222_out, pullup_223_out,
       pullup_224_out, pullup_225_out, pullup_226_out, pullup_227_out, pullup_228_out, pullup_229_out,
       pullup_230_out, pullup_231_out, pullup_232_out, pullup_233_out, pullup_234_out, pullup_235_out,
       pullup_236_out, pullup_237_out, pullup_238_out, pullup_239_out, pullup_240_out, pullup_241_out,
       pullup_253_out, pullup_254_out, pullup_255_out, pullup_256_out, pullup_257_out, pullup_258_out,
       pullup_259_out, pullup_260_out, pullup_271_out, pullup_272_out, pullup_273_out, pullup_280_out,
       pullup_286_out, pullup_287_out, pullup_304_out, pullup_313_out, pullup_314_out, pullup_315_out,
       pullup_316_out, pullup_317_out, pullup_320_out, pullup_321_out, pullup_322_out, pullup_323_out,
       pullup_324_out, pullup_325_out, pullup_326_out, pullup_329_out, pullup_330_out, pullup_331_out,
       pullup_332_out, pullup_333_out, pullup_334_out, pullup_335_out, pullup_336_out, pullup_337_out,
       pullup_338_out, pullup_339_out, pullup_340_out, pullup_341_out, pullup_350_out, pullup_351_out,
       pullup_352_out, pullup_353_out, pullup_354_out, pullup_355_out, pullup_377_out, pullup_378_out,
       pullup_379_out, pullup_380_out, pullup_381_out, pullup_382_out, pullup_383_out, pullup_384_out,
       pullup_385_out, pullup_386_out, pullup_434_out, pullup_435_out, pullup_436_out, pullup_437_out,
       pullup_438_out, pullup_439_out, Q0, Q1, Q2, Q3, Sum_t;

  DiodeBackward diodebackward_1 (.in(INC_t), .out(diodebackward_1_out));
  DiodeBackward diodebackward_2 (.in(Q_10), .out(diodebackward_1_out));
  DiodeBackward diodebackward_3 (.in(not_2_out), .out(diodebackward_3_out));
  DiodeBackward diodebackward_4 (.in(Q_11), .out(diodebackward_3_out));
  DiodeBackward diodebackward_5 (.in(not_4_out), .out(diodebackward_5_out));
  DiodeBackward diodebackward_6 (.in(Q_12), .out(diodebackward_5_out));
  DiodeBackward diodebackward_7 (.in(not_6_out), .out(diodebackward_7_out));
  DiodeBackward diodebackward_8 (.in(Q_13), .out(diodebackward_7_out));
  PullUp pullup_1 (.out(diodebackward_1_out));
  not not_1 (not_1_out, diodebackward_1_out);
  not not_2 (not_2_out, not_1_out);
  PullUp pullup_2 (.out(diodebackward_3_out));
  not not_3 (not_3_out, diodebackward_3_out);
  not not_4 (not_4_out, not_3_out);
  PullUp pullup_3 (.out(diodebackward_5_out));
  not not_5 (not_5_out, diodebackward_5_out);
  not not_6 (not_6_out, not_5_out);
  PullUp pullup_4 (.out(diodebackward_7_out));
  not not_7 (not_7_out, diodebackward_7_out);
  not not_8 (not_8_out, not_7_out);
  DiodeBackward diodebackward_9 (.in(INC_t), .out(diodebackward_9_out));
  DiodeBackward diodebackward_10 (.in(not_1_out), .out(diodebackward_9_out));
  DiodeBackward diodebackward_11 (.in(not_1_out), .out(diodebackward_11_out));
  DiodeBackward diodebackward_12 (.in(Q_10), .out(diodebackward_11_out));
  DiodeBackward diodebackward_13 (.in(not_2_out), .out(diodebackward_13_out));
  DiodeBackward diodebackward_14 (.in(not_3_out), .out(diodebackward_13_out));
  DiodeBackward diodebackward_15 (.in(not_3_out), .out(diodebackward_15_out));
  DiodeBackward diodebackward_16 (.in(Q_11), .out(diodebackward_15_out));
  DiodeBackward diodebackward_17 (.in(not_4_out), .out(diodebackward_17_out));
  DiodeBackward diodebackward_18 (.in(not_5_out), .out(diodebackward_17_out));
  DiodeBackward diodebackward_19 (.in(not_5_out), .out(diodebackward_19_out));
  DiodeBackward diodebackward_20 (.in(Q_12), .out(diodebackward_19_out));
  DiodeBackward diodebackward_21 (.in(not_6_out), .out(diodebackward_21_out));
  DiodeBackward diodebackward_22 (.in(not_7_out), .out(diodebackward_21_out));
  DiodeBackward diodebackward_23 (.in(not_7_out), .out(diodebackward_23_out));
  DiodeBackward diodebackward_24 (.in(Q_13), .out(diodebackward_23_out));
  PullUp pullup_5 (.out(diodebackward_9_out));
  not not_9 (not_9_out, diodebackward_9_out);
  PullUp pullup_6 (.out(diodebackward_11_out));
  not not_10 (not_10_out, diodebackward_11_out);
  PullUp pullup_7 (.out(diodebackward_13_out));
  not not_11 (not_11_out, diodebackward_13_out);
  PullUp pullup_8 (.out(diodebackward_15_out));
  not not_12 (not_12_out, diodebackward_15_out);
  PullUp pullup_9 (.out(diodebackward_17_out));
  not not_13 (not_13_out, diodebackward_17_out);
  PullUp pullup_10 (.out(diodebackward_19_out));
  not not_14 (not_14_out, diodebackward_19_out);
  PullUp pullup_11 (.out(diodebackward_21_out));
  not not_15 (not_15_out, diodebackward_21_out);
  PullUp pullup_12 (.out(diodebackward_23_out));
  not not_16 (not_16_out, diodebackward_23_out);
  DiodeBackward diodebackward_25 (.in(not_9_out), .out(diodebackward_25_out));
  DiodeBackward diodebackward_26 (.in(not_10_out), .out(diodebackward_25_out));
  DiodeBackward diodebackward_27 (.in(not_11_out), .out(diodebackward_27_out));
  DiodeBackward diodebackward_28 (.in(not_12_out), .out(diodebackward_27_out));
  DiodeBackward diodebackward_29 (.in(not_13_out), .out(diodebackward_29_out));
  DiodeBackward diodebackward_30 (.in(not_14_out), .out(diodebackward_29_out));
  DiodeBackward diodebackward_31 (.in(not_15_out), .out(diodebackward_31_out));
  DiodeBackward diodebackward_32 (.in(not_16_out), .out(diodebackward_31_out));
  PullUp pullup_13 (.out(diodebackward_25_out));
  not not_17 (not_17_out, diodebackward_25_out);
  PullUp pullup_14 (.out(diodebackward_27_out));
  not not_18 (not_18_out, diodebackward_27_out);
  PullUp pullup_15 (.out(diodebackward_29_out));
  not not_19 (not_19_out, diodebackward_29_out);
  PullUp pullup_16 (.out(diodebackward_31_out));
  not not_20 (not_20_out, diodebackward_31_out);
  not not_21 (not_21_out, nLD_COUNT);
  not not_22 (not_22_out, nLD_COUNT);
  not not_23 (not_23_out, nLD_COUNT);
  not not_24 (not_24_out, nLD_COUNT);
  PullUp pullup_17 (.out(pullup_17_out));
  DiodeBackward diodebackward_33 (.in(not_17_out), .out(pullup_17_out));
  DiodeBackward diodebackward_34 (.in(nLD_COUNT), .out(pullup_17_out));
  PullUp pullup_18 (.out(pullup_18_out));
  DiodeBackward diodebackward_35 (.in(not_21_out), .out(pullup_18_out));
  DiodeBackward diodebackward_36 (.in(D20), .out(pullup_18_out));
  PullUp pullup_19 (.out(pullup_19_out));
  DiodeBackward diodebackward_37 (.in(not_18_out), .out(pullup_19_out));
  DiodeBackward diodebackward_38 (.in(nLD_COUNT), .out(pullup_19_out));
  PullUp pullup_20 (.out(pullup_20_out));
  DiodeBackward diodebackward_39 (.in(not_22_out), .out(pullup_20_out));
  DiodeBackward diodebackward_40 (.in(D21), .out(pullup_20_out));
  PullUp pullup_21 (.out(pullup_21_out));
  DiodeBackward diodebackward_41 (.in(not_19_out), .out(pullup_21_out));
  DiodeBackward diodebackward_42 (.in(nLD_COUNT), .out(pullup_21_out));
  PullUp pullup_22 (.out(pullup_22_out));
  DiodeBackward diodebackward_43 (.in(not_23_out), .out(pullup_22_out));
  DiodeBackward diodebackward_44 (.in(D22), .out(pullup_22_out));
  PullUp pullup_23 (.out(pullup_23_out));
  DiodeBackward diodebackward_45 (.in(not_20_out), .out(pullup_23_out));
  DiodeBackward diodebackward_46 (.in(nLD_COUNT), .out(pullup_23_out));
  PullUp pullup_24 (.out(pullup_24_out));
  DiodeBackward diodebackward_47 (.in(not_24_out), .out(pullup_24_out));
  DiodeBackward diodebackward_48 (.in(D23), .out(pullup_24_out));
  not not_25 (not_25_out, pullup_17_out);
  not not_26 (not_26_out, pullup_18_out);
  not not_27 (not_27_out, pullup_19_out);
  not not_28 (not_28_out, pullup_20_out);
  not not_29 (not_29_out, pullup_21_out);
  not not_30 (not_30_out, pullup_22_out);
  not not_31 (not_31_out, pullup_23_out);
  not not_32 (not_32_out, pullup_24_out);
  PullUp pullup_25 (.out(pullup_25_out));
  DiodeBackward diodebackward_49 (.in(not_25_out), .out(pullup_25_out));
  DiodeBackward diodebackward_50 (.in(not_26_out), .out(pullup_25_out));
  PullUp pullup_26 (.out(pullup_26_out));
  DiodeBackward diodebackward_51 (.in(not_27_out), .out(pullup_26_out));
  DiodeBackward diodebackward_52 (.in(not_28_out), .out(pullup_26_out));
  PullUp pullup_27 (.out(pullup_27_out));
  DiodeBackward diodebackward_53 (.in(not_29_out), .out(pullup_27_out));
  DiodeBackward diodebackward_54 (.in(not_30_out), .out(pullup_27_out));
  PullUp pullup_28 (.out(pullup_28_out));
  DiodeBackward diodebackward_55 (.in(not_31_out), .out(pullup_28_out));
  DiodeBackward diodebackward_56 (.in(not_32_out), .out(pullup_28_out));
  not not_33 (not_33_out, pullup_25_out);
  not not_34 (not_34_out, pullup_26_out);
  not not_35 (not_35_out, pullup_27_out);
  not not_36 (not_36_out, pullup_28_out);
  PullUp pullup_29 (.out(pullup_29_out));
  not not_37 (not_37_out, pullup_29_out);
  DiodeBackward diodebackward_57 (.in(not_40_out), .out(pullup_29_out));
  DiodeBackward diodebackward_58 (.in(not_38_out), .out(pullup_29_out));
  PullUp pullup_30 (.out(pullup_30_out));
  DiodeBackward diodebackward_59 (.in(not_37_out), .out(pullup_30_out));
  not not_38 (not_38_out, pullup_30_out);
  DiodeBackward diodebackward_60 (.in(clk_7), .out(pullup_30_out));
  DiodeBackward diodebackward_61 (.in(RES), .out(pullup_30_out));
  PullUp pullup_31 (.out(pullup_31_out));
  DiodeBackward diodebackward_62 (.in(not_38_out), .out(pullup_31_out));
  not not_39 (not_39_out, pullup_31_out);
  DiodeBackward diodebackward_63 (.in(clk_7), .out(pullup_31_out));
  DiodeBackward diodebackward_64 (.in(not_40_out), .out(pullup_31_out));
  PullUp pullup_32 (.out(pullup_32_out));
  DiodeBackward diodebackward_65 (.in(not_39_out), .out(pullup_32_out));
  not not_40 (not_40_out, pullup_32_out);
  DiodeBackward diodebackward_66 (.in(not_33_out), .out(pullup_32_out));
  DiodeBackward diodebackward_67 (.in(RES), .out(pullup_32_out));
  PullUp pullup_33 (.out(pullup_33_out));
  not not_41 (not_41_out, pullup_33_out);
  DiodeBackward diodebackward_68 (.in(not_44_out), .out(pullup_33_out));
  DiodeBackward diodebackward_69 (.in(not_42_out), .out(pullup_33_out));
  PullUp pullup_34 (.out(pullup_34_out));
  DiodeBackward diodebackward_70 (.in(not_41_out), .out(pullup_34_out));
  not not_42 (not_42_out, pullup_34_out);
  DiodeBackward diodebackward_71 (.in(clk_7), .out(pullup_34_out));
  DiodeBackward diodebackward_72 (.in(RES), .out(pullup_34_out));
  PullUp pullup_35 (.out(pullup_35_out));
  DiodeBackward diodebackward_73 (.in(not_42_out), .out(pullup_35_out));
  not not_43 (not_43_out, pullup_35_out);
  DiodeBackward diodebackward_74 (.in(clk_7), .out(pullup_35_out));
  DiodeBackward diodebackward_75 (.in(not_44_out), .out(pullup_35_out));
  PullUp pullup_36 (.out(pullup_36_out));
  DiodeBackward diodebackward_76 (.in(not_43_out), .out(pullup_36_out));
  not not_44 (not_44_out, pullup_36_out);
  DiodeBackward diodebackward_77 (.in(not_34_out), .out(pullup_36_out));
  DiodeBackward diodebackward_78 (.in(RES), .out(pullup_36_out));
  PullUp pullup_37 (.out(pullup_37_out));
  not not_45 (not_45_out, pullup_37_out);
  DiodeBackward diodebackward_79 (.in(not_48_out), .out(pullup_37_out));
  DiodeBackward diodebackward_80 (.in(not_46_out), .out(pullup_37_out));
  PullUp pullup_38 (.out(pullup_38_out));
  DiodeBackward diodebackward_81 (.in(not_45_out), .out(pullup_38_out));
  not not_46 (not_46_out, pullup_38_out);
  DiodeBackward diodebackward_82 (.in(clk_7), .out(pullup_38_out));
  DiodeBackward diodebackward_83 (.in(RES), .out(pullup_38_out));
  PullUp pullup_39 (.out(pullup_39_out));
  DiodeBackward diodebackward_84 (.in(not_46_out), .out(pullup_39_out));
  not not_47 (not_47_out, pullup_39_out);
  DiodeBackward diodebackward_85 (.in(clk_7), .out(pullup_39_out));
  DiodeBackward diodebackward_86 (.in(not_48_out), .out(pullup_39_out));
  PullUp pullup_40 (.out(pullup_40_out));
  DiodeBackward diodebackward_87 (.in(not_47_out), .out(pullup_40_out));
  not not_48 (not_48_out, pullup_40_out);
  DiodeBackward diodebackward_88 (.in(not_35_out), .out(pullup_40_out));
  DiodeBackward diodebackward_89 (.in(RES), .out(pullup_40_out));
  PullUp pullup_41 (.out(pullup_41_out));
  not not_49 (not_49_out, pullup_41_out);
  DiodeBackward diodebackward_90 (.in(not_52_out), .out(pullup_41_out));
  DiodeBackward diodebackward_91 (.in(not_50_out), .out(pullup_41_out));
  PullUp pullup_42 (.out(pullup_42_out));
  DiodeBackward diodebackward_92 (.in(not_49_out), .out(pullup_42_out));
  not not_50 (not_50_out, pullup_42_out);
  DiodeBackward diodebackward_93 (.in(clk_7), .out(pullup_42_out));
  DiodeBackward diodebackward_94 (.in(RES), .out(pullup_42_out));
  PullUp pullup_43 (.out(pullup_43_out));
  DiodeBackward diodebackward_95 (.in(not_50_out), .out(pullup_43_out));
  not not_51 (not_51_out, pullup_43_out);
  DiodeBackward diodebackward_96 (.in(clk_7), .out(pullup_43_out));
  DiodeBackward diodebackward_97 (.in(not_52_out), .out(pullup_43_out));
  PullUp pullup_44 (.out(pullup_44_out));
  DiodeBackward diodebackward_98 (.in(not_51_out), .out(pullup_44_out));
  not not_52 (not_52_out, pullup_44_out);
  DiodeBackward diodebackward_99 (.in(not_36_out), .out(pullup_44_out));
  DiodeBackward diodebackward_100 (.in(RES), .out(pullup_44_out));
  DiodeBackward diodebackward_101 (.in(not_38_out), .out(diodebackward_101_out));
  DiodeBackward diodebackward_102 (.in(not_54_out), .out(diodebackward_101_out));
  DiodeBackward diodebackward_103 (.in(Q_10), .out(diodebackward_103_out));
  DiodeBackward diodebackward_104 (.in(not_39_out), .out(diodebackward_103_out));
  DiodeBackward diodebackward_105 (.in(RES), .out(diodebackward_103_out));
  DiodeBackward diodebackward_106 (.in(not_42_out), .out(diodebackward_106_out));
  DiodeBackward diodebackward_107 (.in(not_56_out), .out(diodebackward_106_out));
  DiodeBackward diodebackward_108 (.in(Q_11), .out(diodebackward_108_out));
  DiodeBackward diodebackward_109 (.in(not_43_out), .out(diodebackward_108_out));
  DiodeBackward diodebackward_110 (.in(RES), .out(diodebackward_108_out));
  DiodeBackward diodebackward_111 (.in(not_46_out), .out(diodebackward_111_out));
  DiodeBackward diodebackward_112 (.in(not_58_out), .out(diodebackward_111_out));
  DiodeBackward diodebackward_113 (.in(Q_12), .out(diodebackward_113_out));
  DiodeBackward diodebackward_114 (.in(not_47_out), .out(diodebackward_113_out));
  DiodeBackward diodebackward_115 (.in(RES), .out(diodebackward_113_out));
  DiodeBackward diodebackward_116 (.in(not_50_out), .out(diodebackward_116_out));
  DiodeBackward diodebackward_117 (.in(not_60_out), .out(diodebackward_116_out));
  DiodeBackward diodebackward_118 (.in(Q_13), .out(diodebackward_118_out));
  DiodeBackward diodebackward_119 (.in(not_51_out), .out(diodebackward_118_out));
  DiodeBackward diodebackward_120 (.in(RES), .out(diodebackward_118_out));
  PullUp pullup_45 (.out(diodebackward_101_out));
  not not_53 (Q_10, diodebackward_101_out);
  PullUp pullup_46 (.out(diodebackward_103_out));
  not not_54 (not_54_out, diodebackward_103_out);
  PullUp pullup_47 (.out(diodebackward_106_out));
  not not_55 (Q_11, diodebackward_106_out);
  PullUp pullup_48 (.out(diodebackward_108_out));
  not not_56 (not_56_out, diodebackward_108_out);
  PullUp pullup_49 (.out(diodebackward_111_out));
  not not_57 (Q_12, diodebackward_111_out);
  PullUp pullup_50 (.out(diodebackward_113_out));
  not not_58 (not_58_out, diodebackward_113_out);
  PullUp pullup_51 (.out(diodebackward_116_out));
  not not_59 (Q_13, diodebackward_116_out);
  PullUp pullup_52 (.out(diodebackward_118_out));
  not not_60 (not_60_out, diodebackward_118_out);
  Seven_Seg_Hex seven_seg_hex_1 (.d({Q_13, Q_12, Q_11, Q_10}), .dp(1'b0));
  DiodeBackward diodebackward_121 (.in(INC), .out(diodebackward_121_out));
  DiodeBackward diodebackward_122 (.in(Q_6), .out(diodebackward_121_out));
  DiodeBackward diodebackward_123 (.in(not_62_out), .out(diodebackward_123_out));
  DiodeBackward diodebackward_124 (.in(Q_7), .out(diodebackward_123_out));
  DiodeBackward diodebackward_125 (.in(not_64_out), .out(diodebackward_125_out));
  DiodeBackward diodebackward_126 (.in(Q_8), .out(diodebackward_125_out));
  DiodeBackward diodebackward_127 (.in(not_66_out), .out(diodebackward_127_out));
  DiodeBackward diodebackward_128 (.in(Q_9), .out(diodebackward_127_out));
  PullUp pullup_53 (.out(diodebackward_121_out));
  not not_61 (not_61_out, diodebackward_121_out);
  not not_62 (not_62_out, not_61_out);
  PullUp pullup_54 (.out(diodebackward_123_out));
  not not_63 (not_63_out, diodebackward_123_out);
  not not_64 (not_64_out, not_63_out);
  PullUp pullup_55 (.out(diodebackward_125_out));
  not not_65 (not_65_out, diodebackward_125_out);
  not not_66 (not_66_out, not_65_out);
  PullUp pullup_56 (.out(diodebackward_127_out));
  not not_67 (not_67_out, diodebackward_127_out);
  not not_68 (INC_t, not_67_out);
  PullUp pullup_57 (.out(pullup_57_out));
  DiodeBackward diodebackward_129 (.in(INC), .out(pullup_57_out));
  not not_69 (not_69_out, pullup_57_out);
  DiodeBackward diodebackward_130 (.in(not_61_out), .out(pullup_57_out));
  PullUp pullup_58 (.out(pullup_58_out));
  DiodeBackward diodebackward_131 (.in(not_61_out), .out(pullup_58_out));
  not not_70 (not_70_out, pullup_58_out);
  DiodeBackward diodebackward_132 (.in(Q_6), .out(pullup_58_out));
  PullUp pullup_59 (.out(pullup_59_out));
  DiodeBackward diodebackward_133 (.in(not_62_out), .out(pullup_59_out));
  not not_71 (not_71_out, pullup_59_out);
  DiodeBackward diodebackward_134 (.in(not_63_out), .out(pullup_59_out));
  PullUp pullup_60 (.out(pullup_60_out));
  DiodeBackward diodebackward_135 (.in(not_63_out), .out(pullup_60_out));
  not not_72 (not_72_out, pullup_60_out);
  DiodeBackward diodebackward_136 (.in(Q_7), .out(pullup_60_out));
  PullUp pullup_61 (.out(pullup_61_out));
  DiodeBackward diodebackward_137 (.in(not_64_out), .out(pullup_61_out));
  not not_73 (not_73_out, pullup_61_out);
  DiodeBackward diodebackward_138 (.in(not_65_out), .out(pullup_61_out));
  PullUp pullup_62 (.out(pullup_62_out));
  DiodeBackward diodebackward_139 (.in(not_65_out), .out(pullup_62_out));
  not not_74 (not_74_out, pullup_62_out);
  DiodeBackward diodebackward_140 (.in(Q_8), .out(pullup_62_out));
  PullUp pullup_63 (.out(pullup_63_out));
  DiodeBackward diodebackward_141 (.in(not_66_out), .out(pullup_63_out));
  not not_75 (not_75_out, pullup_63_out);
  DiodeBackward diodebackward_142 (.in(not_67_out), .out(pullup_63_out));
  PullUp pullup_64 (.out(pullup_64_out));
  DiodeBackward diodebackward_143 (.in(not_67_out), .out(pullup_64_out));
  not not_76 (not_76_out, pullup_64_out);
  DiodeBackward diodebackward_144 (.in(Q_9), .out(pullup_64_out));
  PullUp pullup_65 (.out(pullup_65_out));
  DiodeBackward diodebackward_145 (.in(not_69_out), .out(pullup_65_out));
  not not_77 (not_77_out, pullup_65_out);
  DiodeBackward diodebackward_146 (.in(not_70_out), .out(pullup_65_out));
  PullUp pullup_66 (.out(pullup_66_out));
  DiodeBackward diodebackward_147 (.in(not_71_out), .out(pullup_66_out));
  not not_78 (not_78_out, pullup_66_out);
  DiodeBackward diodebackward_148 (.in(not_72_out), .out(pullup_66_out));
  PullUp pullup_67 (.out(pullup_67_out));
  DiodeBackward diodebackward_149 (.in(not_73_out), .out(pullup_67_out));
  not not_79 (not_79_out, pullup_67_out);
  DiodeBackward diodebackward_150 (.in(not_74_out), .out(pullup_67_out));
  PullUp pullup_68 (.out(pullup_68_out));
  DiodeBackward diodebackward_151 (.in(not_75_out), .out(pullup_68_out));
  not not_80 (not_80_out, pullup_68_out);
  DiodeBackward diodebackward_152 (.in(not_76_out), .out(pullup_68_out));
  not not_81 (not_81_out, nLD_COUNT);
  not not_82 (not_82_out, nLD_COUNT);
  not not_83 (not_83_out, nLD_COUNT);
  not not_84 (not_84_out, nLD_COUNT);
  DiodeBackward diodebackward_153 (.in(not_77_out), .out(diodebackward_153_out));
  DiodeBackward diodebackward_154 (.in(nLD_COUNT), .out(diodebackward_153_out));
  DiodeBackward diodebackward_155 (.in(not_81_out), .out(diodebackward_155_out));
  DiodeBackward diodebackward_156 (.in(D16), .out(diodebackward_155_out));
  DiodeBackward diodebackward_157 (.in(not_78_out), .out(diodebackward_157_out));
  DiodeBackward diodebackward_158 (.in(nLD_COUNT), .out(diodebackward_157_out));
  DiodeBackward diodebackward_159 (.in(not_82_out), .out(diodebackward_159_out));
  DiodeBackward diodebackward_160 (.in(D17), .out(diodebackward_159_out));
  DiodeBackward diodebackward_161 (.in(not_79_out), .out(diodebackward_161_out));
  DiodeBackward diodebackward_162 (.in(nLD_COUNT), .out(diodebackward_161_out));
  DiodeBackward diodebackward_163 (.in(not_83_out), .out(diodebackward_163_out));
  DiodeBackward diodebackward_164 (.in(D18), .out(diodebackward_163_out));
  DiodeBackward diodebackward_165 (.in(not_80_out), .out(diodebackward_165_out));
  DiodeBackward diodebackward_166 (.in(nLD_COUNT), .out(diodebackward_165_out));
  DiodeBackward diodebackward_167 (.in(not_84_out), .out(diodebackward_167_out));
  DiodeBackward diodebackward_168 (.in(D19), .out(diodebackward_167_out));
  PullUp pullup_69 (.out(diodebackward_153_out));
  not not_85 (not_85_out, diodebackward_153_out);
  PullUp pullup_70 (.out(diodebackward_155_out));
  not not_86 (not_86_out, diodebackward_155_out);
  PullUp pullup_71 (.out(diodebackward_157_out));
  not not_87 (not_87_out, diodebackward_157_out);
  PullUp pullup_72 (.out(diodebackward_159_out));
  not not_88 (not_88_out, diodebackward_159_out);
  PullUp pullup_73 (.out(diodebackward_161_out));
  not not_89 (not_89_out, diodebackward_161_out);
  PullUp pullup_74 (.out(diodebackward_163_out));
  not not_90 (not_90_out, diodebackward_163_out);
  PullUp pullup_75 (.out(diodebackward_165_out));
  not not_91 (not_91_out, diodebackward_165_out);
  PullUp pullup_76 (.out(diodebackward_167_out));
  not not_92 (not_92_out, diodebackward_167_out);
  DiodeBackward diodebackward_169 (.in(not_85_out), .out(diodebackward_169_out));
  DiodeBackward diodebackward_170 (.in(not_86_out), .out(diodebackward_169_out));
  DiodeBackward diodebackward_171 (.in(not_87_out), .out(diodebackward_171_out));
  DiodeBackward diodebackward_172 (.in(not_88_out), .out(diodebackward_171_out));
  DiodeBackward diodebackward_173 (.in(not_89_out), .out(diodebackward_173_out));
  DiodeBackward diodebackward_174 (.in(not_90_out), .out(diodebackward_173_out));
  DiodeBackward diodebackward_175 (.in(not_91_out), .out(diodebackward_175_out));
  DiodeBackward diodebackward_176 (.in(not_92_out), .out(diodebackward_175_out));
  PullUp pullup_77 (.out(diodebackward_169_out));
  not not_93 (not_93_out, diodebackward_169_out);
  PullUp pullup_78 (.out(diodebackward_171_out));
  not not_94 (not_94_out, diodebackward_171_out);
  PullUp pullup_79 (.out(diodebackward_173_out));
  not not_95 (not_95_out, diodebackward_173_out);
  PullUp pullup_80 (.out(diodebackward_175_out));
  not not_96 (not_96_out, diodebackward_175_out);
  DiodeBackward diodebackward_177 (.in(A_10), .out(diodebackward_177_out));
  DiodeBackward diodebackward_178 (.in(not_98_out), .out(diodebackward_177_out));
  DiodeBackward diodebackward_179 (.in(B_10), .out(diodebackward_179_out));
  DiodeBackward diodebackward_180 (.in(not_98_out), .out(diodebackward_179_out));
  DiodeBackward diodebackward_181 (.in(Cin_6), .out(diodebackward_181_out));
  DiodeBackward diodebackward_182 (.in(not_98_out), .out(diodebackward_181_out));
  DiodeBackward diodebackward_183 (.in(A_10), .out(diodebackward_183_out));
  DiodeBackward diodebackward_184 (.in(B_10), .out(diodebackward_183_out));
  DiodeBackward diodebackward_185 (.in(Cin_6), .out(diodebackward_183_out));
  DiodeBackward diodebackward_186 (.in(A_10), .out(diodebackward_186_out));
  DiodeBackward diodebackward_187 (.in(B_10), .out(diodebackward_186_out));
  DiodeBackward diodebackward_188 (.in(A_10), .out(diodebackward_188_out));
  DiodeBackward diodebackward_189 (.in(Cin_6), .out(diodebackward_188_out));
  DiodeBackward diodebackward_190 (.in(B_10), .out(diodebackward_190_out));
  DiodeBackward diodebackward_191 (.in(Cin_6), .out(diodebackward_190_out));
  PullUp pullup_81 (.out(diodebackward_177_out));
  PullUp pullup_82 (.out(diodebackward_179_out));
  PullUp pullup_83 (.out(diodebackward_186_out));
  PullUp pullup_84 (.out(diodebackward_188_out));
  PullUp pullup_85 (.out(diodebackward_181_out));
  PullUp pullup_86 (.out(diodebackward_183_out));
  PullUp pullup_87 (.out(diodebackward_190_out));
  DiodeForward diodeforward_1 (.in(diodebackward_177_out), .out(diodeforward_1_out));
  DiodeForward diodeforward_2 (.in(diodebackward_179_out), .out(diodeforward_1_out));
  DiodeForward diodeforward_3 (.in(diodebackward_181_out), .out(diodeforward_1_out));
  DiodeForward diodeforward_4 (.in(diodebackward_183_out), .out(diodeforward_1_out));
  DiodeForward diodeforward_5 (.in(diodebackward_186_out), .out(diodeforward_5_out));
  DiodeForward diodeforward_6 (.in(diodebackward_188_out), .out(diodeforward_5_out));
  DiodeForward diodeforward_7 (.in(diodebackward_190_out), .out(diodeforward_5_out));
  PullDown pulldown_1 (.out(diodeforward_1_out));
  PullDown pulldown_2 (.out(diodeforward_5_out));
  not not_97 (not_97_out, diodeforward_1_out);
  not not_98 (not_98_out, diodeforward_5_out);
  PullUp pullup_88 (.out(pullup_88_out));
  DiodeBackward diodebackward_192 (.in(not_103_out), .out(pullup_88_out));
  DiodeBackward diodebackward_193 (.in(not_101_out), .out(pullup_88_out));
  PullUp pullup_89 (.out(pullup_89_out));
  DiodeBackward diodebackward_194 (.in(not_100_out), .out(pullup_89_out));
  DiodeBackward diodebackward_195 (.in(clk_6), .out(pullup_89_out));
  DiodeBackward diodebackward_196 (.in(RES), .out(pullup_89_out));
  PullUp pullup_90 (.out(pullup_90_out));
  DiodeBackward diodebackward_197 (.in(not_101_out), .out(pullup_90_out));
  DiodeBackward diodebackward_198 (.in(clk_6), .out(pullup_90_out));
  DiodeBackward diodebackward_199 (.in(not_103_out), .out(pullup_90_out));
  PullUp pullup_91 (.out(pullup_91_out));
  DiodeBackward diodebackward_200 (.in(not_102_out), .out(pullup_91_out));
  DiodeBackward diodebackward_201 (.in(not_93_out), .out(pullup_91_out));
  DiodeBackward diodebackward_202 (.in(RES), .out(pullup_91_out));
  PullUp pullup_92 (.out(pullup_92_out));
  DiodeBackward diodebackward_203 (.in(not_107_out), .out(pullup_92_out));
  DiodeBackward diodebackward_204 (.in(not_105_out), .out(pullup_92_out));
  PullUp pullup_93 (.out(pullup_93_out));
  DiodeBackward diodebackward_205 (.in(not_104_out), .out(pullup_93_out));
  DiodeBackward diodebackward_206 (.in(clk_6), .out(pullup_93_out));
  DiodeBackward diodebackward_207 (.in(RES), .out(pullup_93_out));
  PullUp pullup_94 (.out(pullup_94_out));
  DiodeBackward diodebackward_208 (.in(not_105_out), .out(pullup_94_out));
  DiodeBackward diodebackward_209 (.in(clk_6), .out(pullup_94_out));
  DiodeBackward diodebackward_210 (.in(not_107_out), .out(pullup_94_out));
  PullUp pullup_95 (.out(pullup_95_out));
  DiodeBackward diodebackward_211 (.in(not_106_out), .out(pullup_95_out));
  DiodeBackward diodebackward_212 (.in(not_94_out), .out(pullup_95_out));
  DiodeBackward diodebackward_213 (.in(RES), .out(pullup_95_out));
  PullUp pullup_96 (.out(pullup_96_out));
  DiodeBackward diodebackward_214 (.in(not_111_out), .out(pullup_96_out));
  DiodeBackward diodebackward_215 (.in(not_109_out), .out(pullup_96_out));
  PullUp pullup_97 (.out(pullup_97_out));
  DiodeBackward diodebackward_216 (.in(not_108_out), .out(pullup_97_out));
  DiodeBackward diodebackward_217 (.in(clk_6), .out(pullup_97_out));
  DiodeBackward diodebackward_218 (.in(RES), .out(pullup_97_out));
  PullUp pullup_98 (.out(pullup_98_out));
  DiodeBackward diodebackward_219 (.in(not_109_out), .out(pullup_98_out));
  DiodeBackward diodebackward_220 (.in(clk_6), .out(pullup_98_out));
  DiodeBackward diodebackward_221 (.in(not_111_out), .out(pullup_98_out));
  PullUp pullup_99 (.out(pullup_99_out));
  DiodeBackward diodebackward_222 (.in(not_110_out), .out(pullup_99_out));
  DiodeBackward diodebackward_223 (.in(not_95_out), .out(pullup_99_out));
  DiodeBackward diodebackward_224 (.in(RES), .out(pullup_99_out));
  PullUp pullup_100 (.out(pullup_100_out));
  DiodeBackward diodebackward_225 (.in(not_115_out), .out(pullup_100_out));
  DiodeBackward diodebackward_226 (.in(not_113_out), .out(pullup_100_out));
  PullUp pullup_101 (.out(pullup_101_out));
  DiodeBackward diodebackward_227 (.in(not_112_out), .out(pullup_101_out));
  DiodeBackward diodebackward_228 (.in(clk_6), .out(pullup_101_out));
  DiodeBackward diodebackward_229 (.in(RES), .out(pullup_101_out));
  PullUp pullup_102 (.out(pullup_102_out));
  DiodeBackward diodebackward_230 (.in(not_113_out), .out(pullup_102_out));
  DiodeBackward diodebackward_231 (.in(clk_6), .out(pullup_102_out));
  DiodeBackward diodebackward_232 (.in(not_115_out), .out(pullup_102_out));
  PullUp pullup_103 (.out(pullup_103_out));
  DiodeBackward diodebackward_233 (.in(not_114_out), .out(pullup_103_out));
  DiodeBackward diodebackward_234 (.in(not_96_out), .out(pullup_103_out));
  DiodeBackward diodebackward_235 (.in(RES), .out(pullup_103_out));
  not not_99 (Sum_3, not_97_out);
  not not_100 (not_100_out, pullup_88_out);
  not not_101 (not_101_out, pullup_89_out);
  not not_102 (not_102_out, pullup_90_out);
  not not_103 (not_103_out, pullup_91_out);
  not not_104 (not_104_out, pullup_92_out);
  not not_105 (not_105_out, pullup_93_out);
  not not_106 (not_106_out, pullup_94_out);
  not not_107 (not_107_out, pullup_95_out);
  not not_108 (not_108_out, pullup_96_out);
  not not_109 (not_109_out, pullup_97_out);
  not not_110 (not_110_out, pullup_98_out);
  not not_111 (not_111_out, pullup_99_out);
  not not_112 (not_112_out, pullup_100_out);
  not not_113 (not_113_out, pullup_101_out);
  not not_114 (not_114_out, pullup_102_out);
  not not_115 (not_115_out, pullup_103_out);
  not not_116 (Cout_2, not_98_out);
  PullUp pullup_104 (.out(pullup_104_out));
  DiodeBackward diodebackward_236 (.in(not_101_out), .out(pullup_104_out));
  not not_117 (Q_6, pullup_104_out);
  DiodeBackward diodebackward_237 (.in(not_118_out), .out(pullup_104_out));
  PullUp pullup_105 (.out(pullup_105_out));
  DiodeBackward diodebackward_238 (.in(Q_6), .out(pullup_105_out));
  not not_118 (not_118_out, pullup_105_out);
  DiodeBackward diodebackward_239 (.in(not_102_out), .out(pullup_105_out));
  DiodeBackward diodebackward_240 (.in(RES), .out(pullup_105_out));
  PullUp pullup_106 (.out(pullup_106_out));
  DiodeBackward diodebackward_241 (.in(not_105_out), .out(pullup_106_out));
  not not_119 (Q_7, pullup_106_out);
  DiodeBackward diodebackward_242 (.in(not_120_out), .out(pullup_106_out));
  PullUp pullup_107 (.out(pullup_107_out));
  DiodeBackward diodebackward_243 (.in(Q_7), .out(pullup_107_out));
  not not_120 (not_120_out, pullup_107_out);
  DiodeBackward diodebackward_244 (.in(not_106_out), .out(pullup_107_out));
  DiodeBackward diodebackward_245 (.in(RES), .out(pullup_107_out));
  PullUp pullup_108 (.out(pullup_108_out));
  DiodeBackward diodebackward_246 (.in(not_109_out), .out(pullup_108_out));
  not not_121 (Q_8, pullup_108_out);
  DiodeBackward diodebackward_247 (.in(not_122_out), .out(pullup_108_out));
  PullUp pullup_109 (.out(pullup_109_out));
  DiodeBackward diodebackward_248 (.in(Q_8), .out(pullup_109_out));
  not not_122 (not_122_out, pullup_109_out);
  DiodeBackward diodebackward_249 (.in(not_110_out), .out(pullup_109_out));
  DiodeBackward diodebackward_250 (.in(RES), .out(pullup_109_out));
  PullUp pullup_110 (.out(pullup_110_out));
  DiodeBackward diodebackward_251 (.in(not_113_out), .out(pullup_110_out));
  not not_123 (Q_9, pullup_110_out);
  DiodeBackward diodebackward_252 (.in(not_124_out), .out(pullup_110_out));
  PullUp pullup_111 (.out(pullup_111_out));
  DiodeBackward diodebackward_253 (.in(Q_9), .out(pullup_111_out));
  not not_124 (not_124_out, pullup_111_out);
  DiodeBackward diodebackward_254 (.in(not_114_out), .out(pullup_111_out));
  DiodeBackward diodebackward_255 (.in(RES), .out(pullup_111_out));
  Seven_Seg_Hex seven_seg_hex_2 (.d({Q_9, Q_8, Q_7, Q_6}), .dp(1'b0));
  DiodeBackward diodebackward_256 (.in(nQ0), .out(diodebackward_256_out));
  DiodeBackward diodebackward_257 (.in(nQ1), .out(diodebackward_256_out));
  DiodeBackward diodebackward_258 (.in(nQ2), .out(diodebackward_256_out));
  DiodeBackward diodebackward_259 (.in(D0_2), .out(diodebackward_256_out));
  DiodeBackward diodebackward_260 (.in(Q0), .out(diodebackward_260_out));
  DiodeBackward diodebackward_261 (.in(nQ1), .out(diodebackward_260_out));
  DiodeBackward diodebackward_262 (.in(nQ2), .out(diodebackward_260_out));
  DiodeBackward diodebackward_263 (.in(D1_2), .out(diodebackward_260_out));
  DiodeBackward diodebackward_264 (.in(nQ0), .out(diodebackward_264_out));
  DiodeBackward diodebackward_265 (.in(Q1), .out(diodebackward_264_out));
  DiodeBackward diodebackward_266 (.in(nQ2), .out(diodebackward_264_out));
  DiodeBackward diodebackward_267 (.in(D2_2), .out(diodebackward_264_out));
  DiodeBackward diodebackward_268 (.in(Q0), .out(diodebackward_268_out));
  DiodeBackward diodebackward_269 (.in(Q1), .out(diodebackward_268_out));
  DiodeBackward diodebackward_270 (.in(nQ2), .out(diodebackward_268_out));
  DiodeBackward diodebackward_271 (.in(D3_2), .out(diodebackward_268_out));
  DiodeBackward diodebackward_272 (.in(nQ0), .out(diodebackward_272_out));
  DiodeBackward diodebackward_273 (.in(nQ1), .out(diodebackward_272_out));
  DiodeBackward diodebackward_274 (.in(Q2), .out(diodebackward_272_out));
  DiodeBackward diodebackward_275 (.in(D4_2), .out(diodebackward_272_out));
  DiodeBackward diodebackward_276 (.in(Q0), .out(diodebackward_276_out));
  DiodeBackward diodebackward_277 (.in(nQ1), .out(diodebackward_276_out));
  DiodeBackward diodebackward_278 (.in(Q2), .out(diodebackward_276_out));
  DiodeBackward diodebackward_279 (.in(D5_2), .out(diodebackward_276_out));
  DiodeBackward diodebackward_280 (.in(nQ0), .out(diodebackward_280_out));
  DiodeBackward diodebackward_281 (.in(Q1), .out(diodebackward_280_out));
  DiodeBackward diodebackward_282 (.in(Q2), .out(diodebackward_280_out));
  DiodeBackward diodebackward_283 (.in(D6_2), .out(diodebackward_280_out));
  DiodeBackward diodebackward_284 (.in(Q0), .out(diodebackward_284_out));
  DiodeBackward diodebackward_285 (.in(Q1), .out(diodebackward_284_out));
  DiodeBackward diodebackward_286 (.in(Q2), .out(diodebackward_284_out));
  DiodeBackward diodebackward_287 (.in(D7_2), .out(diodebackward_284_out));
  DiodeBackward diodebackward_288 (.in(nQ0), .out(diodebackward_288_out));
  DiodeBackward diodebackward_289 (.in(nQ1), .out(diodebackward_288_out));
  DiodeBackward diodebackward_290 (.in(nQ2), .out(diodebackward_288_out));
  DiodeBackward diodebackward_291 (.in(D8), .out(diodebackward_288_out));
  DiodeBackward diodebackward_292 (.in(Q0), .out(diodebackward_292_out));
  DiodeBackward diodebackward_293 (.in(nQ1), .out(diodebackward_292_out));
  DiodeBackward diodebackward_294 (.in(nQ2), .out(diodebackward_292_out));
  DiodeBackward diodebackward_295 (.in(D9), .out(diodebackward_292_out));
  DiodeBackward diodebackward_296 (.in(nQ0), .out(diodebackward_296_out));
  DiodeBackward diodebackward_297 (.in(Q1), .out(diodebackward_296_out));
  DiodeBackward diodebackward_298 (.in(nQ2), .out(diodebackward_296_out));
  DiodeBackward diodebackward_299 (.in(D10), .out(diodebackward_296_out));
  DiodeBackward diodebackward_300 (.in(Q0), .out(diodebackward_300_out));
  DiodeBackward diodebackward_301 (.in(Q1), .out(diodebackward_300_out));
  DiodeBackward diodebackward_302 (.in(nQ2), .out(diodebackward_300_out));
  DiodeBackward diodebackward_303 (.in(D11), .out(diodebackward_300_out));
  DiodeBackward diodebackward_304 (.in(nQ0), .out(diodebackward_304_out));
  DiodeBackward diodebackward_305 (.in(nQ1), .out(diodebackward_304_out));
  DiodeBackward diodebackward_306 (.in(Q2), .out(diodebackward_304_out));
  DiodeBackward diodebackward_307 (.in(D12), .out(diodebackward_304_out));
  DiodeBackward diodebackward_308 (.in(Q0), .out(diodebackward_308_out));
  DiodeBackward diodebackward_309 (.in(nQ1), .out(diodebackward_308_out));
  DiodeBackward diodebackward_310 (.in(Q2), .out(diodebackward_308_out));
  DiodeBackward diodebackward_311 (.in(D13), .out(diodebackward_308_out));
  DiodeBackward diodebackward_312 (.in(nQ0), .out(diodebackward_312_out));
  DiodeBackward diodebackward_313 (.in(Q1), .out(diodebackward_312_out));
  DiodeBackward diodebackward_314 (.in(Q2), .out(diodebackward_312_out));
  DiodeBackward diodebackward_315 (.in(D14), .out(diodebackward_312_out));
  DiodeBackward diodebackward_316 (.in(Q0), .out(diodebackward_316_out));
  DiodeBackward diodebackward_317 (.in(Q1), .out(diodebackward_316_out));
  DiodeBackward diodebackward_318 (.in(Q2), .out(diodebackward_316_out));
  DiodeBackward diodebackward_319 (.in(D15), .out(diodebackward_316_out));
  PullUp pullup_112 (.out(diodebackward_256_out));
  not not_125 (not_125_out, diodebackward_256_out);
  PullUp pullup_113 (.out(diodebackward_260_out));
  not not_126 (not_126_out, diodebackward_260_out);
  PullUp pullup_114 (.out(diodebackward_264_out));
  not not_127 (not_127_out, diodebackward_264_out);
  PullUp pullup_115 (.out(diodebackward_268_out));
  not not_128 (not_128_out, diodebackward_268_out);
  PullUp pullup_116 (.out(diodebackward_272_out));
  not not_129 (not_129_out, diodebackward_272_out);
  PullUp pullup_117 (.out(diodebackward_276_out));
  not not_130 (not_130_out, diodebackward_276_out);
  PullUp pullup_118 (.out(diodebackward_280_out));
  not not_131 (not_131_out, diodebackward_280_out);
  PullUp pullup_119 (.out(diodebackward_284_out));
  not not_132 (not_132_out, diodebackward_284_out);
  PullUp pullup_120 (.out(diodebackward_288_out));
  not not_133 (not_133_out, diodebackward_288_out);
  PullUp pullup_121 (.out(diodebackward_292_out));
  not not_134 (not_134_out, diodebackward_292_out);
  PullUp pullup_122 (.out(diodebackward_296_out));
  not not_135 (not_135_out, diodebackward_296_out);
  PullUp pullup_123 (.out(diodebackward_300_out));
  not not_136 (not_136_out, diodebackward_300_out);
  PullUp pullup_124 (.out(diodebackward_304_out));
  not not_137 (not_137_out, diodebackward_304_out);
  PullUp pullup_125 (.out(diodebackward_308_out));
  not not_138 (not_138_out, diodebackward_308_out);
  PullUp pullup_126 (.out(diodebackward_312_out));
  not not_139 (not_139_out, diodebackward_312_out);
  PullUp pullup_127 (.out(diodebackward_316_out));
  not not_140 (not_140_out, diodebackward_316_out);
  DiodeBackward diodebackward_320 (.in(not_125_out), .out(diodebackward_320_out));
  DiodeBackward diodebackward_321 (.in(not_126_out), .out(diodebackward_320_out));
  DiodeBackward diodebackward_322 (.in(not_127_out), .out(diodebackward_320_out));
  DiodeBackward diodebackward_323 (.in(not_128_out), .out(diodebackward_320_out));
  DiodeBackward diodebackward_324 (.in(not_129_out), .out(diodebackward_320_out));
  DiodeBackward diodebackward_325 (.in(not_130_out), .out(diodebackward_320_out));
  DiodeBackward diodebackward_326 (.in(not_131_out), .out(diodebackward_320_out));
  DiodeBackward diodebackward_327 (.in(not_132_out), .out(diodebackward_320_out));
  DiodeBackward diodebackward_328 (.in(not_133_out), .out(diodebackward_328_out));
  DiodeBackward diodebackward_329 (.in(not_134_out), .out(diodebackward_328_out));
  DiodeBackward diodebackward_330 (.in(not_135_out), .out(diodebackward_328_out));
  DiodeBackward diodebackward_331 (.in(not_136_out), .out(diodebackward_328_out));
  DiodeBackward diodebackward_332 (.in(not_137_out), .out(diodebackward_328_out));
  DiodeBackward diodebackward_333 (.in(not_138_out), .out(diodebackward_328_out));
  DiodeBackward diodebackward_334 (.in(not_139_out), .out(diodebackward_328_out));
  DiodeBackward diodebackward_335 (.in(not_140_out), .out(diodebackward_328_out));
  PullUp pullup_128 (.out(diodebackward_320_out));
  not not_141 (not_141_out, diodebackward_320_out);
  PullUp pullup_129 (.out(diodebackward_328_out));
  not not_142 (not_142_out, diodebackward_328_out);
  DiodeBackward diodebackward_336 (.in(not_141_out), .out(diodebackward_336_out));
  DiodeBackward diodebackward_337 (.in(nQ3), .out(diodebackward_336_out));
  DiodeBackward diodebackward_338 (.in(Q3), .out(diodebackward_338_out));
  DiodeBackward diodebackward_339 (.in(not_142_out), .out(diodebackward_338_out));
  PullUp pullup_130 (.out(diodebackward_336_out));
  not not_143 (not_143_out, diodebackward_336_out);
  PullUp pullup_131 (.out(diodebackward_338_out));
  not not_144 (not_144_out, diodebackward_338_out);
  DiodeBackward diodebackward_340 (.in(not_143_out), .out(diodebackward_340_out));
  DiodeBackward diodebackward_341 (.in(not_144_out), .out(diodebackward_340_out));
  PullUp pullup_132 (.out(diodebackward_340_out));
  not not_145 (out_138, diodebackward_340_out);
  Seven_Seg_Hex seven_seg_hex_3 (.d({A15, A14, A13, A12}), .dp(1'b0));
  Seven_Seg_Hex seven_seg_hex_4 (.d({A11, A10, A9, A8}), .dp(1'b0));
  PullUp pullup_133 (.out(pullup_133_out));
  DiodeBackward diodebackward_342 (.in(I0_4), .out(pullup_133_out));
  not not_146 (not_146_out, pullup_133_out);
  DiodeBackward diodebackward_343 (.in(A0_3), .out(pullup_133_out));
  PullUp pullup_134 (.out(pullup_134_out));
  DiodeBackward diodebackward_344 (.in(I1_4), .out(pullup_134_out));
  not not_147 (not_147_out, pullup_134_out);
  DiodeBackward diodebackward_345 (.in(B0_3), .out(pullup_134_out));
  PullUp pullup_135 (.out(pullup_135_out));
  DiodeBackward diodebackward_346 (.in(I0_4), .out(pullup_135_out));
  not not_148 (not_148_out, pullup_135_out);
  DiodeBackward diodebackward_347 (.in(A1_3), .out(pullup_135_out));
  PullUp pullup_136 (.out(pullup_136_out));
  DiodeBackward diodebackward_348 (.in(I1_4), .out(pullup_136_out));
  not not_149 (not_149_out, pullup_136_out);
  DiodeBackward diodebackward_349 (.in(B1_3), .out(pullup_136_out));
  PullUp pullup_137 (.out(pullup_137_out));
  DiodeBackward diodebackward_350 (.in(I0_4), .out(pullup_137_out));
  not not_150 (not_150_out, pullup_137_out);
  DiodeBackward diodebackward_351 (.in(A2_3), .out(pullup_137_out));
  PullUp pullup_138 (.out(pullup_138_out));
  DiodeBackward diodebackward_352 (.in(I1_4), .out(pullup_138_out));
  not not_151 (not_151_out, pullup_138_out);
  DiodeBackward diodebackward_353 (.in(B2_3), .out(pullup_138_out));
  PullUp pullup_139 (.out(pullup_139_out));
  DiodeBackward diodebackward_354 (.in(I0_4), .out(pullup_139_out));
  not not_152 (not_152_out, pullup_139_out);
  DiodeBackward diodebackward_355 (.in(A3_3), .out(pullup_139_out));
  PullUp pullup_140 (.out(pullup_140_out));
  DiodeBackward diodebackward_356 (.in(I1_4), .out(pullup_140_out));
  not not_153 (not_153_out, pullup_140_out);
  DiodeBackward diodebackward_357 (.in(B3_3), .out(pullup_140_out));
  LED led_1 (.in(out_138));
  Seven_Seg_Hex seven_seg_hex_5 (.d({A7, A6, A5, A4}), .dp(1'b0));
  Seven_Seg_Hex seven_seg_hex_6 (.d({A3_t, A2_t, A1_t, A0_t}), .dp(1'b0));
  not not_154 (not_154_out, D_5);
  PullUp pullup_141 (.out(pullup_141_out));
  DiodeBackward diodebackward_358 (.in(not_146_out), .out(pullup_141_out));
  not not_155 (F0, pullup_141_out);
  DiodeBackward diodebackward_359 (.in(not_147_out), .out(pullup_141_out));
  PullUp pullup_142 (.out(pullup_142_out));
  DiodeBackward diodebackward_360 (.in(not_148_out), .out(pullup_142_out));
  not not_156 (F1, pullup_142_out);
  DiodeBackward diodebackward_361 (.in(not_149_out), .out(pullup_142_out));
  PullUp pullup_143 (.out(pullup_143_out));
  DiodeBackward diodebackward_362 (.in(not_150_out), .out(pullup_143_out));
  not not_157 (F2, pullup_143_out);
  DiodeBackward diodebackward_363 (.in(not_151_out), .out(pullup_143_out));
  PullUp pullup_144 (.out(pullup_144_out));
  DiodeBackward diodebackward_364 (.in(not_152_out), .out(pullup_144_out));
  not not_158 (F3, pullup_144_out);
  DiodeBackward diodebackward_365 (.in(not_153_out), .out(pullup_144_out));
  PullUp pullup_145 (.out(pullup_145_out));
  DiodeBackward diodebackward_366 (.in(CLK_8), .out(pullup_145_out));
  DiodeBackward diodebackward_367 (.in(D_5), .out(pullup_145_out));
  PullUp pullup_146 (.out(pullup_146_out));
  DiodeBackward diodebackward_368 (.in(not_154_out), .out(pullup_146_out));
  DiodeBackward diodebackward_369 (.in(CLK_8), .out(pullup_146_out));
  PullUp pullup_147 (.out(pullup_147_out));
  DiodeBackward diodebackward_370 (.in(not_168_out), .out(pullup_147_out));
  DiodeBackward diodebackward_371 (.in(not_166_out), .out(pullup_147_out));
  PullUp pullup_148 (.out(pullup_148_out));
  DiodeBackward diodebackward_372 (.in(not_165_out), .out(pullup_148_out));
  DiodeBackward diodebackward_373 (.in(CLK_4), .out(pullup_148_out));
  DiodeBackward diodebackward_374 (.in(nRES), .out(pullup_148_out));
  PullUp pullup_149 (.out(pullup_149_out));
  DiodeBackward diodebackward_375 (.in(not_166_out), .out(pullup_149_out));
  DiodeBackward diodebackward_376 (.in(CLK_4), .out(pullup_149_out));
  DiodeBackward diodebackward_377 (.in(not_168_out), .out(pullup_149_out));
  PullUp pullup_150 (.out(pullup_150_out));
  DiodeBackward diodebackward_378 (.in(not_167_out), .out(pullup_150_out));
  DiodeBackward diodebackward_379 (.in(Sum_t), .out(pullup_150_out));
  DiodeBackward diodebackward_380 (.in(nRES), .out(pullup_150_out));
  PullUp pullup_151 (.out(pullup_151_out));
  DiodeBackward diodebackward_381 (.in(not_172_out), .out(pullup_151_out));
  DiodeBackward diodebackward_382 (.in(not_170_out), .out(pullup_151_out));
  PullUp pullup_152 (.out(pullup_152_out));
  DiodeBackward diodebackward_383 (.in(not_169_out), .out(pullup_152_out));
  DiodeBackward diodebackward_384 (.in(CLK_4), .out(pullup_152_out));
  DiodeBackward diodebackward_385 (.in(nRES), .out(pullup_152_out));
  PullUp pullup_153 (.out(pullup_153_out));
  DiodeBackward diodebackward_386 (.in(not_170_out), .out(pullup_153_out));
  DiodeBackward diodebackward_387 (.in(CLK_4), .out(pullup_153_out));
  DiodeBackward diodebackward_388 (.in(not_172_out), .out(pullup_153_out));
  PullUp pullup_154 (.out(pullup_154_out));
  DiodeBackward diodebackward_389 (.in(not_171_out), .out(pullup_154_out));
  DiodeBackward diodebackward_390 (.in(nQ0), .out(pullup_154_out));
  DiodeBackward diodebackward_391 (.in(nRES), .out(pullup_154_out));
  not not_159 (not_159_out, pullup_145_out);
  not not_160 (not_160_out, pullup_146_out);
  not not_161 (not_161_out, CLK_8);
  not not_162 (not_162_out, S0_2);
  not not_163 (not_163_out, S1_2);
  not not_164 (not_164_out, S2);
  not not_165 (not_165_out, pullup_147_out);
  not not_166 (not_166_out, pullup_148_out);
  not not_167 (not_167_out, pullup_149_out);
  not not_168 (not_168_out, pullup_150_out);
  not not_169 (not_169_out, pullup_151_out);
  not not_170 (not_170_out, pullup_152_out);
  not not_171 (not_171_out, pullup_153_out);
  not not_172 (not_172_out, pullup_154_out);
  DiodeBackward diodebackward_392 (.in(not_159_out), .out(diodebackward_392_out));
  DiodeBackward diodebackward_393 (.in(not_174_out), .out(diodebackward_392_out));
  DiodeBackward diodebackward_394 (.in(not_173_out), .out(diodebackward_394_out));
  DiodeBackward diodebackward_395 (.in(not_160_out), .out(diodebackward_394_out));
  PullUp pullup_155 (.out(pullup_155_out));
  DiodeBackward diodebackward_396 (.in(not_166_out), .out(pullup_155_out));
  DiodeBackward diodebackward_397 (.in(not_176_out), .out(pullup_155_out));
  PullUp pullup_156 (.out(pullup_156_out));
  DiodeBackward diodebackward_398 (.in(A15), .out(pullup_156_out));
  DiodeBackward diodebackward_399 (.in(not_167_out), .out(pullup_156_out));
  DiodeBackward diodebackward_400 (.in(nRES), .out(pullup_156_out));
  Seven_Seg_Hex seven_seg_hex_7 (.d({Q3, Q2, Q1, Q0}), .dp(1'b0));
  PullUp pullup_157 (.out(pullup_157_out));
  DiodeBackward diodebackward_401 (.in(not_170_out), .out(pullup_157_out));
  DiodeBackward diodebackward_402 (.in(nQ0), .out(pullup_157_out));
  PullUp pullup_158 (.out(pullup_158_out));
  DiodeBackward diodebackward_403 (.in(Q0), .out(pullup_158_out));
  DiodeBackward diodebackward_404 (.in(not_171_out), .out(pullup_158_out));
  DiodeBackward diodebackward_405 (.in(nRES), .out(pullup_158_out));
  PullUp pullup_159 (.out(diodebackward_392_out));
  not not_173 (not_173_out, diodebackward_392_out);
  PullUp pullup_160 (.out(diodebackward_394_out));
  not not_174 (not_174_out, diodebackward_394_out);
  PullUp pullup_161 (.out(pullup_161_out));
  DiodeBackward diodebackward_406 (.in(not_162_out), .out(pullup_161_out));
  DiodeBackward diodebackward_407 (.in(not_163_out), .out(pullup_161_out));
  DiodeBackward diodebackward_408 (.in(not_164_out), .out(pullup_161_out));
  DiodeBackward diodebackward_409 (.in(D0), .out(pullup_161_out));
  PullUp pullup_162 (.out(pullup_162_out));
  DiodeBackward diodebackward_410 (.in(S0_2), .out(pullup_162_out));
  DiodeBackward diodebackward_411 (.in(not_163_out), .out(pullup_162_out));
  DiodeBackward diodebackward_412 (.in(not_164_out), .out(pullup_162_out));
  DiodeBackward diodebackward_413 (.in(D1), .out(pullup_162_out));
  PullUp pullup_163 (.out(pullup_163_out));
  DiodeBackward diodebackward_414 (.in(not_162_out), .out(pullup_163_out));
  DiodeBackward diodebackward_415 (.in(S1_2), .out(pullup_163_out));
  DiodeBackward diodebackward_416 (.in(not_164_out), .out(pullup_163_out));
  DiodeBackward diodebackward_417 (.in(D2), .out(pullup_163_out));
  PullUp pullup_164 (.out(pullup_164_out));
  DiodeBackward diodebackward_418 (.in(S0_2), .out(pullup_164_out));
  DiodeBackward diodebackward_419 (.in(S1_2), .out(pullup_164_out));
  DiodeBackward diodebackward_420 (.in(not_164_out), .out(pullup_164_out));
  DiodeBackward diodebackward_421 (.in(D3), .out(pullup_164_out));
  PullUp pullup_165 (.out(pullup_165_out));
  DiodeBackward diodebackward_422 (.in(not_162_out), .out(pullup_165_out));
  DiodeBackward diodebackward_423 (.in(not_163_out), .out(pullup_165_out));
  DiodeBackward diodebackward_424 (.in(S2), .out(pullup_165_out));
  DiodeBackward diodebackward_425 (.in(D4), .out(pullup_165_out));
  PullUp pullup_166 (.out(pullup_166_out));
  DiodeBackward diodebackward_426 (.in(S0_2), .out(pullup_166_out));
  DiodeBackward diodebackward_427 (.in(not_163_out), .out(pullup_166_out));
  DiodeBackward diodebackward_428 (.in(S2), .out(pullup_166_out));
  DiodeBackward diodebackward_429 (.in(D5), .out(pullup_166_out));
  PullUp pullup_167 (.out(pullup_167_out));
  DiodeBackward diodebackward_430 (.in(not_162_out), .out(pullup_167_out));
  DiodeBackward diodebackward_431 (.in(S1_2), .out(pullup_167_out));
  DiodeBackward diodebackward_432 (.in(S2), .out(pullup_167_out));
  DiodeBackward diodebackward_433 (.in(D6), .out(pullup_167_out));
  PullUp pullup_168 (.out(pullup_168_out));
  DiodeBackward diodebackward_434 (.in(S0_2), .out(pullup_168_out));
  DiodeBackward diodebackward_435 (.in(S1_2), .out(pullup_168_out));
  DiodeBackward diodebackward_436 (.in(S2), .out(pullup_168_out));
  DiodeBackward diodebackward_437 (.in(D7), .out(pullup_168_out));
  not not_175 (A15, pullup_155_out);
  not not_176 (not_176_out, pullup_156_out);
  not not_177 (Q0, pullup_157_out);
  not not_178 (nQ0, pullup_158_out);
  not not_179 (not_179_out, pullup_161_out);
  not not_180 (not_180_out, pullup_162_out);
  not not_181 (not_181_out, pullup_163_out);
  not not_182 (not_182_out, pullup_164_out);
  not not_183 (not_183_out, pullup_165_out);
  not not_184 (not_184_out, pullup_166_out);
  not not_185 (not_185_out, pullup_167_out);
  not not_186 (not_186_out, pullup_168_out);
  LED Q15 (.in(A15));
  LED u_Q0 (.in(Q0));
  DiodeBackward diodebackward_438 (.in(not_190_out), .out(diodebackward_438_out));
  DiodeBackward diodebackward_439 (.in(not_188_out), .out(diodebackward_438_out));
  DiodeBackward diodebackward_440 (.in(not_187_out), .out(diodebackward_440_out));
  DiodeBackward diodebackward_441 (.in(nQ0), .out(diodebackward_440_out));
  DiodeBackward diodebackward_442 (.in(nRES), .out(diodebackward_440_out));
  DiodeBackward diodebackward_443 (.in(not_188_out), .out(diodebackward_443_out));
  DiodeBackward diodebackward_444 (.in(nQ0), .out(diodebackward_443_out));
  DiodeBackward diodebackward_445 (.in(not_190_out), .out(diodebackward_443_out));
  DiodeBackward diodebackward_446 (.in(not_189_out), .out(diodebackward_446_out));
  DiodeBackward diodebackward_447 (.in(nQ1), .out(diodebackward_446_out));
  DiodeBackward diodebackward_448 (.in(nRES), .out(diodebackward_446_out));
  DiodeBackward diodebackward_449 (.in(not_195_out), .out(diodebackward_449_out));
  DiodeBackward diodebackward_450 (.in(not_193_out), .out(diodebackward_449_out));
  DiodeBackward diodebackward_451 (.in(not_192_out), .out(diodebackward_451_out));
  DiodeBackward diodebackward_452 (.in(CLK_4), .out(diodebackward_451_out));
  DiodeBackward diodebackward_453 (.in(nRES), .out(diodebackward_451_out));
  DiodeBackward diodebackward_454 (.in(not_193_out), .out(diodebackward_454_out));
  DiodeBackward diodebackward_455 (.in(CLK_4), .out(diodebackward_454_out));
  DiodeBackward diodebackward_456 (.in(not_195_out), .out(diodebackward_454_out));
  DiodeBackward diodebackward_457 (.in(not_194_out), .out(diodebackward_457_out));
  DiodeBackward diodebackward_458 (.in(A15), .out(diodebackward_457_out));
  DiodeBackward diodebackward_459 (.in(nRES), .out(diodebackward_457_out));
  PullUp pullup_169 (.out(diodebackward_438_out));
  not not_187 (not_187_out, diodebackward_438_out);
  PullUp pullup_170 (.out(diodebackward_440_out));
  not not_188 (not_188_out, diodebackward_440_out);
  PullUp pullup_171 (.out(diodebackward_443_out));
  not not_189 (not_189_out, diodebackward_443_out);
  PullUp pullup_172 (.out(diodebackward_446_out));
  not not_190 (not_190_out, diodebackward_446_out);
  PullUp pullup_173 (.out(pullup_173_out));
  DiodeBackward diodebackward_460 (.in(not_179_out), .out(pullup_173_out));
  not not_191 (out_78, pullup_173_out);
  DiodeBackward diodebackward_461 (.in(not_180_out), .out(pullup_173_out));
  DiodeBackward diodebackward_462 (.in(not_181_out), .out(pullup_173_out));
  DiodeBackward diodebackward_463 (.in(not_182_out), .out(pullup_173_out));
  DiodeBackward diodebackward_464 (.in(not_183_out), .out(pullup_173_out));
  DiodeBackward diodebackward_465 (.in(not_184_out), .out(pullup_173_out));
  DiodeBackward diodebackward_466 (.in(not_185_out), .out(pullup_173_out));
  DiodeBackward diodebackward_467 (.in(not_186_out), .out(pullup_173_out));
  PullUp pullup_174 (.out(diodebackward_449_out));
  not not_192 (not_192_out, diodebackward_449_out);
  PullUp pullup_175 (.out(diodebackward_451_out));
  not not_193 (not_193_out, diodebackward_451_out);
  PullUp pullup_176 (.out(diodebackward_454_out));
  not not_194 (not_194_out, diodebackward_454_out);
  PullUp pullup_177 (.out(diodebackward_457_out));
  not not_195 (not_195_out, diodebackward_457_out);
  PullUp pullup_178 (.out(pullup_178_out));
  DiodeBackward diodebackward_468 (.in(not_173_out), .out(pullup_178_out));
  not not_196 (not_196_out, pullup_178_out);
  DiodeBackward diodebackward_469 (.in(not_161_out), .out(pullup_178_out));
  PullUp pullup_179 (.out(pullup_179_out));
  DiodeBackward diodebackward_470 (.in(not_174_out), .out(pullup_179_out));
  not not_197 (not_197_out, pullup_179_out);
  DiodeBackward diodebackward_471 (.in(not_161_out), .out(pullup_179_out));
  DiodeBackward diodebackward_472 (.in(not_188_out), .out(diodebackward_472_out));
  DiodeBackward diodebackward_473 (.in(nQ1), .out(diodebackward_472_out));
  DiodeBackward diodebackward_474 (.in(Q1), .out(diodebackward_474_out));
  DiodeBackward diodebackward_475 (.in(not_189_out), .out(diodebackward_474_out));
  DiodeBackward diodebackward_476 (.in(nRES), .out(diodebackward_474_out));
  DiodeBackward diodebackward_477 (.in(not_193_out), .out(diodebackward_477_out));
  DiodeBackward diodebackward_478 (.in(not_201_out), .out(diodebackward_477_out));
  DiodeBackward diodebackward_479 (.in(A14), .out(diodebackward_479_out));
  DiodeBackward diodebackward_480 (.in(not_194_out), .out(diodebackward_479_out));
  DiodeBackward diodebackward_481 (.in(nRES), .out(diodebackward_479_out));
  PullUp pullup_180 (.out(diodebackward_472_out));
  not not_198 (Q1, diodebackward_472_out);
  PullUp pullup_181 (.out(diodebackward_474_out));
  not not_199 (nQ1, diodebackward_474_out);
  PullUp pullup_182 (.out(diodebackward_477_out));
  not not_200 (A14, diodebackward_477_out);
  PullUp pullup_183 (.out(diodebackward_479_out));
  not not_201 (not_201_out, diodebackward_479_out);
  LED u_Q1 (.in(Q1));
  PullUp pullup_184 (.out(pullup_184_out));
  DiodeBackward diodebackward_482 (.in(not_196_out), .out(pullup_184_out));
  DiodeBackward diodebackward_483 (.in(not_203_out), .out(pullup_184_out));
  PullUp pullup_185 (.out(pullup_185_out));
  DiodeBackward diodebackward_484 (.in(not_202_out), .out(pullup_185_out));
  DiodeBackward diodebackward_485 (.in(not_197_out), .out(pullup_185_out));
  LED Q14 (.in(A14));
  not not_202 (not_202_out, pullup_184_out);
  not not_203 (not_203_out, pullup_185_out);
  not not_204 (not_204_out, S1_3);
  not not_205 (not_205_out, S0_3);
  PullUp pullup_186 (.out(pullup_186_out));
  DiodeBackward diodebackward_486 (.in(not_209_out), .out(pullup_186_out));
  DiodeBackward diodebackward_487 (.in(not_207_out), .out(pullup_186_out));
  PullUp pullup_187 (.out(pullup_187_out));
  DiodeBackward diodebackward_488 (.in(not_206_out), .out(pullup_187_out));
  DiodeBackward diodebackward_489 (.in(nQ1), .out(pullup_187_out));
  DiodeBackward diodebackward_490 (.in(nRES), .out(pullup_187_out));
  PullUp pullup_188 (.out(pullup_188_out));
  DiodeBackward diodebackward_491 (.in(not_207_out), .out(pullup_188_out));
  DiodeBackward diodebackward_492 (.in(nQ1), .out(pullup_188_out));
  DiodeBackward diodebackward_493 (.in(not_209_out), .out(pullup_188_out));
  PullUp pullup_189 (.out(pullup_189_out));
  DiodeBackward diodebackward_494 (.in(not_208_out), .out(pullup_189_out));
  DiodeBackward diodebackward_495 (.in(nQ2), .out(pullup_189_out));
  DiodeBackward diodebackward_496 (.in(nRES), .out(pullup_189_out));
  DiodeBackward diodebackward_497 (.in(not_213_out), .out(diodebackward_497_out));
  DiodeBackward diodebackward_498 (.in(not_211_out), .out(diodebackward_497_out));
  DiodeBackward diodebackward_499 (.in(not_210_out), .out(diodebackward_499_out));
  DiodeBackward diodebackward_500 (.in(CLK_4), .out(diodebackward_499_out));
  DiodeBackward diodebackward_501 (.in(nRES), .out(diodebackward_499_out));
  DiodeBackward diodebackward_502 (.in(not_211_out), .out(diodebackward_502_out));
  DiodeBackward diodebackward_503 (.in(CLK_4), .out(diodebackward_502_out));
  DiodeBackward diodebackward_504 (.in(not_213_out), .out(diodebackward_502_out));
  DiodeBackward diodebackward_505 (.in(not_212_out), .out(diodebackward_505_out));
  DiodeBackward diodebackward_506 (.in(A14), .out(diodebackward_505_out));
  DiodeBackward diodebackward_507 (.in(nRES), .out(diodebackward_505_out));
  not not_206 (not_206_out, pullup_186_out);
  not not_207 (not_207_out, pullup_187_out);
  not not_208 (not_208_out, pullup_188_out);
  not not_209 (not_209_out, pullup_189_out);
  PullUp pullup_190 (.out(diodebackward_497_out));
  not not_210 (not_210_out, diodebackward_497_out);
  PullUp pullup_191 (.out(diodebackward_499_out));
  not not_211 (not_211_out, diodebackward_499_out);
  PullUp pullup_192 (.out(diodebackward_502_out));
  not not_212 (not_212_out, diodebackward_502_out);
  PullUp pullup_193 (.out(diodebackward_505_out));
  not not_213 (not_213_out, diodebackward_505_out);
  PullUp pullup_194 (.out(pullup_194_out));
  DiodeBackward diodebackward_508 (.in(not_204_out), .out(pullup_194_out));
  DiodeBackward diodebackward_509 (.in(not_205_out), .out(pullup_194_out));
  DiodeBackward diodebackward_510 (.in(D_4), .out(pullup_194_out));
  DiodeBackward diodebackward_511 (.in(EN), .out(pullup_194_out));
  PullUp pullup_195 (.out(pullup_195_out));
  DiodeBackward diodebackward_512 (.in(S1_3), .out(pullup_195_out));
  DiodeBackward diodebackward_513 (.in(not_205_out), .out(pullup_195_out));
  DiodeBackward diodebackward_514 (.in(C_3), .out(pullup_195_out));
  DiodeBackward diodebackward_515 (.in(EN), .out(pullup_195_out));
  PullUp pullup_196 (.out(pullup_196_out));
  DiodeBackward diodebackward_516 (.in(not_204_out), .out(pullup_196_out));
  DiodeBackward diodebackward_517 (.in(S0_3), .out(pullup_196_out));
  DiodeBackward diodebackward_518 (.in(B_8), .out(pullup_196_out));
  DiodeBackward diodebackward_519 (.in(EN), .out(pullup_196_out));
  PullUp pullup_197 (.out(pullup_197_out));
  DiodeBackward diodebackward_520 (.in(S1_3), .out(pullup_197_out));
  DiodeBackward diodebackward_521 (.in(S0_3), .out(pullup_197_out));
  DiodeBackward diodebackward_522 (.in(A_8), .out(pullup_197_out));
  DiodeBackward diodebackward_523 (.in(EN), .out(pullup_197_out));
  not not_214 (not_214_out, A);
  not not_215 (not_215_out, B);
  not not_216 (not_216_out, C);
  not not_217 (not_217_out, nE);
  PullUp pullup_198 (.out(pullup_198_out));
  DiodeBackward diodebackward_524 (.in(not_207_out), .out(pullup_198_out));
  DiodeBackward diodebackward_525 (.in(nQ2), .out(pullup_198_out));
  PullUp pullup_199 (.out(pullup_199_out));
  DiodeBackward diodebackward_526 (.in(Q2), .out(pullup_199_out));
  DiodeBackward diodebackward_527 (.in(not_208_out), .out(pullup_199_out));
  DiodeBackward diodebackward_528 (.in(nRES), .out(pullup_199_out));
  PullUp pullup_200 (.out(pullup_200_out));
  DiodeBackward diodebackward_529 (.in(not_202_out), .out(pullup_200_out));
  not not_218 (not_218_out, pullup_200_out);
  DiodeBackward diodebackward_530 (.in(CLK_8), .out(pullup_200_out));
  PullUp pullup_201 (.out(pullup_201_out));
  DiodeBackward diodebackward_531 (.in(not_203_out), .out(pullup_201_out));
  not not_219 (not_219_out, pullup_201_out);
  DiodeBackward diodebackward_532 (.in(CLK_8), .out(pullup_201_out));
  not not_220 (not_220_out, pullup_194_out);
  not not_221 (not_221_out, pullup_195_out);
  not not_222 (not_222_out, pullup_196_out);
  not not_223 (not_223_out, pullup_197_out);
  DiodeBackward diodebackward_533 (.in(not_211_out), .out(diodebackward_533_out));
  DiodeBackward diodebackward_534 (.in(not_227_out), .out(diodebackward_533_out));
  DiodeBackward diodebackward_535 (.in(A13), .out(diodebackward_535_out));
  DiodeBackward diodebackward_536 (.in(not_212_out), .out(diodebackward_535_out));
  DiodeBackward diodebackward_537 (.in(nRES), .out(diodebackward_535_out));
  not not_224 (Q2, pullup_198_out);
  not not_225 (nQ2, pullup_199_out);
  PullUp pullup_202 (.out(diodebackward_533_out));
  not not_226 (A13, diodebackward_533_out);
  PullUp pullup_203 (.out(diodebackward_535_out));
  not not_227 (not_227_out, diodebackward_535_out);
  LED u_Q2 (.in(Q2));
  DiodeBackward diodebackward_538 (.in(not_220_out), .out(diodebackward_538_out));
  DiodeBackward diodebackward_539 (.in(not_221_out), .out(diodebackward_538_out));
  DiodeBackward diodebackward_540 (.in(not_222_out), .out(diodebackward_538_out));
  DiodeBackward diodebackward_541 (.in(not_223_out), .out(diodebackward_538_out));
  PullUp pullup_204 (.out(pullup_204_out));
  DiodeBackward diodebackward_542 (.in(not_214_out), .out(pullup_204_out));
  DiodeBackward diodebackward_543 (.in(not_215_out), .out(pullup_204_out));
  DiodeBackward diodebackward_544 (.in(not_216_out), .out(pullup_204_out));
  DiodeBackward diodebackward_545 (.in(not_217_out), .out(pullup_204_out));
  PullUp pullup_205 (.out(pullup_205_out));
  DiodeBackward diodebackward_546 (.in(A), .out(pullup_205_out));
  DiodeBackward diodebackward_547 (.in(not_215_out), .out(pullup_205_out));
  DiodeBackward diodebackward_548 (.in(not_216_out), .out(pullup_205_out));
  DiodeBackward diodebackward_549 (.in(not_217_out), .out(pullup_205_out));
  PullUp pullup_206 (.out(pullup_206_out));
  DiodeBackward diodebackward_550 (.in(not_214_out), .out(pullup_206_out));
  DiodeBackward diodebackward_551 (.in(B), .out(pullup_206_out));
  DiodeBackward diodebackward_552 (.in(not_216_out), .out(pullup_206_out));
  DiodeBackward diodebackward_553 (.in(not_217_out), .out(pullup_206_out));
  PullUp pullup_207 (.out(pullup_207_out));
  DiodeBackward diodebackward_554 (.in(A), .out(pullup_207_out));
  DiodeBackward diodebackward_555 (.in(B), .out(pullup_207_out));
  DiodeBackward diodebackward_556 (.in(not_216_out), .out(pullup_207_out));
  DiodeBackward diodebackward_557 (.in(not_217_out), .out(pullup_207_out));
  PullUp pullup_208 (.out(pullup_208_out));
  DiodeBackward diodebackward_558 (.in(not_214_out), .out(pullup_208_out));
  DiodeBackward diodebackward_559 (.in(not_215_out), .out(pullup_208_out));
  DiodeBackward diodebackward_560 (.in(C), .out(pullup_208_out));
  DiodeBackward diodebackward_561 (.in(not_217_out), .out(pullup_208_out));
  PullUp pullup_209 (.out(pullup_209_out));
  DiodeBackward diodebackward_562 (.in(A), .out(pullup_209_out));
  DiodeBackward diodebackward_563 (.in(not_215_out), .out(pullup_209_out));
  DiodeBackward diodebackward_564 (.in(C), .out(pullup_209_out));
  DiodeBackward diodebackward_565 (.in(not_217_out), .out(pullup_209_out));
  PullUp pullup_210 (.out(pullup_210_out));
  DiodeBackward diodebackward_566 (.in(not_214_out), .out(pullup_210_out));
  DiodeBackward diodebackward_567 (.in(B), .out(pullup_210_out));
  DiodeBackward diodebackward_568 (.in(C), .out(pullup_210_out));
  DiodeBackward diodebackward_569 (.in(not_217_out), .out(pullup_210_out));
  PullUp pullup_211 (.out(pullup_211_out));
  DiodeBackward diodebackward_570 (.in(A), .out(pullup_211_out));
  DiodeBackward diodebackward_571 (.in(B), .out(pullup_211_out));
  DiodeBackward diodebackward_572 (.in(C), .out(pullup_211_out));
  DiodeBackward diodebackward_573 (.in(not_217_out), .out(pullup_211_out));
  LED Q13 (.in(A13));
  PullUp pullup_212 (.out(pullup_212_out));
  DiodeBackward diodebackward_574 (.in(not_218_out), .out(pullup_212_out));
  DiodeBackward diodebackward_575 (.in(not_242_out), .out(pullup_212_out));
  PullUp pullup_213 (.out(pullup_213_out));
  DiodeBackward diodebackward_576 (.in(not_241_out), .out(pullup_213_out));
  DiodeBackward diodebackward_577 (.in(not_219_out), .out(pullup_213_out));
  PullUp pullup_214 (.out(pullup_214_out));
  DiodeBackward diodebackward_578 (.in(nSET_4), .out(pullup_214_out));
  DiodeBackward diodebackward_579 (.in(not_246_out), .out(pullup_214_out));
  DiodeBackward diodebackward_580 (.in(not_244_out), .out(pullup_214_out));
  PullUp pullup_215 (.out(pullup_215_out));
  DiodeBackward diodebackward_581 (.in(not_243_out), .out(pullup_215_out));
  DiodeBackward diodebackward_582 (.in(CLK_5), .out(pullup_215_out));
  DiodeBackward diodebackward_583 (.in(nRESET_4), .out(pullup_215_out));
  PullUp pullup_216 (.out(pullup_216_out));
  DiodeBackward diodebackward_584 (.in(not_244_out), .out(pullup_216_out));
  DiodeBackward diodebackward_585 (.in(CLK_5), .out(pullup_216_out));
  DiodeBackward diodebackward_586 (.in(not_246_out), .out(pullup_216_out));
  PullUp pullup_217 (.out(pullup_217_out));
  DiodeBackward diodebackward_587 (.in(not_245_out), .out(pullup_217_out));
  DiodeBackward diodebackward_588 (.in(DATA_2), .out(pullup_217_out));
  DiodeBackward diodebackward_589 (.in(nRESET_4), .out(pullup_217_out));
  PullUp pullup_218 (.out(diodebackward_538_out));
  not not_228 (out_117, diodebackward_538_out);
  not not_229 (out_8, pullup_204_out);
  not not_230 (out_7, pullup_205_out);
  not not_231 (out_6, pullup_206_out);
  not not_232 (out_5, pullup_207_out);
  not not_233 (out_4, pullup_208_out);
  not not_234 (out_3, pullup_209_out);
  not not_235 (out_2, pullup_210_out);
  not not_236 (out_1, pullup_211_out);
  PullUp pullup_219 (.out(pullup_219_out));
  not not_237 (not_237_out, pullup_219_out);
  DiodeBackward diodebackward_590 (.in(not_240_out), .out(pullup_219_out));
  DiodeBackward diodebackward_591 (.in(not_238_out), .out(pullup_219_out));
  PullUp pullup_220 (.out(pullup_220_out));
  DiodeBackward diodebackward_592 (.in(not_237_out), .out(pullup_220_out));
  not not_238 (not_238_out, pullup_220_out);
  DiodeBackward diodebackward_593 (.in(nQ2), .out(pullup_220_out));
  DiodeBackward diodebackward_594 (.in(nRES), .out(pullup_220_out));
  PullUp pullup_221 (.out(pullup_221_out));
  DiodeBackward diodebackward_595 (.in(not_238_out), .out(pullup_221_out));
  not not_239 (not_239_out, pullup_221_out);
  DiodeBackward diodebackward_596 (.in(nQ2), .out(pullup_221_out));
  DiodeBackward diodebackward_597 (.in(not_240_out), .out(pullup_221_out));
  PullUp pullup_222 (.out(pullup_222_out));
  DiodeBackward diodebackward_598 (.in(not_239_out), .out(pullup_222_out));
  not not_240 (not_240_out, pullup_222_out);
  DiodeBackward diodebackward_599 (.in(nQ3), .out(pullup_222_out));
  DiodeBackward diodebackward_600 (.in(nRES), .out(pullup_222_out));
  not not_241 (not_241_out, pullup_212_out);
  not not_242 (not_242_out, pullup_213_out);
  not not_243 (not_243_out, pullup_214_out);
  not not_244 (not_244_out, pullup_215_out);
  not not_245 (not_245_out, pullup_216_out);
  not not_246 (not_246_out, pullup_217_out);
  PullUp pullup_223 (.out(pullup_223_out));
  DiodeBackward diodebackward_601 (.in(not_250_out), .out(pullup_223_out));
  DiodeBackward diodebackward_602 (.in(not_248_out), .out(pullup_223_out));
  PullUp pullup_224 (.out(pullup_224_out));
  DiodeBackward diodebackward_603 (.in(not_247_out), .out(pullup_224_out));
  DiodeBackward diodebackward_604 (.in(CLK_4), .out(pullup_224_out));
  DiodeBackward diodebackward_605 (.in(nRES), .out(pullup_224_out));
  PullUp pullup_225 (.out(pullup_225_out));
  DiodeBackward diodebackward_606 (.in(not_248_out), .out(pullup_225_out));
  DiodeBackward diodebackward_607 (.in(CLK_4), .out(pullup_225_out));
  DiodeBackward diodebackward_608 (.in(not_250_out), .out(pullup_225_out));
  PullUp pullup_226 (.out(pullup_226_out));
  DiodeBackward diodebackward_609 (.in(not_249_out), .out(pullup_226_out));
  DiodeBackward diodebackward_610 (.in(A13), .out(pullup_226_out));
  DiodeBackward diodebackward_611 (.in(nRES), .out(pullup_226_out));
  not not_247 (not_247_out, pullup_223_out);
  not not_248 (not_248_out, pullup_224_out);
  not not_249 (not_249_out, pullup_225_out);
  not not_250 (not_250_out, pullup_226_out);
  PullUp pullup_227 (.out(pullup_227_out));
  DiodeBackward diodebackward_612 (.in(not_238_out), .out(pullup_227_out));
  not not_251 (Q3, pullup_227_out);
  DiodeBackward diodebackward_613 (.in(nQ3), .out(pullup_227_out));
  PullUp pullup_228 (.out(pullup_228_out));
  DiodeBackward diodebackward_614 (.in(Q3), .out(pullup_228_out));
  not not_252 (nQ3, pullup_228_out);
  DiodeBackward diodebackward_615 (.in(not_239_out), .out(pullup_228_out));
  DiodeBackward diodebackward_616 (.in(nRES), .out(pullup_228_out));
  PullUp pullup_229 (.out(pullup_229_out));
  DiodeBackward diodebackward_617 (.in(nSET_4), .out(pullup_229_out));
  DiodeBackward diodebackward_618 (.in(not_244_out), .out(pullup_229_out));
  not not_253 (Q_5, pullup_229_out);
  DiodeBackward diodebackward_619 (.in(nQ_6), .out(pullup_229_out));
  PullUp pullup_230 (.out(pullup_230_out));
  DiodeBackward diodebackward_620 (.in(Q_5), .out(pullup_230_out));
  not not_254 (nQ_6, pullup_230_out);
  DiodeBackward diodebackward_621 (.in(not_245_out), .out(pullup_230_out));
  DiodeBackward diodebackward_622 (.in(nRESET_4), .out(pullup_230_out));
  LED u_Q3 (.in(Q3));
  PullUp pullup_231 (.out(pullup_231_out));
  DiodeBackward diodebackward_623 (.in(not_241_out), .out(pullup_231_out));
  not not_255 (not_255_out, pullup_231_out);
  DiodeBackward diodebackward_624 (.in(not_161_out), .out(pullup_231_out));
  PullUp pullup_232 (.out(pullup_232_out));
  DiodeBackward diodebackward_625 (.in(not_242_out), .out(pullup_232_out));
  not not_256 (not_256_out, pullup_232_out);
  DiodeBackward diodebackward_626 (.in(not_161_out), .out(pullup_232_out));
  PullUp pullup_233 (.out(pullup_233_out));
  DiodeBackward diodebackward_627 (.in(not_248_out), .out(pullup_233_out));
  DiodeBackward diodebackward_628 (.in(not_258_out), .out(pullup_233_out));
  PullUp pullup_234 (.out(pullup_234_out));
  DiodeBackward diodebackward_629 (.in(A12), .out(pullup_234_out));
  DiodeBackward diodebackward_630 (.in(not_249_out), .out(pullup_234_out));
  DiodeBackward diodebackward_631 (.in(nRES), .out(pullup_234_out));
  not not_257 (A12, pullup_233_out);
  not not_258 (not_258_out, pullup_234_out);
  LED Q12 (.in(A12));
  PullUp pullup_235 (.out(pullup_235_out));
  DiodeBackward diodebackward_632 (.in(not_255_out), .out(pullup_235_out));
  DiodeBackward diodebackward_633 (.in(not_260_out), .out(pullup_235_out));
  PullUp pullup_236 (.out(pullup_236_out));
  DiodeBackward diodebackward_634 (.in(not_259_out), .out(pullup_236_out));
  DiodeBackward diodebackward_635 (.in(not_256_out), .out(pullup_236_out));
  not not_259 (not_259_out, pullup_235_out);
  not not_260 (not_260_out, pullup_236_out);
  PullUp pullup_237 (.out(pullup_237_out));
  DiodeBackward diodebackward_636 (.in(A_5), .out(pullup_237_out));
  DiodeBackward diodebackward_637 (.in(B_5), .out(pullup_237_out));
  not not_261 (not_261_out, B_3);
  not not_262 (not_262_out, A_3);
  not not_263 (not_263_out, S0);
  not not_264 (not_264_out, S1);
  not not_265 (not_265_out, nE1);
  not not_266 (not_266_out, nE2);
  PullUp pullup_238 (.out(pullup_238_out));
  DiodeBackward diodebackward_638 (.in(not_271_out), .out(pullup_238_out));
  DiodeBackward diodebackward_639 (.in(not_269_out), .out(pullup_238_out));
  PullUp pullup_239 (.out(pullup_239_out));
  DiodeBackward diodebackward_640 (.in(not_268_out), .out(pullup_239_out));
  DiodeBackward diodebackward_641 (.in(CLK_4), .out(pullup_239_out));
  DiodeBackward diodebackward_642 (.in(nRES), .out(pullup_239_out));
  PullUp pullup_240 (.out(pullup_240_out));
  DiodeBackward diodebackward_643 (.in(not_269_out), .out(pullup_240_out));
  DiodeBackward diodebackward_644 (.in(CLK_4), .out(pullup_240_out));
  DiodeBackward diodebackward_645 (.in(not_271_out), .out(pullup_240_out));
  PullUp pullup_241 (.out(pullup_241_out));
  DiodeBackward diodebackward_646 (.in(not_270_out), .out(pullup_241_out));
  DiodeBackward diodebackward_647 (.in(A12), .out(pullup_241_out));
  DiodeBackward diodebackward_648 (.in(nRES), .out(pullup_241_out));
  DiodeBackward diodebackward_649 (.in(A0_t), .out(diodebackward_649_out));
  DiodeBackward diodebackward_650 (.in(not_301_out), .out(diodebackward_649_out));
  DiodeBackward diodebackward_651 (.in(not_301_out), .out(diodebackward_651_out));
  DiodeBackward diodebackward_652 (.in(out_138), .out(diodebackward_651_out));
  DiodeBackward diodebackward_653 (.in(not_301_out), .out(diodebackward_653_out));
  DiodeBackward diodebackward_654 (.in(Cin_t), .out(diodebackward_653_out));
  DiodeBackward diodebackward_655 (.in(out_138), .out(diodebackward_655_out));
  DiodeBackward diodebackward_656 (.in(A0_t), .out(diodebackward_655_out));
  DiodeBackward diodebackward_657 (.in(Cin_t), .out(diodebackward_655_out));
  DiodeBackward diodebackward_658 (.in(Cin_t), .out(diodebackward_658_out));
  DiodeBackward diodebackward_659 (.in(out_138), .out(diodebackward_658_out));
  DiodeBackward diodebackward_660 (.in(A0_t), .out(diodebackward_660_out));
  DiodeBackward diodebackward_661 (.in(out_138), .out(diodebackward_660_out));
  DiodeBackward diodebackward_662 (.in(A0_t), .out(diodebackward_662_out));
  DiodeBackward diodebackward_663 (.in(Cin_t), .out(diodebackward_662_out));
  not not_267 (not_267_out, pullup_237_out);
  not not_268 (not_268_out, pullup_238_out);
  not not_269 (not_269_out, pullup_239_out);
  not not_270 (not_270_out, pullup_240_out);
  not not_271 (not_271_out, pullup_241_out);
  PullUp pullup_242 (.out(diodebackward_649_out));
  not not_272 (not_272_out, diodebackward_649_out);
  PullUp pullup_243 (.out(diodebackward_651_out));
  not not_273 (not_273_out, diodebackward_651_out);
  PullUp pullup_244 (.out(diodebackward_653_out));
  not not_274 (not_274_out, diodebackward_653_out);
  PullUp pullup_245 (.out(diodebackward_655_out));
  not not_275 (not_275_out, diodebackward_655_out);
  PullUp pullup_246 (.out(diodebackward_658_out));
  not not_276 (not_276_out, diodebackward_658_out);
  PullUp pullup_247 (.out(diodebackward_660_out));
  not not_277 (not_277_out, diodebackward_660_out);
  PullUp pullup_248 (.out(diodebackward_662_out));
  not not_278 (not_278_out, diodebackward_662_out);
  DiodeBackward diodebackward_664 (.in(A_7), .out(diodebackward_664_out));
  DiodeBackward diodebackward_665 (.in(B_7), .out(diodebackward_664_out));
  DiodeBackward diodebackward_666 (.in(C_2), .out(diodebackward_666_out));
  DiodeBackward diodebackward_667 (.in(D_3), .out(diodebackward_666_out));
  DiodeBackward diodebackward_668 (.in(A_5), .out(diodebackward_668_out));
  DiodeBackward diodebackward_669 (.in(not_267_out), .out(diodebackward_668_out));
  DiodeBackward diodebackward_670 (.in(not_267_out), .out(diodebackward_670_out));
  DiodeBackward diodebackward_671 (.in(B_5), .out(diodebackward_670_out));
  PullUp pullup_249 (.out(diodebackward_664_out));
  not not_279 (not_279_out, diodebackward_664_out);
  PullUp pullup_250 (.out(diodebackward_666_out));
  not not_280 (not_280_out, diodebackward_666_out);
  PullUp pullup_251 (.out(diodebackward_668_out));
  not not_281 (not_281_out, diodebackward_668_out);
  PullUp pullup_252 (.out(diodebackward_670_out));
  not not_282 (not_282_out, diodebackward_670_out);
  PullUp pullup_253 (.out(pullup_253_out));
  DiodeBackward diodebackward_672 (.in(not_261_out), .out(pullup_253_out));
  not not_283 (not_283_out, pullup_253_out);
  DiodeBackward diodebackward_673 (.in(not_262_out), .out(pullup_253_out));
  DiodeBackward diodebackward_674 (.in(I0), .out(pullup_253_out));
  PullUp pullup_254 (.out(pullup_254_out));
  DiodeBackward diodebackward_675 (.in(B_3), .out(pullup_254_out));
  not not_284 (not_284_out, pullup_254_out);
  DiodeBackward diodebackward_676 (.in(not_262_out), .out(pullup_254_out));
  DiodeBackward diodebackward_677 (.in(I1), .out(pullup_254_out));
  PullUp pullup_255 (.out(pullup_255_out));
  DiodeBackward diodebackward_678 (.in(not_261_out), .out(pullup_255_out));
  not not_285 (not_285_out, pullup_255_out);
  DiodeBackward diodebackward_679 (.in(A_3), .out(pullup_255_out));
  DiodeBackward diodebackward_680 (.in(I2), .out(pullup_255_out));
  PullUp pullup_256 (.out(pullup_256_out));
  DiodeBackward diodebackward_681 (.in(B_3), .out(pullup_256_out));
  not not_286 (not_286_out, pullup_256_out);
  DiodeBackward diodebackward_682 (.in(A_3), .out(pullup_256_out));
  DiodeBackward diodebackward_683 (.in(I3), .out(pullup_256_out));
  DiodeBackward diodebackward_684 (.in(not_263_out), .out(diodebackward_684_out));
  DiodeBackward diodebackward_685 (.in(not_264_out), .out(diodebackward_684_out));
  DiodeBackward diodebackward_686 (.in(A0), .out(diodebackward_684_out));
  DiodeBackward diodebackward_687 (.in(not_265_out), .out(diodebackward_684_out));
  DiodeBackward diodebackward_688 (.in(S0), .out(diodebackward_688_out));
  DiodeBackward diodebackward_689 (.in(not_264_out), .out(diodebackward_688_out));
  DiodeBackward diodebackward_690 (.in(A1), .out(diodebackward_688_out));
  DiodeBackward diodebackward_691 (.in(not_265_out), .out(diodebackward_688_out));
  DiodeBackward diodebackward_692 (.in(not_263_out), .out(diodebackward_692_out));
  DiodeBackward diodebackward_693 (.in(S1), .out(diodebackward_692_out));
  DiodeBackward diodebackward_694 (.in(A2), .out(diodebackward_692_out));
  DiodeBackward diodebackward_695 (.in(not_265_out), .out(diodebackward_692_out));
  DiodeBackward diodebackward_696 (.in(S0), .out(diodebackward_696_out));
  DiodeBackward diodebackward_697 (.in(S1), .out(diodebackward_696_out));
  DiodeBackward diodebackward_698 (.in(A3), .out(diodebackward_696_out));
  DiodeBackward diodebackward_699 (.in(not_265_out), .out(diodebackward_696_out));
  DiodeBackward diodebackward_700 (.in(not_263_out), .out(diodebackward_700_out));
  DiodeBackward diodebackward_701 (.in(not_264_out), .out(diodebackward_700_out));
  DiodeBackward diodebackward_702 (.in(B0), .out(diodebackward_700_out));
  DiodeBackward diodebackward_703 (.in(not_266_out), .out(diodebackward_700_out));
  DiodeBackward diodebackward_704 (.in(S0), .out(diodebackward_704_out));
  DiodeBackward diodebackward_705 (.in(not_264_out), .out(diodebackward_704_out));
  DiodeBackward diodebackward_706 (.in(B1), .out(diodebackward_704_out));
  DiodeBackward diodebackward_707 (.in(not_266_out), .out(diodebackward_704_out));
  DiodeBackward diodebackward_708 (.in(not_263_out), .out(diodebackward_708_out));
  DiodeBackward diodebackward_709 (.in(S1), .out(diodebackward_708_out));
  DiodeBackward diodebackward_710 (.in(B2), .out(diodebackward_708_out));
  DiodeBackward diodebackward_711 (.in(not_266_out), .out(diodebackward_708_out));
  DiodeBackward diodebackward_712 (.in(S0), .out(diodebackward_712_out));
  DiodeBackward diodebackward_713 (.in(S1), .out(diodebackward_712_out));
  DiodeBackward diodebackward_714 (.in(B3), .out(diodebackward_712_out));
  DiodeBackward diodebackward_715 (.in(not_266_out), .out(diodebackward_712_out));
  PullUp pullup_257 (.out(pullup_257_out));
  DiodeBackward diodebackward_716 (.in(not_269_out), .out(pullup_257_out));
  DiodeBackward diodebackward_717 (.in(not_296_out), .out(pullup_257_out));
  PullUp pullup_258 (.out(pullup_258_out));
  DiodeBackward diodebackward_718 (.in(A11), .out(pullup_258_out));
  DiodeBackward diodebackward_719 (.in(not_270_out), .out(pullup_258_out));
  DiodeBackward diodebackward_720 (.in(nRES), .out(pullup_258_out));
  PullUp pullup_259 (.out(pullup_259_out));
  DiodeBackward diodebackward_721 (.in(not_272_out), .out(pullup_259_out));
  DiodeBackward diodebackward_722 (.in(not_273_out), .out(pullup_259_out));
  DiodeBackward diodebackward_723 (.in(not_274_out), .out(pullup_259_out));
  DiodeBackward diodebackward_724 (.in(not_275_out), .out(pullup_259_out));
  PullUp pullup_260 (.out(pullup_260_out));
  DiodeBackward diodebackward_725 (.in(not_276_out), .out(pullup_260_out));
  DiodeBackward diodebackward_726 (.in(not_277_out), .out(pullup_260_out));
  DiodeBackward diodebackward_727 (.in(not_278_out), .out(pullup_260_out));
  DiodeBackward diodebackward_728 (.in(not_279_out), .out(diodebackward_728_out));
  DiodeBackward diodebackward_729 (.in(not_280_out), .out(diodebackward_728_out));
  DiodeBackward diodebackward_730 (.in(not_281_out), .out(diodebackward_730_out));
  DiodeBackward diodebackward_731 (.in(not_282_out), .out(diodebackward_730_out));
  PullUp pullup_261 (.out(diodebackward_684_out));
  not not_287 (not_287_out, diodebackward_684_out);
  PullUp pullup_262 (.out(diodebackward_688_out));
  not not_288 (not_288_out, diodebackward_688_out);
  PullUp pullup_263 (.out(diodebackward_692_out));
  not not_289 (not_289_out, diodebackward_692_out);
  PullUp pullup_264 (.out(diodebackward_696_out));
  not not_290 (not_290_out, diodebackward_696_out);
  PullUp pullup_265 (.out(diodebackward_700_out));
  not not_291 (not_291_out, diodebackward_700_out);
  PullUp pullup_266 (.out(diodebackward_704_out));
  not not_292 (not_292_out, diodebackward_704_out);
  PullUp pullup_267 (.out(diodebackward_708_out));
  not not_293 (not_293_out, diodebackward_708_out);
  PullUp pullup_268 (.out(diodebackward_712_out));
  not not_294 (not_294_out, diodebackward_712_out);
  not not_295 (A11, pullup_257_out);
  not not_296 (not_296_out, pullup_258_out);
  not not_297 (Sum_t, pullup_259_out);
  not not_298 (CARRY_3, pullup_260_out);
  PullUp pullup_269 (.out(diodebackward_728_out));
  not not_299 (out_97, diodebackward_728_out);
  PullUp pullup_270 (.out(diodebackward_730_out));
  not not_300 (out_91, diodebackward_730_out);
  LED Q11 (.in(A11));
  not not_301 (not_301_out, CARRY_3);
  PullUp pullup_271 (.out(pullup_271_out));
  DiodeBackward diodebackward_732 (.in(not_283_out), .out(pullup_271_out));
  DiodeBackward diodebackward_733 (.in(not_284_out), .out(pullup_271_out));
  DiodeBackward diodebackward_734 (.in(not_285_out), .out(pullup_271_out));
  DiodeBackward diodebackward_735 (.in(not_286_out), .out(pullup_271_out));
  DiodeBackward diodebackward_736 (.in(Sum_t), .out(diodebackward_736_out));
  DiodeBackward diodebackward_737 (.in(I4), .out(diodebackward_736_out));
  DiodeBackward diodebackward_738 (.in(I5), .out(diodebackward_738_out));
  DiodeBackward diodebackward_739 (.in(CARRY_3), .out(diodebackward_738_out));
  not not_302 (out_58, pullup_271_out);
  PullUp pullup_272 (.out(pullup_272_out));
  DiodeBackward diodebackward_740 (.in(not_287_out), .out(pullup_272_out));
  not not_303 (out_17, pullup_272_out);
  DiodeBackward diodebackward_741 (.in(not_288_out), .out(pullup_272_out));
  DiodeBackward diodebackward_742 (.in(not_289_out), .out(pullup_272_out));
  DiodeBackward diodebackward_743 (.in(not_290_out), .out(pullup_272_out));
  PullUp pullup_273 (.out(pullup_273_out));
  DiodeBackward diodebackward_744 (.in(not_291_out), .out(pullup_273_out));
  not not_304 (out_18, pullup_273_out);
  DiodeBackward diodebackward_745 (.in(not_292_out), .out(pullup_273_out));
  DiodeBackward diodebackward_746 (.in(not_293_out), .out(pullup_273_out));
  DiodeBackward diodebackward_747 (.in(not_294_out), .out(pullup_273_out));
  DiodeBackward diodebackward_748 (.in(not_310_out), .out(diodebackward_748_out));
  DiodeBackward diodebackward_749 (.in(not_308_out), .out(diodebackward_748_out));
  DiodeBackward diodebackward_750 (.in(not_307_out), .out(diodebackward_750_out));
  DiodeBackward diodebackward_751 (.in(CLK_4), .out(diodebackward_750_out));
  DiodeBackward diodebackward_752 (.in(nRES), .out(diodebackward_750_out));
  DiodeBackward diodebackward_753 (.in(not_308_out), .out(diodebackward_753_out));
  DiodeBackward diodebackward_754 (.in(CLK_4), .out(diodebackward_753_out));
  DiodeBackward diodebackward_755 (.in(not_310_out), .out(diodebackward_753_out));
  DiodeBackward diodebackward_756 (.in(not_309_out), .out(diodebackward_756_out));
  DiodeBackward diodebackward_757 (.in(A11), .out(diodebackward_756_out));
  DiodeBackward diodebackward_758 (.in(nRES), .out(diodebackward_756_out));
  PullUp pullup_274 (.out(diodebackward_736_out));
  not not_305 (not_305_out, diodebackward_736_out);
  PullUp pullup_275 (.out(diodebackward_738_out));
  not not_306 (not_306_out, diodebackward_738_out);
  PullUp pullup_276 (.out(diodebackward_748_out));
  not not_307 (not_307_out, diodebackward_748_out);
  PullUp pullup_277 (.out(diodebackward_750_out));
  not not_308 (not_308_out, diodebackward_750_out);
  PullUp pullup_278 (.out(diodebackward_753_out));
  not not_309 (not_309_out, diodebackward_753_out);
  PullUp pullup_279 (.out(diodebackward_756_out));
  not not_310 (not_310_out, diodebackward_756_out);
  PullUp pullup_280 (.out(pullup_280_out));
  DiodeBackward diodebackward_759 (.in(not_305_out), .out(pullup_280_out));
  not not_311 (Fout_2, pullup_280_out);
  DiodeBackward diodebackward_760 (.in(not_306_out), .out(pullup_280_out));
  DiodeBackward diodebackward_761 (.in(not_308_out), .out(diodebackward_761_out));
  DiodeBackward diodebackward_762 (.in(not_313_out), .out(diodebackward_761_out));
  DiodeBackward diodebackward_763 (.in(A10), .out(diodebackward_763_out));
  DiodeBackward diodebackward_764 (.in(not_309_out), .out(diodebackward_763_out));
  DiodeBackward diodebackward_765 (.in(nRES), .out(diodebackward_763_out));
  DiodeBackward diodebackward_766 (.in(A_6), .out(diodebackward_766_out));
  DiodeBackward diodebackward_767 (.in(B_6), .out(diodebackward_766_out));
  PullUp pullup_281 (.out(diodebackward_761_out));
  not not_312 (A10, diodebackward_761_out);
  PullUp pullup_282 (.out(diodebackward_763_out));
  not not_313 (not_313_out, diodebackward_763_out);
  PullUp pullup_283 (.out(diodebackward_766_out));
  not not_314 (not_314_out, diodebackward_766_out);
  not not_315 (not_315_out, out_58);
  not not_316 (not_316_out, Cin_2);
  LED Q10 (.in(A10));
  DiodeBackward diodebackward_768 (.in(A_6), .out(diodebackward_768_out));
  DiodeBackward diodebackward_769 (.in(not_314_out), .out(diodebackward_768_out));
  DiodeBackward diodebackward_770 (.in(not_314_out), .out(diodebackward_770_out));
  DiodeBackward diodebackward_771 (.in(B_6), .out(diodebackward_770_out));
  PullUp pullup_284 (.out(diodebackward_768_out));
  not not_317 (not_317_out, diodebackward_768_out);
  PullUp pullup_285 (.out(diodebackward_770_out));
  not not_318 (not_318_out, diodebackward_770_out);
  PullUp pullup_286 (.out(pullup_286_out));
  DiodeBackward diodebackward_772 (.in(in_33), .out(pullup_286_out));
  not not_319 (not_319_out, pullup_286_out);
  DiodeBackward diodebackward_773 (.in(in_34), .out(pullup_286_out));
  PullUp pullup_287 (.out(pullup_287_out));
  DiodeBackward diodebackward_774 (.in(in_35), .out(pullup_287_out));
  not not_320 (not_320_out, pullup_287_out);
  DiodeBackward diodebackward_775 (.in(in_36), .out(pullup_287_out));
  DiodeBackward diodebackward_776 (.in(not_324_out), .out(diodebackward_776_out));
  DiodeBackward diodebackward_777 (.in(not_322_out), .out(diodebackward_776_out));
  DiodeBackward diodebackward_778 (.in(not_321_out), .out(diodebackward_778_out));
  DiodeBackward diodebackward_779 (.in(CLK_4), .out(diodebackward_778_out));
  DiodeBackward diodebackward_780 (.in(nRES), .out(diodebackward_778_out));
  DiodeBackward diodebackward_781 (.in(not_322_out), .out(diodebackward_781_out));
  DiodeBackward diodebackward_782 (.in(CLK_4), .out(diodebackward_781_out));
  DiodeBackward diodebackward_783 (.in(not_324_out), .out(diodebackward_781_out));
  DiodeBackward diodebackward_784 (.in(not_323_out), .out(diodebackward_784_out));
  DiodeBackward diodebackward_785 (.in(A10), .out(diodebackward_784_out));
  DiodeBackward diodebackward_786 (.in(nRES), .out(diodebackward_784_out));
  DiodeBackward diodebackward_787 (.in(not_317_out), .out(diodebackward_787_out));
  DiodeBackward diodebackward_788 (.in(not_318_out), .out(diodebackward_787_out));
  DiodeBackward diodebackward_789 (.in(not_315_out), .out(diodebackward_789_out));
  DiodeBackward diodebackward_790 (.in(not_316_out), .out(diodebackward_789_out));
  DiodeBackward diodebackward_791 (.in(I0_2), .out(diodebackward_789_out));
  DiodeBackward diodebackward_792 (.in(out_58), .out(diodebackward_792_out));
  DiodeBackward diodebackward_793 (.in(not_316_out), .out(diodebackward_792_out));
  DiodeBackward diodebackward_794 (.in(I1_2), .out(diodebackward_792_out));
  DiodeBackward diodebackward_795 (.in(not_315_out), .out(diodebackward_795_out));
  DiodeBackward diodebackward_796 (.in(Cin_2), .out(diodebackward_795_out));
  DiodeBackward diodebackward_797 (.in(I2_2), .out(diodebackward_795_out));
  DiodeBackward diodebackward_798 (.in(out_58), .out(diodebackward_798_out));
  DiodeBackward diodebackward_799 (.in(Cin_2), .out(diodebackward_798_out));
  DiodeBackward diodebackward_800 (.in(I3_2), .out(diodebackward_798_out));
  DiodeBackward diodebackward_801 (.in(A_2), .out(diodebackward_801_out));
  DiodeBackward diodebackward_802 (.in(pullup_314_out), .out(diodebackward_801_out));
  DiodeBackward diodebackward_803 (.in(pullup_314_out), .out(diodebackward_803_out));
  DiodeBackward diodebackward_804 (.in(B_2), .out(diodebackward_803_out));
  DiodeBackward diodebackward_805 (.in(pullup_314_out), .out(diodebackward_805_out));
  DiodeBackward diodebackward_806 (.in(Cin), .out(diodebackward_805_out));
  DiodeBackward diodebackward_807 (.in(B_2), .out(diodebackward_807_out));
  DiodeBackward diodebackward_808 (.in(A_2), .out(diodebackward_807_out));
  DiodeBackward diodebackward_809 (.in(Cin), .out(diodebackward_807_out));
  DiodeBackward diodebackward_810 (.in(Cin), .out(diodebackward_810_out));
  DiodeBackward diodebackward_811 (.in(B_2), .out(diodebackward_810_out));
  DiodeBackward diodebackward_812 (.in(A_2), .out(diodebackward_812_out));
  DiodeBackward diodebackward_813 (.in(B_2), .out(diodebackward_812_out));
  DiodeBackward diodebackward_814 (.in(A_2), .out(diodebackward_814_out));
  DiodeBackward diodebackward_815 (.in(Cin), .out(diodebackward_814_out));
  PullUp pullup_288 (.out(diodebackward_776_out));
  not not_321 (not_321_out, diodebackward_776_out);
  PullUp pullup_289 (.out(diodebackward_778_out));
  not not_322 (not_322_out, diodebackward_778_out);
  PullUp pullup_290 (.out(diodebackward_781_out));
  not not_323 (not_323_out, diodebackward_781_out);
  PullUp pullup_291 (.out(diodebackward_784_out));
  not not_324 (not_324_out, diodebackward_784_out);
  PullUp pullup_292 (.out(diodebackward_787_out));
  not not_325 (not_325_out, diodebackward_787_out);
  PullUp pullup_293 (.out(diodebackward_789_out));
  not not_326 (not_326_out, diodebackward_789_out);
  PullUp pullup_294 (.out(diodebackward_792_out));
  not not_327 (not_327_out, diodebackward_792_out);
  PullUp pullup_295 (.out(diodebackward_795_out));
  not not_328 (not_328_out, diodebackward_795_out);
  PullUp pullup_296 (.out(diodebackward_798_out));
  not not_329 (not_329_out, diodebackward_798_out);
  PullUp pullup_297 (.out(diodebackward_801_out));
  not not_330 (not_330_out, diodebackward_801_out);
  PullUp pullup_298 (.out(diodebackward_803_out));
  not not_331 (not_331_out, diodebackward_803_out);
  PullUp pullup_299 (.out(diodebackward_805_out));
  not not_332 (not_332_out, diodebackward_805_out);
  PullUp pullup_300 (.out(diodebackward_807_out));
  not not_333 (not_333_out, diodebackward_807_out);
  PullUp pullup_301 (.out(diodebackward_810_out));
  not not_334 (not_334_out, diodebackward_810_out);
  PullUp pullup_302 (.out(diodebackward_812_out));
  not not_335 (not_335_out, diodebackward_812_out);
  PullUp pullup_303 (.out(diodebackward_814_out));
  not not_336 (not_336_out, diodebackward_814_out);
  DiodeBackward diodebackward_816 (.in(nSET_3), .out(diodebackward_816_out));
  DiodeBackward diodebackward_817 (.in(not_340_out), .out(diodebackward_816_out));
  DiodeBackward diodebackward_818 (.in(not_338_out), .out(diodebackward_816_out));
  DiodeBackward diodebackward_819 (.in(not_337_out), .out(diodebackward_819_out));
  DiodeBackward diodebackward_820 (.in(CLK_4), .out(diodebackward_819_out));
  DiodeBackward diodebackward_821 (.in(nRESET_3), .out(diodebackward_819_out));
  DiodeBackward diodebackward_822 (.in(not_338_out), .out(diodebackward_822_out));
  DiodeBackward diodebackward_823 (.in(CLK_4), .out(diodebackward_822_out));
  DiodeBackward diodebackward_824 (.in(not_340_out), .out(diodebackward_822_out));
  DiodeBackward diodebackward_825 (.in(not_339_out), .out(diodebackward_825_out));
  DiodeBackward diodebackward_826 (.in(CARRY_3), .out(diodebackward_825_out));
  DiodeBackward diodebackward_827 (.in(nRESET_3), .out(diodebackward_825_out));
  DiodeBackward diodebackward_828 (.in(not_325_out), .out(diodebackward_828_out));
  DiodeBackward diodebackward_829 (.in(Cin_4), .out(diodebackward_828_out));
  PullUp pullup_304 (.out(pullup_304_out));
  DiodeBackward diodebackward_830 (.in(not_319_out), .out(pullup_304_out));
  DiodeBackward diodebackward_831 (.in(not_320_out), .out(pullup_304_out));
  DiodeBackward diodebackward_832 (.in(not_322_out), .out(diodebackward_832_out));
  DiodeBackward diodebackward_833 (.in(not_344_out), .out(diodebackward_832_out));
  DiodeBackward diodebackward_834 (.in(A9), .out(diodebackward_834_out));
  DiodeBackward diodebackward_835 (.in(not_323_out), .out(diodebackward_834_out));
  DiodeBackward diodebackward_836 (.in(nRES), .out(diodebackward_834_out));
  PullUp pullup_305 (.out(diodebackward_816_out));
  not not_337 (not_337_out, diodebackward_816_out);
  PullUp pullup_306 (.out(diodebackward_819_out));
  not not_338 (not_338_out, diodebackward_819_out);
  PullUp pullup_307 (.out(diodebackward_822_out));
  not not_339 (not_339_out, diodebackward_822_out);
  PullUp pullup_308 (.out(diodebackward_825_out));
  not not_340 (not_340_out, diodebackward_825_out);
  PullUp pullup_309 (.out(diodebackward_828_out));
  not not_341 (not_341_out, diodebackward_828_out);
  DiodeBackward diodebackward_837 (.in(not_326_out), .out(diodebackward_837_out));
  DiodeBackward diodebackward_838 (.in(not_327_out), .out(diodebackward_837_out));
  DiodeBackward diodebackward_839 (.in(not_328_out), .out(diodebackward_837_out));
  DiodeBackward diodebackward_840 (.in(not_329_out), .out(diodebackward_837_out));
  not not_342 (out_32, pullup_304_out);
  PullUp pullup_310 (.out(diodebackward_832_out));
  not not_343 (A9, diodebackward_832_out);
  PullUp pullup_311 (.out(diodebackward_834_out));
  not not_344 (not_344_out, diodebackward_834_out);
  PullUp pullup_312 (.out(diodebackward_837_out));
  not not_345 (out_64, diodebackward_837_out);
  PullUp pullup_313 (.out(pullup_313_out));
  DiodeBackward diodebackward_841 (.in(not_330_out), .out(pullup_313_out));
  DiodeBackward diodebackward_842 (.in(not_331_out), .out(pullup_313_out));
  DiodeBackward diodebackward_843 (.in(not_332_out), .out(pullup_313_out));
  DiodeBackward diodebackward_844 (.in(not_333_out), .out(pullup_313_out));
  PullUp pullup_314 (.out(pullup_314_out));
  DiodeBackward diodebackward_845 (.in(not_334_out), .out(pullup_314_out));
  DiodeBackward diodebackward_846 (.in(not_335_out), .out(pullup_314_out));
  DiodeBackward diodebackward_847 (.in(not_336_out), .out(pullup_314_out));
  LED Q9 (.in(A9));
  DiodeBackward diodebackward_848 (.in(nSET_3), .out(diodebackward_848_out));
  DiodeBackward diodebackward_849 (.in(not_338_out), .out(diodebackward_848_out));
  DiodeBackward diodebackward_850 (.in(nQ_5), .out(diodebackward_848_out));
  DiodeBackward diodebackward_851 (.in(Cin_t), .out(diodebackward_851_out));
  DiodeBackward diodebackward_852 (.in(not_339_out), .out(diodebackward_851_out));
  DiodeBackward diodebackward_853 (.in(nRESET_3), .out(diodebackward_851_out));
  PullUp pullup_315 (.out(pullup_315_out));
  DiodeBackward diodebackward_854 (.in(not_325_out), .out(pullup_315_out));
  not not_346 (not_346_out, pullup_315_out);
  DiodeBackward diodebackward_855 (.in(not_341_out), .out(pullup_315_out));
  PullUp pullup_316 (.out(pullup_316_out));
  DiodeBackward diodebackward_856 (.in(not_341_out), .out(pullup_316_out));
  not not_347 (not_347_out, pullup_316_out);
  DiodeBackward diodebackward_857 (.in(Cin_4), .out(pullup_316_out));
  PullUp pullup_317 (.out(pullup_317_out));
  DiodeBackward diodebackward_858 (.in(not_314_out), .out(pullup_317_out));
  not not_348 (Cout, pullup_317_out);
  DiodeBackward diodebackward_859 (.in(not_341_out), .out(pullup_317_out));
  not not_349 (SUM, pullup_313_out);
  not not_350 (CARRY, pullup_314_out);
  PullUp pullup_318 (.out(diodebackward_848_out));
  not not_351 (Cin_t, diodebackward_848_out);
  PullUp pullup_319 (.out(diodebackward_851_out));
  not not_352 (nQ_5, diodebackward_851_out);
  PullUp pullup_320 (.out(pullup_320_out));
  DiodeBackward diodebackward_860 (.in(not_346_out), .out(pullup_320_out));
  not not_353 (SUM_2, pullup_320_out);
  DiodeBackward diodebackward_861 (.in(not_347_out), .out(pullup_320_out));
  PullUp pullup_321 (.out(pullup_321_out));
  DiodeBackward diodebackward_862 (.in(not_357_out), .out(pullup_321_out));
  DiodeBackward diodebackward_863 (.in(not_355_out), .out(pullup_321_out));
  PullUp pullup_322 (.out(pullup_322_out));
  DiodeBackward diodebackward_864 (.in(not_354_out), .out(pullup_322_out));
  DiodeBackward diodebackward_865 (.in(CLK_4), .out(pullup_322_out));
  DiodeBackward diodebackward_866 (.in(nRES), .out(pullup_322_out));
  PullUp pullup_323 (.out(pullup_323_out));
  DiodeBackward diodebackward_867 (.in(not_355_out), .out(pullup_323_out));
  DiodeBackward diodebackward_868 (.in(CLK_4), .out(pullup_323_out));
  DiodeBackward diodebackward_869 (.in(not_357_out), .out(pullup_323_out));
  PullUp pullup_324 (.out(pullup_324_out));
  DiodeBackward diodebackward_870 (.in(not_356_out), .out(pullup_324_out));
  DiodeBackward diodebackward_871 (.in(A9), .out(pullup_324_out));
  DiodeBackward diodebackward_872 (.in(nRES), .out(pullup_324_out));
  not not_354 (not_354_out, pullup_321_out);
  not not_355 (not_355_out, pullup_322_out);
  not not_356 (not_356_out, pullup_323_out);
  not not_357 (not_357_out, pullup_324_out);
  not not_358 (not_358_out, D);
  PullUp pullup_325 (.out(pullup_325_out));
  DiodeBackward diodebackward_873 (.in(not_355_out), .out(pullup_325_out));
  DiodeBackward diodebackward_874 (.in(not_360_out), .out(pullup_325_out));
  PullUp pullup_326 (.out(pullup_326_out));
  DiodeBackward diodebackward_875 (.in(A8), .out(pullup_326_out));
  DiodeBackward diodebackward_876 (.in(not_356_out), .out(pullup_326_out));
  DiodeBackward diodebackward_877 (.in(nRES), .out(pullup_326_out));
  not not_359 (A8, pullup_325_out);
  not not_360 (not_360_out, pullup_326_out);
  DiodeBackward diodebackward_878 (.in(CLK_2), .out(diodebackward_878_out));
  DiodeBackward diodebackward_879 (.in(D_2), .out(diodebackward_878_out));
  DiodeBackward diodebackward_880 (.in(not_362_out), .out(diodebackward_880_out));
  DiodeBackward diodebackward_881 (.in(CLK_2), .out(diodebackward_880_out));
  not not_361 (not_361_out, CLK);
  LED Q8 (.in(A8));
  PullUp pullup_327 (.out(diodebackward_878_out));
  not not_362 (not_362_out, diodebackward_878_out);
  PullUp pullup_328 (.out(diodebackward_880_out));
  not not_363 (not_363_out, diodebackward_880_out);
  PullUp pullup_329 (.out(pullup_329_out));
  DiodeBackward diodebackward_882 (.in(D), .out(pullup_329_out));
  not not_364 (not_364_out, pullup_329_out);
  DiodeBackward diodebackward_883 (.in(not_361_out), .out(pullup_329_out));
  PullUp pullup_330 (.out(pullup_330_out));
  DiodeBackward diodebackward_884 (.in(not_361_out), .out(pullup_330_out));
  not not_365 (not_365_out, pullup_330_out);
  DiodeBackward diodebackward_885 (.in(not_358_out), .out(pullup_330_out));
  PullUp pullup_331 (.out(pullup_331_out));
  DiodeBackward diodebackward_886 (.in(A_4), .out(pullup_331_out));
  not not_366 (not_366_out, pullup_331_out);
  DiodeBackward diodebackward_887 (.in(not_384_out), .out(pullup_331_out));
  PullUp pullup_332 (.out(pullup_332_out));
  DiodeBackward diodebackward_888 (.in(not_384_out), .out(pullup_332_out));
  not not_367 (not_367_out, pullup_332_out);
  DiodeBackward diodebackward_889 (.in(B_4), .out(pullup_332_out));
  PullUp pullup_333 (.out(pullup_333_out));
  DiodeBackward diodebackward_890 (.in(not_384_out), .out(pullup_333_out));
  not not_368 (not_368_out, pullup_333_out);
  DiodeBackward diodebackward_891 (.in(Cin_3), .out(pullup_333_out));
  PullUp pullup_334 (.out(pullup_334_out));
  DiodeBackward diodebackward_892 (.in(B_4), .out(pullup_334_out));
  not not_369 (not_369_out, pullup_334_out);
  DiodeBackward diodebackward_893 (.in(A_4), .out(pullup_334_out));
  DiodeBackward diodebackward_894 (.in(Cin_3), .out(pullup_334_out));
  PullUp pullup_335 (.out(pullup_335_out));
  DiodeBackward diodebackward_895 (.in(Cin_3), .out(pullup_335_out));
  not not_370 (not_370_out, pullup_335_out);
  DiodeBackward diodebackward_896 (.in(B_4), .out(pullup_335_out));
  PullUp pullup_336 (.out(pullup_336_out));
  DiodeBackward diodebackward_897 (.in(A_4), .out(pullup_336_out));
  not not_371 (not_371_out, pullup_336_out);
  DiodeBackward diodebackward_898 (.in(B_4), .out(pullup_336_out));
  PullUp pullup_337 (.out(pullup_337_out));
  DiodeBackward diodebackward_899 (.in(A_4), .out(pullup_337_out));
  not not_372 (not_372_out, pullup_337_out);
  DiodeBackward diodebackward_900 (.in(Cin_3), .out(pullup_337_out));
  DiodeBackward diodebackward_901 (.in(nSET_2), .out(diodebackward_901_out));
  DiodeBackward diodebackward_902 (.in(nQ_4), .out(diodebackward_901_out));
  DiodeBackward diodebackward_903 (.in(Q_4), .out(diodebackward_903_out));
  DiodeBackward diodebackward_904 (.in(nRESET_2), .out(diodebackward_903_out));
  DiodeBackward diodebackward_905 (.in(not_362_out), .out(diodebackward_905_out));
  DiodeBackward diodebackward_906 (.in(nQ_2), .out(diodebackward_905_out));
  DiodeBackward diodebackward_907 (.in(Q_2), .out(diodebackward_907_out));
  DiodeBackward diodebackward_908 (.in(not_363_out), .out(diodebackward_907_out));
  DiodeBackward diodebackward_909 (.in(not_364_out), .out(diodebackward_909_out));
  DiodeBackward diodebackward_910 (.in(not_378_out), .out(diodebackward_909_out));
  DiodeBackward diodebackward_911 (.in(not_377_out), .out(diodebackward_911_out));
  DiodeBackward diodebackward_912 (.in(not_365_out), .out(diodebackward_911_out));
  PullUp pullup_338 (.out(pullup_338_out));
  DiodeBackward diodebackward_913 (.in(not_382_out), .out(pullup_338_out));
  DiodeBackward diodebackward_914 (.in(not_380_out), .out(pullup_338_out));
  PullUp pullup_339 (.out(pullup_339_out));
  DiodeBackward diodebackward_915 (.in(not_379_out), .out(pullup_339_out));
  DiodeBackward diodebackward_916 (.in(CLK_4), .out(pullup_339_out));
  DiodeBackward diodebackward_917 (.in(nRES), .out(pullup_339_out));
  PullUp pullup_340 (.out(pullup_340_out));
  DiodeBackward diodebackward_918 (.in(not_380_out), .out(pullup_340_out));
  DiodeBackward diodebackward_919 (.in(CLK_4), .out(pullup_340_out));
  DiodeBackward diodebackward_920 (.in(not_382_out), .out(pullup_340_out));
  PullUp pullup_341 (.out(pullup_341_out));
  DiodeBackward diodebackward_921 (.in(not_381_out), .out(pullup_341_out));
  DiodeBackward diodebackward_922 (.in(A8), .out(pullup_341_out));
  DiodeBackward diodebackward_923 (.in(nRES), .out(pullup_341_out));
  PullUp pullup_342 (.out(diodebackward_901_out));
  not not_373 (Q_4, diodebackward_901_out);
  PullUp pullup_343 (.out(diodebackward_903_out));
  not not_374 (nQ_4, diodebackward_903_out);
  PullUp pullup_344 (.out(diodebackward_905_out));
  not not_375 (Q_2, diodebackward_905_out);
  PullUp pullup_345 (.out(diodebackward_907_out));
  not not_376 (nQ_2, diodebackward_907_out);
  PullUp pullup_346 (.out(diodebackward_909_out));
  not not_377 (not_377_out, diodebackward_909_out);
  PullUp pullup_347 (.out(diodebackward_911_out));
  not not_378 (not_378_out, diodebackward_911_out);
  not not_379 (not_379_out, pullup_338_out);
  not not_380 (not_380_out, pullup_339_out);
  not not_381 (not_381_out, pullup_340_out);
  not not_382 (not_382_out, pullup_341_out);
  DiodeBackward diodebackward_924 (.in(not_366_out), .out(diodebackward_924_out));
  DiodeBackward diodebackward_925 (.in(not_367_out), .out(diodebackward_924_out));
  DiodeBackward diodebackward_926 (.in(not_368_out), .out(diodebackward_924_out));
  DiodeBackward diodebackward_927 (.in(not_369_out), .out(diodebackward_924_out));
  DiodeBackward diodebackward_928 (.in(not_370_out), .out(diodebackward_928_out));
  DiodeBackward diodebackward_929 (.in(not_371_out), .out(diodebackward_928_out));
  DiodeBackward diodebackward_930 (.in(not_372_out), .out(diodebackward_928_out));
  PullUp pullup_348 (.out(diodebackward_924_out));
  not not_383 (not_383_out, diodebackward_924_out);
  PullUp pullup_349 (.out(diodebackward_928_out));
  PullUp pullup_350 (.out(pullup_350_out));
  DiodeBackward diodebackward_931 (.in(not_380_out), .out(pullup_350_out));
  DiodeBackward diodebackward_932 (.in(not_389_out), .out(pullup_350_out));
  PullUp pullup_351 (.out(pullup_351_out));
  DiodeBackward diodebackward_933 (.in(A7), .out(pullup_351_out));
  DiodeBackward diodebackward_934 (.in(not_381_out), .out(pullup_351_out));
  DiodeBackward diodebackward_935 (.in(nRES), .out(pullup_351_out));
  not not_384 (not_384_out, CARRY_2);
  not not_385 (CARRY_2, diodebackward_928_out);
  PullUp pullup_352 (.out(pullup_352_out));
  DiodeBackward diodebackward_936 (.in(CLK), .out(pullup_352_out));
  not not_386 (not_386_out, pullup_352_out);
  DiodeBackward diodebackward_937 (.in(not_377_out), .out(pullup_352_out));
  PullUp pullup_353 (.out(pullup_353_out));
  DiodeBackward diodebackward_938 (.in(not_378_out), .out(pullup_353_out));
  not not_387 (not_387_out, pullup_353_out);
  DiodeBackward diodebackward_939 (.in(CLK), .out(pullup_353_out));
  not not_388 (A7, pullup_350_out);
  not not_389 (not_389_out, pullup_351_out);
  LED Q7 (.in(A7));
  PullUp pullup_354 (.out(pullup_354_out));
  DiodeBackward diodebackward_940 (.in(not_383_out), .out(pullup_354_out));
  DiodeBackward diodebackward_941 (.in(I0_3), .out(pullup_354_out));
  PullUp pullup_355 (.out(pullup_355_out));
  DiodeBackward diodebackward_942 (.in(I1_3), .out(pullup_355_out));
  DiodeBackward diodebackward_943 (.in(CARRY_2), .out(pullup_355_out));
  DiodeBackward diodebackward_944 (.in(not_386_out), .out(diodebackward_944_out));
  DiodeBackward diodebackward_945 (.in(nQ), .out(diodebackward_944_out));
  DiodeBackward diodebackward_946 (.in(Q), .out(diodebackward_946_out));
  DiodeBackward diodebackward_947 (.in(not_387_out), .out(diodebackward_946_out));
  not not_390 (not_390_out, pullup_354_out);
  not not_391 (not_391_out, pullup_355_out);
  PullUp pullup_356 (.out(diodebackward_944_out));
  not not_392 (Q, diodebackward_944_out);
  PullUp pullup_357 (.out(diodebackward_946_out));
  not not_393 (nQ, diodebackward_946_out);
  DiodeBackward diodebackward_948 (.in(not_397_out), .out(diodebackward_948_out));
  DiodeBackward diodebackward_949 (.in(not_395_out), .out(diodebackward_948_out));
  DiodeBackward diodebackward_950 (.in(not_394_out), .out(diodebackward_950_out));
  DiodeBackward diodebackward_951 (.in(CLK_4), .out(diodebackward_950_out));
  DiodeBackward diodebackward_952 (.in(nRES), .out(diodebackward_950_out));
  DiodeBackward diodebackward_953 (.in(not_395_out), .out(diodebackward_953_out));
  DiodeBackward diodebackward_954 (.in(CLK_4), .out(diodebackward_953_out));
  DiodeBackward diodebackward_955 (.in(not_397_out), .out(diodebackward_953_out));
  DiodeBackward diodebackward_956 (.in(not_396_out), .out(diodebackward_956_out));
  DiodeBackward diodebackward_957 (.in(A7), .out(diodebackward_956_out));
  DiodeBackward diodebackward_958 (.in(nRES), .out(diodebackward_956_out));
  DiodeBackward diodebackward_959 (.in(not_390_out), .out(diodebackward_959_out));
  DiodeBackward diodebackward_960 (.in(not_391_out), .out(diodebackward_959_out));
  PullUp pullup_358 (.out(diodebackward_948_out));
  not not_394 (not_394_out, diodebackward_948_out);
  PullUp pullup_359 (.out(diodebackward_950_out));
  not not_395 (not_395_out, diodebackward_950_out);
  PullUp pullup_360 (.out(diodebackward_953_out));
  not not_396 (not_396_out, diodebackward_953_out);
  PullUp pullup_361 (.out(diodebackward_956_out));
  not not_397 (not_397_out, diodebackward_956_out);
  PullUp pullup_362 (.out(diodebackward_959_out));
  not not_398 (Fout, diodebackward_959_out);
  DiodeBackward diodebackward_961 (.in(not_395_out), .out(diodebackward_961_out));
  DiodeBackward diodebackward_962 (.in(not_400_out), .out(diodebackward_961_out));
  DiodeBackward diodebackward_963 (.in(A6), .out(diodebackward_963_out));
  DiodeBackward diodebackward_964 (.in(not_396_out), .out(diodebackward_963_out));
  DiodeBackward diodebackward_965 (.in(nRES), .out(diodebackward_963_out));
  DiodeBackward diodebackward_966 (.in(nSET), .out(diodebackward_966_out));
  DiodeBackward diodebackward_967 (.in(not_404_out), .out(diodebackward_966_out));
  DiodeBackward diodebackward_968 (.in(not_402_out), .out(diodebackward_966_out));
  DiodeBackward diodebackward_969 (.in(not_401_out), .out(diodebackward_969_out));
  DiodeBackward diodebackward_970 (.in(CLK_3), .out(diodebackward_969_out));
  DiodeBackward diodebackward_971 (.in(nRESET), .out(diodebackward_969_out));
  DiodeBackward diodebackward_972 (.in(not_402_out), .out(diodebackward_972_out));
  DiodeBackward diodebackward_973 (.in(CLK_3), .out(diodebackward_972_out));
  DiodeBackward diodebackward_974 (.in(not_404_out), .out(diodebackward_972_out));
  DiodeBackward diodebackward_975 (.in(not_403_out), .out(diodebackward_975_out));
  DiodeBackward diodebackward_976 (.in(DATA), .out(diodebackward_975_out));
  DiodeBackward diodebackward_977 (.in(nRESET), .out(diodebackward_975_out));
  PullUp pullup_363 (.out(diodebackward_961_out));
  not not_399 (A6, diodebackward_961_out);
  PullUp pullup_364 (.out(diodebackward_963_out));
  not not_400 (not_400_out, diodebackward_963_out);
  PullUp pullup_365 (.out(diodebackward_966_out));
  not not_401 (not_401_out, diodebackward_966_out);
  PullUp pullup_366 (.out(diodebackward_969_out));
  not not_402 (not_402_out, diodebackward_969_out);
  PullUp pullup_367 (.out(diodebackward_972_out));
  not not_403 (not_403_out, diodebackward_972_out);
  PullUp pullup_368 (.out(diodebackward_975_out));
  not not_404 (not_404_out, diodebackward_975_out);
  LED Q6 (.in(A6));
  DiodeBackward diodebackward_978 (.in(not_408_out), .out(diodebackward_978_out));
  DiodeBackward diodebackward_979 (.in(not_406_out), .out(diodebackward_978_out));
  DiodeBackward diodebackward_980 (.in(not_405_out), .out(diodebackward_980_out));
  DiodeBackward diodebackward_981 (.in(CLK_4), .out(diodebackward_980_out));
  DiodeBackward diodebackward_982 (.in(nRES), .out(diodebackward_980_out));
  DiodeBackward diodebackward_983 (.in(not_406_out), .out(diodebackward_983_out));
  DiodeBackward diodebackward_984 (.in(CLK_4), .out(diodebackward_983_out));
  DiodeBackward diodebackward_985 (.in(not_408_out), .out(diodebackward_983_out));
  DiodeBackward diodebackward_986 (.in(not_407_out), .out(diodebackward_986_out));
  DiodeBackward diodebackward_987 (.in(A6), .out(diodebackward_986_out));
  DiodeBackward diodebackward_988 (.in(nRES), .out(diodebackward_986_out));
  DiodeBackward diodebackward_989 (.in(nSET), .out(diodebackward_989_out));
  DiodeBackward diodebackward_990 (.in(not_402_out), .out(diodebackward_989_out));
  DiodeBackward diodebackward_991 (.in(nQ_3), .out(diodebackward_989_out));
  DiodeBackward diodebackward_992 (.in(Q_3), .out(diodebackward_992_out));
  DiodeBackward diodebackward_993 (.in(not_403_out), .out(diodebackward_992_out));
  DiodeBackward diodebackward_994 (.in(nRESET), .out(diodebackward_992_out));
  PullUp pullup_369 (.out(diodebackward_978_out));
  not not_405 (not_405_out, diodebackward_978_out);
  PullUp pullup_370 (.out(diodebackward_980_out));
  not not_406 (not_406_out, diodebackward_980_out);
  PullUp pullup_371 (.out(diodebackward_983_out));
  not not_407 (not_407_out, diodebackward_983_out);
  PullUp pullup_372 (.out(diodebackward_986_out));
  not not_408 (not_408_out, diodebackward_986_out);
  PullUp pullup_373 (.out(diodebackward_989_out));
  not not_409 (Q_3, diodebackward_989_out);
  PullUp pullup_374 (.out(diodebackward_992_out));
  not not_410 (nQ_3, diodebackward_992_out);
  DiodeBackward diodebackward_995 (.in(not_406_out), .out(diodebackward_995_out));
  DiodeBackward diodebackward_996 (.in(not_412_out), .out(diodebackward_995_out));
  DiodeBackward diodebackward_997 (.in(A5), .out(diodebackward_997_out));
  DiodeBackward diodebackward_998 (.in(not_407_out), .out(diodebackward_997_out));
  DiodeBackward diodebackward_999 (.in(nRES), .out(diodebackward_997_out));
  PullUp pullup_375 (.out(diodebackward_995_out));
  not not_411 (A5, diodebackward_995_out);
  PullUp pullup_376 (.out(diodebackward_997_out));
  not not_412 (not_412_out, diodebackward_997_out);
  LED Q5 (.in(A5));
  PullUp pullup_377 (.out(pullup_377_out));
  DiodeBackward diodebackward_1000 (.in(not_416_out), .out(pullup_377_out));
  DiodeBackward diodebackward_1001 (.in(not_414_out), .out(pullup_377_out));
  PullUp pullup_378 (.out(pullup_378_out));
  DiodeBackward diodebackward_1002 (.in(not_413_out), .out(pullup_378_out));
  DiodeBackward diodebackward_1003 (.in(CLK_4), .out(pullup_378_out));
  DiodeBackward diodebackward_1004 (.in(nRES), .out(pullup_378_out));
  PullUp pullup_379 (.out(pullup_379_out));
  DiodeBackward diodebackward_1005 (.in(not_414_out), .out(pullup_379_out));
  DiodeBackward diodebackward_1006 (.in(CLK_4), .out(pullup_379_out));
  DiodeBackward diodebackward_1007 (.in(not_416_out), .out(pullup_379_out));
  PullUp pullup_380 (.out(pullup_380_out));
  DiodeBackward diodebackward_1008 (.in(not_415_out), .out(pullup_380_out));
  DiodeBackward diodebackward_1009 (.in(A5), .out(pullup_380_out));
  DiodeBackward diodebackward_1010 (.in(nRES), .out(pullup_380_out));
  not not_413 (not_413_out, pullup_377_out);
  not not_414 (not_414_out, pullup_378_out);
  not not_415 (not_415_out, pullup_379_out);
  not not_416 (not_416_out, pullup_380_out);
  PullUp pullup_381 (.out(pullup_381_out));
  DiodeBackward diodebackward_1011 (.in(A3_2), .out(pullup_381_out));
  DiodeBackward diodebackward_1012 (.in(B3_2), .out(pullup_381_out));
  PullUp pullup_382 (.out(pullup_382_out));
  DiodeBackward diodebackward_1013 (.in(A2_2), .out(pullup_382_out));
  DiodeBackward diodebackward_1014 (.in(B2_2), .out(pullup_382_out));
  PullUp pullup_383 (.out(pullup_383_out));
  DiodeBackward diodebackward_1015 (.in(A1_2), .out(pullup_383_out));
  DiodeBackward diodebackward_1016 (.in(B1_2), .out(pullup_383_out));
  PullUp pullup_384 (.out(pullup_384_out));
  DiodeBackward diodebackward_1017 (.in(A0_2), .out(pullup_384_out));
  DiodeBackward diodebackward_1018 (.in(B0_2), .out(pullup_384_out));
  PullUp pullup_385 (.out(pullup_385_out));
  DiodeBackward diodebackward_1019 (.in(not_414_out), .out(pullup_385_out));
  DiodeBackward diodebackward_1020 (.in(not_422_out), .out(pullup_385_out));
  PullUp pullup_386 (.out(pullup_386_out));
  DiodeBackward diodebackward_1021 (.in(A4), .out(pullup_386_out));
  DiodeBackward diodebackward_1022 (.in(not_415_out), .out(pullup_386_out));
  DiodeBackward diodebackward_1023 (.in(nRES), .out(pullup_386_out));
  not not_417 (not_417_out, pullup_381_out);
  not not_418 (not_418_out, pullup_382_out);
  not not_419 (not_419_out, pullup_383_out);
  not not_420 (not_420_out, pullup_384_out);
  not not_421 (A4, pullup_385_out);
  not not_422 (not_422_out, pullup_386_out);
  DiodeBackward diodebackward_1024 (.in(A3_2), .out(diodebackward_1024_out));
  DiodeBackward diodebackward_1025 (.in(not_417_out), .out(diodebackward_1024_out));
  DiodeBackward diodebackward_1026 (.in(not_417_out), .out(diodebackward_1026_out));
  DiodeBackward diodebackward_1027 (.in(B3_2), .out(diodebackward_1026_out));
  DiodeBackward diodebackward_1028 (.in(A2_2), .out(diodebackward_1028_out));
  DiodeBackward diodebackward_1029 (.in(not_418_out), .out(diodebackward_1028_out));
  DiodeBackward diodebackward_1030 (.in(not_418_out), .out(diodebackward_1030_out));
  DiodeBackward diodebackward_1031 (.in(B2_2), .out(diodebackward_1030_out));
  DiodeBackward diodebackward_1032 (.in(A1_2), .out(diodebackward_1032_out));
  DiodeBackward diodebackward_1033 (.in(not_419_out), .out(diodebackward_1032_out));
  DiodeBackward diodebackward_1034 (.in(not_419_out), .out(diodebackward_1034_out));
  DiodeBackward diodebackward_1035 (.in(B1_2), .out(diodebackward_1034_out));
  DiodeBackward diodebackward_1036 (.in(A0_2), .out(diodebackward_1036_out));
  DiodeBackward diodebackward_1037 (.in(not_420_out), .out(diodebackward_1036_out));
  DiodeBackward diodebackward_1038 (.in(not_420_out), .out(diodebackward_1038_out));
  DiodeBackward diodebackward_1039 (.in(B0_2), .out(diodebackward_1038_out));
  LED Q4 (.in(A4));
  PullUp pullup_387 (.out(diodebackward_1024_out));
  not not_423 (not_423_out, diodebackward_1024_out);
  PullUp pullup_388 (.out(diodebackward_1026_out));
  not not_424 (not_424_out, diodebackward_1026_out);
  PullUp pullup_389 (.out(diodebackward_1028_out));
  not not_425 (not_425_out, diodebackward_1028_out);
  PullUp pullup_390 (.out(diodebackward_1030_out));
  not not_426 (not_426_out, diodebackward_1030_out);
  PullUp pullup_391 (.out(diodebackward_1032_out));
  not not_427 (not_427_out, diodebackward_1032_out);
  PullUp pullup_392 (.out(diodebackward_1034_out));
  not not_428 (not_428_out, diodebackward_1034_out);
  PullUp pullup_393 (.out(diodebackward_1036_out));
  not not_429 (not_429_out, diodebackward_1036_out);
  PullUp pullup_394 (.out(diodebackward_1038_out));
  not not_430 (not_430_out, diodebackward_1038_out);
  DiodeBackward diodebackward_1040 (.in(not_423_out), .out(diodebackward_1040_out));
  DiodeBackward diodebackward_1041 (.in(not_424_out), .out(diodebackward_1040_out));
  DiodeBackward diodebackward_1042 (.in(not_425_out), .out(diodebackward_1042_out));
  DiodeBackward diodebackward_1043 (.in(not_426_out), .out(diodebackward_1042_out));
  DiodeBackward diodebackward_1044 (.in(not_427_out), .out(diodebackward_1044_out));
  DiodeBackward diodebackward_1045 (.in(not_428_out), .out(diodebackward_1044_out));
  DiodeBackward diodebackward_1046 (.in(not_429_out), .out(diodebackward_1046_out));
  DiodeBackward diodebackward_1047 (.in(not_430_out), .out(diodebackward_1046_out));
  PullUp pullup_395 (.out(diodebackward_1040_out));
  not not_431 (not_431_out, diodebackward_1040_out);
  PullUp pullup_396 (.out(diodebackward_1042_out));
  not not_432 (not_432_out, diodebackward_1042_out);
  PullUp pullup_397 (.out(diodebackward_1044_out));
  not not_433 (not_433_out, diodebackward_1044_out);
  PullUp pullup_398 (.out(diodebackward_1046_out));
  not not_434 (not_434_out, diodebackward_1046_out);
  DiodeBackward diodebackward_1048 (.in(not_438_out), .out(diodebackward_1048_out));
  DiodeBackward diodebackward_1049 (.in(not_436_out), .out(diodebackward_1048_out));
  DiodeBackward diodebackward_1050 (.in(not_435_out), .out(diodebackward_1050_out));
  DiodeBackward diodebackward_1051 (.in(CLK_4), .out(diodebackward_1050_out));
  DiodeBackward diodebackward_1052 (.in(nRES), .out(diodebackward_1050_out));
  DiodeBackward diodebackward_1053 (.in(not_436_out), .out(diodebackward_1053_out));
  DiodeBackward diodebackward_1054 (.in(CLK_4), .out(diodebackward_1053_out));
  DiodeBackward diodebackward_1055 (.in(not_438_out), .out(diodebackward_1053_out));
  DiodeBackward diodebackward_1056 (.in(not_437_out), .out(diodebackward_1056_out));
  DiodeBackward diodebackward_1057 (.in(A4), .out(diodebackward_1056_out));
  DiodeBackward diodebackward_1058 (.in(nRES), .out(diodebackward_1056_out));
  DiodeBackward diodebackward_1059 (.in(not_431_out), .out(diodebackward_1059_out));
  DiodeBackward diodebackward_1060 (.in(C2), .out(diodebackward_1059_out));
  DiodeBackward diodebackward_1061 (.in(not_432_out), .out(diodebackward_1061_out));
  DiodeBackward diodebackward_1062 (.in(C1), .out(diodebackward_1061_out));
  DiodeBackward diodebackward_1063 (.in(not_433_out), .out(diodebackward_1063_out));
  DiodeBackward diodebackward_1064 (.in(C0), .out(diodebackward_1063_out));
  DiodeBackward diodebackward_1065 (.in(not_434_out), .out(diodebackward_1065_out));
  DiodeBackward diodebackward_1066 (.in(Cin_5), .out(diodebackward_1065_out));
  PullUp pullup_399 (.out(diodebackward_1048_out));
  not not_435 (not_435_out, diodebackward_1048_out);
  PullUp pullup_400 (.out(diodebackward_1050_out));
  not not_436 (not_436_out, diodebackward_1050_out);
  PullUp pullup_401 (.out(diodebackward_1053_out));
  not not_437 (not_437_out, diodebackward_1053_out);
  PullUp pullup_402 (.out(diodebackward_1056_out));
  not not_438 (not_438_out, diodebackward_1056_out);
  PullUp pullup_403 (.out(diodebackward_1059_out));
  not not_439 (not_439_out, diodebackward_1059_out);
  PullUp pullup_404 (.out(diodebackward_1061_out));
  not not_440 (not_440_out, diodebackward_1061_out);
  PullUp pullup_405 (.out(diodebackward_1063_out));
  not not_441 (not_441_out, diodebackward_1063_out);
  PullUp pullup_406 (.out(diodebackward_1065_out));
  not not_442 (not_442_out, diodebackward_1065_out);
  DiodeBackward diodebackward_1067 (.in(not_431_out), .out(diodebackward_1067_out));
  DiodeBackward diodebackward_1068 (.in(not_439_out), .out(diodebackward_1067_out));
  DiodeBackward diodebackward_1069 (.in(not_439_out), .out(diodebackward_1069_out));
  DiodeBackward diodebackward_1070 (.in(C2), .out(diodebackward_1069_out));
  DiodeBackward diodebackward_1071 (.in(not_417_out), .out(diodebackward_1071_out));
  DiodeBackward diodebackward_1072 (.in(not_439_out), .out(diodebackward_1071_out));
  DiodeBackward diodebackward_1073 (.in(not_432_out), .out(diodebackward_1073_out));
  DiodeBackward diodebackward_1074 (.in(not_440_out), .out(diodebackward_1073_out));
  DiodeBackward diodebackward_1075 (.in(not_440_out), .out(diodebackward_1075_out));
  DiodeBackward diodebackward_1076 (.in(C1), .out(diodebackward_1075_out));
  DiodeBackward diodebackward_1077 (.in(not_418_out), .out(diodebackward_1077_out));
  DiodeBackward diodebackward_1078 (.in(not_440_out), .out(diodebackward_1077_out));
  DiodeBackward diodebackward_1079 (.in(not_433_out), .out(diodebackward_1079_out));
  DiodeBackward diodebackward_1080 (.in(not_441_out), .out(diodebackward_1079_out));
  DiodeBackward diodebackward_1081 (.in(not_441_out), .out(diodebackward_1081_out));
  DiodeBackward diodebackward_1082 (.in(C0), .out(diodebackward_1081_out));
  DiodeBackward diodebackward_1083 (.in(not_419_out), .out(diodebackward_1083_out));
  DiodeBackward diodebackward_1084 (.in(not_441_out), .out(diodebackward_1083_out));
  DiodeBackward diodebackward_1085 (.in(not_434_out), .out(diodebackward_1085_out));
  DiodeBackward diodebackward_1086 (.in(not_442_out), .out(diodebackward_1085_out));
  DiodeBackward diodebackward_1087 (.in(not_442_out), .out(diodebackward_1087_out));
  DiodeBackward diodebackward_1088 (.in(Cin_5), .out(diodebackward_1087_out));
  DiodeBackward diodebackward_1089 (.in(not_420_out), .out(diodebackward_1089_out));
  DiodeBackward diodebackward_1090 (.in(not_442_out), .out(diodebackward_1089_out));
  DiodeBackward diodebackward_1091 (.in(not_436_out), .out(diodebackward_1091_out));
  DiodeBackward diodebackward_1092 (.in(not_456_out), .out(diodebackward_1091_out));
  DiodeBackward diodebackward_1093 (.in(A3_t), .out(diodebackward_1093_out));
  DiodeBackward diodebackward_1094 (.in(not_437_out), .out(diodebackward_1093_out));
  DiodeBackward diodebackward_1095 (.in(nRES), .out(diodebackward_1093_out));
  PullUp pullup_407 (.out(diodebackward_1067_out));
  not not_443 (not_443_out, diodebackward_1067_out);
  PullUp pullup_408 (.out(diodebackward_1069_out));
  not not_444 (not_444_out, diodebackward_1069_out);
  PullUp pullup_409 (.out(diodebackward_1071_out));
  not not_445 (C3, diodebackward_1071_out);
  PullUp pullup_410 (.out(diodebackward_1073_out));
  not not_446 (not_446_out, diodebackward_1073_out);
  PullUp pullup_411 (.out(diodebackward_1075_out));
  not not_447 (not_447_out, diodebackward_1075_out);
  PullUp pullup_412 (.out(diodebackward_1077_out));
  not not_448 (C2, diodebackward_1077_out);
  PullUp pullup_413 (.out(diodebackward_1079_out));
  not not_449 (not_449_out, diodebackward_1079_out);
  PullUp pullup_414 (.out(diodebackward_1081_out));
  not not_450 (not_450_out, diodebackward_1081_out);
  PullUp pullup_415 (.out(diodebackward_1083_out));
  not not_451 (C1, diodebackward_1083_out);
  PullUp pullup_416 (.out(diodebackward_1085_out));
  not not_452 (not_452_out, diodebackward_1085_out);
  PullUp pullup_417 (.out(diodebackward_1087_out));
  not not_453 (not_453_out, diodebackward_1087_out);
  PullUp pullup_418 (.out(diodebackward_1089_out));
  not not_454 (C0, diodebackward_1089_out);
  PullUp pullup_419 (.out(diodebackward_1091_out));
  not not_455 (A3_t, diodebackward_1091_out);
  PullUp pullup_420 (.out(diodebackward_1093_out));
  not not_456 (not_456_out, diodebackward_1093_out);
  DiodeBackward diodebackward_1096 (.in(not_443_out), .out(diodebackward_1096_out));
  DiodeBackward diodebackward_1097 (.in(not_444_out), .out(diodebackward_1096_out));
  DiodeBackward diodebackward_1098 (.in(not_446_out), .out(diodebackward_1098_out));
  DiodeBackward diodebackward_1099 (.in(not_447_out), .out(diodebackward_1098_out));
  DiodeBackward diodebackward_1100 (.in(not_449_out), .out(diodebackward_1100_out));
  DiodeBackward diodebackward_1101 (.in(not_450_out), .out(diodebackward_1100_out));
  DiodeBackward diodebackward_1102 (.in(not_452_out), .out(diodebackward_1102_out));
  DiodeBackward diodebackward_1103 (.in(not_453_out), .out(diodebackward_1102_out));
  LED Q3_2 (.in(A3_t));
  PullUp pullup_421 (.out(diodebackward_1096_out));
  not not_457 (not_457_out, diodebackward_1096_out);
  PullUp pullup_422 (.out(diodebackward_1098_out));
  not not_458 (SUM2, diodebackward_1098_out);
  PullUp pullup_423 (.out(diodebackward_1100_out));
  not not_459 (SUM1, diodebackward_1100_out);
  PullUp pullup_424 (.out(diodebackward_1102_out));
  not not_460 (SUM0, diodebackward_1102_out);
  DiodeBackward diodebackward_1104 (.in(not_464_out), .out(diodebackward_1104_out));
  DiodeBackward diodebackward_1105 (.in(not_462_out), .out(diodebackward_1104_out));
  DiodeBackward diodebackward_1106 (.in(not_461_out), .out(diodebackward_1106_out));
  DiodeBackward diodebackward_1107 (.in(CLK_4), .out(diodebackward_1106_out));
  DiodeBackward diodebackward_1108 (.in(nRES), .out(diodebackward_1106_out));
  DiodeBackward diodebackward_1109 (.in(not_462_out), .out(diodebackward_1109_out));
  DiodeBackward diodebackward_1110 (.in(CLK_4), .out(diodebackward_1109_out));
  DiodeBackward diodebackward_1111 (.in(not_464_out), .out(diodebackward_1109_out));
  DiodeBackward diodebackward_1112 (.in(not_463_out), .out(diodebackward_1112_out));
  DiodeBackward diodebackward_1113 (.in(A3_t), .out(diodebackward_1112_out));
  DiodeBackward diodebackward_1114 (.in(nRES), .out(diodebackward_1112_out));
  PullUp pullup_425 (.out(diodebackward_1104_out));
  not not_461 (not_461_out, diodebackward_1104_out);
  PullUp pullup_426 (.out(diodebackward_1106_out));
  not not_462 (not_462_out, diodebackward_1106_out);
  PullUp pullup_427 (.out(diodebackward_1109_out));
  not not_463 (not_463_out, diodebackward_1109_out);
  PullUp pullup_428 (.out(diodebackward_1112_out));
  not not_464 (not_464_out, diodebackward_1112_out);
  DiodeBackward diodebackward_1115 (.in(not_457_out), .out(diodebackward_1115_out));
  DiodeBackward diodebackward_1116 (.in(I0_5), .out(diodebackward_1115_out));
  DiodeBackward diodebackward_1117 (.in(I1_5), .out(diodebackward_1117_out));
  DiodeBackward diodebackward_1118 (.in(C3), .out(diodebackward_1117_out));
  DiodeBackward diodebackward_1119 (.in(M), .out(diodebackward_1117_out));
  DiodeBackward diodebackward_1120 (.in(not_462_out), .out(diodebackward_1120_out));
  DiodeBackward diodebackward_1121 (.in(not_468_out), .out(diodebackward_1120_out));
  DiodeBackward diodebackward_1122 (.in(A2_t), .out(diodebackward_1122_out));
  DiodeBackward diodebackward_1123 (.in(not_463_out), .out(diodebackward_1122_out));
  DiodeBackward diodebackward_1124 (.in(nRES), .out(diodebackward_1122_out));
  PullUp pullup_429 (.out(diodebackward_1115_out));
  not not_465 (not_465_out, diodebackward_1115_out);
  PullUp pullup_430 (.out(diodebackward_1117_out));
  not not_466 (not_466_out, diodebackward_1117_out);
  PullUp pullup_431 (.out(diodebackward_1120_out));
  not not_467 (A2_t, diodebackward_1120_out);
  PullUp pullup_432 (.out(diodebackward_1122_out));
  not not_468 (not_468_out, diodebackward_1122_out);
  DiodeBackward diodebackward_1125 (.in(not_465_out), .out(diodebackward_1125_out));
  DiodeBackward diodebackward_1126 (.in(not_466_out), .out(diodebackward_1125_out));
  LED Q2_2 (.in(A2_t));
  PullUp pullup_433 (.out(diodebackward_1125_out));
  not not_469 (Fout_3, diodebackward_1125_out);
  PullUp pullup_434 (.out(pullup_434_out));
  not not_470 (not_470_out, pullup_434_out);
  DiodeBackward diodebackward_1127 (.in(not_473_out), .out(pullup_434_out));
  DiodeBackward diodebackward_1128 (.in(not_471_out), .out(pullup_434_out));
  PullUp pullup_435 (.out(pullup_435_out));
  DiodeBackward diodebackward_1129 (.in(not_470_out), .out(pullup_435_out));
  not not_471 (not_471_out, pullup_435_out);
  DiodeBackward diodebackward_1130 (.in(CLK_4), .out(pullup_435_out));
  DiodeBackward diodebackward_1131 (.in(nRES), .out(pullup_435_out));
  PullUp pullup_436 (.out(pullup_436_out));
  DiodeBackward diodebackward_1132 (.in(not_471_out), .out(pullup_436_out));
  not not_472 (not_472_out, pullup_436_out);
  DiodeBackward diodebackward_1133 (.in(CLK_4), .out(pullup_436_out));
  DiodeBackward diodebackward_1134 (.in(not_473_out), .out(pullup_436_out));
  PullUp pullup_437 (.out(pullup_437_out));
  DiodeBackward diodebackward_1135 (.in(not_472_out), .out(pullup_437_out));
  not not_473 (not_473_out, pullup_437_out);
  DiodeBackward diodebackward_1136 (.in(A2_t), .out(pullup_437_out));
  DiodeBackward diodebackward_1137 (.in(nRES), .out(pullup_437_out));
  PullUp pullup_438 (.out(pullup_438_out));
  DiodeBackward diodebackward_1138 (.in(not_471_out), .out(pullup_438_out));
  not not_474 (A1_t, pullup_438_out);
  DiodeBackward diodebackward_1139 (.in(not_475_out), .out(pullup_438_out));
  PullUp pullup_439 (.out(pullup_439_out));
  DiodeBackward diodebackward_1140 (.in(A1_t), .out(pullup_439_out));
  not not_475 (not_475_out, pullup_439_out);
  DiodeBackward diodebackward_1141 (.in(not_472_out), .out(pullup_439_out));
  DiodeBackward diodebackward_1142 (.in(nRES), .out(pullup_439_out));
  LED Q1_2 (.in(A1_t));
  not not_476 (not_476_out, A_9);
  not not_477 (not_477_out, B_9);
  not not_478 (not_478_out, C_4);
  not not_479 (not_479_out, nE_2);
  DiodeBackward diodebackward_1143 (.in(not_483_out), .out(diodebackward_1143_out));
  DiodeBackward diodebackward_1144 (.in(not_481_out), .out(diodebackward_1143_out));
  DiodeBackward diodebackward_1145 (.in(not_480_out), .out(diodebackward_1145_out));
  DiodeBackward diodebackward_1146 (.in(CLK_4), .out(diodebackward_1145_out));
  DiodeBackward diodebackward_1147 (.in(nRES), .out(diodebackward_1145_out));
  DiodeBackward diodebackward_1148 (.in(not_481_out), .out(diodebackward_1148_out));
  DiodeBackward diodebackward_1149 (.in(CLK_4), .out(diodebackward_1148_out));
  DiodeBackward diodebackward_1150 (.in(not_483_out), .out(diodebackward_1148_out));
  DiodeBackward diodebackward_1151 (.in(not_482_out), .out(diodebackward_1151_out));
  DiodeBackward diodebackward_1152 (.in(A1_t), .out(diodebackward_1151_out));
  DiodeBackward diodebackward_1153 (.in(nRES), .out(diodebackward_1151_out));
  DiodeBackward diodebackward_1154 (.in(not_476_out), .out(diodebackward_1154_out));
  DiodeBackward diodebackward_1155 (.in(not_477_out), .out(diodebackward_1154_out));
  DiodeBackward diodebackward_1156 (.in(not_478_out), .out(diodebackward_1154_out));
  DiodeBackward diodebackward_1157 (.in(not_479_out), .out(diodebackward_1154_out));
  DiodeBackward diodebackward_1158 (.in(A_9), .out(diodebackward_1158_out));
  DiodeBackward diodebackward_1159 (.in(not_477_out), .out(diodebackward_1158_out));
  DiodeBackward diodebackward_1160 (.in(not_478_out), .out(diodebackward_1158_out));
  DiodeBackward diodebackward_1161 (.in(not_479_out), .out(diodebackward_1158_out));
  DiodeBackward diodebackward_1162 (.in(not_476_out), .out(diodebackward_1162_out));
  DiodeBackward diodebackward_1163 (.in(B_9), .out(diodebackward_1162_out));
  DiodeBackward diodebackward_1164 (.in(not_478_out), .out(diodebackward_1162_out));
  DiodeBackward diodebackward_1165 (.in(not_479_out), .out(diodebackward_1162_out));
  DiodeBackward diodebackward_1166 (.in(A_9), .out(diodebackward_1166_out));
  DiodeBackward diodebackward_1167 (.in(B_9), .out(diodebackward_1166_out));
  DiodeBackward diodebackward_1168 (.in(not_478_out), .out(diodebackward_1166_out));
  DiodeBackward diodebackward_1169 (.in(not_479_out), .out(diodebackward_1166_out));
  DiodeBackward diodebackward_1170 (.in(not_476_out), .out(diodebackward_1170_out));
  DiodeBackward diodebackward_1171 (.in(not_477_out), .out(diodebackward_1170_out));
  DiodeBackward diodebackward_1172 (.in(C_4), .out(diodebackward_1170_out));
  DiodeBackward diodebackward_1173 (.in(not_479_out), .out(diodebackward_1170_out));
  DiodeBackward diodebackward_1174 (.in(A_9), .out(diodebackward_1174_out));
  DiodeBackward diodebackward_1175 (.in(not_477_out), .out(diodebackward_1174_out));
  DiodeBackward diodebackward_1176 (.in(C_4), .out(diodebackward_1174_out));
  DiodeBackward diodebackward_1177 (.in(not_479_out), .out(diodebackward_1174_out));
  DiodeBackward diodebackward_1178 (.in(not_476_out), .out(diodebackward_1178_out));
  DiodeBackward diodebackward_1179 (.in(B_9), .out(diodebackward_1178_out));
  DiodeBackward diodebackward_1180 (.in(C_4), .out(diodebackward_1178_out));
  DiodeBackward diodebackward_1181 (.in(not_479_out), .out(diodebackward_1178_out));
  DiodeBackward diodebackward_1182 (.in(A_9), .out(diodebackward_1182_out));
  DiodeBackward diodebackward_1183 (.in(B_9), .out(diodebackward_1182_out));
  DiodeBackward diodebackward_1184 (.in(C_4), .out(diodebackward_1182_out));
  DiodeBackward diodebackward_1185 (.in(not_479_out), .out(diodebackward_1182_out));
  PullUp pullup_440 (.out(diodebackward_1143_out));
  not not_480 (not_480_out, diodebackward_1143_out);
  PullUp pullup_441 (.out(diodebackward_1145_out));
  not not_481 (not_481_out, diodebackward_1145_out);
  PullUp pullup_442 (.out(diodebackward_1148_out));
  not not_482 (not_482_out, diodebackward_1148_out);
  PullUp pullup_443 (.out(diodebackward_1151_out));
  not not_483 (not_483_out, diodebackward_1151_out);
  PullUp pullup_444 (.out(diodebackward_1154_out));
  not not_484 (out_153, diodebackward_1154_out);
  PullUp pullup_445 (.out(diodebackward_1158_out));
  not not_485 (out_152, diodebackward_1158_out);
  PullUp pullup_446 (.out(diodebackward_1162_out));
  not not_486 (out_151, diodebackward_1162_out);
  PullUp pullup_447 (.out(diodebackward_1166_out));
  not not_487 (out_150, diodebackward_1166_out);
  PullUp pullup_448 (.out(diodebackward_1170_out));
  not not_488 (out_149, diodebackward_1170_out);
  PullUp pullup_449 (.out(diodebackward_1174_out));
  not not_489 (out_148, diodebackward_1174_out);
  PullUp pullup_450 (.out(diodebackward_1178_out));
  not not_490 (out_147, diodebackward_1178_out);
  PullUp pullup_451 (.out(diodebackward_1182_out));
  not not_491 (out_146, diodebackward_1182_out);
  DiodeBackward diodebackward_1186 (.in(out_153), .out(diodebackward_1186_out));
  DiodeBackward diodebackward_1187 (.in(out_152), .out(diodebackward_1186_out));
  DiodeBackward diodebackward_1188 (.in(out_151), .out(diodebackward_1186_out));
  DiodeBackward diodebackward_1189 (.in(out_150), .out(diodebackward_1186_out));
  DiodeBackward diodebackward_1190 (.in(out_149), .out(diodebackward_1186_out));
  DiodeBackward diodebackward_1191 (.in(out_148), .out(diodebackward_1186_out));
  DiodeBackward diodebackward_1192 (.in(out_147), .out(diodebackward_1186_out));
  DiodeBackward diodebackward_1193 (.in(out_146), .out(diodebackward_1186_out));
  DiodeBackward diodebackward_1194 (.in(not_481_out), .out(diodebackward_1194_out));
  DiodeBackward diodebackward_1195 (.in(not_494_out), .out(diodebackward_1194_out));
  DiodeBackward diodebackward_1196 (.in(A0_t), .out(diodebackward_1196_out));
  DiodeBackward diodebackward_1197 (.in(not_482_out), .out(diodebackward_1196_out));
  DiodeBackward diodebackward_1198 (.in(nRES), .out(diodebackward_1196_out));
  PullUp pullup_452 (.out(diodebackward_1186_out));
  DiodeBackward diodebackward_1199 (.in(out_153), .out(diodebackward_1199_out));
  DiodeBackward diodebackward_1200 (.in(out_152), .out(diodebackward_1199_out));
  DiodeBackward diodebackward_1201 (.in(out_151), .out(diodebackward_1199_out));
  DiodeBackward diodebackward_1202 (.in(out_150), .out(diodebackward_1199_out));
  DiodeBackward diodebackward_1203 (.in(out_149), .out(diodebackward_1199_out));
  DiodeBackward diodebackward_1204 (.in(out_148), .out(diodebackward_1199_out));
  DiodeBackward diodebackward_1205 (.in(out_147), .out(diodebackward_1199_out));
  DiodeBackward diodebackward_1206 (.in(out_146), .out(diodebackward_1199_out));
  // Not not_492 has open pins: in=diodebackward_1186_out, out=open
  PullUp pullup_453 (.out(diodebackward_1194_out));
  not not_493 (A0_t, diodebackward_1194_out);
  PullUp pullup_454 (.out(diodebackward_1196_out));
  not not_494 (not_494_out, diodebackward_1196_out);
  PullUp pullup_455 (.out(diodebackward_1199_out));
  DiodeBackward diodebackward_1207 (.in(out_153), .out(diodebackward_1207_out));
  DiodeBackward diodebackward_1208 (.in(out_152), .out(diodebackward_1207_out));
  DiodeBackward diodebackward_1209 (.in(out_151), .out(diodebackward_1207_out));
  DiodeBackward diodebackward_1210 (.in(out_150), .out(diodebackward_1207_out));
  DiodeBackward diodebackward_1211 (.in(out_149), .out(diodebackward_1207_out));
  DiodeBackward diodebackward_1212 (.in(out_148), .out(diodebackward_1207_out));
  DiodeBackward diodebackward_1213 (.in(out_147), .out(diodebackward_1207_out));
  DiodeBackward diodebackward_1214 (.in(out_146), .out(diodebackward_1207_out));
  // Not not_495 has open pins: in=diodebackward_1199_out, out=open
  LED Q0_2 (.in(A0_t));
  PullUp pullup_456 (.out(diodebackward_1207_out));
  DiodeBackward diodebackward_1215 (.in(out_153), .out(diodebackward_1215_out));
  DiodeBackward diodebackward_1216 (.in(out_152), .out(diodebackward_1215_out));
  DiodeBackward diodebackward_1217 (.in(out_151), .out(diodebackward_1215_out));
  DiodeBackward diodebackward_1218 (.in(out_150), .out(diodebackward_1215_out));
  DiodeBackward diodebackward_1219 (.in(out_149), .out(diodebackward_1215_out));
  DiodeBackward diodebackward_1220 (.in(out_148), .out(diodebackward_1215_out));
  DiodeBackward diodebackward_1221 (.in(out_147), .out(diodebackward_1215_out));
  DiodeBackward diodebackward_1222 (.in(out_146), .out(diodebackward_1215_out));
  // Not not_496 has open pins: in=diodebackward_1207_out, out=open
  PullUp pullup_457 (.out(diodebackward_1215_out));
  DiodeBackward diodebackward_1223 (.in(out_153), .out(diodebackward_1223_out));
  DiodeBackward diodebackward_1224 (.in(out_152), .out(diodebackward_1223_out));
  DiodeBackward diodebackward_1225 (.in(out_151), .out(diodebackward_1223_out));
  DiodeBackward diodebackward_1226 (.in(out_150), .out(diodebackward_1223_out));
  DiodeBackward diodebackward_1227 (.in(out_149), .out(diodebackward_1223_out));
  DiodeBackward diodebackward_1228 (.in(out_148), .out(diodebackward_1223_out));
  DiodeBackward diodebackward_1229 (.in(out_147), .out(diodebackward_1223_out));
  DiodeBackward diodebackward_1230 (.in(out_146), .out(diodebackward_1223_out));
  // Not not_497 has open pins: in=diodebackward_1215_out, out=open
  PullUp pullup_458 (.out(diodebackward_1223_out));
  DiodeBackward diodebackward_1231 (.in(out_153), .out(diodebackward_1231_out));
  DiodeBackward diodebackward_1232 (.in(out_152), .out(diodebackward_1231_out));
  DiodeBackward diodebackward_1233 (.in(out_151), .out(diodebackward_1231_out));
  DiodeBackward diodebackward_1234 (.in(out_150), .out(diodebackward_1231_out));
  DiodeBackward diodebackward_1235 (.in(out_149), .out(diodebackward_1231_out));
  DiodeBackward diodebackward_1236 (.in(out_148), .out(diodebackward_1231_out));
  DiodeBackward diodebackward_1237 (.in(out_147), .out(diodebackward_1231_out));
  DiodeBackward diodebackward_1238 (.in(out_146), .out(diodebackward_1231_out));
  // Not not_498 has open pins: in=diodebackward_1223_out, out=open
  PullUp pullup_459 (.out(diodebackward_1231_out));
  DiodeBackward diodebackward_1239 (.in(out_153), .out(diodebackward_1239_out));
  DiodeBackward diodebackward_1240 (.in(out_152), .out(diodebackward_1239_out));
  DiodeBackward diodebackward_1241 (.in(out_151), .out(diodebackward_1239_out));
  DiodeBackward diodebackward_1242 (.in(out_150), .out(diodebackward_1239_out));
  DiodeBackward diodebackward_1243 (.in(out_149), .out(diodebackward_1239_out));
  DiodeBackward diodebackward_1244 (.in(out_148), .out(diodebackward_1239_out));
  DiodeBackward diodebackward_1245 (.in(out_147), .out(diodebackward_1239_out));
  DiodeBackward diodebackward_1246 (.in(out_146), .out(diodebackward_1239_out));
  // Not not_499 has open pins: in=diodebackward_1231_out, out=open
  PullUp pullup_460 (.out(diodebackward_1239_out));
  DiodeBackward diodebackward_1247 (.in(out_153), .out(diodebackward_1247_out));
  DiodeBackward diodebackward_1248 (.in(out_152), .out(diodebackward_1247_out));
  DiodeBackward diodebackward_1249 (.in(out_151), .out(diodebackward_1247_out));
  DiodeBackward diodebackward_1250 (.in(out_150), .out(diodebackward_1247_out));
  DiodeBackward diodebackward_1251 (.in(out_149), .out(diodebackward_1247_out));
  DiodeBackward diodebackward_1252 (.in(out_148), .out(diodebackward_1247_out));
  DiodeBackward diodebackward_1253 (.in(out_147), .out(diodebackward_1247_out));
  DiodeBackward diodebackward_1254 (.in(out_146), .out(diodebackward_1247_out));
  // Not not_500 has open pins: in=diodebackward_1239_out, out=open
  PullUp pullup_461 (.out(diodebackward_1247_out));
  // Not not_501 has open pins: in=diodebackward_1247_out, out=open

  // Other names for the same wires on the sheet: B0_t = out_138; CLK_t = CLK_4; LD_CNT = nLD_COUNT

  // Notes on the sheet:
  //   nSET_3: default 1
  //   nRESET_3: default 1
  //   clk_6: Hz: 2
  //   clk_7: Hz: 2
  //   Half Adder
  //   Presettable 4-bit counter (74xx163)  60 gates
  //   Load / Inc Multiplexer
  //   D-type Flip Flop
  //   DTL Adder using AND-OR-INVERT
  //   ~S=(A.C)+(B.C)+(Cin.C)+(A.B.Cin)
  //   C=(A.B)+(A.Cin)+(B.Cin)
  //   16-bit Serialiser (21 Gates)
  //   Quad 1 of 2 selector 74xx157 / OR gate
  //   1 of 8 selector (74xx151)
  //   4 bit counter with asynchronous reset (24 gates)
  //   1 of 4 data selector with enable
  //   Fail of the Day !
  //   3 to 8 line decoder (74xx138)
  //   Edge Triggered Master-Slave Flip Flop
  //   AND-OR  / Multiplexer
  //   2 input XOR
  //   1 of 4 data selector
  //   Dual 4 input multiplexer (74xx153)
  //   Full Adder
  //   AND-OR Selector
  //   00      Zero
  //   01       XOR/ADD
  //   10      AND
  //   11      OR
  //   16 bit Shift Register (96 gates)
  //   Full Adder in 2-input NANDs
  //   AND-OR / Data Selector
  //   Full Adder (74xx80)
  //   Gated Latch
  //   SR Flip Flop
  //   Edge Triggered D-type Flip Flop (7474 equivalent)
  //   4-bit Adder
endmodule
