// Digital circuit FET_4_BIT_ALU_3.dig as structural Verilog
module FET_4_BIT_ALU_3 (
  input  B1,
  input  I2_INV,
  input  Cin,
  input  CLK,
  input  I0_XOR,
  input  I1_AND,
  input  I3_CS,
  input  B2,
  input  B3,
  input  B0,
  input  in_12,
  input  in_13,
  input  in_14,
  output Cout
);

  wire AC0, AC1, AC2, AC3, C1, C2, C3, F0, F1, F2, F3, nfet_1_d, nfet_4_d, nfet_4_s, nfet_5_s, nfet_7_d,
       nfet_7_s, nfet_8_s, nfet_10_d, nfet_10_s, nfet_11_s, nfet_13_d, nfet_13_s, nfet_14_s, nfet_16_d,
       nfet_16_s, nfet_17_s, nfet_19_d, nfet_19_s, nfet_20_s, nfet_22_d, nfet_22_s, nfet_23_s, nfet_25_d,
       nfet_25_s, nfet_26_s, nfet_36_d, nfet_40_d, nfet_41_d, nfet_42_d, nfet_43_d, nfet_48_d, nfet_49_d,
       nfet_50_d, nfet_52_s, nfet_54_s, nfet_56_s, nfet_58_s, nfet_60_s, nfet_62_s, nfet_64_s, nfet_66_s,
       nfet_70_d, nfet_71_d, nfet_72_d, nfet_73_d, nfet_74_d, nfet_75_d, nfet_82_d, nfet_83_d, nfet_84_s,
       nfet_86_s, nfet_88_s, nfet_90_s, nfet_92_s, nfet_94_s, nfet_96_s, nfet_98_d, nfet_98_s, nfet_100_s,
       nfet_102_s, nfet_104_s, nfet_106_s, nfet_111_d, nfet_112_s, nfet_114_s, nfet_116_s, nfet_118_s,
       nfet_120_d, nfet_121_d, nfet_121_s, nfet_123_d, nfet_124_d, nfet_124_s, nfet_126_d, nfet_127_d,
       nfet_127_s, nfet_129_d, nfet_129_s, nfet_131_s, nfet_133_d, nfet_134_s, nfet_141_s, nfet_144_s,
       nfet_152_s, nfet_154_s, nfet_156_s, nfet_158_s, nfet_160_d, nfet_160_s, nfet_162_d, nfet_162_s,
       nfet_164_s, nfet_166_s, nfet_168_d, nfet_168_s, nfet_170_s, nfet_172_s, nfet_174_s, nfet_176_d,
       nfet_176_s, nfet_178_d, nfet_178_s, nfet_180_d, nfet_180_s, nfet_182_s, nfet_184_s, nfet_186_d,
       nfet_186_s, nfet_188_d, nfet_189_s, nfet_196_s, nfet_198_s, nfet_200_d, nfet_200_s, nfet_202_d,
       nfet_202_s, nfet_204_s, nfet_206_s, nfet_208_s, nfet_210_s, nfet_212_d, nfet_213_s, nfet_215_d,
       nfet_216_s, nfet_218_s, nfet_220_d, nfet_220_s, nfet_224_s, nfet_226_s, pullup_1_out, pullup_3_out,
       pullup_12_out, pullup_13_out, pullup_14_out, pullup_15_out, pullup_16_out, pullup_17_out,
       pullup_18_out, pullup_19_out, pullup_28_out, pullup_29_out, pullup_30_out, pullup_31_out,
       pullup_32_out, pullup_33_out, pullup_34_out, pullup_41_out, pullup_42_out, pullup_45_out,
       pullup_46_out, pullup_47_out, pullup_53_out, pullup_54_out, pullup_55_out, pullup_57_out,
       pullup_58_out, pullup_59_out, pullup_60_out, pullup_65_out, pullup_66_out, pullup_70_out,
       pullup_72_out, pullup_81_out, pullup_83_out, pullup_85_out, pullup_86_out, pullup_88_out,
       pullup_89_out, pullup_91_out, pullup_94_out, pullup_96_out, pullup_97_out, pullup_98_out,
       pullup_99_out, pullup_100_out, pullup_101_out, pullup_102_out, pullup_103_out, pullup_104_out,
       pullup_105_out, pullup_107_out, pullup_109_out, pullup_110_out, pullup_111_out;

  NFET nfet_1 (.G(in_14), .D(nfet_1_d), .S(1'b0));
  PullUp pullup_1 (.out(pullup_1_out));
  PullUp pullup_2 (.out(nfet_1_d));
  NFET nfet_2 (.G(in_13), .D(pullup_1_out), .S(1'b0));
  PullUp pullup_3 (.out(pullup_3_out));
  NFET nfet_3 (.G(in_12), .D(pullup_3_out), .S(1'b0));
  NFET nfet_4 (.G(pullup_3_out), .D(nfet_4_d), .S(nfet_4_s));
  NFET nfet_5 (.G(pullup_1_out), .D(nfet_4_s), .S(nfet_5_s));
  NFET nfet_6 (.G(nfet_1_d), .D(nfet_5_s), .S(1'b0));
  NFET nfet_7 (.G(in_12), .D(nfet_7_d), .S(nfet_7_s));
  NFET nfet_8 (.G(pullup_1_out), .D(nfet_7_s), .S(nfet_8_s));
  NFET nfet_9 (.G(nfet_1_d), .D(nfet_8_s), .S(1'b0));
  NFET nfet_10 (.G(pullup_3_out), .D(nfet_10_d), .S(nfet_10_s));
  NFET nfet_11 (.G(in_13), .D(nfet_10_s), .S(nfet_11_s));
  NFET nfet_12 (.G(nfet_1_d), .D(nfet_11_s), .S(1'b0));
  NFET nfet_13 (.G(in_12), .D(nfet_13_d), .S(nfet_13_s));
  NFET nfet_14 (.G(in_13), .D(nfet_13_s), .S(nfet_14_s));
  NFET nfet_15 (.G(nfet_1_d), .D(nfet_14_s), .S(1'b0));
  NFET nfet_16 (.G(pullup_3_out), .D(nfet_16_d), .S(nfet_16_s));
  NFET nfet_17 (.G(pullup_1_out), .D(nfet_16_s), .S(nfet_17_s));
  NFET nfet_18 (.G(in_14), .D(nfet_17_s), .S(1'b0));
  NFET nfet_19 (.G(in_12), .D(nfet_19_d), .S(nfet_19_s));
  NFET nfet_20 (.G(pullup_1_out), .D(nfet_19_s), .S(nfet_20_s));
  NFET nfet_21 (.G(in_14), .D(nfet_20_s), .S(1'b0));
  NFET nfet_22 (.G(pullup_3_out), .D(nfet_22_d), .S(nfet_22_s));
  NFET nfet_23 (.G(in_13), .D(nfet_22_s), .S(nfet_23_s));
  NFET nfet_24 (.G(in_14), .D(nfet_23_s), .S(1'b0));
  NFET nfet_25 (.G(in_12), .D(nfet_25_d), .S(nfet_25_s));
  NFET nfet_26 (.G(in_13), .D(nfet_25_s), .S(nfet_26_s));
  NFET nfet_27 (.G(in_14), .D(nfet_26_s), .S(1'b0));
  PullUp pullup_4 (.out(nfet_4_d));
  PullUp pullup_5 (.out(nfet_7_d));
  PullUp pullup_6 (.out(nfet_10_d));
  PullUp pullup_7 (.out(nfet_13_d));
  PullUp pullup_8 (.out(nfet_16_d));
  PullUp pullup_9 (.out(nfet_19_d));
  PullUp pullup_10 (.out(nfet_22_d));
  PullUp pullup_11 (.out(nfet_25_d));
  PullUp pullup_12 (.out(pullup_12_out));
  NFET nfet_28 (.G(nfet_4_d), .D(pullup_12_out), .S(1'b0));
  PullUp pullup_13 (.out(pullup_13_out));
  NFET nfet_29 (.G(nfet_7_d), .D(pullup_13_out), .S(1'b0));
  PullUp pullup_14 (.out(pullup_14_out));
  NFET nfet_30 (.G(nfet_10_d), .D(pullup_14_out), .S(1'b0));
  PullUp pullup_15 (.out(pullup_15_out));
  NFET nfet_31 (.G(nfet_13_d), .D(pullup_15_out), .S(1'b0));
  PullUp pullup_16 (.out(pullup_16_out));
  NFET nfet_32 (.G(nfet_16_d), .D(pullup_16_out), .S(1'b0));
  PullUp pullup_17 (.out(pullup_17_out));
  NFET nfet_33 (.G(nfet_19_d), .D(pullup_17_out), .S(1'b0));
  PullUp pullup_18 (.out(pullup_18_out));
  NFET nfet_34 (.G(nfet_22_d), .D(pullup_18_out), .S(1'b0));
  PullUp pullup_19 (.out(pullup_19_out));
  NFET nfet_35 (.G(nfet_25_d), .D(pullup_19_out), .S(1'b0));
  LED led_1 (.in(pullup_12_out));
  LED led_2 (.in(pullup_13_out));
  LED led_3 (.in(pullup_14_out));
  LED led_4 (.in(pullup_15_out));
  LED led_5 (.in(pullup_16_out));
  LED led_6 (.in(pullup_17_out));
  LED led_7 (.in(pullup_18_out));
  LED led_8 (.in(pullup_19_out));
  Seven_Seg_Hex seven_seg_hex_1 (.d({F3, F2, F1, F0}), .dp(1'b0));
  Seven_Seg_Hex seven_seg_hex_2 (.d({AC3, AC2, AC1, AC0}), .dp(1'b0));
  NFET nfet_36 (.G(AC3), .D(nfet_36_d), .S(1'b0));
  PullUp pullup_20 (.out(nfet_36_d));
  NFET nfet_37 (.G(AC2), .D(nfet_36_d), .S(1'b0));
  NFET nfet_38 (.G(AC1), .D(nfet_36_d), .S(1'b0));
  Seven_Seg_Hex seven_seg_hex_3 (.d({B3, B2, B1, B0}), .dp(1'b0));
  NFET nfet_39 (.G(AC0), .D(nfet_36_d), .S(1'b0));
  LED Zero (.in(nfet_36_d));
  NFET nfet_40 (.G(B3), .D(nfet_40_d), .S(1'b0));
  NFET nfet_41 (.G(B2), .D(nfet_41_d), .S(1'b0));
  NFET nfet_42 (.G(B1), .D(nfet_42_d), .S(1'b0));
  PullUp pullup_21 (.out(nfet_40_d));
  PullUp pullup_22 (.out(nfet_41_d));
  NFET nfet_43 (.G(B0), .D(nfet_43_d), .S(1'b0));
  NFET nfet_44 (.G(I2_INV), .D(nfet_40_d), .S(1'b0));
  NFET nfet_45 (.G(I2_INV), .D(nfet_41_d), .S(1'b0));
  PullUp pullup_23 (.out(nfet_42_d));
  NFET nfet_46 (.G(I2_INV), .D(nfet_42_d), .S(1'b0));
  PullUp pullup_24 (.out(nfet_43_d));
  NFET nfet_47 (.G(I2_INV), .D(nfet_43_d), .S(1'b0));
  NFET nfet_48 (.G(nfet_40_d), .D(nfet_48_d), .S(1'b0));
  NFET nfet_49 (.G(nfet_41_d), .D(nfet_49_d), .S(1'b0));
  NFET nfet_50 (.G(nfet_42_d), .D(nfet_50_d), .S(1'b0));
  PullUp pullup_25 (.out(nfet_48_d));
  PullUp pullup_26 (.out(nfet_49_d));
  PullUp pullup_27 (.out(nfet_50_d));
  PullUp pullup_28 (.out(pullup_28_out));
  NFET nfet_51 (.G(nfet_43_d), .D(pullup_28_out), .S(1'b0));
  NFET nfet_52 (.G(B3), .D(nfet_48_d), .S(nfet_52_s));
  NFET nfet_53 (.G(I2_INV), .D(nfet_52_s), .S(1'b0));
  NFET nfet_54 (.G(B2), .D(nfet_49_d), .S(nfet_54_s));
  NFET nfet_55 (.G(I2_INV), .D(nfet_54_s), .S(1'b0));
  NFET nfet_56 (.G(B1), .D(nfet_50_d), .S(nfet_56_s));
  NFET nfet_57 (.G(I2_INV), .D(nfet_56_s), .S(1'b0));
  NFET nfet_58 (.G(B0), .D(pullup_28_out), .S(nfet_58_s));
  NFET nfet_59 (.G(I2_INV), .D(nfet_58_s), .S(1'b0));
  PullUp pullup_29 (.out(pullup_29_out));
  NFET nfet_60 (.G(AC3), .D(pullup_29_out), .S(nfet_60_s));
  NFET nfet_61 (.G(nfet_48_d), .D(nfet_60_s), .S(1'b0));
  PullUp pullup_30 (.out(pullup_30_out));
  NFET nfet_62 (.G(AC2), .D(pullup_30_out), .S(nfet_62_s));
  NFET nfet_63 (.G(nfet_49_d), .D(nfet_62_s), .S(1'b0));
  PullUp pullup_31 (.out(pullup_31_out));
  NFET nfet_64 (.G(AC1), .D(pullup_31_out), .S(nfet_64_s));
  NFET nfet_65 (.G(nfet_50_d), .D(nfet_64_s), .S(1'b0));
  PullUp pullup_32 (.out(pullup_32_out));
  NFET nfet_66 (.G(AC0), .D(pullup_32_out), .S(nfet_66_s));
  NFET nfet_67 (.G(pullup_28_out), .D(nfet_66_s), .S(1'b0));
  PullUp pullup_33 (.out(pullup_33_out));
  NFET nfet_68 (.G(pullup_29_out), .D(pullup_33_out), .S(1'b0));
  PullUp pullup_34 (.out(pullup_34_out));
  NFET nfet_69 (.G(pullup_30_out), .D(pullup_34_out), .S(1'b0));
  NFET nfet_70 (.G(pullup_31_out), .D(nfet_70_d), .S(1'b0));
  NFET nfet_71 (.G(pullup_32_out), .D(nfet_71_d), .S(1'b0));
  PullUp pullup_35 (.out(nfet_70_d));
  PullUp pullup_36 (.out(nfet_71_d));
  NFET nfet_72 (.G(AC3), .D(nfet_72_d), .S(1'b0));
  NFET nfet_73 (.G(AC2), .D(nfet_73_d), .S(1'b0));
  NFET nfet_74 (.G(AC1), .D(nfet_74_d), .S(1'b0));
  NFET nfet_75 (.G(AC0), .D(nfet_75_d), .S(1'b0));
  PullUp pullup_37 (.out(nfet_72_d));
  NFET nfet_76 (.G(nfet_48_d), .D(nfet_72_d), .S(1'b0));
  PullUp pullup_38 (.out(nfet_73_d));
  NFET nfet_77 (.G(nfet_49_d), .D(nfet_73_d), .S(1'b0));
  PullUp pullup_39 (.out(nfet_74_d));
  PullUp pullup_40 (.out(nfet_75_d));
  NFET nfet_78 (.G(nfet_50_d), .D(nfet_74_d), .S(1'b0));
  NFET nfet_79 (.G(pullup_28_out), .D(nfet_75_d), .S(1'b0));
  PullUp pullup_41 (.out(pullup_41_out));
  NFET nfet_80 (.G(nfet_72_d), .D(pullup_41_out), .S(1'b0));
  PullUp pullup_42 (.out(pullup_42_out));
  NFET nfet_81 (.G(nfet_73_d), .D(pullup_42_out), .S(1'b0));
  NFET nfet_82 (.G(nfet_74_d), .D(nfet_82_d), .S(1'b0));
  NFET nfet_83 (.G(nfet_75_d), .D(nfet_83_d), .S(1'b0));
  PullUp pullup_43 (.out(nfet_82_d));
  PullUp pullup_44 (.out(nfet_83_d));
  NFET nfet_84 (.G(AC3), .D(pullup_41_out), .S(nfet_84_s));
  NFET nfet_85 (.G(nfet_48_d), .D(nfet_84_s), .S(1'b0));
  NFET nfet_86 (.G(AC2), .D(pullup_42_out), .S(nfet_86_s));
  NFET nfet_87 (.G(nfet_49_d), .D(nfet_86_s), .S(1'b0));
  NFET nfet_88 (.G(AC1), .D(nfet_82_d), .S(nfet_88_s));
  NFET nfet_89 (.G(nfet_50_d), .D(nfet_88_s), .S(1'b0));
  NFET nfet_90 (.G(AC0), .D(nfet_83_d), .S(nfet_90_s));
  NFET nfet_91 (.G(pullup_28_out), .D(nfet_90_s), .S(1'b0));
  PullUp pullup_45 (.out(pullup_45_out));
  NFET nfet_92 (.G(I0_XOR), .D(pullup_45_out), .S(nfet_92_s));
  NFET nfet_93 (.G(pullup_41_out), .D(nfet_92_s), .S(1'b0));
  PullUp pullup_46 (.out(pullup_46_out));
  NFET nfet_94 (.G(I0_XOR), .D(pullup_46_out), .S(nfet_94_s));
  NFET nfet_95 (.G(pullup_42_out), .D(nfet_94_s), .S(1'b0));
  PullUp pullup_47 (.out(pullup_47_out));
  NFET nfet_96 (.G(I0_XOR), .D(pullup_47_out), .S(nfet_96_s));
  NFET nfet_97 (.G(nfet_82_d), .D(nfet_96_s), .S(1'b0));
  NFET nfet_98 (.G(I0_XOR), .D(nfet_98_d), .S(nfet_98_s));
  NFET nfet_99 (.G(nfet_83_d), .D(nfet_98_s), .S(1'b0));
  PullUp pullup_48 (.out(nfet_98_d));
  PullUp pullup_49 (.out(pullup_45_out));
  NFET nfet_100 (.G(I1_AND), .D(pullup_45_out), .S(nfet_100_s));
  NFET nfet_101 (.G(pullup_33_out), .D(nfet_100_s), .S(1'b0));
  PullUp pullup_50 (.out(pullup_46_out));
  NFET nfet_102 (.G(I1_AND), .D(pullup_46_out), .S(nfet_102_s));
  NFET nfet_103 (.G(pullup_34_out), .D(nfet_102_s), .S(1'b0));
  PullUp pullup_51 (.out(pullup_47_out));
  NFET nfet_104 (.G(I1_AND), .D(pullup_47_out), .S(nfet_104_s));
  NFET nfet_105 (.G(nfet_70_d), .D(nfet_104_s), .S(1'b0));
  PullUp pullup_52 (.out(nfet_98_d));
  NFET nfet_106 (.G(I1_AND), .D(nfet_98_d), .S(nfet_106_s));
  NFET nfet_107 (.G(nfet_71_d), .D(nfet_106_s), .S(1'b0));
  PullUp pullup_53 (.out(pullup_53_out));
  NFET nfet_108 (.G(pullup_45_out), .D(pullup_53_out), .S(1'b0));
  PullUp pullup_54 (.out(pullup_54_out));
  NFET nfet_109 (.G(pullup_46_out), .D(pullup_54_out), .S(1'b0));
  PullUp pullup_55 (.out(pullup_55_out));
  NFET nfet_110 (.G(pullup_47_out), .D(pullup_55_out), .S(1'b0));
  NFET nfet_111 (.G(nfet_98_d), .D(nfet_111_d), .S(1'b0));
  PullUp pullup_56 (.out(nfet_111_d));
  PullUp pullup_57 (.out(pullup_57_out));
  NFET nfet_112 (.G(pullup_53_out), .D(pullup_57_out), .S(nfet_112_s));
  NFET nfet_113 (.G(C3), .D(nfet_112_s), .S(1'b0));
  PullUp pullup_58 (.out(pullup_58_out));
  NFET nfet_114 (.G(pullup_54_out), .D(pullup_58_out), .S(nfet_114_s));
  NFET nfet_115 (.G(C2), .D(nfet_114_s), .S(1'b0));
  PullUp pullup_59 (.out(pullup_59_out));
  NFET nfet_116 (.G(pullup_55_out), .D(pullup_59_out), .S(nfet_116_s));
  NFET nfet_117 (.G(C1), .D(nfet_116_s), .S(1'b0));
  PullUp pullup_60 (.out(pullup_60_out));
  NFET nfet_118 (.G(nfet_111_d), .D(pullup_60_out), .S(nfet_118_s));
  NFET nfet_119 (.G(Cin), .D(nfet_118_s), .S(1'b0));
  NFET nfet_120 (.G(pullup_53_out), .D(nfet_120_d), .S(1'b0));
  NFET nfet_121 (.G(pullup_57_out), .D(nfet_121_d), .S(nfet_121_s));
  NFET nfet_122 (.G(pullup_29_out), .D(nfet_121_s), .S(1'b0));
  NFET nfet_123 (.G(pullup_54_out), .D(nfet_123_d), .S(1'b0));
  NFET nfet_124 (.G(pullup_58_out), .D(nfet_124_d), .S(nfet_124_s));
  NFET nfet_125 (.G(pullup_30_out), .D(nfet_124_s), .S(1'b0));
  NFET nfet_126 (.G(pullup_55_out), .D(nfet_126_d), .S(1'b0));
  PullUp pullup_61 (.out(nfet_120_d));
  PullUp pullup_62 (.out(nfet_121_d));
  NFET nfet_127 (.G(nfet_121_d), .D(nfet_127_d), .S(nfet_127_s));
  NFET nfet_128 (.G(I3_CS), .D(nfet_127_s), .S(1'b0));
  PullUp pullup_63 (.out(nfet_123_d));
  PullUp pullup_64 (.out(nfet_124_d));
  NFET nfet_129 (.G(nfet_124_d), .D(nfet_129_d), .S(nfet_129_s));
  NFET nfet_130 (.G(I3_CS), .D(nfet_129_s), .S(1'b0));
  PullUp pullup_65 (.out(pullup_65_out));
  NFET nfet_131 (.G(pullup_59_out), .D(pullup_65_out), .S(nfet_131_s));
  NFET nfet_132 (.G(pullup_31_out), .D(nfet_131_s), .S(1'b0));
  NFET nfet_133 (.G(nfet_111_d), .D(nfet_133_d), .S(1'b0));
  PullUp pullup_66 (.out(pullup_66_out));
  NFET nfet_134 (.G(pullup_60_out), .D(pullup_66_out), .S(nfet_134_s));
  NFET nfet_135 (.G(pullup_32_out), .D(nfet_134_s), .S(1'b0));
  NFET nfet_136 (.G(C3), .D(nfet_120_d), .S(1'b0));
  NFET nfet_137 (.G(nfet_127_d), .D(Cout), .S(1'b0));
  PullUp pullup_67 (.out(nfet_127_d));
  NFET nfet_138 (.G(C2), .D(nfet_123_d), .S(1'b0));
  NFET nfet_139 (.G(nfet_129_d), .D(C3), .S(1'b0));
  PullUp pullup_68 (.out(nfet_129_d));
  PullUp pullup_69 (.out(nfet_126_d));
  NFET nfet_140 (.G(C1), .D(nfet_126_d), .S(1'b0));
  PullUp pullup_70 (.out(pullup_70_out));
  NFET nfet_141 (.G(pullup_65_out), .D(pullup_70_out), .S(nfet_141_s));
  NFET nfet_142 (.G(I3_CS), .D(nfet_141_s), .S(1'b0));
  PullUp pullup_71 (.out(nfet_133_d));
  NFET nfet_143 (.G(Cin), .D(nfet_133_d), .S(1'b0));
  PullUp pullup_72 (.out(pullup_72_out));
  NFET nfet_144 (.G(pullup_66_out), .D(pullup_72_out), .S(nfet_144_s));
  NFET nfet_145 (.G(I3_CS), .D(nfet_144_s), .S(1'b0));
  NFET nfet_146 (.G(nfet_120_d), .D(F3), .S(1'b0));
  PullUp pullup_73 (.out(Cout));
  NFET nfet_147 (.G(nfet_123_d), .D(F2), .S(1'b0));
  PullUp pullup_74 (.out(C3));
  NFET nfet_148 (.G(nfet_126_d), .D(F1), .S(1'b0));
  PullUp pullup_75 (.out(C2));
  NFET nfet_149 (.G(pullup_70_out), .D(C2), .S(1'b0));
  NFET nfet_150 (.G(pullup_72_out), .D(C1), .S(1'b0));
  NFET nfet_151 (.G(nfet_133_d), .D(F0), .S(1'b0));
  PullUp pullup_76 (.out(C1));
  PullUp pullup_77 (.out(F3));
  PullUp pullup_78 (.out(F2));
  PullUp pullup_79 (.out(F1));
  PullUp pullup_80 (.out(F0));
  NFET nfet_152 (.G(pullup_53_out), .D(F3), .S(nfet_152_s));
  NFET nfet_153 (.G(C3), .D(nfet_152_s), .S(1'b0));
  NFET nfet_154 (.G(pullup_54_out), .D(F2), .S(nfet_154_s));
  NFET nfet_155 (.G(C2), .D(nfet_154_s), .S(1'b0));
  NFET nfet_156 (.G(pullup_55_out), .D(F1), .S(nfet_156_s));
  NFET nfet_157 (.G(C1), .D(nfet_156_s), .S(1'b0));
  NFET nfet_158 (.G(nfet_111_d), .D(F0), .S(nfet_158_s));
  NFET nfet_159 (.G(Cin), .D(nfet_158_s), .S(1'b0));
  NFET nfet_160 (.G(CLK), .D(nfet_160_d), .S(nfet_160_s));
  NFET nfet_161 (.G(nfet_176_d), .D(nfet_160_s), .S(1'b0));
  NFET nfet_162 (.G(CLK), .D(nfet_162_d), .S(nfet_162_s));
  NFET nfet_163 (.G(nfet_178_d), .D(nfet_162_s), .S(1'b0));
  PullUp pullup_81 (.out(pullup_81_out));
  NFET nfet_164 (.G(pullup_89_out), .D(pullup_81_out), .S(nfet_164_s));
  PullUp pullup_82 (.out(nfet_160_d));
  NFET nfet_165 (.G(nfet_160_d), .D(nfet_164_s), .S(1'b0));
  PullUp pullup_83 (.out(pullup_83_out));
  NFET nfet_166 (.G(pullup_91_out), .D(pullup_83_out), .S(nfet_166_s));
  PullUp pullup_84 (.out(nfet_162_d));
  NFET nfet_167 (.G(nfet_162_d), .D(nfet_166_s), .S(1'b0));
  NFET nfet_168 (.G(nfet_186_d), .D(nfet_168_d), .S(nfet_168_s));
  PullUp pullup_85 (.out(pullup_85_out));
  NFET nfet_169 (.G(pullup_85_out), .D(nfet_168_s), .S(1'b0));
  NFET nfet_170 (.G(CLK), .D(pullup_85_out), .S(nfet_170_s));
  NFET nfet_171 (.G(nfet_180_d), .D(nfet_170_s), .S(1'b0));
  PullUp pullup_86 (.out(pullup_86_out));
  NFET nfet_172 (.G(CLK), .D(pullup_86_out), .S(nfet_172_s));
  NFET nfet_173 (.G(pullup_94_out), .D(nfet_172_s), .S(1'b0));
  PullUp pullup_87 (.out(nfet_168_d));
  PullUp pullup_88 (.out(pullup_88_out));
  NFET nfet_174 (.G(pullup_96_out), .D(pullup_88_out), .S(nfet_174_s));
  NFET nfet_175 (.G(pullup_86_out), .D(nfet_174_s), .S(1'b0));
  NFET nfet_176 (.G(CLK), .D(nfet_176_d), .S(nfet_176_s));
  NFET nfet_177 (.G(F3), .D(nfet_176_s), .S(1'b0));
  NFET nfet_178 (.G(CLK), .D(nfet_178_d), .S(nfet_178_s));
  NFET nfet_179 (.G(F2), .D(nfet_178_s), .S(1'b0));
  NFET nfet_180 (.G(CLK), .D(nfet_180_d), .S(nfet_180_s));
  NFET nfet_181 (.G(F1), .D(nfet_180_s), .S(1'b0));
  PullUp pullup_89 (.out(pullup_89_out));
  NFET nfet_182 (.G(pullup_81_out), .D(pullup_89_out), .S(nfet_182_s));
  PullUp pullup_90 (.out(nfet_176_d));
  NFET nfet_183 (.G(nfet_176_d), .D(nfet_182_s), .S(1'b0));
  PullUp pullup_91 (.out(pullup_91_out));
  NFET nfet_184 (.G(pullup_83_out), .D(pullup_91_out), .S(nfet_184_s));
  PullUp pullup_92 (.out(nfet_178_d));
  NFET nfet_185 (.G(nfet_178_d), .D(nfet_184_s), .S(1'b0));
  NFET nfet_186 (.G(nfet_168_d), .D(nfet_186_d), .S(nfet_186_s));
  PullUp pullup_93 (.out(nfet_180_d));
  NFET nfet_187 (.G(nfet_180_d), .D(nfet_186_s), .S(1'b0));
  PullUp pullup_94 (.out(pullup_94_out));
  NFET nfet_188 (.G(pullup_94_out), .D(nfet_188_d), .S(1'b0));
  NFET nfet_189 (.G(CLK), .D(pullup_94_out), .S(nfet_189_s));
  NFET nfet_190 (.G(F0), .D(nfet_189_s), .S(1'b0));
  PullUp pullup_95 (.out(nfet_186_d));
  PullUp pullup_96 (.out(pullup_96_out));
  NFET nfet_191 (.G(pullup_88_out), .D(pullup_96_out), .S(nfet_188_d));
  PullUp pullup_97 (.out(pullup_97_out));
  NFET nfet_192 (.G(CLK), .D(pullup_97_out), .S(1'b0));
  PullUp pullup_98 (.out(pullup_98_out));
  NFET nfet_193 (.G(CLK), .D(pullup_98_out), .S(1'b0));
  PullUp pullup_99 (.out(pullup_99_out));
  NFET nfet_194 (.G(CLK), .D(pullup_99_out), .S(1'b0));
  PullUp pullup_100 (.out(pullup_100_out));
  NFET nfet_195 (.G(CLK), .D(pullup_100_out), .S(1'b0));
  PullUp pullup_101 (.out(pullup_101_out));
  NFET nfet_196 (.G(pullup_97_out), .D(pullup_101_out), .S(nfet_196_s));
  NFET nfet_197 (.G(pullup_81_out), .D(nfet_196_s), .S(1'b0));
  PullUp pullup_102 (.out(pullup_102_out));
  NFET nfet_198 (.G(pullup_98_out), .D(pullup_102_out), .S(nfet_198_s));
  NFET nfet_199 (.G(pullup_83_out), .D(nfet_198_s), .S(1'b0));
  NFET nfet_200 (.G(pullup_99_out), .D(nfet_200_d), .S(nfet_200_s));
  NFET nfet_201 (.G(nfet_168_d), .D(nfet_200_s), .S(1'b0));
  NFET nfet_202 (.G(pullup_100_out), .D(nfet_202_d), .S(nfet_202_s));
  NFET nfet_203 (.G(pullup_88_out), .D(nfet_202_s), .S(1'b0));
  PullUp pullup_103 (.out(pullup_103_out));
  NFET nfet_204 (.G(AC3), .D(pullup_103_out), .S(nfet_204_s));
  NFET nfet_205 (.G(pullup_101_out), .D(nfet_204_s), .S(1'b0));
  PullUp pullup_104 (.out(pullup_104_out));
  NFET nfet_206 (.G(AC2), .D(pullup_104_out), .S(nfet_206_s));
  NFET nfet_207 (.G(pullup_102_out), .D(nfet_206_s), .S(1'b0));
  PullUp pullup_105 (.out(pullup_105_out));
  NFET nfet_208 (.G(AC1), .D(pullup_105_out), .S(nfet_208_s));
  PullUp pullup_106 (.out(nfet_200_d));
  NFET nfet_209 (.G(nfet_200_d), .D(nfet_208_s), .S(1'b0));
  PullUp pullup_107 (.out(pullup_107_out));
  NFET nfet_210 (.G(AC0), .D(pullup_107_out), .S(nfet_210_s));
  PullUp pullup_108 (.out(nfet_202_d));
  NFET nfet_211 (.G(nfet_202_d), .D(nfet_210_s), .S(1'b0));
  PullUp pullup_109 (.out(pullup_109_out));
  NFET nfet_212 (.G(pullup_109_out), .D(nfet_212_d), .S(1'b0));
  NFET nfet_213 (.G(pullup_97_out), .D(pullup_109_out), .S(nfet_213_s));
  NFET nfet_214 (.G(pullup_89_out), .D(nfet_213_s), .S(1'b0));
  PullUp pullup_110 (.out(pullup_110_out));
  NFET nfet_215 (.G(pullup_110_out), .D(nfet_215_d), .S(1'b0));
  NFET nfet_216 (.G(pullup_98_out), .D(pullup_110_out), .S(nfet_216_s));
  NFET nfet_217 (.G(pullup_91_out), .D(nfet_216_s), .S(1'b0));
  PullUp pullup_111 (.out(pullup_111_out));
  NFET nfet_218 (.G(pullup_99_out), .D(pullup_111_out), .S(nfet_218_s));
  NFET nfet_219 (.G(nfet_186_d), .D(nfet_218_s), .S(1'b0));
  NFET nfet_220 (.G(pullup_100_out), .D(nfet_220_d), .S(nfet_220_s));
  NFET nfet_221 (.G(pullup_96_out), .D(nfet_220_s), .S(1'b0));
  PullUp pullup_112 (.out(AC3));
  NFET nfet_222 (.G(pullup_103_out), .D(AC3), .S(nfet_212_d));
  PullUp pullup_113 (.out(AC2));
  NFET nfet_223 (.G(pullup_104_out), .D(AC2), .S(nfet_215_d));
  PullUp pullup_114 (.out(AC1));
  NFET nfet_224 (.G(pullup_105_out), .D(AC1), .S(nfet_224_s));
  NFET nfet_225 (.G(pullup_111_out), .D(nfet_224_s), .S(1'b0));
  PullUp pullup_115 (.out(AC0));
  NFET nfet_226 (.G(pullup_107_out), .D(AC0), .S(nfet_226_s));
  PullUp pullup_116 (.out(nfet_220_d));
  NFET nfet_227 (.G(nfet_220_d), .D(nfet_226_s), .S(1'b0));

  // Other names for the same wires on the sheet: C4 = Cout

  // Notes on the sheet:
  //   ALU
  //   ACC
  //   BUS
endmodule
