// Digital circuit FET_ALU_2.dig as structural Verilog
module FET_ALU_2 (
  input  B1,
  input  I2_INV,
  input  C0in,
  input  CLKin,
  input  I0,
  input  I1,
  input  I3_CS,
  input  B2,
  input  B3,
  input  B0,
  output Cout
);

  wire AC0, AC1, AC2, AC3, C1, C2, C3, F0, F1, F2, F3, nfet_1_d, nfet_2_d, nfet_3_d, nfet_4_d, nfet_9_d,
       nfet_10_d, nfet_11_d, nfet_13_s, nfet_15_s, nfet_17_s, nfet_19_s, nfet_21_s, nfet_23_s, nfet_25_s,
       nfet_27_s, nfet_31_d, nfet_32_d, nfet_33_d, nfet_34_d, nfet_35_d, nfet_36_d, nfet_43_d, nfet_44_d,
       nfet_45_s, nfet_47_s, nfet_49_s, nfet_51_s, nfet_53_s, nfet_55_s, nfet_57_s, nfet_59_s, nfet_61_d,
       nfet_62_d, nfet_62_s, nfet_64_d, nfet_65_d, nfet_65_s, nfet_67_d, nfet_68_s, nfet_70_s, nfet_72_s,
       nfet_74_d, nfet_75_s, nfet_80_s, nfet_83_s, nfet_85_d, nfet_86_d, nfet_87_d, nfet_88_d, nfet_89_s,
       nfet_91_s, nfet_93_s, nfet_95_s, nfet_97_d, nfet_97_s, nfet_99_s, nfet_101_s, nfet_103_s, nfet_105_s,
       nfet_107_s, nfet_109_s, nfet_112_s, nfet_117_s, nfet_119_s, nfet_121_d, nfet_121_s, nfet_123_d,
       nfet_123_s, nfet_125_s, nfet_127_s, nfet_129_s, nfet_131_s, nfet_133_d, nfet_134_s, nfet_136_d,
       nfet_137_s, nfet_139_s, nfet_141_d, nfet_141_s, nfet_145_s, nfet_147_s, nfet_151_d, nfet_152_d,
       nfet_152_s, nfet_154_d, nfet_154_s, nfet_157_s, nfet_159_s, nfet_161_d, nfet_161_s, nfet_163_s,
       nfet_165_s, nfet_167_s, nfet_169_d, nfet_169_s, nfet_171_d, nfet_171_s, nfet_173_d, nfet_173_s,
       nfet_175_s, nfet_177_s, nfet_179_s, nfet_181_d, nfet_182_s, pullup_8_out, pullup_9_out, pullup_10_out,
       pullup_11_out, pullup_12_out, pullup_13_out, pullup_14_out, pullup_21_out, pullup_22_out,
       pullup_26_out, pullup_27_out, pullup_28_out, pullup_29_out, pullup_34_out, pullup_35_out,
       pullup_46_out, pullup_47_out, pullup_49_out, pullup_58_out, pullup_59_out, pullup_60_out,
       pullup_61_out, pullup_62_out, pullup_64_out, pullup_66_out, pullup_67_out, pullup_68_out,
       pullup_69_out, pullup_70_out, pullup_71_out, pullup_72_out, pullup_74_out, pullup_75_out,
       pullup_77_out, pullup_78_out, pullup_80_out, pullup_82_out, pullup_83_out, pullup_85_out,
       pullup_91_out;

  Seven_Seg_Hex seven_seg_hex_1 (.d({F3, F2, F1, F0}), .dp(1'b0));
  Seven_Seg_Hex seven_seg_hex_2 (.d({AC3, AC2, AC1, AC0}), .dp(1'b0));
  Seven_Seg_Hex seven_seg_hex_3 (.d({B3, B2, B1, B0}), .dp(1'b0));
  NFET nfet_1 (.G(B3), .D(nfet_1_d), .S(1'b0));
  NFET nfet_2 (.G(B2), .D(nfet_2_d), .S(1'b0));
  NFET nfet_3 (.G(B1), .D(nfet_3_d), .S(1'b0));
  PullUp pullup_1 (.out(nfet_1_d));
  PullUp pullup_2 (.out(nfet_2_d));
  NFET nfet_4 (.G(B0), .D(nfet_4_d), .S(1'b0));
  NFET nfet_5 (.G(I2_INV), .D(nfet_1_d), .S(1'b0));
  NFET nfet_6 (.G(I2_INV), .D(nfet_2_d), .S(1'b0));
  PullUp pullup_3 (.out(nfet_3_d));
  NFET nfet_7 (.G(I2_INV), .D(nfet_3_d), .S(1'b0));
  PullUp pullup_4 (.out(nfet_4_d));
  NFET nfet_8 (.G(I2_INV), .D(nfet_4_d), .S(1'b0));
  NFET nfet_9 (.G(nfet_1_d), .D(nfet_9_d), .S(1'b0));
  NFET nfet_10 (.G(nfet_2_d), .D(nfet_10_d), .S(1'b0));
  NFET nfet_11 (.G(nfet_3_d), .D(nfet_11_d), .S(1'b0));
  PullUp pullup_5 (.out(nfet_9_d));
  PullUp pullup_6 (.out(nfet_10_d));
  PullUp pullup_7 (.out(nfet_11_d));
  PullUp pullup_8 (.out(pullup_8_out));
  NFET nfet_12 (.G(nfet_4_d), .D(pullup_8_out), .S(1'b0));
  NFET nfet_13 (.G(B3), .D(nfet_9_d), .S(nfet_13_s));
  NFET nfet_14 (.G(I2_INV), .D(nfet_13_s), .S(1'b0));
  NFET nfet_15 (.G(B2), .D(nfet_10_d), .S(nfet_15_s));
  NFET nfet_16 (.G(I2_INV), .D(nfet_15_s), .S(1'b0));
  NFET nfet_17 (.G(B1), .D(nfet_11_d), .S(nfet_17_s));
  NFET nfet_18 (.G(I2_INV), .D(nfet_17_s), .S(1'b0));
  NFET nfet_19 (.G(B0), .D(pullup_8_out), .S(nfet_19_s));
  NFET nfet_20 (.G(I2_INV), .D(nfet_19_s), .S(1'b0));
  PullUp pullup_9 (.out(pullup_9_out));
  NFET nfet_21 (.G(AC3), .D(pullup_9_out), .S(nfet_21_s));
  NFET nfet_22 (.G(nfet_9_d), .D(nfet_21_s), .S(1'b0));
  PullUp pullup_10 (.out(pullup_10_out));
  NFET nfet_23 (.G(AC2), .D(pullup_10_out), .S(nfet_23_s));
  NFET nfet_24 (.G(nfet_10_d), .D(nfet_23_s), .S(1'b0));
  PullUp pullup_11 (.out(pullup_11_out));
  NFET nfet_25 (.G(AC1), .D(pullup_11_out), .S(nfet_25_s));
  NFET nfet_26 (.G(nfet_11_d), .D(nfet_25_s), .S(1'b0));
  PullUp pullup_12 (.out(pullup_12_out));
  NFET nfet_27 (.G(AC0), .D(pullup_12_out), .S(nfet_27_s));
  NFET nfet_28 (.G(pullup_8_out), .D(nfet_27_s), .S(1'b0));
  PullUp pullup_13 (.out(pullup_13_out));
  NFET nfet_29 (.G(pullup_9_out), .D(pullup_13_out), .S(1'b0));
  PullUp pullup_14 (.out(pullup_14_out));
  NFET nfet_30 (.G(pullup_10_out), .D(pullup_14_out), .S(1'b0));
  NFET nfet_31 (.G(pullup_11_out), .D(nfet_31_d), .S(1'b0));
  NFET nfet_32 (.G(pullup_12_out), .D(nfet_32_d), .S(1'b0));
  PullUp pullup_15 (.out(nfet_31_d));
  PullUp pullup_16 (.out(nfet_32_d));
  NFET nfet_33 (.G(AC3), .D(nfet_33_d), .S(1'b0));
  NFET nfet_34 (.G(AC2), .D(nfet_34_d), .S(1'b0));
  NFET nfet_35 (.G(AC1), .D(nfet_35_d), .S(1'b0));
  NFET nfet_36 (.G(AC0), .D(nfet_36_d), .S(1'b0));
  PullUp pullup_17 (.out(nfet_33_d));
  NFET nfet_37 (.G(nfet_9_d), .D(nfet_33_d), .S(1'b0));
  PullUp pullup_18 (.out(nfet_34_d));
  NFET nfet_38 (.G(nfet_10_d), .D(nfet_34_d), .S(1'b0));
  PullUp pullup_19 (.out(nfet_35_d));
  PullUp pullup_20 (.out(nfet_36_d));
  NFET nfet_39 (.G(nfet_11_d), .D(nfet_35_d), .S(1'b0));
  NFET nfet_40 (.G(pullup_8_out), .D(nfet_36_d), .S(1'b0));
  PullUp pullup_21 (.out(pullup_21_out));
  NFET nfet_41 (.G(nfet_33_d), .D(pullup_21_out), .S(1'b0));
  PullUp pullup_22 (.out(pullup_22_out));
  NFET nfet_42 (.G(nfet_34_d), .D(pullup_22_out), .S(1'b0));
  NFET nfet_43 (.G(nfet_35_d), .D(nfet_43_d), .S(1'b0));
  NFET nfet_44 (.G(nfet_36_d), .D(nfet_44_d), .S(1'b0));
  PullUp pullup_23 (.out(nfet_43_d));
  PullUp pullup_24 (.out(nfet_44_d));
  NFET nfet_45 (.G(AC3), .D(pullup_21_out), .S(nfet_45_s));
  NFET nfet_46 (.G(nfet_9_d), .D(nfet_45_s), .S(1'b0));
  NFET nfet_47 (.G(AC2), .D(pullup_22_out), .S(nfet_47_s));
  NFET nfet_48 (.G(nfet_10_d), .D(nfet_47_s), .S(1'b0));
  NFET nfet_49 (.G(AC1), .D(nfet_43_d), .S(nfet_49_s));
  NFET nfet_50 (.G(nfet_11_d), .D(nfet_49_s), .S(1'b0));
  NFET nfet_51 (.G(AC0), .D(nfet_44_d), .S(nfet_51_s));
  NFET nfet_52 (.G(pullup_8_out), .D(nfet_51_s), .S(1'b0));
  PullUp pullup_25 (.out(pullup_21_out));
  PullUp pullup_26 (.out(pullup_26_out));
  NFET nfet_53 (.G(pullup_21_out), .D(pullup_26_out), .S(nfet_53_s));
  NFET nfet_54 (.G(C3), .D(nfet_53_s), .S(1'b0));
  PullUp pullup_27 (.out(pullup_27_out));
  NFET nfet_55 (.G(pullup_22_out), .D(pullup_27_out), .S(nfet_55_s));
  NFET nfet_56 (.G(C2), .D(nfet_55_s), .S(1'b0));
  PullUp pullup_28 (.out(pullup_28_out));
  NFET nfet_57 (.G(nfet_43_d), .D(pullup_28_out), .S(nfet_57_s));
  NFET nfet_58 (.G(C1), .D(nfet_57_s), .S(1'b0));
  PullUp pullup_29 (.out(pullup_29_out));
  NFET nfet_59 (.G(nfet_44_d), .D(pullup_29_out), .S(nfet_59_s));
  NFET nfet_60 (.G(C0in), .D(nfet_59_s), .S(1'b0));
  NFET nfet_61 (.G(pullup_21_out), .D(nfet_61_d), .S(1'b0));
  NFET nfet_62 (.G(pullup_26_out), .D(nfet_62_d), .S(nfet_62_s));
  NFET nfet_63 (.G(pullup_9_out), .D(nfet_62_s), .S(1'b0));
  NFET nfet_64 (.G(pullup_22_out), .D(nfet_64_d), .S(1'b0));
  NFET nfet_65 (.G(pullup_27_out), .D(nfet_65_d), .S(nfet_65_s));
  NFET nfet_66 (.G(pullup_10_out), .D(nfet_65_s), .S(1'b0));
  NFET nfet_67 (.G(nfet_43_d), .D(nfet_67_d), .S(1'b0));
  PullUp pullup_30 (.out(nfet_61_d));
  PullUp pullup_31 (.out(nfet_62_d));
  NFET nfet_68 (.G(nfet_62_d), .D(Cout), .S(nfet_68_s));
  NFET nfet_69 (.G(I3_CS), .D(nfet_68_s), .S(1'b0));
  PullUp pullup_32 (.out(nfet_64_d));
  PullUp pullup_33 (.out(nfet_65_d));
  NFET nfet_70 (.G(nfet_65_d), .D(C3), .S(nfet_70_s));
  NFET nfet_71 (.G(I3_CS), .D(nfet_70_s), .S(1'b0));
  PullUp pullup_34 (.out(pullup_34_out));
  NFET nfet_72 (.G(pullup_28_out), .D(pullup_34_out), .S(nfet_72_s));
  NFET nfet_73 (.G(pullup_11_out), .D(nfet_72_s), .S(1'b0));
  NFET nfet_74 (.G(nfet_44_d), .D(nfet_74_d), .S(1'b0));
  PullUp pullup_35 (.out(pullup_35_out));
  NFET nfet_75 (.G(pullup_29_out), .D(pullup_35_out), .S(nfet_75_s));
  NFET nfet_76 (.G(pullup_12_out), .D(nfet_75_s), .S(1'b0));
  NFET nfet_77 (.G(C3), .D(nfet_61_d), .S(1'b0));
  PullUp pullup_36 (.out(Cout));
  NFET nfet_78 (.G(C2), .D(nfet_64_d), .S(1'b0));
  PullUp pullup_37 (.out(C3));
  PullUp pullup_38 (.out(nfet_67_d));
  NFET nfet_79 (.G(C1), .D(nfet_67_d), .S(1'b0));
  PullUp pullup_39 (.out(C2));
  NFET nfet_80 (.G(pullup_34_out), .D(C2), .S(nfet_80_s));
  NFET nfet_81 (.G(I3_CS), .D(nfet_80_s), .S(1'b0));
  PullUp pullup_40 (.out(nfet_74_d));
  NFET nfet_82 (.G(C0in), .D(nfet_74_d), .S(1'b0));
  PullUp pullup_41 (.out(C1));
  NFET nfet_83 (.G(pullup_35_out), .D(C1), .S(nfet_83_s));
  NFET nfet_84 (.G(I3_CS), .D(nfet_83_s), .S(1'b0));
  NFET nfet_85 (.G(nfet_61_d), .D(nfet_85_d), .S(1'b0));
  NFET nfet_86 (.G(nfet_64_d), .D(nfet_86_d), .S(1'b0));
  NFET nfet_87 (.G(nfet_67_d), .D(nfet_87_d), .S(1'b0));
  NFET nfet_88 (.G(nfet_74_d), .D(nfet_88_d), .S(1'b0));
  PullUp pullup_42 (.out(nfet_85_d));
  PullUp pullup_43 (.out(nfet_86_d));
  PullUp pullup_44 (.out(nfet_87_d));
  PullUp pullup_45 (.out(nfet_88_d));
  NFET nfet_89 (.G(pullup_21_out), .D(nfet_85_d), .S(nfet_89_s));
  NFET nfet_90 (.G(C3), .D(nfet_89_s), .S(1'b0));
  NFET nfet_91 (.G(pullup_22_out), .D(nfet_86_d), .S(nfet_91_s));
  NFET nfet_92 (.G(C2), .D(nfet_91_s), .S(1'b0));
  NFET nfet_93 (.G(nfet_43_d), .D(nfet_87_d), .S(nfet_93_s));
  NFET nfet_94 (.G(C1), .D(nfet_93_s), .S(1'b0));
  NFET nfet_95 (.G(nfet_44_d), .D(nfet_88_d), .S(nfet_95_s));
  NFET nfet_96 (.G(C0in), .D(nfet_95_s), .S(1'b0));
  NFET nfet_97 (.G(nfet_87_d), .D(nfet_97_d), .S(nfet_97_s));
  NFET nfet_98 (.G(I0), .D(nfet_97_s), .S(1'b0));
  PullUp pullup_46 (.out(pullup_46_out));
  NFET nfet_99 (.G(nfet_85_d), .D(pullup_46_out), .S(nfet_99_s));
  NFET nfet_100 (.G(I0), .D(nfet_99_s), .S(1'b0));
  PullUp pullup_47 (.out(pullup_47_out));
  NFET nfet_101 (.G(nfet_86_d), .D(pullup_47_out), .S(nfet_101_s));
  NFET nfet_102 (.G(I0), .D(nfet_101_s), .S(1'b0));
  PullUp pullup_48 (.out(nfet_97_d));
  PullUp pullup_49 (.out(pullup_49_out));
  NFET nfet_103 (.G(nfet_88_d), .D(pullup_49_out), .S(nfet_103_s));
  NFET nfet_104 (.G(I0), .D(nfet_103_s), .S(1'b0));
  PullUp pullup_50 (.out(nfet_97_d));
  NFET nfet_105 (.G(nfet_31_d), .D(nfet_97_d), .S(nfet_105_s));
  NFET nfet_106 (.G(I1), .D(nfet_105_s), .S(1'b0));
  PullUp pullup_51 (.out(pullup_46_out));
  NFET nfet_107 (.G(pullup_13_out), .D(pullup_46_out), .S(nfet_107_s));
  NFET nfet_108 (.G(I1), .D(nfet_107_s), .S(1'b0));
  PullUp pullup_52 (.out(pullup_47_out));
  NFET nfet_109 (.G(pullup_14_out), .D(pullup_47_out), .S(nfet_109_s));
  NFET nfet_110 (.G(I1), .D(nfet_109_s), .S(1'b0));
  NFET nfet_111 (.G(nfet_97_d), .D(F1), .S(1'b0));
  PullUp pullup_53 (.out(pullup_49_out));
  NFET nfet_112 (.G(nfet_32_d), .D(pullup_49_out), .S(nfet_112_s));
  NFET nfet_113 (.G(I1), .D(nfet_112_s), .S(1'b0));
  PullUp pullup_54 (.out(F3));
  NFET nfet_114 (.G(pullup_46_out), .D(F3), .S(1'b0));
  PullUp pullup_55 (.out(F2));
  NFET nfet_115 (.G(pullup_47_out), .D(F2), .S(1'b0));
  PullUp pullup_56 (.out(F1));
  PullUp pullup_57 (.out(F0));
  NFET nfet_116 (.G(pullup_49_out), .D(F0), .S(1'b0));
  PullUp pullup_58 (.out(pullup_58_out));
  NFET nfet_117 (.G(CLKin), .D(pullup_58_out), .S(nfet_117_s));
  NFET nfet_118 (.G(pullup_66_out), .D(nfet_117_s), .S(1'b0));
  PullUp pullup_59 (.out(pullup_59_out));
  NFET nfet_119 (.G(CLKin), .D(pullup_59_out), .S(nfet_119_s));
  NFET nfet_120 (.G(pullup_67_out), .D(nfet_119_s), .S(1'b0));
  NFET nfet_121 (.G(CLKin), .D(nfet_121_d), .S(nfet_121_s));
  NFET nfet_122 (.G(pullup_68_out), .D(nfet_121_s), .S(1'b0));
  NFET nfet_123 (.G(CLKin), .D(nfet_123_d), .S(nfet_123_s));
  NFET nfet_124 (.G(nfet_141_d), .D(nfet_123_s), .S(1'b0));
  PullUp pullup_60 (.out(pullup_60_out));
  NFET nfet_125 (.G(pullup_69_out), .D(pullup_60_out), .S(nfet_125_s));
  NFET nfet_126 (.G(pullup_58_out), .D(nfet_125_s), .S(1'b0));
  PullUp pullup_61 (.out(pullup_61_out));
  NFET nfet_127 (.G(pullup_70_out), .D(pullup_61_out), .S(nfet_127_s));
  NFET nfet_128 (.G(pullup_59_out), .D(nfet_127_s), .S(1'b0));
  PullUp pullup_62 (.out(pullup_62_out));
  NFET nfet_129 (.G(pullup_71_out), .D(pullup_62_out), .S(nfet_129_s));
  PullUp pullup_63 (.out(nfet_121_d));
  NFET nfet_130 (.G(nfet_121_d), .D(nfet_129_s), .S(1'b0));
  PullUp pullup_64 (.out(pullup_64_out));
  NFET nfet_131 (.G(pullup_72_out), .D(pullup_64_out), .S(nfet_131_s));
  PullUp pullup_65 (.out(nfet_123_d));
  NFET nfet_132 (.G(nfet_123_d), .D(nfet_131_s), .S(1'b0));
  PullUp pullup_66 (.out(pullup_66_out));
  NFET nfet_133 (.G(pullup_66_out), .D(nfet_133_d), .S(1'b0));
  NFET nfet_134 (.G(CLKin), .D(pullup_66_out), .S(nfet_134_s));
  NFET nfet_135 (.G(F3), .D(nfet_134_s), .S(1'b0));
  PullUp pullup_67 (.out(pullup_67_out));
  NFET nfet_136 (.G(pullup_67_out), .D(nfet_136_d), .S(1'b0));
  NFET nfet_137 (.G(CLKin), .D(pullup_67_out), .S(nfet_137_s));
  NFET nfet_138 (.G(F2), .D(nfet_137_s), .S(1'b0));
  PullUp pullup_68 (.out(pullup_68_out));
  NFET nfet_139 (.G(CLKin), .D(pullup_68_out), .S(nfet_139_s));
  NFET nfet_140 (.G(F1), .D(nfet_139_s), .S(1'b0));
  NFET nfet_141 (.G(CLKin), .D(nfet_141_d), .S(nfet_141_s));
  NFET nfet_142 (.G(F0), .D(nfet_141_s), .S(1'b0));
  PullUp pullup_69 (.out(pullup_69_out));
  NFET nfet_143 (.G(pullup_60_out), .D(pullup_69_out), .S(nfet_133_d));
  PullUp pullup_70 (.out(pullup_70_out));
  NFET nfet_144 (.G(pullup_61_out), .D(pullup_70_out), .S(nfet_136_d));
  PullUp pullup_71 (.out(pullup_71_out));
  NFET nfet_145 (.G(pullup_62_out), .D(pullup_71_out), .S(nfet_145_s));
  NFET nfet_146 (.G(pullup_68_out), .D(nfet_145_s), .S(1'b0));
  PullUp pullup_72 (.out(pullup_72_out));
  NFET nfet_147 (.G(pullup_64_out), .D(pullup_72_out), .S(nfet_147_s));
  PullUp pullup_73 (.out(nfet_141_d));
  NFET nfet_148 (.G(nfet_141_d), .D(nfet_147_s), .S(1'b0));
  PullUp pullup_74 (.out(pullup_74_out));
  NFET nfet_149 (.G(CLKin), .D(pullup_74_out), .S(1'b0));
  PullUp pullup_75 (.out(pullup_75_out));
  NFET nfet_150 (.G(CLKin), .D(pullup_75_out), .S(1'b0));
  NFET nfet_151 (.G(CLKin), .D(nfet_151_d), .S(1'b0));
  NFET nfet_152 (.G(pullup_74_out), .D(nfet_152_d), .S(nfet_152_s));
  NFET nfet_153 (.G(pullup_60_out), .D(nfet_152_s), .S(1'b0));
  NFET nfet_154 (.G(pullup_75_out), .D(nfet_154_d), .S(nfet_154_s));
  NFET nfet_155 (.G(pullup_61_out), .D(nfet_154_s), .S(1'b0));
  PullUp pullup_76 (.out(nfet_151_d));
  PullUp pullup_77 (.out(pullup_77_out));
  NFET nfet_156 (.G(CLKin), .D(pullup_77_out), .S(1'b0));
  PullUp pullup_78 (.out(pullup_78_out));
  NFET nfet_157 (.G(AC3), .D(pullup_78_out), .S(nfet_157_s));
  PullUp pullup_79 (.out(nfet_152_d));
  NFET nfet_158 (.G(nfet_152_d), .D(nfet_157_s), .S(1'b0));
  PullUp pullup_80 (.out(pullup_80_out));
  NFET nfet_159 (.G(AC2), .D(pullup_80_out), .S(nfet_159_s));
  PullUp pullup_81 (.out(nfet_154_d));
  NFET nfet_160 (.G(nfet_154_d), .D(nfet_159_s), .S(1'b0));
  NFET nfet_161 (.G(AC1), .D(nfet_161_d), .S(nfet_161_s));
  PullUp pullup_82 (.out(pullup_82_out));
  NFET nfet_162 (.G(pullup_82_out), .D(nfet_161_s), .S(1'b0));
  NFET nfet_163 (.G(nfet_151_d), .D(pullup_82_out), .S(nfet_163_s));
  NFET nfet_164 (.G(pullup_62_out), .D(nfet_163_s), .S(1'b0));
  PullUp pullup_83 (.out(pullup_83_out));
  NFET nfet_165 (.G(pullup_77_out), .D(pullup_83_out), .S(nfet_165_s));
  NFET nfet_166 (.G(pullup_64_out), .D(nfet_165_s), .S(1'b0));
  PullUp pullup_84 (.out(nfet_161_d));
  PullUp pullup_85 (.out(pullup_85_out));
  NFET nfet_167 (.G(AC0), .D(pullup_85_out), .S(nfet_167_s));
  NFET nfet_168 (.G(pullup_83_out), .D(nfet_167_s), .S(1'b0));
  NFET nfet_169 (.G(pullup_74_out), .D(nfet_169_d), .S(nfet_169_s));
  NFET nfet_170 (.G(pullup_69_out), .D(nfet_169_s), .S(1'b0));
  NFET nfet_171 (.G(pullup_75_out), .D(nfet_171_d), .S(nfet_171_s));
  NFET nfet_172 (.G(pullup_70_out), .D(nfet_171_s), .S(1'b0));
  NFET nfet_173 (.G(nfet_151_d), .D(nfet_173_d), .S(nfet_173_s));
  NFET nfet_174 (.G(pullup_71_out), .D(nfet_173_s), .S(1'b0));
  PullUp pullup_86 (.out(AC3));
  NFET nfet_175 (.G(pullup_78_out), .D(AC3), .S(nfet_175_s));
  PullUp pullup_87 (.out(nfet_169_d));
  NFET nfet_176 (.G(nfet_169_d), .D(nfet_175_s), .S(1'b0));
  PullUp pullup_88 (.out(AC2));
  NFET nfet_177 (.G(pullup_80_out), .D(AC2), .S(nfet_177_s));
  PullUp pullup_89 (.out(nfet_171_d));
  NFET nfet_178 (.G(nfet_171_d), .D(nfet_177_s), .S(1'b0));
  NFET nfet_179 (.G(nfet_161_d), .D(AC1), .S(nfet_179_s));
  PullUp pullup_90 (.out(nfet_173_d));
  NFET nfet_180 (.G(nfet_173_d), .D(nfet_179_s), .S(1'b0));
  PullUp pullup_91 (.out(pullup_91_out));
  NFET nfet_181 (.G(pullup_91_out), .D(nfet_181_d), .S(1'b0));
  NFET nfet_182 (.G(pullup_77_out), .D(pullup_91_out), .S(nfet_182_s));
  NFET nfet_183 (.G(pullup_72_out), .D(nfet_182_s), .S(1'b0));
  PullUp pullup_92 (.out(AC1));
  PullUp pullup_93 (.out(AC0));
  NFET nfet_184 (.G(pullup_85_out), .D(AC0), .S(nfet_181_d));

  // Other names for the same wires on the sheet: C4 = Cout

  // Notes on the sheet:
  //   ALU
  //   ACC
  //   BUS
endmodule
