// Digital circuit FP+4_Regs_2.dig as structural Verilog
module FP_4_Regs_2 (
  input  in_1,
  input  in_2,
  input  in_3,
  input  clk,
  output GCLK,
  output P1,
  output P0,
  output P3,
  output P4,
  output P2,
  output Kout
);

  wire _0_out, _1_out, _2_out, _3_out, _4_out, _5_out, _6_out, _7_out, _8_out, _9_out, _74173_1_pin7,
       _74173_1_pin13, _74173_1_pin14, _74173_5_pin11, _74173_5_pin12, _74173_5_pin13, _74173_5_pin14, A,
       A_out, AC, Ain, Aout, Arc, B, B_out, BC, Bin, Bout, Brc, C_out, CC, Cin, Cout, Crc, D_out, DC, Din,
       diodebackward_1_out, diodebackward_3_out, diodebackward_5_out, diodebackward_10_out,
       diodebackward_25_out, Dout, Drc, E_out, F_out, GATE, HOLD, LD, MR, n2SD, nand_1_out, nand_2_out,
       nand_3_out, nand_4_out, nand_5_out, nand_6_out, nand_7_out, nand_8_out, nand_9_out, nand_10_out,
       nand_11_out, nand_12_out, nand_20_out, nGATE, nHOLD, nLATCH, not_3_out, not_8_out, not_9_out, nR,
       pullup_4_out, pullup_7_out, pullup_8_out, R, RCO, S0, S1, S2, S3, S4, S5, S6, S7, S8, S9, S10, S11,
       S12, S13, S14, S15, SETC, STA_out, STB_out, STC_out, STD_out, T2, T3, T4, T6, T7, T8, T9, U8_pin9,
       U10_pin9, U12_pin9, U14_pin9, U27_pin9;
  wire [3:0] U8_pin4, U8_pin15, U9_pin4, U9_pin15, U10_pin4, U10_pin15, U11_pin4, U11_pin15, U12_pin4,
       U12_pin15, U13_pin4, U13_pin15, U14_pin4, U14_pin15, U15_pin4, U15_pin15, U17_pin14;

  Button #(.activeLow("true")) STA (.out(STA_out));
  Button #(.activeLow("true")) STB (.out(STB_out));
  DiodeBackward diodebackward_1 (.in(STC_out), .out(diodebackward_1_out));
  Button #(.activeLow("true")) STC (.out(STC_out));
  DiodeBackward diodebackward_2 (.in(STD_out), .out(diodebackward_1_out));
  Button #(.activeLow("true")) STD (.out(STD_out));
  _74173 _74173_1 (
    .pin1(1'b0), .pin2(1'b0), .pin3(A), .pin4(B), .pin7(_74173_1_pin7), .pin8(1'b0), .pin9(1'b0),
    .pin10(1'b0), .pin11(1'b0), .pin12(1'b0), .pin13(_74173_1_pin13), .pin14(_74173_1_pin14), .pin15(1'b0),
    .pin16(1'b1));  // open: pin5, pin6
  _74173 _74173_2 (
    .pin1(1'b0), .pin2(1'b0), .pin3(S12), .pin4(S13), .pin5(S14), .pin6(S15), .pin7(nLATCH), .pin8(1'b0),
    .pin9(1'b0), .pin10(1'b0), .pin11(S11), .pin12(S10), .pin13(S9), .pin14(S8), .pin15(1'b0), .pin16(1'b1));
  _74165 U27 (
    .pin1(P0), .pin2(GCLK), .pin3(S11), .pin4(S10), .pin5(S9), .pin6(S8), .pin8(1'b0), .pin9(U27_pin9),
    .pin10(1'b0), .pin11(S15), .pin12(S14), .pin13(S13), .pin14(S12), .pin15(1'b0), .pin16(1'b1));  // open: pin7
  PullUp pullup_1 (.out(diodebackward_1_out));
  DiodeBackward diodebackward_3 (.in(STB_out), .out(diodebackward_3_out));
  DiodeBackward diodebackward_4 (.in(STD_out), .out(diodebackward_3_out));
  not not_1 (_74173_1_pin13, diodebackward_1_out);
  PullUp pullup_2 (.out(diodebackward_3_out));
  DiodeBackward diodebackward_5 (.in(STA_out), .out(diodebackward_5_out));
  DiodeBackward diodebackward_6 (.in(STB_out), .out(diodebackward_5_out));
  DiodeBackward diodebackward_7 (.in(STC_out), .out(diodebackward_5_out));
  DiodeBackward diodebackward_8 (.in(STD_out), .out(diodebackward_5_out));
  not not_2 (_74173_1_pin14, diodebackward_3_out);
  PullUp pullup_3 (.out(diodebackward_5_out));
  not not_3 (not_3_out, diodebackward_5_out);
  Monoflop monoflop_1 (.C(not_3_out), .R(1'b0), .nQ(_74173_1_pin7));  // open: Q
  _74173 _74173_3 (
    .pin1(1'b0), .pin2(1'b0), .pin3(S8), .pin4(S9), .pin5(S10), .pin6(S11), .pin7(nLATCH), .pin8(1'b0),
    .pin9(1'b0), .pin10(1'b0), .pin11(S7), .pin12(S6), .pin13(S5), .pin14(S4), .pin15(1'b0), .pin16(1'b1));
  Button #(.activeLow("true")) C (.out(C_out));
  Button #(.activeLow("true")) _8 (.out(_8_out));
  Button #(.activeLow("true")) _4 (.out(_4_out));
  Button #(.activeLow("true")) _0 (.out(_0_out));
  _74165 U28 (
    .pin1(P0), .pin2(GCLK), .pin3(S3), .pin4(S2), .pin5(S1), .pin6(S0), .pin8(1'b0), .pin9(Kout),
    .pin10(U27_pin9), .pin11(S7), .pin12(S6), .pin13(S5), .pin14(S4), .pin15(1'b0), .pin16(1'b1));  // open: pin7
  Seven_Seg_Hex seven_seg_hex_1 (.d({S15, S14, S13, S12}), .dp(1'b0));
  Seven_Seg_Hex seven_seg_hex_2 (.d({S11, S10, S9, S8}), .dp(1'b0));
  Button #(.activeLow("true")) D (.out(D_out));
  Button #(.activeLow("true")) _9 (.out(_9_out));
  Button #(.activeLow("true")) _5 (.out(_5_out));
  Button #(.activeLow("true")) _1 (.out(_1_out));
  Seven_Seg_Hex seven_seg_hex_3 (.d({S7, S6, S5, S4}), .dp(1'b0));
  _74173 _74173_4 (
    .pin1(1'b0), .pin2(1'b0), .pin3(S4), .pin4(S5), .pin5(S6), .pin6(S7), .pin7(nLATCH), .pin8(1'b0),
    .pin9(1'b0), .pin10(1'b0), .pin11(S3), .pin12(S2), .pin13(S1), .pin14(S0), .pin15(1'b0), .pin16(1'b1));
  Seven_Seg_Hex seven_seg_hex_4 (.d({S3, S2, S1, S0}), .dp(1'b0));
  Button #(.activeLow("true")) E (.out(E_out));
  Button #(.activeLow("true")) u_A (.out(A_out));
  Button #(.activeLow("true")) _6 (.out(_6_out));
  Button #(.activeLow("true")) _2 (.out(_2_out));
  Button #(.activeLow("true")) F (.out(F_out));
  Button #(.activeLow("true")) u_B (.out(B_out));
  Button #(.activeLow("true")) _7 (.out(_7_out));
  Button #(.activeLow("true")) _3 (.out(_3_out));
  _74173 _74173_5 (
    .pin1(1'b0), .pin2(1'b0), .pin3(S0), .pin4(S1), .pin5(S2), .pin6(S3), .pin7(nLATCH), .pin8(1'b0),
    .pin9(1'b0), .pin10(1'b0), .pin11(_74173_5_pin11), .pin12(_74173_5_pin12), .pin13(_74173_5_pin13),
    .pin14(_74173_5_pin14), .pin15(1'b0), .pin16(1'b1));
  _74139 _74139_1 (
    .pin1(nR), .pin2(A), .pin3(B), .pin4(AC), .pin5(BC), .pin6(CC), .pin7(DC), .pin8(1'b0), .pin9(Dout),
    .pin10(Cout), .pin11(Bout), .pin12(Aout), .pin13(B), .pin14(A), .pin15(Kout), .pin16(1'b1));
  PullUp pullup_4 (.out(pullup_4_out));
  DiodeBackward diodebackward_9 (.in(F_out), .out(pullup_4_out));
  DiodeBackward diodebackward_10 (.in(F_out), .out(diodebackward_10_out));
  DiodeBackward diodebackward_11 (.in(E_out), .out(pullup_4_out));
  DiodeBackward diodebackward_12 (.in(E_out), .out(diodebackward_10_out));
  DiodeBackward diodebackward_13 (.in(D_out), .out(diodebackward_10_out));
  DiodeBackward diodebackward_14 (.in(D_out), .out(pullup_4_out));
  DiodeBackward diodebackward_15 (.in(C_out), .out(diodebackward_10_out));
  DiodeBackward diodebackward_16 (.in(C_out), .out(pullup_4_out));
  DiodeBackward diodebackward_17 (.in(B_out), .out(pullup_4_out));
  DiodeBackward diodebackward_18 (.in(A_out), .out(pullup_4_out));
  DiodeBackward diodebackward_19 (.in(_9_out), .out(pullup_4_out));
  DiodeBackward diodebackward_20 (.in(_8_out), .out(pullup_4_out));
  DiodeBackward diodebackward_21 (.in(_7_out), .out(diodebackward_10_out));
  DiodeBackward diodebackward_22 (.in(_6_out), .out(diodebackward_10_out));
  DiodeBackward diodebackward_23 (.in(_5_out), .out(diodebackward_10_out));
  DiodeBackward diodebackward_24 (.in(_4_out), .out(diodebackward_10_out));
  not not_4 (_74173_5_pin11, pullup_4_out);
  PullUp pullup_5 (.out(diodebackward_10_out));
  DiodeBackward diodebackward_25 (.in(F_out), .out(diodebackward_25_out));
  DiodeBackward diodebackward_26 (.in(E_out), .out(diodebackward_25_out));
  DiodeBackward diodebackward_27 (.in(B_out), .out(diodebackward_25_out));
  DiodeBackward diodebackward_28 (.in(A_out), .out(diodebackward_25_out));
  DiodeBackward diodebackward_29 (.in(_7_out), .out(diodebackward_25_out));
  DiodeBackward diodebackward_30 (.in(_6_out), .out(diodebackward_25_out));
  DiodeBackward diodebackward_31 (.in(_3_out), .out(diodebackward_25_out));
  DiodeBackward diodebackward_32 (.in(_2_out), .out(diodebackward_25_out));
  not not_5 (_74173_5_pin12, diodebackward_10_out);
  PullUp pullup_6 (.out(diodebackward_25_out));
  PullUp pullup_7 (.out(pullup_7_out));
  DiodeBackward diodebackward_33 (.in(F_out), .out(pullup_7_out));
  DiodeBackward diodebackward_34 (.in(D_out), .out(pullup_7_out));
  DiodeBackward diodebackward_35 (.in(B_out), .out(pullup_7_out));
  DiodeBackward diodebackward_36 (.in(_9_out), .out(pullup_7_out));
  DiodeBackward diodebackward_37 (.in(_7_out), .out(pullup_7_out));
  DiodeBackward diodebackward_38 (.in(_5_out), .out(pullup_7_out));
  DiodeBackward diodebackward_39 (.in(_3_out), .out(pullup_7_out));
  DiodeBackward diodebackward_40 (.in(_1_out), .out(pullup_7_out));
  not not_6 (_74173_5_pin14, pullup_7_out);
  not not_7 (_74173_5_pin13, diodebackward_25_out);
  PullUp pullup_8 (.out(pullup_8_out));
  DiodeBackward diodebackward_41 (.in(F_out), .out(pullup_8_out));
  DiodeBackward diodebackward_42 (.in(E_out), .out(pullup_8_out));
  DiodeBackward diodebackward_43 (.in(D_out), .out(pullup_8_out));
  DiodeBackward diodebackward_44 (.in(C_out), .out(pullup_8_out));
  DiodeBackward diodebackward_45 (.in(B_out), .out(pullup_8_out));
  DiodeBackward diodebackward_46 (.in(A_out), .out(pullup_8_out));
  DiodeBackward diodebackward_47 (.in(_9_out), .out(pullup_8_out));
  DiodeBackward diodebackward_48 (.in(_8_out), .out(pullup_8_out));
  DiodeBackward diodebackward_49 (.in(_7_out), .out(pullup_8_out));
  DiodeBackward diodebackward_50 (.in(_6_out), .out(pullup_8_out));
  DiodeBackward diodebackward_51 (.in(_5_out), .out(pullup_8_out));
  DiodeBackward diodebackward_52 (.in(_4_out), .out(pullup_8_out));
  DiodeBackward diodebackward_53 (.in(_3_out), .out(pullup_8_out));
  DiodeBackward diodebackward_54 (.in(_2_out), .out(pullup_8_out));
  DiodeBackward diodebackward_55 (.in(_1_out), .out(pullup_8_out));
  DiodeBackward diodebackward_56 (.in(_0_out), .out(pullup_8_out));
  not not_8 (not_8_out, pullup_8_out);
  Monoflop monoflop_2 (.C(not_8_out), .R(1'b0), .nQ(nLATCH));  // open: Q
  nand nand_1 (nand_1_out, AC, AC);
  nand nand_2 (nand_2_out, BC, BC);
  nand nand_3 (nand_3_out, CC, CC);
  nand nand_4 (nand_4_out, DC, DC);
  nand nand_5 (nand_5_out, Aout, nand_1_out);
  nand nand_6 (nand_6_out, AC, Arc);
  nand nand_7 (nand_7_out, Bout, nand_2_out);
  nand nand_8 (nand_8_out, BC, Brc);
  nand nand_9 (nand_9_out, Cout, nand_3_out);
  nand nand_10 (nand_10_out, CC, Crc);
  nand nand_11 (nand_11_out, Dout, nand_4_out);
  nand nand_12 (nand_12_out, DC, Drc);
  nand nand_13 (Ain, nand_5_out, nand_6_out);
  nand nand_14 (Bin, nand_7_out, nand_8_out);
  nand nand_15 (Cin, nand_9_out, nand_10_out);
  nand nand_16 (Din, nand_11_out, nand_12_out);
  _74595 U8 (
    .pin1(U8_pin15[2]), .pin2(U8_pin15[1]), .pin3(U8_pin15[0]), .pin4(U8_pin4[3]), .pin5(U8_pin4[2]),
    .pin6(U8_pin4[1]), .pin7(U8_pin4[0]), .pin8(1'b0), .pin9(U8_pin9), .pin10(P1), .pin11(GCLK), .pin12(AC),
    .pin13(1'b0), .pin14(Ain), .pin15(U8_pin15[3]), .pin16(1'b1));
  _74595 U10 (
    .pin1(U10_pin15[2]), .pin2(U10_pin15[1]), .pin3(U10_pin15[0]), .pin4(U10_pin4[3]), .pin5(U10_pin4[2]),
    .pin6(U10_pin4[1]), .pin7(U10_pin4[0]), .pin8(1'b0), .pin9(U10_pin9), .pin10(P1), .pin11(GCLK),
    .pin12(BC), .pin13(1'b0), .pin14(Bin), .pin15(U10_pin15[3]), .pin16(1'b1));
  _74595 U12 (
    .pin1(U12_pin15[2]), .pin2(U12_pin15[1]), .pin3(U12_pin15[0]), .pin4(U12_pin4[3]), .pin5(U12_pin4[2]),
    .pin6(U12_pin4[1]), .pin7(U12_pin4[0]), .pin8(1'b0), .pin9(U12_pin9), .pin10(P1), .pin11(GCLK),
    .pin12(CC), .pin13(1'b0), .pin14(Cin), .pin15(U12_pin15[3]), .pin16(1'b1));
  _74595 U14 (
    .pin1(U14_pin15[2]), .pin2(U14_pin15[1]), .pin3(U14_pin15[0]), .pin4(U14_pin4[3]), .pin5(U14_pin4[2]),
    .pin6(U14_pin4[1]), .pin7(U14_pin4[0]), .pin8(1'b0), .pin9(U14_pin9), .pin10(P1), .pin11(GCLK),
    .pin12(DC), .pin13(1'b0), .pin14(Din), .pin15(U14_pin15[3]), .pin16(1'b1));
  _74595 U9 (
    .pin1(U9_pin15[2]), .pin2(U9_pin15[1]), .pin3(U9_pin15[0]), .pin4(U9_pin4[3]), .pin5(U9_pin4[2]),
    .pin6(U9_pin4[1]), .pin7(U9_pin4[0]), .pin8(1'b0), .pin9(Arc), .pin10(P1), .pin11(GCLK), .pin12(AC),
    .pin13(1'b0), .pin14(U8_pin9), .pin15(U9_pin15[3]), .pin16(1'b1));
  _74595 U11 (
    .pin1(U11_pin15[2]), .pin2(U11_pin15[1]), .pin3(U11_pin15[0]), .pin4(U11_pin4[3]), .pin5(U11_pin4[2]),
    .pin6(U11_pin4[1]), .pin7(U11_pin4[0]), .pin8(1'b0), .pin9(Brc), .pin10(P1), .pin11(GCLK), .pin12(BC),
    .pin13(1'b0), .pin14(U10_pin9), .pin15(U11_pin15[3]), .pin16(1'b1));
  _74595 U13 (
    .pin1(U13_pin15[2]), .pin2(U13_pin15[1]), .pin3(U13_pin15[0]), .pin4(U13_pin4[3]), .pin5(U13_pin4[2]),
    .pin6(U13_pin4[1]), .pin7(U13_pin4[0]), .pin8(1'b0), .pin9(Crc), .pin10(P1), .pin11(GCLK), .pin12(CC),
    .pin13(1'b0), .pin14(U12_pin9), .pin15(U13_pin15[3]), .pin16(1'b1));
  _74595 U15 (
    .pin1(U15_pin15[2]), .pin2(U15_pin15[1]), .pin3(U15_pin15[0]), .pin4(U15_pin4[3]), .pin5(U15_pin4[2]),
    .pin6(U15_pin4[1]), .pin7(U15_pin4[0]), .pin8(1'b0), .pin9(Drc), .pin10(P1), .pin11(GCLK), .pin12(DC),
    .pin13(1'b0), .pin14(U14_pin9), .pin15(U15_pin15[3]), .pin16(1'b1));
  Seven_Seg_Hex seven_seg_hex_5 (.d(U8_pin15), .dp(1'b0));
  Seven_Seg_Hex seven_seg_hex_6 (.d(U10_pin15), .dp(1'b0));
  Seven_Seg_Hex seven_seg_hex_7 (.d(U12_pin15), .dp(1'b0));
  Seven_Seg_Hex seven_seg_hex_8 (.d(U14_pin15), .dp(1'b0));
  Seven_Seg_Hex seven_seg_hex_9 (.d(U8_pin4), .dp(1'b0));
  Seven_Seg_Hex seven_seg_hex_10 (.d(U10_pin4), .dp(1'b0));
  Seven_Seg_Hex seven_seg_hex_11 (.d(U12_pin4), .dp(1'b0));
  Seven_Seg_Hex seven_seg_hex_12 (.d(U14_pin4), .dp(1'b0));
  Seven_Seg_Hex seven_seg_hex_13 (.d(U9_pin15), .dp(1'b0));
  Seven_Seg_Hex seven_seg_hex_14 (.d(U11_pin15), .dp(1'b0));
  Seven_Seg_Hex seven_seg_hex_15 (.d(U13_pin15), .dp(1'b0));
  Seven_Seg_Hex seven_seg_hex_16 (.d(U15_pin15), .dp(1'b0));
  Seven_Seg_Hex seven_seg_hex_17 (.d(U9_pin4), .dp(1'b0));
  Seven_Seg_Hex seven_seg_hex_18 (.d(U11_pin4), .dp(1'b0));
  Seven_Seg_Hex seven_seg_hex_19 (.d(U13_pin4), .dp(1'b0));
  Seven_Seg_Hex seven_seg_hex_20 (.d(U15_pin4), .dp(1'b0));
  Reset reset_1 (.out(n2SD));
  not not_9 (not_9_out, MR);
  not not_10 (P4, T4);
  not not_11 (P3, T3);
  not not_12 (P2, T2);
  not not_13 (P1, SETC);
  not not_14 (P0, LD);
  nand nand_17 (GATE, P2, nGATE);
  nand nand_18 (nGATE, GATE, nR);
  nand nand_19 (GCLK, GATE, nand_20_out);
  nand nand_20 (nand_20_out, clk, clk);
  _7474 U30 (
    .pin1(1'b1), .pin2(RCO), .pin3(clk), .pin4(n2SD), .pin5(R), .pin6(nR), .pin7(1'b0), .pin10(1'b1),
    .pin11(1'b1), .pin12(1'b1), .pin13(1'b1), .pin14(1'b1));  // open: pin8, pin9
  nand nand_21 (HOLD, nGATE, nHOLD);
  nand nand_22 (nHOLD, HOLD, nR);
  _744017 U16 (
    .pin1(MR), .pin2(SETC), .pin3(LD), .pin4(T2), .pin5(T6), .pin6(T7), .pin7(T3), .pin8(1'b0), .pin9(T8),
    .pin10(T4), .pin11(T9), .pin13(HOLD), .pin14(clk), .pin15(MR), .pin16(1'b1));  // open: pin12
  _74161 U17 (
    .pin1(GATE), .pin2(clk), .pin3(1'b0), .pin4(1'b0), .pin5(1'b0), .pin6(1'b0), .pin7(1'b1), .pin8(1'b0),
    .pin9(1'b1), .pin10(1'b1), .pin11(U17_pin14[3]), .pin12(U17_pin14[2]), .pin13(U17_pin14[1]),
    .pin14(U17_pin14[0]), .pin15(RCO), .pin16(1'b1));
  Seven_Seg_Hex seven_seg_hex_21 (.d(U17_pin14), .dp(1'b0));

  // Other names for the same wires on the sheet: nAEN = GATE; nCE = in_3; nLD = P0; nOE = in_2; nRES = P1;
  //   nCLR = n2SD; nRRES = n2SD; nSET = P2; nWE = in_1; T0 = LD; T1 = SETC; T5 = MR

  // Notes on the sheet:
  //   in_1: default 1
  //   in_2: default 1
  //   in_3: default 1
  //   clk: Hz: 2
  //   Front Panel
  //   Keypad read register K
  //   Hex Keypad
  //   KEY DATA
  //   KEYSWITCH REGISTER
  //   A,B,C,D Registers
  //   A REGISTER
  //   B REGISTER
  //   C REGISTER
  //   D REGISTER
  //   Clock Sequencer
  //   U11
  //   16th Pulse FF
  //   U19
  //   # Clock
endmodule
