// Digital circuit Inst_decoder_ALU.dig as structural Verilog
module Inst_decoder_ALU (
  input  A,
  input  B,
  input  Cin,
  input  SETC,
  input  LD,
  input  IR6,
  input  IR5,
  input  IR4,
  output Cout,
  output CLC,
  output CtoFF,
  output Fout,
  output CLR
);

  wire ADD, AND, C, CLA, diodebackward_1_out, diodebackward_2_out, diodebackward_7_out, F, I0, I1, LOAD, nA,
       nand_2_out, nand_5_out, nand_6_out, nand_7_out, nand_8_out, nand_9_out, nand_10_out, nB, nJMP, OR,
       pullup_2_out, pullup_4_out, pullup_5_out, pullup_7_out, ST, SUB, XOR, xor_1_out, xor_2_out, xor_3_out,
       xor_4_out;

  _74138 U1 (
    .pin1(IR4), .pin2(IR5), .pin3(IR6), .pin4(1'b0), .pin5(1'b0), .pin6(1'b1), .pin7(nJMP), .pin8(1'b0),
    .pin9(ST), .pin10(SUB), .pin11(ADD), .pin12(XOR), .pin13(OR), .pin14(AND), .pin15(LOAD), .pin16(1'b1));
  DiodeBackward diodebackward_1 (.in(LOAD), .out(diodebackward_1_out));
  PullUp pullup_1 (.out(diodebackward_1_out));
  DiodeBackward diodebackward_2 (.in(LOAD), .out(diodebackward_2_out));
  DiodeBackward diodebackward_3 (.in(ADD), .out(diodebackward_2_out));
  DiodeBackward diodebackward_4 (.in(SUB), .out(diodebackward_2_out));
  PullUp pullup_2 (.out(pullup_2_out));
  PullUp pullup_3 (.out(diodebackward_2_out));
  DiodeBackward diodebackward_5 (.in(SUB), .out(pullup_2_out));
  PullUp pullup_4 (.out(pullup_4_out));
  DiodeBackward diodebackward_6 (.in(SUB), .out(pullup_4_out));
  PullUp pullup_5 (.out(pullup_5_out));
  DiodeBackward diodebackward_7 (.in(AND), .out(diodebackward_7_out));
  DiodeBackward diodebackward_8 (.in(OR), .out(diodebackward_7_out));
  PullUp pullup_6 (.out(diodebackward_7_out));
  PullUp pullup_7 (.out(pullup_7_out));
  DiodeBackward diodebackward_9 (.in(LOAD), .out(pullup_7_out));
  DiodeBackward diodebackward_10 (.in(OR), .out(pullup_7_out));
  DiodeBackward diodebackward_11 (.in(XOR), .out(pullup_7_out));
  DiodeBackward diodebackward_12 (.in(ADD), .out(pullup_7_out));
  DiodeBackward diodebackward_13 (.in(SUB), .out(pullup_7_out));
  DiodeBackward diodebackward_14 (.in(ST), .out(pullup_7_out));
  DiodeBackward diodebackward_15 (.in(nJMP), .out(pullup_7_out));
  _74540 U2 (
    .pin1(1'b0), .pin2(pullup_7_out), .pin3(diodebackward_7_out), .pin4(pullup_5_out), .pin5(pullup_4_out),
    .pin6(pullup_2_out), .pin7(diodebackward_2_out), .pin8(diodebackward_1_out), .pin9(1'b0), .pin10(1'b0),
    .pin12(CLA), .pin13(F), .pin14(C), .pin15(nB), .pin16(nA), .pin17(I1), .pin18(I0), .pin19(1'b0),
    .pin20(1'b1));  // open: pin11
  xor xor_1 (xor_1_out, A, nA);
  xor xor_2 (xor_2_out, nB, B);
  nand nand_1 (CtoFF, SETC, C);
  nand nand_2 (nand_2_out, C, C);
  nand nand_3 (CLC, nand_2_out, LD);
  nand nand_4 (CLR, CLA, LD);
  xor xor_3 (xor_3_out, xor_1_out, xor_2_out);
  xor xor_4 (xor_4_out, xor_3_out, Cin);
  nand nand_5 (nand_5_out, xor_3_out, Cin);
  nand nand_6 (nand_6_out, xor_1_out, xor_2_out);
  nand nand_7 (nand_7_out, nand_5_out, nand_6_out);
  nand nand_8 (nand_8_out, xor_4_out, I0);
  nand nand_9 (nand_9_out, I1, nand_7_out);
  nand nand_10 (nand_10_out, nand_7_out, F);
  nand nand_11 (Fout, nand_8_out, nand_9_out);
  nand nand_12 (Cout, nand_10_out, nand_10_out);

  // Other names for the same wires on the sheet: Ain = A; Bin = B

  // Notes on the sheet:
  //   Decoder "ROM" Logic
  //   Instruction decoder
  //   Instruction Input
  //   Serial Data Inputs
  //   CLA
  //   C
  //   F
  //   ~B
  //   ~A
  //   I0
  //   I1
  //   LOAD
  //   AND
  //   OR
  //   XOR
  //   ADD
  //   SUB
  //   STORE
  //   JMP
  //   ALU
  //   Invert A / B
  //   Carry Input
  //   Carry Control
  //   Full Adder
  //   Carry is only set before Bit 0 of an operation
  //   Any residual carry is cleared before an operation
  //   Multiplexer
  //   Suppress Carry
endmodule
