// Digital circuit KB_181_2.dig as structural Verilog
module KB_181_2 (
  input  B0,
  input  B1,
  input  B2,
  input  B3,
  input  I1,
  input  I0,
  input  NEG,
  input  Cin,
  input  SC,
  input  A3,
  input  A2,
  input  A1,
  input  A0,
  input  VCC,
  input  GND,
  input  AND_NAND,
  output Q0,
  output Q1,
  output Q2,
  output Q3,
  output Cout
);

  wire nand_1_out, nand_2_out, nand_3_out, nand_4_out, nand_5_out, nand_6_out, nand_7_out, nand_8_out,
       nand_9_out, nand_10_out, nand_11_out, nand_12_out, nand_13_out, nand_14_out, nand_15_out, nand_16_out,
       nand_17_out, nand_18_out, nand_19_out, nand_20_out, nand_21_out, nand_22_out, nand_23_out,
       nand_24_out, nand_25_out, nand_26_out, nand_27_out, nand_28_out, nand_29_out, nand_30_out,
       nand_31_out, nand_32_out, nand_33_out, nand_34_out, nand_35_out, nand_36_out, nand_37_out,
       nand_38_out, nand_39_out, nand_40_out, nand_41_out, nand_42_out, nand_44_out, nand_46_out,
       nand_48_out, nand_49_out, nand_51_out, nand_52_out, nand_53_out, xor_1_out, xor_2_out, xor_3_out,
       xor_4_out, xor_5_out, xor_6_out;

  PowerSupply powersupply_1 (.VDD(VCC), .GND(GND));
  xor xor_1 (xor_1_out, B3, NEG);
  xor xor_2 (xor_2_out, B2, NEG);
  xor xor_3 (xor_3_out, B1, NEG);
  xor xor_4 (xor_4_out, B0, NEG);
  nand nand_1 (nand_1_out, A3, xor_1_out);
  nand nand_2 (nand_2_out, A2, xor_2_out);
  nand nand_3 (nand_3_out, A1, xor_3_out);
  nand nand_4 (nand_4_out, A0, xor_4_out);
  xor xor_5 (xor_5_out, A0, xor_4_out);
  nand nand_5 (nand_5_out, A3, nand_1_out);
  nand nand_6 (nand_6_out, nand_1_out, nand_1_out);
  nand nand_7 (nand_7_out, nand_1_out, xor_1_out);
  nand nand_8 (nand_8_out, A2, nand_2_out);
  nand nand_9 (nand_9_out, nand_2_out, nand_2_out);
  nand nand_10 (nand_10_out, nand_2_out, xor_2_out);
  nand nand_11 (nand_11_out, A1, nand_3_out);
  nand nand_12 (nand_12_out, nand_3_out, nand_3_out);
  nand nand_13 (nand_13_out, nand_3_out, xor_3_out);
  xor xor_6 (xor_6_out, nand_4_out, AND_NAND);
  nand nand_14 (nand_14_out, nand_5_out, nand_7_out);
  nand nand_15 (nand_15_out, nand_8_out, nand_10_out);
  nand nand_16 (nand_16_out, nand_11_out, nand_13_out);
  nand nand_17 (nand_17_out, nand_6_out, I1);
  nand nand_18 (nand_18_out, nand_14_out, I0);
  nand nand_19 (nand_19_out, nand_9_out, I1);
  nand nand_20 (nand_20_out, nand_15_out, I0);
  nand nand_21 (nand_21_out, nand_12_out, I1);
  nand nand_22 (nand_22_out, nand_16_out, I0);
  nand nand_23 (nand_23_out, xor_6_out, I1);
  nand nand_24 (nand_24_out, xor_5_out, I0);
  nand nand_25 (nand_25_out, nand_17_out, nand_18_out);
  nand nand_26 (nand_26_out, nand_19_out, nand_20_out);
  nand nand_27 (nand_27_out, nand_21_out, nand_22_out);
  nand nand_28 (nand_28_out, nand_23_out, nand_24_out);
  nand nand_29 (nand_29_out, nand_25_out, nand_51_out);
  nand nand_30 (nand_30_out, nand_26_out, nand_52_out);
  nand nand_31 (nand_31_out, nand_27_out, nand_53_out);
  xor xor_7 (Q0, nand_28_out, Cin);
  nand nand_32 (nand_32_out, Cin, nand_28_out);
  nand nand_33 (nand_33_out, nand_25_out, nand_29_out);
  nand nand_34 (nand_34_out, nand_29_out, nand_51_out);
  nand nand_35 (nand_35_out, nand_29_out, nand_1_out);
  nand nand_36 (nand_36_out, nand_26_out, nand_30_out);
  nand nand_37 (nand_37_out, nand_30_out, nand_52_out);
  nand nand_38 (nand_38_out, nand_30_out, nand_2_out);
  nand nand_39 (nand_39_out, nand_27_out, nand_31_out);
  nand nand_40 (nand_40_out, nand_31_out, nand_53_out);
  nand nand_41 (nand_41_out, nand_31_out, nand_3_out);
  nand nand_42 (nand_42_out, nand_32_out, nand_4_out);
  nand nand_43 (Q3, nand_33_out, nand_34_out);
  nand nand_44 (nand_44_out, nand_35_out, SC);
  nand nand_45 (Q2, nand_36_out, nand_37_out);
  nand nand_46 (nand_46_out, nand_38_out, SC);
  nand nand_47 (Q1, nand_39_out, nand_40_out);
  nand nand_48 (nand_48_out, nand_41_out, SC);
  nand nand_49 (nand_49_out, nand_42_out, SC);
  nand nand_50 (Cout, nand_44_out, nand_44_out);
  nand nand_51 (nand_51_out, nand_46_out, nand_46_out);
  nand nand_52 (nand_52_out, nand_48_out, nand_48_out);
  nand nand_53 (nand_53_out, nand_49_out, nand_49_out);

  // Other names for the same wires on the sheet: AL = SC

  // Notes on the sheet:
  //   B0: pin 8
  //   Q0: pin 11
  //   B1: pin 7
  //   Q1: pin 12
  //   B2: pin 6
  //   Q2: pin 13
  //   B3: pin 5
  //   Q3: pin 14
  //   I1: pin 17
  //   I0: pin 16
  //   NEG: pin 18
  //   Cin: pin 9
  //   SC: pin 19
  //   Cout: pin 15
  //   A3: pin 1
  //   A2: pin 2
  //   A1: pin 3
  //   A0: pin 4
  //   VCC: pin 20, default 1
  //   GND: pin 10
  //   Invert B
  //   Half Adder
  //   4-bit ALU
  //   2:1 Mux
  //   Suppress Carry
endmodule
