// Digital circuit L8_1.dig as structural Verilog
module L8_1 (
);

  wire _74193_1_pin11, _74193_1_pin12, _74193_1_pin13, _74193_1_pin14, _74193_2_pin12, _74193_2_pin13,
       _74193_3_pin12, _74193_3_pin13, A0, A1, A2, A3, A4, A5, A6, A7, A8, A9, A10, A11, BUS0, BUS1, BUS2,
       BUS7, DN, nCE, nOE, nWE, Q0, Q1, Q2, Q3, Q4, Q5, Q6, Q7, Q8, Q9, Q10, Q11, Q12, Q13, Q14, UP;

  _74193 _74193_1 (
    .pin1(A1), .pin2(Q1), .pin3(Q0), .pin4(DN), .pin5(UP), .pin6(Q2), .pin7(Q3), .pin8(1'b0), .pin9(A3),
    .pin10(A2), .pin11(_74193_1_pin11), .pin12(_74193_1_pin12), .pin13(_74193_1_pin13),
    .pin14(_74193_1_pin14), .pin15(A0), .pin16(1'b1));
  _74193 _74193_2 (
    .pin1(A5), .pin2(Q5), .pin3(Q4), .pin4(_74193_1_pin13), .pin5(_74193_1_pin12), .pin6(Q6), .pin7(Q7),
    .pin8(1'b0), .pin9(A7), .pin10(A6), .pin11(_74193_1_pin11), .pin12(_74193_2_pin12),
    .pin13(_74193_2_pin13), .pin14(_74193_1_pin14), .pin15(A4), .pin16(1'b1));
  _74193 _74193_3 (
    .pin1(A9), .pin2(Q9), .pin3(Q8), .pin4(_74193_2_pin13), .pin5(_74193_2_pin12), .pin6(Q10), .pin7(Q11),
    .pin8(1'b0), .pin9(A11), .pin10(A10), .pin11(_74193_1_pin11), .pin12(_74193_3_pin12),
    .pin13(_74193_3_pin13), .pin14(_74193_1_pin14), .pin15(A8), .pin16(1'b1));
  // _62256 _62256_1: pin names not known; wires that end beside it: Q14, Q12, Q7, Q6, Q5, Q4, Q3, Q2, Q1, Q0, BUS0, BUS1, BUS2, 1'b0, 1'b1, nWE, Q13, Q8, Q9, Q11, nOE, Q10, nCE, BUS7

  // Notes on the sheet:
  //   PROGRAM COUNTER
  //   RAM LO
endmodule
