// Digital circuit Mux_BS_ALU.dig as structural Verilog
module Mux_BS_ALU (
  input  A,
  input  B,
  input  in_3,
  input  in_4,
  input  in_5,
  input  in_6,
  input  F__suppress_carry,
  input  in_8,
  input  in_9,
  input  in_10,
  input  in_11,
  input  in_12,
  input  Cin,
  input  in_14,
  input  in_15,
  input  in_16,
  input  in_17,
  input  F,
  input  in_19,
  input  in_20,
  input  in_21,
  input  in_22,
  input  in_23
);

  wire _74153_1_pin7, _74153_1_pin9, _74153_2_pin7, _74153_2_pin9, nand_1_out;

  LED Carry1 (.in(_74153_1_pin7));
  _74153 _74153_1 (
    .pin1(F__suppress_carry), .pin2(B), .pin3(in_3), .pin4(in_4), .pin5(in_5), .pin6(in_6),
    .pin7(_74153_1_pin7), .pin8(1'b0), .pin9(_74153_1_pin9), .pin10(in_11), .pin11(in_10), .pin12(in_9),
    .pin13(in_8), .pin14(A), .pin15(in_12), .pin16(1'b1));
  _74153 _74153_2 (
    .pin1(F), .pin2(Cin), .pin3(in_14), .pin4(in_15), .pin5(in_16), .pin6(in_17), .pin7(_74153_2_pin7),
    .pin8(1'b0), .pin9(_74153_2_pin9), .pin10(in_22), .pin11(in_21), .pin12(in_20), .pin13(in_19),
    .pin14(_74153_1_pin9), .pin15(in_23), .pin16(1'b1));
  nand nand_1 (nand_1_out, _74153_2_pin7, _74153_1_pin7);
  LED Sum1 (.in(_74153_1_pin9));
  LED Sum_Out (.in(_74153_2_pin9));
  LED Carry_out (.in(nand_1_out));

  // Notes on the sheet:
  //   NAND = 0111
  //   AND = 1000
  //   XOR  = 0110
  //   OR =  1110
  //   XOR = 0110
endmodule
