// Digital circuit NAND_ALU_2_INPUT.dig as structural Verilog
module NAND_ALU_2_INPUT (
  input  A,
  input  nA,
  input  nB,
  input  B,
  input  Cin,
  input  F,
  input  SETC,
  input  C,
  input  I1,
  input  I0,
  input  CLA,
  input  LD,
  output Cout,
  output CLC,
  output CtoFF,
  output Fout,
  output CLR
);

  wire nand_1_out, nand_2_out, nand_3_out, nand_4_out, nand_5_out, nand_6_out, nand_7_out, nand_8_out,
       nand_9_out, nand_10_out, nand_11_out, nand_12_out, nand_16_out, nand_17_out, nand_18_out, nand_19_out,
       nand_20_out, nand_21_out, nand_22_out, nand_23_out, not_1_out;

  nand nand_1 (nand_1_out, A, nA);
  nand nand_2 (nand_2_out, B, nB);
  nand nand_3 (nand_3_out, A, nand_1_out);
  nand nand_4 (nand_4_out, nand_1_out, nA);
  nand nand_5 (nand_5_out, B, nand_2_out);
  nand nand_6 (nand_6_out, nand_2_out, nB);
  nand nand_7 (nand_7_out, nand_3_out, nand_4_out);
  nand nand_8 (nand_8_out, nand_5_out, nand_6_out);
  nand nand_9 (nand_9_out, nand_7_out, nand_8_out);
  nand nand_10 (nand_10_out, nand_7_out, nand_9_out);
  nand nand_11 (nand_11_out, nand_9_out, nand_8_out);
  nand nand_12 (nand_12_out, nand_10_out, nand_11_out);
  nand nand_13 (CtoFF, SETC, C);
  not not_1 (not_1_out, C);
  nand nand_14 (CLC, not_1_out, LD);
  nand nand_15 (CLR, CLA, LD);
  nand nand_16 (nand_16_out, nand_12_out, Cin);
  nand nand_17 (nand_17_out, nand_12_out, nand_16_out);
  nand nand_18 (nand_18_out, nand_16_out, Cin);
  nand nand_19 (nand_19_out, nand_17_out, nand_18_out);
  nand nand_20 (nand_20_out, nand_16_out, nand_9_out);
  nand nand_21 (nand_21_out, nand_19_out, I0);
  nand nand_22 (nand_22_out, I1, nand_20_out);
  nand nand_23 (nand_23_out, nand_20_out, F);
  nand nand_24 (Fout, nand_21_out, nand_22_out);
  not not_2 (Cout, nand_23_out);

  // Other names for the same wires on the sheet: Aout = A; Bout = B

  // Notes on the sheet:
  //   ALU
  //   Carry is only set before Bit 0 of an operation
  //   Any residual carry is cleared before an operation
  //   Suppress Carry
endmodule
