// Digital circuit NAND_BS_ALU.dig as structural Verilog
module NAND_BS_ALU (
  input  A,
  input  nA,
  input  nB,
  input  B,
  input  Cin,
  input  F,
  input  SETC,
  input  C,
  input  I1,
  input  I0,
  input  CLA,
  input  LD,
  output Cout,
  output CLC,
  output CtoFF,
  output Fout,
  output CLR
);

  wire nand_1_out, nand_2_out, nand_3_out, nand_5_out, nand_6_out, nand_7_out, nand_8_out, nand_9_out,
       nand_12_out, nand_13_out, nand_14_out, nand_15_out, nand_16_out, nand_17_out, nand_18_out,
       nand_19_out, nand_20_out, nand_21_out, nand_22_out, nand_24_out, nand_25_out, nand_26_out,
       nand_27_out, nand_28_out, nand_29_out, nand_30_out, nand_31_out, nand_32_out, nand_33_out,
       nand_34_out, nand_35_out, nand_36_out, not_1_out, not_2_out, not_3_out, not_4_out, not_5_out,
       not_6_out;

  nand nand_1 (nand_1_out, not_6_out, B, F, nA, not_4_out);
  not not_1 (not_1_out, C);
  not not_2 (not_2_out, Cin);
  not not_3 (not_3_out, B);
  not not_4 (not_4_out, nB);
  not not_5 (not_5_out, nA);
  not not_6 (not_6_out, A);
  nand nand_2 (nand_2_out, not_6_out, not_3_out, F, nA, nB);
  nand nand_3 (nand_3_out, A, B, F, not_5_out, not_4_out);
  nand nand_4 (Cout, nand_1_out, nand_2_out, nand_3_out, nand_5_out, nand_6_out, nand_7_out, nand_8_out, nand_9_out);
  nand nand_5 (nand_5_out, A, not_3_out, F, not_5_out, nB);
  nand nand_6 (nand_6_out, not_6_out, Cin, F, nA);
  nand nand_7 (nand_7_out, A, Cin, F, not_5_out);
  nand nand_8 (nand_8_out, B, Cin, F, not_4_out);
  nand nand_9 (nand_9_out, not_3_out, Cin, F, nB);
  nand nand_10 (CLC, not_1_out, LD);
  nand nand_11 (CtoFF, C, SETC);
  nand nand_12 (nand_12_out, not_6_out, not_3_out, Cin, I0, not_5_out, not_4_out);
  nand nand_13 (nand_13_out, not_6_out, B, not_2_out, I0, not_5_out, not_4_out);
  nand nand_14 (nand_14_out, not_6_out, not_3_out, not_2_out, I0, not_5_out, nB);
  nand nand_15 (nand_15_out, not_6_out, B, Cin, I0, not_5_out, nB);
  nand nand_16 (nand_16_out, not_6_out, not_3_out, not_2_out, I0, nA, not_4_out);
  nand nand_17 (nand_17_out, not_6_out, B, Cin, I0, nA, not_4_out);
  nand nand_18 (nand_18_out, not_6_out, not_3_out, Cin, I0, nA, nB);
  nand nand_19 (nand_19_out, not_6_out, B, not_2_out, I0, nA, nB);
  nand nand_20 (nand_20_out, A, not_3_out, not_2_out, I0, not_5_out, not_4_out);
  nand nand_21 (nand_21_out, A, B, Cin, I0, not_5_out, not_4_out);
  nand nand_22 (nand_22_out, A, not_3_out, Cin, I0, not_5_out, nB);
  nand nand_23 (Fout, nand_12_out, nand_13_out, nand_14_out, nand_15_out, nand_16_out, nand_17_out, nand_18_out, nand_19_out, nand_20_out, nand_21_out, nand_22_out, nand_24_out, nand_25_out, nand_26_out, nand_27_out, nand_28_out, nand_29_out, nand_30_out, nand_31_out, nand_32_out, nand_33_out, nand_34_out, nand_35_out, nand_36_out);
  nand nand_24 (nand_24_out, A, B, not_2_out, I0, not_5_out, nB);
  nand nand_25 (nand_25_out, A, not_3_out, Cin, I0, nA, not_4_out);
  nand nand_26 (nand_26_out, A, B, not_2_out, I0, nA, not_4_out);
  nand nand_27 (nand_27_out, A, not_3_out, not_2_out, I0, nA, nB);
  nand nand_28 (nand_28_out, A, B, Cin, I0, nA, nB);
  nand nand_29 (nand_29_out, not_6_out, B, I1, nA, not_4_out);
  nand nand_30 (nand_30_out, not_6_out, not_3_out, I1, nA, nB);
  nand nand_31 (nand_31_out, A, B, I1, not_5_out, not_4_out);
  nand nand_32 (nand_32_out, A, not_3_out, I1, not_5_out, nB);
  nand nand_33 (nand_33_out, not_6_out, Cin, I1, nA);
  nand nand_34 (nand_34_out, A, Cin, I1, not_5_out);
  nand nand_35 (nand_35_out, B, Cin, I1, not_4_out);
  nand nand_36 (nand_36_out, not_3_out, Cin, I1, nB);
  nand nand_37 (CLR, CLA, LD);
endmodule
