// Digital circuit NAND_Hack.dig as structural Verilog
module NAND_Hack (
  input  D0,
  input  CLK,
  input  I1,
  input  I0,
  input  I2,
  input  SC,
  input  D1,
  input  D2,
  input  D3,
  input  D4,
  input  D5,
  input  D6,
  input  D7,
  input  I4,
  input  I5,
  input  I3,
  input  P0,
  input  CLK_2,
  input  P1,
  input  P2,
  input  P3,
  input  LD,
  input  INC,
  input  in_37,
  input  P4,
  input  P5,
  input  P6,
  input  P7,
  input  in_46,
  input  in_47,
  input  in_48,
  input  in_49,
  input  in_50,
  input  in_51,
  input  in_52,
  input  in_53,
  input  in_54,
  input  in_55,
  input  in_56,
  input  in_57,
  input  in_58,
  input  in_59,
  input  in_60,
  input  in_61,
  input  S1,
  input  S0,
  input  INV,
  input  CK,
  input  in_82,
  input  in_83,
  input  in_84,
  input  in_85,
  input  in_86,
  input  in_87,
  input  in_88,
  input  in_89,
  input  in_90,
  input  in_91,
  output Q0,
  output Q1,
  output Q2,
  output Q3,
  output Q4,
  output Q5,
  output Q6,
  output Q7,
  output Cout,
  output A0,
  output A1,
  output A2,
  output A3,
  output A4,
  output A5,
  output A6,
  output A7,
  output out_62,
  output out_63,
  output out_64,
  output out_65,
  output out_66,
  output out_67,
  output out_68,
  output out_69,
  output A16,
  output A17,
  output A18,
  output A19,
  output A20,
  output A21,
  output A22,
  output A23
);

  wire F0, F1, F2, F3, F4, F5, F6, F7, nand_1_out, nand_2_out, nand_3_out, nand_4_out, nand_5_out,
       nand_6_out, nand_7_out, nand_8_out, nand_9_out, nand_10_out, nand_11_out, nand_12_out, nand_13_out,
       nand_14_out, nand_15_out, nand_16_out, nand_17_out, nand_18_out, nand_19_out, nand_20_out,
       nand_21_out, nand_22_out, nand_23_out, nand_24_out, nand_25_out, nand_26_out, nand_27_out,
       nand_28_out, nand_29_out, nand_30_out, nand_31_out, nand_32_out, nand_33_out, nand_34_out,
       nand_35_out, nand_36_out, nand_37_out, nand_38_out, nand_39_out, nand_40_out, nand_41_out,
       nand_42_out, nand_43_out, nand_44_out, nand_45_out, nand_46_out, nand_47_out, nand_48_out,
       nand_49_out, nand_50_out, nand_51_out, nand_52_out, nand_53_out, nand_54_out, nand_55_out,
       nand_56_out, nand_57_out, nand_58_out, nand_59_out, nand_60_out, nand_61_out, nand_62_out,
       nand_63_out, nand_64_out, nand_65_out, nand_66_out, nand_67_out, nand_68_out, nand_69_out,
       nand_70_out, nand_71_out, nand_72_out, nand_73_out, nand_74_out, nand_75_out, nand_76_out,
       nand_77_out, nand_78_out, nand_79_out, nand_80_out, nand_81_out, nand_82_out, nand_83_out,
       nand_84_out, nand_85_out, nand_86_out, nand_87_out, nand_88_out, nand_89_out, nand_90_out,
       nand_91_out, nand_92_out, nand_93_out, nand_94_out, nand_95_out, nand_96_out, nand_97_out,
       nand_98_out, nand_99_out, nand_100_out, nand_101_out, nand_102_out, nand_103_out, nand_104_out,
       nand_105_out, nand_106_out, nand_107_out, nand_108_out, nand_109_out, nand_110_out, nand_111_out,
       nand_112_out, nand_113_out, nand_114_out, nand_115_out, nand_116_out, nand_117_out, nand_118_out,
       nand_119_out, nand_120_out, nand_121_out, nand_122_out, nand_123_out, nand_124_out, nand_125_out,
       nand_126_out, nand_127_out, nand_128_out, nand_130_out, nand_132_out, nand_134_out, nand_136_out,
       nand_138_out, nand_140_out, nand_142_out, nand_144_out, nand_146_out, nand_147_out, nand_148_out,
       nand_149_out, nand_150_out, nand_151_out, nand_152_out, nand_153_out, nand_154_out, nand_155_out,
       nand_156_out, nand_157_out, nand_158_out, nand_159_out, nand_160_out, nand_161_out, nand_162_out,
       nand_163_out, nand_164_out, nand_165_out, nand_166_out, nand_167_out, nand_168_out, nand_169_out,
       nand_170_out, nand_171_out, nand_172_out, nand_173_out, nand_174_out, nand_175_out, nand_176_out,
       nand_177_out, nand_178_out, nand_179_out, nand_180_out, nand_181_out, nand_182_out, nand_183_out,
       nand_184_out, nand_185_out, nand_186_out, nand_187_out, nand_188_out, nand_189_out, nand_190_out,
       nand_191_out, nand_192_out, nand_193_out, nand_194_out, nand_195_out, nand_196_out, nand_197_out,
       nand_198_out, nand_199_out, nand_200_out, nand_201_out, nand_202_out, nand_203_out, nand_204_out,
       nand_205_out, nand_206_out, nand_207_out, nand_208_out, nand_209_out, nand_210_out, nand_211_out,
       nand_212_out, nand_213_out, nand_214_out, nand_215_out, nand_216_out, nand_217_out, nand_218_out,
       nand_219_out, nand_220_out, nand_221_out, nand_222_out, nand_223_out, nand_224_out, nand_225_out,
       nand_226_out, nand_227_out, nand_228_out, nand_229_out, nand_230_out, nand_231_out, nand_232_out,
       nand_233_out, nand_242_out, nand_243_out, nand_244_out, nand_245_out, nand_246_out, nand_247_out,
       nand_248_out, nand_249_out, nand_250_out, nand_251_out, nand_252_out, nand_253_out, nand_254_out,
       nand_255_out, nand_256_out, nand_257_out, nand_258_out, nand_259_out, nand_260_out, nand_261_out,
       nand_262_out, nand_263_out, nand_264_out, nand_265_out, nand_266_out, nand_267_out, nand_268_out,
       nand_269_out, nand_270_out, nand_271_out, nand_272_out, nand_273_out, nand_274_out, nand_275_out,
       nand_276_out, nand_277_out, nand_278_out, nand_279_out, nand_280_out, nand_281_out, nand_282_out,
       nand_283_out, nand_284_out, nand_285_out, nand_286_out, nand_287_out, nand_288_out, nand_289_out,
       nand_290_out, nand_291_out, nand_292_out, nand_293_out, nand_294_out, nand_295_out, nand_296_out,
       nand_297_out, nand_298_out, nand_299_out, nand_300_out, nand_301_out, nand_302_out, nand_303_out,
       nand_304_out, nand_305_out, nand_306_out, nand_307_out, nand_308_out, nand_309_out, nand_310_out,
       nand_311_out, nand_312_out, nand_313_out, nand_314_out, nand_315_out, nand_316_out, nand_317_out,
       nand_318_out, nand_319_out, nand_320_out, nand_321_out, nand_322_out, nand_323_out, nand_324_out,
       nand_325_out, nand_326_out, nand_327_out, nand_328_out, nand_329_out, nand_330_out, nand_331_out,
       nand_332_out, nand_333_out, nand_334_out, nand_335_out, nand_336_out, nand_337_out, nand_338_out,
       nand_339_out, nand_340_out, nand_341_out, nand_342_out, nand_343_out, nand_344_out, nand_345_out,
       nand_346_out, nand_347_out, nand_348_out, nand_349_out, nand_350_out, nand_351_out, nand_352_out,
       nand_353_out, nand_354_out, nand_355_out, nand_356_out, nand_357_out, nand_358_out, nand_359_out,
       nand_360_out, nand_361_out, nand_362_out, nand_363_out, nand_364_out, nand_365_out, nand_366_out,
       nand_367_out, nand_368_out, nand_369_out, nand_370_out, nand_371_out, nand_372_out, nand_373_out,
       nand_374_out, nand_375_out, nand_376_out, nand_377_out, nand_378_out, nand_379_out, nand_380_out,
       nand_381_out, nand_382_out, nand_383_out, nand_384_out, nand_385_out, nand_386_out, nand_388_out,
       nand_390_out, nand_392_out, nand_394_out, nand_396_out, nand_398_out, nand_400_out, nand_402_out,
       nand_403_out, nand_404_out, nand_405_out, nand_406_out, nand_407_out, nand_408_out, nand_409_out,
       nand_410_out, nand_411_out, nand_412_out, nand_413_out, nand_414_out, nand_415_out, nand_416_out,
       nand_417_out, nand_418_out, nand_427_out, nand_428_out, nand_429_out, nand_430_out, nand_431_out,
       nand_432_out, nand_433_out, nand_434_out, nand_435_out, nand_436_out, nand_437_out, nand_438_out,
       nand_439_out, nand_440_out, nand_441_out, nand_442_out, nand_443_out, nand_444_out, nand_445_out,
       nand_446_out, nand_447_out, nand_448_out, nand_449_out, nand_450_out, nand_451_out, nand_452_out,
       nand_453_out, nand_454_out, nand_455_out, nand_456_out, nand_457_out, nand_458_out, nand_459_out,
       nand_460_out, nand_461_out, nand_462_out, nand_463_out, nand_464_out, nand_465_out, nand_466_out,
       nand_467_out, nand_468_out, nand_469_out, nand_470_out, nand_471_out, nand_472_out, nand_473_out,
       nand_474_out, nand_475_out, nand_476_out, nand_477_out, nand_478_out, nand_479_out, nand_480_out,
       nand_481_out, nand_482_out, nand_483_out, nand_484_out, nand_485_out, nand_486_out, nand_487_out,
       nand_488_out, nand_489_out, nand_490_out, nand_491_out, nand_492_out, nand_493_out, nand_494_out,
       nand_495_out, nand_496_out, nand_497_out, nand_498_out, nand_499_out, nand_501_out, nand_503_out,
       nand_505_out, nand_507_out, nand_509_out, nand_511_out, nand_513_out, nand_515_out;

  Seven_Seg_Hex seven_seg_hex_1 (.d({F7, F6, F5, F4}), .dp(1'b0));
  Seven_Seg_Hex seven_seg_hex_2 (.d({F3, F2, F1, F0}), .dp(1'b0));
  Seven_Seg_Hex seven_seg_hex_3 (.d({Q7, Q6, Q5, Q4}), .dp(1'b0));
  Seven_Seg_Hex seven_seg_hex_4 (.d({Q3, Q2, Q1, Q0}), .dp(1'b0));
  Seven_Seg_Hex seven_seg_hex_5 (.d({D7, D6, D5, D4}), .dp(1'b0));
  Seven_Seg_Hex seven_seg_hex_6 (.d({D3, D2, D1, D0}), .dp(1'b0));
  nand nand_1 (nand_1_out, D7, I3);
  nand nand_2 (nand_2_out, D6, I3);
  nand nand_3 (nand_3_out, D5, I3);
  nand nand_4 (nand_4_out, D4, I3);
  nand nand_5 (nand_5_out, D3, I3);
  nand nand_6 (nand_6_out, D2, I3);
  nand nand_7 (nand_7_out, D1, I3);
  nand nand_8 (nand_8_out, D0, I3);
  nand nand_9 (nand_9_out, D7, nand_1_out);
  nand nand_10 (nand_10_out, nand_1_out, I3);
  nand nand_11 (nand_11_out, D6, nand_2_out);
  nand nand_12 (nand_12_out, nand_2_out, I3);
  nand nand_13 (nand_13_out, D5, nand_3_out);
  nand nand_14 (nand_14_out, nand_3_out, I3);
  nand nand_15 (nand_15_out, D4, nand_4_out);
  nand nand_16 (nand_16_out, nand_4_out, I3);
  nand nand_17 (nand_17_out, D3, nand_5_out);
  nand nand_18 (nand_18_out, nand_5_out, I3);
  nand nand_19 (nand_19_out, D2, nand_6_out);
  nand nand_20 (nand_20_out, nand_6_out, I3);
  nand nand_21 (nand_21_out, D1, nand_7_out);
  nand nand_22 (nand_22_out, nand_7_out, I3);
  nand nand_23 (nand_23_out, D0, nand_8_out);
  nand nand_24 (nand_24_out, nand_8_out, I3);
  nand nand_25 (nand_25_out, nand_9_out, nand_10_out);
  nand nand_26 (nand_26_out, nand_11_out, nand_12_out);
  nand nand_27 (nand_27_out, nand_13_out, nand_14_out);
  nand nand_28 (nand_28_out, nand_15_out, nand_16_out);
  nand nand_29 (nand_29_out, nand_17_out, nand_18_out);
  nand nand_30 (nand_30_out, nand_19_out, nand_20_out);
  nand nand_31 (nand_31_out, nand_21_out, nand_22_out);
  nand nand_32 (nand_32_out, nand_23_out, nand_24_out);
  nand nand_33 (nand_33_out, Q7, nand_25_out);
  nand nand_34 (nand_34_out, Q6, nand_26_out);
  nand nand_35 (nand_35_out, Q5, nand_27_out);
  nand nand_36 (nand_36_out, Q4, nand_28_out);
  nand nand_37 (nand_37_out, Q3, nand_29_out);
  nand nand_38 (nand_38_out, Q2, nand_30_out);
  nand nand_39 (nand_39_out, Q1, nand_31_out);
  nand nand_40 (nand_40_out, Q0, nand_32_out);
  nand nand_41 (nand_41_out, Q7, nand_33_out);
  nand nand_42 (nand_42_out, nand_33_out, nand_33_out);
  nand nand_43 (nand_43_out, nand_33_out, nand_25_out);
  nand nand_44 (nand_44_out, Q6, nand_34_out);
  nand nand_45 (nand_45_out, nand_34_out, nand_34_out);
  nand nand_46 (nand_46_out, nand_34_out, nand_26_out);
  nand nand_47 (nand_47_out, Q5, nand_35_out);
  nand nand_48 (nand_48_out, nand_35_out, nand_35_out);
  nand nand_49 (nand_49_out, nand_35_out, nand_27_out);
  nand nand_50 (nand_50_out, Q4, nand_36_out);
  nand nand_51 (nand_51_out, nand_36_out, nand_36_out);
  nand nand_52 (nand_52_out, nand_36_out, nand_28_out);
  nand nand_53 (nand_53_out, Q3, nand_37_out);
  nand nand_54 (nand_54_out, nand_37_out, nand_37_out);
  nand nand_55 (nand_55_out, nand_37_out, nand_29_out);
  nand nand_56 (nand_56_out, Q2, nand_38_out);
  nand nand_57 (nand_57_out, nand_38_out, nand_38_out);
  nand nand_58 (nand_58_out, nand_38_out, nand_30_out);
  nand nand_59 (nand_59_out, Q1, nand_39_out);
  nand nand_60 (nand_60_out, nand_39_out, nand_39_out);
  nand nand_61 (nand_61_out, nand_39_out, nand_31_out);
  nand nand_62 (nand_62_out, Q0, nand_40_out);
  nand nand_63 (nand_63_out, nand_40_out, nand_40_out);
  nand nand_64 (nand_64_out, nand_40_out, nand_32_out);
  nand nand_65 (nand_65_out, nand_41_out, nand_43_out);
  nand nand_66 (nand_66_out, nand_44_out, nand_46_out);
  nand nand_67 (nand_67_out, nand_47_out, nand_49_out);
  nand nand_68 (nand_68_out, nand_50_out, nand_52_out);
  nand nand_69 (nand_69_out, nand_53_out, nand_55_out);
  nand nand_70 (nand_70_out, nand_56_out, nand_58_out);
  nand nand_71 (nand_71_out, nand_59_out, nand_61_out);
  nand nand_72 (nand_72_out, nand_62_out, nand_64_out);
  nand nand_73 (nand_73_out, nand_42_out, I1);
  nand nand_74 (nand_74_out, nand_65_out, I0);
  nand nand_75 (nand_75_out, nand_45_out, I1);
  nand nand_76 (nand_76_out, nand_66_out, I0);
  nand nand_77 (nand_77_out, nand_48_out, I1);
  nand nand_78 (nand_78_out, nand_67_out, I0);
  nand nand_79 (nand_79_out, nand_51_out, I1);
  nand nand_80 (nand_80_out, nand_68_out, I0);
  nand nand_81 (nand_81_out, nand_54_out, I1);
  nand nand_82 (nand_82_out, nand_69_out, I0);
  nand nand_83 (nand_83_out, nand_57_out, I1);
  nand nand_84 (nand_84_out, nand_70_out, I0);
  nand nand_85 (nand_85_out, nand_60_out, I1);
  nand nand_86 (nand_86_out, nand_71_out, I0);
  nand nand_87 (nand_87_out, nand_63_out, I1);
  nand nand_88 (nand_88_out, nand_72_out, I0);
  nand nand_89 (nand_89_out, nand_73_out, nand_74_out);
  nand nand_90 (nand_90_out, nand_75_out, nand_76_out);
  nand nand_91 (nand_91_out, nand_77_out, nand_78_out);
  nand nand_92 (nand_92_out, nand_79_out, nand_80_out);
  nand nand_93 (nand_93_out, nand_81_out, nand_82_out);
  nand nand_94 (nand_94_out, nand_83_out, nand_84_out);
  nand nand_95 (nand_95_out, nand_85_out, nand_86_out);
  nand nand_96 (nand_96_out, nand_87_out, nand_88_out);
  nand nand_97 (nand_97_out, nand_89_out, nand_146_out);
  nand nand_98 (nand_98_out, nand_90_out, nand_147_out);
  nand nand_99 (nand_99_out, nand_91_out, nand_148_out);
  nand nand_100 (nand_100_out, nand_92_out, nand_149_out);
  nand nand_101 (nand_101_out, nand_93_out, nand_150_out);
  nand nand_102 (nand_102_out, nand_94_out, nand_151_out);
  nand nand_103 (nand_103_out, nand_95_out, nand_152_out);
  nand nand_104 (nand_104_out, nand_96_out, I2);
  nand nand_105 (nand_105_out, nand_89_out, nand_97_out);
  nand nand_106 (nand_106_out, nand_97_out, nand_146_out);
  nand nand_107 (nand_107_out, nand_97_out, nand_33_out);
  nand nand_108 (nand_108_out, nand_90_out, nand_98_out);
  nand nand_109 (nand_109_out, nand_98_out, nand_147_out);
  nand nand_110 (nand_110_out, nand_98_out, nand_34_out);
  nand nand_111 (nand_111_out, nand_91_out, nand_99_out);
  nand nand_112 (nand_112_out, nand_99_out, nand_148_out);
  nand nand_113 (nand_113_out, nand_99_out, nand_35_out);
  nand nand_114 (nand_114_out, nand_92_out, nand_100_out);
  nand nand_115 (nand_115_out, nand_100_out, nand_149_out);
  nand nand_116 (nand_116_out, nand_100_out, nand_36_out);
  nand nand_117 (nand_117_out, nand_93_out, nand_101_out);
  nand nand_118 (nand_118_out, nand_101_out, nand_150_out);
  nand nand_119 (nand_119_out, nand_101_out, nand_37_out);
  nand nand_120 (nand_120_out, nand_94_out, nand_102_out);
  nand nand_121 (nand_121_out, nand_102_out, nand_151_out);
  nand nand_122 (nand_122_out, nand_102_out, nand_38_out);
  nand nand_123 (nand_123_out, nand_95_out, nand_103_out);
  nand nand_124 (nand_124_out, nand_103_out, nand_152_out);
  nand nand_125 (nand_125_out, nand_103_out, nand_39_out);
  nand nand_126 (nand_126_out, nand_96_out, nand_104_out);
  nand nand_127 (nand_127_out, nand_104_out, I2);
  nand nand_128 (nand_128_out, nand_104_out, nand_40_out);
  nand nand_129 (F7, nand_105_out, nand_106_out);
  nand nand_130 (nand_130_out, nand_107_out, SC);
  nand nand_131 (F6, nand_108_out, nand_109_out);
  nand nand_132 (nand_132_out, nand_110_out, SC);
  nand nand_133 (F5, nand_111_out, nand_112_out);
  nand nand_134 (nand_134_out, nand_113_out, SC);
  nand nand_135 (F4, nand_114_out, nand_115_out);
  nand nand_136 (nand_136_out, nand_116_out, SC);
  nand nand_137 (F3, nand_117_out, nand_118_out);
  nand nand_138 (nand_138_out, nand_119_out, SC);
  nand nand_139 (F2, nand_120_out, nand_121_out);
  nand nand_140 (nand_140_out, nand_122_out, SC);
  nand nand_141 (F1, nand_123_out, nand_124_out);
  nand nand_142 (nand_142_out, nand_125_out, SC);
  nand nand_143 (F0, nand_126_out, nand_127_out);
  nand nand_144 (nand_144_out, nand_128_out, SC);
  nand nand_145 (Cout, nand_130_out, nand_130_out);
  nand nand_146 (nand_146_out, nand_132_out, nand_132_out);
  nand nand_147 (nand_147_out, nand_134_out, nand_134_out);
  nand nand_148 (nand_148_out, nand_136_out, nand_136_out);
  nand nand_149 (nand_149_out, nand_138_out, nand_138_out);
  nand nand_150 (nand_150_out, nand_140_out, nand_140_out);
  nand nand_151 (nand_151_out, nand_142_out, nand_142_out);
  nand nand_152 (nand_152_out, nand_144_out, nand_144_out);
  nand nand_153 (nand_153_out, CLK, CLK);
  nand nand_154 (nand_154_out, F7, nand_153_out);
  nand nand_155 (nand_155_out, nand_154_out, nand_153_out);
  nand nand_156 (nand_156_out, F6, nand_153_out);
  nand nand_157 (nand_157_out, nand_156_out, nand_153_out);
  nand nand_158 (nand_158_out, F5, nand_153_out);
  nand nand_159 (nand_159_out, nand_158_out, nand_153_out);
  nand nand_160 (nand_160_out, F4, nand_153_out);
  nand nand_161 (nand_161_out, nand_160_out, nand_153_out);
  nand nand_162 (nand_162_out, F3, nand_153_out);
  nand nand_163 (nand_163_out, nand_162_out, nand_153_out);
  nand nand_164 (nand_164_out, F2, nand_153_out);
  nand nand_165 (nand_165_out, nand_164_out, nand_153_out);
  nand nand_166 (nand_166_out, F1, nand_153_out);
  nand nand_167 (nand_167_out, nand_166_out, nand_153_out);
  nand nand_168 (nand_168_out, F0, nand_153_out);
  nand nand_169 (nand_169_out, nand_168_out, nand_153_out);
  nand nand_170 (nand_170_out, nand_154_out, nand_171_out);
  nand nand_171 (nand_171_out, nand_170_out, nand_155_out);
  nand nand_172 (nand_172_out, nand_156_out, nand_173_out);
  nand nand_173 (nand_173_out, nand_172_out, nand_157_out);
  nand nand_174 (nand_174_out, nand_158_out, nand_175_out);
  nand nand_175 (nand_175_out, nand_174_out, nand_159_out);
  nand nand_176 (nand_176_out, nand_160_out, nand_177_out);
  nand nand_177 (nand_177_out, nand_176_out, nand_161_out);
  nand nand_178 (nand_178_out, nand_162_out, nand_179_out);
  nand nand_179 (nand_179_out, nand_178_out, nand_163_out);
  nand nand_180 (nand_180_out, nand_164_out, nand_181_out);
  nand nand_181 (nand_181_out, nand_180_out, nand_165_out);
  nand nand_182 (nand_182_out, nand_166_out, nand_183_out);
  nand nand_183 (nand_183_out, nand_182_out, nand_167_out);
  nand nand_184 (nand_184_out, nand_168_out, nand_185_out);
  nand nand_185 (nand_185_out, nand_184_out, nand_169_out);
  nand nand_186 (nand_186_out, nand_170_out, CLK);
  nand nand_187 (nand_187_out, nand_186_out, CLK);
  nand nand_188 (nand_188_out, nand_172_out, CLK);
  nand nand_189 (nand_189_out, nand_188_out, CLK);
  nand nand_190 (nand_190_out, nand_174_out, CLK);
  nand nand_191 (nand_191_out, nand_190_out, CLK);
  nand nand_192 (nand_192_out, nand_176_out, CLK);
  nand nand_193 (nand_193_out, nand_192_out, CLK);
  nand nand_194 (nand_194_out, nand_178_out, CLK);
  nand nand_195 (nand_195_out, nand_194_out, CLK);
  nand nand_196 (nand_196_out, nand_180_out, CLK);
  nand nand_197 (nand_197_out, nand_196_out, CLK);
  nand nand_198 (nand_198_out, nand_182_out, CLK);
  nand nand_199 (nand_199_out, nand_198_out, CLK);
  nand nand_200 (nand_200_out, nand_184_out, CLK);
  nand nand_201 (nand_201_out, nand_200_out, CLK);
  nand nand_202 (nand_202_out, nand_186_out, nand_203_out);
  nand nand_203 (nand_203_out, nand_202_out, nand_187_out);
  nand nand_204 (nand_204_out, nand_188_out, nand_205_out);
  nand nand_205 (nand_205_out, nand_204_out, nand_189_out);
  nand nand_206 (nand_206_out, nand_190_out, nand_207_out);
  nand nand_207 (nand_207_out, nand_206_out, nand_191_out);
  nand nand_208 (nand_208_out, nand_192_out, nand_209_out);
  nand nand_209 (nand_209_out, nand_208_out, nand_193_out);
  nand nand_210 (nand_210_out, nand_194_out, nand_211_out);
  nand nand_211 (nand_211_out, nand_210_out, nand_195_out);
  nand nand_212 (nand_212_out, nand_196_out, nand_213_out);
  nand nand_213 (nand_213_out, nand_212_out, nand_197_out);
  nand nand_214 (nand_214_out, nand_198_out, nand_215_out);
  nand nand_215 (nand_215_out, nand_214_out, nand_199_out);
  nand nand_216 (nand_216_out, nand_200_out, nand_217_out);
  nand nand_217 (nand_217_out, nand_216_out, nand_201_out);
  nand nand_218 (nand_218_out, nand_202_out, I4);
  nand nand_219 (nand_219_out, I5, nand_203_out);
  nand nand_220 (nand_220_out, nand_204_out, I4);
  nand nand_221 (nand_221_out, I5, nand_205_out);
  nand nand_222 (nand_222_out, nand_206_out, I4);
  nand nand_223 (nand_223_out, I5, nand_207_out);
  nand nand_224 (nand_224_out, nand_208_out, I4);
  nand nand_225 (nand_225_out, I5, nand_209_out);
  nand nand_226 (nand_226_out, nand_210_out, I4);
  nand nand_227 (nand_227_out, I5, nand_211_out);
  nand nand_228 (nand_228_out, nand_212_out, I4);
  nand nand_229 (nand_229_out, I5, nand_213_out);
  nand nand_230 (nand_230_out, nand_214_out, I4);
  nand nand_231 (nand_231_out, I5, nand_215_out);
  nand nand_232 (nand_232_out, nand_216_out, I4);
  nand nand_233 (nand_233_out, I5, nand_217_out);
  nand nand_234 (Q7, nand_218_out, nand_219_out);
  nand nand_235 (Q6, nand_220_out, nand_221_out);
  nand nand_236 (Q5, nand_222_out, nand_223_out);
  nand nand_237 (Q4, nand_224_out, nand_225_out);
  nand nand_238 (Q3, nand_226_out, nand_227_out);
  nand nand_239 (Q2, nand_228_out, nand_229_out);
  nand nand_240 (Q1, nand_230_out, nand_231_out);
  nand nand_241 (Q0, nand_232_out, nand_233_out);
  nand nand_242 (nand_242_out, P7, INV);
  nand nand_243 (nand_243_out, P6, INV);
  nand nand_244 (nand_244_out, P5, INV);
  nand nand_245 (nand_245_out, P4, INV);
  nand nand_246 (nand_246_out, P3, INV);
  nand nand_247 (nand_247_out, P2, INV);
  nand nand_248 (nand_248_out, P1, INV);
  nand nand_249 (nand_249_out, P0, INV);
  nand nand_250 (nand_250_out, P7, nand_242_out);
  nand nand_251 (nand_251_out, nand_242_out, INV);
  nand nand_252 (nand_252_out, P6, nand_243_out);
  nand nand_253 (nand_253_out, nand_243_out, INV);
  nand nand_254 (nand_254_out, P5, nand_244_out);
  nand nand_255 (nand_255_out, nand_244_out, INV);
  nand nand_256 (nand_256_out, P4, nand_245_out);
  nand nand_257 (nand_257_out, nand_245_out, INV);
  nand nand_258 (nand_258_out, P3, nand_246_out);
  nand nand_259 (nand_259_out, nand_246_out, INV);
  nand nand_260 (nand_260_out, P2, nand_247_out);
  nand nand_261 (nand_261_out, nand_247_out, INV);
  nand nand_262 (nand_262_out, P1, nand_248_out);
  nand nand_263 (nand_263_out, nand_248_out, INV);
  nand nand_264 (nand_264_out, P0, nand_249_out);
  nand nand_265 (nand_265_out, nand_249_out, INV);
  Seven_Seg_Hex seven_seg_hex_7 (.d({A7, A6, A5, A4}), .dp(1'b0));
  Seven_Seg_Hex seven_seg_hex_8 (.d({A3, A2, A1, A0}), .dp(1'b0));
  nand nand_266 (nand_266_out, nand_250_out, nand_251_out);
  nand nand_267 (nand_267_out, nand_252_out, nand_253_out);
  nand nand_268 (nand_268_out, nand_254_out, nand_255_out);
  nand nand_269 (nand_269_out, nand_256_out, nand_257_out);
  nand nand_270 (nand_270_out, nand_258_out, nand_259_out);
  nand nand_271 (nand_271_out, nand_260_out, nand_261_out);
  nand nand_272 (nand_272_out, nand_262_out, nand_263_out);
  nand nand_273 (nand_273_out, nand_264_out, nand_265_out);
  nand nand_274 (nand_274_out, A7, nand_286_out);
  nand nand_275 (nand_275_out, A6, nand_289_out);
  nand nand_276 (nand_276_out, A5, nand_292_out);
  nand nand_277 (nand_277_out, A4, nand_295_out);
  nand nand_278 (nand_278_out, A3, nand_298_out);
  nand nand_279 (nand_279_out, A2, nand_301_out);
  nand nand_280 (nand_280_out, A1, nand_304_out);
  nand nand_281 (nand_281_out, A0, in_37);
  nand nand_282 (nand_282_out, A7, nand_274_out);
  nand nand_283 (nand_283_out, nand_274_out, nand_274_out);
  nand nand_284 (nand_284_out, nand_274_out, nand_286_out);
  nand nand_285 (nand_285_out, A6, nand_275_out);
  nand nand_286 (nand_286_out, nand_275_out, nand_275_out);
  nand nand_287 (nand_287_out, nand_275_out, nand_289_out);
  nand nand_288 (nand_288_out, A5, nand_276_out);
  nand nand_289 (nand_289_out, nand_276_out, nand_276_out);
  nand nand_290 (nand_290_out, nand_276_out, nand_292_out);
  nand nand_291 (nand_291_out, A4, nand_277_out);
  nand nand_292 (nand_292_out, nand_277_out, nand_277_out);
  nand nand_293 (nand_293_out, nand_277_out, nand_295_out);
  nand nand_294 (nand_294_out, A3, nand_278_out);
  nand nand_295 (nand_295_out, nand_278_out, nand_278_out);
  nand nand_296 (nand_296_out, nand_278_out, nand_298_out);
  nand nand_297 (nand_297_out, A2, nand_279_out);
  nand nand_298 (nand_298_out, nand_279_out, nand_279_out);
  nand nand_299 (nand_299_out, nand_279_out, nand_301_out);
  nand nand_300 (nand_300_out, A1, nand_280_out);
  nand nand_301 (nand_301_out, nand_280_out, nand_280_out);
  nand nand_302 (nand_302_out, nand_280_out, nand_304_out);
  nand nand_303 (nand_303_out, A0, nand_281_out);
  nand nand_304 (nand_304_out, nand_281_out, nand_281_out);
  nand nand_305 (nand_305_out, nand_281_out, in_37);
  nand nand_306 (nand_306_out, nand_282_out, nand_284_out);
  nand nand_307 (nand_307_out, nand_285_out, nand_287_out);
  nand nand_308 (nand_308_out, nand_288_out, nand_290_out);
  nand nand_309 (nand_309_out, nand_291_out, nand_293_out);
  nand nand_310 (nand_310_out, nand_294_out, nand_296_out);
  nand nand_311 (nand_311_out, nand_297_out, nand_299_out);
  nand nand_312 (nand_312_out, nand_300_out, nand_302_out);
  nand nand_313 (nand_313_out, nand_303_out, nand_305_out);
  nand nand_314 (nand_314_out, nand_266_out, LD);
  nand nand_315 (nand_315_out, nand_306_out, INC);
  nand nand_316 (nand_316_out, nand_267_out, LD);
  nand nand_317 (nand_317_out, nand_307_out, INC);
  nand nand_318 (nand_318_out, nand_268_out, LD);
  nand nand_319 (nand_319_out, nand_308_out, INC);
  nand nand_320 (nand_320_out, nand_269_out, LD);
  nand nand_321 (nand_321_out, nand_309_out, INC);
  nand nand_322 (nand_322_out, nand_270_out, LD);
  nand nand_323 (nand_323_out, nand_310_out, INC);
  nand nand_324 (nand_324_out, nand_271_out, LD);
  nand nand_325 (nand_325_out, nand_311_out, INC);
  nand nand_326 (nand_326_out, nand_272_out, LD);
  nand nand_327 (nand_327_out, nand_312_out, INC);
  nand nand_328 (nand_328_out, nand_273_out, LD);
  nand nand_329 (nand_329_out, nand_313_out, INC);
  nand nand_330 (nand_330_out, nand_314_out, nand_315_out);
  nand nand_331 (nand_331_out, nand_316_out, nand_317_out);
  nand nand_332 (nand_332_out, nand_318_out, nand_319_out);
  nand nand_333 (nand_333_out, nand_320_out, nand_321_out);
  nand nand_334 (nand_334_out, nand_322_out, nand_323_out);
  nand nand_335 (nand_335_out, nand_324_out, nand_325_out);
  nand nand_336 (nand_336_out, nand_326_out, nand_327_out);
  nand nand_337 (nand_337_out, nand_328_out, nand_329_out);
  nand nand_338 (nand_338_out, CLK_2, CLK_2);
  nand nand_339 (nand_339_out, nand_330_out, nand_338_out);
  nand nand_340 (nand_340_out, nand_339_out, nand_338_out);
  nand nand_341 (nand_341_out, nand_331_out, nand_338_out);
  nand nand_342 (nand_342_out, nand_341_out, nand_338_out);
  nand nand_343 (nand_343_out, nand_332_out, nand_338_out);
  nand nand_344 (nand_344_out, nand_343_out, nand_338_out);
  nand nand_345 (nand_345_out, nand_333_out, nand_338_out);
  nand nand_346 (nand_346_out, nand_345_out, nand_338_out);
  nand nand_347 (nand_347_out, nand_334_out, nand_338_out);
  nand nand_348 (nand_348_out, nand_347_out, nand_338_out);
  nand nand_349 (nand_349_out, nand_335_out, nand_338_out);
  nand nand_350 (nand_350_out, nand_349_out, nand_338_out);
  nand nand_351 (nand_351_out, nand_336_out, nand_338_out);
  nand nand_352 (nand_352_out, nand_351_out, nand_338_out);
  nand nand_353 (nand_353_out, nand_337_out, nand_338_out);
  nand nand_354 (nand_354_out, nand_353_out, nand_338_out);
  nand nand_355 (nand_355_out, nand_339_out, nand_356_out);
  nand nand_356 (nand_356_out, nand_355_out, nand_340_out);
  nand nand_357 (nand_357_out, nand_341_out, nand_358_out);
  nand nand_358 (nand_358_out, nand_357_out, nand_342_out);
  nand nand_359 (nand_359_out, nand_343_out, nand_360_out);
  nand nand_360 (nand_360_out, nand_359_out, nand_344_out);
  nand nand_361 (nand_361_out, nand_345_out, nand_362_out);
  nand nand_362 (nand_362_out, nand_361_out, nand_346_out);
  nand nand_363 (nand_363_out, nand_347_out, nand_364_out);
  nand nand_364 (nand_364_out, nand_363_out, nand_348_out);
  nand nand_365 (nand_365_out, nand_349_out, nand_366_out);
  nand nand_366 (nand_366_out, nand_365_out, nand_350_out);
  nand nand_367 (nand_367_out, nand_351_out, nand_368_out);
  nand nand_368 (nand_368_out, nand_367_out, nand_352_out);
  nand nand_369 (nand_369_out, nand_353_out, nand_370_out);
  nand nand_370 (nand_370_out, nand_369_out, nand_354_out);
  nand nand_371 (nand_371_out, nand_355_out, CLK_2);
  nand nand_372 (nand_372_out, nand_371_out, CLK_2);
  nand nand_373 (nand_373_out, nand_357_out, CLK_2);
  nand nand_374 (nand_374_out, nand_373_out, CLK_2);
  nand nand_375 (nand_375_out, nand_359_out, CLK_2);
  nand nand_376 (nand_376_out, nand_375_out, CLK_2);
  nand nand_377 (nand_377_out, nand_361_out, CLK_2);
  nand nand_378 (nand_378_out, nand_377_out, CLK_2);
  nand nand_379 (nand_379_out, nand_363_out, CLK_2);
  nand nand_380 (nand_380_out, nand_379_out, CLK_2);
  nand nand_381 (nand_381_out, nand_365_out, CLK_2);
  nand nand_382 (nand_382_out, nand_381_out, CLK_2);
  nand nand_383 (nand_383_out, nand_367_out, CLK_2);
  nand nand_384 (nand_384_out, nand_383_out, CLK_2);
  nand nand_385 (nand_385_out, nand_369_out, CLK_2);
  nand nand_386 (nand_386_out, nand_385_out, CLK_2);
  nand nand_387 (A7, nand_371_out, nand_388_out);
  nand nand_388 (nand_388_out, A7, nand_372_out);
  nand nand_389 (A6, nand_373_out, nand_390_out);
  nand nand_390 (nand_390_out, A6, nand_374_out);
  nand nand_391 (A5, nand_375_out, nand_392_out);
  nand nand_392 (nand_392_out, A5, nand_376_out);
  nand nand_393 (A4, nand_377_out, nand_394_out);
  nand nand_394 (nand_394_out, A4, nand_378_out);
  nand nand_395 (A3, nand_379_out, nand_396_out);
  nand nand_396 (nand_396_out, A3, nand_380_out);
  nand nand_397 (A2, nand_381_out, nand_398_out);
  nand nand_398 (nand_398_out, A2, nand_382_out);
  nand nand_399 (A1, nand_383_out, nand_400_out);
  nand nand_400 (nand_400_out, A1, nand_384_out);
  nand nand_401 (A0, nand_385_out, nand_402_out);
  nand nand_402 (nand_402_out, A0, nand_386_out);
  nand nand_403 (nand_403_out, in_57, S0);
  nand nand_404 (nand_404_out, in_53, S1);
  nand nand_405 (nand_405_out, in_56, S0);
  nand nand_406 (nand_406_out, in_52, S1);
  nand nand_407 (nand_407_out, in_55, S0);
  nand nand_408 (nand_408_out, in_51, S1);
  nand nand_409 (nand_409_out, in_54, S0);
  nand nand_410 (nand_410_out, in_50, S1);
  nand nand_411 (nand_411_out, in_58, S0);
  nand nand_412 (nand_412_out, in_49, S1);
  nand nand_413 (nand_413_out, in_59, S0);
  nand nand_414 (nand_414_out, in_48, S1);
  nand nand_415 (nand_415_out, in_60, S0);
  nand nand_416 (nand_416_out, in_47, S1);
  nand nand_417 (nand_417_out, in_61, S0);
  nand nand_418 (nand_418_out, in_46, S1);
  nand nand_419 (out_62, nand_403_out, nand_404_out);
  nand nand_420 (out_63, nand_405_out, nand_406_out);
  nand nand_421 (out_64, nand_407_out, nand_408_out);
  nand nand_422 (out_65, nand_409_out, nand_410_out);
  nand nand_423 (out_66, nand_411_out, nand_412_out);
  nand nand_424 (out_67, nand_413_out, nand_414_out);
  nand nand_425 (out_68, nand_415_out, nand_416_out);
  nand nand_426 (out_69, nand_417_out, nand_418_out);
  nand nand_427 (nand_427_out, A23, in_91);
  nand nand_428 (nand_428_out, in_89, in_90);
  nand nand_429 (nand_429_out, A22, in_91);
  nand nand_430 (nand_430_out, in_88, in_90);
  nand nand_431 (nand_431_out, A21, in_91);
  nand nand_432 (nand_432_out, in_87, in_90);
  nand nand_433 (nand_433_out, A20, in_91);
  nand nand_434 (nand_434_out, in_86, in_90);
  nand nand_435 (nand_435_out, A19, in_91);
  nand nand_436 (nand_436_out, in_85, in_90);
  nand nand_437 (nand_437_out, A18, in_91);
  nand nand_438 (nand_438_out, in_84, in_90);
  nand nand_439 (nand_439_out, A17, in_91);
  nand nand_440 (nand_440_out, in_83, in_90);
  nand nand_441 (nand_441_out, A16, in_91);
  nand nand_442 (nand_442_out, in_82, in_90);
  nand nand_443 (nand_443_out, nand_427_out, nand_428_out);
  nand nand_444 (nand_444_out, nand_429_out, nand_430_out);
  nand nand_445 (nand_445_out, nand_431_out, nand_432_out);
  nand nand_446 (nand_446_out, nand_433_out, nand_434_out);
  nand nand_447 (nand_447_out, nand_435_out, nand_436_out);
  nand nand_448 (nand_448_out, nand_437_out, nand_438_out);
  nand nand_449 (nand_449_out, nand_439_out, nand_440_out);
  nand nand_450 (nand_450_out, nand_441_out, nand_442_out);
  nand nand_451 (nand_451_out, CK, CK);
  nand nand_452 (nand_452_out, nand_443_out, nand_451_out);
  nand nand_453 (nand_453_out, nand_452_out, nand_451_out);
  nand nand_454 (nand_454_out, nand_444_out, nand_451_out);
  nand nand_455 (nand_455_out, nand_454_out, nand_451_out);
  nand nand_456 (nand_456_out, nand_445_out, nand_451_out);
  nand nand_457 (nand_457_out, nand_456_out, nand_451_out);
  nand nand_458 (nand_458_out, nand_446_out, nand_451_out);
  nand nand_459 (nand_459_out, nand_458_out, nand_451_out);
  nand nand_460 (nand_460_out, nand_447_out, nand_451_out);
  nand nand_461 (nand_461_out, nand_460_out, nand_451_out);
  nand nand_462 (nand_462_out, nand_448_out, nand_451_out);
  nand nand_463 (nand_463_out, nand_462_out, nand_451_out);
  nand nand_464 (nand_464_out, nand_449_out, nand_451_out);
  nand nand_465 (nand_465_out, nand_464_out, nand_451_out);
  nand nand_466 (nand_466_out, nand_450_out, nand_451_out);
  nand nand_467 (nand_467_out, nand_466_out, nand_451_out);
  nand nand_468 (nand_468_out, nand_452_out, nand_469_out);
  nand nand_469 (nand_469_out, nand_468_out, nand_453_out);
  nand nand_470 (nand_470_out, nand_454_out, nand_471_out);
  nand nand_471 (nand_471_out, nand_470_out, nand_455_out);
  nand nand_472 (nand_472_out, nand_456_out, nand_473_out);
  nand nand_473 (nand_473_out, nand_472_out, nand_457_out);
  nand nand_474 (nand_474_out, nand_458_out, nand_475_out);
  nand nand_475 (nand_475_out, nand_474_out, nand_459_out);
  nand nand_476 (nand_476_out, nand_460_out, nand_477_out);
  nand nand_477 (nand_477_out, nand_476_out, nand_461_out);
  nand nand_478 (nand_478_out, nand_462_out, nand_479_out);
  nand nand_479 (nand_479_out, nand_478_out, nand_463_out);
  nand nand_480 (nand_480_out, nand_464_out, nand_481_out);
  nand nand_481 (nand_481_out, nand_480_out, nand_465_out);
  nand nand_482 (nand_482_out, nand_466_out, nand_483_out);
  nand nand_483 (nand_483_out, nand_482_out, nand_467_out);
  nand nand_484 (nand_484_out, nand_468_out, CK);
  nand nand_485 (nand_485_out, nand_484_out, CK);
  nand nand_486 (nand_486_out, nand_470_out, CK);
  nand nand_487 (nand_487_out, nand_486_out, CK);
  nand nand_488 (nand_488_out, nand_472_out, CK);
  nand nand_489 (nand_489_out, nand_488_out, CK);
  nand nand_490 (nand_490_out, nand_474_out, CK);
  nand nand_491 (nand_491_out, nand_490_out, CK);
  nand nand_492 (nand_492_out, nand_476_out, CK);
  nand nand_493 (nand_493_out, nand_492_out, CK);
  nand nand_494 (nand_494_out, nand_478_out, CK);
  nand nand_495 (nand_495_out, nand_494_out, CK);
  nand nand_496 (nand_496_out, nand_480_out, CK);
  nand nand_497 (nand_497_out, nand_496_out, CK);
  nand nand_498 (nand_498_out, nand_482_out, CK);
  nand nand_499 (nand_499_out, nand_498_out, CK);
  nand nand_500 (A23, nand_484_out, nand_501_out);
  nand nand_501 (nand_501_out, A23, nand_485_out);
  nand nand_502 (A22, nand_486_out, nand_503_out);
  nand nand_503 (nand_503_out, A22, nand_487_out);
  nand nand_504 (A21, nand_488_out, nand_505_out);
  nand nand_505 (nand_505_out, A21, nand_489_out);
  nand nand_506 (A20, nand_490_out, nand_507_out);
  nand nand_507 (nand_507_out, A20, nand_491_out);
  nand nand_508 (A19, nand_492_out, nand_509_out);
  nand nand_509 (nand_509_out, A19, nand_493_out);
  nand nand_510 (A18, nand_494_out, nand_511_out);
  nand nand_511 (nand_511_out, A18, nand_495_out);
  nand nand_512 (A17, nand_496_out, nand_513_out);
  nand nand_513 (nand_513_out, A17, nand_497_out);
  nand nand_514 (A16, nand_498_out, nand_515_out);
  nand nand_515 (nand_515_out, A16, nand_499_out);

  // Other names for the same wires on the sheet: AC0 = Q0; AC1 = Q1; AC2 = Q2; AC3 = Q3; AC4 = Q4; AC5 = Q5; AC6 = Q6;
  //   AC7 = Q7; AL = SC; HLDA = in_91; LDA = in_90

  // Notes on the sheet:
  //   CLK: Hz: 2147483647
  //   CLK_2: Hz: 2147483647
  //   ALU
  //   ACC
  //   BUS
  //   INC/DEC Index Register
  //   32 NAND gates per bitslice (8 x 74xx00)
  //   Accumulator made from gated D-type latches
  //   Invert Accumulator
  //   ADDRESS
  //   8-bit presettable counter
  //   16 Gates per bit (4 x 74xx00)
  //   Master Slave arrangement using gated D-type latches
  //   8-bit Register
endmodule
