// Digital circuit NOR_full_adder.dig as structural Verilog
module NOR_full_adder (
  input  A,
  input  B,
  input  Cin,
  input  nCen,
  input  AND,
  input  XOR,
  input  A_2,
  input  B_2,
  input  Cin_2,
  input  nCen_2,
  input  XOR_2,
  input  AND_2,
  input  A_3,
  input  B_3,
  input  Cin_3,
  input  nCen_3,
  input  XOR_3,
  input  AND_3,
  output S,
  output C,
  output S_2,
  output C_2,
  output Sum,
  output Cout
);

  wire nand_1_out, nand_2_out, nand_3_out, nand_4_out, nand_5_out, nand_6_out, nand_7_out, nand_9_out,
       nand_10_out, nand_11_out, nand_12_out, nand_13_out, nand_14_out, nand_15_out, nand_16_out,
       nand_17_out, nand_18_out, nor_1_out, nor_2_out, nor_3_out, nor_4_out, nor_5_out, nor_6_out, nor_7_out,
       nor_9_out, nor_10_out, nor_11_out, xor_1_out;

  nor nor_1 (nor_1_out, A, B);
  nand nand_1 (nand_1_out, A_2, B_2);
  xor xor_1 (xor_1_out, A_3, B_3);
  nand nand_2 (nand_2_out, A_3, B_3);
  nor nor_2 (nor_2_out, A, nor_1_out);
  nor nor_3 (nor_3_out, nor_1_out, B);
  nand nand_3 (nand_3_out, A_2, nand_1_out);
  nand nand_4 (nand_4_out, nand_1_out, B_2);
  xor u_xor_2 (Sum, xor_1_out, Cin_3);
  nand nand_5 (nand_5_out, xor_1_out, Cin_3);
  nor nor_4 (nor_4_out, nor_2_out, nor_3_out);
  nand nand_6 (nand_6_out, nand_3_out, nand_4_out);
  nand nand_7 (nand_7_out, Sum, XOR_3);
  nand nand_8 (Cout, nand_5_out, nand_2_out);
  nor nor_5 (nor_5_out, nor_4_out, Cin);
  nand nand_9 (nand_9_out, nand_6_out, Cin_2);
  nand nand_10 (nand_10_out, Cout, AND_3);
  nor nor_6 (nor_6_out, nor_4_out, nor_5_out);
  nor nor_7 (nor_7_out, nor_5_out, Cin);
  nor nor_8 (C, nor_5_out, nCen, nor_1_out);
  nand nand_11 (nand_11_out, nand_6_out, nand_9_out);
  nand nand_12 (nand_12_out, nand_9_out, Cin_2);
  nand nand_13 (nand_13_out, nand_9_out, nand_1_out);
  nor nor_9 (nor_9_out, nor_6_out, nor_7_out);
  nand nand_14 (nand_14_out, nand_11_out, nand_12_out);
  nand nand_15 (nand_15_out, nand_7_out, nand_10_out);
  nor nor_10 (nor_10_out, nor_9_out, AND);
  nor nor_11 (nor_11_out, XOR, C);
  nand nand_16 (nand_16_out, nand_14_out, XOR_2);
  nand nand_17 (nand_17_out, AND_2, nand_13_out);
  nand nand_18 (nand_18_out, nand_13_out, nCen_2);
  nor nor_12 (S, nor_10_out, nor_11_out);
  nand nand_19 (S_2, nand_16_out, nand_17_out);
  nand nand_20 (C_2, nand_18_out, nand_18_out);
endmodule
