// Digital circuit Q3 Q4 Clock Gating.dig as structural Verilog
module Q3_Q4_Clock_Gating (
  input  CLK,
  input  Q3,
  input  Q4,
  output GCLK,
  output nRST
);

  wire not_1_out, or_1_out;

  or or_1 (or_1_out, Q3, Q4);
  nand nand_1 (nRST, Q3, Q4);
  not not_1 (not_1_out, CLK);
  nand nand_2 (GCLK, not_1_out, or_1_out);
  LED led_1 (.in(GCLK));

  // Notes on the sheet:
  //   Note Clock Inverted
endmodule
