// Digital circuit RAM_7.dig as structural Verilog
module RAM_7 (
  input  nRES_COUNT,
  input  JMP,
  input  clk,
  input  READ,
  input  in_5,
  input  WRITE,
  output nLOAD,
  output GCLK,
  output nRCLK,
  output A_nD
);

  wire AD0, AD1, AD2, AD3, AD4, AD5, AD6, AD7, AD8, AD9, AD10, AD11, AD12, AD13, AD14, AD15, AD_Cin,
       Address_in, Address_out, ADin, ADout, Bout, BUS0, BUS1, BUS2, BUS3, BUS4, BUS5, BUS6, BUS7, BUS8,
       BUS9, BUS10, BUS11, BUS12, BUS13, BUS14, BUS15, button_1_out, button_2_out, button_3_out,
       button_4_out, button_5_out, button_6_out, button_7_out, button_8_out, button_9_out, button_10_out,
       button_11_out, button_12_out, button_13_out, button_14_out, button_15_out, button_16_out,
       button_17_out, D0, D1, D2, D3, D4, D5, D6, D7, D8, D9, D10, D11, D12, D13, D14, D15, d_ff_1_nq,
       d_ff_2_nq, d_ff_3_nq, d_ff_4_nq, d_ff_5_nq, d_ff_6_nq, d_ff_7_nq, d_ff_8_nq, d_ff_9_nq, d_ff_10_nq,
       d_ff_11_nq, d_ff_12_nq, Data_in, Data_out, IC16_2_nq, IC16_nq, IC17_2_nq, IC17_nq, LD, n2SD,
       nand_1_out, nand_2_out, nand_3_out, nand_6_out, nand_7_out, nand_9_out, nand_10_out, nand_11_out,
       nand_12_out, nand_13_out, nCLR, nR, nRES, R, RCO, RESET_2_out, RST, Sel_Ad, SETC, Sout, TC, U3_pin9,
       U5_pin9, U8_2_pin9, U17_pin9, U23_pin9, U24_pin9, xor_1_out, xor_2_out, xor_3_out, xor_4_out;
  wire [3:0] U7_pin11, U8_2_pin3, U8_2_pin7, U8_pin11, U9_pin3, U9_pin7, U24_pin3, U24_pin7, U25_pin3,
       U25_pin7;

  Seven_Seg_Hex seven_seg_hex_1 (.d({AD15, AD14, AD13, AD12}), .dp(1'b0));
  _74165 U3 (
    .pin1(nLOAD), .pin2(GCLK), .pin3(BUS11), .pin4(BUS10), .pin5(BUS9), .pin6(BUS8), .pin8(1'b0),
    .pin9(U3_pin9), .pin10(1'b0), .pin11(BUS15), .pin12(BUS14), .pin13(BUS13), .pin14(BUS12), .pin15(1'b0),
    .pin16(1'b1));  // open: pin7
  _74165 U4 (
    .pin1(nLOAD), .pin2(GCLK), .pin3(BUS3), .pin4(BUS2), .pin5(BUS1), .pin6(BUS0), .pin8(1'b0), .pin9(Bout),
    .pin10(U3_pin9), .pin11(BUS7), .pin12(BUS6), .pin13(BUS5), .pin14(BUS4), .pin15(1'b0), .pin16(1'b1));  // open: pin7
  Seven_Seg_Hex seven_seg_hex_2 (.d({AD11, AD10, AD9, AD8}), .dp(1'b0));
  Seven_Seg_Hex seven_seg_hex_3 (.d({AD7, AD6, AD5, AD4}), .dp(1'b0));
  Seven_Seg_Hex seven_seg_hex_4 (.d({AD3, AD2, AD1, AD0}), .dp(1'b0));
  nand nand_1 (nand_1_out, ADout, AD_Cin);
  xor xor_1 (xor_1_out, ADout, AD_Cin);
  xor xor_2 (xor_2_out, JMP, 1'b1);
  _74595 U17 (
    .pin1(BUS14), .pin2(BUS13), .pin3(BUS12), .pin4(BUS11), .pin5(BUS10), .pin6(BUS9), .pin7(BUS8),
    .pin8(1'b0), .pin9(U17_pin9), .pin10(nCLR), .pin11(GCLK), .pin12(nR), .pin13(WRITE), .pin14(Sout),
    .pin15(BUS15), .pin16(1'b1));
  _74595 U16 (
    .pin1(BUS6), .pin2(BUS5), .pin3(BUS4), .pin4(BUS3), .pin5(BUS2), .pin6(BUS1), .pin7(BUS0), .pin8(1'b0),
    .pin10(nCLR), .pin11(GCLK), .pin12(nR), .pin13(WRITE), .pin14(U17_pin9), .pin15(BUS7), .pin16(1'b1));  // open: pin9
  xor xor_3 (xor_3_out, nand_1_out, 1'b1);
  xor xor_4 (xor_4_out, nRES_COUNT, xor_2_out);
  nand nand_2 (nand_2_out, xor_1_out, xor_4_out);
  nand nand_3 (nand_3_out, xor_2_out, Bout);
  Seven_Seg_Hex seven_seg_hex_5 (.d({BUS15, BUS14, BUS13, BUS12}), .dp(1'b0));
  Seven_Seg_Hex seven_seg_hex_6 (.d({BUS11, BUS10, BUS9, BUS8}), .dp(1'b0));
  nand nand_4 (ADin, nand_2_out, nand_3_out);
  Seven_Seg_Hex seven_seg_hex_7 (.d({BUS7, BUS6, BUS5, BUS4}), .dp(1'b0));
  Seven_Seg_Hex seven_seg_hex_8 (.d({BUS3, BUS2, BUS1, BUS0}), .dp(1'b0));
  _74595 U23 (
    .pin1(AD14), .pin2(AD13), .pin3(AD12), .pin4(AD11), .pin5(AD10), .pin6(AD9), .pin7(AD8), .pin8(1'b0),
    .pin9(U23_pin9), .pin10(nCLR), .pin11(GCLK), .pin12(nR), .pin13(1'b0), .pin14(ADin), .pin15(AD15),
    .pin16(1'b1));
  _74595 U22 (
    .pin1(AD6), .pin2(AD5), .pin3(AD4), .pin4(AD3), .pin5(AD2), .pin6(AD1), .pin7(AD0), .pin8(1'b0),
    .pin9(ADout), .pin10(nCLR), .pin11(GCLK), .pin12(nR), .pin13(1'b0), .pin14(U23_pin9), .pin15(AD7),
    .pin16(1'b1));
  _7474 U29 (
    .pin1(1'b1), .pin2(xor_3_out), .pin3(GCLK), .pin4(nLOAD), .pin5(AD_Cin), .pin7(1'b0), .pin8(nR),
    .pin9(R), .pin10(n2SD), .pin11(clk), .pin12(RCO), .pin13(1'b1), .pin14(1'b1));  // open: pin6
  // _62256 U20: pin names not known; wires that end beside it: AD14, AD12, AD7, AD6, AD5, AD4, AD3, AD2, AD1, AD0, BUS8, BUS9, 1'b1, WRITE, AD13, AD8, AD9, AD11, READ, AD10, in_5, BUS15
  // _62256 U21: pin names not known; wires that end beside it: BUS10, 1'b0, AD14, AD12, AD7, AD6, AD5, AD4, AD3, AD2, AD1, AD0, BUS0, BUS1, BUS2, 1'b0, 1'b1, WRITE, AD13, AD8, AD9, AD11, READ, AD10, in_5, BUS7
  LED led_1 (.in(D15));
  Reset reset_1 (.out(n2SD));
  LED led_2 (.in(D14));
  D_FF IC17 (.D(IC17_nq), .C(button_1_out), .Q(D15), .nQ(IC17_nq));
  Button button_1 (.out(button_1_out));
  nand nand_5 (RST, nRES, nand_6_out);
  nand nand_6 (nand_6_out, RST, nR);
  nand nand_7 (nand_7_out, clk, clk);
  _74165 U5 (
    .pin1(nLOAD), .pin2(GCLK), .pin3(D11), .pin4(D10), .pin5(D9), .pin6(D8), .pin8(1'b0), .pin9(U5_pin9),
    .pin10(1'b0), .pin11(D15), .pin12(D14), .pin13(D13), .pin14(D12), .pin15(1'b0), .pin16(1'b1));  // open: pin7
  LED led_3 (.in(D13));
  D_FF d_ff_1 (.D(d_ff_1_nq), .C(button_2_out), .Q(D14), .nQ(d_ff_1_nq));
  Button button_2 (.out(button_2_out));
  LED led_4 (.in(D12));
  D_FF d_ff_2 (.D(d_ff_2_nq), .C(button_3_out), .Q(D13), .nQ(d_ff_2_nq));
  Button button_3 (.out(button_3_out));
  nand nand_8 (GCLK, RST, nand_7_out);
  LED led_5 (.in(D11));
  D_FF d_ff_3 (.D(d_ff_3_nq), .C(button_4_out), .Q(D12), .nQ(d_ff_3_nq));
  Button button_4 (.out(button_4_out));
  LED led_6 (.in(D10));
  D_FF d_ff_4 (.D(d_ff_4_nq), .C(button_5_out), .Q(D11), .nQ(d_ff_4_nq));
  Button button_5 (.out(button_5_out));
  LED led_7 (.in(D9));
  D_FF d_ff_5 (.D(d_ff_5_nq), .C(button_6_out), .Q(D10), .nQ(d_ff_5_nq));
  Button button_6 (.out(button_6_out));
  _74165 U6 (
    .pin1(nLOAD), .pin2(GCLK), .pin3(D3), .pin4(D2), .pin5(D1), .pin6(D0), .pin8(1'b0), .pin9(Sout),
    .pin10(U5_pin9), .pin11(D7), .pin12(D6), .pin13(D5), .pin14(D4), .pin15(1'b0), .pin16(1'b1));  // open: pin7
  LED led_8 (.in(D8));
  D_FF d_ff_6 (.D(d_ff_6_nq), .C(button_7_out), .Q(D9), .nQ(d_ff_6_nq));
  Button button_7 (.out(button_7_out));
  _74161 U7 (
    .pin1(RST), .pin2(clk), .pin3(1'b0), .pin4(1'b0), .pin5(1'b0), .pin6(1'b0), .pin7(1'b1), .pin8(1'b0),
    .pin9(1'b1), .pin10(1'b1), .pin11(U7_pin11[3]), .pin12(U7_pin11[2]), .pin13(U7_pin11[1]),
    .pin14(U7_pin11[0]), .pin15(RCO), .pin16(1'b1));
  D_FF IC17_2 (.D(IC17_2_nq), .C(button_8_out), .Q(D8), .nQ(IC17_2_nq));
  Button button_8 (.out(button_8_out));
  Seven_Seg_Hex seven_seg_hex_9 (.d({D15, D14, D13, D12}), .dp(1'b0));
  Seven_Seg_Hex seven_seg_hex_10 (.d({D11, D10, D9, D8}), .dp(1'b0));
  LED led_9 (.in(D7));
  D_FF IC16 (.D(IC16_nq), .C(button_9_out), .Q(D7), .nQ(IC16_nq));
  Seven_Seg_Hex seven_seg_hex_11 (.d(U7_pin11), .dp(1'b0));
  LED led_10 (.in(D6));
  D_FF d_ff_7 (.D(d_ff_7_nq), .C(button_10_out), .Q(D6), .nQ(d_ff_7_nq));
  Button button_9 (.out(button_9_out));
  LED led_11 (.in(D5));
  D_FF d_ff_8 (.D(d_ff_8_nq), .C(button_11_out), .Q(D5), .nQ(d_ff_8_nq));
  Button button_10 (.out(button_10_out));
  LED led_12 (.in(D4));
  D_FF d_ff_9 (.D(d_ff_9_nq), .C(button_12_out), .Q(D4), .nQ(d_ff_9_nq));
  Button button_11 (.out(button_11_out));
  LED led_13 (.in(D3));
  D_FF d_ff_10 (.D(d_ff_10_nq), .C(button_14_out), .Q(D3), .nQ(d_ff_10_nq));
  Button button_12 (.out(button_12_out));
  Monoflop monoflop_1 (.C(nLOAD), .R(1'b0), .Q(SETC), .nQ(nRES));
  Monoflop monoflop_2 (.C(button_13_out), .R(1'b0), .Q(LD), .nQ(nLOAD));
  Button button_13 (.out(button_13_out));
  LED led_14 (.in(D2));
  D_FF d_ff_11 (.D(d_ff_11_nq), .C(button_15_out), .Q(D2), .nQ(d_ff_11_nq));
  Button button_14 (.out(button_14_out));
  LED led_15 (.in(D1));
  D_FF d_ff_12 (.D(d_ff_12_nq), .C(button_16_out), .Q(D1), .nQ(d_ff_12_nq));
  Button button_15 (.out(button_15_out));
  Monoflop monoflop_3 (.C(RESET_2_out), .R(1'b0), .nQ(nCLR));  // open: Q
  Button RESET_2 (.out(RESET_2_out));
  LED led_16 (.in(D0));
  D_FF IC16_2 (.D(IC16_2_nq), .C(button_17_out), .Q(D0), .nQ(IC16_2_nq));
  Button button_16 (.out(button_16_out));
  Seven_Seg_Hex seven_seg_hex_12 (.d({D7, D6, D5, D4}), .dp(1'b0));
  Button button_17 (.out(button_17_out));
  Seven_Seg_Hex seven_seg_hex_13 (.d({D3, D2, D1, D0}), .dp(1'b0));
  nand nand_9 (nand_9_out, GCLK, GCLK);
  _74161 U8 (
    .pin1(nLOAD), .pin2(nand_9_out), .pin3(1'b0), .pin4(1'b0), .pin5(1'b0), .pin6(1'b0), .pin7(1'b1),
    .pin8(1'b0), .pin9(1'b1), .pin10(1'b1), .pin11(U8_pin11[3]), .pin12(U8_pin11[2]), .pin13(U8_pin11[1]),
    .pin14(U8_pin11[0]), .pin15(TC), .pin16(1'b1));
  _7474 U30 (
    .pin1(1'b1), .pin2(1'b1), .pin3(1'b1), .pin4(1'b1), .pin7(1'b0), .pin8(nRCLK), .pin10(1'b1),
    .pin11(GCLK), .pin12(TC), .pin13(1'b1), .pin14(1'b1));  // open: pin5, pin6, pin9
  D_FF d_ff_13 (.D(Sel_Ad), .C(nRCLK), .Q(A_nD), .nQ(Sel_Ad));
  nand nand_10 (nand_10_out, Sout, Sel_Ad);
  nand nand_11 (nand_11_out, A_nD, Address_out);
  nand nand_12 (nand_12_out, Sout, A_nD);
  nand nand_13 (nand_13_out, Sel_Ad, Data_out);
  nand nand_14 (Address_in, nand_10_out, nand_11_out);
  nand nand_15 (Data_in, nand_12_out, nand_13_out);
  Seven_Seg_Hex seven_seg_hex_14 (.d(U8_pin11), .dp(1'b0));
  _74595 U8_2 (
    .pin1(U8_2_pin3[2]), .pin2(U8_2_pin3[1]), .pin3(U8_2_pin3[0]), .pin4(U8_2_pin7[3]), .pin5(U8_2_pin7[2]),
    .pin6(U8_2_pin7[1]), .pin7(U8_2_pin7[0]), .pin8(1'b0), .pin9(U8_2_pin9), .pin10(1'b1), .pin11(GCLK),
    .pin12(nRCLK), .pin13(1'b0), .pin14(Data_in), .pin15(U8_2_pin3[3]), .pin16(1'b1));
  _74595 U24 (
    .pin1(U24_pin3[2]), .pin2(U24_pin3[1]), .pin3(U24_pin3[0]), .pin4(U24_pin7[3]), .pin5(U24_pin7[2]),
    .pin6(U24_pin7[1]), .pin7(U24_pin7[0]), .pin8(1'b0), .pin9(U24_pin9), .pin10(1'b1), .pin11(GCLK),
    .pin12(nRCLK), .pin13(1'b0), .pin14(Address_in), .pin15(U24_pin3[3]), .pin16(1'b1));
  _74595 U9 (
    .pin1(U9_pin3[2]), .pin2(U9_pin3[1]), .pin3(U9_pin3[0]), .pin4(U9_pin7[3]), .pin5(U9_pin7[2]),
    .pin6(U9_pin7[1]), .pin7(U9_pin7[0]), .pin8(1'b0), .pin9(Data_out), .pin10(1'b1), .pin11(GCLK),
    .pin12(nRCLK), .pin13(1'b0), .pin14(U8_2_pin9), .pin15(U9_pin3[3]), .pin16(1'b1));
  _74595 U25 (
    .pin1(U25_pin3[2]), .pin2(U25_pin3[1]), .pin3(U25_pin3[0]), .pin4(U25_pin7[3]), .pin5(U25_pin7[2]),
    .pin6(U25_pin7[1]), .pin7(U25_pin7[0]), .pin8(1'b0), .pin9(Address_out), .pin10(1'b1), .pin11(GCLK),
    .pin12(nRCLK), .pin13(1'b0), .pin14(U24_pin9), .pin15(U25_pin3[3]), .pin16(1'b1));
  Seven_Seg_Hex seven_seg_hex_15 (.d(U8_2_pin3), .dp(1'b0));
  Seven_Seg_Hex seven_seg_hex_16 (.d(U24_pin3), .dp(1'b0));
  Seven_Seg_Hex seven_seg_hex_17 (.d(U8_2_pin7), .dp(1'b0));
  Seven_Seg_Hex seven_seg_hex_18 (.d(U24_pin7), .dp(1'b0));
  Seven_Seg_Hex seven_seg_hex_19 (.d(U9_pin3), .dp(1'b0));
  Seven_Seg_Hex seven_seg_hex_20 (.d(U25_pin3), .dp(1'b0));
  Seven_Seg_Hex seven_seg_hex_21 (.d(U9_pin7), .dp(1'b0));
  Seven_Seg_Hex seven_seg_hex_22 (.d(U25_pin7), .dp(1'b0));

  // Other names for the same wires on the sheet: nCE = in_5; nLD = nLOAD; nOE = READ; T0 = nR; nRRES = nCLR;
  //   nWE = WRITE; Sel_Dat = A_nD

  // Notes on the sheet:
  //   nRES_COUNT: default 1
  //   JMP: default 1
  //   clk: Hz: 4
  //   READ: default 1
  //   in_5: default 1
  //   RAM Registers & RAM (11 ICs)
  //   RAM ADDRESS
  //   Bus Read Register B
  //   U28A
  //   U27A
  //   U27D
  //   U27C
  //   U27B
  //   U28C
  //   U28B
  //   Carry is only set before Bit 0 of an operation
  //   BUS DATA
  //   BUS Write Register
  //   U28D
  //   S1     S0       MODE
  //   0          0       HOLD
  //   0          1       RIGHT
  //   1          0       LEFT
  //   1          1       LOAD
  //   Address Counter
  //   RAM HI
  //   RAM LO
  //   Input & Clock
  //   Single Step
  //   ENTER H
  //   Data Input
  //   Clock Sequencer
  //   # Clock
  //   ENTER L
  //   Slave Sequencer
  //   Output Display Registers
  //   ADDRESS REGISTER
  //   WRITE REGISTER
endmodule
