// Digital circuit ROM_RAM_REGS_CLK.dig as structural Verilog
module ROM_RAM_REGS_CLK (
  input  nRES_COUNT,
  input  JMP,
  input  in_3,
  input  in_4,
  input  in_5,
  input  in_6,
  input  in_7,
  input  in_8,
  input  clk,
  output GCLK,
  output P2,
  output P1,
  output P3,
  output P4
);

  wire A0, A1, A2, A3, A4, A5, A6, A7, A8, A9, A10, A11, A12, A13, A14, A15, AC0, AC1, AC2, AC3, AC4, AC5,
       AC6, AC7, AC8, AC9, AC10, AC11, AC12, AC13, AC14, AC15, AD0, AD1, AD2, AD3, AD4, AD5, AD6, AD7, AD8,
       AD9, AD10, AD11, AD12, AD13, AD14, AD15, ADin, ADout, Bout, BUS0, BUS1, BUS2, BUS3, BUS4, BUS5, BUS6,
       BUS7, BUS8, BUS9, BUS10, BUS11, BUS12, BUS13, BUS14, BUS15, GATE, HOLD, LD, MR, n2SD, nand_1_out,
       nand_2_out, nand_3_out, nand_8_out, nCLR, nGATE, nHOLD, not_1_out, nR, nSET, PC_Cin, PCin, PCout,
       pulldown_1_out, R, R0, R1, R2, R3, R4, R5, R6, R7, R8, R9, R10, R11, R12, R13, R14, R15, RCO,
       RESET_2_out, SETC, T2, T3, T4, T6, T7, T8, T9, U3_pin9, U17_pin18, U19_pin14, U23_pin9, U25_pin9,
       xor_2_out, xor_3_out, xor_4_out, xor_5_out;
  wire [3:0] U17_2_pin11;

  // XOr xor_1 has open pins: In_1=pulldown_1_out, In_2=1'b1, out=open
  PullDown pulldown_1 (.out(pulldown_1_out));
  DiodeForward diodeforward_1 (.in(AC0), .out(pulldown_1_out));
  DiodeForward diodeforward_2 (.in(AC1), .out(pulldown_1_out));
  DiodeForward diodeforward_3 (.in(AC2), .out(pulldown_1_out));
  DiodeForward diodeforward_4 (.in(AC3), .out(pulldown_1_out));
  DiodeForward diodeforward_5 (.in(AC4), .out(pulldown_1_out));
  DiodeForward diodeforward_6 (.in(AC5), .out(pulldown_1_out));
  DiodeForward diodeforward_7 (.in(AC6), .out(pulldown_1_out));
  DiodeForward diodeforward_8 (.in(AC7), .out(pulldown_1_out));
  DiodeForward diodeforward_9 (.in(AC8), .out(pulldown_1_out));
  DiodeForward diodeforward_10 (.in(AC9), .out(pulldown_1_out));
  DiodeForward diodeforward_11 (.in(AC10), .out(pulldown_1_out));
  DiodeForward diodeforward_12 (.in(AC11), .out(pulldown_1_out));
  DiodeForward diodeforward_13 (.in(AC12), .out(pulldown_1_out));
  DiodeForward diodeforward_14 (.in(AC13), .out(pulldown_1_out));
  DiodeForward diodeforward_15 (.in(AC14), .out(pulldown_1_out));
  DiodeForward diodeforward_16 (.in(AC15), .out(pulldown_1_out));
  Seven_Seg_Hex seven_seg_hex_1 (.d({AD15, AD14, AD13, AD12}), .dp(1'b0));
  Seven_Seg_Hex seven_seg_hex_2 (.d({AD11, AD10, AD9, AD8}), .dp(1'b0));
  _74164 U5 (
    .pin1(1'b1), .pin2(ADin), .pin3(AC15), .pin4(AC14), .pin5(AC13), .pin6(AC12), .pin7(1'b0), .pin8(GCLK),
    .pin9(nCLR), .pin10(AC11), .pin11(AC10), .pin12(AC9), .pin13(AC8), .pin14(1'b1));
  Seven_Seg_Hex seven_seg_hex_3 (.d({AD7, AD6, AD5, AD4}), .dp(1'b0));
  Seven_Seg_Hex seven_seg_hex_4 (.d({AD3, AD2, AD1, AD0}), .dp(1'b0));
  _74595 U19 (
    .pin1(AD6), .pin2(AD5), .pin3(AD4), .pin4(AD3), .pin5(AD2), .pin6(AD1), .pin7(AD0), .pin8(1'b0),
    .pin9(ADout), .pin10(nCLR), .pin11(GCLK), .pin12(nR), .pin13(1'b0), .pin14(U19_pin14), .pin15(AD7),
    .pin16(1'b1));
  _74595 U18 (
    .pin1(AD14), .pin2(AD13), .pin3(AD12), .pin4(AD11), .pin5(AD10), .pin6(AD9), .pin7(AD8), .pin8(1'b0),
    .pin9(U19_pin14), .pin10(nCLR), .pin11(GCLK), .pin12(nR), .pin13(1'b0), .pin14(ADin), .pin15(AD15),
    .pin16(1'b1));
  Seven_Seg_Hex seven_seg_hex_5 (.d({BUS15, BUS14, BUS13, BUS12}), .dp(1'b0));
  _74165 U3 (
    .pin1(P1), .pin2(GCLK), .pin3(BUS11), .pin4(BUS10), .pin5(BUS9), .pin6(BUS8), .pin8(1'b0),
    .pin9(U3_pin9), .pin10(1'b0), .pin11(BUS15), .pin12(BUS14), .pin13(BUS13), .pin14(BUS12), .pin15(1'b0),
    .pin16(1'b1));  // open: pin7
  _74165 U4 (
    .pin1(P1), .pin2(GCLK), .pin3(BUS3), .pin4(BUS2), .pin5(BUS1), .pin6(BUS0), .pin8(1'b0), .pin9(Bout),
    .pin10(U3_pin9), .pin11(BUS7), .pin12(BUS6), .pin13(BUS5), .pin14(BUS4), .pin15(1'b0), .pin16(1'b1));  // open: pin7
  _74164 U6 (
    .pin1(1'b1), .pin2(AC8), .pin3(AC7), .pin4(AC6), .pin5(AC5), .pin6(AC4), .pin7(1'b0), .pin8(GCLK),
    .pin9(nCLR), .pin10(AC3), .pin11(AC2), .pin12(AC1), .pin13(AC0), .pin14(1'b1));
  Seven_Seg_Hex seven_seg_hex_6 (.d({BUS11, BUS10, BUS9, BUS8}), .dp(1'b0));
  Seven_Seg_Hex seven_seg_hex_7 (.d({BUS7, BUS6, BUS5, BUS4}), .dp(1'b0));
  Seven_Seg_Hex seven_seg_hex_8 (.d({BUS3, BUS2, BUS1, BUS0}), .dp(1'b0));
  Seven_Seg_Hex seven_seg_hex_9 (.d({AC15, AC14, AC13, AC12}), .dp(1'b0));
  Seven_Seg_Hex seven_seg_hex_10 (.d({AC11, AC10, AC9, AC8}), .dp(1'b0));
  _74299 U17 (
    .pin1(in_8), .pin2(GATE), .pin3(GATE), .pin4(BUS6), .pin5(BUS4), .pin6(BUS2), .pin7(BUS0), .pin9(1'b1),
    .pin10(1'b0), .pin11(1'b0), .pin12(GCLK), .pin13(BUS1), .pin14(BUS3), .pin15(BUS5), .pin16(BUS7),
    .pin18(U17_pin18), .pin19(in_7), .pin20(1'b1));  // open: pin8, pin17
  _74299 U16 (
    .pin1(in_8), .pin2(GATE), .pin3(GATE), .pin4(BUS14), .pin5(BUS12), .pin6(BUS10), .pin7(BUS8),
    .pin8(U17_pin18), .pin9(1'b1), .pin10(1'b0), .pin11(1'b0), .pin12(GCLK), .pin13(BUS9), .pin14(BUS11),
    .pin15(BUS13), .pin16(BUS15), .pin18(ADin), .pin19(in_7), .pin20(1'b1));  // open: pin17
  Seven_Seg_Hex seven_seg_hex_11 (.d({AC7, AC6, AC5, AC4}), .dp(1'b0));
  Seven_Seg_Hex seven_seg_hex_12 (.d({AC3, AC2, AC1, AC0}), .dp(1'b0));
  // _62256 U20: pin names not known; wires that end beside it: AD14, AD12, AD7, AD6, AD5, AD4, AD3, AD2, AD1, AD0, BUS8, BUS9, 1'b1, in_6, AD13, AD8, AD9, AD11, in_3, AD10, in_4, BUS15
  // _62256 U21: pin names not known; wires that end beside it: BUS10, 1'b0, AD14, AD12, AD7, AD6, AD5, AD4, AD3, AD2, AD1, AD0, BUS0, BUS1, BUS2, 1'b0, 1'b1, in_6, AD13, AD8, AD9, AD11, in_3, AD10, in_4, BUS7
  _74165 U25 (
    .pin1(P1), .pin2(GCLK), .pin3(R11), .pin4(R10), .pin5(R9), .pin6(R8), .pin8(1'b0), .pin9(U25_pin9),
    .pin10(1'b0), .pin11(R15), .pin12(R14), .pin13(R13), .pin14(R12), .pin15(1'b0), .pin16(1'b1));  // open: pin7
  _74165 U26 (
    .pin1(P1), .pin2(GCLK), .pin3(R3), .pin4(R2), .pin5(R1), .pin6(R0), .pin8(1'b0), .pin9(ADin),
    .pin10(U25_pin9), .pin11(R7), .pin12(R6), .pin13(R5), .pin14(R4), .pin15(1'b0), .pin16(1'b1));  // open: pin7
  Seven_Seg_Hex seven_seg_hex_13 (.d({A15, A14, A13, A12}), .dp(1'b0));
  Seven_Seg_Hex seven_seg_hex_14 (.d({A11, A10, A9, A8}), .dp(1'b0));
  Seven_Seg_Hex seven_seg_hex_15 (.d({A7, A6, A5, A4}), .dp(1'b0));
  nand nand_1 (nand_1_out, PCout, PC_Cin);
  xor xor_2 (xor_2_out, PCout, PC_Cin);
  xor xor_3 (xor_3_out, JMP, 1'b1);
  Seven_Seg_Hex seven_seg_hex_16 (.d({A3, A2, A1, A0}), .dp(1'b0));
  // _27C1024 U24: pin names not known; wires that end beside it: 1'b1, 1'b0, R15, R14, R13, R12, R11, R10, R9, R8, 1'b0, R7, R6, R5, R4, R3, 1'b1, A15, A14, A13, A12, A11, A10, A9
  xor xor_4 (xor_4_out, nand_1_out, 1'b1);
  xor xor_5 (xor_5_out, nRES_COUNT, xor_3_out);
  Seven_Seg_Hex seven_seg_hex_17 (.d({R15, R14, R13, R12}), .dp(1'b0));
  Seven_Seg_Hex seven_seg_hex_18 (.d({R11, R10, R9, R8}), .dp(1'b0));
  Seven_Seg_Hex seven_seg_hex_19 (.d({R7, R6, R5, R4}), .dp(1'b0));
  nand nand_2 (nand_2_out, xor_2_out, xor_5_out);
  nand nand_3 (nand_3_out, xor_3_out, ADin);
  Seven_Seg_Hex seven_seg_hex_20 (.d({R3, R2, R1, R0}), .dp(1'b0));
  nand nand_4 (PCin, nand_2_out, nand_3_out);
  _74595 U23 (
    .pin1(A14), .pin2(A13), .pin3(A12), .pin4(A11), .pin5(A10), .pin6(A9), .pin7(A8), .pin8(1'b0),
    .pin9(U23_pin9), .pin10(nCLR), .pin11(GCLK), .pin12(nR), .pin13(1'b0), .pin14(PCin), .pin15(A15),
    .pin16(1'b1));
  _74595 U22 (
    .pin1(A6), .pin2(A5), .pin3(A4), .pin4(A3), .pin5(A2), .pin6(A1), .pin7(A0), .pin8(1'b0), .pin9(PCout),
    .pin10(nCLR), .pin11(GCLK), .pin12(nR), .pin13(1'b0), .pin14(U23_pin9), .pin15(A7), .pin16(1'b1));
  _7474 U29 (
    .pin1(1'b1), .pin2(xor_4_out), .pin3(GCLK), .pin4(P1), .pin5(PC_Cin), .pin7(1'b0), .pin10(1'b1),
    .pin11(1'b1), .pin12(1'b1), .pin13(1'b1), .pin14(1'b1));  // open: pin6, pin8, pin9
  Reset reset_1 (.out(n2SD));
  not not_1 (not_1_out, MR);
  not not_2 (P4, T4);
  not not_3 (P3, T3);
  not not_4 (nSET, T2);
  not not_5 (P2, SETC);
  not not_6 (P1, LD);
  nand nand_5 (GATE, nSET, nGATE);
  nand nand_6 (nGATE, GATE, nR);
  nand nand_7 (GCLK, GATE, nand_8_out);
  nand nand_8 (nand_8_out, clk, clk);
  Monoflop monoflop_1 (.C(RESET_2_out), .R(1'b0), .nQ(nCLR));  // open: Q
  Button RESET_2 (.out(RESET_2_out));
  _7474 U30 (
    .pin1(1'b1), .pin2(RCO), .pin3(clk), .pin4(n2SD), .pin5(R), .pin6(nR), .pin7(1'b0), .pin10(1'b1),
    .pin11(1'b1), .pin12(1'b1), .pin13(1'b1), .pin14(1'b1));  // open: pin8, pin9
  nand nand_9 (HOLD, nGATE, nHOLD);
  nand nand_10 (nHOLD, HOLD, nR);
  _744017 U16_2 (
    .pin1(MR), .pin2(SETC), .pin3(LD), .pin4(T2), .pin5(T6), .pin6(T7), .pin7(T3), .pin8(1'b0), .pin9(T8),
    .pin10(T4), .pin11(T9), .pin13(HOLD), .pin14(clk), .pin15(MR), .pin16(1'b1));  // open: pin12
  _74161 U17_2 (
    .pin1(GATE), .pin2(clk), .pin3(1'b0), .pin4(1'b0), .pin5(1'b0), .pin6(1'b0), .pin7(1'b1), .pin8(1'b0),
    .pin9(1'b1), .pin10(1'b1), .pin11(U17_2_pin11[3]), .pin12(U17_2_pin11[2]), .pin13(U17_2_pin11[1]),
    .pin14(U17_2_pin11[0]), .pin15(RCO), .pin16(1'b1));
  Seven_Seg_Hex seven_seg_hex_21 (.d(U17_2_pin11), .dp(1'b0));

  // Other names for the same wires on the sheet: Aout = AC0; nAE = in_5; nAEN = GATE; nCE = in_4; nLD = P1;
  //   nOE = in_3; nRES = P2; nRRES = nCLR; nWE = in_6; Fout = ADin; Rout = ADin; T0 = LD; T1 = SETC; T5 = MR

  // Notes on the sheet:
  //   nRES_COUNT: default 1
  //   JMP: default 1
  //   in_3: default 1
  //   in_5: default 1
  //   in_6: default 1
  //   in_7: default 1
  //   clk: Hz: 1000
  //   Main Registers & RAM
  //   Zero Detect
  //   U27D
  //   RAM ADDRESS
  //   16 bit Accumulator A
  //   RAM Address Register
  //   BUS DATA
  //   S1     S0       MODE
  //   0          0       HOLD
  //   0          1       RIGHT
  //   1          0       LEFT
  //   1          1       LOAD
  //   Memory Read Register B
  //   ACCUMULATOR
  //   BUS I/O Register
  //   RAM HI
  //   RAM LO
  //   ROM & PC UNIT
  //   ROM Data Register
  //   ROM ADDRESS
  //   U28A
  //   U27A
  //   16-bit ROM
  //   U27C
  //   U27B
  //   ROM DATA
  //   Carry is only set before Bit 0 of an operation
  //   U28C
  //   U28B
  //   U28D
  //   PC Carry FF
  //   Program Counter
  //   Clock Sequencer
  //   U11
  //   Carry FF
  //   U19
  //   # Clock
endmodule
