// Digital circuit ROM_and_clock_sequencer.dig as structural Verilog
module ROM_and_clock_sequencer (
  input  nRES_COUNT,
  input  JMP,
  input  clk,
  output nLD,
  output nSET,
  output nRES,
  output GCLK
);

  wire A0, A1, A2, A3, A4, A5, A6, A7, A8, A9, A10, A11, A12, A13, A14, A15, button_1_out, LD, nand_1_out,
       nand_2_out, nand_3_out, nand_6_out, nand_8_out, nCLR, nCLRPC, nPCRES, PC_Cin, PCin, PCout, R0, R1, R2,
       R3, R4, R5, R6, R7, R8, R9, R10, R11, R12, R13, R14, R15, RES, RESET_out, Rout, SETC, U8_pin15,
       U23_pin9, U25_pin9, xor_1_out, xor_2_out, xor_3_out, xor_4_out;

  _74165 U25 (
    .pin1(nLD), .pin2(GCLK), .pin3(R11), .pin4(R10), .pin5(R9), .pin6(R8), .pin8(1'b0), .pin9(U25_pin9),
    .pin10(1'b0), .pin11(R15), .pin12(R14), .pin13(R13), .pin14(R12), .pin15(1'b0), .pin16(1'b1));  // open: pin7
  _74165 U26 (
    .pin1(nLD), .pin2(GCLK), .pin3(R3), .pin4(R2), .pin5(R1), .pin6(R0), .pin8(1'b0), .pin9(Rout),
    .pin10(U25_pin9), .pin11(R7), .pin12(R6), .pin13(R5), .pin14(R4), .pin15(1'b0), .pin16(1'b1));  // open: pin7
  Seven_Seg_Hex seven_seg_hex_1 (.d({A15, A14, A13, A12}), .dp(1'b0));
  Seven_Seg_Hex seven_seg_hex_2 (.d({A11, A10, A9, A8}), .dp(1'b0));
  Seven_Seg_Hex seven_seg_hex_3 (.d({A7, A6, A5, A4}), .dp(1'b0));
  nand nand_1 (nand_1_out, PCout, PC_Cin);
  xor xor_1 (xor_1_out, PCout, PC_Cin);
  xor xor_2 (xor_2_out, JMP, 1'b1);
  Seven_Seg_Hex seven_seg_hex_4 (.d({A3, A2, A1, A0}), .dp(1'b0));
  // _27C1024 U24: pin names not known; wires that end beside it: 1'b1, 1'b0, R15, R14, R13, R12, R11, R10, R9, R8, 1'b0, R7, R6, R5, R4, R3, 1'b1, A15, A14, A13, A12, A11, A10, A9
  xor xor_3 (xor_3_out, nand_1_out, 1'b1);
  xor xor_4 (xor_4_out, nRES_COUNT, xor_2_out);
  Seven_Seg_Hex seven_seg_hex_5 (.d({R15, R14, R13, R12}), .dp(1'b0));
  Seven_Seg_Hex seven_seg_hex_6 (.d({R11, R10, R9, R8}), .dp(1'b0));
  Seven_Seg_Hex seven_seg_hex_7 (.d({R7, R6, R5, R4}), .dp(1'b0));
  nand nand_2 (nand_2_out, xor_1_out, xor_4_out);
  nand nand_3 (nand_3_out, xor_2_out, Rout);
  Seven_Seg_Hex seven_seg_hex_8 (.d({R3, R2, R1, R0}), .dp(1'b0));
  nand nand_4 (PCin, nand_2_out, nand_3_out);
  _74595 U23 (
    .pin1(A14), .pin2(A13), .pin3(A12), .pin4(A11), .pin5(A10), .pin6(A9), .pin7(A8), .pin8(1'b0),
    .pin9(U23_pin9), .pin10(nPCRES), .pin11(GCLK), .pin12(nRES), .pin13(1'b0), .pin14(PCin), .pin15(A15),
    .pin16(1'b1));
  _74595 U22 (
    .pin1(A6), .pin2(A5), .pin3(A4), .pin4(A3), .pin5(A2), .pin6(A1), .pin7(A0), .pin8(1'b0), .pin9(PCout),
    .pin10(nPCRES), .pin11(GCLK), .pin12(nRES), .pin13(1'b0), .pin14(U23_pin9), .pin15(A7), .pin16(1'b1));
  _7474 U29 (
    .pin1(1'b1), .pin2(xor_3_out), .pin3(GCLK), .pin4(nLD), .pin5(PC_Cin), .pin7(1'b0), .pin10(1'b1),
    .pin11(1'b1), .pin12(1'b1), .pin13(1'b1), .pin14(1'b1));  // open: pin6, pin8, pin9
  Monoflop Mono4 (.C(nLD), .R(1'b0), .Q(SETC), .nQ(nSET));
  Monoflop Mono3 (.C(button_1_out), .R(1'b0), .Q(LD), .nQ(nLD));
  Button button_1 (.out(button_1_out));
  Monoflop monoflop_1 (.C(RESET_out), .R(1'b0), .Q(nCLRPC), .nQ(nPCRES));
  Button RESET (.out(RESET_out));
  nand nand_5 (nCLR, nSET, nand_6_out);
  nand nand_6 (nand_6_out, nCLR, nRES);
  nand nand_7 (GCLK, nCLR, nand_8_out);
  nand nand_8 (nand_8_out, clk, clk);
  _74161 U8 (
    .pin1(nCLR), .pin2(clk), .pin3(1'b0), .pin4(1'b0), .pin5(1'b0), .pin6(1'b0), .pin7(1'b1), .pin8(1'b0),
    .pin9(1'b1), .pin10(1'b1), .pin15(U8_pin15), .pin16(1'b1));  // open: pin11, pin12, pin13, pin14
  _7474 U30 (
    .pin1(1'b1), .pin2(U8_pin15), .pin3(clk), .pin4(1'b1), .pin5(RES), .pin6(nRES), .pin7(1'b0),
    .pin10(1'b1), .pin11(1'b1), .pin12(1'b1), .pin13(1'b1), .pin14(1'b1));  // open: pin8, pin9

  // Other names for the same wires on the sheet: T0 = nRES

  // Notes on the sheet:
  //   nRES_COUNT: default 1
  //   JMP: default 1
  //   clk: Hz: 2
  //   ROM & PC UNIT
  //   ROM Data Register
  //   ROM ADDRESS
  //   U28A
  //   U27A
  //   U27D
  //   16-bit ROM
  //   U27C
  //   U27B
  //   ROM DATA
  //   Carry is only set before Bit 0 of an operation
  //   U28C
  //   U28B
  //   U28D
  //   PC Carry FF
  //   Program Counter
  //   Sequencer
  //   STEP/RUN
  //   U21
  //   U15
  //   Clock Sequencer
  //   U13
  //   Carry FF
endmodule
