// Digital circuit ROM_and_serial_PC.dig as structural Verilog
module ROM_and_serial_PC (
  input  nRES_COUNT,
  input  JMP
);

  wire A0, A1, A2, A3, A4, A5, A6, A7, A8, A9, A10, A11, A12, A13, A14, A15, Bout, BUS3, BUS4, BUS5, BUS6,
       BUS7, BUS8, BUS9, BUS10, BUS11, BUS12, BUS13, BUS14, BUS15, GCLK, nand_1_out, nand_2_out, nand_3_out,
       nLD, nR, nRRES, PC_Cin, PCin, PCout, U23_pin9, xor_1_out, xor_2_out, xor_3_out, xor_4_out;

  nand nand_1 (nand_1_out, PCout, PC_Cin);
  xor xor_1 (xor_1_out, PCout, PC_Cin);
  xor xor_2 (xor_2_out, JMP, 1'b1);
  // _27C1024 U24: pin names not known; wires that end beside it: 1'b1, 1'b0, BUS15, BUS14, BUS13, BUS12, BUS11, BUS10, BUS9, BUS8, 1'b0, BUS7, BUS6, BUS5, BUS4, BUS3, 1'b1, A15, A14, A13, A12, A11, A10, A9
  xor xor_3 (xor_3_out, nand_1_out, 1'b1);
  xor xor_4 (xor_4_out, nRES_COUNT, xor_2_out);
  nand nand_2 (nand_2_out, xor_1_out, xor_4_out);
  nand nand_3 (nand_3_out, xor_2_out, Bout);
  nand nand_4 (PCin, nand_2_out, nand_3_out);
  _74595 U23 (
    .pin1(A14), .pin2(A13), .pin3(A12), .pin4(A11), .pin5(A10), .pin6(A9), .pin7(A8), .pin8(1'b0),
    .pin9(U23_pin9), .pin10(nRRES), .pin11(GCLK), .pin12(nR), .pin13(1'b0), .pin14(PCin), .pin15(A15),
    .pin16(1'b1));
  _74595 U22 (
    .pin1(A6), .pin2(A5), .pin3(A4), .pin4(A3), .pin5(A2), .pin6(A1), .pin7(A0), .pin8(1'b0), .pin9(PCout),
    .pin10(nRRES), .pin11(GCLK), .pin12(nR), .pin13(1'b0), .pin14(U23_pin9), .pin15(A7), .pin16(1'b1));
  _7474 U29 (
    .pin1(1'b1), .pin2(xor_3_out), .pin3(GCLK), .pin4(nLD), .pin5(PC_Cin), .pin7(1'b0), .pin10(1'b1),
    .pin11(1'b1), .pin12(1'b1), .pin13(1'b1), .pin14(1'b1));  // open: pin6, pin8, pin9

  // Notes on the sheet:
  //   nRES_COUNT: default 1
  //   JMP: default 1
  //   ROM and Serial PC
  //   U28A
  //   U27A
  //   U27D
  //   Carry is only set before Bit 0 of an operation
  //   16-bit ROM
  //   U27C
  //   U27B
  //   U28C
  //   U28B
  //   U28D
  //   PC Carry FF
  //   Program Counter
endmodule
