// Digital circuit ROM_circuit.dig as structural Verilog
module ROM_circuit (
);

  wire A9, A10, A11, A12, A13, A14, A15, BUS0, BUS1, BUS2, BUS3, BUS4, BUS5, BUS6, BUS7, D0, D1, D2, D3, D4,
       D5, D6, D7, Fout, GCLK, IR0, IR1, IR2, IR3, IR4, IR5, IR6, IR7, MAin, MAout, nand_1_out, nand_2_out,
       nand_3_out, nand_4_out, nand_5_out, nand_6_out, nDE, nRRES, RAM0, RAM1, RAM2, RAM3, RAM4, RAM5, RAM6,
       RAM7, RAM8, RAM9, RAM10, RAM11, RAM12, RAM13, RAM14, RAM15, SELX, T0, U16_pin9, U33_p9, U33_p10,
       U33_p11, U33_p12, U33_p13, U33_p15, U33_p16, U33_p17, U33_p18, U33_p19, U33_p20, U33_p21, U33_p22,
       U34_pin2, U34_pin3, U34_pin4, Xin, Xout;

  _74595 U16 (
    .pin1(RAM14), .pin2(RAM13), .pin3(RAM12), .pin4(RAM11), .pin5(RAM10), .pin6(RAM9), .pin7(RAM8),
    .pin8(1'b0), .pin9(U16_pin9), .pin10(nRRES), .pin11(GCLK), .pin12(T0), .pin13(1'b0), .pin14(MAin),
    .pin15(RAM15), .pin16(1'b1));
  // _27C1024 U33: pin names not known; wires that end beside it: A9, A10, A11, A12, A13, A14, A15, 1'b1, U33_p9, U33_p10, U33_p11, U33_p12, U33_p13, 1'b0, U33_p15, U33_p16, U33_p17, U33_p18, U33_p19, U33_p20, U33_p21, U33_p22, 1'b0, 1'b1
  _74574 U34 (
    .pin1(1'b0), .pin2(U34_pin2), .pin3(U34_pin3), .pin4(U34_pin4), .pin5(U33_p9), .pin6(U33_p10),
    .pin7(U33_p11), .pin8(U33_p12), .pin9(U33_p13), .pin10(1'b0), .pin11(T0), .pin12(IR7), .pin13(IR6),
    .pin14(IR5), .pin15(IR4), .pin16(IR3), .pin17(IR2), .pin18(IR1), .pin19(IR0), .pin20(1'b1));
  _74574 U35 (
    .pin1(1'b0), .pin2(U33_p15), .pin3(U33_p16), .pin4(U33_p17), .pin5(U33_p18), .pin6(U33_p19),
    .pin7(U33_p20), .pin8(U33_p21), .pin9(U33_p22), .pin10(1'b0), .pin11(T0), .pin12(D7), .pin13(D6),
    .pin14(D5), .pin15(D4), .pin16(D3), .pin17(D2), .pin18(D1), .pin19(D0), .pin20(1'b1));
  _74595 U17 (
    .pin1(RAM6), .pin2(RAM5), .pin3(RAM4), .pin4(RAM3), .pin5(RAM2), .pin6(RAM1), .pin7(RAM0), .pin8(1'b0),
    .pin9(MAout), .pin10(nRRES), .pin11(GCLK), .pin12(T0), .pin13(1'b0), .pin14(U16_pin9), .pin15(RAM7),
    .pin16(1'b1));
  Seven_Seg_Hex seven_seg_hex_1 (.d({IR7, IR6, IR5, IR4}), .dp(1'b0));
  Seven_Seg_Hex seven_seg_hex_2 (.d({RAM15, RAM14, RAM13, RAM12}), .dp(1'b0));
  Seven_Seg_Hex seven_seg_hex_3 (.d({IR3, IR2, IR1, IR0}), .dp(1'b0));
  Seven_Seg_Hex seven_seg_hex_4 (.d({RAM11, RAM10, RAM9, RAM8}), .dp(1'b0));
  _74541 U36 (
    .pin1(nDE), .pin2(D0), .pin3(D1), .pin4(D2), .pin5(D3), .pin6(D4), .pin7(D5), .pin8(D6), .pin9(D7),
    .pin10(1'b0), .pin11(BUS7), .pin12(BUS6), .pin13(BUS5), .pin14(BUS4), .pin15(BUS3), .pin16(BUS2),
    .pin17(BUS1), .pin18(BUS0), .pin19(nDE), .pin20(1'b1));
  Seven_Seg_Hex seven_seg_hex_5 (.d({RAM7, RAM6, RAM5, RAM4}), .dp(1'b0));
  Seven_Seg_Hex seven_seg_hex_6 (.d({D7, D6, D5, D4}), .dp(1'b0));
  Seven_Seg_Hex seven_seg_hex_7 (.d({RAM3, RAM2, RAM1, RAM0}), .dp(1'b0));
  Seven_Seg_Hex seven_seg_hex_8 (.d({D3, D2, D1, D0}), .dp(1'b0));
  nand nand_1 (nand_1_out, SELX, SELX);
  nand nand_2 (nand_2_out, SELX, SELX);
  nand nand_3 (nand_3_out, Xout, SELX);
  nand nand_4 (nand_4_out, nand_1_out, Fout);
  nand nand_5 (nand_5_out, Xout, SELX);
  nand nand_6 (nand_6_out, nand_2_out, Fout);
  nand nand_7 (Xin, nand_3_out, nand_4_out);
  nand nand_8 (Xin, nand_5_out, nand_6_out);
  // _74139 _74139_1: pin names not known

  // Notes on the sheet:
  //   INSTRUCTION
  //   RAM Address
  //   DATA
  //   U21
endmodule
