// Digital circuit Reduced_ALU_slice.dig as structural Verilog
module Reduced_ALU_slice (
  input  I1,
  input  I0,
  input  I2_NEG,
  input  Cin,
  input  I3_SC,
  input  A0,
  input  B0,
  output Cout,
  output Fout
);

  wire and_1_out, and_2_out, nand_1_out, nand_2_out, nand_3_out, xor_1_out, xor_2_out, xor_4_out;

  xor xor_1 (xor_1_out, B0, I2_NEG);
  xor xor_2 (xor_2_out, A0, xor_1_out);
  and and_1 (and_1_out, A0, xor_1_out);
  nand nand_1 (nand_1_out, xor_2_out, I0);
  nand nand_2 (nand_2_out, I1, and_1_out);
  nand nand_3 (nand_3_out, nand_1_out, nand_2_out);
  xor xor_3 (Fout, nand_3_out, Cin);
  and and_2 (and_2_out, nand_3_out, Cin);
  xor xor_4 (xor_4_out, and_2_out, and_1_out);
  and and_3 (Cout, xor_4_out, I3_SC);

  // Other names for the same wires on the sheet: AL = I3_SC
endmodule
