// Digital circuit Spider_Gig_0.dig as structural Verilog
module Spider_Gig_0 (
  input  in_1,
  input  CLK,
  input  clk_2,
  input  in_4,
  input  in_5,
  input  in_6,
  output LD,
  output RES,
  output GCLK,
  output T0,
  output RST
);

  wire A0, A1, A2, A3, A4, A5, A6, A7, A8, A9, A10, A11, A12, A13, A14, A15, AC0, AC1, AC2, AC3, AC4, AC5,
       AC6, AC7, AC8, AC9, AC10, AC11, AC12, AC13, AC14, AC15, ADD, AL, AND, AR0, AR1, AR2, AR3, Bout, BUS0,
       BUS1, BUS2, BUS3, BUS4, BUS5, BUS6, BUS7, BUS8, BUS9, BUS10, BUS11, BUS12, BUS13, BUS14, BUS15,
       button_1_out, button_2_out, button_3_out, button_4_out, button_5_out, button_6_out, button_7_out,
       button_8_out, button_9_out, button_10_out, button_11_out, button_12_out, button_13_out, button_14_out,
       button_15_out, button_16_out, button_17_out, button_18_out, C, Cin, CLA, CLK2, CLR, CO, Cout,
       d_ff_1_nq, d_ff_2_nq, d_ff_3_nq, d_ff_4_nq, d_ff_5_nq, d_ff_6_nq, d_ff_7_nq, d_ff_8_nq, d_ff_9_nq,
       d_ff_10_nq, d_ff_11_nq, d_ff_12_nq, diodebackward_1_out, diodebackward_5_out, diodebackward_7_out,
       diodebackward_9_out, diodebackward_27_out, diodebackward_31_out, diodebackward_32_out,
       diodebackward_38_out, diodebackward_39_out, diodeforward_1_out, EH, EL, F, Fout, I0, I1, IC16_2_nq,
       IC16_nq, IC17_2_nq, IC17_nq, IC21_pin11, IC21_pin12, IC21_pin13, IC21_pin14, IC21_pin15, IC21_pin16,
       IC21_pin17, IC21_pin18, IR0, IR1, IR2, IR3, IR4, IR5, IR6, IR7, IX, LD_t, LOAD, nA, nAE, nand_2_out,
       nand_3_out, nand_5_out, nand_6_out, nand_7_out, nand_8_out, nand_10_out, nand_11_out, nand_13_out,
       nand_14_out, nand_15_out, nB, nBF, nCLRPC, nDE, nIE, nJMP, nLD, nOE, nOL, not_1_out, not_2_out,
       not_3_out, not_4_out, not_5_out, not_6_out, not_8_out, nPH, nPL, nWE, nXL, nYL, OR, OUT0, OUT1, OUT2,
       OUT3, OUT4, OUT5, OUT6, OUT7, PC0, PC1, PC2, PC3, PC4, PC5, PC6, PC7, PC8, PC9, PC10, PC11, PC12,
       PC13, PC14, PC15, pullup_6_out, pullup_8_out, pullup_12_out, pullup_14_out, pullup_17_out, RCO,
       reset_1_out, SETC, ST, SUB, U3_2_pin9, U3_pin15, U4_pin15, U5_pin15, U7_p9, U7_p10, U7_p11, U7_p12,
       U7_p13, U7_p15, U7_p16, U7_p17, U7_p18, U7_p19, U7_p20, U7_p21, U7_p22, U8_2_pin9, U8_pin2, U8_pin3,
       U8_pin4, U9_2_pin9, U12_pin7, U13_pin7, U13_pin9, U13_pin12, U13_pin13, U13_pin14, U13_pin15,
       U29_pin15, U35_pin15, X0, X1, X2, X3, X4, X5, X6, X7, XOR, xor_1_out, xor_2_out, xor_3_out, xor_4_out,
       XOUT0, XOUT1, XOUT2, XOUT3, XOUT4, XOUT5, XOUT6, XOUT7, Y0, Y1, Y2, Y3, Y4, Y5, Y6, Y7, ZERO;
  wire [3:0] U7_2_pin11;

  _74173 U31A (
    .pin1(1'b0), .pin2(1'b0), .pin3(Y3), .pin4(Y2), .pin5(Y1), .pin6(Y0), .pin7(CLK2), .pin8(1'b0),
    .pin9(nYL), .pin10(nYL), .pin11(AC0), .pin12(AC1), .pin13(AC2), .pin14(AC3), .pin15(1'b0), .pin16(1'b1));
  _74173 U31B (
    .pin1(1'b0), .pin2(1'b0), .pin3(Y7), .pin4(Y6), .pin5(Y5), .pin6(Y4), .pin7(CLK2), .pin8(1'b0),
    .pin9(nYL), .pin10(nYL), .pin11(AC4), .pin12(AC5), .pin13(AC6), .pin14(AC7), .pin15(1'b0), .pin16(1'b1));
  // _62256 U37: pin names not known; wires that end beside it: A14, A12, A7, A6, A5, A4, A3, A2, A1, A0, BUS8, BUS9, BUS10, 1'b1, nWE, A13, A8, A9, A11, nOE, A10, 1'b0, BUS15
  // _62256 U36: pin names not known; wires that end beside it: A14, A12, A7, A6, A5, A4, A3, A2, A1, A0, BUS0, BUS1, BUS2, 1'b0, 1'b0, 1'b1, nWE, A13, A8, A9, A11, nOE, A10, 1'b0, BUS7
  _74157 U33 (
    .pin1(1'b0), .pin2(Y4), .pin3(1'b1), .pin4(A12), .pin5(Y5), .pin6(1'b1), .pin7(A13), .pin8(1'b0),
    .pin9(A14), .pin10(1'b1), .pin11(Y6), .pin12(A15), .pin13(1'b1), .pin14(Y7), .pin15(EH), .pin16(1'b1));
  _74157 U32 (
    .pin1(1'b0), .pin2(Y0), .pin3(1'b1), .pin4(A8), .pin5(Y1), .pin6(1'b1), .pin7(A9), .pin8(1'b0),
    .pin9(A10), .pin10(1'b1), .pin11(Y2), .pin12(A11), .pin13(1'b1), .pin14(Y3), .pin15(EH), .pin16(1'b1));
  _74163 U29 (
    .pin1(1'b1), .pin2(CLK2), .pin3(AC0), .pin4(AC1), .pin5(AC2), .pin6(AC3), .pin7(IX), .pin8(1'b0),
    .pin9(nXL), .pin10(1'b1), .pin11(X3), .pin12(X2), .pin13(X1), .pin14(X0), .pin15(U29_pin15), .pin16(1'b1));
  _74163 U30 (
    .pin1(1'b1), .pin2(CLK2), .pin3(AC4), .pin4(AC5), .pin5(AC6), .pin6(AC7), .pin7(IX), .pin8(1'b0),
    .pin9(nXL), .pin10(U29_pin15), .pin11(X7), .pin12(X6), .pin13(X5), .pin14(X4), .pin16(1'b1));  // open: pin15
  _74157 U35 (
    .pin1(EL), .pin2(X4), .pin3(BUS4), .pin4(A4), .pin5(X5), .pin6(BUS5), .pin7(A5), .pin8(1'b0), .pin9(A6),
    .pin10(BUS6), .pin11(X6), .pin12(A7), .pin13(BUS7), .pin14(X7), .pin15(U35_pin15), .pin16(1'b1));
  _74157 U34 (
    .pin1(EL), .pin2(X0), .pin3(BUS0), .pin4(A0), .pin5(X1), .pin6(BUS1), .pin7(A1), .pin8(1'b0), .pin9(A2),
    .pin10(BUS2), .pin11(X2), .pin12(A3), .pin13(BUS3), .pin14(X3), .pin15(U35_pin15), .pin16(1'b1));
  and and_1 (U35_pin15, nWE, nOE);
  Seven_Seg_Hex seven_seg_hex_1 (.d({Y7, Y6, Y5, Y4}), .dp(1'b0));
  Seven_Seg_Hex seven_seg_hex_2 (.d({Y3, Y2, Y1, Y0}), .dp(1'b0));
  Seven_Seg_Hex seven_seg_hex_3 (.d({X7, X6, X5, X4}), .dp(1'b0));
  not not_1 (not_1_out, nDE);
  not not_2 (not_2_out, nOE);
  not not_3 (not_3_out, nAE);
  not not_4 (not_4_out, nIE);
  not not_5 (not_5_out, nOL);
  _74540 IC21 (
    .pin1(1'b0), .pin2(LD_t), .pin3(AND), .pin4(OR), .pin5(XOR), .pin6(ADD), .pin7(SUB), .pin8(ST),
    .pin9(nJMP), .pin10(1'b0), .pin11(IC21_pin11), .pin12(IC21_pin12), .pin13(IC21_pin13),
    .pin14(IC21_pin14), .pin15(IC21_pin15), .pin16(IC21_pin16), .pin17(IC21_pin17), .pin18(IC21_pin18),
    .pin19(1'b0), .pin20(1'b1));
  Seven_Seg_Hex seven_seg_hex_4 (.d({X3, X2, X1, X0}), .dp(1'b0));
  LED DATA (.in(not_1_out));
  LED RAM (.in(not_2_out));
  LED ACC (.in(not_3_out));
  LED INPUT (.in(not_4_out));
  LED OUTPUT (.in(not_5_out));
  Delay delay_1 (.in(CLK), .out(CLK2));
  Seven_Seg_Hex seven_seg_hex_5 (.d({AC7, AC6, AC5, AC4}), .dp(1'b0));
  LED led_1 (.in(IC21_pin18));
  LED led_2 (.in(IC21_pin17));
  LED led_3 (.in(IC21_pin16));
  LED led_4 (.in(IC21_pin15));
  LED led_5 (.in(IC21_pin14));
  LED led_6 (.in(IC21_pin13));
  LED led_7 (.in(IC21_pin12));
  LED led_8 (.in(IC21_pin11));
  Seven_Seg_Hex seven_seg_hex_6 (.d({AC3, AC2, AC1, AC0}), .dp(1'b0));
  Reset reset_1 (.out(reset_1_out));
  LED led_9 (.in(XOUT3));
  Seven_Seg_Hex seven_seg_hex_7 (.d({A15, A14, A13, A12}), .dp(1'b0));
  LED led_10 (.in(XOUT2));
  _74163 U3 (
    .pin1(reset_1_out), .pin2(CLK), .pin3(BUS0), .pin4(BUS1), .pin5(BUS2), .pin6(BUS3), .pin7(1'b1),
    .pin8(1'b0), .pin9(nPL), .pin10(1'b1), .pin11(PC3), .pin12(PC2), .pin13(PC1), .pin14(PC0),
    .pin15(U3_pin15), .pin16(1'b1));
  _74163 U4 (
    .pin1(reset_1_out), .pin2(CLK), .pin3(BUS4), .pin4(BUS5), .pin5(BUS6), .pin6(BUS7), .pin7(1'b1),
    .pin8(1'b0), .pin9(nPL), .pin10(U3_pin15), .pin11(PC7), .pin12(PC6), .pin13(PC5), .pin14(PC4),
    .pin15(U4_pin15), .pin16(1'b1));
  _74163 U5 (
    .pin1(reset_1_out), .pin2(CLK), .pin3(Y0), .pin4(Y1), .pin5(Y2), .pin6(Y3), .pin7(1'b1), .pin8(1'b0),
    .pin9(nPH), .pin10(U4_pin15), .pin11(PC11), .pin12(PC10), .pin13(PC9), .pin14(PC8), .pin15(U5_pin15),
    .pin16(1'b1));
  _74163 U6 (
    .pin1(reset_1_out), .pin2(CLK), .pin3(Y4), .pin4(Y5), .pin5(Y6), .pin6(Y7), .pin7(1'b1), .pin8(1'b0),
    .pin9(nPH), .pin10(U5_pin15), .pin11(PC15), .pin12(PC14), .pin13(PC13), .pin14(PC12), .pin16(1'b1));  // open: pin15
  Seven_Seg_Hex seven_seg_hex_8 (.d({A11, A10, A9, A8}), .dp(1'b0));
  LED led_11 (.in(XOUT1));
  Seven_Seg_Hex seven_seg_hex_9 (.d({A7, A6, A5, A4}), .dp(1'b0));
  LED led_12 (.in(XOUT0));
  Seven_Seg_Hex seven_seg_hex_10 (.d({A3, A2, A1, A0}), .dp(1'b0));
  Seven_Seg_Hex seven_seg_hex_11 (.d({BUS7, BUS6, BUS5, BUS4}), .dp(1'b0));
  Seven_Seg_Hex seven_seg_hex_12 (.d({BUS3, BUS2, BUS1, BUS0}), .dp(1'b0));
  Seven_Seg_Hex seven_seg_hex_13 (.d({OUT7, OUT6, OUT5, OUT4}), .dp(1'b0));
  Seven_Seg_Hex seven_seg_hex_14 (.d({OUT3, OUT2, OUT1, OUT0}), .dp(1'b0));
  // _27C1024 U7: pin names not known; wires that end beside it: PC9, PC10, PC11, PC12, PC13, PC14, PC15, 1'b1, U7_p9, U7_p10, U7_p11, U7_p12, U7_p13, 1'b0, U7_p15, U7_p16, U7_p17, U7_p18, U7_p19, U7_p20, U7_p21, U7_p22, 1'b0, 1'b1
  Seven_Seg_Hex seven_seg_hex_15 (.d({PC15, PC14, PC13, PC12}), .dp(1'b0));
  Seven_Seg_Hex seven_seg_hex_16 (.d({PC11, PC10, PC9, PC8}), .dp(1'b0));
  _74574 U8 (
    .pin1(1'b0), .pin2(U8_pin2), .pin3(U8_pin3), .pin4(U8_pin4), .pin5(U7_p9), .pin6(U7_p10), .pin7(U7_p11),
    .pin8(U7_p12), .pin9(U7_p13), .pin10(1'b0), .pin11(CLK), .pin12(IR7), .pin13(IR6), .pin14(IR5),
    .pin15(IR4), .pin16(IR3), .pin17(IR2), .pin18(IR1), .pin19(IR0), .pin20(1'b1));
  _74574 U9 (
    .pin1(1'b0), .pin2(U7_p15), .pin3(U7_p16), .pin4(U7_p17), .pin5(U7_p18), .pin6(U7_p19), .pin7(U7_p20),
    .pin8(U7_p21), .pin9(U7_p22), .pin10(1'b0), .pin11(CLK), .pin12(BUS7), .pin13(BUS6), .pin14(BUS5),
    .pin15(BUS4), .pin16(BUS3), .pin17(BUS2), .pin18(BUS1), .pin19(BUS0), .pin20(1'b1));
  Seven_Seg_Hex seven_seg_hex_17 (.d({PC7, PC6, PC5, PC4}), .dp(1'b0));
  Seven_Seg_Hex seven_seg_hex_18 (.d({PC3, PC2, PC1, PC0}), .dp(1'b0));
  Seven_Seg_Hex seven_seg_hex_19 (.d({IR7, IR6, IR5, IR4}), .dp(1'b0));
  Seven_Seg_Hex seven_seg_hex_20 (.d({IR3, IR2, IR1, IR0}), .dp(1'b0));
  _74541 U11 (
    .pin1(nDE), .pin2(IR0), .pin3(IR1), .pin4(IR2), .pin5(IR3), .pin6(IR4), .pin7(IR5), .pin8(IR6),
    .pin9(IR7), .pin10(1'b0), .pin11(BUS15), .pin12(BUS14), .pin13(BUS13), .pin14(BUS12), .pin15(BUS11),
    .pin16(BUS10), .pin17(BUS9), .pin18(BUS8), .pin19(nDE), .pin20(1'b1));
  _74541 U10 (
    .pin1(nDE), .pin2(BUS0), .pin3(BUS1), .pin4(BUS2), .pin5(BUS3), .pin6(BUS4), .pin7(BUS5), .pin8(BUS6),
    .pin9(BUS7), .pin10(1'b0), .pin11(BUS7), .pin12(BUS6), .pin13(BUS5), .pin14(BUS4), .pin15(BUS3),
    .pin16(BUS2), .pin17(BUS1), .pin18(BUS0), .pin19(nDE), .pin20(1'b1));
  Seven_Seg_Hex seven_seg_hex_21 (.d({BUS7, BUS6, BUS5, BUS4}), .dp(1'b0));
  Seven_Seg_Hex seven_seg_hex_22 (.d({BUS3, BUS2, BUS1, BUS0}), .dp(1'b0));
  _74139 U11_2 (
    .pin1(1'b0), .pin2(IR0), .pin3(IR1), .pin4(nDE), .pin5(nOE), .pin6(nAE), .pin7(nIE), .pin8(1'b0),
    .pin12(nBF), .pin13(IR2), .pin14(IR3), .pin15(IR4), .pin16(1'b1));  // open: pin9, pin10, pin11
  _74138 U13 (
    .pin1(IR2), .pin2(IR3), .pin3(IR4), .pin4(1'b0), .pin5(1'b0), .pin6(nJMP), .pin7(U13_pin7), .pin8(1'b0),
    .pin9(U13_pin9), .pin10(nYL), .pin11(nXL), .pin12(U13_pin12), .pin13(U13_pin13), .pin14(U13_pin14),
    .pin15(U13_pin15), .pin16(1'b1));
  _74138 U14 (
    .pin1(IR5), .pin2(IR6), .pin3(IR7), .pin4(1'b0), .pin5(1'b0), .pin6(1'b1), .pin7(nJMP), .pin8(1'b0),
    .pin9(ST), .pin10(SUB), .pin11(ADD), .pin12(XOR), .pin13(OR), .pin14(AND), .pin15(LD_t), .pin16(1'b1));
  DiodeBackward diodebackward_1 (.in(U13_pin15), .out(diodebackward_1_out));
  DiodeBackward diodebackward_2 (.in(U13_pin14), .out(diodebackward_1_out));
  DiodeBackward diodebackward_3 (.in(U13_pin13), .out(diodebackward_1_out));
  DiodeBackward diodebackward_4 (.in(U13_pin12), .out(diodebackward_1_out));
  DiodeBackward diodebackward_5 (.in(IR7), .out(diodebackward_5_out));
  DiodeBackward diodebackward_6 (.in(nJMP), .out(diodebackward_5_out));
  PullUp pullup_1 (.out(diodebackward_1_out));
  DiodeBackward diodebackward_7 (.in(U13_pin9), .out(diodebackward_7_out));
  DiodeBackward diodebackward_8 (.in(U13_pin7), .out(diodebackward_7_out));
  PullUp pullup_2 (.out(diodebackward_5_out));
  DiodeBackward diodebackward_9 (.in(LD_t), .out(diodebackward_9_out));
  DiodeBackward diodebackward_10 (.in(AND), .out(diodebackward_9_out));
  DiodeBackward diodebackward_11 (.in(OR), .out(diodebackward_9_out));
  DiodeBackward diodebackward_12 (.in(ADD), .out(diodebackward_9_out));
  PullUp pullup_3 (.out(diodebackward_7_out));
  PullUp pullup_4 (.out(EL));
  DiodeBackward diodebackward_13 (.in(U13_pin14), .out(EL));
  DiodeBackward diodebackward_14 (.in(U13_pin12), .out(EL));
  DiodeBackward diodebackward_15 (.in(U13_pin7), .out(EL));
  PullUp pullup_5 (.out(diodebackward_9_out));
  PullUp pullup_6 (.out(pullup_6_out));
  DiodeBackward diodebackward_16 (.in(LD_t), .out(pullup_6_out));
  DiodeBackward diodebackward_17 (.in(OR), .out(pullup_6_out));
  DiodeBackward diodebackward_18 (.in(XOR), .out(pullup_6_out));
  DiodeBackward diodebackward_19 (.in(ADD), .out(pullup_6_out));
  DiodeBackward diodebackward_20 (.in(ST), .out(pullup_6_out));
  PullUp pullup_7 (.out(EH));
  DiodeBackward diodebackward_21 (.in(U13_pin13), .out(EH));
  DiodeBackward diodebackward_22 (.in(U13_pin12), .out(EH));
  DiodeBackward diodebackward_23 (.in(U13_pin7), .out(EH));
  PullUp pullup_8 (.out(pullup_8_out));
  DiodeBackward diodebackward_24 (.in(OR), .out(pullup_8_out));
  DiodeBackward diodebackward_25 (.in(XOR), .out(pullup_8_out));
  DiodeBackward diodebackward_26 (.in(SUB), .out(pullup_8_out));
  DiodeBackward diodebackward_27 (.in(SUB), .out(diodebackward_27_out));
  DiodeBackward diodebackward_28 (.in(ST), .out(diodebackward_27_out));
  PullUp pullup_9 (.out(diodebackward_27_out));
  _74153 U12 (
    .pin1(nJMP), .pin2(CO), .pin3(1'b0), .pin4(IR4), .pin5(IR3), .pin6(IR2), .pin7(U12_pin7), .pin8(1'b0),
    .pin10(1'b1), .pin11(1'b1), .pin12(1'b1), .pin13(1'b1), .pin14(AC7), .pin15(1'b1), .pin16(1'b1));  // open: pin9
  _74573 U38 (
    .pin1(in_1), .pin2(AC7), .pin3(AC6), .pin4(AC5), .pin5(AC4), .pin6(AC3), .pin7(AC2), .pin8(AC1),
    .pin9(AC0), .pin10(1'b0), .pin11(OUT6), .pin12(XOUT0), .pin13(XOUT1), .pin14(XOUT2), .pin15(XOUT3),
    .pin16(XOUT4), .pin17(XOUT5), .pin18(XOUT6), .pin19(XOUT7), .pin20(1'b1));
  not not_6 (not_6_out, U12_pin7);
  not not_7 (IX, U13_pin7);
  not not_8 (not_8_out, ST);
  _74540 U15 (
    .pin1(1'b0), .pin2(diodebackward_9_out), .pin3(pullup_6_out), .pin4(pullup_8_out),
    .pin5(diodebackward_27_out), .pin6(diodebackward_5_out), .pin7(1'b0), .pin8(1'b0), .pin9(1'b0),
    .pin10(1'b0), .pin14(AL), .pin15(AR0), .pin16(AR1), .pin17(AR2), .pin18(AR3), .pin19(1'b0), .pin20(1'b1));  // open: pin11, pin12, pin13
  DiodeBackward diodebackward_29 (.in(not_6_out), .out(nPL));
  DiodeBackward diodebackward_30 (.in(nPH), .out(nPL));
  or or_1 (nOL, diodebackward_7_out, not_8_out);
  or or_2 (nLD, diodebackward_1_out, not_8_out);
  or or_3 (nWE, CLK, ST);
  or or_4 (nPH, nBF, nJMP);
  PullUp pullup_10 (.out(nPL));
  _74165 U3_2 (
    .pin1(LD), .pin2(GCLK), .pin3(BUS11), .pin4(BUS10), .pin5(BUS9), .pin6(BUS8), .pin8(1'b0),
    .pin9(U3_2_pin9), .pin10(1'b0), .pin11(BUS15), .pin12(BUS14), .pin13(BUS13), .pin14(BUS12), .pin15(1'b0),
    .pin16(1'b1));  // open: pin7
  _74138 U1 (
    .pin1(in_4), .pin2(in_5), .pin3(in_6), .pin4(1'b0), .pin5(1'b0), .pin6(1'b1), .pin7(nJMP), .pin8(1'b0),
    .pin9(ST), .pin10(SUB), .pin11(ADD), .pin12(XOR), .pin13(OR), .pin14(AND), .pin15(LOAD), .pin16(1'b1));
  Monoflop monoflop_1 (.C(LD), .R(1'b0), .Q(SETC), .nQ(RES));
  Monoflop monoflop_2 (.C(button_1_out), .R(1'b0), .Q(LD_t), .nQ(LD));
  Button button_1 (.out(button_1_out));
  DiodeBackward diodebackward_31 (.in(LOAD), .out(diodebackward_31_out));
  Monoflop monoflop_3 (.C(button_2_out), .R(1'b0), .nQ(nCLRPC));  // open: Q
  Button button_2 (.out(button_2_out));
  PullUp pullup_11 (.out(diodebackward_31_out));
  DiodeBackward diodebackward_32 (.in(LOAD), .out(diodebackward_32_out));
  DiodeBackward diodebackward_33 (.in(ADD), .out(diodebackward_32_out));
  DiodeBackward diodebackward_34 (.in(SUB), .out(diodebackward_32_out));
  DiodeBackward diodebackward_35 (.in(nJMP), .out(diodebackward_32_out));
  PullUp pullup_12 (.out(pullup_12_out));
  PullUp pullup_13 (.out(diodebackward_32_out));
  DiodeBackward diodebackward_36 (.in(SUB), .out(pullup_12_out));
  _74165 U4_2 (
    .pin1(LD), .pin2(GCLK), .pin3(BUS3), .pin4(BUS2), .pin5(BUS1), .pin6(BUS0), .pin8(1'b0), .pin9(Bout),
    .pin10(U3_2_pin9), .pin11(BUS7), .pin12(BUS6), .pin13(BUS5), .pin14(BUS4), .pin15(1'b0), .pin16(1'b1));  // open: pin7
  PullUp pullup_14 (.out(pullup_14_out));
  DiodeBackward diodebackward_37 (.in(SUB), .out(pullup_14_out));
  DiodeBackward diodebackward_38 (.in(nJMP), .out(diodebackward_38_out));
  PullUp pullup_15 (.out(diodebackward_38_out));
  DiodeBackward diodebackward_39 (.in(AND), .out(diodebackward_39_out));
  DiodeBackward diodebackward_40 (.in(OR), .out(diodebackward_39_out));
  PullUp pullup_16 (.out(diodebackward_39_out));
  PullUp pullup_17 (.out(pullup_17_out));
  DiodeBackward diodebackward_41 (.in(LOAD), .out(pullup_17_out));
  DiodeBackward diodebackward_42 (.in(OR), .out(pullup_17_out));
  DiodeBackward diodebackward_43 (.in(XOR), .out(pullup_17_out));
  DiodeBackward diodebackward_44 (.in(ADD), .out(pullup_17_out));
  DiodeBackward diodebackward_45 (.in(SUB), .out(pullup_17_out));
  DiodeBackward diodebackward_46 (.in(ST), .out(pullup_17_out));
  DiodeBackward diodebackward_47 (.in(nJMP), .out(pullup_17_out));
  _74540 U2 (
    .pin1(1'b0), .pin2(pullup_17_out), .pin3(diodebackward_39_out), .pin4(diodebackward_38_out),
    .pin5(pullup_14_out), .pin6(pullup_12_out), .pin7(diodebackward_32_out), .pin8(diodebackward_31_out),
    .pin9(1'b0), .pin10(1'b0), .pin12(CLA), .pin13(F), .pin14(C), .pin15(nB), .pin16(nA), .pin17(I1),
    .pin18(I0), .pin19(1'b0), .pin20(1'b1));  // open: pin11
  _74595 U8_2 (
    .pin1(BUS14), .pin2(BUS13), .pin3(BUS12), .pin4(BUS11), .pin5(BUS10), .pin6(BUS9), .pin7(BUS8),
    .pin8(1'b0), .pin9(U8_2_pin9), .pin10(RES), .pin11(GCLK), .pin12(T0), .pin13(nAE), .pin14(Fout),
    .pin15(BUS15), .pin16(1'b1));
  LED led_13 (.in(BUS15));
  D_FF IC17 (.D(IC17_nq), .C(button_3_out), .Q(BUS15), .nQ(IC17_nq));
  LED led_14 (.in(BUS14));
  D_FF d_ff_1 (.D(d_ff_1_nq), .C(button_4_out), .Q(BUS14), .nQ(d_ff_1_nq));
  Button button_3 (.out(button_3_out));
  LED led_15 (.in(BUS13));
  D_FF d_ff_2 (.D(d_ff_2_nq), .C(button_5_out), .Q(BUS13), .nQ(d_ff_2_nq));
  Button button_4 (.out(button_4_out));
  LED led_16 (.in(BUS12));
  D_FF d_ff_3 (.D(d_ff_3_nq), .C(button_6_out), .Q(BUS12), .nQ(d_ff_3_nq));
  Button button_5 (.out(button_5_out));
  _74595 U9_2 (
    .pin1(BUS6), .pin2(BUS5), .pin3(BUS4), .pin4(BUS3), .pin5(BUS2), .pin6(BUS1), .pin7(BUS0), .pin8(1'b0),
    .pin9(U9_2_pin9), .pin10(RES), .pin11(GCLK), .pin12(T0), .pin13(nAE), .pin14(U8_2_pin9), .pin15(BUS7),
    .pin16(1'b1));
  LED led_17 (.in(BUS11));
  D_FF d_ff_4 (.D(d_ff_4_nq), .C(button_7_out), .Q(BUS11), .nQ(d_ff_4_nq));
  Button button_6 (.out(button_6_out));
  LED led_18 (.in(BUS10));
  D_FF d_ff_5 (.D(d_ff_5_nq), .C(button_8_out), .Q(BUS10), .nQ(d_ff_5_nq));
  Button button_7 (.out(button_7_out));
  LED led_19 (.in(BUS9));
  D_FF d_ff_6 (.D(d_ff_6_nq), .C(button_9_out), .Q(BUS9), .nQ(d_ff_6_nq));
  Button button_8 (.out(button_8_out));
  LED led_20 (.in(BUS8));
  D_FF IC17_2 (.D(IC17_2_nq), .C(button_10_out), .Q(BUS8), .nQ(IC17_2_nq));
  Button button_9 (.out(button_9_out));
  Seven_Seg_Hex seven_seg_hex_23 (.d({BUS15, BUS14, BUS13, BUS12}), .dp(1'b0));
  Button button_10 (.out(button_10_out));
  Seven_Seg_Hex seven_seg_hex_24 (.d({BUS15, BUS14, BUS13, BUS12}), .dp(1'b0));
  DiodeForward diodeforward_1 (.in(BUS15), .out(diodeforward_1_out));
  DiodeForward diodeforward_2 (.in(BUS14), .out(diodeforward_1_out));
  DiodeForward diodeforward_3 (.in(BUS13), .out(diodeforward_1_out));
  DiodeForward diodeforward_4 (.in(BUS12), .out(diodeforward_1_out));
  DiodeForward diodeforward_5 (.in(BUS11), .out(diodeforward_1_out));
  DiodeForward diodeforward_6 (.in(BUS10), .out(diodeforward_1_out));
  DiodeForward diodeforward_7 (.in(BUS9), .out(diodeforward_1_out));
  DiodeForward diodeforward_8 (.in(BUS8), .out(diodeforward_1_out));
  DiodeForward diodeforward_9 (.in(BUS7), .out(diodeforward_1_out));
  DiodeForward diodeforward_10 (.in(BUS6), .out(diodeforward_1_out));
  DiodeForward diodeforward_11 (.in(BUS5), .out(diodeforward_1_out));
  DiodeForward diodeforward_12 (.in(BUS4), .out(diodeforward_1_out));
  DiodeForward diodeforward_13 (.in(BUS3), .out(diodeforward_1_out));
  DiodeForward diodeforward_14 (.in(BUS2), .out(diodeforward_1_out));
  DiodeForward diodeforward_15 (.in(BUS1), .out(diodeforward_1_out));
  DiodeForward diodeforward_16 (.in(BUS0), .out(diodeforward_1_out));
  Seven_Seg_Hex seven_seg_hex_25 (.d({BUS11, BUS10, BUS9, BUS8}), .dp(1'b0));
  Seven_Seg_Hex seven_seg_hex_26 (.d({BUS11, BUS10, BUS9, BUS8}), .dp(1'b0));
  PullDown pulldown_1 (.out(diodeforward_1_out));
  Seven_Seg_Hex seven_seg_hex_27 (.d({BUS7, BUS6, BUS5, BUS4}), .dp(1'b0));
  nand nand_1 (ZERO, diodeforward_1_out, diodeforward_1_out);
  LED led_21 (.in(BUS7));
  D_FF IC16 (.D(IC16_nq), .C(button_11_out), .Q(BUS7), .nQ(IC16_nq));
  Button button_11 (.out(button_11_out));
  Seven_Seg_Hex seven_seg_hex_28 (.d({BUS3, BUS2, BUS1, BUS0}), .dp(1'b0));
  LED led_22 (.in(ZERO));
  LED led_23 (.in(BUS6));
  D_FF d_ff_7 (.D(d_ff_7_nq), .C(button_12_out), .Q(BUS6), .nQ(d_ff_7_nq));
  Button button_12 (.out(button_12_out));
  LED led_24 (.in(BUS5));
  D_FF d_ff_8 (.D(d_ff_8_nq), .C(button_13_out), .Q(BUS5), .nQ(d_ff_8_nq));
  Button button_13 (.out(button_13_out));
  LED led_25 (.in(BUS4));
  D_FF d_ff_9 (.D(d_ff_9_nq), .C(button_14_out), .Q(BUS4), .nQ(d_ff_9_nq));
  Button button_14 (.out(button_14_out));
  LED led_26 (.in(BUS3));
  D_FF d_ff_10 (.D(d_ff_10_nq), .C(button_15_out), .Q(BUS3), .nQ(d_ff_10_nq));
  Button button_15 (.out(button_15_out));
  LED led_27 (.in(BUS2));
  D_FF d_ff_11 (.D(d_ff_11_nq), .C(button_16_out), .Q(BUS2), .nQ(d_ff_11_nq));
  Button button_16 (.out(button_16_out));
  LED led_28 (.in(BUS1));
  D_FF d_ff_12 (.D(d_ff_12_nq), .C(button_17_out), .Q(BUS1), .nQ(d_ff_12_nq));
  Button button_17 (.out(button_17_out));
  _74164 U5_2 (
    .pin1(1'b1), .pin2(Fout), .pin3(AC15), .pin4(AC14), .pin5(AC13), .pin6(AC12), .pin7(1'b0), .pin8(GCLK),
    .pin9(CLR), .pin10(AC11), .pin11(AC10), .pin12(AC9), .pin13(AC8), .pin14(1'b1));
  LED led_29 (.in(BUS0));
  D_FF IC16_2 (.D(IC16_2_nq), .C(button_18_out), .Q(BUS0), .nQ(IC16_2_nq));
  Button button_18 (.out(button_18_out));
  Seven_Seg_Hex seven_seg_hex_29 (.d({BUS7, BUS6, BUS5, BUS4}), .dp(1'b0));
  Seven_Seg_Hex seven_seg_hex_30 (.d({BUS3, BUS2, BUS1, BUS0}), .dp(1'b0));
  Seven_Seg_Hex seven_seg_hex_31 (.d({AC15, AC14, AC13, AC12}), .dp(1'b0));
  Seven_Seg_Hex seven_seg_hex_32 (.d({AC11, AC10, AC9, AC8}), .dp(1'b0));
  Seven_Seg_Hex seven_seg_hex_33 (.d({AC7, AC6, AC5, AC4}), .dp(1'b0));
  Seven_Seg_Hex seven_seg_hex_34 (.d({AC3, AC2, AC1, AC0}), .dp(1'b0));
  _74164 U6_2 (
    .pin1(1'b1), .pin2(AC8), .pin3(AC7), .pin4(AC6), .pin5(AC5), .pin6(AC4), .pin7(1'b0), .pin8(GCLK),
    .pin9(CLR), .pin10(AC3), .pin11(AC2), .pin12(AC1), .pin13(AC0), .pin14(1'b1));
  xor xor_1 (xor_1_out, AC0, nA);
  xor xor_2 (xor_2_out, nB, Bout);
  nand nand_2 (nand_2_out, SETC, C);
  nand nand_3 (nand_3_out, C, C);
  nand nand_4 (CLR, CLA, LD_t);
  xor xor_3 (xor_3_out, xor_1_out, xor_2_out);
  nand nand_5 (nand_5_out, nand_3_out, LD_t);
  xor xor_4 (xor_4_out, xor_3_out, Cin);
  nand nand_6 (nand_6_out, xor_3_out, Cin);
  nand nand_7 (nand_7_out, xor_1_out, xor_2_out);
  nand nand_8 (nand_8_out, clk_2, clk_2);
  nand nand_9 (RST, RES, nand_10_out);
  nand nand_10 (nand_10_out, RST, T0);
  nand nand_11 (nand_11_out, nand_6_out, nand_7_out);
  nand nand_12 (GCLK, nand_8_out, RST);
  nand nand_13 (nand_13_out, xor_4_out, I0);
  nand nand_14 (nand_14_out, I1, nand_11_out);
  nand nand_15 (nand_15_out, nand_11_out, F);
  nand nand_16 (Fout, nand_13_out, nand_14_out);
  nand nand_17 (Cout, nand_15_out, nand_15_out);
  _74161 U7_2 (
    .pin1(RST), .pin2(clk_2), .pin3(1'b0), .pin4(1'b0), .pin5(1'b0), .pin6(1'b0), .pin7(1'b1), .pin8(1'b0),
    .pin9(1'b1), .pin10(1'b1), .pin11(U7_2_pin11[3]), .pin12(U7_2_pin11[2]), .pin13(U7_2_pin11[1]),
    .pin14(U7_2_pin11[0]), .pin15(RCO), .pin16(1'b1));
  _7474 _7474_1 (
    .pin1(nand_5_out), .pin2(Cout), .pin3(GCLK), .pin4(nand_2_out), .pin5(Cin), .pin7(1'b0), .pin8(T0),
    .pin9(IX), .pin10(1'b1), .pin11(clk_2), .pin12(RCO), .pin13(1'b1), .pin14(1'b1));  // open: pin6
  LED led_30 (.in(Cin));
  Seven_Seg_Hex seven_seg_hex_35 (.d(U7_2_pin11), .dp(1'b0));

  // Other names for the same wires on the sheet: ALU1 = AC1; ALU2 = AC2; ALU3 = AC3; ALU4 = AC4; ALU5 = AC5;
  //   ALU6 = AC6; ALU7 = AC7; ALU8 = AC8; ALU9 = AC9; ALU10 = AC10; ALU11 = AC11; ALU12 = AC12; ALU13 = AC13;
  //   ALU14 = AC14; ALU15 = AC15; ALU0 = AC0; Aout = AC0; CLK1 = CLK; CLK_t = clk_2; D0 = BUS0; D1 = BUS1; D2 = BUS2;
  //   D3 = BUS3; D4 = BUS4; D5 = BUS5; D6 = BUS6; D7 = BUS7; D8 = BUS8; D9 = BUS9; D10 = BUS10; D11 = BUS11;
  //   D12 = BUS12; D13 = BUS13; D14 = BUS14; D15 = BUS15; nLOAD = LD; nRES = RES

  // Notes on the sheet:
  //   clk_2: Hz: 2147483647
  //   Y REGISTER
  //   RAM & X Y REGS
  //   Y SELECT
  //   X REGISTER
  //   32K RAM
  //   X SELECT
  //   PROGRAM COUNTER & ROM
  //   FRONT PANEL SWITCHES
  //   Y REG
  //   BUS SOURCE
  //   INSTRUCTION
  //   X REG
  //   LOAD
  //   AND
  //   OR
  //   XOR
  //   ADD
  //   SUB
  //   STORE
  //   JMP
  //   ACC
  //   XOUT LEDS
  //   RAM ADDRESS
  //   BUS DATA
  //   OUTPUT
  //   PC ADDRESS
  //   DATA
  //   CONTROL UNIT
  //   REGISTERS
  //   16-bit Jump Detector
  //   OUTPUT REGISTER
  //   EXT. OUTPUT
  //   U15
  //   U16
  //   spider 0
  //   Instruction Input
  //   STEP/RUN
  //   16 bit Shift Register B
  //   CLR PC
  //   Instruction Decode
  //   CLA
  //   C
  //   F
  //   ~B
  //   ~A
  //   I0
  //   I1
  //   Output Display Registers
  //   ENTER H
  //   Data Input
  //   AC -> BUS
  //   ZERO
  //   ENTER L
  //   16 bit Shift Register A
  //   ACCUMULATOR
  //   Spider 0 Bit serial CPU Testbed (15 ICs)
  //   ALU
  //   CLR ACC
  //   Carry is only set before Bit 0 of an operation
  //   Any residual carry is cleared before an operation
  //   Clock Sequencer
  //   Suppress Carry
  //   Carry FF
  //   CARRY
  //   # Clock
endmodule
