// Digital circuit Spider_RAM_system_1.dig as structural Verilog
module Spider_RAM_system_1 (
  input  nRES_COUNT,
  input  JMP,
  input  clk,
  input  in_4,
  input  in_5,
  input  in_6,
  input  READ,
  input  in_8
);

  wire AC0, AC1, AC2, AC3, AC4, AC5, AC6, AC7, AC8, AC9, AC10, AC11, AC12, AC13, AC14, AC15, AD0, AD1, AD2,
       AD3, AD4, AD5, AD6, AD7, AD8, AD9, AD10, AD11, AD12, AD13, AD14, AD15, ADD, AND, Bout, BUS0, BUS1,
       BUS2, BUS3, BUS4, BUS5, BUS6, BUS7, BUS8, BUS9, BUS10, BUS11, BUS12, BUS13, BUS14, BUS15,
       button_1_out, C, Cin, CLA, CLR, Cout, F, Fout, GCLK, I0, I1, LD, LOAD, n2SD, nA, nand_2_out,
       nand_3_out, nand_4_out, nand_6_out, nand_8_out, nand_10_out, nand_11_out, nand_12_out, nand_14_out,
       nand_15_out, nand_16_out, nand_17_out, nand_18_out, nand_19_out, nB, nCLR, nF0, nF1, nF2, nF3, nF4,
       nF5, nF6, nF7, nJMP, nLD, nR, nRES, nWE, OR, PC_Cin, PCin, PCout, pulldown_1_out, R, RCO, RESET_2_out,
       RST, SETC, ST, SUB, U3_pin9, U17_pin9, U23_pin9, XOR, xor_1_out, xor_2_out, xor_3_out, xor_4_out,
       xor_5_out, xor_6_out, xor_7_out, xor_8_out;
  wire [3:0] U7_pin11;

  Seven_Seg_Hex seven_seg_hex_1 (.d({AD15, AD14, AD13, AD12}), .dp(1'b0));
  Seven_Seg_Hex seven_seg_hex_2 (.d({AD11, AD10, AD9, AD8}), .dp(1'b0));
  // NAnd nand_1 has open pins: In_1=pulldown_1_out, In_2=pulldown_1_out, out=open
  _74164 U5 (
    .pin1(1'b1), .pin2(Fout), .pin3(AC15), .pin4(AC14), .pin5(AC13), .pin6(AC12), .pin7(1'b0), .pin8(GCLK),
    .pin9(nCLR), .pin10(AC11), .pin11(AC10), .pin12(AC9), .pin13(AC8), .pin14(1'b1));
  Seven_Seg_Hex seven_seg_hex_3 (.d({AD7, AD6, AD5, AD4}), .dp(1'b0));
  PullDown pulldown_1 (.out(pulldown_1_out));
  Seven_Seg_Hex seven_seg_hex_4 (.d({AD3, AD2, AD1, AD0}), .dp(1'b0));
  DiodeForward diodeforward_1 (.in(AC0), .out(pulldown_1_out));
  DiodeForward diodeforward_2 (.in(AC1), .out(pulldown_1_out));
  DiodeForward diodeforward_3 (.in(AC2), .out(pulldown_1_out));
  DiodeForward diodeforward_4 (.in(AC3), .out(pulldown_1_out));
  DiodeForward diodeforward_5 (.in(AC4), .out(pulldown_1_out));
  DiodeForward diodeforward_6 (.in(AC5), .out(pulldown_1_out));
  DiodeForward diodeforward_7 (.in(AC6), .out(pulldown_1_out));
  DiodeForward diodeforward_8 (.in(AC7), .out(pulldown_1_out));
  DiodeForward diodeforward_9 (.in(AC8), .out(pulldown_1_out));
  DiodeForward diodeforward_10 (.in(AC9), .out(pulldown_1_out));
  DiodeForward diodeforward_11 (.in(AC10), .out(pulldown_1_out));
  DiodeForward diodeforward_12 (.in(AC11), .out(pulldown_1_out));
  DiodeForward diodeforward_13 (.in(AC12), .out(pulldown_1_out));
  DiodeForward diodeforward_14 (.in(AC13), .out(pulldown_1_out));
  DiodeForward diodeforward_15 (.in(AC14), .out(pulldown_1_out));
  DiodeForward diodeforward_16 (.in(AC15), .out(pulldown_1_out));
  Seven_Seg_Hex seven_seg_hex_5 (.d({BUS15, BUS14, BUS13, BUS12}), .dp(1'b0));
  _74165 U3 (
    .pin1(nLD), .pin2(GCLK), .pin3(BUS11), .pin4(BUS10), .pin5(BUS9), .pin6(BUS8), .pin8(1'b0),
    .pin9(U3_pin9), .pin10(1'b0), .pin11(BUS15), .pin12(BUS14), .pin13(BUS13), .pin14(BUS12), .pin15(1'b0),
    .pin16(1'b1));  // open: pin7
  _74165 U4 (
    .pin1(nLD), .pin2(GCLK), .pin3(BUS3), .pin4(BUS2), .pin5(BUS1), .pin6(BUS0), .pin8(1'b0), .pin9(Bout),
    .pin10(U3_pin9), .pin11(BUS7), .pin12(BUS6), .pin13(BUS5), .pin14(BUS4), .pin15(1'b0), .pin16(1'b1));  // open: pin7
  _74164 U6 (
    .pin1(1'b1), .pin2(AC8), .pin3(AC7), .pin4(AC6), .pin5(AC5), .pin6(AC4), .pin7(1'b0), .pin8(GCLK),
    .pin9(nCLR), .pin10(AC3), .pin11(AC2), .pin12(AC1), .pin13(AC0), .pin14(1'b1));
  Seven_Seg_Hex seven_seg_hex_6 (.d({BUS11, BUS10, BUS9, BUS8}), .dp(1'b0));
  Seven_Seg_Hex seven_seg_hex_7 (.d({BUS7, BUS6, BUS5, BUS4}), .dp(1'b0));
  Seven_Seg_Hex seven_seg_hex_8 (.d({BUS3, BUS2, BUS1, BUS0}), .dp(1'b0));
  Seven_Seg_Hex seven_seg_hex_9 (.d({AC15, AC14, AC13, AC12}), .dp(1'b0));
  Seven_Seg_Hex seven_seg_hex_10 (.d({AC11, AC10, AC9, AC8}), .dp(1'b0));
  Seven_Seg_Hex seven_seg_hex_11 (.d({AC7, AC6, AC5, AC4}), .dp(1'b0));
  _74595 U17 (
    .pin1(BUS14), .pin2(BUS13), .pin3(BUS12), .pin4(BUS11), .pin5(BUS10), .pin6(BUS9), .pin7(BUS8),
    .pin8(1'b0), .pin9(U17_pin9), .pin10(nCLR), .pin11(GCLK), .pin12(nR), .pin13(nWE), .pin14(Fout),
    .pin15(BUS15), .pin16(1'b1));
  _74595 U16 (
    .pin1(BUS6), .pin2(BUS5), .pin3(BUS4), .pin4(BUS3), .pin5(BUS2), .pin6(BUS1), .pin7(BUS0), .pin8(1'b0),
    .pin10(nCLR), .pin11(GCLK), .pin12(nR), .pin13(nWE), .pin14(U17_pin9), .pin15(BUS7), .pin16(1'b1));  // open: pin9
  Seven_Seg_Hex seven_seg_hex_12 (.d({AC3, AC2, AC1, AC0}), .dp(1'b0));
  // _62256 U20: pin names not known; wires that end beside it: AD14, AD12, AD7, AD6, AD5, AD4, AD3, AD2, AD1, AD0, BUS8, BUS9, 1'b1, nWE, AD13, AD8, AD9, AD11, READ, AD10, in_8, BUS15
  // _62256 U21: pin names not known; wires that end beside it: BUS10, 1'b0, AD14, AD12, AD7, AD6, AD5, AD4, AD3, AD2, AD1, AD0, BUS0, BUS1, BUS2, 1'b0, 1'b1, nWE, AD13, AD8, AD9, AD11, READ, AD10, in_8, BUS7
  _74138 U1 (
    .pin1(in_4), .pin2(in_5), .pin3(in_6), .pin4(1'b0), .pin5(1'b0), .pin6(1'b1), .pin7(nJMP), .pin8(1'b0),
    .pin9(ST), .pin10(SUB), .pin11(ADD), .pin12(XOR), .pin13(OR), .pin14(AND), .pin15(LOAD), .pin16(1'b1));
  nand nand_2 (nand_2_out, PCout, PC_Cin);
  xor xor_1 (xor_1_out, PCout, PC_Cin);
  xor xor_2 (xor_2_out, JMP, 1'b1);
  PullUp pullup_1 (.out(nF7));
  DiodeBackward diodebackward_1 (.in(LOAD), .out(nF6));
  PullUp pullup_2 (.out(nF5));
  PullUp pullup_3 (.out(nF6));
  DiodeBackward diodebackward_2 (.in(LOAD), .out(nF5));
  DiodeBackward diodebackward_3 (.in(ADD), .out(nF5));
  DiodeBackward diodebackward_4 (.in(SUB), .out(nF5));
  DiodeBackward diodebackward_5 (.in(nJMP), .out(nF5));
  xor xor_3 (xor_3_out, nand_2_out, 1'b1);
  xor xor_4 (xor_4_out, nRES_COUNT, xor_2_out);
  PullUp pullup_4 (.out(nF4));
  DiodeBackward diodebackward_6 (.in(SUB), .out(nF3));
  DiodeBackward diodebackward_7 (.in(SUB), .out(nF4));
  nand nand_3 (nand_3_out, xor_1_out, xor_4_out);
  nand nand_4 (nand_4_out, xor_2_out, Bout);
  PullUp pullup_5 (.out(nF3));
  PullUp pullup_6 (.out(nF2));
  PullUp pullup_7 (.out(nF1));
  DiodeBackward diodebackward_8 (.in(AND), .out(nF1));
  DiodeBackward diodebackward_9 (.in(OR), .out(nF1));
  nand nand_5 (PCin, nand_3_out, nand_4_out);
  PullUp pullup_8 (.out(nF0));
  DiodeBackward diodebackward_10 (.in(LOAD), .out(nF0));
  DiodeBackward diodebackward_11 (.in(OR), .out(nF0));
  DiodeBackward diodebackward_12 (.in(XOR), .out(nF0));
  DiodeBackward diodebackward_13 (.in(ADD), .out(nF0));
  DiodeBackward diodebackward_14 (.in(SUB), .out(nF0));
  DiodeBackward diodebackward_15 (.in(ST), .out(nF0));
  _74595 U23 (
    .pin1(AD14), .pin2(AD13), .pin3(AD12), .pin4(AD11), .pin5(AD10), .pin6(AD9), .pin7(AD8), .pin8(1'b0),
    .pin9(U23_pin9), .pin10(nCLR), .pin11(GCLK), .pin12(nR), .pin13(1'b0), .pin14(PCin), .pin15(AD15),
    .pin16(1'b1));
  _74595 U22 (
    .pin1(AD6), .pin2(AD5), .pin3(AD4), .pin4(AD3), .pin5(AD2), .pin6(AD1), .pin7(AD0), .pin8(1'b0),
    .pin9(PCout), .pin10(nCLR), .pin11(GCLK), .pin12(nR), .pin13(1'b0), .pin14(U23_pin9), .pin15(AD7),
    .pin16(1'b1));
  _7474 U29 (
    .pin1(1'b1), .pin2(xor_3_out), .pin3(GCLK), .pin4(nLD), .pin5(PC_Cin), .pin7(1'b0), .pin10(1'b1),
    .pin11(1'b1), .pin12(1'b1), .pin13(1'b1), .pin14(1'b1));  // open: pin6, pin8, pin9
  _74540 U2 (
    .pin1(1'b0), .pin2(nF0), .pin3(nF1), .pin4(nF2), .pin5(nF3), .pin6(nF4), .pin7(nF5), .pin8(nF6),
    .pin9(nF7), .pin10(1'b0), .pin11(nWE), .pin12(CLA), .pin13(F), .pin14(C), .pin15(nB), .pin16(nA),
    .pin17(I1), .pin18(I0), .pin19(1'b0), .pin20(1'b1));
  Reset reset_1 (.out(n2SD));
  xor xor_5 (xor_5_out, AC0, nA);
  xor xor_6 (xor_6_out, nB, Bout);
  nand nand_6 (nand_6_out, C, C);
  nand nand_7 (CLR, CLA, LD);
  nand nand_8 (nand_8_out, C, SETC);
  nand nand_9 (RST, nRES, nand_10_out);
  nand nand_10 (nand_10_out, RST, nR);
  nand nand_11 (nand_11_out, clk, clk);
  xor xor_7 (xor_7_out, xor_5_out, xor_6_out);
  nand nand_12 (nand_12_out, nand_6_out, LD);
  nand nand_13 (GCLK, RST, nand_11_out);
  xor xor_8 (xor_8_out, xor_7_out, Cin);
  nand nand_14 (nand_14_out, xor_7_out, Cin);
  nand nand_15 (nand_15_out, xor_5_out, xor_6_out);
  _7474 U9 (
    .pin1(nand_12_out), .pin2(Cout), .pin3(GCLK), .pin4(nand_8_out), .pin5(Cin), .pin7(1'b0), .pin8(nR),
    .pin9(R), .pin10(n2SD), .pin11(clk), .pin12(RCO), .pin13(1'b1), .pin14(1'b1));  // open: pin6
  _74161 U7 (
    .pin1(RST), .pin2(clk), .pin3(1'b0), .pin4(1'b0), .pin5(1'b0), .pin6(1'b0), .pin7(1'b1), .pin8(1'b0),
    .pin9(1'b1), .pin10(1'b1), .pin11(U7_pin11[3]), .pin12(U7_pin11[2]), .pin13(U7_pin11[1]),
    .pin14(U7_pin11[0]), .pin15(RCO), .pin16(1'b1));
  nand nand_16 (nand_16_out, nand_14_out, nand_15_out);
  Monoflop monoflop_1 (.C(nLD), .R(1'b0), .Q(SETC), .nQ(nRES));
  Monoflop monoflop_2 (.C(button_1_out), .R(1'b0), .Q(LD), .nQ(nLD));
  Button button_1 (.out(button_1_out));
  nand nand_17 (nand_17_out, xor_8_out, I0);
  nand nand_18 (nand_18_out, I1, nand_16_out);
  nand nand_19 (nand_19_out, nand_16_out, F);
  nand nand_20 (Cout, nand_19_out, nand_19_out);
  Monoflop monoflop_3 (.C(RESET_2_out), .R(1'b0), .nQ(nCLR));  // open: Q
  Button RESET_2 (.out(RESET_2_out));
  Seven_Seg_Hex seven_seg_hex_13 (.d(U7_pin11), .dp(1'b0));
  nand nand_21 (Fout, nand_17_out, nand_18_out);

  // Other names for the same wires on the sheet: Aout = AC0; nCE = in_8; nOE = READ; T0 = nR; nRRES = nCLR

  // Notes on the sheet:
  //   nRES_COUNT: default 1
  //   JMP: default 1
  //   clk: Hz: 2147483647
  //   READ: default 1
  //   in_8: default 1
  //   Main Registers & RAM (8 ICs)
  //   RAM ADDRESS
  //   U19C
  //   Zero Detect
  //   16 bit Accumulator A
  //   RAM Address Register
  //   BUS DATA
  //   S1     S0       MODE
  //   0          0       HOLD
  //   0          1       RIGHT
  //   1          0       LEFT
  //   1          1       LOAD
  //   Bus Read Register B
  //   ACCUMULATOR
  //   BUS Write Register
  //   RAM HI
  //   RAM LO
  //   PC UNIT (8 ICs)
  //   U28A
  //   U27A
  //   U27D
  //   F
  //   CLA
  //   U27C
  //   U27B
  //   Carry is only set before Bit 0 of an operation
  //   C
  //   U28C
  //   U28B
  //   ~B
  //   I1
  //   ~A
  //   U28D
  //   I0
  //   LOAD
  //   AND
  //   OR
  //   XOR
  //   ADD
  //   SUB
  //   STORE
  //   JMP
  //   PC Carry  and Zero FF
  //   Program Counter
  //   Clock Sequencer (5 ICs)
  //   Bit Serial ALU (5 ICs)
  //   Carry is only set before Bit 0
  //   of an operation. 
  //   Any residual carry is cleared
  //   before an operation
  //   Carry FF
  //   U9, U10, U11, U12, U13
  //   Clock Sequencer
  //   Suppress Carry
  //   # Clock
endmodule
