// Digital circuit Spider_RAM_system_2.dig as structural Verilog
module Spider_RAM_system_2 (
  input  nRES_COUNT,
  input  JMP,
  input  clk,
  input  READ,
  input  in_5,
  input  WRITE
);

  wire AD0, AD1, AD2, AD3, AD4, AD5, AD6, AD7, AD8, AD9, AD10, AD11, AD12, AD13, AD14, AD15, AD_Cin, ADin,
       ADout, Bout, BUS0, BUS1, BUS2, BUS3, BUS4, BUS5, BUS6, BUS7, BUS8, BUS9, BUS10, BUS11, BUS12, BUS13,
       BUS14, BUS15, button_1_out, GCLK, LD, n2SD, nand_1_out, nand_2_out, nand_3_out, nand_6_out,
       nand_7_out, nCLR, nLD, nR, nRES, R, RCO, RESET_2_out, RST, SETC, U3_pin9, U17_pin9, U23_pin9,
       xor_1_out, xor_2_out, xor_3_out, xor_4_out;
  wire [3:0] U7_pin11;

  Seven_Seg_Hex seven_seg_hex_1 (.d({AD15, AD14, AD13, AD12}), .dp(1'b0));
  _74165 U3 (
    .pin1(nLD), .pin2(GCLK), .pin3(BUS11), .pin4(BUS10), .pin5(BUS9), .pin6(BUS8), .pin8(1'b0),
    .pin9(U3_pin9), .pin10(1'b0), .pin11(BUS15), .pin12(BUS14), .pin13(BUS13), .pin14(BUS12), .pin15(1'b0),
    .pin16(1'b1));  // open: pin7
  _74165 U4 (
    .pin1(nLD), .pin2(GCLK), .pin3(BUS3), .pin4(BUS2), .pin5(BUS1), .pin6(BUS0), .pin8(1'b0), .pin9(Bout),
    .pin10(U3_pin9), .pin11(BUS7), .pin12(BUS6), .pin13(BUS5), .pin14(BUS4), .pin15(1'b0), .pin16(1'b1));  // open: pin7
  Seven_Seg_Hex seven_seg_hex_2 (.d({AD11, AD10, AD9, AD8}), .dp(1'b0));
  Seven_Seg_Hex seven_seg_hex_3 (.d({AD7, AD6, AD5, AD4}), .dp(1'b0));
  Seven_Seg_Hex seven_seg_hex_4 (.d({AD3, AD2, AD1, AD0}), .dp(1'b0));
  nand nand_1 (nand_1_out, ADout, AD_Cin);
  xor xor_1 (xor_1_out, ADout, AD_Cin);
  xor xor_2 (xor_2_out, JMP, 1'b1);
  _74595 U17 (
    .pin1(BUS14), .pin2(BUS13), .pin3(BUS12), .pin4(BUS11), .pin5(BUS10), .pin6(BUS9), .pin7(BUS8),
    .pin8(1'b0), .pin9(U17_pin9), .pin10(nCLR), .pin11(GCLK), .pin12(nR), .pin13(WRITE), .pin14(ADout),
    .pin15(BUS15), .pin16(1'b1));
  _74595 U16 (
    .pin1(BUS6), .pin2(BUS5), .pin3(BUS4), .pin4(BUS3), .pin5(BUS2), .pin6(BUS1), .pin7(BUS0), .pin8(1'b0),
    .pin10(nCLR), .pin11(GCLK), .pin12(nR), .pin13(WRITE), .pin14(U17_pin9), .pin15(BUS7), .pin16(1'b1));  // open: pin9
  xor xor_3 (xor_3_out, nand_1_out, 1'b1);
  xor xor_4 (xor_4_out, nRES_COUNT, xor_2_out);
  nand nand_2 (nand_2_out, xor_1_out, xor_4_out);
  nand nand_3 (nand_3_out, xor_2_out, Bout);
  Seven_Seg_Hex seven_seg_hex_5 (.d({BUS15, BUS14, BUS13, BUS12}), .dp(1'b0));
  Seven_Seg_Hex seven_seg_hex_6 (.d({BUS11, BUS10, BUS9, BUS8}), .dp(1'b0));
  nand nand_4 (ADin, nand_2_out, nand_3_out);
  Seven_Seg_Hex seven_seg_hex_7 (.d({BUS7, BUS6, BUS5, BUS4}), .dp(1'b0));
  Seven_Seg_Hex seven_seg_hex_8 (.d({BUS3, BUS2, BUS1, BUS0}), .dp(1'b0));
  _74595 U23 (
    .pin1(AD14), .pin2(AD13), .pin3(AD12), .pin4(AD11), .pin5(AD10), .pin6(AD9), .pin7(AD8), .pin8(1'b0),
    .pin9(U23_pin9), .pin10(nCLR), .pin11(GCLK), .pin12(nR), .pin13(1'b0), .pin14(ADin), .pin15(AD15),
    .pin16(1'b1));
  _74595 U22 (
    .pin1(AD6), .pin2(AD5), .pin3(AD4), .pin4(AD3), .pin5(AD2), .pin6(AD1), .pin7(AD0), .pin8(1'b0),
    .pin9(ADout), .pin10(nCLR), .pin11(GCLK), .pin12(nR), .pin13(1'b0), .pin14(U23_pin9), .pin15(AD7),
    .pin16(1'b1));
  _7474 U29 (
    .pin1(1'b1), .pin2(xor_3_out), .pin3(GCLK), .pin4(nLD), .pin5(AD_Cin), .pin7(1'b0), .pin8(nR), .pin9(R),
    .pin10(n2SD), .pin11(clk), .pin12(RCO), .pin13(1'b1), .pin14(1'b1));  // open: pin6
  // _62256 U20: pin names not known; wires that end beside it: AD14, AD12, AD7, AD6, AD5, AD4, AD3, AD2, AD1, AD0, BUS8, BUS9, 1'b1, WRITE, AD13, AD8, AD9, AD11, READ, AD10, in_5, BUS15
  // _62256 U21: pin names not known; wires that end beside it: BUS10, 1'b0, AD14, AD12, AD7, AD6, AD5, AD4, AD3, AD2, AD1, AD0, BUS0, BUS1, BUS2, 1'b0, 1'b1, WRITE, AD13, AD8, AD9, AD11, READ, AD10, in_5, BUS7
  Reset reset_1 (.out(n2SD));
  nand nand_5 (RST, nRES, nand_6_out);
  nand nand_6 (nand_6_out, RST, nR);
  nand nand_7 (nand_7_out, clk, clk);
  nand nand_8 (GCLK, RST, nand_7_out);
  _74161 U7 (
    .pin1(RST), .pin2(clk), .pin3(1'b0), .pin4(1'b0), .pin5(1'b0), .pin6(1'b0), .pin7(1'b1), .pin8(1'b0),
    .pin9(1'b1), .pin10(1'b1), .pin11(U7_pin11[3]), .pin12(U7_pin11[2]), .pin13(U7_pin11[1]),
    .pin14(U7_pin11[0]), .pin15(RCO), .pin16(1'b1));
  Monoflop monoflop_1 (.C(nLD), .R(1'b0), .Q(SETC), .nQ(nRES));
  Monoflop monoflop_2 (.C(button_1_out), .R(1'b0), .Q(LD), .nQ(nLD));
  Button button_1 (.out(button_1_out));
  Monoflop monoflop_3 (.C(RESET_2_out), .R(1'b0), .nQ(nCLR));  // open: Q
  Button RESET_2 (.out(RESET_2_out));
  Seven_Seg_Hex seven_seg_hex_9 (.d(U7_pin11), .dp(1'b0));

  // Other names for the same wires on the sheet: nCE = in_5; nOE = READ; T0 = nR; nRRES = nCLR; nWE = WRITE

  // Notes on the sheet:
  //   nRES_COUNT: default 1
  //   JMP: default 1
  //   clk: Hz: 2147483647
  //   READ: default 1
  //   in_5: default 1
  //   RAM Registers & RAM (11 ICs)
  //   RAM ADDRESS
  //   Bus Read Register B
  //   U28A
  //   U27A
  //   U27D
  //   U27C
  //   U27B
  //   U28C
  //   U28B
  //   Carry is only set before Bit 0 of an operation
  //   BUS DATA
  //   BUS Write Register
  //   U28D
  //   S1     S0       MODE
  //   0          0       HOLD
  //   0          1       RIGHT
  //   1          0       LEFT
  //   1          1       LOAD
  //   Address Counter
  //   RAM HI
  //   RAM LO
  //   Clock Sequencer (5 ICs)
  //   Single STep
  //   Clock Sequencer
  //   # Clock
endmodule
