// Digital circuit Spider_ROMless_2.dig as structural Verilog
module Spider_ROMless_2 (
  input  nRES_COUNT,
  input  JMP,
  input  clk,
  input  in_5,
  input  in_6,
  input  in_7,
  input  READ,
  input  in_9,
  input  in_10,
  input  nCS,
  input  nWE,
  input  A0,
  input  A1,
  input  A2,
  input  A3,
  input  in_17,
  input  in_18,
  input  in_19,
  input  nRES_COUNT_2,
  input  JMP_2,
  output GCLK
);

  wire A0_t, A1_t, A2_t, A3_t, A4, A5, A6, A7, A8, A9, A10, A11, A12, A13, A14, A15, AC0, AC1, AC2, AC3, AC4,
       AC5, AC6, AC7, AC8, AC9, AC10, AC11, AC12, AC13, AC14, AC15, ADD, AND, Bout, BUS0, BUS1, BUS2, BUS3,
       BUS4, BUS5, BUS6, BUS7, BUS8, BUS9, BUS10, BUS11, BUS12, BUS13, BUS14, BUS15, C, Cin, CLA, CLR, Cout,
       D0, D1, D2, D3, D4, D5, D6, D7, D8, D9, D10, D11, D12, D13, D14, D15, F, Fout, GATE, HOLD, I0, I1, LD,
       LOAD, MR, n2SD, nA, nand_2_out, nand_3_out, nand_4_out, nand_5_out, nand_6_out, nand_7_out,
       nand_13_out, nand_14_out, nand_16_out, nand_17_out, nand_18_out, nand_19_out, nand_22_out,
       nand_23_out, nand_24_out, nand_25_out, nB, nCLR, nF0, nF1, nF2, nF3, nF4, nF5, nF6, nF7, nGATE, nHOLD,
       nJMP, nLD, not_1_out, nR, nRES, nSET, OR, PC_Cin, PCin, PCout, pulldown_1_out, R, RCO, RESET_2_out,
       SETC, ST, SUB, T2, T3, T4, T6, T7, T8, T9, U3_pin9, U5_2_pin9, U17_pin9, U23_pin9, U25_pin9, XOR,
       xor_1_out, xor_2_out, xor_3_out, xor_4_out, xor_5_out, xor_6_out, xor_7_out, xor_8_out, xor_9_out,
       xor_10_out, xor_11_out, xor_12_out;
  wire [3:0] U17_2_pin11;

  _74573 _74573_1 (
    .pin1(in_10), .pin2(BUS15), .pin3(BUS14), .pin4(BUS13), .pin5(BUS12), .pin6(BUS11), .pin7(BUS10),
    .pin8(BUS9), .pin9(BUS8), .pin10(1'b0), .pin11(T2), .pin12(A8), .pin13(A9), .pin14(A10), .pin15(A11),
    .pin16(A12), .pin17(A13), .pin18(A14), .pin19(A15), .pin20(1'b1));
  _74573 _74573_2 (
    .pin1(in_10), .pin2(BUS7), .pin3(BUS6), .pin4(BUS5), .pin5(BUS4), .pin6(BUS3), .pin7(BUS2), .pin8(BUS1),
    .pin9(BUS0), .pin10(1'b0), .pin11(T2), .pin12(A0_t), .pin13(A1_t), .pin14(A2_t), .pin15(A3_t),
    .pin16(A4), .pin17(A5), .pin18(A6), .pin19(A7), .pin20(1'b1));
  Seven_Seg_Hex seven_seg_hex_1 (.d({A15, A14, A13, A12}), .dp(1'b0));
  Seven_Seg_Hex seven_seg_hex_2 (.d({A11, A10, A9, A8}), .dp(1'b0));
  // NAnd nand_1 has open pins: In_1=pulldown_1_out, In_2=pulldown_1_out, out=open
  _74164 U5 (
    .pin1(1'b1), .pin2(Fout), .pin3(AC15), .pin4(AC14), .pin5(AC13), .pin6(AC12), .pin7(1'b0), .pin8(GCLK),
    .pin9(nCLR), .pin10(AC11), .pin11(AC10), .pin12(AC9), .pin13(AC8), .pin14(1'b1));
  Seven_Seg_Hex seven_seg_hex_3 (.d({A7, A6, A5, A4}), .dp(1'b0));
  PullDown pulldown_1 (.out(pulldown_1_out));
  _74595 U25 (
    .pin1(D14), .pin2(D13), .pin3(D12), .pin4(D11), .pin5(D10), .pin6(D9), .pin7(D8), .pin8(1'b0),
    .pin9(U25_pin9), .pin10(nRES), .pin11(GCLK), .pin12(LD), .pin13(nWE), .pin14(Fout), .pin15(D15),
    .pin16(1'b1));
  Seven_Seg_Hex seven_seg_hex_4 (.d({A3_t, A2_t, A1_t, A0_t}), .dp(1'b0));
  DiodeForward diodeforward_1 (.in(AC0), .out(pulldown_1_out));
  DiodeForward diodeforward_2 (.in(AC1), .out(pulldown_1_out));
  DiodeForward diodeforward_3 (.in(AC2), .out(pulldown_1_out));
  DiodeForward diodeforward_4 (.in(AC3), .out(pulldown_1_out));
  DiodeForward diodeforward_5 (.in(AC4), .out(pulldown_1_out));
  DiodeForward diodeforward_6 (.in(AC5), .out(pulldown_1_out));
  DiodeForward diodeforward_7 (.in(AC6), .out(pulldown_1_out));
  DiodeForward diodeforward_8 (.in(AC7), .out(pulldown_1_out));
  DiodeForward diodeforward_9 (.in(AC8), .out(pulldown_1_out));
  DiodeForward diodeforward_10 (.in(AC9), .out(pulldown_1_out));
  DiodeForward diodeforward_11 (.in(AC10), .out(pulldown_1_out));
  DiodeForward diodeforward_12 (.in(AC11), .out(pulldown_1_out));
  DiodeForward diodeforward_13 (.in(AC12), .out(pulldown_1_out));
  DiodeForward diodeforward_14 (.in(AC13), .out(pulldown_1_out));
  DiodeForward diodeforward_15 (.in(AC14), .out(pulldown_1_out));
  DiodeForward diodeforward_16 (.in(AC15), .out(pulldown_1_out));
  Seven_Seg_Hex seven_seg_hex_5 (.d({BUS15, BUS14, BUS13, BUS12}), .dp(1'b0));
  _74165 U3 (
    .pin1(nLD), .pin2(GCLK), .pin3(BUS11), .pin4(BUS10), .pin5(BUS9), .pin6(BUS8), .pin8(1'b0),
    .pin9(U3_pin9), .pin10(1'b0), .pin11(BUS15), .pin12(BUS14), .pin13(BUS13), .pin14(BUS12), .pin15(1'b0),
    .pin16(1'b1));  // open: pin7
  _74165 U4 (
    .pin1(nLD), .pin2(GCLK), .pin3(BUS3), .pin4(BUS2), .pin5(BUS1), .pin6(BUS0), .pin8(1'b0), .pin9(Bout),
    .pin10(U3_pin9), .pin11(BUS7), .pin12(BUS6), .pin13(BUS5), .pin14(BUS4), .pin15(1'b0), .pin16(1'b1));  // open: pin7
  _74164 U6 (
    .pin1(1'b1), .pin2(AC8), .pin3(AC7), .pin4(AC6), .pin5(AC5), .pin6(AC4), .pin7(1'b0), .pin8(GCLK),
    .pin9(nCLR), .pin10(AC3), .pin11(AC2), .pin12(AC1), .pin13(AC0), .pin14(1'b1));
  Seven_Seg_Hex seven_seg_hex_6 (.d({BUS11, BUS10, BUS9, BUS8}), .dp(1'b0));
  Seven_Seg_Hex seven_seg_hex_7 (.d({BUS7, BUS6, BUS5, BUS4}), .dp(1'b0));
  _74595 U24 (
    .pin1(D6), .pin2(D5), .pin3(D4), .pin4(D3), .pin5(D2), .pin6(D1), .pin7(D0), .pin8(1'b0), .pin10(nRES),
    .pin11(GCLK), .pin12(LD), .pin13(nWE), .pin14(U25_pin9), .pin15(D7), .pin16(1'b1));  // open: pin9
  _74219 _74219_1 (
    .pin1(A0), .pin2(nCS), .pin3(nWE), .pin4(D12), .pin5(BUS12), .pin6(D13), .pin7(BUS13), .pin8(1'b0),
    .pin9(BUS14), .pin10(D14), .pin11(BUS15), .pin12(D15), .pin13(A3), .pin14(A2), .pin15(A1), .pin16(1'b1));
  Seven_Seg_Hex seven_seg_hex_8 (.d({BUS3, BUS2, BUS1, BUS0}), .dp(1'b0));
  Seven_Seg_Hex seven_seg_hex_9 (.d({AC15, AC14, AC13, AC12}), .dp(1'b0));
  Seven_Seg_Hex seven_seg_hex_10 (.d({AC11, AC10, AC9, AC8}), .dp(1'b0));
  Seven_Seg_Hex seven_seg_hex_11 (.d({AC7, AC6, AC5, AC4}), .dp(1'b0));
  _74595 U17 (
    .pin1(BUS14), .pin2(BUS13), .pin3(BUS12), .pin4(BUS11), .pin5(BUS10), .pin6(BUS9), .pin7(BUS8),
    .pin8(1'b0), .pin9(U17_pin9), .pin10(nCLR), .pin11(GCLK), .pin12(nR), .pin13(nWE), .pin14(Fout),
    .pin15(BUS15), .pin16(1'b1));
  _74595 U16 (
    .pin1(BUS6), .pin2(BUS5), .pin3(BUS4), .pin4(BUS3), .pin5(BUS2), .pin6(BUS1), .pin7(BUS0), .pin8(1'b0),
    .pin10(nCLR), .pin11(GCLK), .pin12(nR), .pin13(nWE), .pin14(U17_pin9), .pin15(BUS7), .pin16(1'b1));  // open: pin9
  Seven_Seg_Hex seven_seg_hex_12 (.d({AC3, AC2, AC1, AC0}), .dp(1'b0));
  _74219 _74219_2 (
    .pin1(A0), .pin2(nCS), .pin3(nWE), .pin4(D8), .pin5(BUS8), .pin6(D9), .pin7(BUS9), .pin8(1'b0),
    .pin9(BUS10), .pin10(D10), .pin11(BUS11), .pin12(D11), .pin13(A3), .pin14(A2), .pin15(A1), .pin16(1'b1));
  // _62256 U20: pin names not known; wires that end beside it: A14, A12, A7, A6, A5, A4, A3_t, A2_t, A1_t, A0_t, BUS8, BUS9, 1'b1, nWE, A13, A8, A9, A11, READ, A10, in_9, BUS15
  // _62256 U21: pin names not known; wires that end beside it: BUS10, 1'b0, A14, A12, A7, A6, A5, A4, A3_t, A2_t, A1_t, A0_t, BUS0, BUS1, BUS2, 1'b0, 1'b1, nWE, A13, A8, A9, A11, READ, A10, in_9, BUS7
  _74219 _74219_3 (
    .pin1(A0), .pin2(nCS), .pin3(nWE), .pin4(D4), .pin5(BUS4), .pin6(D5), .pin7(BUS5), .pin8(1'b0),
    .pin9(BUS6), .pin10(D6), .pin11(BUS7), .pin12(D7), .pin13(A3), .pin14(A2), .pin15(A1), .pin16(1'b1));
  _74138 U1 (
    .pin1(in_5), .pin2(in_6), .pin3(in_7), .pin4(1'b0), .pin5(1'b0), .pin6(1'b1), .pin7(nJMP), .pin8(1'b0),
    .pin9(ST), .pin10(SUB), .pin11(ADD), .pin12(XOR), .pin13(OR), .pin14(AND), .pin15(LOAD), .pin16(1'b1));
  nand nand_2 (nand_2_out, PCout, PC_Cin);
  xor xor_1 (xor_1_out, PCout, PC_Cin);
  xor xor_2 (xor_2_out, JMP_2, 1'b1);
  _74219 _74219_4 (
    .pin1(A0), .pin2(nCS), .pin3(nWE), .pin4(D0), .pin5(BUS0), .pin6(D1), .pin7(BUS1), .pin8(1'b0),
    .pin9(BUS2), .pin10(D2), .pin11(BUS3), .pin12(D3), .pin13(A3), .pin14(A2), .pin15(A1), .pin16(1'b1));
  // _27C1024 U24_2: pin names not known; wires that end beside it: 1'b1, 1'b0, BUS15, BUS14, BUS13, BUS12, BUS11, BUS10, BUS9, BUS8, 1'b0, BUS7, BUS6, BUS5, BUS4, BUS3, 1'b1, A15, A14, A13, A12, A11, A10, A9
  nand nand_3 (nand_3_out, PCout, PC_Cin);
  xor xor_3 (xor_3_out, PCout, PC_Cin);
  xor xor_4 (xor_4_out, JMP, 1'b1);
  xor xor_5 (xor_5_out, nRES_COUNT_2, xor_2_out);
  PullUp pullup_1 (.out(nF7));
  DiodeBackward diodebackward_1 (.in(LOAD), .out(nF6));
  xor xor_6 (xor_6_out, nand_2_out, 1'b1);
  PullUp pullup_2 (.out(nF5));
  PullUp pullup_3 (.out(nF6));
  DiodeBackward diodebackward_2 (.in(LOAD), .out(nF5));
  DiodeBackward diodebackward_3 (.in(ADD), .out(nF5));
  DiodeBackward diodebackward_4 (.in(SUB), .out(nF5));
  DiodeBackward diodebackward_5 (.in(nJMP), .out(nF5));
  xor xor_7 (xor_7_out, nand_3_out, 1'b1);
  xor xor_8 (xor_8_out, nRES_COUNT, xor_4_out);
  nand nand_4 (nand_4_out, xor_1_out, xor_5_out);
  nand nand_5 (nand_5_out, xor_2_out, Bout);
  PullUp pullup_4 (.out(nF4));
  DiodeBackward diodebackward_6 (.in(SUB), .out(nF3));
  DiodeBackward diodebackward_7 (.in(SUB), .out(nF4));
  nand nand_6 (nand_6_out, xor_3_out, xor_8_out);
  nand nand_7 (nand_7_out, xor_4_out, Bout);
  _74165 U5_2 (
    .pin1(nLD), .pin2(GCLK), .pin3(BUS11), .pin4(BUS10), .pin5(BUS9), .pin6(BUS8), .pin8(1'b0),
    .pin9(U5_2_pin9), .pin10(1'b0), .pin11(BUS15), .pin12(BUS14), .pin13(BUS13), .pin14(BUS12), .pin15(1'b0),
    .pin16(1'b1));  // open: pin7
  _74165 U6_2 (
    .pin1(nLD), .pin2(GCLK), .pin3(BUS3), .pin4(BUS2), .pin5(BUS1), .pin6(BUS0), .pin8(1'b0), .pin9(Bout),
    .pin10(U5_2_pin9), .pin11(BUS7), .pin12(BUS6), .pin13(BUS5), .pin14(BUS4), .pin15(1'b0), .pin16(1'b1));  // open: pin7
  PullUp pullup_5 (.out(nF3));
  nand nand_8 (PCin, nand_4_out, nand_5_out);
  PullUp pullup_6 (.out(nF2));
  PullUp pullup_7 (.out(nF1));
  DiodeBackward diodebackward_8 (.in(AND), .out(nF1));
  DiodeBackward diodebackward_9 (.in(OR), .out(nF1));
  nand nand_9 (PCin, nand_6_out, nand_7_out);
  PullUp pullup_8 (.out(nF0));
  DiodeBackward diodebackward_10 (.in(LOAD), .out(nF0));
  DiodeBackward diodebackward_11 (.in(OR), .out(nF0));
  DiodeBackward diodebackward_12 (.in(XOR), .out(nF0));
  DiodeBackward diodebackward_13 (.in(ADD), .out(nF0));
  DiodeBackward diodebackward_14 (.in(SUB), .out(nF0));
  DiodeBackward diodebackward_15 (.in(ST), .out(nF0));
  _7474 U2 (
    .pin1(1'b1), .pin2(xor_6_out), .pin3(GCLK), .pin4(nLD), .pin5(PC_Cin), .pin7(1'b0), .pin10(1'b1),
    .pin11(1'b1), .pin12(1'b1), .pin13(1'b1), .pin14(1'b1));  // open: pin6, pin8, pin9
  _74595 U23 (
    .pin1(A14), .pin2(A13), .pin3(A12), .pin4(A11), .pin5(A10), .pin6(A9), .pin7(A8), .pin8(1'b0),
    .pin9(U23_pin9), .pin10(nCLR), .pin11(GCLK), .pin12(nR), .pin13(1'b0), .pin14(PCin), .pin15(A15),
    .pin16(1'b1));
  _74595 U22 (
    .pin1(A6), .pin2(A5), .pin3(A4), .pin4(A3_t), .pin5(A2_t), .pin6(A1_t), .pin7(A0_t), .pin8(1'b0),
    .pin9(PCout), .pin10(nCLR), .pin11(GCLK), .pin12(nR), .pin13(1'b0), .pin14(U23_pin9), .pin15(A7),
    .pin16(1'b1));
  _7474 U29 (
    .pin1(1'b1), .pin2(xor_7_out), .pin3(GCLK), .pin4(nLD), .pin5(PC_Cin), .pin7(1'b0), .pin10(1'b1),
    .pin11(1'b1), .pin12(1'b1), .pin13(1'b1), .pin14(1'b1));  // open: pin6, pin8, pin9
  _74540 U2_2 (
    .pin1(1'b0), .pin2(nF0), .pin3(nF1), .pin4(nF2), .pin5(nF3), .pin6(nF4), .pin7(nF5), .pin8(nF6),
    .pin9(nF7), .pin10(1'b0), .pin11(nWE), .pin12(CLA), .pin13(F), .pin14(C), .pin15(nB), .pin16(nA),
    .pin17(I1), .pin18(I0), .pin19(1'b0), .pin20(1'b1));
  Reset reset_1 (.out(n2SD));
  not not_1 (not_1_out, MR);
  not not_2 (nSET, T2);
  not not_3 (nRES, SETC);
  not not_4 (nLD, LD);
  nand nand_10 (GATE, nSET, nGATE);
  nand nand_11 (nGATE, GATE, nR);
  nand nand_12 (GCLK, GATE, nand_13_out);
  nand nand_13 (nand_13_out, clk, clk);
  xor xor_9 (xor_9_out, AC0, nA);
  xor xor_10 (xor_10_out, nB, Bout);
  nand nand_14 (nand_14_out, C, C);
  nand nand_15 (CLR, CLA, LD);
  nand nand_16 (nand_16_out, C, SETC);
  xor xor_11 (xor_11_out, xor_9_out, xor_10_out);
  nand nand_17 (nand_17_out, nand_14_out, LD);
  xor xor_12 (xor_12_out, xor_11_out, Cin);
  nand nand_18 (nand_18_out, xor_11_out, Cin);
  nand nand_19 (nand_19_out, xor_9_out, xor_10_out);
  _7474 U9 (
    .pin1(nand_17_out), .pin2(Cout), .pin3(GCLK), .pin4(nand_16_out), .pin5(Cin), .pin7(1'b0), .pin8(nR),
    .pin9(R), .pin10(n2SD), .pin11(clk), .pin12(RCO), .pin13(1'b1), .pin14(1'b1));  // open: pin6
  nand nand_20 (HOLD, nGATE, nHOLD);
  nand nand_21 (nHOLD, HOLD, nR);
  nand nand_22 (nand_22_out, nand_18_out, nand_19_out);
  _744017 U16_2 (
    .pin1(MR), .pin2(SETC), .pin3(LD), .pin4(T2), .pin5(T6), .pin6(T7), .pin7(T3), .pin8(1'b0), .pin9(T8),
    .pin10(T4), .pin11(T9), .pin13(HOLD), .pin14(clk), .pin15(MR), .pin16(1'b1));  // open: pin12
  _74161 U17_2 (
    .pin1(GATE), .pin2(clk), .pin3(1'b0), .pin4(1'b0), .pin5(1'b0), .pin6(1'b0), .pin7(1'b1), .pin8(1'b0),
    .pin9(1'b1), .pin10(1'b1), .pin11(U17_2_pin11[3]), .pin12(U17_2_pin11[2]), .pin13(U17_2_pin11[1]),
    .pin14(U17_2_pin11[0]), .pin15(RCO), .pin16(1'b1));
  nand nand_23 (nand_23_out, xor_12_out, I0);
  nand nand_24 (nand_24_out, I1, nand_22_out);
  nand nand_25 (nand_25_out, nand_22_out, F);
  nand nand_26 (Cout, nand_25_out, nand_25_out);
  Monoflop monoflop_1 (.C(RESET_2_out), .R(1'b0), .nQ(nCLR));  // open: Q
  Button RESET_2 (.out(RESET_2_out));
  nand nand_27 (Fout, nand_23_out, nand_24_out);
  Seven_Seg_Hex seven_seg_hex_13 (.d(U17_2_pin11), .dp(1'b0));

  // Other names for the same wires on the sheet: AD0 = A0_t; AD1 = A1_t; AD2 = A2_t; AD3 = A3_t; AD4 = A4; AD5 = A5;
  //   AD6 = A6; AD7 = A7; AD8 = A8; AD9 = A9; AD10 = A10; AD11 = A11; AD12 = A12; AD13 = A13; AD14 = A14; AD15 = A15;
  //   Aout = AC0; DN = in_18; nAEN = GATE; nCE = in_9; nOE = READ; nRRES = nCLR; RES = in_19; T0 = LD; T1 = SETC;
  //   T5 = MR; UP = in_17

  // Notes on the sheet:
  //   nRES_COUNT: default 1
  //   JMP: default 1
  //   clk: Hz: 20
  //   READ: default 1
  //   in_9: default 1
  //   nWE: default 1
  //   nRES_COUNT_2: default 1
  //   JMP_2: default 1
  //   Main Registers & RAM (8 ICs)
  //   RAM ADDRESS
  //   U19C
  //   Zero Detect
  //   16 bit Accumulator A
  //   RAM Address Register
  //   BUS DATA
  //   S1     S0       MODE
  //   0          0       HOLD
  //   0          1       RIGHT
  //   1          0       LEFT
  //   1          1       LOAD
  //   Bus Read Register B
  //   ACCUMULATOR
  //   BUS Write Register
  //   RAM HI
  //   RAM LO
  //   PC UNIT (8 ICs)
  //   U16A
  //   U17A
  //   U17D
  //   U28A
  //   U27A
  //   U27D
  //   U17B
  //   Carry is only set before Bit 0 of an operation
  //   16-bit ROM
  //   U17C
  //   F
  //   CLA
  //   U27C
  //   U27B
  //   U16C
  //   U16B
  //   C
  //   U28C
  //   U28B
  //   ~B
  //   U16D
  //   I1
  //   ~A
  //   U28D
  //   I0
  //   LOAD
  //   AND
  //   OR
  //   XOR
  //   ADD
  //   SUB
  //   STORE
  //   JMP
  //   PC Carry  FF
  //   PC Carry  and Zero FF
  //   Program Counter
  //   Clock Sequencer (5 ICs)
  //   U11
  //   Bit Serial ALU (5 ICs)
  //   Carry is only set before Bit 0
  //   of an operation. 
  //   Any residual carry is cleared
  //   before an operation
  //   Carry FF
  //   U19
  //   U9, U10, U11, U12, U13
  //   Suppress Carry
  //   # Clock
endmodule
