// Digital circuit Spider_clock_sequencer.dig as structural Verilog
module Spider_clock_sequencer (
  input  clk,
  output nLD,
  output nSET,
  output nRES,
  output GCLK
);

  wire _744017_1_pin2, _744017_1_pin3, button_1_out, LD, MR, nand_2_out, nand_4_out, nCLR, nCLRPC, nPCRES,
       RES, RESET_out, SETC, U7_pin15;

  Monoflop Mono2 (.C(nLD), .R(1'b0), .Q(SETC), .nQ(nSET));
  Monoflop Mono1 (.C(button_1_out), .R(1'b0), .Q(LD), .nQ(nLD));
  Button button_1 (.out(button_1_out));
  Monoflop monoflop_1 (.C(RESET_out), .R(1'b0), .Q(nCLRPC), .nQ(nPCRES));
  Button RESET (.out(RESET_out));
  nand nand_1 (nCLR, nSET, nand_2_out);
  nand nand_2 (nand_2_out, nCLR, nRES);
  nand nand_3 (GCLK, nCLR, nand_4_out);
  nand nand_4 (nand_4_out, clk, clk);
  _74161 U7 (
    .pin1(nCLR), .pin2(clk), .pin3(1'b0), .pin4(1'b0), .pin5(1'b0), .pin6(1'b0), .pin7(1'b1), .pin8(1'b0),
    .pin9(1'b1), .pin10(1'b1), .pin15(U7_pin15), .pin16(1'b1));  // open: pin11, pin12, pin13, pin14
  _7474 U9 (
    .pin1(1'b1), .pin2(U7_pin15), .pin3(clk), .pin4(1'b1), .pin5(RES), .pin6(nRES), .pin7(1'b0),
    .pin10(1'b1), .pin11(1'b1), .pin12(1'b1), .pin13(1'b1), .pin14(1'b1));  // open: pin8, pin9
  _744017 _744017_1 (
    .pin2(_744017_1_pin2), .pin3(_744017_1_pin3), .pin4(MR), .pin8(1'b0), .pin13(1'b0), .pin14(clk),
    .pin15(MR), .pin16(1'b1));  // open: pin1, pin5, pin6, pin7, pin9, pin10, pin11, pin12

  // Notes on the sheet:
  //   Sequencer
  //   STEP/RUN
  //   U14
  //   U8
  //   Clock Sequencer
  //   U13
  //   Carry FF
endmodule
