// Digital circuit Spider_hack_core_1.dig as structural Verilog
module Spider_hack_core_1 (
  input  clk,
  input  in_3,
  input  in_4,
  input  in_5,
  output Fout,
  output nLDB,
  output out_7,
  output SETC,
  output RES,
  output RUN,
  output T0,
  output GCLK,
  output RST,
  output CLK_2
);

  wire AC0, AC1, AC2, AC3, AC4, AC5, AC6, AC7, AC8, AC9, AC10, AC11, AC12, AC13, AC14, AC15, ADD, AND, Bout,
       BUS0, BUS1, BUS2, BUS3, BUS4, BUS5, BUS6, BUS7, BUS12, BUS13, BUS14, BUS15, button_2_out, C, Cin, CL0,
       CL1, CL2, CL3, CLA, CLR, Cout, D8, D9, D10, D11, diodeforward_1_out, F, F0, F1, F2, F3, F4, F5, F6,
       I0, I1, IX, LOAD, nA, nand_2_out, nand_3_out, nand_5_out, nand_7_out, nand_8_out, nand_10_out,
       nand_11_out, nand_12_out, nand_13_out, nand_14_out, nand_15_out, nB, nCLRPC, nJMP, nZERO, OR, ST, SUB,
       U3_pin9, U7_pin15, XOR, xor_1_out, xor_2_out, xor_3_out, xor_4_out;

  _74165 U3 (
    .pin1(out_7), .pin2(GCLK), .pin3(D11), .pin4(D10), .pin5(D9), .pin6(D8), .pin8(1'b0), .pin9(U3_pin9),
    .pin10(1'b0), .pin11(BUS15), .pin12(BUS14), .pin13(BUS13), .pin14(BUS12), .pin15(1'b0), .pin16(1'b1));  // open: pin7
  _74165 U4 (
    .pin1(out_7), .pin2(GCLK), .pin3(BUS3), .pin4(BUS2), .pin5(BUS1), .pin6(BUS0), .pin8(1'b0), .pin9(Bout),
    .pin10(U3_pin9), .pin11(BUS7), .pin12(BUS6), .pin13(BUS5), .pin14(BUS4), .pin15(1'b0), .pin16(1'b1));  // open: pin7
  _74164 U5 (
    .pin1(1'b1), .pin2(Fout), .pin3(AC15), .pin4(AC14), .pin5(AC13), .pin6(AC12), .pin7(1'b0), .pin8(GCLK),
    .pin9(CLR), .pin10(AC11), .pin11(AC10), .pin12(AC9), .pin13(AC8), .pin14(1'b1));
  Seven_Seg_Hex seven_seg_hex_1 (.d({AC15, AC14, AC13, AC12}), .dp(1'b0));
  Seven_Seg_Hex seven_seg_hex_2 (.d({AC11, AC10, AC9, AC8}), .dp(1'b0));
  Seven_Seg_Hex seven_seg_hex_3 (.d({AC7, AC6, AC5, AC4}), .dp(1'b0));
  Seven_Seg_Hex seven_seg_hex_4 (.d({AC3, AC2, AC1, AC0}), .dp(1'b0));
  _74164 U6 (
    .pin1(1'b1), .pin2(AC8), .pin3(AC7), .pin4(AC6), .pin5(AC5), .pin6(AC4), .pin7(1'b0), .pin8(GCLK),
    .pin9(CLR), .pin10(AC3), .pin11(AC2), .pin12(AC1), .pin13(AC0), .pin14(1'b1));
  Monoflop monoflop_1 (.C(RUN), .R(1'b0), .Q(nLDB), .nQ(out_7));
  Button button_1 (.out(RUN));
  DiodeForward diodeforward_1 (.in(AC15), .out(diodeforward_1_out));
  DiodeForward diodeforward_2 (.in(AC14), .out(diodeforward_1_out));
  DiodeForward diodeforward_3 (.in(AC13), .out(diodeforward_1_out));
  DiodeForward diodeforward_4 (.in(AC12), .out(diodeforward_1_out));
  DiodeForward diodeforward_5 (.in(AC11), .out(diodeforward_1_out));
  DiodeForward diodeforward_6 (.in(AC10), .out(diodeforward_1_out));
  DiodeForward diodeforward_7 (.in(AC9), .out(diodeforward_1_out));
  DiodeForward diodeforward_8 (.in(AC8), .out(diodeforward_1_out));
  DiodeForward diodeforward_9 (.in(AC7), .out(diodeforward_1_out));
  DiodeForward diodeforward_10 (.in(AC6), .out(diodeforward_1_out));
  DiodeForward diodeforward_11 (.in(AC5), .out(diodeforward_1_out));
  DiodeForward diodeforward_12 (.in(AC4), .out(diodeforward_1_out));
  DiodeForward diodeforward_13 (.in(AC3), .out(diodeforward_1_out));
  DiodeForward diodeforward_14 (.in(AC2), .out(diodeforward_1_out));
  DiodeForward diodeforward_15 (.in(AC1), .out(diodeforward_1_out));
  DiodeForward diodeforward_16 (.in(AC0), .out(diodeforward_1_out));
  Monoflop monoflop_2 (.C(out_7), .R(1'b0), .Q(SETC), .nQ(RES));
  LED led_1 (.in(diodeforward_1_out));
  PullDown pulldown_1 (.out(diodeforward_1_out));
  nand nand_1 (nZERO, diodeforward_1_out, diodeforward_1_out);
  Monoflop monoflop_3 (.C(button_2_out), .R(1'b0), .nQ(nCLRPC));  // open: Q
  Button button_2 (.out(button_2_out));
  nand nand_2 (nand_2_out, SETC, C);
  nand nand_3 (nand_3_out, C, C);
  nand nand_4 (CLR, CLA, nLDB);
  _74138 U1 (
    .pin1(in_3), .pin2(in_4), .pin3(in_5), .pin4(1'b0), .pin5(1'b0), .pin6(1'b1), .pin7(nJMP), .pin8(1'b0),
    .pin9(ST), .pin10(SUB), .pin11(ADD), .pin12(XOR), .pin13(OR), .pin14(AND), .pin15(LOAD), .pin16(1'b1));
  nand nand_5 (nand_5_out, clk, clk);
  nand nand_6 (RST, RES, nand_7_out);
  nand nand_7 (nand_7_out, RST, T0);
  xor xor_1 (xor_1_out, AC0, nA);
  xor xor_2 (xor_2_out, nB, Bout);
  nand nand_8 (nand_8_out, nand_3_out, nLDB);
  DiodeBackward diodebackward_1 (.in(LOAD), .out(F6));
  PullUp pullup_1 (.out(F6));
  DiodeBackward diodebackward_2 (.in(LOAD), .out(F5));
  DiodeBackward diodebackward_3 (.in(ADD), .out(F5));
  DiodeBackward diodebackward_4 (.in(SUB), .out(F5));
  DiodeBackward diodebackward_5 (.in(nJMP), .out(F5));
  nand nand_9 (GCLK, nand_5_out, RST);
  xor xor_3 (xor_3_out, xor_1_out, xor_2_out);
  PullUp pullup_2 (.out(F4));
  PullUp pullup_3 (.out(F5));
  DiodeBackward diodebackward_6 (.in(SUB), .out(F4));
  Seven_Seg_Hex seven_seg_hex_5 (.d({CL3, CL2, CL1, CL0}), .dp(1'b0));
  PullUp pullup_4 (.out(F3));
  DiodeBackward diodebackward_7 (.in(SUB), .out(F3));
  xor xor_4 (xor_4_out, xor_3_out, Cin);
  nand nand_10 (nand_10_out, xor_3_out, Cin);
  nand nand_11 (nand_11_out, xor_1_out, xor_2_out);
  PullUp pullup_5 (.out(F2));
  DiodeBackward diodebackward_8 (.in(AND), .out(F1));
  DiodeBackward diodebackward_9 (.in(OR), .out(F1));
  _74161 U7 (
    .pin1(RST), .pin2(clk), .pin3(1'b0), .pin4(1'b0), .pin5(1'b0), .pin6(1'b0), .pin7(1'b1), .pin8(1'b0),
    .pin9(1'b1), .pin10(1'b1), .pin11(CL3), .pin12(CL2), .pin13(CL1), .pin14(CL0), .pin15(U7_pin15),
    .pin16(1'b1));
  PullUp pullup_6 (.out(F1));
  PullUp pullup_7 (.out(F0));
  DiodeBackward diodebackward_10 (.in(LOAD), .out(F0));
  DiodeBackward diodebackward_11 (.in(OR), .out(F0));
  DiodeBackward diodebackward_12 (.in(XOR), .out(F0));
  DiodeBackward diodebackward_13 (.in(ADD), .out(F0));
  DiodeBackward diodebackward_14 (.in(SUB), .out(F0));
  DiodeBackward diodebackward_15 (.in(ST), .out(F0));
  nand nand_12 (nand_12_out, nand_10_out, nand_11_out);
  nand nand_13 (nand_13_out, xor_4_out, I0);
  nand nand_14 (nand_14_out, I1, nand_12_out);
  nand nand_15 (nand_15_out, nand_12_out, F);
  _74540 U2 (
    .pin1(1'b0), .pin2(F0), .pin3(F1), .pin4(F2), .pin5(F3), .pin6(F4), .pin7(F5), .pin8(F6), .pin9(1'b0),
    .pin10(1'b0), .pin12(CLA), .pin13(F), .pin14(C), .pin15(nB), .pin16(nA), .pin17(I1), .pin18(I0),
    .pin19(1'b0), .pin20(1'b1));  // open: pin11
  _7474 U8 (
    .pin1(1'b1), .pin2(U7_pin15), .pin3(clk), .pin4(1'b1), .pin5(IX), .pin6(T0), .pin7(1'b0), .pin9(Cin),
    .pin10(nand_2_out), .pin11(GCLK), .pin12(Cout), .pin13(nand_8_out), .pin14(1'b1));  // open: pin8
  nand nand_16 (Fout, nand_13_out, nand_14_out);
  nand nand_17 (Cout, nand_15_out, nand_15_out);

  assign CLK_2 = clk;

  // Other names for the same wires on the sheet: Aout = AC0; LDA = nLDB; nLDB_t = out_7

  // Notes on the sheet:
  //   clk: Hz: 2147483647
  //   spider000
  //   Spider 000 Bit serial CPU Testbed
  //   16 bit Shift Register B
  //   16 bit Shift Register A
  //   ACCUMULATOR
  //   STEP/RUN
  //   Instruction Input
  //   CLR PC
  //   000 LOAD
  //   001 AND
  //   010 OR
  //   011 XOR
  //   100 ADD
  //   101 SUB
  //   110 STORE
  //   111 JUMP
  //   CLR ACC
  //   CLA
  //   # Clock
  //   Carry is only set before Bit 0 of an operation
  //   Any residual carry is cleared before an operation
  //   C
  //   F
  //   ~B
  //   ~A
  //   I0
  //   I1
  //   Clock Sequencer
  //   LOAD
  //   AND
  //   OR
  //   XOR
  //   ADD
  //   SUB
  //   STORE
  //   JMP
  //   Instruction Decode
  //   Suppress Carry
  //   Carry FF
endmodule
