// Digital circuit Spider_with 4017_clock_sequencer.dig as structural Verilog
module Spider_with_4017_clock_sequencer (
  input  nRES_COUNT,
  input  JMP,
  input  in_3,
  input  in_4,
  input  clk,
  input  in_11,
  input  in_12,
  input  in_13,
  input  in_14,
  input  in_15,
  input  in_16,
  input  in_17,
  input  in_19,
  output GCLK,
  output P1,
  output P0,
  output P3,
  output P4,
  output P2
);

  wire _10_out, _11_out, _12_out, _13_out, _14_out, _15_out, _16_out, _17_out, _18_out, _19_out,
       _74173_4_pin11, _74173_4_pin12, _74173_4_pin13, _74173_4_pin14, _74540_1_pin11, _74540_1_pin12,
       _74540_1_pin13, _74540_1_pin14, _74540_1_pin15, _74540_1_pin16, _74540_1_pin17, A0, A1, A2, A3, A4,
       A5, A6, A7, A8, A9, A10, A11, A12, A13, A14, A15, A_out, AC0, AC1, AC2, AC3, AC4, AC5, AC6, AC7, AC8,
       AC9, AC10, AC11, AC12, AC13, AC14, AC15, AD0, AD1, AD2, AD3, AD4, AD5, AD6, AD7, AD8, AD9, AD10, AD11,
       AD12, AD13, AD14, AD15, ADD, Address_out, ADin, ADout, ALU, ALU_to_RAM_out, AND, B_out, Bout, BUS0,
       BUS1, BUS2, BUS3, BUS4, BUS5, BUS6, BUS7, BUS8, BUS9, BUS10, BUS11, BUS12, BUS13, BUS14, BUS15, C,
       C_out, Cin, CLA, Clear_out, CLR, Cout, D_out, Dec_out, Deposit_nWR_out, diodebackward_1_out,
       diodebackward_3_out, diodebackward_8_out, diodebackward_12_out, diodebackward_23_out,
       diodebackward_38_out, DN, Dout, E_out, Examine_nRD_out, F, F_out, Fout, GATE, HOLD, I0, I1, Inc_out,
       Kout, LD, LOAD, MR, MUXout, n2SD, nA, nALB, nand_4_out, nand_5_out, nand_6_out, nand_11_out,
       nand_12_out, nand_14_out, nand_15_out, nand_16_out, nand_17_out, nand_20_out, nand_21_out,
       nand_22_out, nand_23_out, nB, nCLR, nDE, nF0, nF1, nF2, nF3, nF4, nF5, nF6, nF7, nGATE, nHOLD, nJMP,
       nLATCH, nLOAD, nOE, not_3_out, not_9_out, not_10_out, nR, nWE, OR, PC_Cin, PCin, PCout,
       pulldown_1_out, pullup_2_out, pullup_3_out, pullup_6_out, pullup_7_out, pullup_9_out, pullup_10_out,
       pullup_13_out, R, R0, R1, R2, R3, R4, R5, R6, R7, R8, R9, R10, R11, R12, R13, R14, R15, RCO, RES,
       RESET_2_out, S0, S1, S2, S3, S4, S5, S6, S7, S8, S9, S10, S11, S12, S13, S14, S15, SETC, ST, SUB, T2,
       T3, T4, T6, T7, T8, T9, U2_pin11, U3_pin9, U17_pin18, U19_pin14, U23_pin9, U25_pin9, U27_pin9, UP,
       XOR, xor_2_out, xor_3_out, xor_4_out, xor_5_out, xor_6_out, xor_7_out, xor_8_out, xor_9_out;
  wire [3:0] U17_2_pin11;

  DiodeBackward diodebackward_1 (.in(Address_out), .out(diodebackward_1_out));
  PullUp pullup_1 (.out(diodebackward_1_out));
  PullUp pullup_2 (.out(pullup_2_out));
  DiodeBackward diodebackward_2 (.in(Dec_out), .out(pullup_2_out));
  not not_1 (nLOAD, _74540_1_pin11);
  _74139 _74139_1 (
    .pin1(1'b1), .pin2(1'b1), .pin3(1'b1), .pin8(1'b0), .pin11(nALB), .pin12(nDE), .pin13(1'b0), .pin14(ALU),
    .pin15(nWE), .pin16(1'b1));  // open: pin4, pin5, pin6, pin7, pin9, pin10
  PullUp pullup_3 (.out(pullup_3_out));
  DiodeBackward diodebackward_3 (.in(ALU_to_RAM_out), .out(diodebackward_3_out));
  DiodeBackward diodebackward_4 (.in(Examine_nRD_out), .out(diodebackward_3_out));
  DiodeBackward diodebackward_5 (.in(Dec_out), .out(diodebackward_3_out));
  DiodeBackward diodebackward_6 (.in(Inc_out), .out(pullup_3_out));
  DiodeBackward diodebackward_7 (.in(Inc_out), .out(diodebackward_3_out));
  _74165 U27 (
    .pin1(P0), .pin2(GCLK), .pin3(S11), .pin4(S10), .pin5(S9), .pin6(S8), .pin8(1'b0), .pin9(U27_pin9),
    .pin10(1'b0), .pin11(S15), .pin12(S14), .pin13(S13), .pin14(S12), .pin15(1'b0), .pin16(1'b1));  // open: pin7
  PullUp pullup_4 (.out(diodebackward_3_out));
  DiodeBackward diodebackward_8 (.in(Examine_nRD_out), .out(diodebackward_8_out));
  DiodeBackward diodebackward_9 (.in(Deposit_nWR_out), .out(diodebackward_8_out));
  not not_2 (ALU, _74540_1_pin15);
  PullUp pullup_5 (.out(diodebackward_8_out));
  PullUp pullup_6 (.out(pullup_6_out));
  DiodeBackward diodebackward_10 (.in(ALU_to_RAM_out), .out(pullup_6_out));
  DiodeBackward diodebackward_11 (.in(Deposit_nWR_out), .out(pullup_6_out));
  not not_3 (not_3_out, _74540_1_pin17);
  not not_4 (nWE, _74540_1_pin16);
  nand nand_1 (UP, _74540_1_pin13, _74540_1_pin14);
  nand nand_2 (DN, _74540_1_pin12, _74540_1_pin14);
  PullUp pullup_7 (.out(pullup_7_out));
  DiodeBackward diodebackward_12 (.in(Clear_out), .out(diodebackward_12_out));
  DiodeBackward diodebackward_13 (.in(Examine_nRD_out), .out(pullup_7_out));
  PullUp pullup_8 (.out(diodebackward_12_out));
  _74540 _74540_1 (
    .pin1(1'b0), .pin2(diodebackward_12_out), .pin3(pullup_7_out), .pin4(pullup_6_out),
    .pin5(diodebackward_8_out), .pin6(diodebackward_3_out), .pin7(pullup_3_out), .pin8(pullup_2_out),
    .pin9(diodebackward_1_out), .pin10(1'b0), .pin11(_74540_1_pin11), .pin12(_74540_1_pin12),
    .pin13(_74540_1_pin13), .pin14(_74540_1_pin14), .pin15(_74540_1_pin15), .pin16(_74540_1_pin16),
    .pin17(_74540_1_pin17), .pin18(RES), .pin19(1'b0), .pin20(1'b1));
  Button #(.activeLow("true")) ALU_to_RAM (.out(ALU_to_RAM_out));
  Button #(.activeLow("true")) Clear (.out(Clear_out));
  Button #(.activeLow("true")) Examine_nRD (.out(Examine_nRD_out));
  Button #(.activeLow("true")) Deposit_nWR (.out(Deposit_nWR_out));
  Button #(.activeLow("true")) Dec (.out(Dec_out));
  Button #(.activeLow("true")) Inc (.out(Inc_out));
  Button #(.activeLow("true")) Address (.out(Address_out));
  nand nand_3 (nOE, not_3_out, in_19);
  _74173 _74173_1 (
    .pin1(1'b0), .pin2(1'b0), .pin3(S12), .pin4(S13), .pin5(S14), .pin6(S15), .pin7(nLATCH), .pin8(1'b0),
    .pin9(1'b0), .pin10(1'b0), .pin11(S11), .pin12(S10), .pin13(S9), .pin14(S8), .pin15(RES), .pin16(1'b1));
  _74165 U28 (
    .pin1(P0), .pin2(GCLK), .pin3(S3), .pin4(S2), .pin5(S1), .pin6(S0), .pin8(1'b0), .pin9(Kout),
    .pin10(U27_pin9), .pin11(S7), .pin12(S6), .pin13(S5), .pin14(S4), .pin15(1'b0), .pin16(1'b1));  // open: pin7
  _74173 _74173_2 (
    .pin1(1'b0), .pin2(1'b0), .pin3(S8), .pin4(S9), .pin5(S10), .pin6(S11), .pin7(nLATCH), .pin8(1'b0),
    .pin9(1'b0), .pin10(1'b0), .pin11(S7), .pin12(S6), .pin13(S5), .pin14(S4), .pin15(RES), .pin16(1'b1));
  Button #(.activeLow("true")) u_C (.out(C_out));
  Button #(.activeLow("true")) _18 (.out(_18_out));
  Button #(.activeLow("true")) _14 (.out(_14_out));
  Button #(.activeLow("true")) _10 (.out(_10_out));
  Seven_Seg_Hex seven_seg_hex_1 (.d({S15, S14, S13, S12}), .dp(1'b0));
  Seven_Seg_Hex seven_seg_hex_2 (.d({S11, S10, S9, S8}), .dp(1'b0));
  Button #(.activeLow("true")) D (.out(D_out));
  Button #(.activeLow("true")) _19 (.out(_19_out));
  Button #(.activeLow("true")) _15 (.out(_15_out));
  Button #(.activeLow("true")) _11 (.out(_11_out));
  Seven_Seg_Hex seven_seg_hex_3 (.d({S7, S6, S5, S4}), .dp(1'b0));
  _74173 _74173_3 (
    .pin1(1'b0), .pin2(1'b0), .pin3(S4), .pin4(S5), .pin5(S6), .pin6(S7), .pin7(nLATCH), .pin8(1'b0),
    .pin9(1'b0), .pin10(1'b0), .pin11(S3), .pin12(S2), .pin13(S1), .pin14(S0), .pin15(RES), .pin16(1'b1));
  Seven_Seg_Hex seven_seg_hex_4 (.d({S3, S2, S1, S0}), .dp(1'b0));
  Button #(.activeLow("true")) E (.out(E_out));
  Button #(.activeLow("true")) A (.out(A_out));
  Button #(.activeLow("true")) _16 (.out(_16_out));
  Button #(.activeLow("true")) _12 (.out(_12_out));
  Button #(.activeLow("true")) u_F (.out(F_out));
  Button #(.activeLow("true")) B (.out(B_out));
  Button #(.activeLow("true")) _17 (.out(_17_out));
  Button #(.activeLow("true")) _13 (.out(_13_out));
  _74173 _74173_4 (
    .pin1(1'b0), .pin2(1'b0), .pin3(S0), .pin4(S1), .pin5(S2), .pin6(S3), .pin7(nLATCH), .pin8(1'b0),
    .pin9(1'b0), .pin10(1'b0), .pin11(_74173_4_pin11), .pin12(_74173_4_pin12), .pin13(_74173_4_pin13),
    .pin14(_74173_4_pin14), .pin15(RES), .pin16(1'b1));
  PullUp pullup_9 (.out(pullup_9_out));
  DiodeBackward diodebackward_14 (.in(F_out), .out(pullup_9_out));
  DiodeBackward diodebackward_15 (.in(E_out), .out(pullup_9_out));
  DiodeBackward diodebackward_16 (.in(D_out), .out(pullup_9_out));
  DiodeBackward diodebackward_17 (.in(C_out), .out(pullup_9_out));
  DiodeBackward diodebackward_18 (.in(B_out), .out(pullup_9_out));
  DiodeBackward diodebackward_19 (.in(A_out), .out(pullup_9_out));
  DiodeBackward diodebackward_20 (.in(_19_out), .out(pullup_9_out));
  DiodeBackward diodebackward_21 (.in(_18_out), .out(pullup_9_out));
  not not_5 (_74173_4_pin11, pullup_9_out);
  PullUp pullup_10 (.out(pullup_10_out));
  DiodeBackward diodebackward_22 (.in(F_out), .out(pullup_10_out));
  DiodeBackward diodebackward_23 (.in(F_out), .out(diodebackward_23_out));
  DiodeBackward diodebackward_24 (.in(E_out), .out(pullup_10_out));
  DiodeBackward diodebackward_25 (.in(E_out), .out(diodebackward_23_out));
  DiodeBackward diodebackward_26 (.in(D_out), .out(pullup_10_out));
  DiodeBackward diodebackward_27 (.in(C_out), .out(pullup_10_out));
  DiodeBackward diodebackward_28 (.in(B_out), .out(diodebackward_23_out));
  DiodeBackward diodebackward_29 (.in(A_out), .out(diodebackward_23_out));
  DiodeBackward diodebackward_30 (.in(_17_out), .out(pullup_10_out));
  DiodeBackward diodebackward_31 (.in(_17_out), .out(diodebackward_23_out));
  DiodeBackward diodebackward_32 (.in(_16_out), .out(pullup_10_out));
  DiodeBackward diodebackward_33 (.in(_16_out), .out(diodebackward_23_out));
  DiodeBackward diodebackward_34 (.in(_15_out), .out(pullup_10_out));
  DiodeBackward diodebackward_35 (.in(_14_out), .out(pullup_10_out));
  DiodeBackward diodebackward_36 (.in(_13_out), .out(diodebackward_23_out));
  DiodeBackward diodebackward_37 (.in(_12_out), .out(diodebackward_23_out));
  not not_6 (_74173_4_pin12, pullup_10_out);
  PullUp pullup_11 (.out(diodebackward_23_out));
  DiodeBackward diodebackward_38 (.in(F_out), .out(diodebackward_38_out));
  DiodeBackward diodebackward_39 (.in(D_out), .out(diodebackward_38_out));
  DiodeBackward diodebackward_40 (.in(B_out), .out(diodebackward_38_out));
  DiodeBackward diodebackward_41 (.in(_19_out), .out(diodebackward_38_out));
  DiodeBackward diodebackward_42 (.in(_17_out), .out(diodebackward_38_out));
  DiodeBackward diodebackward_43 (.in(_15_out), .out(diodebackward_38_out));
  DiodeBackward diodebackward_44 (.in(_13_out), .out(diodebackward_38_out));
  DiodeBackward diodebackward_45 (.in(_11_out), .out(diodebackward_38_out));
  not not_7 (_74173_4_pin13, diodebackward_23_out);
  PullUp pullup_12 (.out(diodebackward_38_out));
  PullUp pullup_13 (.out(pullup_13_out));
  DiodeBackward diodebackward_46 (.in(F_out), .out(pullup_13_out));
  DiodeBackward diodebackward_47 (.in(E_out), .out(pullup_13_out));
  DiodeBackward diodebackward_48 (.in(D_out), .out(pullup_13_out));
  DiodeBackward diodebackward_49 (.in(C_out), .out(pullup_13_out));
  DiodeBackward diodebackward_50 (.in(B_out), .out(pullup_13_out));
  DiodeBackward diodebackward_51 (.in(A_out), .out(pullup_13_out));
  DiodeBackward diodebackward_52 (.in(_19_out), .out(pullup_13_out));
  DiodeBackward diodebackward_53 (.in(_18_out), .out(pullup_13_out));
  DiodeBackward diodebackward_54 (.in(_17_out), .out(pullup_13_out));
  DiodeBackward diodebackward_55 (.in(_16_out), .out(pullup_13_out));
  DiodeBackward diodebackward_56 (.in(_15_out), .out(pullup_13_out));
  DiodeBackward diodebackward_57 (.in(_14_out), .out(pullup_13_out));
  DiodeBackward diodebackward_58 (.in(_13_out), .out(pullup_13_out));
  DiodeBackward diodebackward_59 (.in(_12_out), .out(pullup_13_out));
  DiodeBackward diodebackward_60 (.in(_11_out), .out(pullup_13_out));
  DiodeBackward diodebackward_61 (.in(_10_out), .out(pullup_13_out));
  not not_8 (_74173_4_pin14, diodebackward_38_out);
  not not_9 (not_9_out, pullup_13_out);
  Monoflop monoflop_1 (.C(not_9_out), .R(1'b0), .Q(nLATCH));  // open: nQ
  // XOr xor_1 has open pins: In_1=pulldown_1_out, In_2=1'b1, out=open
  PullDown pulldown_1 (.out(pulldown_1_out));
  _74138 U1 (
    .pin1(in_11), .pin2(in_12), .pin3(in_13), .pin4(1'b0), .pin5(1'b0), .pin6(1'b1), .pin7(nJMP),
    .pin8(1'b0), .pin9(ST), .pin10(SUB), .pin11(ADD), .pin12(XOR), .pin13(OR), .pin14(AND), .pin15(LOAD),
    .pin16(1'b1));
  DiodeForward diodeforward_1 (.in(AC0), .out(pulldown_1_out));
  DiodeForward diodeforward_2 (.in(AC1), .out(pulldown_1_out));
  DiodeForward diodeforward_3 (.in(AC2), .out(pulldown_1_out));
  DiodeForward diodeforward_4 (.in(AC3), .out(pulldown_1_out));
  DiodeForward diodeforward_5 (.in(AC4), .out(pulldown_1_out));
  DiodeForward diodeforward_6 (.in(AC5), .out(pulldown_1_out));
  DiodeForward diodeforward_7 (.in(AC6), .out(pulldown_1_out));
  DiodeForward diodeforward_8 (.in(AC7), .out(pulldown_1_out));
  DiodeForward diodeforward_9 (.in(AC8), .out(pulldown_1_out));
  DiodeForward diodeforward_10 (.in(AC9), .out(pulldown_1_out));
  DiodeForward diodeforward_11 (.in(AC10), .out(pulldown_1_out));
  DiodeForward diodeforward_12 (.in(AC11), .out(pulldown_1_out));
  DiodeForward diodeforward_13 (.in(AC12), .out(pulldown_1_out));
  DiodeForward diodeforward_14 (.in(AC13), .out(pulldown_1_out));
  DiodeForward diodeforward_15 (.in(AC14), .out(pulldown_1_out));
  DiodeForward diodeforward_16 (.in(AC15), .out(pulldown_1_out));
  Seven_Seg_Hex seven_seg_hex_5 (.d({AD15, AD14, AD13, AD12}), .dp(1'b0));
  Seven_Seg_Hex seven_seg_hex_6 (.d({AD11, AD10, AD9, AD8}), .dp(1'b0));
  _74164 U5 (
    .pin1(1'b1), .pin2(Fout), .pin3(AC15), .pin4(AC14), .pin5(AC13), .pin6(AC12), .pin7(1'b0), .pin8(GCLK),
    .pin9(nCLR), .pin10(AC11), .pin11(AC10), .pin12(AC9), .pin13(AC8), .pin14(1'b1));
  PullUp pullup_14 (.out(nF7));
  DiodeBackward diodebackward_62 (.in(LOAD), .out(nF6));
  Seven_Seg_Hex seven_seg_hex_7 (.d({AD7, AD6, AD5, AD4}), .dp(1'b0));
  PullUp pullup_15 (.out(nF6));
  DiodeBackward diodebackward_63 (.in(LOAD), .out(nF5));
  DiodeBackward diodebackward_64 (.in(ADD), .out(nF5));
  DiodeBackward diodebackward_65 (.in(SUB), .out(nF5));
  DiodeBackward diodebackward_66 (.in(nJMP), .out(nF5));
  Seven_Seg_Hex seven_seg_hex_8 (.d({AD3, AD2, AD1, AD0}), .dp(1'b0));
  _74595 U19 (
    .pin1(AD6), .pin2(AD5), .pin3(AD4), .pin4(AD3), .pin5(AD2), .pin6(AD1), .pin7(AD0), .pin8(1'b0),
    .pin9(ADout), .pin10(nCLR), .pin11(GCLK), .pin12(nR), .pin13(1'b0), .pin14(U19_pin14), .pin15(AD7),
    .pin16(1'b1));
  _74595 U18 (
    .pin1(AD14), .pin2(AD13), .pin3(AD12), .pin4(AD11), .pin5(AD10), .pin6(AD9), .pin7(AD8), .pin8(1'b0),
    .pin9(U19_pin14), .pin10(nCLR), .pin11(GCLK), .pin12(nR), .pin13(1'b0), .pin14(ADin), .pin15(AD15),
    .pin16(1'b1));
  PullUp pullup_16 (.out(nF4));
  PullUp pullup_17 (.out(nF5));
  DiodeBackward diodebackward_67 (.in(SUB), .out(nF4));
  PullUp pullup_18 (.out(nF3));
  DiodeBackward diodebackward_68 (.in(SUB), .out(nF3));
  Seven_Seg_Hex seven_seg_hex_9 (.d({BUS15, BUS14, BUS13, BUS12}), .dp(1'b0));
  _74165 U3 (
    .pin1(P0), .pin2(GCLK), .pin3(BUS11), .pin4(BUS10), .pin5(BUS9), .pin6(BUS8), .pin8(1'b0),
    .pin9(U3_pin9), .pin10(1'b0), .pin11(BUS15), .pin12(BUS14), .pin13(BUS13), .pin14(BUS12), .pin15(1'b0),
    .pin16(1'b1));  // open: pin7
  _74165 U4 (
    .pin1(P0), .pin2(GCLK), .pin3(BUS3), .pin4(BUS2), .pin5(BUS1), .pin6(BUS0), .pin8(1'b0), .pin9(Bout),
    .pin10(U3_pin9), .pin11(BUS7), .pin12(BUS6), .pin13(BUS5), .pin14(BUS4), .pin15(1'b0), .pin16(1'b1));  // open: pin7
  _74164 U6 (
    .pin1(1'b1), .pin2(AC8), .pin3(AC7), .pin4(AC6), .pin5(AC5), .pin6(AC4), .pin7(1'b0), .pin8(GCLK),
    .pin9(nCLR), .pin10(AC3), .pin11(AC2), .pin12(AC1), .pin13(AC0), .pin14(1'b1));
  PullUp pullup_19 (.out(nF2));
  DiodeBackward diodebackward_69 (.in(AND), .out(nF1));
  DiodeBackward diodebackward_70 (.in(OR), .out(nF1));
  Seven_Seg_Hex seven_seg_hex_10 (.d({BUS11, BUS10, BUS9, BUS8}), .dp(1'b0));
  PullUp pullup_20 (.out(nF1));
  PullUp pullup_21 (.out(nF0));
  DiodeBackward diodebackward_71 (.in(LOAD), .out(nF0));
  DiodeBackward diodebackward_72 (.in(OR), .out(nF0));
  DiodeBackward diodebackward_73 (.in(XOR), .out(nF0));
  DiodeBackward diodebackward_74 (.in(ADD), .out(nF0));
  DiodeBackward diodebackward_75 (.in(SUB), .out(nF0));
  DiodeBackward diodebackward_76 (.in(ST), .out(nF0));
  Seven_Seg_Hex seven_seg_hex_11 (.d({BUS7, BUS6, BUS5, BUS4}), .dp(1'b0));
  Seven_Seg_Hex seven_seg_hex_12 (.d({BUS3, BUS2, BUS1, BUS0}), .dp(1'b0));
  Seven_Seg_Hex seven_seg_hex_13 (.d({AC15, AC14, AC13, AC12}), .dp(1'b0));
  Seven_Seg_Hex seven_seg_hex_14 (.d({AC11, AC10, AC9, AC8}), .dp(1'b0));
  _74299 U17 (
    .pin1(in_4), .pin2(GATE), .pin3(GATE), .pin4(BUS6), .pin5(BUS4), .pin6(BUS2), .pin7(BUS0), .pin9(1'b1),
    .pin10(1'b0), .pin11(1'b0), .pin12(GCLK), .pin13(BUS1), .pin14(BUS3), .pin15(BUS5), .pin16(BUS7),
    .pin18(U17_pin18), .pin19(in_3), .pin20(1'b1));  // open: pin8, pin17
  _74299 U16 (
    .pin1(in_4), .pin2(GATE), .pin3(GATE), .pin4(BUS14), .pin5(BUS12), .pin6(BUS10), .pin7(BUS8),
    .pin8(U17_pin18), .pin9(1'b1), .pin10(1'b0), .pin11(1'b0), .pin12(GCLK), .pin13(BUS9), .pin14(BUS11),
    .pin15(BUS13), .pin16(BUS15), .pin18(Fout), .pin19(in_3), .pin20(1'b1));  // open: pin17
  Seven_Seg_Hex seven_seg_hex_15 (.d({AC7, AC6, AC5, AC4}), .dp(1'b0));
  _74540 U2 (
    .pin1(1'b0), .pin2(nF0), .pin3(nF1), .pin4(nF2), .pin5(nF3), .pin6(nF4), .pin7(nF5), .pin8(nF6),
    .pin9(nF7), .pin10(1'b0), .pin11(U2_pin11), .pin12(CLA), .pin13(F), .pin14(C), .pin15(nB), .pin16(nA),
    .pin17(I1), .pin18(I0), .pin19(1'b0), .pin20(1'b1));
  Seven_Seg_Hex seven_seg_hex_16 (.d({AC3, AC2, AC1, AC0}), .dp(1'b0));
  // _62256 U20: pin names not known; wires that end beside it: AD14, AD12, AD7, AD6, AD5, AD4, AD3, AD2, AD1, AD0, BUS8, BUS9, 1'b1, nWE, AD13, AD8, AD9, AD11, nOE, AD10, 1'b0, BUS15
  // _62256 U21: pin names not known; wires that end beside it: BUS10, 1'b0, AD14, AD12, AD7, AD6, AD5, AD4, AD3, AD2, AD1, AD0, BUS0, BUS1, BUS2, 1'b0, 1'b1, nWE, AD13, AD8, AD9, AD11, nOE, AD10, 1'b0, BUS7
  _74153 U14 (
    .pin1(1'b0), .pin2(in_17), .pin3(Dout), .pin4(AC0), .pin5(Bout), .pin6(ADout), .pin7(ADin), .pin8(1'b0),
    .pin10(1'b1), .pin11(1'b1), .pin12(1'b1), .pin13(1'b1), .pin14(in_16), .pin15(1'b1), .pin16(1'b1));  // open: pin9
  _74165 U25 (
    .pin1(P0), .pin2(GCLK), .pin3(R11), .pin4(R10), .pin5(R9), .pin6(R8), .pin8(1'b0), .pin9(U25_pin9),
    .pin10(1'b0), .pin11(R15), .pin12(R14), .pin13(R13), .pin14(R12), .pin15(1'b0), .pin16(1'b1));  // open: pin7
  _74165 U26 (
    .pin1(P0), .pin2(GCLK), .pin3(R3), .pin4(R2), .pin5(R1), .pin6(R0), .pin8(1'b0), .pin9(Dout),
    .pin10(U25_pin9), .pin11(R7), .pin12(R6), .pin13(R5), .pin14(R4), .pin15(1'b0), .pin16(1'b1));  // open: pin7
  Seven_Seg_Hex seven_seg_hex_17 (.d({A15, A14, A13, A12}), .dp(1'b0));
  _74153 U15 (
    .pin1(1'b0), .pin2(in_15), .pin3(Dout), .pin4(ADout), .pin5(Bout), .pin6(AC0), .pin7(MUXout),
    .pin8(1'b0), .pin10(1'b1), .pin11(1'b1), .pin12(1'b1), .pin13(1'b1), .pin14(in_14), .pin15(1'b1),
    .pin16(1'b1));  // open: pin9
  Seven_Seg_Hex seven_seg_hex_18 (.d({A11, A10, A9, A8}), .dp(1'b0));
  Seven_Seg_Hex seven_seg_hex_19 (.d({A7, A6, A5, A4}), .dp(1'b0));
  nand nand_4 (nand_4_out, PCout, PC_Cin);
  xor xor_2 (xor_2_out, PCout, PC_Cin);
  xor xor_3 (xor_3_out, JMP, 1'b1);
  Seven_Seg_Hex seven_seg_hex_20 (.d({A3, A2, A1, A0}), .dp(1'b0));
  // _27C1024 U24: pin names not known; wires that end beside it: 1'b1, 1'b0, R15, R14, R13, R12, R11, R10, R9, R8, 1'b0, R7, R6, R5, R4, R3, 1'b1, A15, A14, A13, A12, A11, A10, A9
  xor xor_4 (xor_4_out, nand_4_out, 1'b1);
  xor xor_5 (xor_5_out, nRES_COUNT, xor_3_out);
  Seven_Seg_Hex seven_seg_hex_21 (.d({R15, R14, R13, R12}), .dp(1'b0));
  Seven_Seg_Hex seven_seg_hex_22 (.d({R11, R10, R9, R8}), .dp(1'b0));
  nand nand_5 (nand_5_out, xor_2_out, xor_5_out);
  nand nand_6 (nand_6_out, xor_3_out, Dout);
  Seven_Seg_Hex seven_seg_hex_23 (.d({R7, R6, R5, R4}), .dp(1'b0));
  nand nand_7 (PCin, nand_5_out, nand_6_out);
  Seven_Seg_Hex seven_seg_hex_24 (.d({R3, R2, R1, R0}), .dp(1'b0));
  _74595 U23 (
    .pin1(A14), .pin2(A13), .pin3(A12), .pin4(A11), .pin5(A10), .pin6(A9), .pin7(A8), .pin8(1'b0),
    .pin9(U23_pin9), .pin10(nCLR), .pin11(GCLK), .pin12(nR), .pin13(1'b0), .pin14(PCin), .pin15(A15),
    .pin16(1'b1));
  _74595 U22 (
    .pin1(A6), .pin2(A5), .pin3(A4), .pin4(A3), .pin5(A2), .pin6(A1), .pin7(A0), .pin8(1'b0), .pin9(PCout),
    .pin10(nCLR), .pin11(GCLK), .pin12(nR), .pin13(1'b0), .pin14(U23_pin9), .pin15(A7), .pin16(1'b1));
  _7474 U29 (
    .pin1(1'b1), .pin2(xor_4_out), .pin3(GCLK), .pin4(P0), .pin5(PC_Cin), .pin7(1'b0), .pin10(1'b1),
    .pin11(1'b1), .pin12(1'b1), .pin13(1'b1), .pin14(1'b1));  // open: pin6, pin8, pin9
  Reset reset_1 (.out(n2SD));
  not not_10 (not_10_out, MR);
  not not_11 (P4, T4);
  not not_12 (P3, T3);
  not not_13 (P2, T2);
  not not_14 (P1, SETC);
  not not_15 (P0, LD);
  nand nand_8 (GATE, P2, nGATE);
  nand nand_9 (nGATE, GATE, nR);
  nand nand_10 (GCLK, GATE, nand_11_out);
  nand nand_11 (nand_11_out, clk, clk);
  xor xor_6 (xor_6_out, AC0, nA);
  xor xor_7 (xor_7_out, nB, MUXout);
  nand nand_12 (nand_12_out, C, C);
  nand nand_13 (CLR, CLA, LD);
  nand nand_14 (nand_14_out, C, SETC);
  xor xor_8 (xor_8_out, xor_6_out, xor_7_out);
  nand nand_15 (nand_15_out, nand_12_out, LD);
  xor xor_9 (xor_9_out, xor_8_out, Cin);
  nand nand_16 (nand_16_out, xor_8_out, Cin);
  nand nand_17 (nand_17_out, xor_6_out, xor_7_out);
  _7474 U9 (
    .pin1(nand_15_out), .pin2(Cout), .pin3(GCLK), .pin4(nand_14_out), .pin5(Cin), .pin7(1'b0), .pin8(nR),
    .pin9(R), .pin10(n2SD), .pin11(clk), .pin12(RCO), .pin13(1'b1), .pin14(1'b1));  // open: pin6
  _7474 U30 (
    .pin1(1'b1), .pin2(RCO), .pin3(clk), .pin4(n2SD), .pin5(R), .pin6(nR), .pin7(1'b0), .pin10(1'b1),
    .pin11(1'b1), .pin12(1'b1), .pin13(1'b1), .pin14(1'b1));  // open: pin8, pin9
  nand nand_18 (HOLD, nGATE, nHOLD);
  nand nand_19 (nHOLD, HOLD, nR);
  nand nand_20 (nand_20_out, nand_16_out, nand_17_out);
  _744017 U16_2 (
    .pin1(MR), .pin2(SETC), .pin3(LD), .pin4(T2), .pin5(T6), .pin6(T7), .pin7(T3), .pin8(1'b0), .pin9(T8),
    .pin10(T4), .pin11(T9), .pin13(HOLD), .pin14(clk), .pin15(MR), .pin16(1'b1));  // open: pin12
  _74161 U17_2 (
    .pin1(GATE), .pin2(clk), .pin3(1'b0), .pin4(1'b0), .pin5(1'b0), .pin6(1'b0), .pin7(1'b1), .pin8(1'b0),
    .pin9(1'b1), .pin10(1'b1), .pin11(U17_2_pin11[3]), .pin12(U17_2_pin11[2]), .pin13(U17_2_pin11[1]),
    .pin14(U17_2_pin11[0]), .pin15(RCO), .pin16(1'b1));
  nand nand_21 (nand_21_out, xor_9_out, I0);
  nand nand_22 (nand_22_out, I1, nand_20_out);
  nand nand_23 (nand_23_out, nand_20_out, F);
  nand nand_24 (Cout, nand_23_out, nand_23_out);
  Monoflop monoflop_2 (.C(RESET_2_out), .R(1'b0), .nQ(nCLR));  // open: Q
  Button RESET_2 (.out(RESET_2_out));
  nand nand_25 (Fout, nand_21_out, nand_22_out);
  Seven_Seg_Hex seven_seg_hex_25 (.d(U17_2_pin11), .dp(1'b0));

  // Other names for the same wires on the sheet: Aout = AC0; nAEN = GATE; nLD = P0; nRES = P1; nRRES = nCLR;
  //   nSET = P2; T0 = LD; T1 = SETC; T5 = MR

  // Notes on the sheet:
  //   nRES_COUNT: default 1
  //   JMP: default 1
  //   in_3: default 1
  //   clk: Hz: 1000
  //   in_19: default 1
  //   Front Panel
  //   LOAD
  //   UP
  //   DOWN
  //   ~DE
  //   COUNT
  //   WRITE
  //   Keypad read register K
  //   READ
  //   RESET
  //   Hex Keypad
  //   KEYSWITCH REGISTER
  //   KEY DATA
  //   Main Registers & RAM
  //   Instruction Decode
  //   Zero Detect
  //   U27D
  //   RAM ADDRESS
  //   16 bit Accumulator A
  //   CLA
  //   C
  //   F
  //   RAM Address Register
  //   ~B
  //   BUS DATA
  //   ~A
  //   I0
  //   I1
  //   AND
  //   OR
  //   XOR
  //   ADD
  //   SUB
  //   STORE
  //   JMP
  //   S1     S0       MODE
  //   0          0       HOLD
  //   0          1       RIGHT
  //   1          0       LEFT
  //   1          1       LOAD
  //   Memory Read Register B
  //   ACCUMULATOR
  //   BUS I/O Register
  //   Control Section
  //   RAM HI
  //   RAM LO
  //   Address Register Mux
  //   ROM & PC UNIT
  //   ROM Data Register
  //   ROM ADDRESS
  //   ALU Mux
  //   U28A
  //   U27A
  //   16-bit ROM
  //   U27C
  //   U27B
  //   ROM DATA
  //   U28C
  //   U28B
  //   Carry is only set before Bit 0 of an operation
  //   U28D
  //   PC Carry FF
  //   Program Counter
  //   Clock Sequencer
  //   U11
  //   Bit Serial ALU
  //   Carry is only set before Bit 0
  //   of an operation. 
  //   Any residualcarry is cleared
  //   before an operation
  //   Carry FF
  //   U19
  //   U9, U10, U11, U12, U13
  //   Suppress Carry
  //   # Clock
endmodule
