// Digital circuit Spider_with_299_USR.dig as structural Verilog
module Spider_with_299_USR (
  input  clk,
  input  in_2,
  input  in_3,
  input  in_4,
  input  in_5,
  input  in_6
);

  wire ADD, AND, Aout, Bout, BUS0, BUS1, BUS2, BUS3, BUS4, BUS5, BUS6, BUS7, BUS8, BUS9, BUS10, BUS11, BUS12,
       BUS13, BUS14, BUS15, button_1_out, button_2_out, button_3_out, button_4_out, button_5_out,
       button_6_out, button_7_out, button_8_out, button_9_out, button_10_out, button_11_out, button_12_out,
       button_13_out, button_14_out, button_15_out, button_16_out, button_17_out, C, Cin, CLA, CLR, Cout, D0,
       D1, D2, D3, D4, D5, D6, D7, D8, D9, D10, D11, D12, D13, D14, D15, d_ff_1_nq, d_ff_2_nq, d_ff_3_nq,
       d_ff_4_nq, d_ff_5_nq, d_ff_6_nq, d_ff_7_nq, d_ff_8_nq, d_ff_9_nq, d_ff_10_nq, d_ff_11_nq, d_ff_12_nq,
       diodebackward_5_out, diodebackward_7_out, diodebackward_8_out, F, Fout, GCLK, I0, I1, IC16_2_nq,
       IC16_nq, IC17_2_nq, IC17_nq, IX, LD, LOAD, nA, nand_1_out, nand_2_out, nand_4_out, nand_5_out,
       nand_6_out, nand_7_out, nand_8_out, nand_11_out, nand_12_out, nand_13_out, nB, nJMP, nLOAD, nRES,
       nRST, OR, pullup_1_out, pullup_2_out, pullup_3_out, pullup_6_out, pullup_7_out, RCO, RST, SETC, ST,
       SUB, T0, U2_pin11, U3_pin9, U15_2_pin18, U15_pin9, XOR, xor_1_out, xor_2_out, xor_3_out, xor_4_out;
  wire [3:0] U5_pin6, U5_pin13, U6_pin6, U15_pin3, U15_pin7, U16_pin3, U16_pin7;
  wire [3:1] U6_pin10;

  LED led_1 (.in(D15));
  D_FF IC17 (.D(IC17_nq), .C(button_1_out), .Q(D15), .nQ(IC17_nq));
  LED led_2 (.in(D14));
  D_FF d_ff_1 (.D(d_ff_1_nq), .C(button_2_out), .Q(D14), .nQ(d_ff_1_nq));
  Button button_1 (.out(button_1_out));
  LED led_3 (.in(D13));
  D_FF d_ff_2 (.D(d_ff_2_nq), .C(button_3_out), .Q(D13), .nQ(d_ff_2_nq));
  Button button_2 (.out(button_2_out));
  LED led_4 (.in(D12));
  D_FF d_ff_3 (.D(d_ff_3_nq), .C(button_4_out), .Q(D12), .nQ(d_ff_3_nq));
  Button button_3 (.out(button_3_out));
  _74595 U15 (
    .pin1(U15_pin3[2]), .pin2(U15_pin3[1]), .pin3(U15_pin3[0]), .pin4(U15_pin7[3]), .pin5(U15_pin7[2]),
    .pin6(U15_pin7[1]), .pin7(U15_pin7[0]), .pin8(1'b0), .pin9(U15_pin9), .pin10(nRES), .pin11(GCLK),
    .pin12(T0), .pin13(1'b0), .pin14(Fout), .pin15(U15_pin3[3]), .pin16(1'b1));
  LED led_5 (.in(D11));
  D_FF d_ff_4 (.D(d_ff_4_nq), .C(button_5_out), .Q(D11), .nQ(d_ff_4_nq));
  Button button_4 (.out(button_4_out));
  LED led_6 (.in(D10));
  D_FF d_ff_5 (.D(d_ff_5_nq), .C(button_6_out), .Q(D10), .nQ(d_ff_5_nq));
  Button button_5 (.out(button_5_out));
  LED led_7 (.in(D9));
  D_FF d_ff_6 (.D(d_ff_6_nq), .C(button_7_out), .Q(D9), .nQ(d_ff_6_nq));
  Button button_6 (.out(button_6_out));
  LED led_8 (.in(D8));
  D_FF IC17_2 (.D(IC17_2_nq), .C(button_8_out), .Q(D8), .nQ(IC17_2_nq));
  Button button_7 (.out(button_7_out));
  _74595 U16 (
    .pin1(U16_pin3[2]), .pin2(U16_pin3[1]), .pin3(U16_pin3[0]), .pin4(U16_pin7[3]), .pin5(U16_pin7[2]),
    .pin6(U16_pin7[1]), .pin7(U16_pin7[0]), .pin8(1'b0), .pin10(nRES), .pin11(GCLK), .pin12(T0),
    .pin13(1'b0), .pin14(U15_pin9), .pin15(U16_pin3[3]), .pin16(1'b1));  // open: pin9
  Seven_Seg_Hex seven_seg_hex_1 (.d({D15, D14, D13, D12}), .dp(1'b0));
  Button button_8 (.out(button_8_out));
  Seven_Seg_Hex seven_seg_hex_2 (.d({D11, D10, D9, D8}), .dp(1'b0));
  Seven_Seg_Hex seven_seg_hex_3 (.d({D7, D6, D5, D4}), .dp(1'b0));
  Seven_Seg_Hex seven_seg_hex_4 (.d({D3, D2, D1, D0}), .dp(1'b0));
  LED led_9 (.in(D7));
  D_FF IC16 (.D(IC16_nq), .C(button_9_out), .Q(D7), .nQ(IC16_nq));
  Seven_Seg_Hex seven_seg_hex_5 (.d(U15_pin3), .dp(1'b0));
  LED led_10 (.in(D6));
  D_FF d_ff_7 (.D(d_ff_7_nq), .C(button_10_out), .Q(D6), .nQ(d_ff_7_nq));
  Button button_9 (.out(button_9_out));
  Seven_Seg_Hex seven_seg_hex_6 (.d(U15_pin7), .dp(1'b0));
  LED led_11 (.in(D5));
  D_FF d_ff_8 (.D(d_ff_8_nq), .C(button_11_out), .Q(D5), .nQ(d_ff_8_nq));
  Button button_10 (.out(button_10_out));
  Seven_Seg_Hex seven_seg_hex_7 (.d(U16_pin3), .dp(1'b0));
  LED led_12 (.in(D4));
  D_FF d_ff_9 (.D(d_ff_9_nq), .C(button_12_out), .Q(D4), .nQ(d_ff_9_nq));
  Button button_11 (.out(button_11_out));
  Seven_Seg_Hex seven_seg_hex_8 (.d(U16_pin7), .dp(1'b0));
  LED led_13 (.in(D3));
  D_FF d_ff_10 (.D(d_ff_10_nq), .C(button_13_out), .Q(D3), .nQ(d_ff_10_nq));
  Button button_12 (.out(button_12_out));
  LED led_14 (.in(D2));
  D_FF d_ff_11 (.D(d_ff_11_nq), .C(button_14_out), .Q(D2), .nQ(d_ff_11_nq));
  Button button_13 (.out(button_13_out));
  LED led_15 (.in(D1));
  D_FF d_ff_12 (.D(d_ff_12_nq), .C(button_15_out), .Q(D1), .nQ(d_ff_12_nq));
  Button button_14 (.out(button_14_out));
  LED led_16 (.in(D0));
  D_FF IC16_2 (.D(IC16_2_nq), .C(button_16_out), .Q(D0), .nQ(IC16_2_nq));
  Button button_15 (.out(button_15_out));
  Button button_16 (.out(button_16_out));
  _74165 U3 (
    .pin1(nLOAD), .pin2(GCLK), .pin3(D11), .pin4(D10), .pin5(D9), .pin6(D8), .pin8(1'b0), .pin9(U3_pin9),
    .pin10(1'b0), .pin11(D15), .pin12(D14), .pin13(D13), .pin14(D12), .pin15(1'b0), .pin16(1'b1));  // open: pin7
  _74138 U1 (
    .pin1(in_2), .pin2(in_3), .pin3(in_4), .pin4(1'b0), .pin5(1'b0), .pin6(1'b1), .pin7(nJMP), .pin8(1'b0),
    .pin9(ST), .pin10(SUB), .pin11(ADD), .pin12(XOR), .pin13(OR), .pin14(AND), .pin15(LOAD), .pin16(1'b1));
  Monoflop Mono2 (.C(nLOAD), .R(1'b0), .Q(SETC), .nQ(nRES));
  Monoflop Mono1 (.C(button_17_out), .R(1'b0), .Q(LD), .nQ(nLOAD));
  Button button_17 (.out(button_17_out));
  _74165 U4 (
    .pin1(nLOAD), .pin2(GCLK), .pin3(D3), .pin4(D2), .pin5(D1), .pin6(D0), .pin8(1'b0), .pin9(Bout),
    .pin10(U3_pin9), .pin11(D7), .pin12(D6), .pin13(D5), .pin14(D4), .pin15(1'b0), .pin16(1'b1));  // open: pin7
  PullUp pullup_1 (.out(pullup_1_out));
  PullUp pullup_2 (.out(pullup_2_out));
  DiodeBackward diodebackward_1 (.in(LOAD), .out(pullup_1_out));
  PullUp pullup_3 (.out(pullup_3_out));
  DiodeBackward diodebackward_2 (.in(LOAD), .out(pullup_3_out));
  DiodeBackward diodebackward_3 (.in(ADD), .out(pullup_3_out));
  DiodeBackward diodebackward_4 (.in(SUB), .out(pullup_3_out));
  DiodeBackward diodebackward_5 (.in(SUB), .out(diodebackward_5_out));
  DiodeBackward diodebackward_6 (.in(nJMP), .out(pullup_3_out));
  PullUp pullup_4 (.out(diodebackward_5_out));
  DiodeBackward diodebackward_7 (.in(SUB), .out(diodebackward_7_out));
  PullUp pullup_5 (.out(diodebackward_7_out));
  PullUp pullup_6 (.out(pullup_6_out));
  PullUp pullup_7 (.out(pullup_7_out));
  DiodeBackward diodebackward_8 (.in(LOAD), .out(diodebackward_8_out));
  DiodeBackward diodebackward_9 (.in(AND), .out(pullup_7_out));
  DiodeBackward diodebackward_10 (.in(OR), .out(diodebackward_8_out));
  DiodeBackward diodebackward_11 (.in(OR), .out(pullup_7_out));
  DiodeBackward diodebackward_12 (.in(XOR), .out(diodebackward_8_out));
  DiodeBackward diodebackward_13 (.in(ADD), .out(diodebackward_8_out));
  DiodeBackward diodebackward_14 (.in(SUB), .out(diodebackward_8_out));
  DiodeBackward diodebackward_15 (.in(ST), .out(diodebackward_8_out));
  PullUp pullup_8 (.out(diodebackward_8_out));
  _74164 U5 (
    .pin1(1'b1), .pin2(Fout), .pin3(U5_pin6[3]), .pin4(U5_pin6[2]), .pin5(U5_pin6[1]), .pin6(U5_pin6[0]),
    .pin7(1'b0), .pin8(GCLK), .pin9(CLR), .pin10(U5_pin13[3]), .pin11(U5_pin13[2]), .pin12(U5_pin13[1]),
    .pin13(U5_pin13[0]), .pin14(1'b1));
  _74540 U2 (
    .pin1(1'b0), .pin2(diodebackward_8_out), .pin3(pullup_7_out), .pin4(pullup_6_out),
    .pin5(diodebackward_7_out), .pin6(diodebackward_5_out), .pin7(pullup_3_out), .pin8(pullup_1_out),
    .pin9(pullup_2_out), .pin10(1'b0), .pin11(U2_pin11), .pin12(CLA), .pin13(F), .pin14(C), .pin15(nB),
    .pin16(nA), .pin17(I1), .pin18(I0), .pin19(1'b0), .pin20(1'b1));
  Seven_Seg_Hex seven_seg_hex_9 (.d(U5_pin6), .dp(1'b0));
  Seven_Seg_Hex seven_seg_hex_10 (.d(U5_pin13), .dp(1'b0));
  xor xor_1 (xor_1_out, Aout, nA);
  xor xor_2 (xor_2_out, nB, Bout);
  Seven_Seg_Hex seven_seg_hex_11 (.d(U6_pin6), .dp(1'b0));
  nand nand_1 (nand_1_out, SETC, C);
  nand nand_2 (nand_2_out, C, C);
  nand nand_3 (CLR, CLA, LD);
  Seven_Seg_Hex seven_seg_hex_12 (.d({U6_pin10, Aout}), .dp(1'b0));
  _74164 U6 (
    .pin1(1'b1), .pin2(U5_pin13[0]), .pin3(U6_pin6[3]), .pin4(U6_pin6[2]), .pin5(U6_pin6[1]),
    .pin6(U6_pin6[0]), .pin7(1'b0), .pin8(GCLK), .pin9(CLR), .pin10(U6_pin10[3]), .pin11(U6_pin10[2]),
    .pin12(U6_pin10[1]), .pin13(Aout), .pin14(1'b1));
  nand nand_4 (nand_4_out, nand_2_out, LD);
  xor xor_3 (xor_3_out, xor_1_out, xor_2_out);
  xor xor_4 (xor_4_out, xor_3_out, Cin);
  nand nand_5 (nand_5_out, xor_3_out, Cin);
  nand nand_6 (nand_6_out, xor_1_out, xor_2_out);
  nand nand_7 (nand_7_out, nand_5_out, nand_6_out);
  nand nand_8 (nand_8_out, clk, clk);
  nand nand_9 (RST, nRES, nRST);
  nand nand_10 (nRST, RST, T0);
  nand nand_11 (nand_11_out, xor_4_out, I0);
  nand nand_12 (nand_12_out, I1, nand_7_out);
  nand nand_13 (nand_13_out, nand_7_out, F);
  nand nand_14 (GCLK, nand_8_out, RST);
  nand nand_15 (Fout, nand_11_out, nand_12_out);
  nand nand_16 (Cout, nand_13_out, nand_13_out);
  _74161 U7 (
    .pin1(RST), .pin2(clk), .pin3(1'b0), .pin4(1'b0), .pin5(1'b0), .pin6(1'b0), .pin7(1'b1), .pin8(1'b0),
    .pin9(1'b1), .pin10(1'b1), .pin15(RCO), .pin16(1'b1));  // open: pin11, pin12, pin13, pin14
  _7474 U9 (
    .pin1(nand_4_out), .pin2(Cout), .pin3(GCLK), .pin4(nand_1_out), .pin5(Cin), .pin7(1'b0), .pin8(T0),
    .pin9(IX), .pin10(1'b1), .pin11(clk), .pin12(RCO), .pin13(1'b1), .pin14(1'b1));  // open: pin6
  Seven_Seg_Hex seven_seg_hex_13 (.d({BUS15, BUS14, BUS13, BUS12}), .dp(1'b0));
  Seven_Seg_Hex seven_seg_hex_14 (.d({BUS11, BUS10, BUS9, BUS8}), .dp(1'b0));
  Seven_Seg_Hex seven_seg_hex_15 (.d({BUS7, BUS6, BUS5, BUS4}), .dp(1'b0));
  _74299 U15_2 (
    .pin1(in_6), .pin2(RST), .pin3(RST), .pin4(BUS6), .pin5(BUS4), .pin6(BUS2), .pin7(BUS0), .pin9(1'b1),
    .pin10(1'b0), .pin11(1'b0), .pin12(GCLK), .pin13(BUS1), .pin14(BUS3), .pin15(BUS5), .pin16(BUS7),
    .pin18(U15_2_pin18), .pin19(in_5), .pin20(1'b1));  // open: pin8, pin17
  _74299 U16_2 (
    .pin1(in_6), .pin2(RST), .pin3(RST), .pin4(BUS14), .pin5(BUS12), .pin6(BUS10), .pin7(BUS8),
    .pin8(U15_2_pin18), .pin9(1'b1), .pin10(1'b0), .pin11(1'b0), .pin12(GCLK), .pin13(BUS9), .pin14(BUS11),
    .pin15(BUS13), .pin16(BUS15), .pin18(Fout), .pin19(in_5), .pin20(1'b1));  // open: pin17
  Seven_Seg_Hex seven_seg_hex_16 (.d({BUS3, BUS2, BUS1, BUS0}), .dp(1'b0));

  // Notes on the sheet:
  //   clk: Hz: 2147483647
  //   in_5: default 1
  //   Front Panel
  //   ENTER H
  //   Output  Register
  //   Data Input
  //   OUTPUT REGISTER
  //   ENTER L
  //   .
  //   Instruction Input
  //   16 bit Shift Register B
  //   U14
  //   STEP/RUN
  //   CLA
  //   Instruction Decode
  //   F
  //   C
  //   ~A
  //   ~B
  //   I1
  //   I0
  //   LOAD
  //   AND
  //   OR
  //   XOR
  //   ADD
  //   SUB
  //   STORE
  //   JMP
  //   16 bit Shift Register A
  //   ACCUMULATOR
  //   Bit Serial ALU
  //   U9, U10, U11, U12, U13
  //   Carry is only set before Bit 0 of an operation
  //   Any residual carry is cleared before an operation
  //   Spider Bit Serial CPU Testbed
  //   U8
  //   Clock Sequencer
  //   Suppress Carry
  //   Carry FF
  //   S1     S0       MODE
  //   0          0       HOLD
  //   0          1       RIGHT
  //   1          0       LEFT
  //   1          1       LOAD
  //   BUS I/O Register
endmodule
