// Digital circuit Spider_with_ROM_module.dig as structural Verilog
module Spider_with_ROM_module (
  input  clk,
  input  in_2,
  input  in_3,
  input  in_4,
  input  nRES_COUNT
);

  wire A0, A1, A2, A3, A4, A5, A6, A7, A8, A9, A10, A11, A12, A13, A14, A15, ADD, AND, Aout, Bout,
       button_1_out, button_2_out, button_3_out, button_4_out, button_5_out, button_6_out, button_7_out,
       button_8_out, button_9_out, button_10_out, button_11_out, button_12_out, button_13_out, button_14_out,
       button_15_out, button_16_out, button_17_out, C, Cin, CLA, CLR, Cout, D0, D1, D2, D3, D4, D5, D6, D7,
       D8, D9, D10, D11, D12, D13, D14, D15, d_ff_1_nq, d_ff_2_nq, d_ff_3_nq, d_ff_4_nq, d_ff_5_nq,
       d_ff_6_nq, d_ff_7_nq, d_ff_8_nq, d_ff_9_nq, d_ff_10_nq, d_ff_11_nq, d_ff_12_nq, diodebackward_2_out,
       diodebackward_6_out, diodebackward_8_out, diodebackward_10_out, F, Fout, GCLK, I0, I1, IC16_2_nq,
       IC16_nq, IC17_2_nq, IC17_nq, IX, LD, LOAD, nA, nand_1_out, nand_2_out, nand_3_out, nand_5_out,
       nand_6_out, nand_8_out, nand_9_out, nand_10_out, nand_11_out, nand_12_out, nand_13_out, nand_14_out,
       nand_15_out, nB, nCLRPC, nJMP, nLOAD, nPCRES, nRES, nRST, OR, PC_Cin, PCin, PCout, pullup_1_out,
       pullup_2_out, pullup_5_out, pullup_6_out, R0, R1, R2, R3, R4, R5, R6, R7, R8, R9, R10, R11, R12, R13,
       R14, R15, RCO, RESET_out, Rout, RST, SETC, ST, SUB, T0, U2_pin11, U3_pin9, U22_pin14, U25_pin9, XOR,
       xor_1_out, xor_2_out, xor_3_out, xor_4_out, xor_5_out, xor_6_out, xor_7_out, xor_8_out;
  wire [3:0] U5_pin3, U5_pin13, U6_pin6;
  wire [3:1] U6_pin10;

  nand nand_1 (nand_1_out, PCout, PC_Cin);
  xor xor_1 (xor_1_out, PCout, PC_Cin);
  xor xor_2 (xor_2_out, nJMP, 1'b1);
  _74595 U22 (
    .pin1(A6), .pin2(A5), .pin3(A4), .pin4(A3), .pin5(A2), .pin6(A1), .pin7(A0), .pin8(1'b0), .pin9(PCout),
    .pin10(nPCRES), .pin11(GCLK), .pin12(T0), .pin13(1'b0), .pin14(U22_pin14), .pin15(A7), .pin16(1'b1));
  _74595 U23 (
    .pin1(A14), .pin2(A13), .pin3(A12), .pin4(A11), .pin5(A10), .pin6(A9), .pin7(A8), .pin8(1'b0),
    .pin9(U22_pin14), .pin10(nPCRES), .pin11(GCLK), .pin12(T0), .pin13(1'b0), .pin14(PCin), .pin15(A15),
    .pin16(1'b1));
  Seven_Seg_Hex seven_seg_hex_1 (.d({A15, A14, A13, A12}), .dp(1'b0));
  xor xor_3 (xor_3_out, nand_1_out, 1'b1);
  xor xor_4 (xor_4_out, nRES_COUNT, xor_2_out);
  Seven_Seg_Hex seven_seg_hex_2 (.d({A11, A10, A9, A8}), .dp(1'b0));
  Seven_Seg_Hex seven_seg_hex_3 (.d({A7, A6, A5, A4}), .dp(1'b0));
  nand nand_2 (nand_2_out, xor_1_out, xor_4_out);
  nand nand_3 (nand_3_out, xor_2_out, Aout);
  Seven_Seg_Hex seven_seg_hex_4 (.d({A3, A2, A1, A0}), .dp(1'b0));
  // _27C1024 U24: pin names not known; wires that end beside it: A9, A10, A11, A12, A13, A14, A15, 1'b1, R3, R4, R5, R6, R7, 1'b0, R8, R9, R10, R11, R12, R13, R14, R15, 1'b0, 1'b1
  nand nand_4 (PCin, nand_2_out, nand_3_out);
  Seven_Seg_Hex seven_seg_hex_5 (.d({R15, R14, R13, R12}), .dp(1'b0));
  Seven_Seg_Hex seven_seg_hex_6 (.d({R11, R10, R9, R8}), .dp(1'b0));
  Seven_Seg_Hex seven_seg_hex_7 (.d({R7, R6, R5, R4}), .dp(1'b0));
  _74165 U25 (
    .pin1(LD), .pin2(GCLK), .pin3(R11), .pin4(R10), .pin5(R9), .pin6(R8), .pin8(1'b0), .pin9(U25_pin9),
    .pin10(1'b0), .pin11(R15), .pin12(R14), .pin13(R13), .pin14(R12), .pin15(1'b0), .pin16(1'b1));  // open: pin7
  _74165 U26 (
    .pin1(LD), .pin2(GCLK), .pin3(R3), .pin4(R2), .pin5(R1), .pin6(R0), .pin8(1'b0), .pin9(Rout),
    .pin10(U25_pin9), .pin11(R7), .pin12(R6), .pin13(R5), .pin14(R4), .pin15(1'b0), .pin16(1'b1));  // open: pin7
  _7474 U29 (
    .pin1(1'b1), .pin2(xor_3_out), .pin3(GCLK), .pin4(nLOAD), .pin5(PC_Cin), .pin7(1'b0), .pin10(1'b1),
    .pin11(1'b1), .pin12(1'b1), .pin13(1'b1), .pin14(1'b1));  // open: pin6, pin8, pin9
  Seven_Seg_Hex seven_seg_hex_8 (.d({R3, R2, R1, R0}), .dp(1'b0));
  LED led_1 (.in(D14));
  LED led_2 (.in(D15));
  D_FF d_ff_1 (.D(d_ff_1_nq), .C(button_3_out), .Q(D14), .nQ(d_ff_1_nq));
  D_FF IC17 (.D(IC17_nq), .C(button_1_out), .Q(D15), .nQ(IC17_nq));
  Button button_1 (.out(button_1_out));
  LED led_3 (.in(D13));
  D_FF d_ff_2 (.D(d_ff_2_nq), .C(button_2_out), .Q(D13), .nQ(d_ff_2_nq));
  Button button_2 (.out(button_2_out));
  Button button_3 (.out(button_3_out));
  LED led_4 (.in(D12));
  D_FF d_ff_3 (.D(d_ff_3_nq), .C(button_4_out), .Q(D12), .nQ(d_ff_3_nq));
  Button button_4 (.out(button_4_out));
  LED led_5 (.in(D10));
  LED led_6 (.in(D11));
  D_FF d_ff_4 (.D(d_ff_4_nq), .C(button_7_out), .Q(D10), .nQ(d_ff_4_nq));
  D_FF d_ff_5 (.D(d_ff_5_nq), .C(button_5_out), .Q(D11), .nQ(d_ff_5_nq));
  Button button_5 (.out(button_5_out));
  LED led_7 (.in(D9));
  D_FF d_ff_6 (.D(d_ff_6_nq), .C(button_6_out), .Q(D9), .nQ(d_ff_6_nq));
  Button button_6 (.out(button_6_out));
  Button button_7 (.out(button_7_out));
  Seven_Seg_Hex seven_seg_hex_9 (.d({D15, D14, D13, D12}), .dp(1'b0));
  LED led_8 (.in(D8));
  D_FF IC17_2 (.D(IC17_2_nq), .C(button_8_out), .Q(D8), .nQ(IC17_2_nq));
  Button button_8 (.out(button_8_out));
  Seven_Seg_Hex seven_seg_hex_10 (.d({D11, D10, D9, D8}), .dp(1'b0));
  Seven_Seg_Hex seven_seg_hex_11 (.d({D7, D6, D5, D4}), .dp(1'b0));
  Seven_Seg_Hex seven_seg_hex_12 (.d({D3, D2, D1, D0}), .dp(1'b0));
  LED led_9 (.in(D7));
  D_FF IC16 (.D(IC16_nq), .C(button_9_out), .Q(D7), .nQ(IC16_nq));
  Button button_9 (.out(button_9_out));
  LED led_10 (.in(D5));
  LED led_11 (.in(D6));
  D_FF d_ff_7 (.D(d_ff_7_nq), .C(button_12_out), .Q(D5), .nQ(d_ff_7_nq));
  D_FF d_ff_8 (.D(d_ff_8_nq), .C(button_10_out), .Q(D6), .nQ(d_ff_8_nq));
  Button button_10 (.out(button_10_out));
  LED led_12 (.in(D4));
  D_FF d_ff_9 (.D(d_ff_9_nq), .C(button_11_out), .Q(D4), .nQ(d_ff_9_nq));
  Button button_11 (.out(button_11_out));
  Button button_12 (.out(button_12_out));
  LED led_13 (.in(D3));
  D_FF d_ff_10 (.D(d_ff_10_nq), .C(button_13_out), .Q(D3), .nQ(d_ff_10_nq));
  Button button_13 (.out(button_13_out));
  LED led_14 (.in(D1));
  LED led_15 (.in(D2));
  D_FF d_ff_11 (.D(d_ff_11_nq), .C(button_16_out), .Q(D1), .nQ(d_ff_11_nq));
  D_FF d_ff_12 (.D(d_ff_12_nq), .C(button_14_out), .Q(D2), .nQ(d_ff_12_nq));
  Button button_14 (.out(button_14_out));
  LED led_16 (.in(D0));
  D_FF IC16_2 (.D(IC16_2_nq), .C(button_15_out), .Q(D0), .nQ(IC16_2_nq));
  Button button_15 (.out(button_15_out));
  Button button_16 (.out(button_16_out));
  _74165 U3 (
    .pin1(nLOAD), .pin2(GCLK), .pin3(D11), .pin4(D10), .pin5(D9), .pin6(D8), .pin8(1'b0), .pin9(U3_pin9),
    .pin10(1'b0), .pin11(D15), .pin12(D14), .pin13(D13), .pin14(D12), .pin15(1'b0), .pin16(1'b1));  // open: pin7
  Monoflop Mono2 (.C(nLOAD), .R(1'b0), .Q(SETC), .nQ(nRES));
  Monoflop Mono1 (.C(button_17_out), .R(1'b0), .Q(LD), .nQ(nLOAD));
  Button button_17 (.out(button_17_out));
  _74138 U1 (
    .pin1(in_2), .pin2(in_3), .pin3(in_4), .pin4(1'b0), .pin5(1'b0), .pin6(1'b1), .pin7(nJMP), .pin8(1'b0),
    .pin9(ST), .pin10(SUB), .pin11(ADD), .pin12(XOR), .pin13(OR), .pin14(AND), .pin15(LOAD), .pin16(1'b1));
  Monoflop monoflop_1 (.C(RESET_out), .R(1'b0), .Q(nCLRPC), .nQ(nPCRES));
  Button RESET (.out(RESET_out));
  PullUp pullup_1 (.out(pullup_1_out));
  _74165 U4 (
    .pin1(nLOAD), .pin2(GCLK), .pin3(D3), .pin4(D2), .pin5(D1), .pin6(D0), .pin8(1'b0), .pin9(Bout),
    .pin10(U3_pin9), .pin11(D7), .pin12(D6), .pin13(D5), .pin14(D4), .pin15(1'b0), .pin16(1'b1));  // open: pin7
  PullUp pullup_2 (.out(pullup_2_out));
  DiodeBackward diodebackward_1 (.in(LOAD), .out(pullup_2_out));
  DiodeBackward diodebackward_2 (.in(LOAD), .out(diodebackward_2_out));
  DiodeBackward diodebackward_3 (.in(ADD), .out(diodebackward_2_out));
  DiodeBackward diodebackward_4 (.in(SUB), .out(diodebackward_2_out));
  DiodeBackward diodebackward_5 (.in(nJMP), .out(diodebackward_2_out));
  PullUp pullup_3 (.out(diodebackward_2_out));
  DiodeBackward diodebackward_6 (.in(SUB), .out(diodebackward_6_out));
  PullUp pullup_4 (.out(diodebackward_6_out));
  PullUp pullup_5 (.out(pullup_5_out));
  DiodeBackward diodebackward_7 (.in(SUB), .out(pullup_5_out));
  PullUp pullup_6 (.out(pullup_6_out));
  DiodeBackward diodebackward_8 (.in(AND), .out(diodebackward_8_out));
  DiodeBackward diodebackward_9 (.in(OR), .out(diodebackward_8_out));
  PullUp pullup_7 (.out(diodebackward_8_out));
  DiodeBackward diodebackward_10 (.in(LOAD), .out(diodebackward_10_out));
  DiodeBackward diodebackward_11 (.in(OR), .out(diodebackward_10_out));
  DiodeBackward diodebackward_12 (.in(XOR), .out(diodebackward_10_out));
  DiodeBackward diodebackward_13 (.in(ADD), .out(diodebackward_10_out));
  DiodeBackward diodebackward_14 (.in(SUB), .out(diodebackward_10_out));
  DiodeBackward diodebackward_15 (.in(ST), .out(diodebackward_10_out));
  PullUp pullup_8 (.out(diodebackward_10_out));
  _74540 U2 (
    .pin1(1'b0), .pin2(diodebackward_10_out), .pin3(diodebackward_8_out), .pin4(pullup_6_out),
    .pin5(pullup_5_out), .pin6(diodebackward_6_out), .pin7(diodebackward_2_out), .pin8(pullup_2_out),
    .pin9(pullup_1_out), .pin10(1'b0), .pin11(U2_pin11), .pin12(CLA), .pin13(F), .pin14(C), .pin15(nB),
    .pin16(nA), .pin17(I1), .pin18(I0), .pin19(1'b0), .pin20(1'b1));
  _74164 U5 (
    .pin1(1'b1), .pin2(Fout), .pin3(U5_pin3[3]), .pin4(U5_pin3[2]), .pin5(U5_pin3[1]), .pin6(U5_pin3[0]),
    .pin7(1'b0), .pin8(GCLK), .pin9(CLR), .pin10(U5_pin13[3]), .pin11(U5_pin13[2]), .pin12(U5_pin13[1]),
    .pin13(U5_pin13[0]), .pin14(1'b1));
  Seven_Seg_Hex seven_seg_hex_13 (.d(U5_pin3), .dp(1'b0));
  xor xor_5 (xor_5_out, Aout, nA);
  xor xor_6 (xor_6_out, nB, Bout);
  nand nand_5 (nand_5_out, SETC, C);
  nand nand_6 (nand_6_out, C, C);
  nand nand_7 (CLR, CLA, LD);
  Seven_Seg_Hex seven_seg_hex_14 (.d(U5_pin13), .dp(1'b0));
  Seven_Seg_Hex seven_seg_hex_15 (.d(U6_pin6), .dp(1'b0));
  xor xor_7 (xor_7_out, xor_5_out, xor_6_out);
  nand nand_8 (nand_8_out, nand_6_out, LD);
  Seven_Seg_Hex seven_seg_hex_16 (.d({U6_pin10, Aout}), .dp(1'b0));
  _74164 U6 (
    .pin1(1'b1), .pin2(U5_pin13[0]), .pin3(U6_pin6[3]), .pin4(U6_pin6[2]), .pin5(U6_pin6[1]),
    .pin6(U6_pin6[0]), .pin7(1'b0), .pin8(GCLK), .pin9(CLR), .pin10(U6_pin10[3]), .pin11(U6_pin10[2]),
    .pin12(U6_pin10[1]), .pin13(Aout), .pin14(1'b1));
  xor xor_8 (xor_8_out, xor_7_out, Cin);
  nand nand_9 (nand_9_out, xor_7_out, Cin);
  nand nand_10 (nand_10_out, xor_5_out, xor_6_out);
  nand nand_11 (nand_11_out, nand_9_out, nand_10_out);
  nand nand_12 (nand_12_out, xor_8_out, I0);
  nand nand_13 (nand_13_out, I1, nand_11_out);
  nand nand_14 (nand_14_out, nand_11_out, F);
  nand nand_15 (nand_15_out, clk, clk);
  nand nand_16 (RST, nRES, nRST);
  nand nand_17 (nRST, RST, T0);
  nand nand_18 (Fout, nand_12_out, nand_13_out);
  nand nand_19 (Cout, nand_14_out, nand_14_out);
  nand nand_20 (GCLK, nand_15_out, RST);
  _7474 U9 (
    .pin1(nand_8_out), .pin2(Cout), .pin3(GCLK), .pin4(nand_5_out), .pin5(Cin), .pin7(1'b0), .pin8(T0),
    .pin9(IX), .pin10(1'b1), .pin11(clk), .pin12(RCO), .pin13(1'b1), .pin14(1'b1));  // open: pin6
  _74161 U7 (
    .pin1(RST), .pin2(clk), .pin3(1'b0), .pin4(1'b0), .pin5(1'b0), .pin6(1'b0), .pin7(1'b1), .pin8(1'b0),
    .pin9(1'b1), .pin10(1'b1), .pin15(RCO), .pin16(1'b1));  // open: pin11, pin12, pin13, pin14

  // Notes on the sheet:
  //   clk: Hz: 2147483647
  //   nRES_COUNT: default 1
  //   ROM & PC UNIT
  //   Program Counter
  //   U28A
  //   U27A
  //   U27D
  //   ROM ADDRESS
  //   U27C
  //   U27B
  //   16-bit ROM
  //   U28C
  //   U28B
  //   Carry is only set before Bit 0 of an operation
  //   U28D
  //   ROM DATA
  //   ROM Data Register
  //   PC Carry FF
  //   Front Panel
  //   ENTER H
  //   Data Input
  //   ENTER L
  //   .
  //   Instruction Input
  //   STEP/RUN
  //   U14
  //   16 bit Shift Register B
  //   CLA
  //   Instruction Decode
  //   F
  //   ~B
  //   C
  //   ~A
  //   I1
  //   I0
  //   LOAD
  //   AND
  //   OR
  //   XOR
  //   ADD
  //   SUB
  //   STORE
  //   JMP
  //   16 bit Shift Register A
  //   Bit Serial ALU
  //   ACCUMULATOR
  //   U9, U10, U11, U12, U13
  //   Any residual carry is cleared before an operation
  //   Spider Bit Serial CPU Testbed
  //   U8
  //   Clock Sequencer
  //   Suppress Carry
  //   Carry FF
endmodule
