// Digital circuit Spider_with_regs_1.dig as structural Verilog
module Spider_with_regs_1 (
  input  clk,
  input  in_2,
  input  in_3,
  input  in_4,
  input  nCS,
  input  nWE,
  input  A0,
  input  A1,
  input  A2,
  input  A3,
  input  in_16,
  input  in_17,
  input  in_18,
  output LD,
  output RES,
  output GCLK,
  output T0,
  output RST
);

  wire ADD, AND, Aout, Bout, BUS0, BUS1, BUS2, BUS3, BUS4, BUS5, BUS6, BUS7, BUS8, BUS9, BUS10, BUS11, BUS12,
       BUS13, BUS14, BUS15, button_1_out, button_2_out, button_3_out, button_4_out, button_5_out,
       button_6_out, button_7_out, button_8_out, button_9_out, button_10_out, button_11_out, button_12_out,
       button_13_out, button_14_out, button_15_out, button_16_out, button_17_out, button_18_out, C, Cin, CLA,
       CLR, Cout, D0, D1, D2, D3, D4, D5, D6, D7, D8, D9, D10, D11, D12, D13, D14, D15, d_ff_1_nq, d_ff_2_nq,
       d_ff_3_nq, d_ff_4_nq, d_ff_5_nq, d_ff_6_nq, d_ff_7_nq, d_ff_8_nq, d_ff_9_nq, d_ff_10_nq, d_ff_11_nq,
       d_ff_12_nq, diodebackward_1_out, diodebackward_2_out, diodebackward_8_out, diodebackward_9_out,
       diodeforward_1_out, F, Fout, I0, I1, IC16_2_nq, IC16_nq, IC17_2_nq, IC17_nq, IX, LD_t, LOAD, nA,
       nand_1_out, nand_2_out, nand_4_out, nand_5_out, nand_6_out, nand_8_out, nand_9_out, nand_10_out,
       nand_11_out, nand_12_out, nand_13_out, nB, nJMP, nLDSW, OR, pullup_2_out, pullup_4_out, pullup_7_out,
       RCO, S0, S1, S2, S3, S4, S5, S6, S7, S8, S9, S10, S11, S12, S13, S14, S15, SETC, ST, SUB, U5_pin9,
       U17_pin9, XOR, xor_1_out, xor_2_out, xor_3_out, xor_4_out, ZERO;
  wire [3:0] U5_2_pin6, U5_2_pin13, U6_2_pin6, U7_pin11;
  wire [3:1] U6_2_pin10;

  _74595 U17 (
    .pin1(D14), .pin2(D13), .pin3(D12), .pin4(D11), .pin5(D10), .pin6(D9), .pin7(D8), .pin8(1'b0),
    .pin9(U17_pin9), .pin10(RES), .pin11(GCLK), .pin12(T0), .pin13(nWE), .pin14(Fout), .pin15(D15),
    .pin16(1'b1));
  _74138 U1 (
    .pin1(in_2), .pin2(in_3), .pin3(in_4), .pin4(1'b0), .pin5(1'b0), .pin6(1'b1), .pin7(nJMP), .pin8(1'b0),
    .pin9(ST), .pin10(SUB), .pin11(ADD), .pin12(XOR), .pin13(OR), .pin14(AND), .pin15(LOAD), .pin16(1'b1));
  Monoflop monoflop_1 (.C(LD), .R(1'b0), .Q(SETC), .nQ(RES));
  Monoflop monoflop_2 (.C(button_1_out), .R(1'b0), .Q(LD_t), .nQ(LD));
  Button button_1 (.out(button_1_out));
  DiodeBackward diodebackward_1 (.in(LOAD), .out(diodebackward_1_out));
  Monoflop monoflop_3 (.C(button_2_out), .R(1'b0), .nQ(nLDSW));  // open: Q
  Button button_2 (.out(button_2_out));
  PullUp pullup_1 (.out(diodebackward_1_out));
  DiodeBackward diodebackward_2 (.in(LOAD), .out(diodebackward_2_out));
  DiodeBackward diodebackward_3 (.in(ADD), .out(diodebackward_2_out));
  DiodeBackward diodebackward_4 (.in(SUB), .out(diodebackward_2_out));
  DiodeBackward diodebackward_5 (.in(nJMP), .out(diodebackward_2_out));
  _74595 U16 (
    .pin1(D6), .pin2(D5), .pin3(D4), .pin4(D3), .pin5(D2), .pin6(D1), .pin7(D0), .pin8(1'b0), .pin10(RES),
    .pin11(GCLK), .pin12(T0), .pin13(nWE), .pin14(U17_pin9), .pin15(D7), .pin16(1'b1));  // open: pin9
  PullUp pullup_2 (.out(pullup_2_out));
  PullUp pullup_3 (.out(diodebackward_2_out));
  DiodeBackward diodebackward_6 (.in(SUB), .out(pullup_2_out));
  _74219 _74219_1 (
    .pin1(A0), .pin2(nCS), .pin3(nWE), .pin4(D12), .pin5(BUS12), .pin6(D13), .pin7(BUS13), .pin8(1'b0),
    .pin9(BUS14), .pin10(D14), .pin11(BUS15), .pin12(D15), .pin13(A3), .pin14(A2), .pin15(A1), .pin16(1'b1));
  PullUp pullup_4 (.out(pullup_4_out));
  DiodeBackward diodebackward_7 (.in(SUB), .out(pullup_4_out));
  DiodeBackward diodebackward_8 (.in(nJMP), .out(diodebackward_8_out));
  PullUp pullup_5 (.out(diodebackward_8_out));
  DiodeBackward diodebackward_9 (.in(AND), .out(diodebackward_9_out));
  DiodeBackward diodebackward_10 (.in(OR), .out(diodebackward_9_out));
  PullUp pullup_6 (.out(diodebackward_9_out));
  PullUp pullup_7 (.out(pullup_7_out));
  DiodeBackward diodebackward_11 (.in(LOAD), .out(pullup_7_out));
  DiodeBackward diodebackward_12 (.in(OR), .out(pullup_7_out));
  DiodeBackward diodebackward_13 (.in(XOR), .out(pullup_7_out));
  DiodeBackward diodebackward_14 (.in(ADD), .out(pullup_7_out));
  DiodeBackward diodebackward_15 (.in(SUB), .out(pullup_7_out));
  DiodeBackward diodebackward_16 (.in(ST), .out(pullup_7_out));
  DiodeBackward diodebackward_17 (.in(nJMP), .out(pullup_7_out));
  _74540 U2 (
    .pin1(1'b0), .pin2(pullup_7_out), .pin3(diodebackward_9_out), .pin4(diodebackward_8_out),
    .pin5(pullup_4_out), .pin6(pullup_2_out), .pin7(diodebackward_2_out), .pin8(diodebackward_1_out),
    .pin9(1'b0), .pin10(1'b0), .pin12(CLA), .pin13(F), .pin14(C), .pin15(nB), .pin16(nA), .pin17(I1),
    .pin18(I0), .pin19(1'b0), .pin20(1'b1));  // open: pin11
  _74219 _74219_2 (
    .pin1(A0), .pin2(nCS), .pin3(nWE), .pin4(D8), .pin5(BUS8), .pin6(D9), .pin7(BUS9), .pin8(1'b0),
    .pin9(BUS10), .pin10(D10), .pin11(BUS11), .pin12(D11), .pin13(A3), .pin14(A2), .pin15(A1), .pin16(1'b1));
  D_FF IC17 (.D(IC17_nq), .C(button_3_out), .Q(S15), .nQ(IC17_nq));
  D_FF d_ff_1 (.D(d_ff_1_nq), .C(button_4_out), .Q(S14), .nQ(d_ff_1_nq));
  Button button_3 (.out(button_3_out));
  _74219 _74219_3 (
    .pin1(A0), .pin2(nCS), .pin3(nWE), .pin4(D4), .pin5(BUS4), .pin6(D5), .pin7(BUS5), .pin8(1'b0),
    .pin9(BUS6), .pin10(D6), .pin11(BUS7), .pin12(D7), .pin13(A3), .pin14(A2), .pin15(A1), .pin16(1'b1));
  D_FF d_ff_2 (.D(d_ff_2_nq), .C(button_5_out), .Q(S13), .nQ(d_ff_2_nq));
  Button button_4 (.out(button_4_out));
  D_FF d_ff_3 (.D(d_ff_3_nq), .C(button_6_out), .Q(S12), .nQ(d_ff_3_nq));
  Button button_5 (.out(button_5_out));
  _74541 _74541_1 (
    .pin1(nLDSW), .pin2(S15), .pin3(S14), .pin4(S13), .pin5(S12), .pin6(S11), .pin7(S10), .pin8(S9),
    .pin9(S8), .pin10(1'b0), .pin11(D8), .pin12(D9), .pin13(D10), .pin14(D11), .pin15(D12), .pin16(D13),
    .pin17(D14), .pin18(D15), .pin19(nLDSW), .pin20(1'b1));
  D_FF d_ff_4 (.D(d_ff_4_nq), .C(button_7_out), .Q(S11), .nQ(d_ff_4_nq));
  Button button_6 (.out(button_6_out));
  D_FF d_ff_5 (.D(d_ff_5_nq), .C(button_8_out), .Q(S10), .nQ(d_ff_5_nq));
  Button button_7 (.out(button_7_out));
  D_FF d_ff_6 (.D(d_ff_6_nq), .C(button_9_out), .Q(S9), .nQ(d_ff_6_nq));
  Button button_8 (.out(button_8_out));
  _74219 _74219_4 (
    .pin1(A0), .pin2(nCS), .pin3(nWE), .pin4(D0), .pin5(BUS0), .pin6(D1), .pin7(BUS1), .pin8(1'b0),
    .pin9(BUS2), .pin10(D2), .pin11(BUS3), .pin12(D3), .pin13(A3), .pin14(A2), .pin15(A1), .pin16(1'b1));
  D_FF IC17_2 (.D(IC17_2_nq), .C(button_10_out), .Q(S8), .nQ(IC17_2_nq));
  Button button_9 (.out(button_9_out));
  Seven_Seg_Hex seven_seg_hex_1 (.d({S15, S14, S13, S12}), .dp(1'b0));
  Button button_10 (.out(button_10_out));
  Seven_Seg_Hex seven_seg_hex_2 (.d({S11, S10, S9, S8}), .dp(1'b0));
  _74541 _74541_2 (
    .pin1(nLDSW), .pin2(S7), .pin3(S6), .pin4(S5), .pin5(S4), .pin6(S3), .pin7(S2), .pin8(S1), .pin9(S0),
    .pin10(1'b0), .pin11(D0), .pin12(D1), .pin13(D2), .pin14(D3), .pin15(D4), .pin16(D5), .pin17(D6),
    .pin18(D7), .pin19(nLDSW), .pin20(1'b1));
  D_FF IC16 (.D(IC16_nq), .C(button_11_out), .Q(S7), .nQ(IC16_nq));
  Button button_11 (.out(button_11_out));
  _74165 U5 (
    .pin1(LD), .pin2(GCLK), .pin3(BUS11), .pin4(BUS10), .pin5(BUS9), .pin6(BUS8), .pin8(1'b0),
    .pin9(U5_pin9), .pin10(1'b0), .pin11(BUS15), .pin12(BUS14), .pin13(BUS13), .pin14(BUS12), .pin15(1'b0),
    .pin16(1'b1));  // open: pin7
  _74165 U6 (
    .pin1(LD), .pin2(GCLK), .pin3(BUS3), .pin4(BUS2), .pin5(BUS1), .pin6(BUS0), .pin8(1'b0), .pin9(Bout),
    .pin10(U5_pin9), .pin11(BUS7), .pin12(BUS6), .pin13(BUS5), .pin14(BUS4), .pin15(1'b0), .pin16(1'b1));  // open: pin7
  D_FF d_ff_7 (.D(d_ff_7_nq), .C(button_12_out), .Q(S6), .nQ(d_ff_7_nq));
  Button button_12 (.out(button_12_out));
  D_FF d_ff_8 (.D(d_ff_8_nq), .C(button_13_out), .Q(S5), .nQ(d_ff_8_nq));
  Button button_13 (.out(button_13_out));
  D_FF d_ff_9 (.D(d_ff_9_nq), .C(button_14_out), .Q(S4), .nQ(d_ff_9_nq));
  Button button_14 (.out(button_14_out));
  D_FF d_ff_10 (.D(d_ff_10_nq), .C(button_15_out), .Q(S3), .nQ(d_ff_10_nq));
  Button button_15 (.out(button_15_out));
  D_FF d_ff_11 (.D(d_ff_11_nq), .C(button_16_out), .Q(S2), .nQ(d_ff_11_nq));
  Button button_16 (.out(button_16_out));
  D_FF d_ff_12 (.D(d_ff_12_nq), .C(button_17_out), .Q(S1), .nQ(d_ff_12_nq));
  Button button_17 (.out(button_17_out));
  _74164 U5_2 (
    .pin1(1'b1), .pin2(Fout), .pin3(U5_2_pin6[3]), .pin4(U5_2_pin6[2]), .pin5(U5_2_pin6[1]),
    .pin6(U5_2_pin6[0]), .pin7(1'b0), .pin8(GCLK), .pin9(CLR), .pin10(U5_2_pin13[3]), .pin11(U5_2_pin13[2]),
    .pin12(U5_2_pin13[1]), .pin13(U5_2_pin13[0]), .pin14(1'b1));
  D_FF IC16_2 (.D(IC16_2_nq), .C(button_18_out), .Q(S0), .nQ(IC16_2_nq));
  Button button_18 (.out(button_18_out));
  Seven_Seg_Hex seven_seg_hex_3 (.d({S7, S6, S5, S4}), .dp(1'b0));
  Seven_Seg_Hex seven_seg_hex_4 (.d({BUS15, BUS14, BUS13, BUS12}), .dp(1'b0));
  Seven_Seg_Hex seven_seg_hex_5 (.d({S3, S2, S1, S0}), .dp(1'b0));
  Seven_Seg_Hex seven_seg_hex_6 (.d({BUS11, BUS10, BUS9, BUS8}), .dp(1'b0));
  Seven_Seg_Hex seven_seg_hex_7 (.d(U5_2_pin6), .dp(1'b0));
  Seven_Seg_Hex seven_seg_hex_8 (.d({BUS7, BUS6, BUS5, BUS4}), .dp(1'b0));
  Seven_Seg_Hex seven_seg_hex_9 (.d(U5_2_pin13), .dp(1'b0));
  Seven_Seg_Hex seven_seg_hex_10 (.d({BUS3, BUS2, BUS1, BUS0}), .dp(1'b0));
  Seven_Seg_Hex seven_seg_hex_11 (.d(U6_2_pin6), .dp(1'b0));
  Seven_Seg_Hex seven_seg_hex_12 (.d({U6_2_pin10, Aout}), .dp(1'b0));
  _74164 U6_2 (
    .pin1(1'b1), .pin2(U5_2_pin13[0]), .pin3(U6_2_pin6[3]), .pin4(U6_2_pin6[2]), .pin5(U6_2_pin6[1]),
    .pin6(U6_2_pin6[0]), .pin7(1'b0), .pin8(GCLK), .pin9(CLR), .pin10(U6_2_pin10[3]), .pin11(U6_2_pin10[2]),
    .pin12(U6_2_pin10[1]), .pin13(Aout), .pin14(1'b1));
  xor xor_1 (xor_1_out, Aout, nA);
  xor xor_2 (xor_2_out, nB, Bout);
  nand nand_1 (nand_1_out, SETC, C);
  nand nand_2 (nand_2_out, C, C);
  nand nand_3 (CLR, CLA, LD_t);
  Seven_Seg_Hex seven_seg_hex_13 (.d({D15, D14, D13, D12}), .dp(1'b0));
  xor xor_3 (xor_3_out, xor_1_out, xor_2_out);
  nand nand_4 (nand_4_out, nand_2_out, LD_t);
  Seven_Seg_Hex seven_seg_hex_14 (.d({D11, D10, D9, D8}), .dp(1'b0));
  Seven_Seg_Hex seven_seg_hex_15 (.d({D7, D6, D5, D4}), .dp(1'b0));
  xor xor_4 (xor_4_out, xor_3_out, Cin);
  nand nand_5 (nand_5_out, xor_3_out, Cin);
  nand nand_6 (nand_6_out, xor_1_out, xor_2_out);
  Seven_Seg_Hex seven_seg_hex_16 (.d({D3, D2, D1, D0}), .dp(1'b0));
  nand nand_7 (RST, RES, nand_8_out);
  nand nand_8 (nand_8_out, RST, T0);
  nand nand_9 (nand_9_out, clk, clk);
  nand nand_10 (nand_10_out, nand_5_out, nand_6_out);
  nand nand_11 (nand_11_out, xor_4_out, I0);
  nand nand_12 (nand_12_out, I1, nand_10_out);
  nand nand_13 (nand_13_out, nand_10_out, F);
  nand nand_14 (GCLK, RST, nand_9_out);
  nand nand_15 (Fout, nand_11_out, nand_12_out);
  nand nand_16 (Cout, nand_13_out, nand_13_out);
  _74161 U7 (
    .pin1(RST), .pin2(clk), .pin3(1'b0), .pin4(1'b0), .pin5(1'b0), .pin6(1'b0), .pin7(1'b1), .pin8(1'b0),
    .pin9(1'b1), .pin10(1'b1), .pin11(U7_pin11[3]), .pin12(U7_pin11[2]), .pin13(U7_pin11[1]),
    .pin14(U7_pin11[0]), .pin15(RCO), .pin16(1'b1));
  DiodeForward diodeforward_1 (.in(BUS15), .out(diodeforward_1_out));
  DiodeForward diodeforward_2 (.in(BUS14), .out(diodeforward_1_out));
  DiodeForward diodeforward_3 (.in(BUS13), .out(diodeforward_1_out));
  DiodeForward diodeforward_4 (.in(BUS12), .out(diodeforward_1_out));
  DiodeForward diodeforward_5 (.in(BUS11), .out(diodeforward_1_out));
  DiodeForward diodeforward_6 (.in(BUS10), .out(diodeforward_1_out));
  DiodeForward diodeforward_7 (.in(BUS9), .out(diodeforward_1_out));
  DiodeForward diodeforward_8 (.in(BUS8), .out(diodeforward_1_out));
  DiodeForward diodeforward_9 (.in(BUS7), .out(diodeforward_1_out));
  DiodeForward diodeforward_10 (.in(BUS6), .out(diodeforward_1_out));
  DiodeForward diodeforward_11 (.in(BUS5), .out(diodeforward_1_out));
  DiodeForward diodeforward_12 (.in(BUS4), .out(diodeforward_1_out));
  DiodeForward diodeforward_13 (.in(BUS3), .out(diodeforward_1_out));
  DiodeForward diodeforward_14 (.in(BUS2), .out(diodeforward_1_out));
  DiodeForward diodeforward_15 (.in(BUS1), .out(diodeforward_1_out));
  DiodeForward diodeforward_16 (.in(BUS0), .out(diodeforward_1_out));
  _7474 _7474_1 (
    .pin1(nand_4_out), .pin2(Cout), .pin3(GCLK), .pin4(nand_1_out), .pin5(Cin), .pin7(1'b0), .pin8(T0),
    .pin9(IX), .pin10(1'b1), .pin11(clk), .pin12(RCO), .pin13(1'b1), .pin14(1'b1));  // open: pin6
  PullDown pulldown_1 (.out(diodeforward_1_out));
  nand nand_17 (ZERO, diodeforward_1_out, diodeforward_1_out);
  LED led_1 (.in(Cin));
  LED led_2 (.in(ZERO));
  Seven_Seg_Hex seven_seg_hex_17 (.d(U7_pin11), .dp(1'b0));

  // Other names for the same wires on the sheet: DN = in_17; nLD = LD; nRES = RES; RES_t = in_18; UP = in_16

  // Notes on the sheet:
  //   clk: Hz: 2147483647
  //   nWE: default 1
  //   spider 0
  //   Instruction Decode
  //   STEP/RUN
  //   CLR PC
  //   CLA
  //   C
  //   F
  //   ~B
  //   ~A
  //   I0
  //   I1
  //   LOAD
  //   AND
  //   OR
  //   XOR
  //   ADD
  //   SUB
  //   STORE
  //   JMP
  //   ENTER H
  //   Data Input
  //   Bus Read Register B
  //   ENTER L
  //   16 bit Shift Register A
  //   BUS DATA
  //   ACCUMULATOR
  //   ALU
  //   CLR ACC
  //   Spider 0 Bit serial CPU Testbed
  //   Carry is only set before Bit 0 of an operation
  //   Any residual carry is cleared before an operation
  //   Suppress Carry
  //   Clock Sequencer
  //   Carry FF
  //   CARRY
  //   # Clock
endmodule
