// Digital circuit Spider_with_regs_ROM_2.dig as structural Verilog
module Spider_with_regs_ROM_2 (
  input  clk,
  input  in_2,
  input  in_3,
  input  in_4,
  input  nRES_COUNT,
  input  JMP,
  input  in_12,
  input  in_13,
  input  READ,
  input  in_15,
  output LD,
  output RES,
  output GCLK,
  output T0,
  output RST
);

  wire A0, A1, A2, A3, A4, A5, A6, A7, A8, A9, A10, A11, A12, A13, A14, A15, AC0, AC1, AC2, AC3, AC4, AC5,
       AC6, AC7, AC8, AC9, AC10, AC11, AC12, AC13, AC14, AC15, AD0, AD1, AD2, AD3, AD4, AD5, AD6, AD7, AD8,
       AD9, AD10, AD11, AD12, AD13, AD14, AD15, ADD, AND, Bout, BUS0, BUS1, BUS2, BUS3, BUS4, BUS5, BUS6,
       BUS7, BUS8, BUS9, BUS10, BUS11, BUS12, BUS13, BUS14, BUS15, button_1_out, button_2_out, C, Cin, CLA,
       CLR, Cout, D0, D1, D2, D3, D4, D5, D6, D7, D8, D9, D10, D11, D12, D13, D14, D15, diodebackward_1_out,
       diodebackward_2_out, diodebackward_8_out, diodebackward_9_out, diodeforward_1_out,
       diodeforward_17_out, F, Fout, I0, I1, IX, LD_t, LOAD, nA, nand_2_out, nand_3_out, nand_4_out,
       nand_6_out, nand_7_out, nand_9_out, nand_10_out, nand_11_out, nand_13_out, nand_14_out, nand_15_out,
       nand_17_out, nand_18_out, nand_19_out, nB, nCLR, nCLRPC, nJMP, nRRES, OR, PC_Cin, PCin, PCout,
       pullup_2_out, pullup_4_out, pullup_7_out, RCO, ROM0, ROM1, ROM2, ROM3, ROM4, ROM5, ROM6, ROM7, ROM8,
       ROM9, ROM10, ROM11, ROM12, ROM13, ROM14, ROM15, SETC, ST, SUB, U3_pin9, U5_pin9, U17_pin9, U23_pin9,
       U25_pin9, XOR, xor_1_out, xor_2_out, xor_3_out, xor_4_out, xor_5_out, xor_6_out, xor_7_out, xor_8_out,
       ZERO;
  wire [3:0] U5_2_pin6, U5_2_pin13, U6_2_pin6, U7_2_pin11;
  wire [3:1] U6_2_pin10;

  Seven_Seg_Hex seven_seg_hex_1 (.d({AD15, AD14, AD13, AD12}), .dp(1'b0));
  Seven_Seg_Hex seven_seg_hex_2 (.d({AD11, AD10, AD9, AD8}), .dp(1'b0));
  // NAnd nand_1 has open pins: In_1=diodeforward_1_out, In_2=diodeforward_1_out, out=open
  _74164 U7 (
    .pin1(1'b1), .pin2(Fout), .pin3(AC15), .pin4(AC14), .pin5(AC13), .pin6(AC12), .pin7(1'b0), .pin8(GCLK),
    .pin9(nCLR), .pin10(AC11), .pin11(AC10), .pin12(AC9), .pin13(AC8), .pin14(1'b1));
  Seven_Seg_Hex seven_seg_hex_3 (.d({AD7, AD6, AD5, AD4}), .dp(1'b0));
  DiodeForward diodeforward_1 (.in(AC0), .out(diodeforward_1_out));
  DiodeForward diodeforward_2 (.in(AC1), .out(diodeforward_1_out));
  DiodeForward diodeforward_3 (.in(AC2), .out(diodeforward_1_out));
  DiodeForward diodeforward_4 (.in(AC3), .out(diodeforward_1_out));
  DiodeForward diodeforward_5 (.in(AC4), .out(diodeforward_1_out));
  DiodeForward diodeforward_6 (.in(AC5), .out(diodeforward_1_out));
  DiodeForward diodeforward_7 (.in(AC6), .out(diodeforward_1_out));
  DiodeForward diodeforward_8 (.in(AC7), .out(diodeforward_1_out));
  DiodeForward diodeforward_9 (.in(AC8), .out(diodeforward_1_out));
  DiodeForward diodeforward_10 (.in(AC9), .out(diodeforward_1_out));
  DiodeForward diodeforward_11 (.in(AC10), .out(diodeforward_1_out));
  DiodeForward diodeforward_12 (.in(AC11), .out(diodeforward_1_out));
  DiodeForward diodeforward_13 (.in(AC12), .out(diodeforward_1_out));
  DiodeForward diodeforward_14 (.in(AC13), .out(diodeforward_1_out));
  DiodeForward diodeforward_15 (.in(AC14), .out(diodeforward_1_out));
  DiodeForward diodeforward_16 (.in(AC15), .out(diodeforward_1_out));
  PullDown pulldown_1 (.out(diodeforward_1_out));
  Seven_Seg_Hex seven_seg_hex_4 (.d({AD3, AD2, AD1, AD0}), .dp(1'b0));
  Seven_Seg_Hex seven_seg_hex_5 (.d({BUS15, BUS14, BUS13, BUS12}), .dp(1'b0));
  Seven_Seg_Hex seven_seg_hex_6 (.d({BUS11, BUS10, BUS9, BUS8}), .dp(1'b0));
  _74165 U5 (
    .pin1(LD), .pin2(GCLK), .pin3(BUS11), .pin4(BUS10), .pin5(BUS9), .pin6(BUS8), .pin8(1'b0),
    .pin9(U5_pin9), .pin10(1'b0), .pin11(BUS15), .pin12(BUS14), .pin13(BUS13), .pin14(BUS12), .pin15(1'b0),
    .pin16(1'b1));  // open: pin7
  _74165 U6 (
    .pin1(LD), .pin2(GCLK), .pin3(BUS3), .pin4(BUS2), .pin5(BUS1), .pin6(BUS0), .pin8(1'b0), .pin9(Bout),
    .pin10(U5_pin9), .pin11(BUS7), .pin12(BUS6), .pin13(BUS5), .pin14(BUS4), .pin15(1'b0), .pin16(1'b1));  // open: pin7
  _74164 U8 (
    .pin1(1'b1), .pin2(AC8), .pin3(AC7), .pin4(AC6), .pin5(AC5), .pin6(AC4), .pin7(1'b0), .pin8(GCLK),
    .pin9(nCLR), .pin10(AC3), .pin11(AC2), .pin12(AC1), .pin13(AC0), .pin14(1'b1));
  Seven_Seg_Hex seven_seg_hex_7 (.d({BUS7, BUS6, BUS5, BUS4}), .dp(1'b0));
  Seven_Seg_Hex seven_seg_hex_8 (.d({BUS3, BUS2, BUS1, BUS0}), .dp(1'b0));
  Seven_Seg_Hex seven_seg_hex_9 (.d({AC15, AC14, AC13, AC12}), .dp(1'b0));
  Seven_Seg_Hex seven_seg_hex_10 (.d({AC11, AC10, AC9, AC8}), .dp(1'b0));
  _74595 U25 (
    .pin1(BUS14), .pin2(BUS13), .pin3(BUS12), .pin4(BUS11), .pin5(BUS10), .pin6(BUS9), .pin7(BUS8),
    .pin8(1'b0), .pin9(U25_pin9), .pin10(nRRES), .pin11(GCLK), .pin12(T0), .pin13(in_13), .pin14(Fout),
    .pin15(BUS15), .pin16(1'b1));
  _74595 U24 (
    .pin1(BUS6), .pin2(BUS5), .pin3(BUS4), .pin4(BUS3), .pin5(BUS2), .pin6(BUS1), .pin7(BUS0), .pin8(1'b0),
    .pin10(nRRES), .pin11(GCLK), .pin12(T0), .pin13(in_13), .pin14(U25_pin9), .pin15(BUS7), .pin16(1'b1));  // open: pin9
  Seven_Seg_Hex seven_seg_hex_11 (.d({AC7, AC6, AC5, AC4}), .dp(1'b0));
  Seven_Seg_Hex seven_seg_hex_12 (.d({AC3, AC2, AC1, AC0}), .dp(1'b0));
  // _62256 U20: pin names not known; wires that end beside it: AD14, AD12, AD7, AD6, AD5, AD4, AD3, AD2, AD1, AD0, BUS8, BUS9, 1'b1, in_13, AD13, AD8, AD9, AD11, READ, AD10, in_15, BUS15
  // _62256 U21: pin names not known; wires that end beside it: BUS10, 1'b0, AD14, AD12, AD7, AD6, AD5, AD4, AD3, AD2, AD1, AD0, BUS0, BUS1, BUS2, 1'b0, 1'b1, in_13, AD13, AD8, AD9, AD11, READ, AD10, in_15, BUS7
  _74595 U17 (
    .pin1(BUS14), .pin2(BUS13), .pin3(BUS12), .pin4(BUS11), .pin5(BUS10), .pin6(BUS9), .pin7(BUS8),
    .pin8(1'b0), .pin9(U17_pin9), .pin10(RES), .pin11(GCLK), .pin12(T0), .pin13(in_13), .pin14(Fout),
    .pin15(BUS15), .pin16(1'b1));
  _74165 U3 (
    .pin1(LD), .pin2(GCLK), .pin3(D11), .pin4(D10), .pin5(D9), .pin6(D8), .pin8(1'b0), .pin9(U3_pin9),
    .pin10(1'b0), .pin11(D15), .pin12(D14), .pin13(D13), .pin14(D12), .pin15(1'b0), .pin16(1'b1));  // open: pin7
  _74138 U1 (
    .pin1(in_2), .pin2(in_3), .pin3(in_4), .pin4(1'b0), .pin5(1'b0), .pin6(1'b1), .pin7(nJMP), .pin8(1'b0),
    .pin9(ST), .pin10(SUB), .pin11(ADD), .pin12(XOR), .pin13(OR), .pin14(AND), .pin15(LOAD), .pin16(1'b1));
  Monoflop monoflop_1 (.C(LD), .R(1'b0), .Q(SETC), .nQ(RES));
  Monoflop monoflop_2 (.C(button_1_out), .R(1'b0), .Q(LD_t), .nQ(LD));
  Button button_1 (.out(button_1_out));
  DiodeBackward diodebackward_1 (.in(LOAD), .out(diodebackward_1_out));
  Monoflop monoflop_3 (.C(button_2_out), .R(1'b0), .nQ(nCLRPC));  // open: Q
  Button button_2 (.out(button_2_out));
  _74165 U4 (
    .pin1(LD), .pin2(GCLK), .pin3(D3), .pin4(D2), .pin5(D1), .pin6(D0), .pin8(1'b0), .pin9(Bout),
    .pin10(U3_pin9), .pin11(D7), .pin12(D6), .pin13(D5), .pin14(D4), .pin15(1'b0), .pin16(1'b1));  // open: pin7
  _74595 U16 (
    .pin1(BUS6), .pin2(BUS5), .pin3(BUS4), .pin4(BUS3), .pin5(BUS2), .pin6(BUS1), .pin7(BUS0), .pin8(1'b0),
    .pin10(RES), .pin11(GCLK), .pin12(T0), .pin13(in_13), .pin14(U17_pin9), .pin15(BUS7), .pin16(1'b1));  // open: pin9
  PullUp pullup_1 (.out(diodebackward_1_out));
  DiodeBackward diodebackward_2 (.in(LOAD), .out(diodebackward_2_out));
  DiodeBackward diodebackward_3 (.in(ADD), .out(diodebackward_2_out));
  DiodeBackward diodebackward_4 (.in(SUB), .out(diodebackward_2_out));
  DiodeBackward diodebackward_5 (.in(nJMP), .out(diodebackward_2_out));
  PullUp pullup_2 (.out(pullup_2_out));
  PullUp pullup_3 (.out(diodebackward_2_out));
  DiodeBackward diodebackward_6 (.in(SUB), .out(pullup_2_out));
  PullUp pullup_4 (.out(pullup_4_out));
  DiodeBackward diodebackward_7 (.in(SUB), .out(pullup_4_out));
  DiodeBackward diodebackward_8 (.in(nJMP), .out(diodebackward_8_out));
  PullUp pullup_5 (.out(diodebackward_8_out));
  DiodeBackward diodebackward_9 (.in(AND), .out(diodebackward_9_out));
  DiodeBackward diodebackward_10 (.in(OR), .out(diodebackward_9_out));
  PullUp pullup_6 (.out(diodebackward_9_out));
  PullUp pullup_7 (.out(pullup_7_out));
  DiodeBackward diodebackward_11 (.in(LOAD), .out(pullup_7_out));
  DiodeBackward diodebackward_12 (.in(OR), .out(pullup_7_out));
  DiodeBackward diodebackward_13 (.in(XOR), .out(pullup_7_out));
  DiodeBackward diodebackward_14 (.in(ADD), .out(pullup_7_out));
  DiodeBackward diodebackward_15 (.in(SUB), .out(pullup_7_out));
  DiodeBackward diodebackward_16 (.in(ST), .out(pullup_7_out));
  DiodeBackward diodebackward_17 (.in(nJMP), .out(pullup_7_out));
  _74540 U2 (
    .pin1(1'b0), .pin2(pullup_7_out), .pin3(diodebackward_9_out), .pin4(diodebackward_8_out),
    .pin5(pullup_4_out), .pin6(pullup_2_out), .pin7(diodebackward_2_out), .pin8(diodebackward_1_out),
    .pin9(1'b0), .pin10(1'b0), .pin12(CLA), .pin13(F), .pin14(C), .pin15(nB), .pin16(nA), .pin17(I1),
    .pin18(I0), .pin19(1'b0), .pin20(1'b1));  // open: pin11
  _74541 _74541_1 (
    .pin1(in_12), .pin2(ROM15), .pin3(ROM14), .pin4(ROM13), .pin5(ROM12), .pin6(ROM11), .pin7(ROM10),
    .pin8(ROM9), .pin9(ROM8), .pin10(1'b0), .pin11(D8), .pin12(D9), .pin13(D10), .pin14(D11), .pin15(D12),
    .pin16(D13), .pin17(D14), .pin18(D15), .pin19(in_12), .pin20(1'b1));
  _74541 _74541_2 (
    .pin1(in_12), .pin2(ROM7), .pin3(ROM6), .pin4(ROM5), .pin5(ROM4), .pin6(ROM3), .pin7(ROM2), .pin8(ROM1),
    .pin9(ROM0), .pin10(1'b0), .pin11(D0), .pin12(D1), .pin13(D2), .pin14(D3), .pin15(D4), .pin16(D5),
    .pin17(D6), .pin18(D7), .pin19(in_12), .pin20(1'b1));
  nand nand_2 (nand_2_out, PCout, PC_Cin);
  xor xor_1 (xor_1_out, PCout, PC_Cin);
  xor xor_2 (xor_2_out, JMP, 1'b1);
  Seven_Seg_Hex seven_seg_hex_13 (.d({A15, A14, A13, A12}), .dp(1'b0));
  Seven_Seg_Hex seven_seg_hex_14 (.d({A11, A10, A9, A8}), .dp(1'b0));
  xor xor_3 (xor_3_out, nand_2_out, 1'b1);
  xor xor_4 (xor_4_out, nRES_COUNT, xor_2_out);
  Seven_Seg_Hex seven_seg_hex_15 (.d({A7, A6, A5, A4}), .dp(1'b0));
  // _27C1024 U24_2: pin names not known; wires that end beside it: 1'b1, 1'b0, ROM15, ROM14, ROM13, ROM12, ROM11, ROM10, ROM9, ROM8, 1'b0, ROM7, ROM6, ROM5, ROM4, ROM3, 1'b1, A15, A14, A13, A12, A11, A10, A9
  nand nand_3 (nand_3_out, xor_1_out, xor_4_out);
  nand nand_4 (nand_4_out, xor_2_out, Bout);
  Seven_Seg_Hex seven_seg_hex_16 (.d({A3, A2, A1, A0}), .dp(1'b0));
  nand nand_5 (PCin, nand_3_out, nand_4_out);
  Seven_Seg_Hex seven_seg_hex_17 (.d({ROM15, ROM14, ROM13, ROM12}), .dp(1'b0));
  Seven_Seg_Hex seven_seg_hex_18 (.d({ROM11, ROM10, ROM9, ROM8}), .dp(1'b0));
  Seven_Seg_Hex seven_seg_hex_19 (.d({ROM7, ROM6, ROM5, ROM4}), .dp(1'b0));
  _74595 U23 (
    .pin1(A14), .pin2(A13), .pin3(A12), .pin4(A11), .pin5(A10), .pin6(A9), .pin7(A8), .pin8(1'b0),
    .pin9(U23_pin9), .pin10(nCLRPC), .pin11(GCLK), .pin12(T0), .pin13(1'b0), .pin14(PCin), .pin15(A15),
    .pin16(1'b1));
  _74595 U22 (
    .pin1(A6), .pin2(A5), .pin3(A4), .pin4(A3), .pin5(A2), .pin6(A1), .pin7(A0), .pin8(1'b0), .pin9(PCout),
    .pin10(nCLRPC), .pin11(GCLK), .pin12(T0), .pin13(1'b0), .pin14(U23_pin9), .pin15(A7), .pin16(1'b1));
  _7474 U29 (
    .pin1(1'b1), .pin2(xor_3_out), .pin3(GCLK), .pin4(LD), .pin5(PC_Cin), .pin7(1'b0), .pin10(1'b1),
    .pin11(1'b1), .pin12(1'b1), .pin13(1'b1), .pin14(1'b1));  // open: pin6, pin8, pin9
  Seven_Seg_Hex seven_seg_hex_20 (.d({ROM3, ROM2, ROM1, ROM0}), .dp(1'b0));
  _74164 U5_2 (
    .pin1(1'b1), .pin2(Fout), .pin3(U5_2_pin6[3]), .pin4(U5_2_pin6[2]), .pin5(U5_2_pin6[1]),
    .pin6(U5_2_pin6[0]), .pin7(1'b0), .pin8(GCLK), .pin9(CLR), .pin10(U5_2_pin13[3]), .pin11(U5_2_pin13[2]),
    .pin12(U5_2_pin13[1]), .pin13(U5_2_pin13[0]), .pin14(1'b1));
  Seven_Seg_Hex seven_seg_hex_21 (.d(U5_2_pin6), .dp(1'b0));
  Seven_Seg_Hex seven_seg_hex_22 (.d(U5_2_pin13), .dp(1'b0));
  Seven_Seg_Hex seven_seg_hex_23 (.d(U6_2_pin6), .dp(1'b0));
  Seven_Seg_Hex seven_seg_hex_24 (.d({U6_2_pin10, AC0}), .dp(1'b0));
  _74164 U6_2 (
    .pin1(1'b1), .pin2(U5_2_pin13[0]), .pin3(U6_2_pin6[3]), .pin4(U6_2_pin6[2]), .pin5(U6_2_pin6[1]),
    .pin6(U6_2_pin6[0]), .pin7(1'b0), .pin8(GCLK), .pin9(CLR), .pin10(U6_2_pin10[3]), .pin11(U6_2_pin10[2]),
    .pin12(U6_2_pin10[1]), .pin13(AC0), .pin14(1'b1));
  xor xor_5 (xor_5_out, AC0, nA);
  xor xor_6 (xor_6_out, nB, Bout);
  nand nand_6 (nand_6_out, SETC, C);
  nand nand_7 (nand_7_out, C, C);
  nand nand_8 (CLR, CLA, LD_t);
  Seven_Seg_Hex seven_seg_hex_25 (.d({BUS15, BUS14, BUS13, BUS12}), .dp(1'b0));
  xor xor_7 (xor_7_out, xor_5_out, xor_6_out);
  nand nand_9 (nand_9_out, nand_7_out, LD_t);
  Seven_Seg_Hex seven_seg_hex_26 (.d({BUS11, BUS10, BUS9, BUS8}), .dp(1'b0));
  Seven_Seg_Hex seven_seg_hex_27 (.d({BUS7, BUS6, BUS5, BUS4}), .dp(1'b0));
  xor xor_8 (xor_8_out, xor_7_out, Cin);
  nand nand_10 (nand_10_out, xor_7_out, Cin);
  nand nand_11 (nand_11_out, xor_5_out, xor_6_out);
  Seven_Seg_Hex seven_seg_hex_28 (.d({BUS3, BUS2, BUS1, BUS0}), .dp(1'b0));
  nand nand_12 (RST, RES, nand_13_out);
  nand nand_13 (nand_13_out, RST, T0);
  nand nand_14 (nand_14_out, clk, clk);
  Seven_Seg_Hex seven_seg_hex_29 (.d({D15, D14, D13, D12}), .dp(1'b0));
  nand nand_15 (nand_15_out, nand_10_out, nand_11_out);
  Seven_Seg_Hex seven_seg_hex_30 (.d({D11, D10, D9, D8}), .dp(1'b0));
  nand nand_16 (GCLK, RST, nand_14_out);
  Seven_Seg_Hex seven_seg_hex_31 (.d({D7, D6, D5, D4}), .dp(1'b0));
  nand nand_17 (nand_17_out, xor_8_out, I0);
  nand nand_18 (nand_18_out, I1, nand_15_out);
  nand nand_19 (nand_19_out, nand_15_out, F);
  Seven_Seg_Hex seven_seg_hex_32 (.d({D3, D2, D1, D0}), .dp(1'b0));
  nand nand_20 (Fout, nand_17_out, nand_18_out);
  nand nand_21 (Cout, nand_19_out, nand_19_out);
  _74161 U7_2 (
    .pin1(RST), .pin2(clk), .pin3(1'b0), .pin4(1'b0), .pin5(1'b0), .pin6(1'b0), .pin7(1'b1), .pin8(1'b0),
    .pin9(1'b1), .pin10(1'b1), .pin11(U7_2_pin11[3]), .pin12(U7_2_pin11[2]), .pin13(U7_2_pin11[1]),
    .pin14(U7_2_pin11[0]), .pin15(RCO), .pin16(1'b1));
  DiodeForward diodeforward_17 (.in(BUS15), .out(diodeforward_17_out));
  DiodeForward diodeforward_18 (.in(BUS14), .out(diodeforward_17_out));
  DiodeForward diodeforward_19 (.in(BUS13), .out(diodeforward_17_out));
  DiodeForward diodeforward_20 (.in(BUS12), .out(diodeforward_17_out));
  DiodeForward diodeforward_21 (.in(BUS11), .out(diodeforward_17_out));
  DiodeForward diodeforward_22 (.in(BUS10), .out(diodeforward_17_out));
  DiodeForward diodeforward_23 (.in(BUS9), .out(diodeforward_17_out));
  DiodeForward diodeforward_24 (.in(BUS8), .out(diodeforward_17_out));
  DiodeForward diodeforward_25 (.in(BUS7), .out(diodeforward_17_out));
  DiodeForward diodeforward_26 (.in(BUS6), .out(diodeforward_17_out));
  DiodeForward diodeforward_27 (.in(BUS5), .out(diodeforward_17_out));
  DiodeForward diodeforward_28 (.in(BUS4), .out(diodeforward_17_out));
  DiodeForward diodeforward_29 (.in(BUS3), .out(diodeforward_17_out));
  DiodeForward diodeforward_30 (.in(BUS2), .out(diodeforward_17_out));
  DiodeForward diodeforward_31 (.in(BUS1), .out(diodeforward_17_out));
  DiodeForward diodeforward_32 (.in(BUS0), .out(diodeforward_17_out));
  PullDown pulldown_2 (.out(diodeforward_17_out));
  _7474 _7474_1 (
    .pin1(nand_9_out), .pin2(Cout), .pin3(GCLK), .pin4(nand_6_out), .pin5(Cin), .pin7(1'b0), .pin8(T0),
    .pin9(IX), .pin10(1'b1), .pin11(clk), .pin12(RCO), .pin13(1'b1), .pin14(1'b1));  // open: pin6
  nand nand_22 (ZERO, diodeforward_17_out, diodeforward_17_out);
  LED led_1 (.in(ZERO));
  Seven_Seg_Hex seven_seg_hex_33 (.d(U7_2_pin11), .dp(1'b0));
  LED led_2 (.in(Cin));

  // Other names for the same wires on the sheet: Aout = AC0; nCE = in_15; nLD = LD; nLDSW = nCLRPC; nOE = READ;
  //   nR = T0; nRES = RES; nWE = in_13

  // Notes on the sheet:
  //   clk: Hz: 2147483647
  //   nRES_COUNT: default 1
  //   JMP: default 1
  //   READ: default 1
  //   in_15: default 1
  //   Main Registers & RAM (8 ICs)
  //   RAM ADDRESS
  //   U19C
  //   Zero Detect
  //   16 bit Accumulator A
  //   RAM Address Register
  //   BUS DATA
  //   Bus Read Register B
  //   S1     S0       MODE
  //   0          0       HOLD
  //   0          1       RIGHT
  //   1          0       LEFT
  //   1          1       LOAD
  //   ACCUMULATOR
  //   BUS Write Register
  //   RAM HI
  //   RAM LO
  //   spider 0
  //   Instruction Decode
  //   STEP/RUN
  //   16 bit Shift Register B
  //   CLR PC
  //   CLA
  //   C
  //   F
  //   ~B
  //   ~A
  //   I0
  //   I1
  //   LOAD
  //   AND
  //   OR
  //   XOR
  //   ADD
  //   SUB
  //   STORE
  //   JMP
  //   U28A
  //   U27A
  //   U27D
  //   U27C
  //   U27B
  //   16-bit ROM
  //   U28C
  //   U28B
  //   Carry is only set before Bit 0 of an operation
  //   Program Counter
  //   U28D
  //   PC Carry  and Zero FF
  //   ROM Data
  //   16 bit Shift Register A
  //   ALU
  //   CLR ACC
  //   Spider 0 Bit serial CPU Testbed
  //   Any residual carry is cleared before an operation
  //   Suppress Carry
  //   Clock Sequencer
  //   # Clock
  //   Carry FF
  //   CARRY
endmodule
