// Digital circuit UD_counter.dig as structural Verilog
module UD_counter (
  input  nRES_INC,
  input  nBRA,
  input  A,
  input  B,
  input  Cin,
  input  nADD,
  output SUM,
  output Cout
);

  wire Ain, and_1_out, Bin, Bout, Cin_t, GCLK, nA, nand_1_out, nand_2_out, nand_3_out, nand_4_out,
       nand_5_out, nand_6_out, nand_7_out, nB, nLOAD, not_1_out, PC_Cin, PCin, PCout, xor_1_out, xor_2_out,
       xor_3_out, xor_4_out, xor_5_out, xor_6_out, xor_7_out, xor_8_out, xor_9_out;

  xor xor_1 (xor_1_out, Ain, nA);
  xor xor_2 (xor_2_out, nB, Bin);
  xor xor_3 (xor_3_out, A, nADD);
  xor xor_4 (xor_4_out, nADD, Cin);
  xor xor_5 (xor_5_out, xor_1_out, xor_2_out);
  and and_1 (and_1_out, PCout, PC_Cin);
  xor xor_6 (xor_6_out, PCout, PC_Cin);
  not not_1 (not_1_out, nBRA);
  xor xor_7 (xor_7_out, nRES_INC, not_1_out);
  xor xor_8 (xor_8_out, A, B);
  nand nand_1 (nand_1_out, xor_3_out, B);
  xor xor_9 (xor_9_out, xor_5_out, Cin_t);
  nand nand_2 (nand_2_out, xor_5_out, Cin_t);
  nand nand_3 (nand_3_out, xor_1_out, xor_2_out);
  nand nand_4 (nand_4_out, xor_6_out, xor_7_out);
  nand nand_5 (nand_5_out, not_1_out, Bout);
  nand nand_6 (nand_6_out, xor_8_out, xor_4_out);
  nand nand_7 (nand_7_out, nand_2_out, nand_3_out);
  nand nand_8 (PCin, nand_4_out, nand_5_out);
  xor xor_10 (SUM, xor_8_out, Cin);
  nand nand_9 (Cout, nand_6_out, nand_1_out);
  _7474 U3 (
    .pin1(1'b1), .pin2(and_1_out), .pin3(GCLK), .pin4(nLOAD), .pin5(PC_Cin), .pin7(1'b0), .pin10(1'b1),
    .pin11(1'b1), .pin12(1'b1), .pin13(1'b1), .pin14(1'b1));  // open: pin6, pin8, pin9

  // Notes on the sheet:
  //   nRES_INC: default 1
  //   nBRA: default 1
  //   Invert A / B
  //   Carry Input
  //   Full Adder/Subtractor
  //   U16A
  //   U17A
  //   Full Adder
  //   U17B
  //   Carry is only set before Bit 0 of an operation
  //   U16C
  //   U16B
  //   U16D
  //   Multiplexer
  //   PC Carry  FF
endmodule
