// Digital circuit UD_counter_2.dig as structural Verilog
module UD_counter_2 (
  input  CK,
  input  in_6,
  output A0,
  output A1,
  output A2,
  output A3
);

  wire A4, A5, A6, A7, LDA, nand_2_out, nand_3_out, nand_4_out, nand_5_out, nand_6_out, nand_7_out,
       nand_8_out, nand_9_out, nand_10_out, nand_11_out, nand_12_out, nand_13_out, nand_14_out, nand_15_out,
       nand_16_out, nand_17_out, nand_18_out, nand_19_out, nand_20_out, nand_21_out, nand_22_out,
       nand_23_out, nand_24_out, nand_25_out, nand_26_out, nand_27_out, nand_28_out, nand_29_out,
       nand_31_out, nand_33_out, nand_35_out, nand_37_out, nand_38_out, nand_39_out, nand_40_out,
       nand_41_out, nand_42_out, nand_43_out, nand_44_out, nand_45_out;

  Seven_Seg_Hex seven_seg_hex_1 (.d({A7, A6, A5, A4}), .dp(1'b0));
  Seven_Seg_Hex seven_seg_hex_2 (.d({A3, A2, A1, A0}), .dp(1'b0));
  nand nand_1 (LDA, in_6, in_6);
  nand nand_2 (nand_2_out, nand_31_out, A2);
  nand nand_3 (nand_3_out, nand_2_out, A2);
  nand nand_4 (nand_4_out, nand_33_out, A1);
  nand nand_5 (nand_5_out, nand_4_out, A1);
  nand nand_6 (nand_6_out, nand_35_out, A0);
  nand nand_7 (nand_7_out, nand_6_out, A0);
  nand nand_8 (nand_8_out, nand_37_out, CK);
  nand nand_9 (nand_9_out, nand_8_out, CK);
  nand nand_10 (nand_10_out, nand_2_out, nand_11_out);
  nand nand_11 (nand_11_out, nand_10_out, nand_3_out);
  nand nand_12 (nand_12_out, A2, A2);
  nand nand_13 (nand_13_out, nand_4_out, nand_14_out);
  nand nand_14 (nand_14_out, nand_13_out, nand_5_out);
  nand nand_15 (nand_15_out, A1, A1);
  nand nand_16 (nand_16_out, nand_6_out, nand_17_out);
  nand nand_17 (nand_17_out, nand_16_out, nand_7_out);
  nand nand_18 (nand_18_out, A0, A0);
  nand nand_19 (nand_19_out, nand_8_out, nand_20_out);
  nand nand_20 (nand_20_out, nand_19_out, nand_9_out);
  nand nand_21 (nand_21_out, CK, CK);
  nand nand_22 (nand_22_out, nand_10_out, nand_12_out);
  nand nand_23 (nand_23_out, nand_22_out, nand_12_out);
  nand nand_24 (nand_24_out, nand_13_out, nand_15_out);
  nand nand_25 (nand_25_out, nand_24_out, nand_15_out);
  nand nand_26 (nand_26_out, nand_16_out, nand_18_out);
  nand nand_27 (nand_27_out, nand_26_out, nand_18_out);
  nand nand_28 (nand_28_out, nand_19_out, nand_21_out);
  nand nand_29 (nand_29_out, nand_28_out, nand_21_out);
  nand nand_30 (A7, nand_22_out, nand_31_out);
  nand nand_31 (nand_31_out, A7, nand_23_out);
  nand nand_32 (A6, nand_24_out, nand_33_out);
  nand nand_33 (nand_33_out, A6, nand_25_out);
  nand nand_34 (A5, nand_26_out, nand_35_out);
  nand nand_35 (nand_35_out, A5, nand_27_out);
  nand nand_36 (A4, nand_28_out, nand_37_out);
  nand nand_37 (nand_37_out, A4, nand_29_out);
  nand nand_38 (nand_38_out, A7, in_6);
  nand nand_39 (nand_39_out, nand_31_out, LDA);
  nand nand_40 (nand_40_out, A6, in_6);
  nand nand_41 (nand_41_out, nand_33_out, LDA);
  nand nand_42 (nand_42_out, A5, in_6);
  nand nand_43 (nand_43_out, nand_35_out, LDA);
  nand nand_44 (nand_44_out, A4, in_6);
  nand nand_45 (nand_45_out, nand_37_out, LDA);
  nand nand_46 (A3, nand_38_out, nand_39_out);
  nand nand_47 (A2, nand_40_out, nand_41_out);
  nand nand_48 (A1, nand_42_out, nand_43_out);
  nand nand_49 (A0, nand_44_out, nand_45_out);

  // Other names for the same wires on the sheet: HLDA = in_6

  // Notes on the sheet:
  //   ADDRESS
  //   8-bit Register
endmodule
