// Digital circuit UD_counter_20gates.dig as structural Verilog
module UD_counter_20gates (
  input  D0,
  input  CLK,
  input  I1,
  input  I0,
  input  Cin,
  input  D1,
  input  D2,
  input  D3,
  input  D4,
  input  D5,
  input  D6,
  input  D7,
  output Q0,
  output Q1,
  output Q2,
  output Q3,
  output Q4,
  output Q5,
  output Q6,
  output Q7,
  output Cout
);

  wire F0, F1, F2, F3, F4, F5, F6, F7, nand_1_out, nand_2_out, nand_3_out, nand_4_out, nand_5_out,
       nand_6_out, nand_7_out, nand_8_out, nand_9_out, nand_10_out, nand_11_out, nand_12_out, nand_13_out,
       nand_14_out, nand_15_out, nand_16_out, nand_17_out, nand_18_out, nand_19_out, nand_20_out,
       nand_21_out, nand_22_out, nand_23_out, nand_24_out, nand_25_out, nand_26_out, nand_27_out,
       nand_28_out, nand_29_out, nand_30_out, nand_31_out, nand_32_out, nand_33_out, nand_34_out,
       nand_35_out, nand_36_out, nand_37_out, nand_38_out, nand_39_out, nand_40_out, nand_41_out,
       nand_42_out, nand_44_out, nand_45_out, nand_46_out, nand_47_out, nand_48_out, nand_49_out,
       nand_50_out, nand_51_out, nand_52_out, nand_53_out, nand_54_out, nand_55_out, nand_56_out,
       nand_57_out, nand_58_out, nand_59_out, nand_60_out, nand_61_out, nand_62_out, nand_63_out,
       nand_64_out, nand_73_out, nand_74_out, nand_75_out, nand_76_out, nand_77_out, nand_78_out,
       nand_79_out, nand_80_out, nand_81_out, nand_82_out, nand_83_out, nand_84_out, nand_85_out,
       nand_86_out, nand_87_out, nand_88_out, nand_89_out, nand_90_out, nand_91_out, nand_92_out,
       nand_93_out, nand_94_out, nand_95_out, nand_96_out, nand_97_out, nand_98_out, nand_99_out,
       nand_100_out, nand_101_out, nand_102_out, nand_103_out, nand_104_out, nand_105_out, nand_106_out,
       nand_107_out, nand_108_out, nand_109_out, nand_110_out, nand_111_out, nand_112_out, nand_113_out,
       nand_114_out, nand_115_out, nand_116_out, nand_117_out, nand_118_out, nand_119_out, nand_120_out,
       nand_121_out, nand_122_out, nand_123_out, nand_124_out, nand_125_out, nand_126_out, nand_127_out,
       nand_128_out, nand_129_out, nand_130_out, nand_131_out, nand_132_out, nand_133_out, nand_134_out,
       nand_135_out, nand_136_out, nand_137_out, nand_138_out, nand_139_out, nand_140_out, nand_141_out,
       nand_142_out, nand_143_out, nand_144_out, nand_145_out, nand_146_out, nand_147_out, nand_148_out,
       nand_149_out, nand_150_out, nand_151_out, nand_152_out, nand_153_out;

  Seven_Seg_Hex seven_seg_hex_1 (.d({F7, F6, F5, F4}), .dp(1'b0));
  Seven_Seg_Hex seven_seg_hex_2 (.d({F3, F2, F1, F0}), .dp(1'b0));
  Seven_Seg_Hex seven_seg_hex_3 (.d({Q7, Q6, Q5, Q4}), .dp(1'b0));
  Seven_Seg_Hex seven_seg_hex_4 (.d({Q3, Q2, Q1, Q0}), .dp(1'b0));
  Seven_Seg_Hex seven_seg_hex_5 (.d({D7, D6, D5, D4}), .dp(1'b0));
  Seven_Seg_Hex seven_seg_hex_6 (.d({D3, D2, D1, D0}), .dp(1'b0));
  nand nand_1 (nand_1_out, Q7, D7);
  nand nand_2 (nand_2_out, Q6, D6);
  nand nand_3 (nand_3_out, Q5, D5);
  nand nand_4 (nand_4_out, Q4, D4);
  nand nand_5 (nand_5_out, Q3, D3);
  nand nand_6 (nand_6_out, Q2, D2);
  nand nand_7 (nand_7_out, Q1, D1);
  nand nand_8 (nand_8_out, Q0, D0);
  nand nand_9 (nand_9_out, Q7, nand_1_out);
  nand nand_10 (nand_10_out, nand_1_out, D7);
  nand nand_11 (nand_11_out, Q6, nand_2_out);
  nand nand_12 (nand_12_out, nand_2_out, D6);
  nand nand_13 (nand_13_out, Q5, nand_3_out);
  nand nand_14 (nand_14_out, nand_3_out, D5);
  nand nand_15 (nand_15_out, Q4, nand_4_out);
  nand nand_16 (nand_16_out, nand_4_out, D4);
  nand nand_17 (nand_17_out, Q3, nand_5_out);
  nand nand_18 (nand_18_out, nand_5_out, D3);
  nand nand_19 (nand_19_out, Q2, nand_6_out);
  nand nand_20 (nand_20_out, nand_6_out, D2);
  nand nand_21 (nand_21_out, Q1, nand_7_out);
  nand nand_22 (nand_22_out, nand_7_out, D1);
  nand nand_23 (nand_23_out, Q0, nand_8_out);
  nand nand_24 (nand_24_out, nand_8_out, D0);
  nand nand_25 (nand_25_out, nand_9_out, nand_10_out);
  nand nand_26 (nand_26_out, nand_11_out, nand_12_out);
  nand nand_27 (nand_27_out, nand_13_out, nand_14_out);
  nand nand_28 (nand_28_out, nand_15_out, nand_16_out);
  nand nand_29 (nand_29_out, nand_17_out, nand_18_out);
  nand nand_30 (nand_30_out, nand_19_out, nand_20_out);
  nand nand_31 (nand_31_out, nand_21_out, nand_22_out);
  nand nand_32 (nand_32_out, nand_23_out, nand_24_out);
  nand nand_33 (nand_33_out, nand_25_out, nand_46_out);
  nand nand_34 (nand_34_out, nand_26_out, nand_49_out);
  nand nand_35 (nand_35_out, nand_27_out, nand_52_out);
  nand nand_36 (nand_36_out, nand_28_out, nand_55_out);
  nand nand_37 (nand_37_out, nand_29_out, nand_58_out);
  nand nand_38 (nand_38_out, nand_30_out, nand_61_out);
  nand nand_39 (nand_39_out, nand_31_out, nand_64_out);
  nand nand_40 (nand_40_out, nand_32_out, Cin);
  nand nand_41 (nand_41_out, nand_25_out, nand_33_out);
  nand nand_42 (nand_42_out, nand_33_out, nand_46_out);
  nand nand_43 (Cout, nand_33_out, nand_1_out);
  nand nand_44 (nand_44_out, nand_26_out, nand_34_out);
  nand nand_45 (nand_45_out, nand_34_out, nand_49_out);
  nand nand_46 (nand_46_out, nand_34_out, nand_2_out);
  nand nand_47 (nand_47_out, nand_27_out, nand_35_out);
  nand nand_48 (nand_48_out, nand_35_out, nand_52_out);
  nand nand_49 (nand_49_out, nand_35_out, nand_3_out);
  nand nand_50 (nand_50_out, nand_28_out, nand_36_out);
  nand nand_51 (nand_51_out, nand_36_out, nand_55_out);
  nand nand_52 (nand_52_out, nand_36_out, nand_4_out);
  nand nand_53 (nand_53_out, nand_29_out, nand_37_out);
  nand nand_54 (nand_54_out, nand_37_out, nand_58_out);
  nand nand_55 (nand_55_out, nand_37_out, nand_5_out);
  nand nand_56 (nand_56_out, nand_30_out, nand_38_out);
  nand nand_57 (nand_57_out, nand_38_out, nand_61_out);
  nand nand_58 (nand_58_out, nand_38_out, nand_6_out);
  nand nand_59 (nand_59_out, nand_31_out, nand_39_out);
  nand nand_60 (nand_60_out, nand_39_out, nand_64_out);
  nand nand_61 (nand_61_out, nand_39_out, nand_7_out);
  nand nand_62 (nand_62_out, nand_32_out, nand_40_out);
  nand nand_63 (nand_63_out, nand_40_out, Cin);
  nand nand_64 (nand_64_out, nand_40_out, nand_8_out);
  nand nand_65 (F7, nand_41_out, nand_42_out);
  nand nand_66 (F6, nand_44_out, nand_45_out);
  nand nand_67 (F5, nand_47_out, nand_48_out);
  nand nand_68 (F4, nand_50_out, nand_51_out);
  nand nand_69 (F3, nand_53_out, nand_54_out);
  nand nand_70 (F2, nand_56_out, nand_57_out);
  nand nand_71 (F1, nand_59_out, nand_60_out);
  nand nand_72 (F0, nand_62_out, nand_63_out);
  nand nand_73 (nand_73_out, CLK, CLK);
  nand nand_74 (nand_74_out, F7, nand_73_out);
  nand nand_75 (nand_75_out, nand_74_out, nand_73_out);
  nand nand_76 (nand_76_out, F6, nand_73_out);
  nand nand_77 (nand_77_out, nand_76_out, nand_73_out);
  nand nand_78 (nand_78_out, F5, nand_73_out);
  nand nand_79 (nand_79_out, nand_78_out, nand_73_out);
  nand nand_80 (nand_80_out, F4, nand_73_out);
  nand nand_81 (nand_81_out, nand_80_out, nand_73_out);
  nand nand_82 (nand_82_out, F3, nand_73_out);
  nand nand_83 (nand_83_out, nand_82_out, nand_73_out);
  nand nand_84 (nand_84_out, F2, nand_73_out);
  nand nand_85 (nand_85_out, nand_84_out, nand_73_out);
  nand nand_86 (nand_86_out, F1, nand_73_out);
  nand nand_87 (nand_87_out, nand_86_out, nand_73_out);
  nand nand_88 (nand_88_out, F0, nand_73_out);
  nand nand_89 (nand_89_out, nand_88_out, nand_73_out);
  nand nand_90 (nand_90_out, nand_74_out, nand_91_out);
  nand nand_91 (nand_91_out, nand_90_out, nand_75_out);
  nand nand_92 (nand_92_out, nand_76_out, nand_93_out);
  nand nand_93 (nand_93_out, nand_92_out, nand_77_out);
  nand nand_94 (nand_94_out, nand_78_out, nand_95_out);
  nand nand_95 (nand_95_out, nand_94_out, nand_79_out);
  nand nand_96 (nand_96_out, nand_80_out, nand_97_out);
  nand nand_97 (nand_97_out, nand_96_out, nand_81_out);
  nand nand_98 (nand_98_out, nand_82_out, nand_99_out);
  nand nand_99 (nand_99_out, nand_98_out, nand_83_out);
  nand nand_100 (nand_100_out, nand_84_out, nand_101_out);
  nand nand_101 (nand_101_out, nand_100_out, nand_85_out);
  nand nand_102 (nand_102_out, nand_86_out, nand_103_out);
  nand nand_103 (nand_103_out, nand_102_out, nand_87_out);
  nand nand_104 (nand_104_out, nand_88_out, nand_105_out);
  nand nand_105 (nand_105_out, nand_104_out, nand_89_out);
  nand nand_106 (nand_106_out, nand_90_out, CLK);
  nand nand_107 (nand_107_out, nand_106_out, CLK);
  nand nand_108 (nand_108_out, nand_92_out, CLK);
  nand nand_109 (nand_109_out, nand_108_out, CLK);
  nand nand_110 (nand_110_out, nand_94_out, CLK);
  nand nand_111 (nand_111_out, nand_110_out, CLK);
  nand nand_112 (nand_112_out, nand_96_out, CLK);
  nand nand_113 (nand_113_out, nand_112_out, CLK);
  nand nand_114 (nand_114_out, nand_98_out, CLK);
  nand nand_115 (nand_115_out, nand_114_out, CLK);
  nand nand_116 (nand_116_out, nand_100_out, CLK);
  nand nand_117 (nand_117_out, nand_116_out, CLK);
  nand nand_118 (nand_118_out, nand_102_out, CLK);
  nand nand_119 (nand_119_out, nand_118_out, CLK);
  nand nand_120 (nand_120_out, nand_104_out, CLK);
  nand nand_121 (nand_121_out, nand_120_out, CLK);
  nand nand_122 (nand_122_out, nand_106_out, nand_123_out);
  nand nand_123 (nand_123_out, nand_122_out, nand_107_out);
  nand nand_124 (nand_124_out, nand_108_out, nand_125_out);
  nand nand_125 (nand_125_out, nand_124_out, nand_109_out);
  nand nand_126 (nand_126_out, nand_110_out, nand_127_out);
  nand nand_127 (nand_127_out, nand_126_out, nand_111_out);
  nand nand_128 (nand_128_out, nand_112_out, nand_129_out);
  nand nand_129 (nand_129_out, nand_128_out, nand_113_out);
  nand nand_130 (nand_130_out, nand_114_out, nand_131_out);
  nand nand_131 (nand_131_out, nand_130_out, nand_115_out);
  nand nand_132 (nand_132_out, nand_116_out, nand_133_out);
  nand nand_133 (nand_133_out, nand_132_out, nand_117_out);
  nand nand_134 (nand_134_out, nand_118_out, nand_135_out);
  nand nand_135 (nand_135_out, nand_134_out, nand_119_out);
  nand nand_136 (nand_136_out, nand_120_out, nand_137_out);
  nand nand_137 (nand_137_out, nand_136_out, nand_121_out);
  nand nand_138 (nand_138_out, nand_122_out, I0);
  nand nand_139 (nand_139_out, I1, nand_123_out);
  nand nand_140 (nand_140_out, nand_124_out, I0);
  nand nand_141 (nand_141_out, I1, nand_125_out);
  nand nand_142 (nand_142_out, nand_126_out, I0);
  nand nand_143 (nand_143_out, I1, nand_127_out);
  nand nand_144 (nand_144_out, nand_128_out, I0);
  nand nand_145 (nand_145_out, I1, nand_129_out);
  nand nand_146 (nand_146_out, nand_130_out, I0);
  nand nand_147 (nand_147_out, I1, nand_131_out);
  nand nand_148 (nand_148_out, nand_132_out, I0);
  nand nand_149 (nand_149_out, I1, nand_133_out);
  nand nand_150 (nand_150_out, nand_134_out, I0);
  nand nand_151 (nand_151_out, I1, nand_135_out);
  nand nand_152 (nand_152_out, nand_136_out, I0);
  nand nand_153 (nand_153_out, I1, nand_137_out);
  nand nand_154 (Q7, nand_138_out, nand_139_out);
  nand nand_155 (Q6, nand_140_out, nand_141_out);
  nand nand_156 (Q5, nand_142_out, nand_143_out);
  nand nand_157 (Q4, nand_144_out, nand_145_out);
  nand nand_158 (Q3, nand_146_out, nand_147_out);
  nand nand_159 (Q2, nand_148_out, nand_149_out);
  nand nand_160 (Q1, nand_150_out, nand_151_out);
  nand nand_161 (Q0, nand_152_out, nand_153_out);

  // Other names for the same wires on the sheet: AC0 = Q0; AC1 = Q1; AC2 = Q2; AC3 = Q3; AC4 = Q4; AC5 = Q5; AC6 = Q6;
  //   AC7 = Q7

  // Notes on the sheet:
  //   CLK: Hz: 2147483647
  //   ALU
  //   ACC
  //   BUS
  //   8-bit ALU and Accumulator
  //   28 NAND gates per bitslice (7 x 74xx00)
  //   Accumulator made from gated D-type latches
endmodule
