// Digital circuit XOR.dig as structural Verilog
module XOR (
  input  Ain,
  input  Bin,
  input  Cin,
  output Fout,
  output Cout
);

  wire nand_1_out, nand_2_out, nand_3_out, nand_4_out, nand_5_out, nand_6_out, nand_7_out, not_1_out,
       not_2_out, not_3_out, not_4_out;

  not not_1 (not_1_out, Cin);
  not not_2 (not_2_out, Ain);
  not not_3 (not_3_out, Bin);
  nand nand_1 (nand_1_out, not_2_out, Bin);
  nand nand_2 (nand_2_out, Ain, not_3_out);
  nand nand_3 (nand_3_out, Bin, Ain);
  nand nand_4 (nand_4_out, nand_1_out, nand_2_out);
  not not_4 (not_4_out, nand_4_out);
  nand nand_5 (nand_5_out, not_4_out, Cin);
  nand nand_6 (nand_6_out, nand_4_out, not_1_out);
  nand nand_7 (nand_7_out, nand_4_out, not_1_out);
  nand nand_8 (Fout, nand_5_out, nand_6_out);
  nand nand_9 (Cout, nand_7_out, nand_3_out);
endmodule
