// Digital circuit XOR_ALU.dig as structural Verilog
module XOR_ALU (
  input  A,
  input  INV_A,
  input  B,
  input  INV_B,
  input  C,
  output Sum,
  output Carry
);

  wire _7400_1_pin3, _7400_1_pin5, _7486_1_pin3, _7486_1_pin5, _7486_1_pin6;

  _7486 _7486_1 (
    .pin1(INV_A), .pin2(A), .pin3(_7486_1_pin3), .pin4(_7486_1_pin3), .pin5(_7486_1_pin5),
    .pin6(_7486_1_pin6), .pin7(1'b0), .pin8(Sum), .pin9(_7486_1_pin6), .pin10(C), .pin11(_7486_1_pin5),
    .pin12(B), .pin13(INV_B), .pin14(1'b1));
  _7400 _7400_1 (
    .pin1(_7486_1_pin5), .pin2(_7486_1_pin3), .pin3(_7400_1_pin3), .pin4(_7400_1_pin3), .pin5(_7400_1_pin5),
    .pin6(Carry), .pin7(1'b0), .pin9(1'b0), .pin10(1'b0), .pin11(_7400_1_pin5), .pin12(C),
    .pin13(_7486_1_pin6), .pin14(1'b1));  // open: pin8
  // _7474 _7474_1: pin names not known
endmodule
