// Digital circuit XOR_from_NAND.dig as structural Verilog
module XOR_from_NAND (
  input  A,
  input  B,
  output Fout,
  output T1,
  output T2,
  output T3
);

  nand nand_1 (T1, A, B);
  nand nand_2 (T2, A, T1);
  nand nand_3 (T3, T1, B);
  nand nand_4 (Fout, T2, T3);

  // Notes on the sheet:
  //   XOR implemented from NAND gates
endmodule
