// Digital circuit Xor_2.dig as structural Verilog
module Xor_2 (
  input  Ain,
  input  Bin,
  output Fout
);

  wire nand_1_out, nand_2_out, not_1_out, not_2_out;

  not not_1 (not_1_out, Ain);
  not not_2 (not_2_out, Bin);
  nand nand_1 (nand_1_out, not_1_out, not_2_out);
  nand nand_2 (nand_2_out, Ain, Bin);
  and and_1 (Fout, nand_1_out, nand_2_out);

  // Other names for the same wires on the sheet: Aout = Ain; Bout = Bin
endmodule
