// Digital circuit ZP_registers.dig as structural Verilog
module ZP_registers (
  input  CLK,
  input  I1,
  input  I0,
  input  Cin,
  input  SC,
  input  INV,
  input  in_16,
  input  in_17,
  input  in_18,
  input  in_19,
  input  in_20,
  input  in_21,
  input  in_22,
  input  in_23,
  input  nCE,
  input  in_25,
  input  in_26,
  input  in_27,
  input  in_28,
  input  in_29,
  input  in_30,
  input  in_31,
  input  in_32,
  input  in_33,
  input  in_34,
  input  in_35,
  input  in_36,
  output Q0,
  output Q1,
  output Q2,
  output Q3,
  output Q4,
  output Q5,
  output Q6,
  output Q7,
  output Cout
);

  wire AC_BUS, BUS0, BUS1, BUS2, BUS3, BUS4, BUS5, BUS6, BUS7, F0, F1, F2, F3, F4, F5, F6, F7, nand_1_out,
       nand_2_out, nand_3_out, nand_4_out, nand_5_out, nand_6_out, nand_7_out, nand_8_out, nand_9_out,
       nand_10_out, nand_11_out, nand_12_out, nand_13_out, nand_14_out, nand_15_out, nand_16_out,
       nand_17_out, nand_18_out, nand_19_out, nand_20_out, nand_21_out, nand_22_out, nand_23_out,
       nand_24_out, nand_26_out, nand_27_out, nand_28_out, nand_29_out, nand_30_out, nand_31_out,
       nand_32_out, nand_33_out, nand_34_out, nand_35_out, nand_36_out, nand_37_out, nand_38_out,
       nand_39_out, nand_40_out, nand_41_out, nand_42_out, nand_43_out, nand_44_out, nand_45_out,
       nand_46_out, nand_47_out, nand_48_out, nand_49_out, nand_50_out, nand_51_out, nand_52_out,
       nand_53_out, nand_54_out, nand_55_out, nand_56_out, nand_57_out, nand_58_out, nand_59_out,
       nand_60_out, nand_61_out, nand_62_out, nand_63_out, nand_64_out, nand_65_out, nand_66_out,
       nand_67_out, nand_68_out, nand_69_out, nand_70_out, nand_71_out, nand_72_out, nand_73_out,
       nand_74_out, nand_75_out, nand_76_out, nand_77_out, nand_78_out, nand_79_out, nand_80_out,
       nand_81_out, nand_82_out, nand_83_out, nand_84_out, nand_85_out, nand_86_out, nand_87_out,
       nand_88_out, nand_89_out, nand_90_out, nand_91_out, nand_92_out, nand_93_out, nand_94_out,
       nand_95_out, nand_96_out, nand_97_out, nand_98_out, nand_99_out, nand_100_out, nand_101_out,
       nand_102_out, nand_103_out, nand_104_out, nand_105_out, nand_106_out, nand_107_out, nand_108_out,
       nand_109_out, nand_110_out, nand_111_out, nand_112_out, nand_113_out, nand_114_out, nand_115_out,
       nand_116_out, nand_117_out, nand_118_out, nand_119_out, nand_120_out, nand_121_out, nand_122_out,
       nand_123_out, nand_124_out, nand_125_out, nand_126_out, nand_127_out, nand_128_out, nand_129_out,
       nand_130_out, nand_131_out, nand_133_out, nand_135_out, nand_138_out, nand_140_out, nand_142_out,
       nand_145_out, nand_147_out, nand_148_out, nand_149_out, nand_150_out, nand_151_out, nand_152_out,
       nand_153_out, nand_154_out, nand_155_out, nand_156_out, nand_157_out, nand_158_out, nand_159_out,
       nand_160_out, nand_161_out, nand_162_out, nand_163_out, nand_164_out, nand_165_out, nand_166_out,
       nand_167_out, nand_168_out, nand_169_out, nand_170_out, nand_171_out, nand_172_out, nand_173_out,
       nand_174_out, nand_175_out, nand_176_out, nand_177_out, nand_178_out, nand_179_out, nand_180_out,
       nand_181_out, nand_182_out, nand_183_out, nand_184_out, nand_185_out, nand_186_out, nand_187_out,
       nand_188_out, nand_189_out, nand_190_out, nand_191_out, nand_192_out, nand_193_out, nand_194_out,
       nand_195_out, nand_196_out, nand_197_out, nand_198_out, nand_199_out, nand_200_out, nand_201_out,
       nand_202_out, nand_204_out, nand_206_out, nand_208_out, nand_210_out, nand_212_out, nand_214_out,
       nand_216_out, nand_218_out, nand_219_out, nand_220_out, nand_221_out;

  Seven_Seg_Hex seven_seg_hex_1 (.d({BUS7, BUS6, BUS5, BUS4}), .dp(1'b0));
  Seven_Seg_Hex seven_seg_hex_2 (.d({BUS3, BUS2, BUS1, BUS0}), .dp(1'b0));
  Seven_Seg_Hex seven_seg_hex_3 (.d({in_20, in_21, in_22, in_23}), .dp(1'b0));
  Seven_Seg_Hex seven_seg_hex_4 (.d({in_19, in_18, in_17, in_16}), .dp(1'b0));
  Seven_Seg_Hex seven_seg_hex_5 (.d({F7, F6, F5, F4}), .dp(1'b0));
  Seven_Seg_Hex seven_seg_hex_6 (.d({F3, F2, F1, F0}), .dp(1'b0));
  Seven_Seg_Hex seven_seg_hex_7 (.d({Q7, Q6, Q5, Q4}), .dp(1'b0));
  Seven_Seg_Hex seven_seg_hex_8 (.d({Q3, Q2, Q1, Q0}), .dp(1'b0));
  Seven_Seg_Hex seven_seg_hex_9 (.d({in_32, in_31, in_30, in_29}), .dp(1'b0));
  Seven_Seg_Hex seven_seg_hex_10 (.d({in_25, in_28, in_27, in_26}), .dp(1'b0));
  nand nand_1 (nand_1_out, in_32, INV);
  nand nand_2 (nand_2_out, in_31, INV);
  nand nand_3 (nand_3_out, in_30, INV);
  nand nand_4 (nand_4_out, in_29, INV);
  nand nand_5 (nand_5_out, in_25, INV);
  nand nand_6 (nand_6_out, in_28, INV);
  nand nand_7 (nand_7_out, in_27, INV);
  nand nand_8 (nand_8_out, in_26, INV);
  nand nand_9 (nand_9_out, in_32, nand_1_out);
  nand nand_10 (nand_10_out, nand_1_out, INV);
  nand nand_11 (nand_11_out, in_31, nand_2_out);
  nand nand_12 (nand_12_out, nand_2_out, INV);
  nand nand_13 (nand_13_out, in_30, nand_3_out);
  nand nand_14 (nand_14_out, nand_3_out, INV);
  nand nand_15 (nand_15_out, in_29, nand_4_out);
  nand nand_16 (nand_16_out, nand_4_out, INV);
  nand nand_17 (nand_17_out, in_25, nand_5_out);
  nand nand_18 (nand_18_out, nand_5_out, INV);
  nand nand_19 (nand_19_out, in_28, nand_6_out);
  nand nand_20 (nand_20_out, nand_6_out, INV);
  nand nand_21 (nand_21_out, in_27, nand_7_out);
  nand nand_22 (nand_22_out, nand_7_out, INV);
  nand nand_23 (nand_23_out, in_26, nand_8_out);
  nand nand_24 (nand_24_out, nand_8_out, INV);
  nand nand_25 (AC_BUS, CLK, CLK);
  nand nand_26 (nand_26_out, nand_9_out, nand_10_out);
  nand nand_27 (nand_27_out, nand_11_out, nand_12_out);
  nand nand_28 (nand_28_out, nand_13_out, nand_14_out);
  nand nand_29 (nand_29_out, nand_15_out, nand_16_out);
  nand nand_30 (nand_30_out, nand_17_out, nand_18_out);
  nand nand_31 (nand_31_out, nand_19_out, nand_20_out);
  nand nand_32 (nand_32_out, nand_21_out, nand_22_out);
  nand nand_33 (nand_33_out, nand_23_out, nand_24_out);
  nand nand_34 (nand_34_out, Q7, nand_26_out);
  nand nand_35 (nand_35_out, Q6, nand_27_out);
  nand nand_36 (nand_36_out, Q5, nand_28_out);
  nand nand_37 (nand_37_out, Q4, nand_29_out);
  nand nand_38 (nand_38_out, Q3, nand_30_out);
  nand nand_39 (nand_39_out, Q2, nand_31_out);
  nand nand_40 (nand_40_out, Q1, nand_32_out);
  nand nand_41 (nand_41_out, Q0, nand_33_out);
  nand nand_42 (nand_42_out, Q7, nand_34_out);
  nand nand_43 (nand_43_out, nand_34_out, nand_34_out);
  nand nand_44 (nand_44_out, nand_34_out, nand_26_out);
  nand nand_45 (nand_45_out, Q6, nand_35_out);
  nand nand_46 (nand_46_out, nand_35_out, nand_35_out);
  nand nand_47 (nand_47_out, nand_35_out, nand_27_out);
  nand nand_48 (nand_48_out, Q5, nand_36_out);
  nand nand_49 (nand_49_out, nand_36_out, nand_36_out);
  nand nand_50 (nand_50_out, nand_36_out, nand_28_out);
  nand nand_51 (nand_51_out, Q4, nand_37_out);
  nand nand_52 (nand_52_out, nand_37_out, nand_37_out);
  nand nand_53 (nand_53_out, nand_37_out, nand_29_out);
  nand nand_54 (nand_54_out, Q3, nand_38_out);
  nand nand_55 (nand_55_out, nand_38_out, nand_38_out);
  nand nand_56 (nand_56_out, nand_38_out, nand_30_out);
  nand nand_57 (nand_57_out, Q2, nand_39_out);
  nand nand_58 (nand_58_out, nand_39_out, nand_39_out);
  nand nand_59 (nand_59_out, nand_39_out, nand_31_out);
  nand nand_60 (nand_60_out, Q1, nand_40_out);
  nand nand_61 (nand_61_out, nand_40_out, nand_40_out);
  nand nand_62 (nand_62_out, nand_40_out, nand_32_out);
  nand nand_63 (nand_63_out, Q0, nand_41_out);
  nand nand_64 (nand_64_out, nand_41_out, nand_41_out);
  nand nand_65 (nand_65_out, nand_41_out, nand_33_out);
  nand nand_66 (nand_66_out, nand_42_out, nand_44_out);
  nand nand_67 (nand_67_out, nand_45_out, nand_47_out);
  nand nand_68 (nand_68_out, nand_48_out, nand_50_out);
  nand nand_69 (nand_69_out, nand_51_out, nand_53_out);
  nand nand_70 (nand_70_out, nand_54_out, nand_56_out);
  nand nand_71 (nand_71_out, nand_57_out, nand_59_out);
  nand nand_72 (nand_72_out, nand_60_out, nand_62_out);
  nand nand_73 (nand_73_out, nand_63_out, nand_65_out);
  nand nand_74 (nand_74_out, nand_43_out, I1);
  nand nand_75 (nand_75_out, nand_66_out, I0);
  nand nand_76 (nand_76_out, nand_46_out, I1);
  nand nand_77 (nand_77_out, nand_67_out, I0);
  nand nand_78 (nand_78_out, nand_49_out, I1);
  nand nand_79 (nand_79_out, nand_68_out, I0);
  nand nand_80 (nand_80_out, nand_52_out, I1);
  nand nand_81 (nand_81_out, nand_69_out, I0);
  nand nand_82 (nand_82_out, nand_55_out, I1);
  nand nand_83 (nand_83_out, nand_70_out, I0);
  nand nand_84 (nand_84_out, nand_58_out, I1);
  nand nand_85 (nand_85_out, nand_71_out, I0);
  nand nand_86 (nand_86_out, nand_61_out, I1);
  nand nand_87 (nand_87_out, nand_72_out, I0);
  nand nand_88 (nand_88_out, nand_64_out, I1);
  nand nand_89 (nand_89_out, nand_73_out, I0);
  nand nand_90 (nand_90_out, nand_74_out, nand_75_out);
  nand nand_91 (nand_91_out, nand_76_out, nand_77_out);
  nand nand_92 (nand_92_out, nand_78_out, nand_79_out);
  nand nand_93 (nand_93_out, nand_80_out, nand_81_out);
  nand nand_94 (nand_94_out, nand_82_out, nand_83_out);
  nand nand_95 (nand_95_out, nand_84_out, nand_85_out);
  nand nand_96 (nand_96_out, nand_86_out, nand_87_out);
  nand nand_97 (nand_97_out, nand_88_out, nand_89_out);
  nand nand_98 (nand_98_out, nand_90_out, nand_147_out);
  nand nand_99 (nand_99_out, nand_91_out, nand_148_out);
  nand nand_100 (nand_100_out, nand_92_out, nand_149_out);
  nand nand_101 (nand_101_out, nand_93_out, nand_150_out);
  nand nand_102 (nand_102_out, nand_94_out, nand_151_out);
  nand nand_103 (nand_103_out, nand_95_out, nand_152_out);
  nand nand_104 (nand_104_out, nand_96_out, nand_153_out);
  nand nand_105 (nand_105_out, nand_97_out, Cin);
  nand nand_106 (nand_106_out, nand_90_out, nand_98_out);
  nand nand_107 (nand_107_out, nand_98_out, nand_147_out);
  nand nand_108 (nand_108_out, nand_98_out, nand_34_out);
  nand nand_109 (nand_109_out, nand_91_out, nand_99_out);
  nand nand_110 (nand_110_out, nand_99_out, nand_148_out);
  nand nand_111 (nand_111_out, nand_99_out, nand_35_out);
  nand nand_112 (nand_112_out, nand_92_out, nand_100_out);
  nand nand_113 (nand_113_out, nand_100_out, nand_149_out);
  nand nand_114 (nand_114_out, nand_100_out, nand_36_out);
  nand nand_115 (nand_115_out, nand_93_out, nand_101_out);
  nand nand_116 (nand_116_out, nand_101_out, nand_150_out);
  nand nand_117 (nand_117_out, nand_101_out, nand_37_out);
  nand nand_118 (nand_118_out, nand_94_out, nand_102_out);
  nand nand_119 (nand_119_out, nand_102_out, nand_151_out);
  nand nand_120 (nand_120_out, nand_102_out, nand_38_out);
  nand nand_121 (nand_121_out, nand_95_out, nand_103_out);
  nand nand_122 (nand_122_out, nand_103_out, nand_152_out);
  nand nand_123 (nand_123_out, nand_103_out, nand_39_out);
  nand nand_124 (nand_124_out, nand_96_out, nand_104_out);
  nand nand_125 (nand_125_out, nand_104_out, nand_153_out);
  nand nand_126 (nand_126_out, nand_104_out, nand_40_out);
  nand nand_127 (nand_127_out, nand_97_out, nand_105_out);
  nand nand_128 (nand_128_out, nand_105_out, Cin);
  nand nand_129 (nand_129_out, nand_105_out, nand_41_out);
  nand nand_130 (nand_130_out, nand_114_out, SC);
  nand nand_131 (nand_131_out, nand_126_out, SC);
  nand nand_132 (F7, nand_106_out, nand_107_out);
  nand nand_133 (nand_133_out, nand_108_out, SC);
  nand nand_134 (F6, nand_109_out, nand_110_out);
  nand nand_135 (nand_135_out, nand_111_out, SC);
  nand nand_136 (F5, nand_112_out, nand_113_out);
  nand nand_137 (F4, nand_115_out, nand_116_out);
  nand nand_138 (nand_138_out, nand_117_out, SC);
  nand nand_139 (F3, nand_118_out, nand_119_out);
  nand nand_140 (nand_140_out, nand_120_out, SC);
  nand nand_141 (F2, nand_121_out, nand_122_out);
  nand nand_142 (nand_142_out, nand_123_out, SC);
  nand nand_143 (F1, nand_124_out, nand_125_out);
  nand nand_144 (F0, nand_127_out, nand_128_out);
  nand nand_145 (nand_145_out, nand_129_out, SC);
  nand nand_146 (Cout, nand_133_out, nand_133_out);
  nand nand_147 (nand_147_out, nand_135_out, nand_135_out);
  nand nand_148 (nand_148_out, nand_130_out, nand_130_out);
  nand nand_149 (nand_149_out, nand_138_out, nand_138_out);
  nand nand_150 (nand_150_out, nand_140_out, nand_140_out);
  nand nand_151 (nand_151_out, nand_142_out, nand_142_out);
  nand nand_152 (nand_152_out, nand_131_out, nand_131_out);
  nand nand_153 (nand_153_out, nand_145_out, nand_145_out);
  nand nand_154 (nand_154_out, CLK, CLK);
  nand nand_155 (nand_155_out, F7, nand_154_out);
  nand nand_156 (nand_156_out, nand_155_out, nand_154_out);
  nand nand_157 (nand_157_out, F6, nand_154_out);
  nand nand_158 (nand_158_out, nand_157_out, nand_154_out);
  nand nand_159 (nand_159_out, F5, nand_154_out);
  nand nand_160 (nand_160_out, nand_159_out, nand_154_out);
  nand nand_161 (nand_161_out, F4, nand_154_out);
  nand nand_162 (nand_162_out, nand_161_out, nand_154_out);
  nand nand_163 (nand_163_out, F3, nand_154_out);
  nand nand_164 (nand_164_out, nand_163_out, nand_154_out);
  nand nand_165 (nand_165_out, F2, nand_154_out);
  nand nand_166 (nand_166_out, nand_165_out, nand_154_out);
  nand nand_167 (nand_167_out, F1, nand_154_out);
  nand nand_168 (nand_168_out, nand_167_out, nand_154_out);
  nand nand_169 (nand_169_out, F0, nand_154_out);
  nand nand_170 (nand_170_out, nand_169_out, nand_154_out);
  nand nand_171 (nand_171_out, nand_155_out, nand_172_out);
  nand nand_172 (nand_172_out, nand_171_out, nand_156_out);
  nand nand_173 (nand_173_out, nand_157_out, nand_174_out);
  nand nand_174 (nand_174_out, nand_173_out, nand_158_out);
  nand nand_175 (nand_175_out, nand_159_out, nand_176_out);
  nand nand_176 (nand_176_out, nand_175_out, nand_160_out);
  nand nand_177 (nand_177_out, nand_161_out, nand_178_out);
  nand nand_178 (nand_178_out, nand_177_out, nand_162_out);
  nand nand_179 (nand_179_out, nand_163_out, nand_180_out);
  nand nand_180 (nand_180_out, nand_179_out, nand_164_out);
  nand nand_181 (nand_181_out, nand_165_out, nand_182_out);
  nand nand_182 (nand_182_out, nand_181_out, nand_166_out);
  nand nand_183 (nand_183_out, nand_167_out, nand_184_out);
  nand nand_184 (nand_184_out, nand_183_out, nand_168_out);
  nand nand_185 (nand_185_out, nand_169_out, nand_186_out);
  nand nand_186 (nand_186_out, nand_185_out, nand_170_out);
  nand nand_187 (nand_187_out, nand_171_out, CLK);
  nand nand_188 (nand_188_out, nand_187_out, CLK);
  nand nand_189 (nand_189_out, nand_173_out, CLK);
  nand nand_190 (nand_190_out, nand_189_out, CLK);
  nand nand_191 (nand_191_out, nand_175_out, CLK);
  nand nand_192 (nand_192_out, nand_191_out, CLK);
  nand nand_193 (nand_193_out, nand_177_out, CLK);
  nand nand_194 (nand_194_out, nand_193_out, CLK);
  nand nand_195 (nand_195_out, nand_179_out, CLK);
  nand nand_196 (nand_196_out, nand_195_out, CLK);
  nand nand_197 (nand_197_out, nand_181_out, CLK);
  nand nand_198 (nand_198_out, nand_197_out, CLK);
  nand nand_199 (nand_199_out, nand_183_out, CLK);
  nand nand_200 (nand_200_out, nand_199_out, CLK);
  nand nand_201 (nand_201_out, nand_185_out, CLK);
  nand nand_202 (nand_202_out, nand_201_out, CLK);
  nand nand_203 (Q7, nand_187_out, nand_204_out);
  nand nand_204 (nand_204_out, Q7, nand_188_out);
  nand nand_205 (Q6, nand_189_out, nand_206_out);
  nand nand_206 (nand_206_out, Q6, nand_190_out);
  nand nand_207 (Q5, nand_191_out, nand_208_out);
  nand nand_208 (nand_208_out, Q5, nand_192_out);
  nand nand_209 (Q4, nand_193_out, nand_210_out);
  nand nand_210 (nand_210_out, Q4, nand_194_out);
  nand nand_211 (Q3, nand_195_out, nand_212_out);
  nand nand_212 (nand_212_out, Q3, nand_196_out);
  nand nand_213 (Q2, nand_197_out, nand_214_out);
  nand nand_214 (nand_214_out, Q2, nand_198_out);
  nand nand_215 (Q1, nand_199_out, nand_216_out);
  nand nand_216 (nand_216_out, Q1, nand_200_out);
  nand nand_217 (Q0, nand_201_out, nand_218_out);
  nand nand_218 (nand_218_out, Q0, nand_202_out);
  nand nand_219 (nand_219_out, in_33, in_34);
  nand nand_220 (nand_220_out, in_35, in_36);
  _74541 _74541_1 (
    .pin1(AC_BUS), .pin2(Q0), .pin3(Q1), .pin4(Q2), .pin5(Q3), .pin6(Q4), .pin7(Q5), .pin8(Q6), .pin9(Q7),
    .pin10(1'b0), .pin11(BUS7), .pin12(BUS6), .pin13(BUS5), .pin14(BUS4), .pin15(BUS3), .pin16(BUS2),
    .pin17(BUS1), .pin18(BUS0), .pin19(AC_BUS), .pin20(1'b1));
  nand nand_221 (nand_221_out, nand_219_out, nand_220_out);
  // _62256 _62256_1: pin names not known; wires that end beside it: 1'b0, 1'b0, in_23, in_22, in_21, in_20, in_19, in_18, in_17, in_16, BUS0, BUS1, BUS2, 1'b0, 1'b1, AC_BUS, 1'b0, 1'b0, 1'b0, 1'b0, CLK, 1'b0, nCE, BUS7

  // Other names for the same wires on the sheet: A0 = in_16; A1 = in_17; A2 = in_18; A3 = in_19; A4 = in_20;
  //   A5 = in_21; A6 = in_22; A7 = in_23; AC0 = Q0; AC1 = Q1; AC2 = Q2; AC3 = Q3; AC4 = Q4; AC5 = Q5; AC6 = Q6;
  //   AC7 = Q7; AL = SC; nRD = CLK; nWR = AC_BUS

  // Notes on the sheet:
  //   CLK: Hz: 2147483647
  //   RAM
  //   ADDRESS
  //   ALU
  //   ACC
  //   BUS
  //   8-bit ALU and Accumulator
  //   28 NAND gates per bitslice (7 x 74xx00)
  //   Accumulator made from gated D-type latches
endmodule
