// Digital circuit alternative clock sequencer 74HC590.dig as structural Verilog
module alternative_clock_sequencer_74HC590 (
);

  wire _74590_1_pin10, CLK, U32_pin7, U32_pin9, U32_pin10, U32_pin11, U32_pin12, U32_pin13, U32_pin14,
       U32_pin15;
  wire [0:0] _74590_1_pin4;
  wire [3:0] _74590_1_pin15;

  _74590 _74590_1 (
    .pin1(_74590_1_pin15[1]), .pin2(_74590_1_pin15[2]), .pin3(_74590_1_pin15[3]), .pin4(_74590_1_pin4[0]),
    .pin8(1'b0), .pin10(_74590_1_pin10), .pin11(CLK), .pin12(1'b0), .pin13(CLK), .pin14(1'b0),
    .pin15(_74590_1_pin15[0]), .pin16(1'b1));  // open: pin5, pin6, pin7, pin9
  Seven_Seg_Hex seven_seg_hex_1 (.d({3'b000, _74590_1_pin4[0]}), .dp(1'b0));
  Seven_Seg_Hex seven_seg_hex_2 (.d(_74590_1_pin15), .dp(1'b0));
  nand nand_1 (_74590_1_pin10, _74590_1_pin4[0], _74590_1_pin15[2], _74590_1_pin15[1], _74590_1_pin15[0]);
  _74138 U32 (
    .pin1(_74590_1_pin15[0]), .pin2(_74590_1_pin15[1]), .pin3(_74590_1_pin15[2]), .pin4(_74590_1_pin15[3]),
    .pin5(_74590_1_pin4[0]), .pin6(1'b1), .pin7(U32_pin7), .pin8(1'b0), .pin9(U32_pin9), .pin10(U32_pin10),
    .pin11(U32_pin11), .pin12(U32_pin12), .pin13(U32_pin13), .pin14(U32_pin14), .pin15(U32_pin15),
    .pin16(1'b1));

  // Notes on the sheet:
  //   # Clock
endmodule
