// Digital circuit basic_gates_1.dig as structural Verilog
module basic_gates_1 (
  input  in_2,
  input  in_3,
  input  in_4,
  input  in_5,
  input  in_6,
  input  in_7,
  input  in_8,
  input  in_9,
  input  in_11,
  input  in_12,
  input  in_14,
  input  in_15,
  input  in_17,
  input  in_18,
  input  A,
  input  B,
  input  in_27,
  input  in_28,
  input  in_29,
  input  in_30,
  input  in_32,
  input  in_33,
  input  in_34,
  input  in_35,
  input  in_37,
  input  in_38,
  input  in_39,
  input  in_40,
  input  in_41,
  input  in_42,
  input  B_2,
  input  A_2,
  input  E5,
  input  E4,
  input  C,
  input  C_2,
  input  S0,
  input  D,
  input  A_3,
  input  B_3,
  input  S1,
  input  EN,
  input  S0_2,
  input  S1_2,
  input  EN_2,
  input  in_59,
  input  in_60,
  input  in_61,
  input  in_62,
  input  in_63,
  input  in_64,
  input  A_4,
  input  B_4,
  input  Cin,
  input  A_5,
  input  B_5,
  input  Cin_2,
  input  in_78,
  input  in_79,
  input  in_80,
  input  in_81,
  input  C_3,
  input  S0_3,
  input  D_2,
  input  A_6,
  input  B_6,
  input  S1_3,
  input  A_7,
  input  B_7,
  input  nEN,
  input  in_95,
  input  in_96,
  input  in_98,
  input  in_99,
  input  in_101,
  input  in_102,
  input  in_104,
  input  in_105,
  input  in_107,
  input  in_108,
  input  in_110,
  input  in_111,
  input  in_113,
  input  in_114,
  input  in_116,
  input  in_117,
  input  in_119,
  input  in_120,
  input  A0,
  input  B0,
  input  I0,
  input  I1,
  input  I2,
  input  A0_2,
  input  I3,
  input  I0_2,
  input  I1_2,
  input  B0_2,
  input  A1,
  input  B1,
  input  in_135,
  input  in_137,
  input  C_4,
  input  S0_4,
  input  D_3,
  input  A_8,
  input  B_8,
  input  S1_4,
  input  S2,
  input  G,
  input  H,
  input  E,
  input  F,
  input  C_5,
  input  S0_5,
  input  D_4,
  input  A_9,
  input  B_9,
  input  S1_5,
  input  S2_2,
  input  E_2,
  input  F_2,
  input  in_159,
  input  in_160,
  input  A_10,
  input  B_10,
  input  A_11,
  input  B_11,
  input  Cin_3,
  input  A_12,
  input  B_12,
  input  I0_3,
  input  I1_3,
  input  A_13,
  input  B_13,
  input  I0_4,
  input  I1_4,
  input  Cin_4,
  input  A_14,
  input  B_14,
  input  I0_5,
  input  I1_5,
  input  Cin_5,
  input  I2_2,
  input  A_15,
  input  B_15,
  input  I0_6,
  input  I1_6,
  input  Cin_6,
  input  I2_3,
  input  I3_2,
  input  A_16,
  input  B_16,
  input  I0_7,
  input  I1_7,
  input  Cin_7,
  input  I2_4,
  input  I3_3,
  input  A_17,
  input  B_17,
  input  Cin_8,
  input  in_213,
  input  in_214,
  input  in_215,
  input  in_216,
  input  I1_8,
  input  I0_8,
  input  A_18,
  input  B_18,
  input  in_222,
  input  in_223,
  input  in_224,
  input  in_225,
  input  in_226,
  input  A_19,
  input  B_19,
  input  Sa,
  input  Sb,
  input  A_20,
  input  B_20,
  input  Sa_2,
  input  Sb_2,
  input  in_237,
  input  in_238,
  input  A_21,
  input  B_21,
  input  Cin_9,
  input  I0_9,
  input  I1_9,
  input  nSC,
  input  INV_A,
  input  INV_B,
  input  S0_6,
  input  S1_6,
  input  in_253,
  input  in_254,
  input  in_255,
  input  in_256,
  input  in_257,
  input  in_258,
  input  in_259,
  input  in_260,
  input  A_22,
  input  B_22,
  input  D_5,
  input  E_3,
  input  C_6,
  input  A_23,
  input  B_23,
  input  D_6,
  input  E_4,
  input  C_7,
  input  G_2,
  input  H_2,
  input  I,
  input  J,
  input  K,
  input  in_278,
  input  in_279,
  input  in_280,
  input  in_281,
  input  in_282,
  input  in_283,
  input  in_285,
  input  in_286,
  input  in_290,
  input  in_291,
  input  in_292,
  input  in_293,
  input  S,
  input  A2,
  input  EN_3,
  input  B2,
  input  A3,
  input  B3,
  input  A2_2,
  input  B2_2,
  input  A3_2,
  input  B3_2,
  input  in_308,
  input  in_309,
  input  in_314,
  input  in_315,
  input  in_320,
  input  in_321,
  input  in_326,
  input  in_328,
  input  in_329,
  input  in_330,
  input  in_331,
  input  in_333,
  input  in_334,
  input  in_335,
  input  in_336,
  input  in_338,
  input  in_339,
  input  in_340,
  input  in_341,
  input  in_342,
  input  in_343,
  input  Bin,
  input  INV,
  input  A2_3,
  input  B2_3,
  input  Cin_10,
  input  A3_3,
  input  B3_3,
  input  A2_4,
  input  B2_4,
  input  A3_4,
  input  B3_4,
  input  A2_5,
  input  B2_5,
  input  Cin_11,
  input  A4,
  input  B4,
  input  Cin_12,
  input  D_7,
  input  A5,
  input  B5,
  input  Cin_13,
  input  D_8,
  input  A2_6,
  input  B2_6,
  input  I4,
  input  I5,
  input  I4_2,
  input  I5_2,
  input  in_387,
  input  in_388,
  input  in_389,
  input  in_390,
  input  in_391,
  input  in_392,
  input  in_393,
  input  in_394,
  input  in_395,
  input  in_396,
  input  DAT,
  input  CLK,
  input  in_399,
  input  DAT_2,
  input  CLK_2,
  input  DAT_3,
  input  in_403,
  input  DATA,
  input  CK,
  input  nLD,
  input  in_407,
  input  in_408,
  input  in_409,
  input  in_410,
  input  in_411,
  input  in_412,
  input  D3,
  input  D2,
  input  D1,
  input  D0,
  input  S4,
  input  S3,
  input  E1,
  input  E0,
  input  in_421,
  input  in_422,
  input  in_423,
  input  in_424,
  input  C_8,
  input  S3_2,
  input  D_9,
  input  A_24,
  input  B_24,
  input  S4_2,
  input  EN_4,
  input  in_432,
  input  in_433,
  input  in_434,
  input  in_435,
  input  in_436,
  input  in_437,
  input  in_438,
  input  in_439,
  input  in_440,
  input  C_9,
  input  S3_3,
  input  D_10,
  input  A_25,
  input  B_25,
  input  S4_3,
  input  Cin_14,
  input  C_10,
  input  S3_4,
  input  D_11,
  input  A_26,
  input  B_26,
  input  S4_4,
  input  SC,
  output out_1,
  output out_10,
  output out_13,
  output out_16,
  output out_19,
  output out_22,
  output out_23,
  output out_24,
  output out_25,
  output out_26,
  output out_31,
  output out_36,
  output out_43,
  output Carry,
  output Sum,
  output Carry_2,
  output Sum_2,
  output Carry_3,
  output Sum_3,
  output out_77,
  output out_90,
  output out_91,
  output out_92,
  output out_93,
  output out_97,
  output out_100,
  output out_103,
  output out_106,
  output out_109,
  output out_112,
  output out_115,
  output out_118,
  output Fout,
  output Fout_2,
  output out_136,
  output out_158,
  output out_163,
  output out_164,
  output Sum_4,
  output Cout,
  output Fout_3,
  output Sum_5,
  output Cout_2,
  output Sum_6,
  output Cout_3,
  output Sum_7,
  output Cout_4,
  output Sum_8,
  output Cout_5,
  output Sum_9,
  output Cout_6,
  output out_221,
  output out_227,
  output out_232,
  output out_239,
  output Fout_4,
  output Cout_7,
  output out_252,
  output F_3,
  output F_4,
  output out_284,
  output out_287,
  output out_288,
  output out_289,
  output out_298,
  output out_301,
  output out_304,
  output out_307,
  output out_310,
  output out_311,
  output out_312,
  output out_313,
  output out_316,
  output out_317,
  output out_318,
  output out_319,
  output out_322,
  output out_323,
  output out_324,
  output out_325,
  output out_327,
  output out_332,
  output out_337,
  output out_344,
  output Out,
  output SUM0,
  output SUM1,
  output SUM2,
  output SUM3,
  output C3out,
  output SUM_10,
  output Cout_8,
  output Fout_5,
  output C0out,
  output Fout_6,
  output C0out_2,
  output Fout_7,
  output Fout_8
);

  wire AL, and_2_out, and_3_out, and_4_out, and_5_out, and_6_out, and_7_out, and_8_out, and_9_out,
       and_11_out, and_13_out, and_14_out, and_16_out, and_17_out, and_18_out, and_19_out, and_20_out,
       and_21_out, and_22_out, and_23_out, and_24_out, and_25_out, and_26_out, and_27_out, and_28_out,
       and_29_out, and_30_out, and_31_out, and_32_out, and_34_out, and_35_out, AR0, AR1, AR2, AR3, E0_t,
       E1_t, E2, E3, nand_1_out, nand_2_out, nand_3_out, nand_4_out, nand_5_out, nand_6_out, nand_7_out,
       nand_8_out, nand_9_out, nand_10_out, nand_11_out, nand_12_out, nand_13_out, nand_14_out, nand_15_out,
       nand_16_out, nand_17_out, nand_18_out, nand_19_out, nand_20_out, nand_21_out, nand_22_out,
       nand_23_out, nand_24_out, nand_25_out, nand_26_out, nand_27_out, nand_28_out, nand_29_out,
       nand_30_out, nand_31_out, nand_32_out, nand_33_out, nand_34_out, nand_35_out, nand_36_out,
       nand_37_out, nand_40_out, nand_41_out, nand_42_out, nand_43_out, nand_44_out, nand_45_out,
       nand_46_out, nand_47_out, nand_48_out, nand_49_out, nand_50_out, nand_51_out, nand_52_out,
       nand_53_out, nand_56_out, nand_57_out, nand_58_out, nand_59_out, nand_60_out, nand_61_out,
       nand_62_out, nand_63_out, nand_64_out, nand_65_out, nand_66_out, nand_67_out, nand_68_out,
       nand_69_out, nand_70_out, nand_71_out, nand_72_out, nand_73_out, nand_74_out, nand_75_out,
       nand_76_out, nand_77_out, nand_78_out, nand_79_out, nand_80_out, nand_81_out, nand_82_out,
       nand_83_out, nand_84_out, nand_85_out, nand_86_out, nand_87_out, nand_88_out, nand_89_out,
       nand_90_out, nand_91_out, nand_92_out, nand_93_out, nand_94_out, nand_95_out, nand_96_out,
       nand_97_out, nand_98_out, nand_100_out, nand_101_out, nand_102_out, nand_103_out, nand_104_out,
       nand_105_out, nand_106_out, nand_107_out, nand_108_out, nand_109_out, nand_110_out, nand_111_out,
       nand_112_out, nand_113_out, nand_114_out, nand_115_out, nand_116_out, nand_117_out, nand_118_out,
       nand_119_out, nand_120_out, nand_121_out, nand_122_out, nand_123_out, nand_124_out, nand_125_out,
       nand_126_out, nand_127_out, nand_128_out, nand_129_out, nand_130_out, nand_131_out, nand_132_out,
       nand_133_out, nand_134_out, nand_135_out, nand_136_out, nand_137_out, nand_138_out, nand_139_out,
       nand_140_out, nand_141_out, nand_142_out, nand_143_out, nand_144_out, nand_145_out, nand_146_out,
       nand_147_out, nand_148_out, nand_149_out, nand_150_out, nand_151_out, nand_152_out, nand_153_out,
       nand_154_out, nand_155_out, nand_156_out, nand_157_out, nand_158_out, nand_159_out, nand_160_out,
       nand_161_out, nand_162_out, nand_163_out, nand_164_out, nand_165_out, nand_166_out, nand_167_out,
       nand_168_out, nand_169_out, nand_170_out, nand_171_out, nand_172_out, nand_173_out, nand_174_out,
       nand_175_out, nand_176_out, nand_179_out, nand_184_out, nand_185_out, nand_186_out, nand_187_out,
       nand_188_out, nand_192_out, nand_193_out, nand_194_out, nand_195_out, nand_196_out, nand_197_out,
       nand_198_out, nand_199_out, nand_200_out, nand_201_out, nand_202_out, nand_203_out, nand_204_out,
       nand_205_out, nand_206_out, nand_207_out, nand_208_out, nand_209_out, nand_210_out, nand_211_out,
       nand_212_out, nand_213_out, nand_218_out, nand_219_out, nand_220_out, nand_221_out, nand_222_out,
       nand_223_out, nand_225_out, nand_226_out, nand_227_out, nand_228_out, nand_229_out, nand_230_out,
       nand_235_out, nand_236_out, nand_237_out, nand_238_out, nand_239_out, nand_240_out, nand_241_out,
       nand_242_out, nand_251_out, nand_252_out, nand_253_out, nand_254_out, nand_255_out, nand_256_out,
       nand_257_out, nand_258_out, nand_259_out, nand_260_out, nand_261_out, nand_262_out, nand_263_out,
       nand_264_out, nand_265_out, nand_266_out, nand_267_out, nand_268_out, nand_269_out, nand_270_out,
       nand_271_out, nand_272_out, nand_273_out, nand_274_out, nand_283_out, nand_284_out, nand_285_out,
       nand_286_out, nand_287_out, nand_288_out, nand_289_out, nand_290_out, nand_291_out, nand_292_out,
       nand_293_out, nand_294_out, nand_295_out, nand_296_out, nand_297_out, nand_298_out, nand_299_out,
       nand_300_out, nand_301_out, nand_302_out, nand_303_out, nand_304_out, nand_305_out, nand_306_out,
       nand_307_out, nand_308_out, nand_309_out, nand_310_out, nand_311_out, nand_313_out, nand_315_out,
       nand_316_out, nand_318_out, nand_319_out, nand_320_out, nand_321_out, nand_322_out, nand_323_out,
       nand_324_out, nand_325_out, nand_326_out, nand_327_out, nand_328_out, nand_329_out, nand_334_out,
       nand_335_out, nand_337_out, nand_338_out, nand_343_out, nand_344_out, nand_345_out, nand_346_out,
       nand_347_out, nand_348_out, nand_349_out, nand_350_out, nand_351_out, nand_352_out, nand_353_out,
       nand_356_out, nand_357_out, nand_358_out, nand_359_out, nand_360_out, nand_362_out, nand_363_out,
       nand_364_out, nand_365_out, nand_366_out, nand_367_out, nand_368_out, nand_369_out, nand_370_out,
       nand_371_out, nand_374_out, nand_375_out, nand_376_out, nand_377_out, nand_378_out, nand_379_out,
       nand_380_out, nand_381_out, nand_382_out, nand_383_out, nand_384_out, nand_385_out, nand_386_out,
       nand_387_out, nand_388_out, nand_389_out, nand_390_out, nand_391_out, nand_392_out, nand_393_out,
       nand_394_out, nand_395_out, nand_396_out, nand_397_out, nand_398_out, nand_399_out, nand_400_out,
       nand_401_out, nand_402_out, nand_403_out, nand_404_out, nand_405_out, nand_406_out, nand_407_out,
       nand_408_out, nand_409_out, nand_410_out, nand_411_out, nand_412_out, nand_413_out, nand_415_out,
       nand_416_out, nand_417_out, nand_418_out, nand_419_out, nand_420_out, nand_421_out, nand_422_out,
       nand_423_out, nand_424_out, nand_425_out, nand_426_out, nand_427_out, nand_429_out, nand_430_out,
       nand_432_out, nand_433_out, nand_434_out, nand_436_out, nand_437_out, nand_443_out, nand_444_out,
       nand_445_out, nand_447_out, nand_449_out, nand_450_out, nand_451_out, nand_452_out, nand_453_out,
       nand_454_out, nand_457_out, nand_458_out, nand_459_out, nand_461_out, nand_462_out, nand_463_out,
       nand_464_out, nand_465_out, nand_466_out, nand_467_out, nand_468_out, nand_469_out, nand_470_out,
       nand_473_out, nand_474_out, nand_475_out, nand_476_out, nand_477_out, nand_478_out, nand_479_out,
       nand_480_out, nand_481_out, nand_482_out, nand_483_out, nand_484_out, nand_485_out, nand_486_out,
       nand_487_out, nand_488_out, nand_489_out, nand_490_out, nand_495_out, nand_496_out, nand_497_out,
       nand_498_out, nand_499_out, nand_500_out, nand_501_out, nand_502_out, nand_503_out, nand_504_out,
       nand_505_out, nand_506_out, nand_519_out, nand_520_out, nand_522_out, nand_524_out, nand_525_out,
       nand_528_out, nand_529_out, nand_530_out, nand_531_out, nand_532_out, nand_533_out, nand_534_out,
       nand_535_out, nand_536_out, nand_537_out, nand_538_out, nand_539_out, nand_540_out, nand_541_out,
       nand_542_out, nand_543_out, nand_544_out, nand_545_out, nand_546_out, nand_547_out, nand_548_out,
       nand_549_out, nand_550_out, nand_551_out, nand_552_out, nand_553_out, nand_554_out, nand_555_out,
       nand_556_out, nand_557_out, nand_558_out, nand_559_out, nand_560_out, nand_561_out, nand_562_out,
       nand_563_out, nand_564_out, nand_565_out, nand_566_out, nand_567_out, nand_568_out, nand_569_out,
       nand_570_out, nand_571_out, nand_572_out, nand_573_out, nand_574_out, nand_575_out, nand_576_out,
       nand_577_out, nand_578_out, nand_579_out, nand_580_out, nand_581_out, nand_582_out, nand_583_out,
       nand_584_out, nand_585_out, nand_586_out, nand_587_out, nand_588_out, nand_589_out, nand_590_out,
       nand_591_out, nand_592_out, nand_593_out, nand_594_out, nand_595_out, nand_596_out, nand_597_out,
       nand_598_out, nand_599_out, nand_600_out, nand_601_out, nand_602_out, nand_603_out, nand_604_out,
       nand_605_out, nand_606_out, nand_607_out, nand_608_out, nand_609_out, nand_610_out, nand_611_out,
       nand_612_out, nand_613_out, nand_614_out, nand_615_out, nand_616_out, nand_617_out, nand_618_out,
       nand_619_out, nand_620_out, nand_621_out, nand_622_out, nand_623_out, nand_624_out, nand_625_out,
       nand_626_out, nand_627_out, nand_628_out, nand_629_out, nand_630_out, nand_631_out, nand_632_out,
       nand_633_out, nand_634_out, nand_635_out, nand_636_out, nand_637_out, nand_638_out, nand_639_out,
       nand_640_out, nand_641_out, nand_642_out, nand_643_out, nand_644_out, nand_645_out, nand_646_out,
       nand_647_out, nand_648_out, nand_649_out, nand_650_out, nand_651_out, nand_652_out, nand_653_out,
       nand_654_out, nand_655_out, nand_656_out, nand_657_out, nand_658_out, nand_659_out, nand_660_out,
       nand_661_out, nand_662_out, nand_663_out, nand_664_out, nand_665_out, nand_666_out, nand_667_out,
       nand_668_out, nand_669_out, nJMP, nor_1_out, nor_2_out, nor_3_out, nor_4_out, nor_5_out, nor_6_out,
       nor_7_out, nor_8_out, nor_9_out, nor_10_out, nor_11_out, nor_12_out, nor_13_out, nor_14_out,
       nor_15_out, nW, or_4_out, or_5_out, or_6_out, or_10_out, or_11_out, pullup_1_out, pullup_2_out,
       pullup_3_out, pullup_4_out, pullup_5_out, W, xor_2_out, xor_3_out, xor_6_out, xor_7_out, xor_8_out,
       xor_9_out, xor_10_out, xor_12_out, xor_13_out, xor_14_out, xor_15_out, xor_16_out, xor_17_out,
       xor_18_out, xor_19_out, xor_21_out, xor_26_out, xor_28_out, xor_29_out, xor_30_out, xor_31_out;

  nand nand_1 (nand_1_out, S0_4, S0_4);
  nand nand_2 (nand_2_out, S1_4, S1_4);
  nand nand_3 (nand_3_out, S2, S2);
  nand nand_4 (nand_4_out, H, S0_4);
  nand nand_5 (nand_5_out, G, nand_1_out);
  nand nand_6 (nand_6_out, F, S0_4);
  nand nand_7 (nand_7_out, E, nand_1_out);
  nand nand_8 (nand_8_out, D_3, S0_4);
  nand nand_9 (nand_9_out, C_4, nand_1_out);
  nand nand_10 (nand_10_out, B_8, S0_4);
  nand nand_11 (nand_11_out, A_8, nand_1_out);
  nand nand_12 (nand_12_out, nand_4_out, nand_5_out);
  nand nand_13 (nand_13_out, nand_6_out, nand_7_out);
  nand nand_14 (nand_14_out, nand_8_out, nand_9_out);
  nand nand_15 (nand_15_out, nand_10_out, nand_11_out);
  nand nand_16 (nand_16_out, S1_4, nand_12_out);
  nand nand_17 (nand_17_out, nand_13_out, nand_2_out);
  nand nand_18 (nand_18_out, S1_4, nand_14_out);
  nand nand_19 (nand_19_out, nand_15_out, nand_2_out);
  nand nand_20 (nand_20_out, nand_16_out, nand_17_out);
  nand nand_21 (nand_21_out, nand_18_out, nand_19_out);
  nand nand_22 (nand_22_out, S0_5, S0_5);
  nand nand_23 (nand_23_out, S1_5, S1_5);
  nand nand_24 (nand_24_out, S0_5, S0_5);
  nand nand_25 (nand_25_out, S1_5, S1_5);
  nand nand_26 (nand_26_out, S2_2, S2_2);
  nand nand_27 (nand_27_out, in_59, in_59);
  nand nand_28 (nand_28_out, in_60, in_60);
  nand nand_29 (nand_29_out, nand_20_out, S2);
  nand nand_30 (nand_30_out, nand_21_out, nand_3_out);
  nand nand_31 (nand_31_out, F_2, S0_5);
  nand nand_32 (nand_32_out, E_2, nand_22_out);
  nand nand_33 (nand_33_out, D_4, S0_5);
  nand nand_34 (nand_34_out, C_5, nand_24_out);
  nand nand_35 (nand_35_out, B_9, S0_5);
  nand nand_36 (nand_36_out, A_9, nand_24_out);
  nand nand_37 (nand_37_out, nand_29_out, nand_30_out);
  nand nand_38 (E0_t, in_61, nand_28_out);
  nand nand_39 (E1_t, in_61, nand_27_out);
  nand nand_40 (nand_40_out, nand_27_out, nand_28_out);
  nand nand_41 (nand_41_out, in_59, nand_28_out);
  nand nand_42 (nand_42_out, nand_27_out, in_60);
  nand nand_43 (nand_43_out, in_59, in_60);
  nand nand_44 (nand_44_out, E2, E3);
  nand nand_45 (nand_45_out, E0_t, E3);
  nand nand_46 (nand_46_out, E2, E1_t);
  nand nand_47 (nand_47_out, E0_t, E1_t);
  nand nand_48 (nand_48_out, nand_31_out, nand_32_out);
  nand nand_49 (nand_49_out, nand_33_out, nand_34_out);
  nand nand_50 (nand_50_out, nand_35_out, nand_36_out);
  LED led_1 (.in(nand_37_out));
  nand nand_51 (nand_51_out, nand_48_out, nand_23_out);
  nand nand_52 (nand_52_out, S1_5, nand_49_out);
  nand nand_53 (nand_53_out, nand_50_out, nand_25_out);
  nand nand_54 (E2, E0_t, E0_t);
  nand nand_55 (E3, E1_t, E1_t);
  LED led_2 (.in(nand_40_out));
  LED led_3 (.in(nand_41_out));
  LED led_4 (.in(nand_42_out));
  LED led_5 (.in(nand_43_out));
  LED led_6 (.in(nand_44_out));
  LED led_7 (.in(nand_45_out));
  LED led_8 (.in(nand_46_out));
  LED led_9 (.in(nand_47_out));
  nand nand_56 (nand_56_out, 1'b1, nand_51_out);
  nand nand_57 (nand_57_out, nand_52_out, nand_53_out);
  nand nand_58 (nand_58_out, nand_56_out, S2_2);
  nand nand_59 (nand_59_out, nand_57_out, nand_26_out);
  nand nand_60 (nand_60_out, nand_58_out, nand_59_out);
  LED led_10 (.in(nand_60_out));
  nand nand_61 (nand_61_out, S0_2, S0_2);
  nand nand_62 (nand_62_out, S1_2, S1_2);
  nand nand_63 (nand_63_out, nand_61_out, nand_62_out);
  nand nand_64 (nand_64_out, S0_2, nand_62_out);
  nand nand_65 (nand_65_out, nand_61_out, S1_2);
  nand nand_66 (nand_66_out, S0_2, S1_2);
  nand nand_67 (nand_67_out, S0_6, S0_6);
  nand nand_68 (nand_68_out, S1_6, S1_6);
  nand nand_69 (nand_69_out, nand_63_out, nand_63_out);
  nand nand_70 (nand_70_out, nand_64_out, nand_64_out);
  nand nand_71 (nand_71_out, nand_65_out, nand_65_out);
  nand nand_72 (nand_72_out, nand_66_out, nand_66_out);
  nand nand_73 (nand_73_out, nand_69_out, EN_2);
  nand nand_74 (nand_74_out, nand_70_out, EN_2);
  nand nand_75 (nand_75_out, nand_71_out, EN_2);
  nand nand_76 (nand_76_out, nand_72_out, EN_2);
  nand nand_77 (nand_77_out, nand_67_out, nand_68_out);
  nand nand_78 (nand_78_out, nand_68_out, S0_6);
  nand nand_79 (nand_79_out, nand_67_out, S1_6);
  nand nand_80 (nand_80_out, S1_6, S0_6);
  nand nand_81 (nand_81_out, C, C);
  nand nand_82 (nand_82_out, B_2, B_2);
  nand nand_83 (nand_83_out, A_2, A_2);
  nand nand_84 (nand_84_out, E5, E4);
  LED led_11 (.in(nand_73_out));
  LED led_12 (.in(nand_74_out));
  LED led_13 (.in(nand_75_out));
  LED led_14 (.in(nand_76_out));
  LED led_15 (.in(nand_77_out));
  LED led_16 (.in(nand_78_out));
  LED led_17 (.in(nand_79_out));
  LED led_18 (.in(nand_80_out));
  nand nand_85 (nand_85_out, S0_3, S0_3);
  nand nand_86 (nand_86_out, S1_3, S1_3);
  nand nand_87 (nand_87_out, S0, S0);
  nand nand_88 (nand_88_out, S1, S1);
  and and_1 (Carry, in_63, in_64);
  xor xor_1 (Sum, in_63, in_64);
  and and_2 (and_2_out, A_4, B_4);
  xor xor_2 (xor_2_out, A_4, B_4);
  nand nand_89 (nand_89_out, A_5, B_5);
  xor xor_3 (xor_3_out, A_5, B_5);
  nand nand_90 (nand_90_out, xor_3_out, Cin_2);
  xor xor_4 (Sum_3, xor_3_out, Cin_2);
  nand nand_91 (nand_91_out, D_2, S0_3);
  nand nand_92 (nand_92_out, C_3, nand_85_out);
  nand nand_93 (nand_93_out, B_6, S0_3);
  nand nand_94 (nand_94_out, A_6, nand_85_out);
  nand nand_95 (nand_95_out, D, S0);
  nand nand_96 (nand_96_out, C_2, nand_87_out);
  nand nand_97 (nand_97_out, B_3, S0);
  nand nand_98 (nand_98_out, A_3, nand_87_out);
  and and_3 (and_3_out, xor_2_out, Cin);
  xor xor_5 (Sum_2, xor_2_out, Cin);
  nand nand_99 (Carry_3, nand_89_out, nand_90_out);
  nand nand_100 (nand_100_out, nand_91_out, nand_92_out);
  nand nand_101 (nand_101_out, nand_93_out, nand_94_out);
  nand nand_102 (nand_102_out, nand_95_out, nand_96_out);
  nand nand_103 (nand_103_out, nand_97_out, nand_98_out);
  nand nand_104 (nand_104_out, nand_84_out, nand_81_out);
  nand nand_105 (nand_105_out, nand_82_out, nand_83_out);
  nand nand_106 (nand_106_out, nand_84_out, nand_81_out);
  nand nand_107 (nand_107_out, A_2, nand_82_out);
  nand nand_108 (nand_108_out, nand_84_out, nand_81_out);
  nand nand_109 (nand_109_out, nand_83_out, B_2);
  nand nand_110 (nand_110_out, nand_84_out, nand_81_out);
  nand nand_111 (nand_111_out, A_2, B_2);
  nand nand_112 (nand_112_out, nand_84_out, C);
  nand nand_113 (nand_113_out, nand_82_out, nand_83_out);
  nand nand_114 (nand_114_out, nand_84_out, C);
  nand nand_115 (nand_115_out, A_2, nand_82_out);
  nand nand_116 (nand_116_out, nand_84_out, C);
  nand nand_117 (nand_117_out, nand_83_out, B_2);
  nand nand_118 (nand_118_out, nand_84_out, C);
  nand nand_119 (nand_119_out, A_2, B_2);
  or or_1 (Carry_2, and_2_out, and_3_out);
  nand nand_120 (nand_120_out, S1_3, nand_100_out);
  nand nand_121 (nand_121_out, nand_101_out, nand_86_out);
  nand nand_122 (nand_122_out, S1, nand_102_out);
  nand nand_123 (nand_123_out, nand_103_out, nand_88_out);
  nand nand_124 (nand_124_out, nand_104_out, nand_104_out);
  nand nand_125 (nand_125_out, nand_105_out, nand_105_out);
  nand nand_126 (nand_126_out, nand_106_out, nand_106_out);
  nand nand_127 (nand_127_out, nand_107_out, nand_107_out);
  nand nand_128 (nand_128_out, nand_108_out, nand_108_out);
  nand nand_129 (nand_129_out, nand_109_out, nand_109_out);
  nand nand_130 (nand_130_out, nand_110_out, nand_110_out);
  nand nand_131 (nand_131_out, nand_111_out, nand_111_out);
  nand nand_132 (nand_132_out, nand_112_out, nand_112_out);
  nand nand_133 (nand_133_out, nand_113_out, nand_113_out);
  nand nand_134 (nand_134_out, nand_114_out, nand_114_out);
  nand nand_135 (nand_135_out, nand_115_out, nand_115_out);
  nand nand_136 (nand_136_out, nand_116_out, nand_116_out);
  nand nand_137 (nand_137_out, nand_117_out, nand_117_out);
  nand nand_138 (nand_138_out, nand_118_out, nand_118_out);
  nand nand_139 (nand_139_out, nand_119_out, nand_119_out);
  nand nand_140 (nand_140_out, nand_120_out, nand_121_out);
  nand nand_141 (nand_141_out, nand_122_out, nand_123_out);
  nand nand_142 (nand_142_out, nand_124_out, nand_125_out);
  nand nand_143 (nand_143_out, nand_126_out, nand_127_out);
  nand nand_144 (nand_144_out, nand_128_out, nand_129_out);
  nand nand_145 (nand_145_out, nand_130_out, nand_131_out);
  nand nand_146 (nand_146_out, nand_132_out, nand_133_out);
  nand nand_147 (nand_147_out, nand_134_out, nand_135_out);
  nand nand_148 (nand_148_out, nand_136_out, nand_137_out);
  nand nand_149 (nand_149_out, nand_138_out, nand_139_out);
  LED led_19 (.in(nand_140_out));
  nand nand_150 (nand_150_out, nand_141_out, EN);
  LED led_20 (.in(nand_142_out));
  LED led_21 (.in(nand_143_out));
  LED led_22 (.in(nand_144_out));
  LED led_23 (.in(nand_145_out));
  LED led_24 (.in(nand_146_out));
  LED led_25 (.in(nand_147_out));
  LED led_26 (.in(nand_148_out));
  LED led_27 (.in(nand_149_out));
  nand nand_151 (nand_151_out, nand_150_out, nand_150_out);
  nand nand_152 (nand_152_out, in_59, in_59);
  nand nand_153 (nand_153_out, in_60, in_60);
  nand nand_154 (nand_154_out, in_61, in_61);
  LED led_28 (.in(nand_151_out));
  nand nand_155 (nand_155_out, nand_152_out, nand_153_out);
  nand nand_156 (nand_156_out, in_59, nand_153_out);
  nand nand_157 (nand_157_out, nand_152_out, in_60);
  nand nand_158 (nand_158_out, in_59, in_60);
  nand nand_159 (nand_159_out, nand_152_out, nand_153_out);
  nand nand_160 (nand_160_out, in_59, nand_153_out);
  nand nand_161 (nand_161_out, nand_152_out, in_60);
  nand nand_162 (nand_162_out, in_59, in_60);
  nand nand_163 (nand_163_out, in_62, nand_155_out);
  nand nand_164 (nand_164_out, in_62, nand_156_out);
  nand nand_165 (nand_165_out, in_62, nand_157_out);
  nand nand_166 (nand_166_out, in_62, nand_158_out);
  nand nand_167 (nand_167_out, in_62, nand_159_out);
  nand nand_168 (nand_168_out, in_62, nand_160_out);
  nand nand_169 (nand_169_out, in_62, nand_161_out);
  nand nand_170 (nand_170_out, in_62, nand_162_out);
  nand nand_171 (nand_171_out, nand_163_out, nand_154_out);
  nand nand_172 (nand_172_out, nand_164_out, nand_154_out);
  nand nand_173 (nand_173_out, nand_165_out, nand_154_out);
  nand nand_174 (nand_174_out, nand_166_out, nand_154_out);
  nand nand_175 (nand_175_out, nand_167_out, in_61);
  nand nand_176 (nand_176_out, nand_168_out, in_61);
  nand nand_177 (nW, nand_169_out, in_61);
  nand nand_178 (nJMP, nand_170_out, in_61);
  PullUp pullup_1 (.out(pullup_1_out));
  DiodeBackward diodebackward_1 (.in(nJMP), .out(pullup_1_out));
  DiodeBackward diodebackward_2 (.in(in_61), .out(pullup_1_out));
  nand nand_179 (nand_179_out, in_6, in_6);
  PullUp pullup_2 (.out(pullup_2_out));
  DiodeBackward diodebackward_3 (.in(nand_171_out), .out(pullup_2_out));
  DiodeBackward diodebackward_4 (.in(nand_172_out), .out(pullup_2_out));
  DiodeBackward diodebackward_5 (.in(nand_173_out), .out(pullup_2_out));
  DiodeBackward diodebackward_6 (.in(nand_175_out), .out(pullup_2_out));
  nand nand_180 (AL, pullup_1_out, pullup_1_out);
  PullUp pullup_3 (.out(pullup_3_out));
  DiodeBackward diodebackward_7 (.in(nand_171_out), .out(pullup_3_out));
  DiodeBackward diodebackward_8 (.in(nand_173_out), .out(pullup_3_out));
  DiodeBackward diodebackward_9 (.in(nand_174_out), .out(pullup_3_out));
  DiodeBackward diodebackward_10 (.in(nand_175_out), .out(pullup_3_out));
  DiodeBackward diodebackward_11 (.in(nW), .out(pullup_3_out));
  nand nand_181 (AR3, pullup_2_out, pullup_2_out);
  PullUp pullup_4 (.out(pullup_4_out));
  DiodeBackward diodebackward_12 (.in(nand_173_out), .out(pullup_4_out));
  DiodeBackward diodebackward_13 (.in(nand_174_out), .out(pullup_4_out));
  DiodeBackward diodebackward_14 (.in(nand_176_out), .out(pullup_4_out));
  nand nand_182 (AR2, pullup_3_out, pullup_3_out);
  and and_4 (and_4_out, nand_179_out, in_8);
  and and_5 (and_5_out, in_6, in_8);
  PullUp pullup_5 (.out(pullup_5_out));
  DiodeBackward diodebackward_15 (.in(nand_176_out), .out(pullup_5_out));
  DiodeBackward diodebackward_16 (.in(nW), .out(pullup_5_out));
  nand nand_183 (AR1, pullup_4_out, pullup_4_out);
  nand nand_184 (nand_184_out, A, A);
  nand nand_185 (nand_185_out, B, B);
  nand nand_186 (nand_186_out, A_7, A_7);
  nand nand_187 (nand_187_out, B_7, B_7);
  nand nand_188 (nand_188_out, nEN, nEN);
  nand nand_189 (AR0, pullup_5_out, pullup_5_out);
  nand nand_190 (out_239, in_237, in_238);
  nand nand_191 (W, nW, nW);
  LED led_29 (.in(nand_171_out));
  LED led_30 (.in(nand_172_out));
  LED led_31 (.in(nand_173_out));
  LED led_32 (.in(nand_174_out));
  LED led_33 (.in(nand_175_out));
  LED led_34 (.in(nand_176_out));
  LED led_35 (.in(nW));
  LED led_36 (.in(nJMP));
  nand nand_192 (nand_192_out, 1'b0, 1'b0);
  and and_6 (and_6_out, in_2, in_3);
  and and_7 (and_7_out, in_4, in_5);
  nand nand_193 (nand_193_out, 1'b0, 1'b0);
  nand nand_194 (nand_194_out, in_41, in_41);
  nand nand_195 (nand_195_out, in_42, in_42);
  nand nand_196 (nand_196_out, in_39, in_39);
  nand nand_197 (nand_197_out, in_40, in_40);
  nand nand_198 (nand_198_out, in_37, in_37);
  nand nand_199 (nand_199_out, in_38, in_38);
  nand nand_200 (nand_200_out, in_78, in_79);
  nand nand_201 (nand_201_out, in_80, in_81);
  nand nand_202 (nand_202_out, in_32, in_33);
  nand nand_203 (nand_203_out, in_34, in_35);
  nand nand_204 (nand_204_out, in_27, in_28);
  nand nand_205 (nand_205_out, in_29, in_30);
  nand nand_206 (nand_206_out, and_4_out, in_7);
  nand nand_207 (nand_207_out, and_5_out, in_9);
  nand nand_208 (nand_208_out, and_4_out, in_11);
  nand nand_209 (nand_209_out, and_5_out, in_12);
  nand nand_210 (nand_210_out, and_4_out, in_14);
  nand nand_211 (nand_211_out, and_5_out, in_15);
  nand nand_212 (nand_212_out, and_4_out, in_17);
  nand nand_213 (nand_213_out, and_5_out, in_18);
  nand nand_214 (out_22, nand_184_out, nand_185_out);
  nand nand_215 (out_23, A, nand_185_out);
  nand nand_216 (out_24, nand_184_out, B);
  nand nand_217 (out_25, A, B);
  nand nand_218 (nand_218_out, nand_186_out, nand_187_out);
  nand nand_219 (nand_219_out, A_7, nand_187_out);
  nand nand_220 (nand_220_out, nand_186_out, B_7);
  nand nand_221 (nand_221_out, A_7, B_7);
  and and_8 (and_8_out, A_22, B_22);
  and and_9 (and_9_out, D_5, E_3);
  nand nand_222 (nand_222_out, nand_194_out, nand_195_out);
  nand nand_223 (nand_223_out, nand_196_out, nand_197_out);
  nand nand_224 (out_36, nand_198_out, nand_199_out);
  nand nand_225 (nand_225_out, nand_200_out, nand_200_out);
  nand nand_226 (nand_226_out, nand_201_out, nand_201_out);
  nand nand_227 (nand_227_out, nand_202_out, nand_202_out);
  nand nand_228 (nand_228_out, nand_203_out, nand_203_out);
  nand nand_229 (nand_229_out, nand_204_out, nand_204_out);
  nand nand_230 (nand_230_out, nand_205_out, nand_205_out);
  and and_10 (out_1, and_6_out, and_7_out);
  nand nand_231 (out_10, nand_206_out, nand_207_out);
  nand nand_232 (out_13, nand_208_out, nand_209_out);
  nand nand_233 (out_16, nand_210_out, nand_211_out);
  nand nand_234 (out_19, nand_212_out, nand_213_out);
  nand nand_235 (nand_235_out, nand_218_out, nand_218_out);
  nand nand_236 (nand_236_out, nand_219_out, nand_219_out);
  nand nand_237 (nand_237_out, nand_220_out, nand_220_out);
  nand nand_238 (nand_238_out, nand_221_out, nand_221_out);
  and and_11 (and_11_out, and_8_out, C_6);
  nand nand_239 (nand_239_out, nand_222_out, nand_222_out);
  nand nand_240 (nand_240_out, nand_223_out, nand_223_out);
  nand nand_241 (nand_241_out, nand_225_out, nand_226_out);
  nand nand_242 (nand_242_out, nand_227_out, nand_228_out);
  nand nand_243 (out_26, nand_229_out, nand_230_out);
  and and_12 (F_3, and_11_out, and_9_out);
  nand nand_244 (out_90, nand_235_out, nand_188_out);
  nand nand_245 (out_91, nand_236_out, nand_188_out);
  nand nand_246 (out_92, nand_237_out, nand_188_out);
  nand nand_247 (out_93, nand_238_out, nand_188_out);
  Seven_Seg_Hex seven_seg_hex_1 (.d({3'b000, AL}), .dp(1'b0));
  Seven_Seg_Hex seven_seg_hex_2 (.d({AR3, AR2, AR1, AR0}), .dp(1'b0));
  nand nand_248 (out_77, nand_241_out, nand_241_out);
  nand nand_249 (out_31, nand_241_out, nand_242_out);
  nand nand_250 (out_43, nand_239_out, nand_240_out);
  nand nand_251 (nand_251_out, in_119, in_95);
  nand nand_252 (nand_252_out, in_120, in_96);
  nand nand_253 (nand_253_out, in_119, in_98);
  nand nand_254 (nand_254_out, in_120, in_99);
  nand nand_255 (nand_255_out, in_119, in_101);
  nand nand_256 (nand_256_out, in_120, in_102);
  nand nand_257 (nand_257_out, in_119, in_104);
  nand nand_258 (nand_258_out, in_120, in_105);
  nand nand_259 (nand_259_out, in_119, in_107);
  nand nand_260 (nand_260_out, in_120, in_108);
  nand nand_261 (nand_261_out, in_119, in_110);
  nand nand_262 (nand_262_out, in_120, in_111);
  nand nand_263 (nand_263_out, in_119, in_113);
  nand nand_264 (nand_264_out, in_120, in_114);
  nand nand_265 (nand_265_out, in_119, in_116);
  nand nand_266 (nand_266_out, in_120, in_117);
  nand nand_267 (nand_267_out, A_23, B_23);
  nand nand_268 (nand_268_out, D_6, E_4);
  nand nand_269 (nand_269_out, G_2, H_2);
  nand nand_270 (nand_270_out, I, J);
  nand nand_271 (nand_271_out, A0_2, A0_2);
  nand nand_272 (nand_272_out, B0_2, B0_2);
  nand nand_273 (nand_273_out, in_159, in_159);
  nand nand_274 (nand_274_out, in_160, in_160);
  nand nand_275 (out_97, nand_251_out, nand_252_out);
  nand nand_276 (out_100, nand_253_out, nand_254_out);
  nand nand_277 (out_103, nand_255_out, nand_256_out);
  nand nand_278 (out_106, nand_257_out, nand_258_out);
  nand nand_279 (out_109, nand_259_out, nand_260_out);
  nand nand_280 (out_112, nand_261_out, nand_262_out);
  nand nand_281 (out_115, nand_263_out, nand_264_out);
  nand nand_282 (out_118, nand_265_out, nand_266_out);
  nand nand_283 (nand_283_out, A0, B0);
  nand nand_284 (nand_284_out, in_278, in_279);
  nand nand_285 (nand_285_out, in_281, in_282);
  nand nand_286 (nand_286_out, in_253, in_254);
  nand nand_287 (nand_287_out, in_255, in_256);
  nand nand_288 (nand_288_out, in_257, in_258);
  nand nand_289 (nand_289_out, in_259, in_260);
  nand nand_290 (nand_290_out, nand_267_out, nand_267_out);
  nand nand_291 (nand_291_out, nand_268_out, nand_268_out);
  nand nand_292 (nand_292_out, nand_269_out, nand_269_out);
  nand nand_293 (nand_293_out, nand_270_out, nand_270_out);
  nand nand_294 (nand_294_out, I3, A0_2);
  nand nand_295 (nand_295_out, I2, nand_271_out);
  nand nand_296 (nand_296_out, I1_2, A0_2);
  nand nand_297 (nand_297_out, I0_2, nand_271_out);
  nand nand_298 (nand_298_out, nand_294_out, nand_295_out);
  nand nand_299 (nand_299_out, nand_296_out, nand_297_out);
  nand nand_300 (nand_300_out, A0, nand_283_out);
  nand nand_301 (nand_301_out, nand_283_out, B0);
  nand nand_302 (nand_302_out, in_159, in_160);
  nand nand_303 (nand_303_out, nand_273_out, nand_274_out);
  nand nand_304 (nand_304_out, nand_284_out, nand_284_out);
  nand nand_305 (nand_305_out, nand_285_out, nand_285_out);
  nand nand_306 (nand_306_out, nand_286_out, nand_286_out);
  nand nand_307 (nand_307_out, nand_287_out, nand_287_out);
  nand nand_308 (nand_308_out, nand_288_out, nand_288_out);
  nand nand_309 (nand_309_out, nand_289_out, nand_289_out);
  nand nand_310 (nand_310_out, nand_290_out, C_7);
  nand nand_311 (nand_311_out, nand_292_out, K);
  // NAnd nand_312 has open pins: In_1=A1, In_2=in_135, out=open
  nand nand_313 (nand_313_out, A1, B1);
  // NAnd nand_314 has open pins: In_1=in_137, In_2=B1, out=open
  nand nand_315 (nand_315_out, nand_300_out, nand_301_out);
  nand nand_316 (nand_316_out, nand_283_out, nand_283_out);
  nand nand_317 (out_158, nand_302_out, nand_303_out);
  nand nand_318 (nand_318_out, nand_304_out, in_280);
  nand nand_319 (nand_319_out, nand_305_out, in_283);
  nand nand_320 (nand_320_out, nand_306_out, nand_307_out);
  nand nand_321 (nand_321_out, nand_308_out, nand_309_out);
  nand nand_322 (nand_322_out, nand_310_out, nand_310_out);
  nand nand_323 (nand_323_out, nand_311_out, nand_311_out);
  nand nand_324 (nand_324_out, A_20, Sa_2);
  nand nand_325 (nand_325_out, B_20, Sb_2);
  and and_13 (and_13_out, A_19, Sa);
  and and_14 (and_14_out, B_19, Sb);
  nand nand_326 (nand_326_out, B0_2, nand_298_out);
  nand nand_327 (nand_327_out, nand_299_out, nand_272_out);
  nand nand_328 (nand_328_out, A1, nand_313_out);
  nand nand_329 (nand_329_out, nand_313_out, B1);
  nand nand_330 (out_232, nand_324_out, nand_325_out);
  or or_2 (out_227, and_13_out, and_14_out);
  nand nand_331 (Fout_2, nand_326_out, nand_327_out);
  nand nand_332 (out_284, nand_318_out, nand_319_out);
  nand nand_333 (out_252, nand_320_out, nand_321_out);
  nand nand_334 (nand_334_out, nand_322_out, nand_291_out);
  nand nand_335 (nand_335_out, nand_323_out, nand_293_out);
  nand nand_336 (out_136, nand_328_out, nand_329_out);
  nand nand_337 (nand_337_out, nand_315_out, I0);
  nand nand_338 (nand_338_out, nand_316_out, I1);
  nand nand_339 (F_4, nand_334_out, nand_335_out);
  nand nand_340 (Fout, nand_337_out, nand_338_out);
  nor nor_1 (nor_1_out, in_222, in_223);
  nor nor_2 (nor_2_out, in_224, in_225);
  nor nor_3 (nor_3_out, in_222, nor_1_out);
  nor nor_4 (nor_4_out, nor_1_out, in_223);
  nor nor_5 (nor_5_out, in_224, nor_2_out);
  nor nor_6 (nor_6_out, nor_2_out, in_225);
  xor xor_6 (xor_6_out, B_14, I2_2);
  xor xor_7 (xor_7_out, B_15, I2_3);
  xor xor_8 (xor_8_out, B_16, I2_4);
  nor nor_7 (nor_7_out, nor_3_out, nor_4_out);
  nor nor_8 (nor_8_out, nor_5_out, nor_6_out);
  xor xor_9 (xor_9_out, A_21, INV_A);
  xor xor_10 (xor_10_out, INV_B, B_21);
  nand nand_341 (out_287, in_285, out_288);
  nand nand_342 (out_288, out_287, in_286);
  nor nor_9 (nor_9_out, nor_8_out, in_226);
  xor xor_11 (out_163, A_10, B_10);
  and and_15 (out_164, A_10, B_10);
  xor xor_12 (xor_12_out, A_11, B_11);
  and and_16 (and_16_out, A_11, B_11);
  xor xor_13 (xor_13_out, A_12, B_12);
  and and_17 (and_17_out, A_12, B_12);
  xor xor_14 (xor_14_out, A_13, B_13);
  and and_18 (and_18_out, A_13, B_13);
  xor xor_15 (xor_15_out, A_14, xor_6_out);
  and and_19 (and_19_out, A_14, xor_6_out);
  xor xor_16 (xor_16_out, A_15, xor_7_out);
  and and_20 (and_20_out, A_15, xor_7_out);
  xor xor_17 (xor_17_out, A_16, xor_8_out);
  nand nand_343 (nand_343_out, A_16, xor_8_out);
  xor xor_18 (xor_18_out, xor_9_out, xor_10_out);
  nor nor_10 (nor_10_out, nor_8_out, nor_9_out);
  nor nor_11 (nor_11_out, nor_9_out, in_226);
  nor nor_12 (nor_12_out, nor_9_out, nor_2_out);
  nor nor_13 (nor_13_out, nor_10_out, nor_11_out);
  and and_21 (and_21_out, I0_3, xor_13_out);
  and and_22 (and_22_out, and_17_out, I1_3);
  and and_23 (and_23_out, I0_4, xor_14_out);
  and and_24 (and_24_out, and_18_out, I1_4);
  and and_25 (and_25_out, I0_5, xor_15_out);
  and and_26 (and_26_out, and_19_out, I1_5);
  and and_27 (and_27_out, I0_6, xor_16_out);
  and and_28 (and_28_out, and_20_out, I1_6);
  xor xor_19 (xor_19_out, 1'b1, nand_343_out);
  xor xor_20 (Sum_4, xor_12_out, Cin_3);
  and and_29 (and_29_out, xor_12_out, Cin_3);
  xor xor_21 (xor_21_out, xor_18_out, Cin_9);
  nand nand_344 (nand_344_out, xor_18_out, Cin_9);
  nand nand_345 (nand_345_out, xor_9_out, xor_10_out);
  or or_3 (Fout_3, and_21_out, and_22_out);
  or or_4 (or_4_out, and_23_out, and_24_out);
  or or_5 (or_5_out, and_25_out, and_26_out);
  or or_6 (or_6_out, and_27_out, and_28_out);
  nand nand_346 (nand_346_out, I0_7, xor_17_out);
  nand nand_347 (nand_347_out, xor_19_out, I1_7);
  nand nand_348 (nand_348_out, nand_344_out, nand_345_out);
  or or_7 (Cout, and_29_out, and_16_out);
  nand nand_349 (nand_349_out, nand_346_out, nand_347_out);
  xor xor_22 (Sum_5, or_4_out, Cin_4);
  and and_30 (and_30_out, or_4_out, Cin_4);
  xor xor_23 (Sum_6, or_5_out, Cin_5);
  and and_31 (and_31_out, or_5_out, Cin_5);
  xor xor_24 (Sum_7, or_6_out, Cin_6);
  and and_32 (and_32_out, or_6_out, Cin_6);
  xor xor_25 (Sum_8, nand_349_out, Cin_7);
  nand nand_350 (nand_350_out, nand_349_out, Cin_7);
  nand nand_351 (nand_351_out, xor_21_out, I0_9);
  nand nand_352 (nand_352_out, I1_9, nand_348_out);
  nand nand_353 (nand_353_out, nand_348_out, nSC);
  or or_8 (Cout_2, and_30_out, and_18_out);
  or or_9 (Cout_3, and_31_out, and_19_out);
  or or_10 (or_10_out, and_32_out, and_20_out);
  nand nand_354 (Fout_4, nand_351_out, nand_352_out);
  nand nand_355 (Cout_7, nand_353_out, nand_353_out);
  and and_33 (Cout_4, or_10_out, I3_2);
  nand nand_356 (nand_356_out, nand_350_out, nand_343_out);
  nand nand_357 (nand_357_out, in_215, in_216);
  nand nand_358 (nand_358_out, nand_356_out, I3_3);
  nand nand_359 (nand_359_out, nand_357_out, nand_357_out);
  nand nand_360 (nand_360_out, A_18, B_18);
  nand nand_361 (Cout_5, nand_358_out, nand_358_out);
  nand nand_362 (nand_362_out, in_213, in_213);
  nand nand_363 (nand_363_out, in_214, in_214);
  nand nand_364 (nand_364_out, A_18, nand_360_out);
  nand nand_365 (nand_365_out, nand_360_out, nand_360_out);
  nand nand_366 (nand_366_out, nand_360_out, B_18);
  xor xor_26 (xor_26_out, A_17, B_17);
  or or_11 (or_11_out, nand_362_out, nand_363_out);
  nand nand_367 (nand_367_out, nand_364_out, nand_366_out);
  nand nand_368 (nand_368_out, I0_8, nand_367_out);
  nand nand_369 (nand_369_out, nand_365_out, I1_8);
  xor xor_27 (Sum_9, xor_26_out, Cin_8);
  nand nand_370 (nand_370_out, xor_26_out, Cin_8);
  nand nand_371 (nand_371_out, A_17, B_17);
  nand nand_372 (out_221, nand_368_out, nand_369_out);
  nand nand_373 (Cout_6, nand_370_out, nand_371_out);
  nand nand_374 (nand_374_out, A2_3, B2_3);
  nand nand_375 (nand_375_out, A3_3, B3_3);
  nand nand_376 (nand_376_out, A2_4, B2_4);
  nand nand_377 (nand_377_out, A3_4, B3_4);
  nand nand_378 (nand_378_out, A5, B5);
  nand nand_379 (nand_379_out, A2_5, B2_5);
  nand nand_380 (nand_380_out, A4, B4);
  nand nand_381 (nand_381_out, A2_3, nand_374_out);
  nand nand_382 (nand_382_out, nand_374_out, B2_3);
  nand nand_383 (nand_383_out, A3_3, nand_375_out);
  nand nand_384 (nand_384_out, nand_375_out, B3_3);
  nand nand_385 (nand_385_out, A2_4, nand_376_out);
  nand nand_386 (nand_386_out, nand_376_out, B2_4);
  nand nand_387 (nand_387_out, A3_4, nand_377_out);
  nand nand_388 (nand_388_out, nand_377_out, B3_4);
  nand nand_389 (nand_389_out, A2_5, nand_379_out);
  nand nand_390 (nand_390_out, nand_379_out, B2_5);
  nand nand_391 (nand_391_out, A4, nand_380_out);
  nand nand_392 (nand_392_out, nand_380_out, B4);
  nand nand_393 (nand_393_out, A5, nand_378_out);
  nand nand_394 (nand_394_out, nand_378_out, B5);
  nand nand_395 (nand_395_out, A2_6, B2_6);
  nand nand_396 (nand_396_out, in_387, I4_2);
  nand nand_397 (nand_397_out, I5_2, in_388);
  nand nand_398 (nand_398_out, nand_381_out, nand_382_out);
  nand nand_399 (nand_399_out, nand_383_out, nand_384_out);
  nand nand_400 (nand_400_out, nand_385_out, nand_386_out);
  nand nand_401 (nand_401_out, nand_387_out, nand_388_out);
  nand nand_402 (nand_402_out, nand_389_out, nand_390_out);
  nand nand_403 (nand_403_out, nand_391_out, nand_392_out);
  nand nand_404 (nand_404_out, nand_393_out, nand_394_out);
  nand nand_405 (nand_405_out, nand_396_out, nand_397_out);
  nand nand_406 (nand_406_out, nand_398_out, Cin_10);
  nand nand_407 (nand_407_out, nand_399_out, nand_419_out);
  nand nand_408 (nand_408_out, nand_400_out, nand_422_out);
  nand nand_409 (nand_409_out, nand_401_out, nand_425_out);
  nand nand_410 (nand_410_out, nand_404_out, C0out);
  nand nand_411 (nand_411_out, A2_6, nand_395_out);
  nand nand_412 (nand_412_out, nand_395_out, B2_6);
  nand nand_413 (nand_413_out, nand_395_out, nand_395_out);
  nand nand_414 (Fout_8, nand_405_out, nand_405_out);
  nand nand_415 (nand_415_out, nand_402_out, Cin_11);
  nand nand_416 (nand_416_out, nand_403_out, Cin_12);
  nand nand_417 (nand_417_out, nand_398_out, nand_406_out);
  nand nand_418 (nand_418_out, nand_406_out, Cin_10);
  nand nand_419 (nand_419_out, nand_374_out, nand_406_out);
  nand nand_420 (nand_420_out, nand_399_out, nand_407_out);
  nand nand_421 (nand_421_out, nand_407_out, nand_419_out);
  nand nand_422 (nand_422_out, nand_375_out, nand_407_out);
  nand nand_423 (nand_423_out, nand_400_out, nand_408_out);
  nand nand_424 (nand_424_out, nand_408_out, nand_422_out);
  nand nand_425 (nand_425_out, nand_376_out, nand_408_out);
  nand nand_426 (nand_426_out, nand_401_out, nand_409_out);
  nand nand_427 (nand_427_out, nand_409_out, nand_425_out);
  nand nand_428 (C3out, nand_377_out, nand_409_out);
  nand nand_429 (nand_429_out, nand_404_out, nand_410_out);
  nand nand_430 (nand_430_out, nand_410_out, C0out);
  nand nand_431 (C0out_2, nand_378_out, nand_410_out);
  nand nand_432 (nand_432_out, nand_411_out, nand_412_out);
  nand nand_433 (nand_433_out, nand_402_out, nand_415_out);
  nand nand_434 (nand_434_out, nand_415_out, Cin_11);
  nand nand_435 (Cout_8, nand_379_out, nand_415_out);
  nand nand_436 (nand_436_out, nand_403_out, nand_416_out);
  nand nand_437 (nand_437_out, nand_416_out, Cin_12);
  nand nand_438 (C0out, nand_380_out, nand_416_out);
  nand nand_439 (SUM0, nand_417_out, nand_418_out);
  nand nand_440 (SUM1, nand_420_out, nand_421_out);
  nand nand_441 (SUM2, nand_423_out, nand_424_out);
  nand nand_442 (SUM3, nand_426_out, nand_427_out);
  nand nand_443 (nand_443_out, nand_429_out, nand_430_out);
  nand nand_444 (nand_444_out, nand_432_out, I4);
  nand nand_445 (nand_445_out, I5, nand_413_out);
  nand nand_446 (SUM_10, nand_433_out, nand_434_out);
  nand nand_447 (nand_447_out, nand_436_out, nand_437_out);
  nand nand_448 (Fout_7, nand_444_out, nand_445_out);
  nand nand_449 (nand_449_out, D_7, D_7);
  nand nand_450 (nand_450_out, D_8, D_8);
  nand nand_451 (nand_451_out, nand_447_out, nand_449_out);
  nand nand_452 (nand_452_out, D_7, Cin_13);
  nand nand_453 (nand_453_out, nand_443_out, nand_450_out);
  nand nand_454 (nand_454_out, D_8, C0out_2);
  nand nand_455 (Fout_5, nand_451_out, nand_452_out);
  nand nand_456 (Fout_6, nand_453_out, nand_454_out);
  nand nand_457 (nand_457_out, Bin, INV);
  nand nand_458 (nand_458_out, Bin, nand_457_out);
  nand nand_459 (nand_459_out, nand_457_out, INV);
  nand nand_460 (Out, nand_458_out, nand_459_out);
  nand nand_461 (nand_461_out, S, S);
  nand nand_462 (nand_462_out, nand_461_out, EN_3);
  nand nand_463 (nand_463_out, S, EN_3);
  nand nand_464 (nand_464_out, nand_462_out, nand_462_out);
  nand nand_465 (nand_465_out, nand_463_out, nand_463_out);
  nand nand_466 (nand_466_out, in_308, in_308);
  nand nand_467 (nand_467_out, in_309, in_309);
  nand nand_468 (nand_468_out, in_314, in_314);
  nand nand_469 (nand_469_out, in_315, in_315);
  nand nand_470 (nand_470_out, in_326, in_326);
  // NAnd nand_471 has open pins: In_1=in_320, In_2=in_320, out=open
  // NAnd nand_472 has open pins: In_1=in_321, In_2=in_321, out=open
  nand nand_473 (nand_473_out, in_342, in_342);
  nand nand_474 (nand_474_out, in_343, in_343);
  nand nand_475 (nand_475_out, in_340, in_340);
  nand nand_476 (nand_476_out, in_341, in_341);
  nand nand_477 (nand_477_out, in_338, in_338);
  nand nand_478 (nand_478_out, in_339, in_339);
  nand nand_479 (nand_479_out, in_333, in_334);
  nand nand_480 (nand_480_out, in_335, in_336);
  nand nand_481 (nand_481_out, in_328, in_329);
  nand nand_482 (nand_482_out, in_330, in_331);
  and and_34 (and_34_out, in_290, in_291);
  and and_35 (and_35_out, in_292, in_293);
  nand nand_483 (nand_483_out, nand_464_out, A2);
  nand nand_484 (nand_484_out, nand_465_out, B2);
  nand nand_485 (nand_485_out, nand_464_out, A3);
  nand nand_486 (nand_486_out, nand_465_out, B3);
  nand nand_487 (nand_487_out, nand_464_out, A2_2);
  nand nand_488 (nand_488_out, nand_465_out, B2_2);
  nand nand_489 (nand_489_out, nand_464_out, A3_2);
  nand nand_490 (nand_490_out, nand_465_out, B3_2);
  nand nand_491 (out_310, nand_466_out, nand_467_out);
  nand nand_492 (out_311, in_308, nand_467_out);
  nand nand_493 (out_312, nand_466_out, in_309);
  nand nand_494 (out_313, in_308, in_309);
  nand nand_495 (nand_495_out, nand_468_out, nand_469_out);
  nand nand_496 (nand_496_out, in_314, nand_469_out);
  nand nand_497 (nand_497_out, nand_468_out, in_315);
  nand nand_498 (nand_498_out, in_314, in_315);
  nand nand_499 (nand_499_out, nand_468_out, nand_469_out);
  nand nand_500 (nand_500_out, in_314, nand_469_out);
  nand nand_501 (nand_501_out, nand_468_out, in_315);
  nand nand_502 (nand_502_out, in_314, in_315);
  nand nand_503 (nand_503_out, nand_479_out, nand_479_out);
  nand nand_504 (nand_504_out, nand_480_out, nand_480_out);
  nand nand_505 (nand_505_out, nand_481_out, nand_481_out);
  nand nand_506 (nand_506_out, nand_482_out, nand_482_out);
  and and_36 (out_289, and_34_out, and_35_out);
  nand nand_507 (out_298, nand_483_out, nand_484_out);
  nand nand_508 (out_301, nand_485_out, nand_486_out);
  nand nand_509 (out_304, nand_487_out, nand_488_out);
  nand nand_510 (out_307, nand_489_out, nand_490_out);
  nand nand_511 (out_316, nand_470_out, nand_495_out);
  nand nand_512 (out_317, nand_470_out, nand_496_out);
  nand nand_513 (out_318, nand_470_out, nand_497_out);
  nand nand_514 (out_319, nand_470_out, nand_498_out);
  nand nand_515 (out_322, in_326, nand_499_out);
  nand nand_516 (out_323, in_326, nand_500_out);
  nand nand_517 (out_324, in_326, nand_501_out);
  nand nand_518 (out_325, in_326, nand_502_out);
  nand nand_519 (nand_519_out, nand_473_out, nand_474_out);
  nand nand_520 (nand_520_out, nand_475_out, nand_476_out);
  nand nand_521 (out_337, nand_477_out, nand_478_out);
  nand nand_522 (nand_522_out, nand_503_out, nand_504_out);
  nand nand_523 (out_327, nand_505_out, nand_506_out);
  nand nand_524 (nand_524_out, nand_519_out, nand_519_out);
  nand nand_525 (nand_525_out, nand_520_out, nand_520_out);
  nand nand_526 (out_332, nand_522_out, nand_522_out);
  nand nand_527 (out_344, nand_524_out, nand_525_out);
  nand nand_528 (nand_528_out, S3_3, S3_3);
  nand nand_529 (nand_529_out, S4_3, S4_3);
  nand nand_530 (nand_530_out, S3_3, S4_3);
  nand nand_531 (nand_531_out, S3_2, S3_2);
  nand nand_532 (nand_532_out, S4_2, S4_2);
  nand nand_533 (nand_533_out, S3_4, S3_4);
  nand nand_534 (nand_534_out, S4_4, S4_4);
  nand nand_535 (nand_535_out, S3, S3);
  nand nand_536 (nand_536_out, E1, E0);
  nand nand_537 (nand_537_out, D_10, S3_3);
  nand nand_538 (nand_538_out, C_9, nand_528_out);
  nand nand_539 (nand_539_out, B_25, S3_3);
  nand nand_540 (nand_540_out, A_25, nand_528_out);
  nand nand_541 (nand_541_out, S4, S4);
  nand nand_542 (nand_542_out, D_9, S3_2);
  nand nand_543 (nand_543_out, C_8, nand_531_out);
  nand nand_544 (nand_544_out, B_24, S3_2);
  nand nand_545 (nand_545_out, A_24, nand_531_out);
  nand nand_546 (nand_546_out, D_11, S3_4);
  nand nand_547 (nand_547_out, C_10, nand_533_out);
  nand nand_548 (nand_548_out, B_26, S3_4);
  nand nand_549 (nand_549_out, A_26, nand_533_out);
  nand nand_550 (nand_550_out, D3, nand_536_out);
  nand nand_551 (nand_551_out, S4, S3);
  nand nand_552 (nand_552_out, D2, nand_536_out);
  nand nand_553 (nand_553_out, nand_535_out, S4);
  nand nand_554 (nand_554_out, D1, nand_536_out);
  nand nand_555 (nand_555_out, S3, nand_541_out);
  nand nand_556 (nand_556_out, D0, nand_536_out);
  nand nand_557 (nand_557_out, nand_535_out, nand_541_out);
  nand nand_558 (nand_558_out, nand_537_out, nand_538_out);
  nand nand_559 (nand_559_out, nand_539_out, nand_540_out);
  nand nand_560 (nand_560_out, nand_542_out, nand_543_out);
  nand nand_561 (nand_561_out, nand_544_out, nand_545_out);
  nand nand_562 (nand_562_out, nand_546_out, nand_547_out);
  nand nand_563 (nand_563_out, nand_548_out, nand_549_out);
  nand nand_564 (nand_564_out, S4_3, nand_558_out);
  nand nand_565 (nand_565_out, nand_559_out, nand_529_out);
  nand nand_566 (nand_566_out, nand_550_out, nand_550_out);
  nand nand_567 (nand_567_out, nand_551_out, nand_551_out);
  nand nand_568 (nand_568_out, nand_552_out, nand_552_out);
  nand nand_569 (nand_569_out, nand_553_out, nand_553_out);
  nand nand_570 (nand_570_out, nand_554_out, nand_554_out);
  nand nand_571 (nand_571_out, nand_555_out, nand_555_out);
  nand nand_572 (nand_572_out, nand_556_out, nand_556_out);
  nand nand_573 (nand_573_out, nand_557_out, nand_557_out);
  nand nand_574 (nand_574_out, S4_2, nand_560_out);
  nand nand_575 (nand_575_out, nand_561_out, nand_532_out);
  nand nand_576 (nand_576_out, S4_4, nand_562_out);
  nand nand_577 (nand_577_out, nand_563_out, nand_534_out);
  nand nand_578 (nand_578_out, nand_564_out, nand_565_out);
  nand nand_579 (nand_579_out, nand_574_out, nand_575_out);
  nand nand_580 (nand_580_out, nand_576_out, nand_577_out);
  nand nand_581 (nand_581_out, nand_566_out, nand_567_out);
  nand nand_582 (nand_582_out, nand_568_out, nand_569_out);
  nand nand_583 (nand_583_out, nand_570_out, nand_571_out);
  nand nand_584 (nand_584_out, nand_572_out, nand_573_out);
  nand nand_585 (nand_585_out, nand_578_out, Cin_14);
  nand nand_586 (nand_586_out, nand_579_out, EN_4);
  LED led_37 (.in(nand_580_out));
  nand nand_587 (nand_587_out, nand_578_out, nand_585_out);
  nand nand_588 (nand_588_out, nand_585_out, Cin_14);
  nand nand_589 (nand_589_out, nand_585_out, nand_530_out);
  nand nand_590 (nand_590_out, nand_581_out, nand_582_out);
  nand nand_591 (nand_591_out, nand_583_out, nand_584_out);
  nand nand_592 (nand_592_out, nand_586_out, nand_586_out);
  nand nand_593 (nand_593_out, nand_587_out, nand_588_out);
  nand nand_594 (nand_594_out, nand_589_out, SC);
  nand nand_595 (nand_595_out, nand_590_out, nand_590_out);
  nand nand_596 (nand_596_out, nand_591_out, nand_591_out);
  LED led_38 (.in(nand_592_out));
  LED u_Sum (.in(nand_593_out));
  nand nand_597 (nand_597_out, nand_594_out, nand_594_out);
  nand nand_598 (nand_598_out, nand_595_out, nand_596_out);
  LED u_Cout (.in(nand_597_out));
  LED led_39 (.in(nand_598_out));
  nand nand_599 (nand_599_out, in_432, in_433);
  nand nand_600 (nand_600_out, in_434, in_435);
  nand nand_601 (nand_601_out, in_421, in_422);
  nand nand_602 (nand_602_out, in_423, in_424);
  nand nand_603 (nand_603_out, in_407, in_408);
  nand nand_604 (nand_604_out, in_436, in_436);
  nand nand_605 (nand_605_out, in_409, in_410);
  nand nand_606 (nand_606_out, in_411, in_411);
  nand nand_607 (nand_607_out, in_412, in_412);
  nand nand_608 (nand_608_out, nand_601_out, nand_601_out);
  nand nand_609 (nand_609_out, nand_602_out, nand_602_out);
  nand nand_610 (nand_610_out, nand_603_out, nand_604_out);
  nand nand_611 (nand_611_out, nand_604_out, nand_605_out);
  nand nand_612 (nand_612_out, nand_599_out, nand_599_out);
  nand nand_613 (nand_613_out, nand_600_out, nand_600_out);
  nand nand_614 (nand_614_out, nand_606_out, nand_607_out);
  nand nand_615 (nand_615_out, nand_612_out, nand_613_out);
  nand nand_616 (nand_616_out, nand_608_out, nand_609_out);
  nand nand_617 (nand_617_out, nand_610_out, nand_611_out);
  LED led_40 (.in(nand_616_out));
  LED led_41 (.in(nand_614_out));
  LED led_42 (.in(nand_615_out));
  LED led_43 (.in(nand_617_out));
  nand nand_618 (nand_618_out, in_439, in_439);
  nand nand_619 (nand_619_out, in_440, in_440);
  nand nand_620 (nand_620_out, in_437, in_437);
  nand nand_621 (nand_621_out, in_438, in_438);
  nor nor_14 (nor_14_out, in_389, in_391, in_393, in_395);
  xor xor_28 (xor_28_out, in_389, in_390);
  xor xor_29 (xor_29_out, in_391, in_392);
  xor xor_30 (xor_30_out, in_393, in_394);
  xor xor_31 (xor_31_out, in_395, in_396);
  nand nand_622 (nand_622_out, nand_618_out, nand_619_out);
  nand nand_623 (nand_623_out, nand_620_out, nand_621_out);
  nand nand_624 (nand_624_out, nand_622_out, nand_622_out);
  nand nand_625 (nand_625_out, nand_623_out, nand_623_out);
  nor nor_15 (nor_15_out, xor_28_out, xor_29_out, xor_30_out, xor_31_out);
  nand nand_626 (nand_626_out, nand_624_out, nand_625_out);
  LED led_44 (.in(nor_14_out));
  LED led_45 (.in(nor_15_out));
  nand nand_627 (nand_627_out, nLD, nLD);
  LED led_46 (.in(nand_626_out));
  nand nand_628 (nand_628_out, nand_662_out, nLD);
  nand nand_629 (nand_629_out, nand_627_out, DATA);
  nand nand_630 (nand_630_out, nand_628_out, nand_629_out);
  nand nand_631 (nand_631_out, CK, CK);
  nand nand_632 (nand_632_out, nand_630_out, nand_630_out);
  nand nand_633 (nand_633_out, in_403, in_403);
  nand nand_634 (nand_634_out, nand_669_out, nand_669_out);
  nand nand_635 (nand_635_out, CLK_2, CLK_2);
  nand nand_636 (nand_636_out, DAT_2, DAT_2);
  nand nand_637 (nand_637_out, nand_630_out, nand_631_out);
  nand nand_638 (nand_638_out, nand_631_out, nand_632_out);
  nand nand_639 (nand_639_out, nand_667_out, DAT, in_399);
  nand nand_640 (nand_640_out, in_399, DAT, nand_666_out);
  nand nand_641 (nand_641_out, in_399, in_399);
  nand nand_642 (nand_642_out, nand_669_out, nand_633_out);
  nand nand_643 (nand_643_out, nand_633_out, nand_634_out);
  nand nand_644 (nand_644_out, DAT_2, nand_635_out);
  nand nand_645 (nand_645_out, nand_635_out, nand_636_out);
  nand nand_646 (nand_646_out, nand_637_out, nand_647_out);
  nand nand_647 (nand_647_out, nand_646_out, nand_638_out);
  nand nand_648 (nand_648_out, nand_642_out, nand_649_out);
  nand nand_649 (nand_649_out, nand_648_out, nand_643_out);
  nand nand_650 (nand_650_out, nand_639_out, nand_651_out);
  nand nand_651 (nand_651_out, nand_650_out, nand_640_out);
  nand nand_652 (nand_652_out, nand_644_out, nand_653_out);
  nand nand_653 (nand_653_out, nand_652_out, nand_645_out);
  nand nand_654 (nand_654_out, nand_646_out, CK);
  nand nand_655 (nand_655_out, CK, nand_647_out);
  nand nand_656 (nand_656_out, CLK_2, nand_652_out);
  nand nand_657 (nand_657_out, nand_653_out, CLK_2);
  nand nand_658 (nand_658_out, nand_648_out, in_403);
  nand nand_659 (nand_659_out, in_403, nand_649_out);
  nand nand_660 (nand_660_out, nand_650_out, nand_641_out);
  nand nand_661 (nand_661_out, nand_641_out, nand_651_out);
  nand nand_662 (nand_662_out, nand_654_out, nand_663_out);
  nand nand_663 (nand_663_out, nand_662_out, nand_655_out);
  nand nand_664 (nand_664_out, nand_656_out, nand_665_out);
  nand nand_665 (nand_665_out, nand_664_out, nand_657_out);
  nand nand_666 (nand_666_out, nand_660_out, nand_667_out);
  nand nand_667 (nand_667_out, nand_666_out, nand_661_out);
  nand nand_668 (nand_668_out, nand_658_out, nand_669_out);
  nand nand_669 (nand_669_out, nand_668_out, nand_659_out);
  LED Q (.in(nand_662_out));
  LED nQ (.in(nand_663_out));
  LED Q_2 (.in(nand_664_out));
  LED nQ_2 (.in(nand_665_out));
  LED Q_3 (.in(nand_668_out));
  LED nQ_3 (.in(nand_669_out));
  LED Q_4 (.in(nand_666_out));
  LED nQ_4 (.in(nand_667_out));

  // Other names for the same wires on the sheet: IR4 = in_59; IR5 = in_60; IR6 = in_61

  // Notes on the sheet:
  //   8 Input Multiplexer (74151) 24 Gates
  //   6 Input Multiplexer 22 Gates
  //   3 to 8 Instruction decoder - 27 Gates
  //   LOAD
  //   AND
  //   OR
  //   XOR
  //   ADD
  //   SUB
  //   STORE
  //   JMP
  //   2 to 4 line decoder with enable ('139)
  //   2 to 4 line decoder without enable
  //   4:1 Multiplexer with Enable
  //   1 of 8 decoder (74xx138)
  //   CONTROL UNIT
  //   S
  //   EN
  //   74xx157 equiv
  //   half 74xx139 without enable equiv 5 gates
  //   Octal Inverter/Driver
  //   Half 74139 equiv  15 gates
  //   4 Input AND
  //   4 Input NAND
  //   4-input AND
  //   2 Input OR
  //   4 Input OR
  //   INSTRUCTION
  //   4:1 Multiplexer (Half 74153 equiv).
  //   Mux1
  //   Mux2
  //   Dual 4-Input AND-OR
  //   Dual 5-Input AND-OR
  //   Dual 3-Input AND-OR
  //   XNOR using A-O
  //   Mux Equiv.
  //   Mux3
  //   I1 I0
  //   0      0    Zero
  //   0      1    XOR
  //   1      0   AND
  //   1      1   OR
  //   XNOR made from NOR
  //   Carry Suppress
  //   Suppress Carry
  //   Invert B
  //   Full Adder made from NOR
  //   Half Adder
  //   Half Adder 1
  //   Three Chip ALU bitslice
  //   Partial Sum
  //   Partial Carry
  //   Partial Sum =  A XOR B
  //   Partial Carry = A AND B
  //   Half Adder 2
  //   2 Input MUX
  //   ZERO, XOR, AND, OR network.
  //   1 Bit full adder
  //   1-bit Full Adder
  //   AND-OR-INV Gate
  //   1-bit Logic Gate
  //   2-input XOR used to selectively invert an input.
  //   If INV=1, the Bin will be inverted.
  //   A
  //   B
  //   C
  //   half 74xx139 equiv
  //   19 gate ALU with carry suppress
  //   4:1 Multiplexer (no enable)
  //   4:1 Multiplexer (MK 2)
  //   4:1 Multiplexer
  //   4 Input AND-OR
  //   2-Input OR
  //   4-Input Nand
  //   4-bit Comparator A=B and Zero Detect A=0
  //   4002
  //   A=0
  //   A=B
  //   1-bit register
  //   D-Type Flipflop
  //   Toggle -Type Flipflop
  //   Master-Slave JK Flipflop
endmodule
