// Digital circuit basic_gates_2.dig as structural Verilog
module basic_gates_2 (
  input  in_2,
  input  in_3,
  input  in_4,
  input  in_5,
  input  S,
  input  A0,
  input  EN,
  input  B0,
  input  A1,
  input  B1,
  input  A2,
  input  B2,
  input  A3,
  input  B3,
  input  in_20,
  input  in_21,
  input  in_26,
  input  in_27,
  input  in_32,
  input  in_33,
  input  in_38,
  input  in_40,
  input  in_41,
  input  in_42,
  input  in_43,
  input  in_45,
  input  in_46,
  input  in_47,
  input  in_48,
  input  in_50,
  input  in_51,
  input  in_52,
  input  in_53,
  input  in_54,
  input  in_55,
  input  Bin,
  input  INV,
  input  A0_2,
  input  B0_2,
  input  Cin,
  input  A1_2,
  input  B1_2,
  input  A2_2,
  input  B2_2,
  input  A3_2,
  input  B3_2,
  input  A0_3,
  input  B0_3,
  input  Cin_2,
  input  A4,
  input  B4,
  input  Cin_3,
  input  D,
  input  A5,
  input  B5,
  input  Cin_4,
  input  D_2,
  input  A0_4,
  input  B0_4,
  input  I0,
  input  I1,
  input  I0_2,
  input  I1_2,
  input  in_99,
  input  in_100,
  output out_1,
  output out_10,
  output out_13,
  output out_16,
  output out_19,
  output out_22,
  output out_23,
  output out_24,
  output out_25,
  output out_28,
  output out_29,
  output out_30,
  output out_31,
  output out_34,
  output out_35,
  output out_36,
  output out_37,
  output out_39,
  output out_44,
  output out_49,
  output out_56,
  output Out,
  output SUM0,
  output SUM1,
  output SUM2,
  output SUM3,
  output C3out,
  output SUM,
  output Cout,
  output Fout,
  output C0out,
  output Fout_2,
  output C0out_2,
  output Fout_3,
  output Fout_4
);

  wire and_1_out, and_2_out, nand_1_out, nand_2_out, nand_3_out, nand_4_out, nand_5_out, nand_6_out,
       nand_7_out, nand_8_out, nand_9_out, nand_10_out, nand_11_out, nand_12_out, nand_13_out, nand_14_out,
       nand_15_out, nand_16_out, nand_17_out, nand_18_out, nand_19_out, nand_20_out, nand_21_out,
       nand_22_out, nand_23_out, nand_24_out, nand_25_out, nand_26_out, nand_27_out, nand_28_out,
       nand_29_out, nand_30_out, nand_31_out, nand_32_out, nand_33_out, nand_34_out, nand_35_out,
       nand_36_out, nand_37_out, nand_38_out, nand_39_out, nand_40_out, nand_41_out, nand_42_out,
       nand_44_out, nand_45_out, nand_46_out, nand_47_out, nand_48_out, nand_49_out, nand_50_out,
       nand_51_out, nand_52_out, nand_53_out, nand_54_out, nand_55_out, nand_57_out, nand_58_out,
       nand_60_out, nand_61_out, nand_63_out, nand_64_out, nand_66_out, nand_67_out, nand_73_out,
       nand_74_out, nand_76_out, nand_77_out, nand_78_out, nand_79_out, nand_80_out, nand_81_out,
       nand_84_out, nand_85_out, nand_86_out, nand_88_out, nand_89_out, nand_90_out, nand_91_out,
       nand_92_out, nand_93_out, nand_94_out, nand_95_out, nand_96_out, nand_97_out, nand_100_out,
       nand_101_out, nand_102_out, nand_103_out, nand_104_out, nand_105_out, nand_106_out, nand_107_out,
       nand_112_out, nand_113_out, nand_114_out, nand_115_out, nand_116_out, nand_117_out, nand_118_out,
       nand_119_out, nand_120_out, nand_121_out, nand_122_out, nand_123_out, nand_124_out, nand_125_out,
       nand_126_out, nand_127_out, nand_128_out, nand_129_out, nand_130_out, nand_131_out, nand_133_out,
       nand_134_out, nand_135_out, nand_136_out, nand_149_out, nand_150_out, nand_151_out;

  nand nand_1 (nand_1_out, A0_2, B0_2);
  nand nand_2 (nand_2_out, A1_2, B1_2);
  nand nand_3 (nand_3_out, A2_2, B2_2);
  nand nand_4 (nand_4_out, A3_2, B3_2);
  nand nand_5 (nand_5_out, A0_3, B0_3);
  nand nand_6 (nand_6_out, A4, B4);
  nand nand_7 (nand_7_out, A5, B5);
  nand nand_8 (nand_8_out, A0_2, nand_1_out);
  nand nand_9 (nand_9_out, nand_1_out, B0_2);
  nand nand_10 (nand_10_out, A1_2, nand_2_out);
  nand nand_11 (nand_11_out, nand_2_out, B1_2);
  nand nand_12 (nand_12_out, A2_2, nand_3_out);
  nand nand_13 (nand_13_out, nand_3_out, B2_2);
  nand nand_14 (nand_14_out, A3_2, nand_4_out);
  nand nand_15 (nand_15_out, nand_4_out, B3_2);
  nand nand_16 (nand_16_out, A5, nand_7_out);
  nand nand_17 (nand_17_out, nand_7_out, B5);
  nand nand_18 (nand_18_out, A0_3, nand_5_out);
  nand nand_19 (nand_19_out, nand_5_out, B0_3);
  nand nand_20 (nand_20_out, A4, nand_6_out);
  nand nand_21 (nand_21_out, nand_6_out, B4);
  nand nand_22 (nand_22_out, in_99, I0_2);
  nand nand_23 (nand_23_out, I1_2, in_100);
  nand nand_24 (nand_24_out, nand_8_out, nand_9_out);
  nand nand_25 (nand_25_out, nand_10_out, nand_11_out);
  nand nand_26 (nand_26_out, nand_12_out, nand_13_out);
  nand nand_27 (nand_27_out, nand_14_out, nand_15_out);
  nand nand_28 (nand_28_out, nand_16_out, nand_17_out);
  nand nand_29 (nand_29_out, A0_4, B0_4);
  nand nand_30 (nand_30_out, nand_18_out, nand_19_out);
  nand nand_31 (nand_31_out, nand_20_out, nand_21_out);
  nand nand_32 (nand_32_out, nand_22_out, nand_23_out);
  nand nand_33 (nand_33_out, A0_4, nand_29_out);
  nand nand_34 (nand_34_out, nand_29_out, B0_4);
  nand nand_35 (nand_35_out, nand_29_out, nand_29_out);
  nand nand_36 (nand_36_out, nand_24_out, Cin);
  nand nand_37 (nand_37_out, nand_25_out, nand_47_out);
  nand nand_38 (nand_38_out, nand_26_out, nand_50_out);
  nand nand_39 (nand_39_out, nand_27_out, nand_53_out);
  nand nand_40 (nand_40_out, nand_30_out, Cin_2);
  nand nand_41 (nand_41_out, nand_31_out, Cin_3);
  nand nand_42 (nand_42_out, nand_28_out, C0out);
  nand nand_43 (Fout_4, nand_32_out, nand_32_out);
  nand nand_44 (nand_44_out, nand_33_out, nand_34_out);
  nand nand_45 (nand_45_out, nand_24_out, nand_36_out);
  nand nand_46 (nand_46_out, nand_36_out, Cin);
  nand nand_47 (nand_47_out, nand_1_out, nand_36_out);
  nand nand_48 (nand_48_out, nand_25_out, nand_37_out);
  nand nand_49 (nand_49_out, nand_37_out, nand_47_out);
  nand nand_50 (nand_50_out, nand_2_out, nand_37_out);
  nand nand_51 (nand_51_out, nand_26_out, nand_38_out);
  nand nand_52 (nand_52_out, nand_38_out, nand_50_out);
  nand nand_53 (nand_53_out, nand_3_out, nand_38_out);
  nand nand_54 (nand_54_out, nand_27_out, nand_39_out);
  nand nand_55 (nand_55_out, nand_39_out, nand_53_out);
  nand nand_56 (C3out, nand_4_out, nand_39_out);
  nand nand_57 (nand_57_out, nand_30_out, nand_40_out);
  nand nand_58 (nand_58_out, nand_40_out, Cin_2);
  nand nand_59 (Cout, nand_5_out, nand_40_out);
  nand nand_60 (nand_60_out, nand_31_out, nand_41_out);
  nand nand_61 (nand_61_out, nand_41_out, Cin_3);
  nand nand_62 (C0out, nand_6_out, nand_41_out);
  nand nand_63 (nand_63_out, nand_28_out, nand_42_out);
  nand nand_64 (nand_64_out, nand_42_out, C0out);
  nand nand_65 (C0out_2, nand_7_out, nand_42_out);
  nand nand_66 (nand_66_out, nand_44_out, I0);
  nand nand_67 (nand_67_out, I1, nand_35_out);
  nand nand_68 (SUM0, nand_45_out, nand_46_out);
  nand nand_69 (SUM1, nand_48_out, nand_49_out);
  nand nand_70 (SUM2, nand_51_out, nand_52_out);
  nand nand_71 (SUM3, nand_54_out, nand_55_out);
  nand nand_72 (SUM, nand_57_out, nand_58_out);
  nand nand_73 (nand_73_out, nand_60_out, nand_61_out);
  nand nand_74 (nand_74_out, nand_63_out, nand_64_out);
  nand nand_75 (Fout_3, nand_66_out, nand_67_out);
  nand nand_76 (nand_76_out, D_2, D_2);
  nand nand_77 (nand_77_out, D, D);
  nand nand_78 (nand_78_out, nand_74_out, nand_76_out);
  nand nand_79 (nand_79_out, D_2, C0out_2);
  nand nand_80 (nand_80_out, nand_73_out, nand_77_out);
  nand nand_81 (nand_81_out, D, Cin_4);
  nand nand_82 (Fout_2, nand_78_out, nand_79_out);
  nand nand_83 (Fout, nand_80_out, nand_81_out);
  nand nand_84 (nand_84_out, Bin, INV);
  nand nand_85 (nand_85_out, Bin, nand_84_out);
  nand nand_86 (nand_86_out, nand_84_out, INV);
  nand nand_87 (Out, nand_85_out, nand_86_out);
  nand nand_88 (nand_88_out, S, S);
  nand nand_89 (nand_89_out, nand_88_out, EN);
  nand nand_90 (nand_90_out, S, EN);
  nand nand_91 (nand_91_out, nand_89_out, nand_89_out);
  nand nand_92 (nand_92_out, nand_90_out, nand_90_out);
  nand nand_93 (nand_93_out, in_20, in_20);
  nand nand_94 (nand_94_out, in_21, in_21);
  nand nand_95 (nand_95_out, in_26, in_26);
  nand nand_96 (nand_96_out, in_27, in_27);
  nand nand_97 (nand_97_out, in_38, in_38);
  // NAnd nand_98 has open pins: In_1=in_32, In_2=in_32, out=open
  // NAnd nand_99 has open pins: In_1=in_33, In_2=in_33, out=open
  and and_1 (and_1_out, in_2, in_3);
  and and_2 (and_2_out, in_4, in_5);
  nand nand_100 (nand_100_out, nand_91_out, A0);
  nand nand_101 (nand_101_out, nand_92_out, B0);
  nand nand_102 (nand_102_out, nand_91_out, A1);
  nand nand_103 (nand_103_out, nand_92_out, B1);
  nand nand_104 (nand_104_out, nand_91_out, A2);
  nand nand_105 (nand_105_out, nand_92_out, B2);
  nand nand_106 (nand_106_out, nand_91_out, A3);
  nand nand_107 (nand_107_out, nand_92_out, B3);
  nand nand_108 (out_22, nand_93_out, nand_94_out);
  nand nand_109 (out_23, in_20, nand_94_out);
  nand nand_110 (out_24, nand_93_out, in_21);
  nand nand_111 (out_25, in_20, in_21);
  nand nand_112 (nand_112_out, nand_95_out, nand_96_out);
  nand nand_113 (nand_113_out, in_26, nand_96_out);
  nand nand_114 (nand_114_out, nand_95_out, in_27);
  nand nand_115 (nand_115_out, in_26, in_27);
  nand nand_116 (nand_116_out, nand_95_out, nand_96_out);
  nand nand_117 (nand_117_out, in_26, nand_96_out);
  nand nand_118 (nand_118_out, nand_95_out, in_27);
  nand nand_119 (nand_119_out, in_26, in_27);
  nand nand_120 (nand_120_out, in_54, in_54);
  nand nand_121 (nand_121_out, in_55, in_55);
  nand nand_122 (nand_122_out, in_52, in_52);
  nand nand_123 (nand_123_out, in_53, in_53);
  nand nand_124 (nand_124_out, in_50, in_50);
  nand nand_125 (nand_125_out, in_51, in_51);
  nand nand_126 (nand_126_out, in_45, in_46);
  nand nand_127 (nand_127_out, in_47, in_48);
  nand nand_128 (nand_128_out, in_40, in_41);
  nand nand_129 (nand_129_out, in_42, in_43);
  nand nand_130 (nand_130_out, nand_120_out, nand_121_out);
  nand nand_131 (nand_131_out, nand_122_out, nand_123_out);
  nand nand_132 (out_49, nand_124_out, nand_125_out);
  nand nand_133 (nand_133_out, nand_126_out, nand_126_out);
  nand nand_134 (nand_134_out, nand_127_out, nand_127_out);
  nand nand_135 (nand_135_out, nand_128_out, nand_128_out);
  nand nand_136 (nand_136_out, nand_129_out, nand_129_out);
  and and_3 (out_1, and_1_out, and_2_out);
  nand nand_137 (out_10, nand_100_out, nand_101_out);
  nand nand_138 (out_13, nand_102_out, nand_103_out);
  nand nand_139 (out_16, nand_104_out, nand_105_out);
  nand nand_140 (out_19, nand_106_out, nand_107_out);
  nand nand_141 (out_28, nand_97_out, nand_112_out);
  nand nand_142 (out_29, nand_97_out, nand_113_out);
  nand nand_143 (out_30, nand_97_out, nand_114_out);
  nand nand_144 (out_31, nand_97_out, nand_115_out);
  nand nand_145 (out_34, in_38, nand_116_out);
  nand nand_146 (out_35, in_38, nand_117_out);
  nand nand_147 (out_36, in_38, nand_118_out);
  nand nand_148 (out_37, in_38, nand_119_out);
  nand nand_149 (nand_149_out, nand_130_out, nand_130_out);
  nand nand_150 (nand_150_out, nand_131_out, nand_131_out);
  nand nand_151 (nand_151_out, nand_133_out, nand_134_out);
  nand nand_152 (out_39, nand_135_out, nand_136_out);
  nand nand_153 (out_44, nand_151_out, nand_151_out);
  nand nand_154 (out_56, nand_149_out, nand_150_out);

  // Notes on the sheet:
  //   1 Bit full adder
  //   1-bit Full Adder
  //   AND-OR-INV Gate
  //   1-bit Logic Gate
  //   2-input XOR used to selectively invert an input.
  //   If INV=1, the Bin will be inverted.
  //   A
  //   B
  //   C
  //   half 74xx139 equiv
  //   74xx157 equiv
  //   4 Input AND
  //   4 Input NAND
  //   4-input AND
  //   2 Input OR
  //   4 Input OR
endmodule
