// Digital circuit basic_gates_3.dig as structural Verilog
module basic_gates_3 (
  input  in_1,
  input  in_2,
  input  in_3,
  input  in_4,
  input  in_5,
  input  in_6,
  input  in_7,
  input  in_8,
  input  A,
  input  B,
  input  DAT,
  input  CLK,
  input  in_13,
  input  DAT_2,
  input  CLK_2,
  input  DAT_3,
  input  in_17,
  input  DATA,
  input  CK,
  input  nLD,
  input  in_21,
  input  in_22,
  input  in_23,
  input  in_24,
  input  in_25,
  input  in_26,
  input  D3,
  input  D2,
  input  D1,
  input  D0,
  input  S1,
  input  S0,
  input  E1,
  input  E0,
  input  in_35,
  input  in_36,
  input  in_37,
  input  in_38,
  input  C,
  input  S0_2,
  input  D,
  input  A_2,
  input  B_2,
  input  S1_2,
  input  EN,
  input  in_46,
  input  in_47,
  input  in_48,
  input  in_49,
  input  in_50,
  input  in_51,
  input  in_52,
  input  in_53,
  input  in_54,
  input  C_2,
  input  S0_3,
  input  D_2,
  input  A_3,
  input  B_3,
  input  S1_3,
  input  Cin,
  input  C_3,
  input  S0_4,
  input  D_3,
  input  A_4,
  input  B_4,
  input  S1_4,
  input  SC,
  input  nG,
  input  nA_B,
  input  in_71,
  input  in_72,
  input  A_5,
  input  B_5,
  input  nA_B_2,
  input  A_6,
  input  B_6
);

  wire and_1_out, and_2_out, and_3_out, and_4_out, nand_1_out, nand_2_out, nand_3_out, nand_4_out,
       nand_5_out, nand_6_out, nand_7_out, nand_8_out, nand_9_out, nand_10_out, nand_11_out, nand_12_out,
       nand_13_out, nand_14_out, nand_15_out, nand_16_out, nand_17_out, nand_18_out, nand_19_out,
       nand_20_out, nand_21_out, nand_22_out, nand_23_out, nand_24_out, nand_25_out, nand_26_out,
       nand_27_out, nand_28_out, nand_29_out, nand_30_out, nand_31_out, nand_32_out, nand_33_out,
       nand_34_out, nand_35_out, nand_36_out, nand_37_out, nand_38_out, nand_39_out, nand_40_out,
       nand_41_out, nand_42_out, nand_43_out, nand_44_out, nand_45_out, nand_46_out, nand_47_out,
       nand_48_out, nand_49_out, nand_50_out, nand_51_out, nand_52_out, nand_53_out, nand_54_out,
       nand_55_out, nand_56_out, nand_57_out, nand_58_out, nand_59_out, nand_60_out, nand_61_out,
       nand_62_out, nand_63_out, nand_64_out, nand_65_out, nand_66_out, nand_67_out, nand_68_out,
       nand_69_out, nand_70_out, nand_71_out, nand_72_out, nand_73_out, nand_74_out, nand_75_out,
       nand_76_out, nand_77_out, nand_78_out, nand_79_out, nand_80_out, nand_81_out, nand_82_out,
       nand_83_out, nand_84_out, nand_85_out, nand_86_out, nand_87_out, nand_88_out, nand_89_out,
       nand_90_out, nand_91_out, nand_92_out, nand_93_out, nand_94_out, nand_95_out, nand_96_out,
       nand_97_out, nand_98_out, nand_99_out, nand_100_out, nand_101_out, nand_102_out, nand_103_out,
       nand_104_out, nand_105_out, nand_106_out, nand_107_out, nand_108_out, nand_109_out, nand_110_out,
       nand_111_out, nand_112_out, nand_113_out, nand_114_out, nand_115_out, nand_116_out, nand_117_out,
       nand_118_out, nand_119_out, nand_120_out, nand_121_out, nand_122_out, nand_123_out, nand_124_out,
       nand_125_out, nand_126_out, nand_127_out, nand_128_out, nand_129_out, nand_130_out, nand_131_out,
       nand_132_out, nand_133_out, nand_134_out, nand_135_out, nand_136_out, nand_137_out, nand_138_out,
       nand_139_out, nand_140_out, nand_141_out, nand_142_out, nand_143_out, nand_144_out, nand_145_out,
       nand_146_out, nand_147_out, nand_148_out, nand_149_out, nand_150_out, nand_151_out, nand_152_out,
       nand_153_out, nor_1_out, nor_2_out, or_1_out, xor_1_out, xor_2_out, xor_3_out, xor_4_out;

  nand nand_1 (nand_1_out, S0_3, S0_3);
  nand nand_2 (nand_2_out, S1_3, S1_3);
  nand nand_3 (nand_3_out, S0_3, S1_3);
  nand nand_4 (nand_4_out, S0_2, S0_2);
  nand nand_5 (nand_5_out, S1_2, S1_2);
  nand nand_6 (nand_6_out, S0_4, S0_4);
  nand nand_7 (nand_7_out, S1_4, S1_4);
  nand nand_8 (nand_8_out, E1, E0);
  nand nand_9 (nand_9_out, S0, S0);
  nand nand_10 (nand_10_out, D_2, S0_3);
  nand nand_11 (nand_11_out, C_2, nand_1_out);
  nand nand_12 (nand_12_out, B_3, S0_3);
  nand nand_13 (nand_13_out, A_3, nand_1_out);
  nand nand_14 (nand_14_out, S1, S1);
  nand nand_15 (nand_15_out, D, S0_2);
  nand nand_16 (nand_16_out, C, nand_4_out);
  nand nand_17 (nand_17_out, B_2, S0_2);
  nand nand_18 (nand_18_out, A_2, nand_4_out);
  nand nand_19 (nand_19_out, D_3, S0_4);
  nand nand_20 (nand_20_out, C_3, nand_6_out);
  nand nand_21 (nand_21_out, B_4, S0_4);
  nand nand_22 (nand_22_out, A_4, nand_6_out);
  nand nand_23 (nand_23_out, nand_10_out, nand_11_out);
  nand nand_24 (nand_24_out, nand_12_out, nand_13_out);
  nand nand_25 (nand_25_out, D3, nand_8_out);
  nand nand_26 (nand_26_out, S1, S0);
  nand nand_27 (nand_27_out, D2, nand_8_out);
  nand nand_28 (nand_28_out, nand_9_out, S1);
  nand nand_29 (nand_29_out, D1, nand_8_out);
  nand nand_30 (nand_30_out, S0, nand_14_out);
  nand nand_31 (nand_31_out, D0, nand_8_out);
  nand nand_32 (nand_32_out, nand_9_out, nand_14_out);
  nand nand_33 (nand_33_out, nand_15_out, nand_16_out);
  nand nand_34 (nand_34_out, nand_17_out, nand_18_out);
  nand nand_35 (nand_35_out, nand_19_out, nand_20_out);
  nand nand_36 (nand_36_out, nand_21_out, nand_22_out);
  nand nand_37 (nand_37_out, S1_3, nand_23_out);
  nand nand_38 (nand_38_out, nand_24_out, nand_2_out);
  nand nand_39 (nand_39_out, nand_25_out, nand_25_out);
  nand nand_40 (nand_40_out, nand_26_out, nand_26_out);
  nand nand_41 (nand_41_out, nand_27_out, nand_27_out);
  nand nand_42 (nand_42_out, nand_28_out, nand_28_out);
  nand nand_43 (nand_43_out, nand_29_out, nand_29_out);
  nand nand_44 (nand_44_out, nand_30_out, nand_30_out);
  nand nand_45 (nand_45_out, nand_31_out, nand_31_out);
  nand nand_46 (nand_46_out, nand_32_out, nand_32_out);
  nand nand_47 (nand_47_out, S1_2, nand_33_out);
  nand nand_48 (nand_48_out, nand_34_out, nand_5_out);
  nand nand_49 (nand_49_out, S1_4, nand_35_out);
  nand nand_50 (nand_50_out, nand_36_out, nand_7_out);
  nand nand_51 (nand_51_out, nand_37_out, nand_38_out);
  nand nand_52 (nand_52_out, nand_39_out, nand_40_out);
  nand nand_53 (nand_53_out, nand_41_out, nand_42_out);
  nand nand_54 (nand_54_out, nand_43_out, nand_44_out);
  nand nand_55 (nand_55_out, nand_45_out, nand_46_out);
  nand nand_56 (nand_56_out, nand_47_out, nand_48_out);
  nand nand_57 (nand_57_out, nand_49_out, nand_50_out);
  nand nand_58 (nand_58_out, nand_51_out, Cin);
  nand nand_59 (nand_59_out, nand_56_out, EN);
  LED led_1 (.in(nand_57_out));
  nand nand_60 (nand_60_out, nand_51_out, nand_58_out);
  nand nand_61 (nand_61_out, nand_58_out, Cin);
  nand nand_62 (nand_62_out, nand_58_out, nand_3_out);
  nand nand_63 (nand_63_out, nand_52_out, nand_53_out);
  nand nand_64 (nand_64_out, nand_54_out, nand_55_out);
  nand nand_65 (nand_65_out, nand_59_out, nand_59_out);
  nand nand_66 (nand_66_out, nand_60_out, nand_61_out);
  nand nand_67 (nand_67_out, nand_62_out, SC);
  nand nand_68 (nand_68_out, nand_63_out, nand_63_out);
  nand nand_69 (nand_69_out, nand_64_out, nand_64_out);
  LED led_2 (.in(nand_65_out));
  LED Sum (.in(nand_66_out));
  nand nand_70 (nand_70_out, nand_67_out, nand_67_out);
  nand nand_71 (nand_71_out, nand_68_out, nand_69_out);
  LED Cout (.in(nand_70_out));
  LED led_3 (.in(nand_71_out));
  nand nand_72 (nand_72_out, in_46, in_47);
  nand nand_73 (nand_73_out, in_48, in_49);
  nand nand_74 (nand_74_out, in_35, in_36);
  nand nand_75 (nand_75_out, in_37, in_38);
  nand nand_76 (nand_76_out, in_21, in_22);
  nand nand_77 (nand_77_out, in_50, in_50);
  nand nand_78 (nand_78_out, in_23, in_24);
  nand nand_79 (nand_79_out, in_25, in_25);
  nand nand_80 (nand_80_out, in_26, in_26);
  nand nand_81 (nand_81_out, nand_72_out, nand_72_out);
  nand nand_82 (nand_82_out, nand_73_out, nand_73_out);
  nand nand_83 (nand_83_out, nand_74_out, nand_74_out);
  nand nand_84 (nand_84_out, nand_75_out, nand_75_out);
  nand nand_85 (nand_85_out, nand_76_out, nand_77_out);
  nand nand_86 (nand_86_out, nand_77_out, nand_78_out);
  nand nand_87 (nand_87_out, nand_79_out, nand_80_out);
  nand nand_88 (nand_88_out, nand_81_out, nand_82_out);
  nand nand_89 (nand_89_out, nand_83_out, nand_84_out);
  nand nand_90 (nand_90_out, nand_85_out, nand_86_out);
  LED led_4 (.in(nand_87_out));
  LED led_5 (.in(nand_88_out));
  LED led_6 (.in(nand_89_out));
  LED led_7 (.in(nand_90_out));
  nand nand_91 (nand_91_out, in_53, in_53);
  nand nand_92 (nand_92_out, in_54, in_54);
  nand nand_93 (nand_93_out, in_51, in_51);
  nand nand_94 (nand_94_out, in_52, in_52);
  nor nor_1 (nor_1_out, in_1, in_3, in_5, in_7);
  xor xor_1 (xor_1_out, in_1, in_2);
  xor xor_2 (xor_2_out, in_3, in_4);
  xor xor_3 (xor_3_out, in_5, in_6);
  xor xor_4 (xor_4_out, in_7, in_8);
  nand nand_95 (nand_95_out, nand_91_out, nand_92_out);
  nand nand_96 (nand_96_out, nand_93_out, nand_94_out);
  nand nand_97 (nand_97_out, nand_95_out, nand_95_out);
  nand nand_98 (nand_98_out, nand_96_out, nand_96_out);
  nor nor_2 (nor_2_out, xor_1_out, xor_2_out, xor_3_out, xor_4_out);
  nand nand_99 (nand_99_out, nand_97_out, nand_98_out);
  LED led_8 (.in(nor_1_out));
  LED led_9 (.in(nor_2_out));
  nand nand_100 (nand_100_out, nLD, nLD);
  LED led_10 (.in(nand_99_out));
  and and_1 (and_1_out, ~nG, ~nA_B);  // And
  and and_2 (and_2_out, ~nG, nA_B);  // And
  nand nand_101 (nand_101_out, nand_146_out, nLD);
  nand nand_102 (nand_102_out, nand_100_out, DATA);
  and and_3 (and_3_out, nG, and_1_out);
  and and_4 (and_4_out, and_2_out, nA_B);
  nand nand_103 (nand_103_out, nand_101_out, nand_102_out);
  nand nand_104 (nand_104_out, nA_B_2, nA_B_2);
  nand nand_105 (nand_105_out, A, B);
  or or_1 (or_1_out, and_3_out, and_4_out);
  nand nand_106 (nand_106_out, A_6, A_6);
  nand nand_107 (nand_107_out, B_6, B_6);
  nand nand_108 (nand_108_out, A_5, nand_104_out);
  nand nand_109 (nand_109_out, nA_B_2, B_5);
  nand nand_110 (nand_110_out, A, nand_105_out);
  nand nand_111 (nand_111_out, nand_105_out, B);
  nand nand_112 (nand_112_out, CK, CK);
  nand nand_113 (nand_113_out, nand_103_out, nand_103_out);
  nand nand_114 (nand_114_out, in_17, in_17);
  nand nand_115 (nand_115_out, nand_151_out, nand_151_out);
  nand nand_116 (nand_116_out, nand_106_out, nand_107_out);
  nand nand_117 (nand_117_out, nand_108_out, nand_109_out);
  nand nand_118 (nand_118_out, nand_110_out, nand_111_out);
  nand nand_119 (nand_119_out, CLK_2, CLK_2);
  nand nand_120 (nand_120_out, DAT_2, DAT_2);
  nand nand_121 (nand_121_out, nand_103_out, nand_112_out);
  nand nand_122 (nand_122_out, nand_112_out, nand_113_out);
  nand nand_123 (nand_123_out, nand_153_out, DAT, in_13);
  nand nand_124 (nand_124_out, in_13, DAT, nand_152_out);
  nand nand_125 (nand_125_out, in_13, in_13);
  nand nand_126 (nand_126_out, nand_151_out, nand_114_out);
  nand nand_127 (nand_127_out, nand_114_out, nand_115_out);
  LED led_11 (.in(nand_116_out));
  LED led_12 (.in(nand_117_out));
  LED led_13 (.in(nand_118_out));
  nand nand_128 (nand_128_out, DAT_2, nand_119_out);
  nand nand_129 (nand_129_out, nand_119_out, nand_120_out);
  nand nand_130 (nand_130_out, nand_121_out, nand_131_out);
  nand nand_131 (nand_131_out, nand_130_out, nand_122_out);
  nand nand_132 (nand_132_out, nand_123_out, nand_133_out);
  nand nand_133 (nand_133_out, nand_132_out, nand_124_out);
  nand nand_134 (nand_134_out, nand_128_out, nand_135_out);
  nand nand_135 (nand_135_out, nand_134_out, nand_129_out);
  nand nand_136 (nand_136_out, nand_126_out, nand_137_out);
  nand nand_137 (nand_137_out, nand_136_out, nand_127_out);
  nand nand_138 (nand_138_out, nand_130_out, CK);
  nand nand_139 (nand_139_out, CK, nand_131_out);
  nand nand_140 (nand_140_out, CLK_2, nand_134_out);
  nand nand_141 (nand_141_out, nand_135_out, CLK_2);
  nand nand_142 (nand_142_out, nand_132_out, nand_125_out);
  nand nand_143 (nand_143_out, nand_125_out, nand_133_out);
  nand nand_144 (nand_144_out, nand_136_out, in_17);
  nand nand_145 (nand_145_out, in_17, nand_137_out);
  nand nand_146 (nand_146_out, nand_138_out, nand_147_out);
  nand nand_147 (nand_147_out, nand_146_out, nand_139_out);
  nand nand_148 (nand_148_out, nand_140_out, nand_149_out);
  nand nand_149 (nand_149_out, nand_148_out, nand_141_out);
  nand nand_150 (nand_150_out, nand_144_out, nand_151_out);
  nand nand_151 (nand_151_out, nand_150_out, nand_145_out);
  nand nand_152 (nand_152_out, nand_142_out, nand_153_out);
  nand nand_153 (nand_153_out, nand_152_out, nand_143_out);
  LED Q (.in(nand_148_out));
  LED nQ (.in(nand_149_out));
  LED Q_2 (.in(nand_146_out));
  LED nQ_2 (.in(nand_147_out));
  LED Q_3 (.in(nand_152_out));
  LED nQ_3 (.in(nand_153_out));
  LED Q_4 (.in(nand_150_out));
  LED nQ_4 (.in(nand_151_out));

  // Notes on the sheet:
  //   19 gate ALU with carry suppress
  //   4:1 Multiplexer (no enable)
  //   4:1 Multiplexer (MK 2)
  //   4:1 Multiplexer
  //   4 Input AND-OR
  //   2-Input OR
  //   4-Input Nand
  //   4-bit Comparator A=B and Zero Detect A=0
  //   4 Input OR
  //   4002
  //   A=0
  //   A=B
  //   2 Input MUX
  //   2 Input XOR
  //   1-bit register
  //   Master-Slave JK Flipflop
  //   D-Type Flipflop
  //   Toggle -Type Flipflop
endmodule
