// Digital circuit clock_gate.dig as structural Verilog
module clock_gate (
  input  C,
  input  A,
  input  B,
  output G,
  output nRST
);

  wire and_1_out, not_1_out, or_1_out;

  not not_1 (not_1_out, C);
  or or_1 (or_1_out, A, B);
  and and_1 (and_1_out, A, B);
  not not_2 (nRST, and_1_out);
  and and_2 (G, not_1_out, or_1_out);
endmodule
