// Digital circuit hex_keypad_serial_out.dig as structural Verilog
module hex_keypad_serial_out (
  input  in_1,
  input  clk
);

  wire _0_out, _1_out, _2_out, _3_out, _4_out, _5_out, _6_out, _7_out, _8_out, _9_out, _74173_4_pin11,
       _74173_4_pin12, _74173_4_pin13, _74173_4_pin14, _74540_1_pin11, _74540_1_pin12, _74540_1_pin13,
       _74540_1_pin14, _74540_1_pin15, _74540_1_pin16, _74540_1_pin17, A_out, Address_out, ALU,
       ALU_to_RAM_out, B_out, C_out, Clear_out, D_out, Dec_out, Deposit_nWR_out, diodebackward_1_out,
       diodebackward_3_out, diodebackward_8_out, diodebackward_12_out, diodebackward_14_out,
       diodebackward_22_out, diodebackward_39_out, DN, E_out, Examine_nRD_out, F_out, Inc_out, nALB, nDE,
       nLATCH, nLD, nOE, not_4_out, not_9_out, nWE, pullup_1_out, pullup_4_out, pullup_5_out, pullup_8_out,
       pullup_11_out, pullup_12_out, RES, S0, S1, S2, S3, S4, S5, S6, S7, S8, S9, S10, S11, S12, S13, S14,
       S15, UP;

  PullUp pullup_1 (.out(pullup_1_out));
  DiodeBackward diodebackward_1 (.in(Dec_out), .out(diodebackward_1_out));
  DiodeBackward diodebackward_2 (.in(Address_out), .out(pullup_1_out));
  PullUp pullup_2 (.out(diodebackward_1_out));
  DiodeBackward diodebackward_3 (.in(Inc_out), .out(diodebackward_3_out));
  not not_1 (nLD, _74540_1_pin11);
  _74139 _74139_1 (
    .pin1(1'b1), .pin2(1'b1), .pin3(1'b1), .pin8(1'b0), .pin11(nALB), .pin12(nDE), .pin13(1'b0), .pin14(ALU),
    .pin15(nWE), .pin16(1'b1));  // open: pin4, pin5, pin6, pin7, pin9, pin10
  PullUp pullup_3 (.out(diodebackward_3_out));
  PullUp pullup_4 (.out(pullup_4_out));
  DiodeBackward diodebackward_4 (.in(ALU_to_RAM_out), .out(pullup_4_out));
  DiodeBackward diodebackward_5 (.in(Examine_nRD_out), .out(pullup_4_out));
  DiodeBackward diodebackward_6 (.in(Dec_out), .out(pullup_4_out));
  DiodeBackward diodebackward_7 (.in(Inc_out), .out(pullup_4_out));
  PullUp pullup_5 (.out(pullup_5_out));
  DiodeBackward diodebackward_8 (.in(ALU_to_RAM_out), .out(diodebackward_8_out));
  DiodeBackward diodebackward_9 (.in(Examine_nRD_out), .out(pullup_5_out));
  DiodeBackward diodebackward_10 (.in(Deposit_nWR_out), .out(diodebackward_8_out));
  DiodeBackward diodebackward_11 (.in(Deposit_nWR_out), .out(pullup_5_out));
  not not_2 (ALU, _74540_1_pin15);
  not not_3 (nWE, _74540_1_pin16);
  nand nand_1 (UP, _74540_1_pin13, _74540_1_pin14);
  nand nand_2 (DN, _74540_1_pin12, _74540_1_pin14);
  PullUp pullup_6 (.out(diodebackward_8_out));
  DiodeBackward diodebackward_12 (.in(Examine_nRD_out), .out(diodebackward_12_out));
  not not_4 (not_4_out, _74540_1_pin17);
  PullUp pullup_7 (.out(diodebackward_12_out));
  PullUp pullup_8 (.out(pullup_8_out));
  DiodeBackward diodebackward_13 (.in(Clear_out), .out(pullup_8_out));
  _74540 _74540_1 (
    .pin1(1'b0), .pin2(pullup_8_out), .pin3(diodebackward_12_out), .pin4(diodebackward_8_out),
    .pin5(pullup_5_out), .pin6(pullup_4_out), .pin7(diodebackward_3_out), .pin8(diodebackward_1_out),
    .pin9(pullup_1_out), .pin10(1'b0), .pin11(_74540_1_pin11), .pin12(_74540_1_pin12),
    .pin13(_74540_1_pin13), .pin14(_74540_1_pin14), .pin15(_74540_1_pin15), .pin16(_74540_1_pin16),
    .pin17(_74540_1_pin17), .pin18(RES), .pin19(1'b0), .pin20(1'b1));
  nand nand_3 (nOE, not_4_out, in_1);
  _74173 _74173_1 (
    .pin1(1'b0), .pin2(1'b0), .pin3(S12), .pin4(S13), .pin5(S14), .pin6(S15), .pin7(nLATCH), .pin8(1'b0),
    .pin9(1'b0), .pin10(1'b0), .pin11(S11), .pin12(S10), .pin13(S9), .pin14(S8), .pin15(RES), .pin16(1'b1));
  Button #(.activeLow("true")) ALU_to_RAM (.out(ALU_to_RAM_out));
  Button #(.activeLow("true")) Clear (.out(Clear_out));
  Button #(.activeLow("true")) Examine_nRD (.out(Examine_nRD_out));
  Button #(.activeLow("true")) Deposit_nWR (.out(Deposit_nWR_out));
  Button #(.activeLow("true")) Dec (.out(Dec_out));
  Button #(.activeLow("true")) Inc (.out(Inc_out));
  Button #(.activeLow("true")) Address (.out(Address_out));
  Seven_Seg_Hex seven_seg_hex_1 (.d({S15, S14, S13, S12}), .dp(1'b0));
  Seven_Seg_Hex seven_seg_hex_2 (.d({S11, S10, S9, S8}), .dp(1'b0));
  Seven_Seg_Hex seven_seg_hex_3 (.d({S7, S6, S5, S4}), .dp(1'b0));
  _74173 _74173_2 (
    .pin1(1'b0), .pin2(1'b0), .pin3(S8), .pin4(S9), .pin5(S10), .pin6(S11), .pin7(nLATCH), .pin8(1'b0),
    .pin9(1'b0), .pin10(1'b0), .pin11(S7), .pin12(S6), .pin13(S5), .pin14(S4), .pin15(RES), .pin16(1'b1));
  Seven_Seg_Hex seven_seg_hex_4 (.d({S3, S2, S1, S0}), .dp(1'b0));
  Button #(.activeLow("true")) C (.out(C_out));
  Button #(.activeLow("true")) _8 (.out(_8_out));
  Button #(.activeLow("true")) _4 (.out(_4_out));
  Button #(.activeLow("true")) _0 (.out(_0_out));
  Button #(.activeLow("true")) D (.out(D_out));
  Button #(.activeLow("true")) _9 (.out(_9_out));
  Button #(.activeLow("true")) _5 (.out(_5_out));
  Button #(.activeLow("true")) _1 (.out(_1_out));
  Button #(.activeLow("true")) E (.out(E_out));
  Button #(.activeLow("true")) A (.out(A_out));
  Button #(.activeLow("true")) _6 (.out(_6_out));
  Button #(.activeLow("true")) _2 (.out(_2_out));
  _74173 _74173_3 (
    .pin1(1'b0), .pin2(1'b0), .pin3(S4), .pin4(S5), .pin5(S6), .pin6(S7), .pin7(nLATCH), .pin8(1'b0),
    .pin9(1'b0), .pin10(1'b0), .pin11(S3), .pin12(S2), .pin13(S1), .pin14(S0), .pin15(RES), .pin16(1'b1));
  Button #(.activeLow("true")) F (.out(F_out));
  Button #(.activeLow("true")) B (.out(B_out));
  Button #(.activeLow("true")) _7 (.out(_7_out));
  Button #(.activeLow("true")) _3 (.out(_3_out));
  _74173 _74173_4 (
    .pin1(1'b0), .pin2(1'b0), .pin3(S0), .pin4(S1), .pin5(S2), .pin6(S3), .pin7(nLATCH), .pin8(1'b0),
    .pin9(1'b0), .pin10(1'b0), .pin11(_74173_4_pin11), .pin12(_74173_4_pin12), .pin13(_74173_4_pin13),
    .pin14(_74173_4_pin14), .pin15(RES), .pin16(1'b1));
  DiodeBackward diodebackward_14 (.in(F_out), .out(diodebackward_14_out));
  DiodeBackward diodebackward_15 (.in(E_out), .out(diodebackward_14_out));
  DiodeBackward diodebackward_16 (.in(D_out), .out(diodebackward_14_out));
  DiodeBackward diodebackward_17 (.in(C_out), .out(diodebackward_14_out));
  DiodeBackward diodebackward_18 (.in(B_out), .out(diodebackward_14_out));
  DiodeBackward diodebackward_19 (.in(A_out), .out(diodebackward_14_out));
  DiodeBackward diodebackward_20 (.in(_9_out), .out(diodebackward_14_out));
  DiodeBackward diodebackward_21 (.in(_8_out), .out(diodebackward_14_out));
  PullUp pullup_9 (.out(diodebackward_14_out));
  DiodeBackward diodebackward_22 (.in(F_out), .out(diodebackward_22_out));
  DiodeBackward diodebackward_23 (.in(E_out), .out(diodebackward_22_out));
  DiodeBackward diodebackward_24 (.in(D_out), .out(diodebackward_22_out));
  DiodeBackward diodebackward_25 (.in(C_out), .out(diodebackward_22_out));
  DiodeBackward diodebackward_26 (.in(_7_out), .out(diodebackward_22_out));
  DiodeBackward diodebackward_27 (.in(_6_out), .out(diodebackward_22_out));
  DiodeBackward diodebackward_28 (.in(_5_out), .out(diodebackward_22_out));
  DiodeBackward diodebackward_29 (.in(_4_out), .out(diodebackward_22_out));
  not not_5 (_74173_4_pin11, diodebackward_14_out);
  PullUp pullup_10 (.out(diodebackward_22_out));
  PullUp pullup_11 (.out(pullup_11_out));
  DiodeBackward diodebackward_30 (.in(F_out), .out(pullup_11_out));
  DiodeBackward diodebackward_31 (.in(E_out), .out(pullup_11_out));
  DiodeBackward diodebackward_32 (.in(B_out), .out(pullup_11_out));
  DiodeBackward diodebackward_33 (.in(A_out), .out(pullup_11_out));
  DiodeBackward diodebackward_34 (.in(_7_out), .out(pullup_11_out));
  DiodeBackward diodebackward_35 (.in(_6_out), .out(pullup_11_out));
  DiodeBackward diodebackward_36 (.in(_3_out), .out(pullup_11_out));
  DiodeBackward diodebackward_37 (.in(_2_out), .out(pullup_11_out));
  not not_6 (_74173_4_pin13, pullup_11_out);
  not not_7 (_74173_4_pin12, diodebackward_22_out);
  PullUp pullup_12 (.out(pullup_12_out));
  DiodeBackward diodebackward_38 (.in(F_out), .out(pullup_12_out));
  DiodeBackward diodebackward_39 (.in(F_out), .out(diodebackward_39_out));
  DiodeBackward diodebackward_40 (.in(E_out), .out(diodebackward_39_out));
  DiodeBackward diodebackward_41 (.in(D_out), .out(pullup_12_out));
  DiodeBackward diodebackward_42 (.in(D_out), .out(diodebackward_39_out));
  DiodeBackward diodebackward_43 (.in(C_out), .out(diodebackward_39_out));
  DiodeBackward diodebackward_44 (.in(B_out), .out(pullup_12_out));
  DiodeBackward diodebackward_45 (.in(B_out), .out(diodebackward_39_out));
  DiodeBackward diodebackward_46 (.in(A_out), .out(diodebackward_39_out));
  DiodeBackward diodebackward_47 (.in(_9_out), .out(pullup_12_out));
  DiodeBackward diodebackward_48 (.in(_9_out), .out(diodebackward_39_out));
  DiodeBackward diodebackward_49 (.in(_8_out), .out(diodebackward_39_out));
  DiodeBackward diodebackward_50 (.in(_7_out), .out(pullup_12_out));
  DiodeBackward diodebackward_51 (.in(_7_out), .out(diodebackward_39_out));
  DiodeBackward diodebackward_52 (.in(_6_out), .out(diodebackward_39_out));
  DiodeBackward diodebackward_53 (.in(_5_out), .out(pullup_12_out));
  DiodeBackward diodebackward_54 (.in(_5_out), .out(diodebackward_39_out));
  DiodeBackward diodebackward_55 (.in(_4_out), .out(diodebackward_39_out));
  DiodeBackward diodebackward_56 (.in(_3_out), .out(pullup_12_out));
  DiodeBackward diodebackward_57 (.in(_3_out), .out(diodebackward_39_out));
  DiodeBackward diodebackward_58 (.in(_2_out), .out(diodebackward_39_out));
  DiodeBackward diodebackward_59 (.in(_1_out), .out(pullup_12_out));
  DiodeBackward diodebackward_60 (.in(_1_out), .out(diodebackward_39_out));
  DiodeBackward diodebackward_61 (.in(_0_out), .out(diodebackward_39_out));
  not not_8 (_74173_4_pin14, pullup_12_out);
  PullUp pullup_13 (.out(diodebackward_39_out));
  not not_9 (not_9_out, diodebackward_39_out);
  Monoflop monoflop_1 (.C(not_9_out), .R(1'b0), .nQ(nLATCH));  // open: Q
  LED led_1 (.in(nLATCH));

  // Notes on the sheet:
  //   in_1: default 1
  //   clk: Hz: 2147483647
  //   Front Panel
  //   LOAD
  //   UP
  //   DOWN
  //   COUNT
  //   ~DE
  //   READ
  //   WRITE
  //   RESET
  //   KEY DATA
  //   Hex Keypad
  //   KEYSWITCH REGISTER
endmodule
