// Digital circuit index_register_1.dig as structural Verilog
module index_register_1 (
  input  D0,
  input  CLK,
  input  I1,
  input  I0,
  input  Cin,
  input  SC,
  input  D1,
  input  D2,
  input  D3,
  input  D4,
  input  D5,
  input  D6,
  input  D7,
  input  INV
);

  wire AC0, AC1, AC2, AC3, AC4, AC5, AC6, AC7, F0, F1, F2, F3, F4, F5, F6, F7;

  Seven_Seg_Hex seven_seg_hex_1 (.d({F7, F6, F5, F4}), .dp(1'b0));
  Seven_Seg_Hex seven_seg_hex_2 (.d({F3, F2, F1, F0}), .dp(1'b0));
  Seven_Seg_Hex seven_seg_hex_3 (.d({AC7, AC6, AC5, AC4}), .dp(1'b0));
  Seven_Seg_Hex seven_seg_hex_4 (.d({AC3, AC2, AC1, AC0}), .dp(1'b0));
  Seven_Seg_Hex seven_seg_hex_5 (.d({D7, D6, D5, D4}), .dp(1'b0));
  Seven_Seg_Hex seven_seg_hex_6 (.d({D3, D2, D1, D0}), .dp(1'b0));

  // Other names for the same wires on the sheet: AL = SC

  // Notes on the sheet:
  //   CLK: Hz: 2147483647
  //   ALU
  //   ACC
  //   BUS
endmodule
