// Digital circuit memory_access.dig as structural Verilog
module memory_access (
  input  T8,
  input  IR6,
  input  IR5,
  input  IR4,
  output nWR,
  output nRD,
  output INC_LD
);

  wire nJMP, PC_INC, ST;

  not not_1 (PC_INC, T8);
  nand nand_1 (nJMP, IR4, IR5, IR6);
  nand nand_2 (ST, ~IR4, IR5, IR6);  // NAnd
  or or_1 (INC_LD, PC_INC, nJMP);
  or or_2 (nWR, PC_INC, ST);
  or or_3 (nRD, IR4, IR5, IR6);

  // Other names for the same wires on the sheet: nCTRLD = INC_LD; RDRAM = nRD; WRRAM = nWR

  // Notes on the sheet:
  //   Memory Access
endmodule
