// Digital circuit mite000.dig as structural Verilog
module mite000 (
  input  clk,
  input  in_2,
  input  in_3,
  input  in_4,
  input  in_5,
  input  in_6,
  input  in_7,
  input  in_8,
  input  in_9,
  input  in_10,
  input  in_11
);

  wire A, AC1, AC2, AC3, AC4, AC5, AC6, AC7, ADD, AND, Aout, Bout, BUS0, BUS1, BUS2, BUS3, BUS4, BUS5, BUS6,
       BUS7, BUS8, BUS9, BUS10, BUS11, BUS12, BUS13, BUS14, BUS15, button_1_out, C, Cin, CLA, CLR, Cout,
       diodebackward_1_out, diodebackward_2_out, diodebackward_6_out, diodeforward_1_out, F, Fout, GCLK, I0,
       I1, I2, I3, I4, I5, I6, I7, INCPC, LDA, MAR0, MAR1, MAR2, MAR3, MAR4, MAR5, MAR6, MAR7, MAR8, MAR9,
       MAR10, MAR11, MAR12, MAR13, MAR14, MAR15, monoflop_1_nq, nA, nand_1_out, nand_4_out, nand_5_out,
       nand_7_out, nand_8_out, nand_9_out, nand_10_out, nand_11_out, nand_12_out, nand_14_out, nand_15_out,
       nand_16_out, nand_17_out, nand_18_out, nB, nCLRPC, nJMP, nLD, nLDB, nOE, nRST, nSEL0, nSEL1, nSEL2,
       nSEL3, nSEL4, nSEL5, nSEL6, nSEL7, nST, nSTEP, nTP0, nTP1, nTP3, nTP5, nTP6, nTP7, OR, PC0, PC1, PC2,
       PC3, PC4, PC5, PC6, PC7, PC8, PC9, PC10, PC11, PC12, PC13, PC14, PC15, pullup_1_out, pullup_3_out,
       pullup_5_out, pullup_7_out, pullup_8_out, pullup_9_out, Q3, RAM0, RAM1, RAM2, RAM3, RAM4, RAM5, RAM6,
       RAM7, RCO, RD, SETC, SUB, T0, U3_pin15, U4_pin15, U5_pin15, U12_pin15, U16_pin9, WR, X0, X1, XOR,
       xor_1_out, xor_2_out, xor_3_out, xor_4_out, ZERO;
  wire [2:0] U19_pin14;

  _74161 U3 (
    .pin1(nCLRPC), .pin2(INCPC), .pin3(BUS0), .pin4(BUS1), .pin5(BUS2), .pin6(BUS3), .pin7(1'b1),
    .pin8(1'b0), .pin9(nJMP), .pin10(1'b1), .pin11(PC3), .pin12(PC2), .pin13(PC1), .pin14(PC0),
    .pin15(U3_pin15), .pin16(1'b1));
  _74161 U4 (
    .pin1(nCLRPC), .pin2(INCPC), .pin3(BUS4), .pin4(BUS5), .pin5(BUS6), .pin6(BUS7), .pin7(1'b1),
    .pin8(1'b0), .pin9(nJMP), .pin10(U3_pin15), .pin11(PC7), .pin12(PC6), .pin13(PC5), .pin14(PC4),
    .pin15(U4_pin15), .pin16(1'b1));
  _74161 U5 (
    .pin1(nCLRPC), .pin2(INCPC), .pin3(BUS8), .pin4(BUS9), .pin5(BUS10), .pin6(BUS11), .pin7(1'b1),
    .pin8(1'b0), .pin9(in_2), .pin10(U4_pin15), .pin11(PC11), .pin12(PC10), .pin13(PC9), .pin14(PC8),
    .pin15(U5_pin15), .pin16(1'b1));
  _74161 U6 (
    .pin1(nCLRPC), .pin2(INCPC), .pin3(in_3), .pin4(in_4), .pin5(in_5), .pin6(in_6), .pin7(1'b1),
    .pin8(1'b0), .pin9(in_2), .pin10(U5_pin15), .pin11(PC15), .pin12(PC14), .pin13(PC13), .pin14(PC12),
    .pin16(1'b1));  // open: pin15
  // _62256 U10: pin names not known; wires that end beside it: in_9, in_11, MAR7, MAR6, MAR5, MAR4, MAR3, MAR2, MAR1, MAR0, RAM0, RAM1, RAM2, 1'b0
  // _27C1024 U1: pin names not known; wires that end beside it: PC9, PC10, PC11, PC12, PC13, PC14, PC15, 1'b1, BUS3, BUS4, BUS5, BUS6, BUS7, 1'b0, BUS8, BUS9, BUS10, BUS11, BUS12, BUS13, BUS14, BUS15, 1'b0, 1'b1, 1'b1, 1'b1, in_10, MAR8, MAR9, MAR11, 1'b1, MAR10, 1'b0, RAM7, RAM6, RAM5, RAM4
  _74138 U12 (
    .pin1(I4), .pin2(I5), .pin3(I6), .pin4(1'b0), .pin5(1'b0), .pin6(I7), .pin7(nJMP), .pin8(1'b0),
    .pin9(nST), .pin10(SUB), .pin11(ADD), .pin12(XOR), .pin13(OR), .pin14(AND), .pin15(U12_pin15),
    .pin16(1'b1));
  _74138 U7 (
    .pin1(I0), .pin2(I1), .pin3(I2), .pin4(1'b0), .pin5(1'b0), .pin6(1'b1), .pin7(nSEL7), .pin8(1'b0),
    .pin9(nSEL6), .pin10(nSEL5), .pin11(nSEL4), .pin12(nSEL3), .pin13(nSEL2), .pin14(nSEL1), .pin15(nSEL0),
    .pin16(1'b1));
  and and_1 (nLD, I7, U12_pin15);
  Seven_Seg_Hex seven_seg_hex_1 (.d({AC7, AC6, AC5, AC4}), .dp(1'b0));
  PullUp pullup_1 (.out(pullup_1_out));
  DiodeBackward diodebackward_1 (.in(nLD), .out(diodebackward_1_out));
  Seven_Seg_Hex seven_seg_hex_2 (.d({AC3, AC2, AC1, A}), .dp(1'b0));
  _74164 U14 (
    .pin1(1'b1), .pin2(Fout), .pin3(AC7), .pin4(AC6), .pin5(AC5), .pin6(AC4), .pin7(1'b0), .pin8(GCLK),
    .pin9(nCLRPC), .pin10(AC3), .pin11(AC2), .pin12(AC1), .pin13(A), .pin14(1'b1));
  PullUp pullup_2 (.out(diodebackward_1_out));
  DiodeBackward diodebackward_2 (.in(nLD), .out(diodebackward_2_out));
  _74165 U16 (
    .pin1(nLDB), .pin2(GCLK), .pin3(BUS3), .pin4(BUS2), .pin5(BUS1), .pin6(BUS0), .pin8(1'b0),
    .pin9(U16_pin9), .pin10(1'b0), .pin11(BUS7), .pin12(BUS6), .pin13(BUS5), .pin14(BUS4), .pin15(1'b0),
    .pin16(1'b1));  // open: pin7
  PullUp pullup_3 (.out(pullup_3_out));
  PullUp pullup_4 (.out(diodebackward_2_out));
  DiodeBackward diodebackward_3 (.in(nLD), .out(pullup_3_out));
  DiodeBackward diodebackward_4 (.in(ADD), .out(pullup_3_out));
  DiodeBackward diodebackward_5 (.in(SUB), .out(pullup_3_out));
  PullUp pullup_5 (.out(pullup_5_out));
  DiodeBackward diodebackward_6 (.in(SUB), .out(diodebackward_6_out));
  DiodeBackward diodebackward_7 (.in(SUB), .out(pullup_5_out));
  and and_2 (Aout, nLD, A);
  PullUp pullup_6 (.out(diodebackward_6_out));
  PullUp pullup_7 (.out(pullup_7_out));
  PullUp pullup_8 (.out(pullup_8_out));
  DiodeBackward diodebackward_8 (.in(AND), .out(pullup_8_out));
  DiodeBackward diodebackward_9 (.in(OR), .out(pullup_8_out));
  DiodeBackward diodebackward_10 (.in(nJMP), .out(pullup_8_out));
  DiodeForward diodeforward_1 (.in(AC7), .out(diodeforward_1_out));
  DiodeForward diodeforward_2 (.in(AC6), .out(diodeforward_1_out));
  DiodeForward diodeforward_3 (.in(AC5), .out(diodeforward_1_out));
  DiodeForward diodeforward_4 (.in(AC4), .out(diodeforward_1_out));
  DiodeForward diodeforward_5 (.in(AC3), .out(diodeforward_1_out));
  DiodeForward diodeforward_6 (.in(AC2), .out(diodeforward_1_out));
  DiodeForward diodeforward_7 (.in(AC1), .out(diodeforward_1_out));
  DiodeForward diodeforward_8 (.in(A), .out(diodeforward_1_out));
  and and_3 (Bout, nJMP, U16_pin9);
  PullUp pullup_9 (.out(pullup_9_out));
  DiodeBackward diodebackward_11 (.in(nLD), .out(pullup_9_out));
  DiodeBackward diodebackward_12 (.in(OR), .out(pullup_9_out));
  DiodeBackward diodebackward_13 (.in(XOR), .out(pullup_9_out));
  DiodeBackward diodebackward_14 (.in(ADD), .out(pullup_9_out));
  DiodeBackward diodebackward_15 (.in(SUB), .out(pullup_9_out));
  DiodeBackward diodebackward_16 (.in(nST), .out(pullup_9_out));
  DiodeBackward diodebackward_17 (.in(nJMP), .out(pullup_9_out));
  PullDown pulldown_1 (.out(diodeforward_1_out));
  not not_1 (WR, pullup_1_out);
  _74540 U18 (
    .pin1(1'b0), .pin2(pullup_9_out), .pin3(pullup_8_out), .pin4(pullup_7_out), .pin5(diodebackward_6_out),
    .pin6(pullup_5_out), .pin7(pullup_3_out), .pin8(diodebackward_2_out), .pin9(diodebackward_1_out),
    .pin10(1'b0), .pin11(RD), .pin12(CLA), .pin13(F), .pin14(C), .pin15(nB), .pin16(nA), .pin17(X1),
    .pin18(X0), .pin19(1'b0), .pin20(1'b1));
  LED led_1 (.in(ZERO));
  not not_2 (ZERO, diodeforward_1_out);
  _74574 U2 (
    .pin1(1'b0), .pin2(BUS8), .pin3(BUS9), .pin4(BUS10), .pin5(BUS11), .pin6(BUS12), .pin7(BUS13),
    .pin8(BUS14), .pin9(BUS15), .pin10(1'b0), .pin11(nLDB), .pin12(I7), .pin13(I6), .pin14(I5), .pin15(I4),
    .pin16(I3), .pin17(I2), .pin18(I1), .pin19(I0), .pin20(1'b1));
  _74574 U8 (
    .pin1(1'b0), .pin2(BUS7), .pin3(BUS6), .pin4(BUS5), .pin5(BUS4), .pin6(BUS3), .pin7(BUS2), .pin8(BUS1),
    .pin9(BUS0), .pin10(1'b0), .pin11(nLDB), .pin12(MAR0), .pin13(MAR1), .pin14(MAR2), .pin15(MAR3),
    .pin16(MAR4), .pin17(MAR5), .pin18(MAR6), .pin19(MAR7), .pin20(1'b1));
  _74574 U9 (
    .pin1(1'b0), .pin2(BUS7), .pin3(BUS6), .pin4(BUS5), .pin5(BUS4), .pin6(BUS3), .pin7(BUS2), .pin8(BUS1),
    .pin9(BUS0), .pin10(1'b0), .pin11(nLDB), .pin12(MAR8), .pin13(MAR9), .pin14(MAR10), .pin15(MAR11),
    .pin16(MAR12), .pin17(MAR13), .pin18(MAR14), .pin19(MAR15), .pin20(1'b1));
  _74541 _74541_1 (
    .pin1(1'b1), .pin2(RAM7), .pin3(RAM6), .pin4(RAM5), .pin5(RAM4), .pin6(RAM3), .pin7(RAM2), .pin8(RAM1),
    .pin9(RAM0), .pin10(1'b0), .pin11(BUS0), .pin12(BUS1), .pin13(BUS2), .pin14(BUS3), .pin15(BUS4),
    .pin16(BUS5), .pin17(BUS6), .pin18(BUS7), .pin19(1'b0), .pin20(1'b1));
  _74161 U19 (
    .pin1(nRST), .pin2(clk), .pin3(1'b0), .pin4(1'b0), .pin5(1'b0), .pin6(1'b0), .pin7(1'b1), .pin8(1'b0),
    .pin9(1'b1), .pin10(1'b1), .pin11(Q3), .pin12(U19_pin14[2]), .pin13(U19_pin14[1]), .pin14(U19_pin14[0]),
    .pin15(RCO), .pin16(1'b1));
  not not_3 (LDA, nLDB);
  not not_4 (SETC, nTP7);
  not not_5 (T0, nRST);
  Seven_Seg_Hex seven_seg_hex_3 (.d({RAM7, RAM6, RAM4, RAM5}), .dp(1'b0));
  Reset reset_1 (.out(nCLRPC));
  Seven_Seg_Hex seven_seg_hex_4 (.d({RAM3, RAM2, RAM1, RAM0}), .dp(1'b0));
  Seven_Seg_Hex seven_seg_hex_5 (.d({MAR15, MAR14, MAR13, MAR12}), .dp(1'b0));
  Seven_Seg_Hex seven_seg_hex_6 (.d({Q3, U19_pin14}), .dp(1'b0));
  _74138 U21 (
    .pin1(U19_pin14[0]), .pin2(U19_pin14[1]), .pin3(U19_pin14[2]), .pin4(Q3), .pin5(Q3), .pin6(1'b1),
    .pin7(nTP7), .pin8(1'b0), .pin9(nTP6), .pin10(nTP5), .pin11(nLDB), .pin12(nTP3), .pin13(INCPC),
    .pin14(nTP1), .pin15(nTP0), .pin16(1'b1));
  Seven_Seg_Hex seven_seg_hex_7 (.d({MAR11, MAR10, MAR9, MAR8}), .dp(1'b0));
  Seven_Seg_Hex seven_seg_hex_8 (.d({MAR7, MAR6, MAR5, MAR4}), .dp(1'b0));
  Seven_Seg_Hex seven_seg_hex_9 (.d({MAR3, MAR2, MAR1, MAR0}), .dp(1'b0));
  nand nand_1 (nand_1_out, clk, clk);
  // NAnd nand_2 has open pins: In_1=1'b0, In_2=1'b0, out=open
  xor xor_1 (xor_1_out, Aout, nA);
  xor xor_2 (xor_2_out, nB, Bout);
  nand nand_3 (CLR, CLA, LDA);
  nand nand_4 (nand_4_out, C, C);
  nand nand_5 (nand_5_out, C, SETC);
  nand nand_6 (GCLK, nand_1_out, Q3);
  xor xor_3 (xor_3_out, xor_1_out, xor_2_out);
  nand nand_7 (nand_7_out, LDA, nand_4_out);
  Seven_Seg_Hex seven_seg_hex_10 (.d({PC15, PC14, PC13, PC12}), .dp(1'b0));
  LED TP0 (.in(nTP0));
  LED TP1 (.in(nTP1));
  LED TP2 (.in(INCPC));
  LED TP3 (.in(nTP3));
  LED TP4 (.in(nLDB));
  LED TP5 (.in(nTP5));
  LED TP6 (.in(nTP6));
  LED TP7 (.in(nTP7));
  Seven_Seg_Hex seven_seg_hex_11 (.d({PC11, PC10, PC9, PC8}), .dp(1'b0));
  xor xor_4 (xor_4_out, xor_3_out, Cin);
  nand nand_8 (nand_8_out, xor_3_out, Cin);
  nand nand_9 (nand_9_out, xor_1_out, xor_2_out);
  Seven_Seg_Hex seven_seg_hex_12 (.d({PC7, PC6, PC5, PC4}), .dp(1'b0));
  Seven_Seg_Hex seven_seg_hex_13 (.d({PC3, PC2, PC1, PC0}), .dp(1'b0));
  nand nand_10 (nand_10_out, nTP0, nand_11_out);
  nand nand_11 (nand_11_out, nand_10_out, INCPC);
  nand nand_12 (nand_12_out, nTP3, nOE);
  nand nand_13 (nOE, nand_12_out, nTP5);
  nand nand_14 (nand_14_out, nand_8_out, nand_9_out);
  Button button_1 (.out(button_1_out));
  Monoflop monoflop_1 (.C(button_1_out), .R(1'b0), .nQ(monoflop_1_nq));  // open: Q
  nand nand_15 (nand_15_out, xor_4_out, X0);
  nand nand_16 (nand_16_out, X1, nand_14_out);
  nand nand_17 (nand_17_out, nand_14_out, F);
  Seven_Seg_Hex seven_seg_hex_14 (.d({BUS15, BUS14, BUS13, BUS12}), .dp(1'b0));
  Seven_Seg_Hex seven_seg_hex_15 (.d({BUS11, BUS10, BUS9, BUS8}), .dp(1'b0));
  // Or or_1 has open pins: In_1=nST, In_2=nTP7, out=open
  // Or or_2 has open pins: In_1=nLD, In_2=nTP6, out=open
  nand nand_18 (nand_18_out, nRST, nSTEP);
  nand nand_19 (nSTEP, nand_18_out, monoflop_1_nq);
  nand nand_20 (Fout, nand_15_out, nand_16_out);
  nand nand_21 (Cout, nand_17_out, nand_17_out);
  Seven_Seg_Hex seven_seg_hex_16 (.d({BUS7, BUS6, BUS5, BUS4}), .dp(1'b0));
  Seven_Seg_Hex seven_seg_hex_17 (.d({BUS3, BUS2, BUS1, BUS0}), .dp(1'b0));
  _7474 U23 (
    .pin1(nand_7_out), .pin2(Cout), .pin3(GCLK), .pin4(nand_5_out), .pin5(Cin), .pin7(1'b0), .pin8(nRST),
    .pin10(1'b1), .pin11(clk), .pin12(RCO), .pin13(1'b1), .pin14(1'b1));  // open: pin6, pin9

  // Other names for the same wires on the sheet: AC0 = A; nPCEN = in_7; nPH = in_2; nPL = nJMP; nTP2 = INCPC;
  //   nTP4 = nLDB; RES = nTP7; P0 = in_11; P1 = in_10; P2 = in_9; P3 = in_8

  // Notes on the sheet:
  //   clk: Hz: 24
  //   in_2: default 1
  //   Spider 011 16-bit serial CPU Testbed
  //   RAM LO
  //   Instruction Decoder
  //   ACCUMULATOR
  //   B Shift Register
  //   U31A
  //   WR
  //   CLA
  //   RD
  //   F
  //   C
  //   Zero A for
  //   Load instructions
  //   ~B
  //   I1
  //   ~A
  //   U31C
  //   I0
  //   U30F
  //   LOAD
  //   AND
  //   OR
  //   XOR
  //   ADD
  //   SUB
  //   STORE
  //   JMP
  //   Zero B for
  //   Jump instructions
  //   Instruction Latch
  //   Data Latch
  //   Clock Sequencer
  //   U30
  //   RAM DATA
  //   74HC04
  //   Note Clock Inverted
  //   # Clock
  //   RAM ADDRESS
  //   U24, U25, U26
  //   U27
  //   U28
  //   U24A
  //   U24B
  //   U27D
  //   U27A
  //   U27B
  //   ROM ADDRESS (PC)
  //   U24C
  //   U27C
  //   CLR ACC
  //   Carry is only set before Bit 0 of an operation
  //   Any residual carry is cleared before an operation
  //   Bit Serial ALU
  //   U24D
  //   U25D
  //   U25C
  //   Latch Result
  //   Write Result to RAM
  //   Increment PC
  //   Read Instruction from ROM
  //   Latch Instruction and MAR Address/Data
  //   Load B Register from Bus
  //   Set Carry
  //   U22
  //   U25B
  //   U26B
  //   U26C
  //   U26A
  //   Suppress Carry
  //   BUS DATA
  //   U29
  //   U26D
  //   U25A
  //   Carry FF
endmodule
