// Digital circuit multifunction_network.dig as structural Verilog
module multifunction_network (
  input  A0,
  input  B0,
  input  I0,
  input  I1,
  input  in_6,
  output Fout
);

  wire nand_1_out, nand_2_out, nand_3_out, nand_4_out, nand_5_out, nand_6_out, nand_7_out;

  nand nand_1 (nand_1_out, A0, B0);
  nand nand_2 (nand_2_out, A0, nand_1_out);
  nand nand_3 (nand_3_out, nand_1_out, B0);
  nand nand_4 (nand_4_out, nand_2_out, nand_3_out);
  nand nand_5 (nand_5_out, nand_1_out, in_6);
  nand nand_6 (nand_6_out, nand_4_out, I0);
  nand nand_7 (nand_7_out, nand_5_out, I1);
  nand nand_8 (Fout, nand_6_out, nand_7_out);
endmodule
