// Digital circuit mux_alu_1.dig as structural Verilog
module mux_alu_1 (
);

  // _74157 _74157_1: pin names not known; wires that end beside it: 1'b0, 1'b1
  // _74283 _74283_1: pin names not known; wires that end beside it: 1'b0, 1'b1
  // _74173 _74173_1: pin names not known; wires that end beside it: 1'b0, 1'b1
endmodule
