// Digital circuit serial_ALU.dig as structural Verilog
module serial_ALU (
  input  A,
  input  nA,
  input  nB,
  input  B,
  input  Cin,
  input  F,
  input  SETC,
  input  C,
  input  I1,
  input  I0,
  input  CLA,
  input  LD,
  output Cout,
  output CLC,
  output CtoFF,
  output Fout,
  output CLR
);

  wire nand_2_out, nand_5_out, nand_6_out, nand_7_out, nand_8_out, nand_9_out, nand_10_out, xor_1_out,
       xor_2_out, xor_3_out, xor_4_out;

  xor xor_1 (xor_1_out, A, nA);
  xor xor_2 (xor_2_out, nB, B);
  nand nand_1 (CtoFF, SETC, C);
  nand nand_2 (nand_2_out, C, C);
  xor xor_3 (xor_3_out, xor_1_out, xor_2_out);
  nand nand_3 (CLC, nand_2_out, LD);
  nand nand_4 (CLR, CLA, LD);
  xor xor_4 (xor_4_out, xor_3_out, Cin);
  nand nand_5 (nand_5_out, xor_3_out, Cin);
  nand nand_6 (nand_6_out, xor_1_out, xor_2_out);
  nand nand_7 (nand_7_out, nand_5_out, nand_6_out);
  nand nand_8 (nand_8_out, xor_4_out, I0);
  nand nand_9 (nand_9_out, I1, nand_7_out);
  nand nand_10 (nand_10_out, nand_7_out, F);
  nand nand_11 (Fout, nand_8_out, nand_9_out);
  nand nand_12 (Cout, nand_10_out, nand_10_out);

  // Other names for the same wires on the sheet: Aout = A; Bout = B

  // Notes on the sheet:
  //   ALU
  //   Any residual carry is cleared before an operation
  //   Carry is only set before Bit 0 of an operation
  //   Suppress Carry
endmodule
