// Digital circuit simplified_front_panel.dig as structural Verilog
module simplified_front_panel (
  input  in_1,
  input  in_2,
  input  in_3,
  input  clk,
  output GCLK,
  output P1,
  output P0,
  output P3,
  output P4,
  output P2
);

  wire _0_out, _1_out, _2_out, _3_out, _4_out, _5_out, _6_out, _7_out, _8_out, _9_out, _74173_4_pin11,
       _74173_4_pin12, _74173_4_pin13, _74173_4_pin14, A_out, AC, Ain, Arc, B_out, C_out, D_out,
       diodebackward_1_out, diodebackward_3_out, diodebackward_18_out, E_out, F_out, GATE, HOLD, Kout, LD,
       MR, n2SD, nand_1_out, nand_2_out, nand_3_out, nand_8_out, nGATE, nHOLD, nLATCH, not_5_out, not_6_out,
       nR, pullup_2_out, pullup_5_out, pullup_6_out, R, RCO, S0, S1, S2, S3, S4, S5, S6, S7, S8, S9, S10,
       S11, S12, S13, S14, S15, SETC, T2, T3, T4, T6, T7, T8, T9, U8_pin9, U27_pin9;
  wire [3:0] U8_pin4, U8_pin15, U9_pin4, U9_pin15, U17_pin14;

  Button #(.activeLow("true")) STA (.out(AC));
  _74173 _74173_1 (
    .pin1(1'b0), .pin2(1'b0), .pin3(S12), .pin4(S13), .pin5(S14), .pin6(S15), .pin7(nLATCH), .pin8(1'b0),
    .pin9(1'b0), .pin10(1'b0), .pin11(S11), .pin12(S10), .pin13(S9), .pin14(S8), .pin15(1'b0), .pin16(1'b1));
  _74165 U27 (
    .pin1(P0), .pin2(GCLK), .pin3(S11), .pin4(S10), .pin5(S9), .pin6(S8), .pin8(1'b0), .pin9(U27_pin9),
    .pin10(1'b0), .pin11(S15), .pin12(S14), .pin13(S13), .pin14(S12), .pin15(1'b0), .pin16(1'b1));  // open: pin7
  DiodeBackward diodebackward_1 (.in(AC), .out(diodebackward_1_out));
  PullUp pullup_1 (.out(diodebackward_1_out));
  _74173 _74173_2 (
    .pin1(1'b0), .pin2(1'b0), .pin3(S8), .pin4(S9), .pin5(S10), .pin6(S11), .pin7(nLATCH), .pin8(1'b0),
    .pin9(1'b0), .pin10(1'b0), .pin11(S7), .pin12(S6), .pin13(S5), .pin14(S4), .pin15(1'b0), .pin16(1'b1));
  Button #(.activeLow("true")) C (.out(C_out));
  Button #(.activeLow("true")) _8 (.out(_8_out));
  Button #(.activeLow("true")) _4 (.out(_4_out));
  Button #(.activeLow("true")) _0 (.out(_0_out));
  _74165 U28 (
    .pin1(P0), .pin2(GCLK), .pin3(S3), .pin4(S2), .pin5(S1), .pin6(S0), .pin8(1'b0), .pin9(Kout),
    .pin10(U27_pin9), .pin11(S7), .pin12(S6), .pin13(S5), .pin14(S4), .pin15(1'b0), .pin16(1'b1));  // open: pin7
  Seven_Seg_Hex seven_seg_hex_1 (.d({S15, S14, S13, S12}), .dp(1'b0));
  Seven_Seg_Hex seven_seg_hex_2 (.d({S11, S10, S9, S8}), .dp(1'b0));
  Button #(.activeLow("true")) D (.out(D_out));
  Button #(.activeLow("true")) _9 (.out(_9_out));
  Button #(.activeLow("true")) _5 (.out(_5_out));
  Button #(.activeLow("true")) _1 (.out(_1_out));
  Seven_Seg_Hex seven_seg_hex_3 (.d({S7, S6, S5, S4}), .dp(1'b0));
  _74173 _74173_3 (
    .pin1(1'b0), .pin2(1'b0), .pin3(S4), .pin4(S5), .pin5(S6), .pin6(S7), .pin7(nLATCH), .pin8(1'b0),
    .pin9(1'b0), .pin10(1'b0), .pin11(S3), .pin12(S2), .pin13(S1), .pin14(S0), .pin15(1'b0), .pin16(1'b1));
  Seven_Seg_Hex seven_seg_hex_4 (.d({S3, S2, S1, S0}), .dp(1'b0));
  Button #(.activeLow("true")) E (.out(E_out));
  Button #(.activeLow("true")) A (.out(A_out));
  Button #(.activeLow("true")) _6 (.out(_6_out));
  Button #(.activeLow("true")) _2 (.out(_2_out));
  Button #(.activeLow("true")) F (.out(F_out));
  Button #(.activeLow("true")) B (.out(B_out));
  Button #(.activeLow("true")) _7 (.out(_7_out));
  Button #(.activeLow("true")) _3 (.out(_3_out));
  _74173 _74173_4 (
    .pin1(1'b0), .pin2(1'b0), .pin3(S0), .pin4(S1), .pin5(S2), .pin6(S3), .pin7(nLATCH), .pin8(1'b0),
    .pin9(1'b0), .pin10(1'b0), .pin11(_74173_4_pin11), .pin12(_74173_4_pin12), .pin13(_74173_4_pin13),
    .pin14(_74173_4_pin14), .pin15(1'b0), .pin16(1'b1));
  PullUp pullup_2 (.out(pullup_2_out));
  DiodeBackward diodebackward_2 (.in(F_out), .out(pullup_2_out));
  DiodeBackward diodebackward_3 (.in(F_out), .out(diodebackward_3_out));
  DiodeBackward diodebackward_4 (.in(E_out), .out(pullup_2_out));
  DiodeBackward diodebackward_5 (.in(E_out), .out(diodebackward_3_out));
  DiodeBackward diodebackward_6 (.in(D_out), .out(diodebackward_3_out));
  DiodeBackward diodebackward_7 (.in(D_out), .out(pullup_2_out));
  DiodeBackward diodebackward_8 (.in(C_out), .out(diodebackward_3_out));
  DiodeBackward diodebackward_9 (.in(C_out), .out(pullup_2_out));
  DiodeBackward diodebackward_10 (.in(B_out), .out(pullup_2_out));
  DiodeBackward diodebackward_11 (.in(A_out), .out(pullup_2_out));
  DiodeBackward diodebackward_12 (.in(_9_out), .out(pullup_2_out));
  DiodeBackward diodebackward_13 (.in(_8_out), .out(pullup_2_out));
  DiodeBackward diodebackward_14 (.in(_7_out), .out(diodebackward_3_out));
  DiodeBackward diodebackward_15 (.in(_6_out), .out(diodebackward_3_out));
  DiodeBackward diodebackward_16 (.in(_5_out), .out(diodebackward_3_out));
  DiodeBackward diodebackward_17 (.in(_4_out), .out(diodebackward_3_out));
  not not_1 (_74173_4_pin11, pullup_2_out);
  PullUp pullup_3 (.out(diodebackward_3_out));
  DiodeBackward diodebackward_18 (.in(F_out), .out(diodebackward_18_out));
  DiodeBackward diodebackward_19 (.in(E_out), .out(diodebackward_18_out));
  DiodeBackward diodebackward_20 (.in(B_out), .out(diodebackward_18_out));
  DiodeBackward diodebackward_21 (.in(A_out), .out(diodebackward_18_out));
  DiodeBackward diodebackward_22 (.in(_7_out), .out(diodebackward_18_out));
  DiodeBackward diodebackward_23 (.in(_6_out), .out(diodebackward_18_out));
  DiodeBackward diodebackward_24 (.in(_3_out), .out(diodebackward_18_out));
  DiodeBackward diodebackward_25 (.in(_2_out), .out(diodebackward_18_out));
  not not_2 (_74173_4_pin12, diodebackward_3_out);
  PullUp pullup_4 (.out(diodebackward_18_out));
  PullUp pullup_5 (.out(pullup_5_out));
  DiodeBackward diodebackward_26 (.in(F_out), .out(pullup_5_out));
  DiodeBackward diodebackward_27 (.in(D_out), .out(pullup_5_out));
  DiodeBackward diodebackward_28 (.in(B_out), .out(pullup_5_out));
  DiodeBackward diodebackward_29 (.in(_9_out), .out(pullup_5_out));
  DiodeBackward diodebackward_30 (.in(_7_out), .out(pullup_5_out));
  DiodeBackward diodebackward_31 (.in(_5_out), .out(pullup_5_out));
  DiodeBackward diodebackward_32 (.in(_3_out), .out(pullup_5_out));
  DiodeBackward diodebackward_33 (.in(_1_out), .out(pullup_5_out));
  not not_3 (_74173_4_pin14, pullup_5_out);
  not not_4 (_74173_4_pin13, diodebackward_18_out);
  PullUp pullup_6 (.out(pullup_6_out));
  DiodeBackward diodebackward_34 (.in(F_out), .out(pullup_6_out));
  DiodeBackward diodebackward_35 (.in(E_out), .out(pullup_6_out));
  DiodeBackward diodebackward_36 (.in(D_out), .out(pullup_6_out));
  DiodeBackward diodebackward_37 (.in(C_out), .out(pullup_6_out));
  DiodeBackward diodebackward_38 (.in(B_out), .out(pullup_6_out));
  DiodeBackward diodebackward_39 (.in(A_out), .out(pullup_6_out));
  DiodeBackward diodebackward_40 (.in(_9_out), .out(pullup_6_out));
  DiodeBackward diodebackward_41 (.in(_8_out), .out(pullup_6_out));
  DiodeBackward diodebackward_42 (.in(_7_out), .out(pullup_6_out));
  DiodeBackward diodebackward_43 (.in(_6_out), .out(pullup_6_out));
  DiodeBackward diodebackward_44 (.in(_5_out), .out(pullup_6_out));
  DiodeBackward diodebackward_45 (.in(_4_out), .out(pullup_6_out));
  DiodeBackward diodebackward_46 (.in(_3_out), .out(pullup_6_out));
  DiodeBackward diodebackward_47 (.in(_2_out), .out(pullup_6_out));
  DiodeBackward diodebackward_48 (.in(_1_out), .out(pullup_6_out));
  DiodeBackward diodebackward_49 (.in(_0_out), .out(pullup_6_out));
  not not_5 (not_5_out, pullup_6_out);
  Monoflop monoflop_1 (.C(not_5_out), .R(1'b0), .nQ(nLATCH));  // open: Q
  nand nand_1 (nand_1_out, AC, AC);
  nand nand_2 (nand_2_out, Kout, nand_1_out);
  nand nand_3 (nand_3_out, AC, Arc);
  nand nand_4 (Ain, nand_2_out, nand_3_out);
  _74595 U8 (
    .pin1(U8_pin15[2]), .pin2(U8_pin15[1]), .pin3(U8_pin15[0]), .pin4(U8_pin4[3]), .pin5(U8_pin4[2]),
    .pin6(U8_pin4[1]), .pin7(U8_pin4[0]), .pin8(1'b0), .pin9(U8_pin9), .pin10(P1), .pin11(GCLK), .pin12(AC),
    .pin13(1'b0), .pin14(Ain), .pin15(U8_pin15[3]), .pin16(1'b1));
  _74595 U9 (
    .pin1(U9_pin15[2]), .pin2(U9_pin15[1]), .pin3(U9_pin15[0]), .pin4(U9_pin4[3]), .pin5(U9_pin4[2]),
    .pin6(U9_pin4[1]), .pin7(U9_pin4[0]), .pin8(1'b0), .pin9(Arc), .pin10(P1), .pin11(GCLK), .pin12(AC),
    .pin13(1'b0), .pin14(U8_pin9), .pin15(U9_pin15[3]), .pin16(1'b1));
  Seven_Seg_Hex seven_seg_hex_5 (.d(U8_pin15), .dp(1'b0));
  Seven_Seg_Hex seven_seg_hex_6 (.d(U8_pin4), .dp(1'b0));
  Seven_Seg_Hex seven_seg_hex_7 (.d(U9_pin15), .dp(1'b0));
  Seven_Seg_Hex seven_seg_hex_8 (.d(U9_pin4), .dp(1'b0));
  Reset reset_1 (.out(n2SD));
  not not_6 (not_6_out, MR);
  not not_7 (P4, T4);
  not not_8 (P3, T3);
  not not_9 (P2, T2);
  not not_10 (P1, SETC);
  not not_11 (P0, LD);
  nand nand_5 (GATE, P2, nGATE);
  nand nand_6 (nGATE, GATE, nR);
  nand nand_7 (GCLK, GATE, nand_8_out);
  nand nand_8 (nand_8_out, clk, clk);
  _7474 U30 (
    .pin1(1'b1), .pin2(RCO), .pin3(clk), .pin4(n2SD), .pin5(R), .pin6(nR), .pin7(1'b0), .pin10(1'b1),
    .pin11(1'b1), .pin12(1'b1), .pin13(1'b1), .pin14(1'b1));  // open: pin8, pin9
  nand nand_9 (HOLD, nGATE, nHOLD);
  nand nand_10 (nHOLD, HOLD, nR);
  _744017 U16 (
    .pin1(MR), .pin2(SETC), .pin3(LD), .pin4(T2), .pin5(T6), .pin6(T7), .pin7(T3), .pin8(1'b0), .pin9(T8),
    .pin10(T4), .pin11(T9), .pin13(HOLD), .pin14(clk), .pin15(MR), .pin16(1'b1));  // open: pin12
  _74161 U17 (
    .pin1(GATE), .pin2(clk), .pin3(1'b0), .pin4(1'b0), .pin5(1'b0), .pin6(1'b0), .pin7(1'b1), .pin8(1'b0),
    .pin9(1'b1), .pin10(1'b1), .pin11(U17_pin14[3]), .pin12(U17_pin14[2]), .pin13(U17_pin14[1]),
    .pin14(U17_pin14[0]), .pin15(RCO), .pin16(1'b1));
  Seven_Seg_Hex seven_seg_hex_9 (.d(U17_pin14), .dp(1'b0));

  // Other names for the same wires on the sheet: nAEN = GATE; nCE = in_3; nLD = P0; nOE = in_2; nRES = P1;
  //   nCLR = n2SD; nRRES = n2SD; nSET = P2; nWE = in_1; T0 = LD; T1 = SETC; T5 = MR

  // Notes on the sheet:
  //   in_1: default 1
  //   in_2: default 1
  //   in_3: default 1
  //   clk: Hz: 2147483647
  //   Front Panel
  //   Keypad read register K
  //   Hex Keypad
  //   KEY DATA
  //   KEYSWITCH REGISTER
  //   A,B,C,D Registers
  //   K REGISTER
  //   Clock Sequencer
  //   U11
  //   16th Pulse FF
  //   U19
  //   # Clock
endmodule
