// Digital circuit spider002.dig as structural Verilog
module spider002 (
  input  in_2,
  input  in_3,
  input  in_4,
  input  clk,
  input  in_15,
  input  nSW,
  input  in_17,
  input  in_18,
  input  in_19,
  input  in_20,
  input  in_21,
  input  in_22,
  input  in_24,
  output Fout,
  output nLDB,
  output out_6,
  output SETC,
  output RES,
  output RUN,
  output T0,
  output GCLK,
  output CLK_2,
  output GCLK_2,
  output out_23
);

  wire _74161_1_pin15, _74173_1_pin3, _74173_1_pin4, _74173_1_pin5, _74173_1_pin6, _74173_2_pin3,
       _74173_2_pin4, _74173_2_pin5, _74173_2_pin6, _74173_3_pin3, _74173_3_pin4, _74173_3_pin5,
       _74173_3_pin6, AC0, AC1, AC2, AC3, AC4, AC5, AC6, AC7, AC8, AC9, AC10, AC11, AC12, AC13, AC14, AC15,
       ADD, AND, Aout, Bout, BUS0, BUS1, BUS2, BUS3, BUS4, BUS5, BUS6, BUS7, BUS8, BUS9, BUS10, BUS11, BUS12,
       BUS13, BUS14, BUS15, button_1_out, button_2_out, button_3_out, button_4_out, button_5_out,
       button_6_out, button_7_out, button_8_out, button_9_out, button_10_out, button_11_out, button_12_out,
       button_13_out, button_14_out, button_15_out, button_16_out, button_18_out, C, Cin, CLA, CLR, Cout, D0,
       D1, D2, D3, D4, D5, D6, D7, D8, D9, D10, D11, D12, D13, D14, D15, d_ff_1_nq, d_ff_2_nq, d_ff_3_nq,
       d_ff_4_nq, d_ff_5_nq, d_ff_6_nq, d_ff_7_nq, d_ff_8_nq, d_ff_9_nq, d_ff_10_nq, d_ff_11_nq, d_ff_12_nq,
       diodebackward_2_out, diodebackward_6_out, diodebackward_8_out, diodebackward_10_out,
       diodeforward_1_out, F, I0, I1, I4, I5, I6, I7, IC18_2_nq, IC18_nq, IC19_2_nq, IC19_nq, INCPC, LOAD,
       nA, nand_2_out, nand_3_out, nand_6_out, nand_8_out, nand_9_out, nand_10_out, nand_11_out, nand_12_out,
       nand_13_out, nand_16_out, nand_18_out, nB, nCLRPC, nJMP, not_1_out, not_2_out, nRST, nTP0, nTP1, nTP3,
       nTP5, nTP6, nWE, nZERO, OR, or_1_out, PC0, PC1, PC2, PC3, PC4, PC5, PC6, PC7, PC8, PC9, PC10, PC11,
       PC12, PC13, PC14, PC15, pullup_1_out, pullup_4_out, pullup_5_out, Q3, Q4, reset_1_out, ST, SUB,
       U3_pin11, U3_pin12, U3_pin13, U3_pin14, U3_pin15, U4_pin11, U4_pin12, U4_pin13, U4_pin14, U4_pin15,
       U5_2_pin9, U5_pin11, U5_pin12, U5_pin13, U5_pin14, U5_pin15, U6_pin11, U6_pin12, U6_pin13, U6_pin14,
       U8_pin9, XOR, xor_1_out, xor_2_out, xor_3_out, xor_4_out;
  wire [2:0] _74161_1_pin12;
  wire [3:0] _74541_3_pin5, _74541_3_pin9, _74541_4_pin6, IC18_q, U5_3_pin6, U5_3_pin13, U6_3_pin6;
  wire [3:1] U6_3_pin10;

  Reset reset_1 (.out(reset_1_out));
  _74163 U3 (
    .pin1(reset_1_out), .pin2(INCPC), .pin3(BUS0), .pin4(BUS1), .pin5(BUS2), .pin6(BUS3), .pin7(1'b1),
    .pin8(1'b0), .pin9(in_18), .pin10(1'b1), .pin11(U3_pin11), .pin12(U3_pin12), .pin13(U3_pin13),
    .pin14(U3_pin14), .pin15(U3_pin15), .pin16(1'b1));
  _74163 U4 (
    .pin1(reset_1_out), .pin2(INCPC), .pin3(BUS4), .pin4(BUS5), .pin5(BUS6), .pin6(BUS7), .pin7(1'b1),
    .pin8(1'b0), .pin9(in_18), .pin10(U3_pin15), .pin11(U4_pin11), .pin12(U4_pin12), .pin13(U4_pin13),
    .pin14(U4_pin14), .pin15(U4_pin15), .pin16(1'b1));
  _74163 U5 (
    .pin1(reset_1_out), .pin2(INCPC), .pin3(BUS8), .pin4(BUS9), .pin5(BUS10), .pin6(BUS11), .pin7(1'b1),
    .pin8(1'b0), .pin9(in_17), .pin10(U4_pin15), .pin11(U5_pin11), .pin12(U5_pin12), .pin13(U5_pin13),
    .pin14(U5_pin14), .pin15(U5_pin15), .pin16(1'b1));
  _74163 U6 (
    .pin1(reset_1_out), .pin2(INCPC), .pin3(in_19), .pin4(in_20), .pin5(in_21), .pin6(in_22), .pin7(1'b1),
    .pin8(1'b0), .pin9(in_17), .pin10(U5_pin15), .pin11(U6_pin11), .pin12(U6_pin12), .pin13(U6_pin13),
    .pin14(U6_pin14), .pin16(1'b1));  // open: pin15
  _74541 _74541_1 (
    .pin1(in_24), .pin2(U3_pin14), .pin3(U3_pin13), .pin4(U3_pin12), .pin5(U3_pin11), .pin6(U4_pin14),
    .pin7(U4_pin13), .pin8(U4_pin12), .pin9(U4_pin11), .pin10(1'b0), .pin11(PC7), .pin12(PC6), .pin13(PC5),
    .pin14(PC4), .pin15(PC3), .pin16(PC2), .pin17(PC1), .pin18(PC0), .pin19(1'b0), .pin20(1'b1));
  _74541 _74541_2 (
    .pin1(in_24), .pin2(U5_pin14), .pin3(U5_pin13), .pin4(U5_pin12), .pin5(U5_pin11), .pin6(U6_pin14),
    .pin7(U6_pin13), .pin8(U6_pin12), .pin9(U6_pin11), .pin10(1'b0), .pin11(PC15), .pin12(PC14),
    .pin13(PC13), .pin14(PC12), .pin15(PC11), .pin16(PC10), .pin17(PC9), .pin18(PC8), .pin19(1'b0),
    .pin20(1'b1));
  not not_1 (not_1_out, in_24);
  // _62256 _62256_1: pin names not known; wires that end beside it: PC14, PC12, PC7, PC6, PC5, PC4, PC3, PC2, PC1, PC0, BUS8, BUS9, BUS10, 1'b0, 1'b1, nWE, PC13, PC8, PC9, PC11, out_23, PC10, 1'b0, BUS15
  _74173 _74173_1 (
    .pin1(not_1_out), .pin2(not_1_out), .pin3(_74173_1_pin3), .pin4(_74173_1_pin4), .pin5(_74173_1_pin5),
    .pin6(_74173_1_pin6), .pin7(out_6), .pin8(1'b0), .pin9(1'b0), .pin10(1'b0), .pin11(BUS3), .pin12(BUS2),
    .pin13(BUS1), .pin14(BUS0), .pin15(1'b0), .pin16(1'b1));
  _74173 _74173_2 (
    .pin1(not_1_out), .pin2(not_1_out), .pin3(_74173_2_pin3), .pin4(_74173_2_pin4), .pin5(_74173_2_pin5),
    .pin6(_74173_2_pin6), .pin7(out_6), .pin8(1'b0), .pin9(1'b0), .pin10(1'b0), .pin11(BUS7), .pin12(BUS6),
    .pin13(BUS5), .pin14(BUS4), .pin15(1'b0), .pin16(1'b1));
  _74173 _74173_3 (
    .pin1(not_1_out), .pin2(not_1_out), .pin3(_74173_3_pin3), .pin4(_74173_3_pin4), .pin5(_74173_3_pin5),
    .pin6(_74173_3_pin6), .pin7(out_6), .pin8(1'b0), .pin9(1'b0), .pin10(1'b0), .pin11(BUS11), .pin12(BUS10),
    .pin13(BUS9), .pin14(BUS8), .pin15(1'b0), .pin16(1'b1));
  // _62256 _62256_2: pin names not known; wires that end beside it: PC14, PC12, PC7, PC6, PC5, PC4, PC3, PC2, PC1, PC0, BUS0, BUS1, BUS2, 1'b0, 1'b1, nWE, PC13, PC8, PC9, PC11, out_23, PC10, 1'b0, BUS7
  Seven_Seg_Hex seven_seg_hex_1 (.d({PC15, PC14, PC13, PC12}), .dp(1'b0));
  Seven_Seg_Hex seven_seg_hex_2 (.d({PC11, PC10, PC9, PC8}), .dp(1'b0));
  Seven_Seg_Hex seven_seg_hex_3 (.d({PC7, PC6, PC5, PC4}), .dp(1'b0));
  _74138 U1 (
    .pin1(I4), .pin2(I5), .pin3(I6), .pin4(1'b0), .pin5(1'b0), .pin6(1'b1), .pin7(nJMP), .pin8(1'b0),
    .pin9(ST), .pin10(SUB), .pin11(ADD), .pin12(XOR), .pin13(OR), .pin14(AND), .pin15(LOAD), .pin16(1'b1));
  _74173 _74173_4 (
    .pin1(1'b0), .pin2(1'b0), .pin3(I4), .pin4(I5), .pin5(I6), .pin6(I7), .pin7(out_6), .pin8(1'b0),
    .pin9(1'b0), .pin10(1'b0), .pin11(in_2), .pin12(in_3), .pin13(in_4), .pin14(in_15), .pin15(1'b0),
    .pin16(1'b1));
  Seven_Seg_Hex seven_seg_hex_4 (.d({PC3, PC2, PC1, PC0}), .dp(1'b0));
  PullUp pullup_1 (.out(pullup_1_out));
  DiodeBackward diodebackward_1 (.in(LOAD), .out(pullup_1_out));
  DiodeBackward diodebackward_2 (.in(LOAD), .out(diodebackward_2_out));
  DiodeBackward diodebackward_3 (.in(ADD), .out(diodebackward_2_out));
  DiodeBackward diodebackward_4 (.in(SUB), .out(diodebackward_2_out));
  DiodeBackward diodebackward_5 (.in(nJMP), .out(diodebackward_2_out));
  Seven_Seg_Hex seven_seg_hex_5 (.d({BUS15, BUS14, BUS13, BUS12}), .dp(1'b0));
  PullUp pullup_2 (.out(diodebackward_2_out));
  DiodeBackward diodebackward_6 (.in(SUB), .out(diodebackward_6_out));
  Seven_Seg_Hex seven_seg_hex_6 (.d({BUS11, BUS10, BUS9, BUS8}), .dp(1'b0));
  PullUp pullup_3 (.out(diodebackward_6_out));
  PullUp pullup_4 (.out(pullup_4_out));
  DiodeBackward diodebackward_7 (.in(SUB), .out(pullup_4_out));
  Seven_Seg_Hex seven_seg_hex_7 (.d({BUS7, BUS6, BUS5, BUS4}), .dp(1'b0));
  PullUp pullup_5 (.out(pullup_5_out));
  DiodeBackward diodebackward_8 (.in(AND), .out(diodebackward_8_out));
  DiodeBackward diodebackward_9 (.in(OR), .out(diodebackward_8_out));
  Seven_Seg_Hex seven_seg_hex_8 (.d({BUS3, BUS2, BUS1, BUS0}), .dp(1'b0));
  PullUp pullup_6 (.out(diodebackward_8_out));
  DiodeBackward diodebackward_10 (.in(LOAD), .out(diodebackward_10_out));
  DiodeBackward diodebackward_11 (.in(OR), .out(diodebackward_10_out));
  DiodeBackward diodebackward_12 (.in(XOR), .out(diodebackward_10_out));
  DiodeBackward diodebackward_13 (.in(ADD), .out(diodebackward_10_out));
  DiodeBackward diodebackward_14 (.in(SUB), .out(diodebackward_10_out));
  DiodeBackward diodebackward_15 (.in(ST), .out(diodebackward_10_out));
  PullUp pullup_7 (.out(diodebackward_10_out));
  _74540 U2 (
    .pin1(1'b0), .pin2(diodebackward_10_out), .pin3(diodebackward_8_out), .pin4(pullup_5_out),
    .pin5(pullup_4_out), .pin6(diodebackward_6_out), .pin7(diodebackward_2_out), .pin8(pullup_1_out),
    .pin9(1'b0), .pin10(1'b0), .pin12(CLA), .pin13(F), .pin14(C), .pin15(nB), .pin16(nA), .pin17(I1),
    .pin18(I0), .pin19(1'b0), .pin20(1'b1));  // open: pin11
  _74165 U5_2 (
    .pin1(out_6), .pin2(GCLK), .pin3(BUS11), .pin4(BUS10), .pin5(BUS9), .pin6(BUS8), .pin8(1'b0),
    .pin9(U5_2_pin9), .pin10(1'b0), .pin11(BUS15), .pin12(BUS14), .pin13(BUS13), .pin14(BUS12), .pin15(1'b0),
    .pin16(1'b1));  // open: pin7
  LED led_1 (.in(_74541_3_pin5[3]));
  D_FF IC19 (.D(IC19_nq), .C(button_1_out), .Q(_74541_3_pin5[3]), .nQ(IC19_nq));
  LED led_2 (.in(_74541_3_pin5[2]));
  D_FF d_ff_1 (.D(d_ff_1_nq), .C(button_2_out), .Q(_74541_3_pin5[2]), .nQ(d_ff_1_nq));
  Button button_1 (.out(button_1_out));
  _74541 _74541_3 (
    .pin1(1'b0), .pin2(_74541_3_pin5[3]), .pin3(_74541_3_pin5[2]), .pin4(_74541_3_pin5[1]),
    .pin5(_74541_3_pin5[0]), .pin6(_74541_3_pin9[3]), .pin7(_74541_3_pin9[2]), .pin8(_74541_3_pin9[1]),
    .pin9(_74541_3_pin9[0]), .pin10(1'b0), .pin11(D8), .pin12(D9), .pin13(D10), .pin14(D11), .pin15(D12),
    .pin16(D13), .pin17(D14), .pin18(D15), .pin19(nSW), .pin20(1'b1));
  LED led_3 (.in(_74541_3_pin5[1]));
  D_FF d_ff_2 (.D(d_ff_2_nq), .C(button_3_out), .Q(_74541_3_pin5[1]), .nQ(d_ff_2_nq));
  Button button_2 (.out(button_2_out));
  _74595 U8 (
    .pin1(AC14), .pin2(AC13), .pin3(AC12), .pin4(AC11), .pin5(AC10), .pin6(AC9), .pin7(AC8), .pin8(1'b0),
    .pin9(U8_pin9), .pin10(RES), .pin11(GCLK), .pin12(T0), .pin13(1'b0), .pin14(Fout), .pin15(AC15),
    .pin16(1'b1));
  LED led_4 (.in(_74541_3_pin5[0]));
  D_FF d_ff_3 (.D(d_ff_3_nq), .C(button_4_out), .Q(_74541_3_pin5[0]), .nQ(d_ff_3_nq));
  Button button_3 (.out(button_3_out));
  LED led_5 (.in(_74541_3_pin9[3]));
  D_FF d_ff_4 (.D(d_ff_4_nq), .C(button_5_out), .Q(_74541_3_pin9[3]), .nQ(d_ff_4_nq));
  Button button_4 (.out(button_4_out));
  LED led_6 (.in(_74541_3_pin9[2]));
  D_FF d_ff_5 (.D(d_ff_5_nq), .C(button_6_out), .Q(_74541_3_pin9[2]), .nQ(d_ff_5_nq));
  Button button_5 (.out(button_5_out));
  _74165 U6_2 (
    .pin1(out_6), .pin2(GCLK), .pin3(BUS3), .pin4(BUS2), .pin5(BUS1), .pin6(BUS0), .pin8(1'b0), .pin9(Bout),
    .pin10(U5_2_pin9), .pin11(BUS7), .pin12(BUS6), .pin13(BUS5), .pin14(BUS4), .pin15(1'b0), .pin16(1'b1));  // open: pin7
  LED led_7 (.in(_74541_3_pin9[1]));
  D_FF d_ff_6 (.D(d_ff_6_nq), .C(button_7_out), .Q(_74541_3_pin9[1]), .nQ(d_ff_6_nq));
  Button button_6 (.out(button_6_out));
  LED led_8 (.in(_74541_3_pin9[0]));
  D_FF IC19_2 (.D(IC19_2_nq), .C(button_8_out), .Q(_74541_3_pin9[0]), .nQ(IC19_2_nq));
  Button button_7 (.out(button_7_out));
  _74595 U9 (
    .pin1(AC6), .pin2(AC5), .pin3(AC4), .pin4(AC3), .pin5(AC2), .pin6(AC1), .pin7(AC0), .pin8(1'b0),
    .pin10(RES), .pin11(GCLK), .pin12(T0), .pin13(1'b0), .pin14(U8_pin9), .pin15(AC7), .pin16(1'b1));  // open: pin9
  Button button_8 (.out(button_8_out));
  Seven_Seg_Hex seven_seg_hex_9 (.d(_74541_3_pin5), .dp(1'b0));
  Seven_Seg_Hex seven_seg_hex_10 (.d(_74541_3_pin9), .dp(1'b0));
  DiodeForward diodeforward_1 (.in(AC15), .out(diodeforward_1_out));
  DiodeForward diodeforward_2 (.in(AC14), .out(diodeforward_1_out));
  DiodeForward diodeforward_3 (.in(AC13), .out(diodeforward_1_out));
  DiodeForward diodeforward_4 (.in(AC12), .out(diodeforward_1_out));
  DiodeForward diodeforward_5 (.in(AC11), .out(diodeforward_1_out));
  DiodeForward diodeforward_6 (.in(AC10), .out(diodeforward_1_out));
  DiodeForward diodeforward_7 (.in(AC9), .out(diodeforward_1_out));
  DiodeForward diodeforward_8 (.in(AC8), .out(diodeforward_1_out));
  DiodeForward diodeforward_9 (.in(AC7), .out(diodeforward_1_out));
  DiodeForward diodeforward_10 (.in(AC6), .out(diodeforward_1_out));
  DiodeForward diodeforward_11 (.in(AC5), .out(diodeforward_1_out));
  DiodeForward diodeforward_12 (.in(AC4), .out(diodeforward_1_out));
  DiodeForward diodeforward_13 (.in(AC3), .out(diodeforward_1_out));
  DiodeForward diodeforward_14 (.in(AC2), .out(diodeforward_1_out));
  DiodeForward diodeforward_15 (.in(AC1), .out(diodeforward_1_out));
  DiodeForward diodeforward_16 (.in(AC0), .out(diodeforward_1_out));
  LED led_9 (.in(IC18_q[3]));
  D_FF IC18 (.D(IC18_nq), .C(button_9_out), .Q(IC18_q[3]), .nQ(IC18_nq));
  Button button_9 (.out(button_9_out));
  Seven_Seg_Hex seven_seg_hex_11 (.d({AC15, AC14, AC13, AC12}), .dp(1'b0));
  LED led_10 (.in(diodeforward_1_out));
  PullDown pulldown_1 (.out(diodeforward_1_out));
  LED led_11 (.in(IC18_q[2]));
  D_FF d_ff_7 (.D(d_ff_7_nq), .C(button_10_out), .Q(IC18_q[2]), .nQ(d_ff_7_nq));
  Button button_10 (.out(button_10_out));
  Seven_Seg_Hex seven_seg_hex_12 (.d({AC11, AC10, AC9, AC8}), .dp(1'b0));
  _74541 _74541_4 (
    .pin1(1'b0), .pin2(IC18_q[3]), .pin3(IC18_q[2]), .pin4(IC18_q[1]), .pin5(IC18_q[0]),
    .pin6(_74541_4_pin6[3]), .pin7(_74541_4_pin6[2]), .pin8(_74541_4_pin6[1]), .pin9(_74541_4_pin6[0]),
    .pin10(1'b0), .pin11(D0), .pin12(D1), .pin13(D2), .pin14(D3), .pin15(D4), .pin16(D5), .pin17(D6),
    .pin18(D7), .pin19(nSW), .pin20(1'b1));
  LED led_12 (.in(IC18_q[1]));
  D_FF d_ff_8 (.D(d_ff_8_nq), .C(button_11_out), .Q(IC18_q[1]), .nQ(d_ff_8_nq));
  Button button_11 (.out(button_11_out));
  Seven_Seg_Hex seven_seg_hex_13 (.d({AC7, AC6, AC5, AC4}), .dp(1'b0));
  nand nand_1 (nZERO, diodeforward_1_out, diodeforward_1_out);
  _74164 U5_3 (
    .pin1(1'b1), .pin2(Fout), .pin3(U5_3_pin6[3]), .pin4(U5_3_pin6[2]), .pin5(U5_3_pin6[1]),
    .pin6(U5_3_pin6[0]), .pin7(1'b0), .pin8(GCLK), .pin9(CLR), .pin10(U5_3_pin13[3]), .pin11(U5_3_pin13[2]),
    .pin12(U5_3_pin13[1]), .pin13(U5_3_pin13[0]), .pin14(1'b1));
  LED led_13 (.in(IC18_q[0]));
  D_FF d_ff_9 (.D(d_ff_9_nq), .C(button_12_out), .Q(IC18_q[0]), .nQ(d_ff_9_nq));
  Button button_12 (.out(button_12_out));
  Seven_Seg_Hex seven_seg_hex_14 (.d({AC3, AC2, AC1, AC0}), .dp(1'b0));
  LED led_14 (.in(_74541_4_pin6[3]));
  D_FF d_ff_10 (.D(d_ff_10_nq), .C(button_13_out), .Q(_74541_4_pin6[3]), .nQ(d_ff_10_nq));
  Button button_13 (.out(button_13_out));
  LED led_15 (.in(_74541_4_pin6[2]));
  D_FF d_ff_11 (.D(d_ff_11_nq), .C(button_14_out), .Q(_74541_4_pin6[2]), .nQ(d_ff_11_nq));
  Button button_14 (.out(button_14_out));
  Seven_Seg_Hex seven_seg_hex_15 (.d(U5_3_pin6), .dp(1'b0));
  LED led_16 (.in(_74541_4_pin6[1]));
  D_FF d_ff_12 (.D(d_ff_12_nq), .C(button_15_out), .Q(_74541_4_pin6[1]), .nQ(d_ff_12_nq));
  Button button_15 (.out(button_15_out));
  Seven_Seg_Hex seven_seg_hex_16 (.d(U5_3_pin13), .dp(1'b0));
  LED led_17 (.in(_74541_4_pin6[0]));
  D_FF IC18_2 (.D(IC18_2_nq), .C(button_16_out), .Q(_74541_4_pin6[0]), .nQ(IC18_2_nq));
  Button button_16 (.out(button_16_out));
  Seven_Seg_Hex seven_seg_hex_17 (.d(U6_3_pin6), .dp(1'b0));
  Seven_Seg_Hex seven_seg_hex_18 (.d(IC18_q), .dp(1'b0));
  Seven_Seg_Hex seven_seg_hex_19 (.d({U6_3_pin10, Aout}), .dp(1'b0));
  _74164 U6_3 (
    .pin1(1'b1), .pin2(U5_3_pin13[0]), .pin3(U6_3_pin6[3]), .pin4(U6_3_pin6[2]), .pin5(U6_3_pin6[1]),
    .pin6(U6_3_pin6[0]), .pin7(1'b0), .pin8(GCLK), .pin9(CLR), .pin10(U6_3_pin10[3]), .pin11(U6_3_pin10[2]),
    .pin12(U6_3_pin10[1]), .pin13(Aout), .pin14(1'b1));
  Seven_Seg_Hex seven_seg_hex_20 (.d(_74541_4_pin6), .dp(1'b0));
  Button button_17 (.out(RUN));
  _74161 _74161_1 (
    .pin1(nRST), .pin2(clk), .pin3(1'b0), .pin4(1'b0), .pin5(1'b0), .pin6(1'b0), .pin7(1'b1), .pin8(1'b0),
    .pin9(1'b1), .pin10(1'b1), .pin11(Q3), .pin12(_74161_1_pin12[2]), .pin13(_74161_1_pin12[1]),
    .pin14(_74161_1_pin12[0]), .pin15(_74161_1_pin15), .pin16(1'b1));
  _74161 _74161_2 (
    .pin1(nRST), .pin2(clk), .pin3(1'b0), .pin4(1'b0), .pin5(1'b0), .pin6(1'b0), .pin7(1'b1), .pin8(1'b0),
    .pin9(1'b1), .pin10(_74161_1_pin15), .pin14(Q4), .pin16(1'b1));  // open: pin11, pin12, pin13, pin15
  Monoflop monoflop_1 (.C(button_18_out), .R(1'b0), .nQ(nCLRPC));  // open: Q
  Button button_18 (.out(button_18_out));
  nand nand_2 (nand_2_out, SETC, C);
  nand nand_3 (nand_3_out, C, C);
  nand nand_4 (CLR, CLA, nLDB);
  nand nand_5 (nRST, Q3, Q4);
  Seven_Seg_Hex seven_seg_hex_21 (.d({3'b000, Q4}), .dp(1'b0));
  xor xor_1 (xor_1_out, Aout, nA);
  xor xor_2 (xor_2_out, nB, Bout);
  nand nand_6 (nand_6_out, nand_3_out, nLDB);
  Seven_Seg_Hex seven_seg_hex_22 (.d({Q3, _74161_1_pin12}), .dp(1'b0));
  or or_1 (or_1_out, Q3, Q4);
  xor xor_3 (xor_3_out, xor_1_out, xor_2_out);
  _74138 _74138_1 (
    .pin1(_74161_1_pin12[0]), .pin2(_74161_1_pin12[1]), .pin3(_74161_1_pin12[2]), .pin4(Q3), .pin5(Q4),
    .pin6(1'b1), .pin7(RES), .pin8(1'b0), .pin9(nTP6), .pin10(nTP5), .pin11(out_6), .pin12(nTP3),
    .pin13(INCPC), .pin14(nTP1), .pin15(nTP0), .pin16(1'b1));
  not not_2 (not_2_out, clk);
  not not_3 (T0, nRST);
  nand nand_7 (GCLK, not_2_out, or_1_out);
  xor xor_4 (xor_4_out, xor_3_out, Cin);
  nand nand_8 (nand_8_out, xor_3_out, Cin);
  nand nand_9 (nand_9_out, xor_1_out, xor_2_out);
  LED led_18 (.in(GCLK));
  nand nand_10 (nand_10_out, nand_8_out, nand_9_out);
  LED TP0 (.in(nTP0));
  LED TP1 (.in(nTP1));
  LED TP2 (.in(INCPC));
  LED TP3 (.in(nTP3));
  LED TP4 (.in(out_6));
  LED TP5 (.in(nTP5));
  LED TP6 (.in(nTP6));
  LED TP7 (.in(RES));
  nand nand_11 (nand_11_out, xor_4_out, I0);
  nand nand_12 (nand_12_out, I1, nand_10_out);
  nand nand_13 (nand_13_out, nand_10_out, F);
  _7474 _7474_1 (
    .pin1(1'b1), .pin2(1'b1), .pin3(clk), .pin4(1'b1), .pin7(1'b0), .pin9(Cin), .pin10(nand_2_out),
    .pin11(GCLK), .pin12(Cout), .pin13(nand_6_out), .pin14(1'b1));  // open: pin5, pin6, pin8
  nand nand_14 (Fout, nand_11_out, nand_12_out);
  nand nand_15 (Cout, nand_13_out, nand_13_out);
  nand nand_16 (nand_16_out, nTP0, nWE);
  nand nand_17 (nWE, nand_16_out, INCPC);
  nand nand_18 (nand_18_out, nTP3, out_23);
  nand nand_19 (out_23, nand_18_out, nTP5);
  not not_4 (nLDB, out_6);
  not not_5 (SETC, RES);

  assign CLK_2 = clk;
  assign GCLK_2 = GCLK;

  // Other names for the same wires on the sheet: LDA = nLDB; nOE = out_23; nPCEN = in_24; nPH = in_17; nPL = in_18;
  //   nTP2 = INCPC; nLDB_t = out_6; nTP4 = out_6; nTP7 = RES

  // Notes on the sheet:
  //   nSW: default 1
  //   in_17: default 1
  //   in_18: default 1
  //   in_24: default 1
  //   RAM HI
  //   RAM LO
  //   spider-0
  //   RAM ADDRESS
  //   Instruction Input
  //   Instruction Decode
  //   CLA
  //   RAM DATA
  //   F
  //   ~B
  //   C
  //   ~A
  //   I1
  //   I0
  //   LOAD
  //   AND
  //   OR
  //   XOR
  //   ADD
  //   SUB
  //   STORE
  //   JMP
  //   16 bit Shift Register B
  //   ENTER H
  //   Data Input
  //   Output Display Registers
  //   OUTPUT REGISTER
  //   ENTER L
  //   ACCUMULATOR
  //   STEP/RUN
  //   Clock Sequencer
  //   16 bit Shift Register A
  //   CLR PC
  //   CLR ACC
  //   # Clock
  //   Note Clock Inverted
  //   Carry is only set before Bit 0 of an operation
  //   Any residual carry is cleared before an operation
  //   Spider_0 Bit serial CPU Testbed
  //   Suppress Carry
  //   Latch Result
  //   Write Result to RAM
  //   Increment PC
  //   Read RAM
  //   Latch Instruction and Data
  //   Load B Register from Bus
  //   Set Carry
  //   Carry FF
endmodule
