// Digital circuit spider011.dig as structural Verilog
module spider011 (
  input  clk,
  input  in_2,
  input  in_3,
  input  in_4,
  input  in_5,
  input  in_6,
  input  in_7
);

  wire A, AC1, AC2, AC3, AC4, AC5, AC6, AC7, AC8, AC9, AC10, AC11, AC12, AC13, AC14, AC15, ADD, AND,
       and_1_out, and_5_out, Aout, Bout, BUS0, BUS1, BUS2, BUS3, BUS4, BUS5, BUS6, BUS7, BUS8, BUS9, BUS10,
       BUS11, BUS12, BUS13, BUS14, BUS15, button_1_out, C, Cin, CLA, CLR, Cout, diodebackward_1_out,
       diodebackward_3_out, diodebackward_7_out, diodeforward_1_out, F, Fout, GCLK, I0, I1, I2, I3, I4, I5,
       I6, I7, INCPC, LDA, LOAD, MAR0, MAR1, MAR2, MAR3, MAR4, MAR5, MAR6, MAR7, MAR8, MAR9, MAR10, MAR11,
       MAR12, MAR13, MAR14, MAR15, monoflop_1_nq, nA, nand_1_out, nand_2_out, nand_5_out, nand_6_out,
       nand_8_out, nand_9_out, nand_10_out, nand_11_out, nand_12_out, nand_13_out, nand_15_out, nand_16_out,
       nand_17_out, nand_18_out, nand_21_out, nB, nCLRPC, nJMP, nLDB, nMBR, nOE, nQ3, nQ4, nRD, nRST, nSEL0,
       nSEL1, nSEL2, nSEL3, nSEL4, nSEL5, nSEL6, nSEL7, nSTEP, nTP0, nTP1, nTP3, nTP4, nTP5, nTP7, nWR, OR,
       PC0, PC1, PC2, PC3, PC4, PC5, PC6, PC7, PC8, PC9, PC10, PC11, PC12, PC13, PC14, PC15, pullup_1_out,
       pullup_3_out, pullup_5_out, pullup_7_out, pullup_8_out, pullup_9_out, Q3, Q4, RAM0, RAM1, RAM2, RAM3,
       RAM4, RAM5, RAM6, RAM7, RAM8, RAM9, RAM10, RAM11, RAM12, RAM13, RAM14, RAM15, RCO, RD, SETC, ST, SUB,
       T0, U3_pin15, U4_pin15, U5_pin15, U8_pin9, U12_pin15, U15_pin9, U16_pin9, U32_pin9, U34_pin9,
       U35_pin9, WR, X0, X1, XOR, xor_1_out, xor_2_out, xor_3_out, xor_4_out, Y12, Y13, Y14, Y15, ZERO;
  wire [2:0] U19_pin14;
  wire [3:0] U15_2_pin6, U15_2_pin13, U16_2_pin6, U16_2_pin10, U17_2_pin3, U17_2_pin13, U18_2_pin6,
       U18_2_pin10, U34_pin4, U34_pin15, U35_pin4, U35_pin15;

  _74161 U3 (
    .pin1(nCLRPC), .pin2(INCPC), .pin3(BUS0), .pin4(BUS1), .pin5(BUS2), .pin6(BUS3), .pin7(1'b1),
    .pin8(1'b0), .pin9(nJMP), .pin10(1'b1), .pin11(PC3), .pin12(PC2), .pin13(PC1), .pin14(PC0),
    .pin15(U3_pin15), .pin16(1'b1));
  _74161 U4 (
    .pin1(nCLRPC), .pin2(INCPC), .pin3(BUS4), .pin4(BUS5), .pin5(BUS6), .pin6(BUS7), .pin7(1'b1),
    .pin8(1'b0), .pin9(nJMP), .pin10(U3_pin15), .pin11(PC7), .pin12(PC6), .pin13(PC5), .pin14(PC4),
    .pin15(U4_pin15), .pin16(1'b1));
  _74161 U5 (
    .pin1(nCLRPC), .pin2(INCPC), .pin3(BUS8), .pin4(BUS9), .pin5(BUS10), .pin6(BUS11), .pin7(1'b1),
    .pin8(1'b0), .pin9(in_2), .pin10(U4_pin15), .pin11(PC11), .pin12(PC10), .pin13(PC9), .pin14(PC8),
    .pin15(U5_pin15), .pin16(1'b1));
  _74161 U6 (
    .pin1(nCLRPC), .pin2(INCPC), .pin3(in_3), .pin4(in_4), .pin5(in_5), .pin6(in_6), .pin7(1'b1),
    .pin8(1'b0), .pin9(in_2), .pin10(U5_pin15), .pin11(PC15), .pin12(PC14), .pin13(PC13), .pin14(PC12),
    .pin16(1'b1));  // open: pin15
  _74595 U8 (
    .pin1(MAR14), .pin2(MAR13), .pin3(MAR12), .pin4(MAR11), .pin5(MAR10), .pin6(MAR9), .pin7(MAR8),
    .pin8(1'b0), .pin9(U8_pin9), .pin10(nTP7), .pin11(GCLK), .pin12(T0), .pin13(1'b0), .pin14(Fout),
    .pin15(MAR15), .pin16(1'b1));
  _74595 U9 (
    .pin1(MAR6), .pin2(MAR5), .pin3(MAR4), .pin4(MAR3), .pin5(MAR2), .pin6(MAR1), .pin7(MAR0), .pin8(1'b0),
    .pin9(nMBR), .pin10(nTP7), .pin11(GCLK), .pin12(T0), .pin13(1'b0), .pin14(U8_pin9), .pin15(MAR7),
    .pin16(1'b1));
  // _62256 U11: pin names not known; wires that end beside it: MAR14, MAR12, MAR7, MAR6, MAR5, MAR4, MAR3, MAR2, MAR1, MAR0, BUS8, BUS9
  // _62256 U10: pin names not known; wires that end beside it: BUS10, 1'b0, MAR14, MAR12, MAR7, MAR6, MAR5, MAR4, MAR3, MAR2, MAR1, MAR0, BUS0, BUS1, BUS2, 1'b0, 1'b1, nWR, MAR13, MAR8, MAR9, MAR11, nRD, MAR10, 1'b1, BUS7
  // _27C1024 U1: pin names not known; wires that end beside it: PC9, PC10, PC11, PC12, PC13, PC14, PC15, 1'b1, BUS3, BUS4, BUS5, BUS6, BUS7, 1'b0, BUS8, BUS9, BUS10, BUS11, BUS12, BUS13, BUS14, BUS15, 1'b0, 1'b1, 1'b1, nWR, MAR13, MAR8, MAR9, MAR11, nRD, MAR10, 1'b1, BUS15, BUS14, BUS13, BUS12, nCLRPC
  _74157 U17 (
    .pin1(I7), .pin2(BUS12), .pin3(1'b0), .pin4(Y12), .pin5(BUS13), .pin6(1'b0), .pin7(Y13), .pin8(1'b0),
    .pin9(Y14), .pin10(1'b0), .pin11(BUS14), .pin12(Y15), .pin13(1'b0), .pin14(BUS15), .pin15(1'b0),
    .pin16(1'b1));
  and and_1 (and_1_out, nCLRPC, nCLRPC);
  _74138 U12 (
    .pin1(I4), .pin2(I5), .pin3(I6), .pin4(1'b0), .pin5(1'b0), .pin6(I7), .pin7(nJMP), .pin8(1'b0),
    .pin9(ST), .pin10(SUB), .pin11(ADD), .pin12(XOR), .pin13(OR), .pin14(AND), .pin15(U12_pin15), .pin16(1'b1));
  _74138 U7 (
    .pin1(I0), .pin2(I1), .pin3(I2), .pin4(1'b0), .pin5(1'b0), .pin6(1'b1), .pin7(nSEL7), .pin8(1'b0),
    .pin9(nSEL6), .pin10(nSEL5), .pin11(nSEL4), .pin12(nSEL3), .pin13(nSEL2), .pin14(nSEL1), .pin15(nSEL0),
    .pin16(1'b1));
  and and_2 (LOAD, I7, U12_pin15);
  _74164 U13 (
    .pin1(1'b1), .pin2(Fout), .pin3(AC15), .pin4(AC14), .pin5(AC13), .pin6(AC12), .pin7(1'b0), .pin8(GCLK),
    .pin9(and_1_out), .pin10(AC11), .pin11(AC10), .pin12(AC9), .pin13(AC8), .pin14(1'b1));
  PullUp pullup_1 (.out(pullup_1_out));
  DiodeBackward diodebackward_1 (.in(LOAD), .out(diodebackward_1_out));
  DiodeBackward diodebackward_2 (.in(ST), .out(pullup_1_out));
  Seven_Seg_Hex seven_seg_hex_1 (.d({AC15, AC14, AC13, AC12}), .dp(1'b0));
  PullUp pullup_2 (.out(diodebackward_1_out));
  DiodeBackward diodebackward_3 (.in(LOAD), .out(diodebackward_3_out));
  Seven_Seg_Hex seven_seg_hex_2 (.d({AC11, AC10, AC9, AC8}), .dp(1'b0));
  _74165 U15 (
    .pin1(nLDB), .pin2(GCLK), .pin3(BUS11), .pin4(BUS10), .pin5(BUS9), .pin6(BUS8), .pin8(1'b0),
    .pin9(U15_pin9), .pin10(1'b0), .pin11(Y15), .pin12(Y14), .pin13(Y13), .pin14(Y12), .pin15(1'b0),
    .pin16(1'b1));  // open: pin7
  PullUp pullup_3 (.out(pullup_3_out));
  PullUp pullup_4 (.out(diodebackward_3_out));
  DiodeBackward diodebackward_4 (.in(LOAD), .out(pullup_3_out));
  DiodeBackward diodebackward_5 (.in(ADD), .out(pullup_3_out));
  DiodeBackward diodebackward_6 (.in(SUB), .out(pullup_3_out));
  Seven_Seg_Hex seven_seg_hex_3 (.d({AC7, AC6, AC5, AC4}), .dp(1'b0));
  PullUp pullup_5 (.out(pullup_5_out));
  DiodeBackward diodebackward_7 (.in(SUB), .out(diodebackward_7_out));
  DiodeBackward diodebackward_8 (.in(SUB), .out(pullup_5_out));
  Seven_Seg_Hex seven_seg_hex_4 (.d({AC3, AC2, AC1, A}), .dp(1'b0));
  PullUp pullup_6 (.out(diodebackward_7_out));
  _74164 U14 (
    .pin1(1'b1), .pin2(AC8), .pin3(AC7), .pin4(AC6), .pin5(AC5), .pin6(AC4), .pin7(1'b0), .pin8(GCLK),
    .pin9(and_1_out), .pin10(AC3), .pin11(AC2), .pin12(AC1), .pin13(A), .pin14(1'b1));
  PullUp pullup_7 (.out(pullup_7_out));
  PullUp pullup_8 (.out(pullup_8_out));
  DiodeBackward diodebackward_9 (.in(AND), .out(pullup_8_out));
  DiodeBackward diodebackward_10 (.in(OR), .out(pullup_8_out));
  DiodeBackward diodebackward_11 (.in(nJMP), .out(pullup_8_out));
  _74165 U16 (
    .pin1(nLDB), .pin2(GCLK), .pin3(BUS3), .pin4(BUS2), .pin5(BUS1), .pin6(BUS0), .pin8(1'b0),
    .pin9(U16_pin9), .pin10(U15_pin9), .pin11(BUS7), .pin12(BUS6), .pin13(BUS5), .pin14(BUS4), .pin15(1'b0),
    .pin16(1'b1));  // open: pin7
  PullUp pullup_9 (.out(pullup_9_out));
  DiodeBackward diodebackward_12 (.in(LOAD), .out(pullup_9_out));
  DiodeBackward diodebackward_13 (.in(OR), .out(pullup_9_out));
  DiodeBackward diodebackward_14 (.in(XOR), .out(pullup_9_out));
  DiodeBackward diodebackward_15 (.in(ADD), .out(pullup_9_out));
  DiodeBackward diodebackward_16 (.in(SUB), .out(pullup_9_out));
  DiodeBackward diodebackward_17 (.in(ST), .out(pullup_9_out));
  DiodeBackward diodebackward_18 (.in(nJMP), .out(pullup_9_out));
  not not_1 (WR, pullup_1_out);
  _74540 U18 (
    .pin1(1'b0), .pin2(pullup_9_out), .pin3(pullup_8_out), .pin4(pullup_7_out), .pin5(diodebackward_7_out),
    .pin6(pullup_5_out), .pin7(pullup_3_out), .pin8(diodebackward_3_out), .pin9(diodebackward_1_out),
    .pin10(1'b0), .pin11(RD), .pin12(CLA), .pin13(F), .pin14(C), .pin15(nB), .pin16(nA), .pin17(X1),
    .pin18(X0), .pin19(1'b0), .pin20(1'b1));
  and and_3 (Aout, LOAD, A);
  DiodeForward diodeforward_1 (.in(AC15), .out(diodeforward_1_out));
  DiodeForward diodeforward_2 (.in(AC14), .out(diodeforward_1_out));
  DiodeForward diodeforward_3 (.in(AC13), .out(diodeforward_1_out));
  DiodeForward diodeforward_4 (.in(AC12), .out(diodeforward_1_out));
  DiodeForward diodeforward_5 (.in(AC11), .out(diodeforward_1_out));
  DiodeForward diodeforward_6 (.in(AC10), .out(diodeforward_1_out));
  DiodeForward diodeforward_7 (.in(AC9), .out(diodeforward_1_out));
  DiodeForward diodeforward_8 (.in(AC8), .out(diodeforward_1_out));
  DiodeForward diodeforward_9 (.in(AC7), .out(diodeforward_1_out));
  DiodeForward diodeforward_10 (.in(AC6), .out(diodeforward_1_out));
  DiodeForward diodeforward_11 (.in(AC5), .out(diodeforward_1_out));
  DiodeForward diodeforward_12 (.in(AC4), .out(diodeforward_1_out));
  DiodeForward diodeforward_13 (.in(AC3), .out(diodeforward_1_out));
  DiodeForward diodeforward_14 (.in(AC2), .out(diodeforward_1_out));
  DiodeForward diodeforward_15 (.in(AC1), .out(diodeforward_1_out));
  DiodeForward diodeforward_16 (.in(A), .out(diodeforward_1_out));
  and and_4 (Bout, nJMP, U16_pin9);
  PullDown pulldown_1 (.out(diodeforward_1_out));
  LED led_1 (.in(ZERO));
  not not_2 (ZERO, diodeforward_1_out);
  _74574 U2 (
    .pin1(1'b0), .pin2(BUS8), .pin3(BUS9), .pin4(BUS10), .pin5(BUS11), .pin6(BUS12), .pin7(BUS13),
    .pin8(BUS14), .pin9(BUS15), .pin10(1'b0), .pin11(nTP4), .pin12(I7), .pin13(I6), .pin14(I5), .pin15(I4),
    .pin16(I3), .pin17(I2), .pin18(I1), .pin19(I0), .pin20(1'b1));
  _74595 U32 (
    .pin1(BUS14), .pin2(BUS13), .pin3(BUS12), .pin4(BUS11), .pin5(BUS10), .pin6(BUS9), .pin7(BUS8),
    .pin8(1'b0), .pin9(U32_pin9), .pin10(nTP7), .pin11(GCLK), .pin12(T0), .pin13(1'b1), .pin14(nMBR),
    .pin15(BUS15), .pin16(1'b1));
  _74595 U33 (
    .pin1(BUS6), .pin2(BUS5), .pin3(BUS4), .pin4(BUS3), .pin5(BUS2), .pin6(BUS1), .pin7(BUS0), .pin8(1'b0),
    .pin10(nTP7), .pin11(GCLK), .pin12(T0), .pin13(1'b1), .pin14(U32_pin9), .pin15(BUS7), .pin16(1'b1));  // open: pin9
  not not_3 (LDA, nLDB);
  not not_4 (SETC, nTP7);
  not not_5 (nQ3, Q3);
  not not_6 (nQ4, Q4);
  not not_7 (T0, nRST);
  and and_5 (and_5_out, nTP0, nWR);
  _74574 _74574_1 (
    .pin1(1'b0), .pin2(BUS15), .pin3(BUS14), .pin4(BUS13), .pin5(BUS12), .pin6(BUS11), .pin7(BUS10),
    .pin8(BUS9), .pin9(BUS8), .pin10(1'b0), .pin11(nTP4), .pin12(MAR8), .pin13(MAR9), .pin14(MAR10),
    .pin15(MAR11), .pin16(MAR12), .pin17(MAR13), .pin18(MAR14), .pin19(MAR15), .pin20(1'b1));
  _74574 _74574_2 (
    .pin1(1'b0), .pin2(BUS7), .pin3(BUS6), .pin4(BUS5), .pin5(BUS4), .pin6(BUS3), .pin7(BUS2), .pin8(BUS1),
    .pin9(BUS0), .pin10(1'b0), .pin11(nTP4), .pin12(MAR0), .pin13(MAR1), .pin14(MAR2), .pin15(MAR3),
    .pin16(MAR4), .pin17(MAR5), .pin18(MAR6), .pin19(MAR7), .pin20(1'b1));
  _74161 U19 (
    .pin1(nRST), .pin2(clk), .pin3(1'b0), .pin4(1'b0), .pin5(1'b0), .pin6(1'b0), .pin7(1'b1), .pin8(1'b0),
    .pin9(1'b1), .pin10(1'b1), .pin11(Q3), .pin12(U19_pin14[2]), .pin13(U19_pin14[1]), .pin14(U19_pin14[0]),
    .pin15(RCO), .pin16(1'b1));
  _74161 U20 (
    .pin1(nRST), .pin2(clk), .pin3(1'b0), .pin4(1'b0), .pin5(1'b0), .pin6(1'b0), .pin7(1'b1), .pin8(1'b0),
    .pin9(1'b1), .pin10(RCO), .pin14(Q4), .pin16(1'b1));  // open: pin11, pin12, pin13, pin15
  Reset reset_1 (.out(nCLRPC));
  _74574 _74574_3 (
    .pin1(1'b0), .pin2(MAR15), .pin3(MAR14), .pin4(MAR13), .pin5(MAR12), .pin6(MAR11), .pin7(MAR10),
    .pin8(MAR9), .pin9(MAR8), .pin10(1'b0), .pin11(nTP4), .pin12(RAM8), .pin13(RAM9), .pin14(RAM10),
    .pin15(RAM11), .pin16(RAM12), .pin17(RAM13), .pin18(RAM14), .pin19(RAM15), .pin20(1'b1));
  _74574 _74574_4 (
    .pin1(1'b0), .pin2(MAR7), .pin3(MAR6), .pin4(MAR5), .pin5(MAR4), .pin6(MAR3), .pin7(MAR2), .pin8(MAR1),
    .pin9(MAR0), .pin10(1'b0), .pin11(nTP4), .pin12(RAM0), .pin13(RAM1), .pin14(RAM2), .pin15(RAM3),
    .pin16(RAM4), .pin17(RAM5), .pin18(RAM6), .pin19(RAM7), .pin20(1'b1));
  Seven_Seg_Hex seven_seg_hex_5 (.d({3'b000, Q4}), .dp(1'b0));
  Seven_Seg_Hex seven_seg_hex_6 (.d({MAR15, MAR14, MAR13, MAR12}), .dp(1'b0));
  Seven_Seg_Hex seven_seg_hex_7 (.d({Q3, U19_pin14}), .dp(1'b0));
  _74138 U21 (
    .pin1(U19_pin14[0]), .pin2(U19_pin14[1]), .pin3(U19_pin14[2]), .pin4(Q3), .pin5(Q4), .pin6(1'b1),
    .pin7(nTP7), .pin8(1'b0), .pin9(nLDB), .pin10(nTP5), .pin11(nTP4), .pin12(nTP3), .pin13(INCPC),
    .pin14(nTP1), .pin15(nTP0), .pin16(1'b1));
  Seven_Seg_Hex seven_seg_hex_8 (.d({MAR11, MAR10, MAR9, MAR8}), .dp(1'b0));
  Seven_Seg_Hex seven_seg_hex_9 (.d({MAR7, MAR6, MAR5, MAR4}), .dp(1'b0));
  Seven_Seg_Hex seven_seg_hex_10 (.d({MAR3, MAR2, MAR1, MAR0}), .dp(1'b0));
  nand nand_1 (nand_1_out, clk, clk);
  nand nand_2 (nand_2_out, nQ3, nQ4);
  nand nand_3 (nRST, Q3, Q4);
  xor xor_1 (xor_1_out, Aout, nA);
  xor xor_2 (xor_2_out, nB, Bout);
  nand nand_4 (CLR, CLA, LDA);
  nand nand_5 (nand_5_out, C, C);
  nand nand_6 (nand_6_out, C, SETC);
  nand nand_7 (GCLK, nand_1_out, nand_2_out);
  xor xor_3 (xor_3_out, xor_1_out, xor_2_out);
  nand nand_8 (nand_8_out, LDA, nand_5_out);
  Seven_Seg_Hex seven_seg_hex_11 (.d({PC15, PC14, PC13, PC12}), .dp(1'b0));
  LED TP0 (.in(nTP0));
  LED TP1 (.in(nTP1));
  LED TP2 (.in(INCPC));
  LED TP3 (.in(nTP3));
  LED TP4 (.in(nTP4));
  LED TP5 (.in(nTP5));
  LED TP6 (.in(nLDB));
  LED TP7 (.in(nTP7));
  Seven_Seg_Hex seven_seg_hex_12 (.d({PC11, PC10, PC9, PC8}), .dp(1'b0));
  xor xor_4 (xor_4_out, xor_3_out, Cin);
  nand nand_9 (nand_9_out, xor_3_out, Cin);
  nand nand_10 (nand_10_out, xor_1_out, xor_2_out);
  Seven_Seg_Hex seven_seg_hex_13 (.d({PC7, PC6, PC5, PC4}), .dp(1'b0));
  Seven_Seg_Hex seven_seg_hex_14 (.d({PC3, PC2, PC1, PC0}), .dp(1'b0));
  nand nand_11 (nand_11_out, nTP0, nand_12_out);
  nand nand_12 (nand_12_out, nand_11_out, INCPC);
  nand nand_13 (nand_13_out, nTP3, nOE);
  nand nand_14 (nOE, nand_13_out, nTP5);
  nand nand_15 (nand_15_out, nand_9_out, nand_10_out);
  Button button_1 (.out(button_1_out));
  Monoflop monoflop_1 (.C(button_1_out), .R(1'b0), .nQ(monoflop_1_nq));  // open: Q
  nand nand_16 (nand_16_out, xor_4_out, X0);
  nand nand_17 (nand_17_out, X1, nand_15_out);
  nand nand_18 (nand_18_out, nand_15_out, F);
  Seven_Seg_Hex seven_seg_hex_15 (.d({BUS15, BUS14, BUS13, BUS12}), .dp(1'b0));
  Seven_Seg_Hex seven_seg_hex_16 (.d({BUS11, BUS10, BUS9, BUS8}), .dp(1'b0));
  nand nand_19 (nRD, RD, nand_11_out);
  nand nand_20 (nWR, WR, nand_11_out);
  nand nand_21 (nand_21_out, nRST, nSTEP);
  nand nand_22 (nSTEP, nand_21_out, monoflop_1_nq);
  nand nand_23 (Fout, nand_16_out, nand_17_out);
  nand nand_24 (Cout, nand_18_out, nand_18_out);
  Seven_Seg_Hex seven_seg_hex_17 (.d({BUS7, BUS6, BUS5, BUS4}), .dp(1'b0));
  Seven_Seg_Hex seven_seg_hex_18 (.d({BUS3, BUS2, BUS1, BUS0}), .dp(1'b0));
  _7474 U23 (
    .pin1(nand_8_out), .pin2(Cout), .pin3(GCLK), .pin4(nand_6_out), .pin5(Cin), .pin7(1'b0), .pin10(1'b1),
    .pin11(1'b1), .pin12(1'b1), .pin13(1'b1), .pin14(1'b1));  // open: pin6, pin8, pin9
  _74595 U34 (
    .pin1(U34_pin15[2]), .pin2(U34_pin15[1]), .pin3(U34_pin15[0]), .pin4(U34_pin4[3]), .pin5(U34_pin4[2]),
    .pin6(U34_pin4[1]), .pin7(U34_pin4[0]), .pin8(1'b0), .pin9(U34_pin9), .pin10(nTP7), .pin11(GCLK),
    .pin12(T0), .pin13(1'b0), .pin14(nMBR), .pin15(U34_pin15[3]), .pin16(1'b1));
  _74164 U15_2 (
    .pin1(1'b1), .pin2(A), .pin3(U15_2_pin6[3]), .pin4(U15_2_pin6[2]), .pin5(U15_2_pin6[1]),
    .pin6(U15_2_pin6[0]), .pin7(1'b0), .pin8(GCLK), .pin9(nCLRPC), .pin10(U15_2_pin13[3]),
    .pin11(U15_2_pin13[2]), .pin12(U15_2_pin13[1]), .pin13(U15_2_pin13[0]), .pin14(1'b1));
  Seven_Seg_Hex seven_seg_hex_19 (.d(U15_2_pin6), .dp(1'b0));
  Seven_Seg_Hex seven_seg_hex_20 (.d(U15_2_pin13), .dp(1'b0));
  Seven_Seg_Hex seven_seg_hex_21 (.d(U16_2_pin6), .dp(1'b0));
  _74595 U35 (
    .pin1(U35_pin15[2]), .pin2(U35_pin15[1]), .pin3(U35_pin15[0]), .pin4(U35_pin4[3]), .pin5(U35_pin4[2]),
    .pin6(U35_pin4[1]), .pin7(U35_pin4[0]), .pin8(1'b0), .pin9(U35_pin9), .pin10(nTP7), .pin11(GCLK),
    .pin12(T0), .pin13(1'b0), .pin14(U34_pin9), .pin15(U35_pin15[3]), .pin16(1'b1));
  Seven_Seg_Hex seven_seg_hex_22 (.d(U16_2_pin10), .dp(1'b0));
  _74164 U16_2 (
    .pin1(1'b1), .pin2(U15_2_pin13[0]), .pin3(U16_2_pin6[3]), .pin4(U16_2_pin6[2]), .pin5(U16_2_pin6[1]),
    .pin6(U16_2_pin6[0]), .pin7(1'b0), .pin8(GCLK), .pin9(nCLRPC), .pin10(U16_2_pin10[3]),
    .pin11(U16_2_pin10[2]), .pin12(U16_2_pin10[1]), .pin13(U16_2_pin10[0]), .pin14(1'b1));
  Seven_Seg_Hex seven_seg_hex_23 (.d(U34_pin15), .dp(1'b0));
  Seven_Seg_Hex seven_seg_hex_24 (.d(U34_pin4), .dp(1'b0));
  Seven_Seg_Hex seven_seg_hex_25 (.d(U35_pin15), .dp(1'b0));
  Seven_Seg_Hex seven_seg_hex_26 (.d(U35_pin4), .dp(1'b0));
  _74164 U17_2 (
    .pin1(1'b1), .pin2(U16_2_pin10[0]), .pin3(U17_2_pin3[3]), .pin4(U17_2_pin3[2]), .pin5(U17_2_pin3[1]),
    .pin6(U17_2_pin3[0]), .pin7(1'b0), .pin8(GCLK), .pin9(nCLRPC), .pin10(U17_2_pin13[3]),
    .pin11(U17_2_pin13[2]), .pin12(U17_2_pin13[1]), .pin13(U17_2_pin13[0]), .pin14(1'b1));
  Seven_Seg_Hex seven_seg_hex_27 (.d(U17_2_pin3), .dp(1'b0));
  Seven_Seg_Hex seven_seg_hex_28 (.d(U17_2_pin13), .dp(1'b0));
  Seven_Seg_Hex seven_seg_hex_29 (.d(U18_2_pin6), .dp(1'b0));
  Seven_Seg_Hex seven_seg_hex_30 (.d(U18_2_pin10), .dp(1'b0));
  _74164 U18_2 (
    .pin1(1'b1), .pin2(U17_2_pin13[0]), .pin3(U18_2_pin6[3]), .pin4(U18_2_pin6[2]), .pin5(U18_2_pin6[1]),
    .pin6(U18_2_pin6[0]), .pin7(1'b0), .pin8(GCLK), .pin9(nCLRPC), .pin10(U18_2_pin10[3]),
    .pin11(U18_2_pin10[2]), .pin12(U18_2_pin10[1]), .pin13(U18_2_pin10[0]), .pin14(1'b1));

  // Other names for the same wires on the sheet: AC0 = A; nPCEN = in_7; nPH = in_2; nPL = nJMP; nTP2 = INCPC;
  //   nTP6 = nLDB; RES = nTP7

  // Notes on the sheet:
  //   clk: Hz: 24
  //   in_2: default 1
  //   Spider 011 16-bit serial CPU Testbed
  //   Memory Address Register
  //   RAM HI
  //   RAM LO
  //   ACCUMULATOR
  //   B Shift Register
  //   Instruction Decoder
  //   Mask Instruction Field
  //   U31B
  //   U31A
  //   WR
  //   CLA
  //   RD
  //   F
  //   C
  //   ~B
  //   I1
  //   ~A
  //   I0
  //   U30F
  //   LOAD
  //   AND
  //   OR
  //   XOR
  //   ADD
  //   SUB
  //   STORE
  //   JMP
  //   Zero A for
  //   Load instructions
  //   U31C
  //   Zero B for
  //   Jump instructions
  //   Instruction Latch
  //   Memory Buffer Register
  //   U30
  //   74HC04
  //   U31D
  //   Clock Sequencer
  //   Note Clock Inverted
  //   RAM ADDRESS (MAR)
  //   # Clock
  //   U24, U25, U26
  //   U27
  //   U28
  //   U24A
  //   U24B
  //   U27D
  //   U27A
  //   U27B
  //   ROM ADDRESS (PC)
  //   U24C
  //   U27C
  //   CLR ACC
  //   Carry is only set before Bit 0 of an operation
  //   Any residual carry is cleared before an operation
  //   Bit Serial ALU
  //   U24D
  //   U25D
  //   U25C
  //   Latch Result
  //   Write Result to RAM
  //   Increment PC
  //   Read Instruction from ROM
  //   Latch Instruction and MAR Address/Data
  //   Load B Register from Bus
  //   Set Carry
  //   U22
  //   U25B
  //   U26B
  //   U26C
  //   U26A
  //   Suppress Carry
  //   BUS DATA
  //   U29
  //   U26D
  //   U25A
  //   Carry FF
  //   OUTPUT REGISTER
endmodule
