// Digital circuit spider02.dig as structural Verilog
module spider02 (
  input  clk,
  input  in_3,
  input  in_4,
  input  in_5,
  input  nCE,
  input  nOE,
  input  nWE,
  input  nSW,
  output Fout
);

  wire A0, A1, A2, A3, A4, A5, A6, A7, A8, A9, A10, A11, A12, A13, A14, A15, ADD, AND, Aout, Bout, BUS0,
       BUS1, BUS2, BUS3, BUS4, BUS5, BUS6, BUS7, button_1_out, button_2_out, button_3_out, button_4_out,
       button_5_out, button_6_out, button_7_out, button_8_out, button_9_out, button_10_out, button_11_out,
       button_12_out, button_13_out, button_14_out, button_15_out, button_16_out, button_17_out,
       button_18_out, C, Cin, CLA, CLR, Cout, D0, D1, D2, D3, D4, D5, D6, D7, D8, D9, D10, D11, D12, D13,
       D14, D15, d_ff_1_nq, d_ff_2_nq, d_ff_3_nq, d_ff_4_nq, d_ff_5_nq, d_ff_6_nq, d_ff_7_nq, d_ff_8_nq,
       d_ff_9_nq, d_ff_10_nq, d_ff_11_nq, d_ff_12_nq, diodebackward_2_out, diodebackward_6_out,
       diodebackward_8_out, diodebackward_10_out, diodeforward_1_out, F, GCLK, I0, I1, IC16_2_nq, IC16_nq,
       IC17_2_nq, IC17_nq, IX, LD, LOAD, nA, nand_2_out, nand_3_out, nand_5_out, nand_6_out, nand_7_out,
       nand_8_out, nand_11_out, nand_12_out, nand_13_out, nand_14_out, nand_15_out, nB, nCLRPC, nJMP, nLD,
       nZERO, OR, pullup_1_out, pullup_4_out, pullup_5_out, RES, RST, SETC, ST, SUB, T0, U3_pin9, U7_pin15,
       U8_pin9, U9_pin9, U10_pin9, U11_pin9, XOR, xor_1_out, xor_2_out, xor_3_out, xor_4_out;
  wire [3:0] _74541_1_pin5, _74541_1_pin9, _74541_2_pin4, _74541_2_pin6, U5_pin6, U5_pin13, U6_pin6,
       U7_pin11, U8_pin3, U8_pin7;
  wire [3:1] U6_pin10;

  _74138 U1 (
    .pin1(in_3), .pin2(in_4), .pin3(in_5), .pin4(1'b0), .pin5(1'b0), .pin6(1'b1), .pin7(nJMP), .pin8(1'b0),
    .pin9(ST), .pin10(SUB), .pin11(ADD), .pin12(XOR), .pin13(OR), .pin14(AND), .pin15(LOAD), .pin16(1'b1));
  PullUp pullup_1 (.out(pullup_1_out));
  DiodeBackward diodebackward_1 (.in(LOAD), .out(pullup_1_out));
  DiodeBackward diodebackward_2 (.in(LOAD), .out(diodebackward_2_out));
  DiodeBackward diodebackward_3 (.in(ADD), .out(diodebackward_2_out));
  DiodeBackward diodebackward_4 (.in(SUB), .out(diodebackward_2_out));
  DiodeBackward diodebackward_5 (.in(nJMP), .out(diodebackward_2_out));
  PullUp pullup_2 (.out(diodebackward_2_out));
  DiodeBackward diodebackward_6 (.in(SUB), .out(diodebackward_6_out));
  PullUp pullup_3 (.out(diodebackward_6_out));
  PullUp pullup_4 (.out(pullup_4_out));
  DiodeBackward diodebackward_7 (.in(SUB), .out(pullup_4_out));
  PullUp pullup_5 (.out(pullup_5_out));
  DiodeBackward diodebackward_8 (.in(AND), .out(diodebackward_8_out));
  DiodeBackward diodebackward_9 (.in(OR), .out(diodebackward_8_out));
  PullUp pullup_6 (.out(diodebackward_8_out));
  DiodeBackward diodebackward_10 (.in(LOAD), .out(diodebackward_10_out));
  DiodeBackward diodebackward_11 (.in(OR), .out(diodebackward_10_out));
  DiodeBackward diodebackward_12 (.in(XOR), .out(diodebackward_10_out));
  DiodeBackward diodebackward_13 (.in(ADD), .out(diodebackward_10_out));
  DiodeBackward diodebackward_14 (.in(SUB), .out(diodebackward_10_out));
  DiodeBackward diodebackward_15 (.in(ST), .out(diodebackward_10_out));
  PullUp pullup_7 (.out(diodebackward_10_out));
  _74540 U2 (
    .pin1(1'b0), .pin2(diodebackward_10_out), .pin3(diodebackward_8_out), .pin4(pullup_5_out),
    .pin5(pullup_4_out), .pin6(diodebackward_6_out), .pin7(diodebackward_2_out), .pin8(pullup_1_out),
    .pin9(1'b0), .pin10(1'b0), .pin12(CLA), .pin13(F), .pin14(C), .pin15(nB), .pin16(nA), .pin17(I1),
    .pin18(I0), .pin19(1'b0), .pin20(1'b1));  // open: pin11
  LED led_1 (.in(_74541_1_pin5[3]));
  D_FF IC17 (.D(IC17_nq), .C(button_1_out), .Q(_74541_1_pin5[3]), .nQ(IC17_nq));
  _74165 U3 (
    .pin1(LD), .pin2(GCLK), .pin3(D11), .pin4(D10), .pin5(D9), .pin6(D8), .pin8(1'b0), .pin9(U3_pin9),
    .pin10(1'b0), .pin11(D15), .pin12(D14), .pin13(D13), .pin14(D12), .pin15(1'b0), .pin16(1'b1));  // open: pin7
  LED led_2 (.in(_74541_1_pin5[2]));
  D_FF d_ff_1 (.D(d_ff_1_nq), .C(button_2_out), .Q(_74541_1_pin5[2]), .nQ(d_ff_1_nq));
  Button button_1 (.out(button_1_out));
  _74541 _74541_1 (
    .pin1(1'b0), .pin2(_74541_1_pin5[3]), .pin3(_74541_1_pin5[2]), .pin4(_74541_1_pin5[1]),
    .pin5(_74541_1_pin5[0]), .pin6(_74541_1_pin9[3]), .pin7(_74541_1_pin9[2]), .pin8(_74541_1_pin9[1]),
    .pin9(_74541_1_pin9[0]), .pin10(1'b0), .pin11(D8), .pin12(D9), .pin13(D10), .pin14(D11), .pin15(D12),
    .pin16(D13), .pin17(D14), .pin18(D15), .pin19(nSW), .pin20(1'b1));
  LED led_3 (.in(_74541_1_pin5[1]));
  D_FF d_ff_2 (.D(d_ff_2_nq), .C(button_3_out), .Q(_74541_1_pin5[1]), .nQ(d_ff_2_nq));
  Button button_2 (.out(button_2_out));
  LED led_4 (.in(_74541_1_pin5[0]));
  D_FF d_ff_3 (.D(d_ff_3_nq), .C(button_4_out), .Q(_74541_1_pin5[0]), .nQ(d_ff_3_nq));
  Button button_3 (.out(button_3_out));
  _74595 U8 (
    .pin1(U8_pin3[2]), .pin2(U8_pin3[1]), .pin3(U8_pin3[0]), .pin4(U8_pin7[3]), .pin5(U8_pin7[2]),
    .pin6(U8_pin7[1]), .pin7(U8_pin7[0]), .pin8(1'b0), .pin9(U8_pin9), .pin10(RES), .pin11(GCLK), .pin12(T0),
    .pin13(1'b0), .pin14(Fout), .pin15(U8_pin3[3]), .pin16(1'b1));
  LED led_5 (.in(_74541_1_pin9[3]));
  D_FF d_ff_4 (.D(d_ff_4_nq), .C(button_5_out), .Q(_74541_1_pin9[3]), .nQ(d_ff_4_nq));
  Button button_4 (.out(button_4_out));
  LED led_6 (.in(_74541_1_pin9[2]));
  D_FF d_ff_5 (.D(d_ff_5_nq), .C(button_6_out), .Q(_74541_1_pin9[2]), .nQ(d_ff_5_nq));
  Button button_5 (.out(button_5_out));
  LED led_7 (.in(_74541_1_pin9[1]));
  D_FF d_ff_6 (.D(d_ff_6_nq), .C(button_7_out), .Q(_74541_1_pin9[1]), .nQ(d_ff_6_nq));
  Button button_6 (.out(button_6_out));
  _74165 U4 (
    .pin1(LD), .pin2(GCLK), .pin3(D3), .pin4(D2), .pin5(D1), .pin6(D0), .pin8(1'b0), .pin9(Bout),
    .pin10(U3_pin9), .pin11(D7), .pin12(D6), .pin13(D5), .pin14(D4), .pin15(1'b0), .pin16(1'b1));  // open: pin7
  LED led_8 (.in(_74541_1_pin9[0]));
  D_FF IC17_2 (.D(IC17_2_nq), .C(button_8_out), .Q(_74541_1_pin9[0]), .nQ(IC17_2_nq));
  Button button_7 (.out(button_7_out));
  Button button_8 (.out(button_8_out));
  _74595 U9 (
    .pin1(BUS6), .pin2(BUS5), .pin3(BUS4), .pin4(BUS3), .pin5(BUS2), .pin6(BUS1), .pin7(BUS0), .pin8(1'b0),
    .pin9(U9_pin9), .pin10(RES), .pin11(GCLK), .pin12(T0), .pin13(1'b0), .pin14(U8_pin9), .pin15(BUS7),
    .pin16(1'b1));
  Seven_Seg_Hex seven_seg_hex_1 (.d(_74541_1_pin5), .dp(1'b0));
  Seven_Seg_Hex seven_seg_hex_2 (.d(_74541_1_pin9), .dp(1'b0));
  LED led_9 (.in(_74541_2_pin4[3]));
  D_FF IC16 (.D(IC16_nq), .C(button_9_out), .Q(_74541_2_pin4[3]), .nQ(IC16_nq));
  Button button_9 (.out(button_9_out));
  DiodeForward diodeforward_1 (.in(U8_pin3[3]), .out(diodeforward_1_out));
  DiodeForward diodeforward_2 (.in(U8_pin3[2]), .out(diodeforward_1_out));
  DiodeForward diodeforward_3 (.in(U8_pin3[1]), .out(diodeforward_1_out));
  DiodeForward diodeforward_4 (.in(U8_pin3[0]), .out(diodeforward_1_out));
  DiodeForward diodeforward_5 (.in(U8_pin7[3]), .out(diodeforward_1_out));
  DiodeForward diodeforward_6 (.in(U8_pin7[2]), .out(diodeforward_1_out));
  DiodeForward diodeforward_7 (.in(U8_pin7[1]), .out(diodeforward_1_out));
  DiodeForward diodeforward_8 (.in(U8_pin7[0]), .out(diodeforward_1_out));
  DiodeForward diodeforward_9 (.in(BUS7), .out(diodeforward_1_out));
  DiodeForward diodeforward_10 (.in(BUS6), .out(diodeforward_1_out));
  DiodeForward diodeforward_11 (.in(BUS5), .out(diodeforward_1_out));
  DiodeForward diodeforward_12 (.in(BUS4), .out(diodeforward_1_out));
  DiodeForward diodeforward_13 (.in(BUS3), .out(diodeforward_1_out));
  DiodeForward diodeforward_14 (.in(BUS2), .out(diodeforward_1_out));
  DiodeForward diodeforward_15 (.in(BUS1), .out(diodeforward_1_out));
  DiodeForward diodeforward_16 (.in(BUS0), .out(diodeforward_1_out));
  LED led_10 (.in(_74541_2_pin4[2]));
  D_FF d_ff_7 (.D(d_ff_7_nq), .C(button_10_out), .Q(_74541_2_pin4[2]), .nQ(d_ff_7_nq));
  Button button_10 (.out(button_10_out));
  Seven_Seg_Hex seven_seg_hex_3 (.d(U8_pin3), .dp(1'b0));
  LED led_11 (.in(diodeforward_1_out));
  PullDown pulldown_1 (.out(diodeforward_1_out));
  _74541 _74541_2 (
    .pin1(1'b0), .pin2(_74541_2_pin4[3]), .pin3(_74541_2_pin4[2]), .pin4(_74541_2_pin4[1]),
    .pin5(_74541_2_pin4[0]), .pin6(_74541_2_pin6[3]), .pin7(_74541_2_pin6[2]), .pin8(_74541_2_pin6[1]),
    .pin9(_74541_2_pin6[0]), .pin10(1'b0), .pin11(D0), .pin12(D1), .pin13(D2), .pin14(D3), .pin15(D4),
    .pin16(D5), .pin17(D6), .pin18(D7), .pin19(nSW), .pin20(1'b1));
  LED led_12 (.in(_74541_2_pin4[1]));
  D_FF d_ff_8 (.D(d_ff_8_nq), .C(button_11_out), .Q(_74541_2_pin4[1]), .nQ(d_ff_8_nq));
  Button button_11 (.out(button_11_out));
  Seven_Seg_Hex seven_seg_hex_4 (.d(U8_pin7), .dp(1'b0));
  nand nand_1 (nZERO, diodeforward_1_out, diodeforward_1_out);
  _74164 U5 (
    .pin1(1'b1), .pin2(Fout), .pin3(U5_pin6[3]), .pin4(U5_pin6[2]), .pin5(U5_pin6[1]), .pin6(U5_pin6[0]),
    .pin7(1'b0), .pin8(GCLK), .pin9(CLR), .pin10(U5_pin13[3]), .pin11(U5_pin13[2]), .pin12(U5_pin13[1]),
    .pin13(U5_pin13[0]), .pin14(1'b1));
  LED led_13 (.in(_74541_2_pin4[0]));
  D_FF d_ff_9 (.D(d_ff_9_nq), .C(button_12_out), .Q(_74541_2_pin4[0]), .nQ(d_ff_9_nq));
  Button button_12 (.out(button_12_out));
  Seven_Seg_Hex seven_seg_hex_5 (.d({BUS7, BUS6, BUS5, BUS4}), .dp(1'b0));
  LED led_14 (.in(_74541_2_pin6[3]));
  D_FF d_ff_10 (.D(d_ff_10_nq), .C(button_13_out), .Q(_74541_2_pin6[3]), .nQ(d_ff_10_nq));
  Button button_13 (.out(button_13_out));
  Seven_Seg_Hex seven_seg_hex_6 (.d({BUS3, BUS2, BUS1, BUS0}), .dp(1'b0));
  LED led_15 (.in(_74541_2_pin6[2]));
  D_FF d_ff_11 (.D(d_ff_11_nq), .C(button_14_out), .Q(_74541_2_pin6[2]), .nQ(d_ff_11_nq));
  Button button_14 (.out(button_14_out));
  Seven_Seg_Hex seven_seg_hex_7 (.d(U5_pin6), .dp(1'b0));
  LED led_16 (.in(_74541_2_pin6[1]));
  D_FF d_ff_12 (.D(d_ff_12_nq), .C(button_15_out), .Q(_74541_2_pin6[1]), .nQ(d_ff_12_nq));
  Button button_15 (.out(button_15_out));
  Seven_Seg_Hex seven_seg_hex_8 (.d(U5_pin13), .dp(1'b0));
  LED led_17 (.in(_74541_2_pin6[0]));
  D_FF IC16_2 (.D(IC16_2_nq), .C(button_16_out), .Q(_74541_2_pin6[0]), .nQ(IC16_2_nq));
  Button button_16 (.out(button_16_out));
  _74595 U10 (
    .pin1(A14), .pin2(A13), .pin3(A12), .pin4(A10), .pin5(A11), .pin6(A9), .pin7(A8), .pin8(1'b0),
    .pin9(U10_pin9), .pin10(RES), .pin11(GCLK), .pin12(T0), .pin13(1'b0), .pin14(U9_pin9), .pin15(A15),
    .pin16(1'b1));
  Seven_Seg_Hex seven_seg_hex_9 (.d(U6_pin6), .dp(1'b0));
  Seven_Seg_Hex seven_seg_hex_10 (.d(_74541_2_pin4), .dp(1'b0));
  Seven_Seg_Hex seven_seg_hex_11 (.d({U6_pin10, Aout}), .dp(1'b0));
  Seven_Seg_Hex seven_seg_hex_12 (.d(_74541_2_pin6), .dp(1'b0));
  _74164 U6 (
    .pin1(1'b1), .pin2(U5_pin13[0]), .pin3(U6_pin6[3]), .pin4(U6_pin6[2]), .pin5(U6_pin6[1]),
    .pin6(U6_pin6[0]), .pin7(1'b0), .pin8(GCLK), .pin9(CLR), .pin10(U6_pin10[3]), .pin11(U6_pin10[2]),
    .pin12(U6_pin10[1]), .pin13(Aout), .pin14(1'b1));
  Monoflop monoflop_1 (.C(button_17_out), .R(1'b0), .Q(nLD), .nQ(LD));
  Button button_17 (.out(button_17_out));
  _74595 U11 (
    .pin1(A6), .pin2(A5), .pin3(A4), .pin4(A3), .pin5(A2), .pin6(A1), .pin7(A0), .pin8(1'b0),
    .pin9(U11_pin9), .pin10(RES), .pin11(GCLK), .pin12(T0), .pin13(1'b0), .pin14(U10_pin9), .pin15(A7),
    .pin16(1'b1));
  Monoflop monoflop_2 (.C(LD), .R(1'b0), .Q(SETC), .nQ(RES));
  _74161 U7 (
    .pin1(RST), .pin2(clk), .pin3(1'b0), .pin4(1'b0), .pin5(1'b0), .pin6(1'b0), .pin7(1'b1), .pin8(1'b0),
    .pin9(1'b1), .pin10(1'b1), .pin11(U7_pin11[3]), .pin12(U7_pin11[2]), .pin13(U7_pin11[1]),
    .pin14(U7_pin11[0]), .pin15(U7_pin15), .pin16(1'b1));
  Monoflop monoflop_3 (.C(button_18_out), .R(1'b0), .nQ(nCLRPC));  // open: Q
  Button button_18 (.out(button_18_out));
  Seven_Seg_Hex seven_seg_hex_13 (.d({A15, A14, A13, A12}), .dp(1'b0));
  Seven_Seg_Hex seven_seg_hex_14 (.d({A10, A11, A9, A8}), .dp(1'b0));
  nand nand_2 (nand_2_out, SETC, C);
  nand nand_3 (nand_3_out, C, C);
  nand nand_4 (CLR, CLA, nLD);
  Seven_Seg_Hex seven_seg_hex_15 (.d({A7, A6, A5, A4}), .dp(1'b0));
  Seven_Seg_Hex seven_seg_hex_16 (.d(U7_pin11), .dp(1'b0));
  Seven_Seg_Hex seven_seg_hex_17 (.d({A3, A2, A1, A0}), .dp(1'b0));
  xor xor_1 (xor_1_out, Aout, nA);
  xor xor_2 (xor_2_out, nB, Bout);
  nand nand_5 (nand_5_out, nand_3_out, nLD);
  xor xor_3 (xor_3_out, xor_1_out, xor_2_out);
  Seven_Seg_Hex seven_seg_hex_18 (.d({D15, D14, D13, D12}), .dp(1'b0));
  nand nand_6 (nand_6_out, clk, clk);
  Seven_Seg_Hex seven_seg_hex_19 (.d({D11, D10, D9, D8}), .dp(1'b0));
  xor xor_4 (xor_4_out, xor_3_out, Cin);
  nand nand_7 (nand_7_out, xor_3_out, Cin);
  nand nand_8 (nand_8_out, xor_1_out, xor_2_out);
  Seven_Seg_Hex seven_seg_hex_20 (.d({D7, D6, D5, D4}), .dp(1'b0));
  nand nand_9 (GCLK, nand_6_out, RST);
  nand nand_10 (RST, RES, nand_11_out);
  nand nand_11 (nand_11_out, RST, T0);
  Seven_Seg_Hex seven_seg_hex_21 (.d({D3, D2, D1, D0}), .dp(1'b0));
  nand nand_12 (nand_12_out, nand_7_out, nand_8_out);
  // _62256 _62256_1: pin names not known; wires that end beside it: A14, A12, A7, A6, A5, A4, A3, A2, A1, A0, D8, 1'b1, nWE, A13, A8, A9, A11, nOE, A10, nCE, D15
  // _62256 _62256_2: pin names not known; wires that end beside it: D9, D10, 1'b0, A14, A12, A7, A6, A5, A4, A3, A2, A1, A0, D0, D1, D2, 1'b0, D11, 1'b1, nWE, A13, A8, A9, A11, nOE, A10, nCE, D7
  nand nand_13 (nand_13_out, xor_4_out, I0);
  nand nand_14 (nand_14_out, I1, nand_12_out);
  nand nand_15 (nand_15_out, nand_12_out, F);
  _7474 _7474_1 (
    .pin1(1'b1), .pin2(U7_pin15), .pin3(clk), .pin4(1'b1), .pin5(IX), .pin6(T0), .pin7(1'b0), .pin9(Cin),
    .pin10(nand_2_out), .pin11(GCLK), .pin12(Cout), .pin13(nand_5_out), .pin14(1'b1));  // open: pin8
  nand nand_16 (Fout, nand_13_out, nand_14_out);
  nand nand_17 (Cout, nand_15_out, nand_15_out);

  // Notes on the sheet:
  //   clk: Hz: 1000
  //   nCE: default 1
  //   nOE: default 1
  //   nWE: default 1
  //   spider-00
  //   Instruction Input
  //   Spider_0 Bit serial CPU Testbed
  //   Instruction Decode
  //   CLA
  //   F
  //   ~B
  //   C
  //   ~A
  //   I1
  //   I0
  //   LOAD
  //   AND
  //   OR
  //   XOR
  //   ADD
  //   SUB
  //   STORE
  //   JMP
  //   16 bit Shift Register B "BUS"
  //   ENTER H
  //   Output Display Registers
  //   Data Input
  //   OUTPUT REGISTER
  //   16 bit Shift Register A "ACCUMULATOR"
  //   ENTER L
  //   ACCUMULATOR
  //   STEP/RUN
  //   CLR PC
  //   ADDRESS REGISTER
  //   Bit Serial ALU
  //   Clock Sequencer
  //   CLR ACC
  //   # Clock
  //   Carry is only set before Bit 0 of an operation
  //   Any residual carry is cleared before an operation
  //   DATA BUS
  //   Suppress Carry
  //   Carry FF
endmodule
