// Digital circuit spider04.dig as structural Verilog
module spider04 (
  input  clk,
  input  in_3,
  input  in_4,
  input  in_5,
  output Fout
);

  wire _0_out, _1_out, _2_out, _3_out, _4_out, _5_out, _6_out, _7_out, _8_out, _9_out, _74139_2_pin5,
       _74139_2_pin6, _74163_1_pin14, _74173_4_pin11, _74173_4_pin12, _74173_4_pin13, _74173_4_pin14,
       _74193_1_pin12, _74193_1_pin13, _74193_2_pin12, _74193_2_pin13, _74193_3_pin12, _74193_3_pin13,
       _74540_1_pin11, _74540_1_pin12, _74540_1_pin13, _74540_1_pin14, _74540_1_pin15, _74540_1_pin16,
       _74540_1_pin17, A0, A1, A2, A3, A4, A5, A6, A7, A8, A9, A10, A11, A12, A13, A14, A15, A_out, ACC0,
       ACC1, ACC2, ACC3, ACC4, ACC5, ACC6, ACC7, ACC8, ACC9, ACC10, ACC11, ACC12, ACC13, ACC14, ACC15, ADD,
       Address_out, ALU, ALU_to_RAM_out, AND, Aout, B_out, Bout, BUS0, BUS1, BUS2, BUS3, BUS4, BUS5, BUS6,
       BUS7, BUS8, BUS9, BUS10, BUS11, BUS12, BUS13, BUS14, BUS15, button_1_out, button_2_out, button_3_out,
       button_4_out, button_5_out, button_6_out, button_7_out, button_8_out, button_9_out, button_10_out,
       button_11_out, button_12_out, button_13_out, button_14_out, button_15_out, button_16_out,
       button_17_out, button_18_out, C, C_out, Cin, CLA, Clear_out, CLKIR, CLR, CLR4017, Cout, D0, D1, D2,
       D3, D4, D5, D6, D7, D8, D9, D10, D11, D12, D13, D14, D15, d_ff_1_nq, d_ff_2_nq, d_ff_3_nq, d_ff_4_nq,
       d_ff_5_nq, d_ff_6_nq, d_ff_7_nq, d_ff_8_nq, d_ff_9_nq, d_ff_10_nq, d_ff_11_nq, d_ff_12_nq, D_out,
       Dec_out, Deposit_nWR_out, diodebackward_1_out, diodebackward_2_out, diodebackward_5_out,
       diodebackward_10_out, diodebackward_14_out, diodebackward_31_out, diodebackward_46_out,
       diodebackward_63_out, diodebackward_67_out, diodebackward_69_out, diodebackward_71_out,
       diodeforward_1_out, diodeforward_4_out, DN, E_out, Examine_nRD_out, F, F_out, GCLK, I0, I1, IC16_2_nq,
       IC16_nq, IC17_2_nq, IC17_nq, Inc_out, IR0, IR1, IR2, IR3, IR4, IR5, IR6, IR7, IX, LOAD, nA, nALB,
       nand_3_out, nand_4_out, nand_5_out, nand_7_out, nand_8_out, nand_10_out, nand_11_out, nand_12_out,
       nand_13_out, nand_16_out, nand_17_out, nand_18_out, nand_19_out, nand_20_out, nB, nCLRPC, nDE, nJMP,
       nLATCH, nLD, nLDA, nLDB, nOE, not_9_out, not_10_out, not_11_out, not_12_out, not_13_out, not_14_out,
       not_15_out, not_16_out, not_17_out, not_18_out, not_19_out, not_20_out, not_21_out, not_22_out,
       nRAMOE, nRAMWE, nWE, nZERO, OR, pullup_3_out, pullup_4_out, pullup_7_out, pullup_8_out, pullup_10_out,
       pullup_11_out, pullup_14_out, pullup_17_out, pullup_18_out, Q0, Q1, Q2, Q3, Q4, Q5, Q6, Q7, Q8, Q9,
       Q10, Q11, Q12, Q13, Q14, Q15, RES, RESET, RST, SETC, ST, SUB, T0, TP0, TP2, TP3, TP20, U3_pin9,
       U7_2_pin15, U7_pin1, U7_pin11, U7_pin12, U7_pin13, U7_pin14, U7_pin15, U8_2_pin9, U9_2_pin9, U9_pin12,
       U9_pin13, U9_pin14, U9_pin15, U9_pin16, U9_pin17, U9_pin18, U9_pin19, UP, XOR, xor_2_out, xor_3_out,
       xor_4_out, xor_5_out;
  wire [3:0] U5_pin6, U5_pin13, U6_pin6, U7_2_pin11;
  wire [3:1] U6_pin10;

  DiodeBackward diodebackward_1 (.in(Address_out), .out(diodebackward_1_out));
  PullUp pullup_1 (.out(diodebackward_1_out));
  DiodeBackward diodebackward_2 (.in(Dec_out), .out(diodebackward_2_out));
  not not_1 (nLD, _74540_1_pin11);
  PullUp pullup_2 (.out(diodebackward_2_out));
  PullUp pullup_3 (.out(pullup_3_out));
  DiodeBackward diodebackward_3 (.in(Inc_out), .out(pullup_3_out));
  _74139 _74139_1 (
    .pin1(1'b1), .pin2(1'b1), .pin3(1'b1), .pin8(1'b0), .pin11(nALB), .pin12(nDE), .pin13(1'b0), .pin14(ALU),
    .pin15(nWE), .pin16(1'b1));  // open: pin4, pin5, pin6, pin7, pin9, pin10
  PullUp pullup_4 (.out(pullup_4_out));
  DiodeBackward diodebackward_4 (.in(ALU_to_RAM_out), .out(pullup_4_out));
  DiodeBackward diodebackward_5 (.in(Examine_nRD_out), .out(diodebackward_5_out));
  DiodeBackward diodebackward_6 (.in(Examine_nRD_out), .out(pullup_4_out));
  DiodeBackward diodebackward_7 (.in(Deposit_nWR_out), .out(diodebackward_5_out));
  DiodeBackward diodebackward_8 (.in(Dec_out), .out(pullup_4_out));
  DiodeBackward diodebackward_9 (.in(Inc_out), .out(pullup_4_out));
  not not_2 (ALU, _74540_1_pin15);
  PullUp pullup_5 (.out(diodebackward_5_out));
  DiodeBackward diodebackward_10 (.in(ALU_to_RAM_out), .out(diodebackward_10_out));
  DiodeBackward diodebackward_11 (.in(Deposit_nWR_out), .out(diodebackward_10_out));
  not not_3 (nRAMOE, _74540_1_pin17);
  not not_4 (nRAMWE, _74540_1_pin16);
  nand nand_1 (UP, _74540_1_pin13, _74540_1_pin14);
  nand nand_2 (DN, _74540_1_pin12, _74540_1_pin14);
  PullUp pullup_6 (.out(diodebackward_10_out));
  PullUp pullup_7 (.out(pullup_7_out));
  DiodeBackward diodebackward_12 (.in(Examine_nRD_out), .out(pullup_7_out));
  PullUp pullup_8 (.out(pullup_8_out));
  DiodeBackward diodebackward_13 (.in(Clear_out), .out(pullup_8_out));
  _74540 _74540_1 (
    .pin1(1'b0), .pin2(pullup_8_out), .pin3(pullup_7_out), .pin4(diodebackward_10_out),
    .pin5(diodebackward_5_out), .pin6(pullup_4_out), .pin7(pullup_3_out), .pin8(diodebackward_2_out),
    .pin9(diodebackward_1_out), .pin10(1'b0), .pin11(_74540_1_pin11), .pin12(_74540_1_pin12),
    .pin13(_74540_1_pin13), .pin14(_74540_1_pin14), .pin15(_74540_1_pin15), .pin16(_74540_1_pin16),
    .pin17(_74540_1_pin17), .pin18(RESET), .pin19(1'b0), .pin20(1'b1));
  Button #(.activeLow("true")) ALU_to_RAM (.out(ALU_to_RAM_out));
  Button #(.activeLow("true")) Clear (.out(Clear_out));
  Button #(.activeLow("true")) Examine_nRD (.out(Examine_nRD_out));
  Button #(.activeLow("true")) Deposit_nWR (.out(Deposit_nWR_out));
  Button #(.activeLow("true")) Dec (.out(Dec_out));
  Button #(.activeLow("true")) Inc (.out(Inc_out));
  Button #(.activeLow("true")) Address (.out(Address_out));
  _74173 _74173_1 (
    .pin1(1'b0), .pin2(1'b0), .pin3(A12), .pin4(A13), .pin5(A14), .pin6(A15), .pin7(nLATCH), .pin8(1'b0),
    .pin9(1'b0), .pin10(1'b0), .pin11(A11), .pin12(A10), .pin13(A9), .pin14(A8), .pin15(1'b0), .pin16(1'b1));
  Seven_Seg_Hex seven_seg_hex_1 (.d({A15, A14, A13, A12}), .dp(1'b0));
  Seven_Seg_Hex seven_seg_hex_2 (.d({A11, A10, A9, A8}), .dp(1'b0));
  Seven_Seg_Hex seven_seg_hex_3 (.d({A7, A6, A5, A4}), .dp(1'b0));
  _74173 _74173_2 (
    .pin1(1'b0), .pin2(1'b0), .pin3(A8), .pin4(A9), .pin5(A10), .pin6(A11), .pin7(nLATCH), .pin8(1'b0),
    .pin9(1'b0), .pin10(1'b0), .pin11(A7), .pin12(A6), .pin13(A5), .pin14(A4), .pin15(1'b0), .pin16(1'b1));
  Seven_Seg_Hex seven_seg_hex_4 (.d({A3, A2, A1, A0}), .dp(1'b0));
  Button #(.activeLow("true")) u_C (.out(C_out));
  Button #(.activeLow("true")) _8 (.out(_8_out));
  Button #(.activeLow("true")) _4 (.out(_4_out));
  Button #(.activeLow("true")) _0 (.out(_0_out));
  Button #(.activeLow("true")) D (.out(D_out));
  Button #(.activeLow("true")) _9 (.out(_9_out));
  Button #(.activeLow("true")) _5 (.out(_5_out));
  Button #(.activeLow("true")) _1 (.out(_1_out));
  Seven_Seg_Hex seven_seg_hex_5 (.d({Q15, Q14, Q13, Q12}), .dp(1'b0));
  Seven_Seg_Hex seven_seg_hex_6 (.d({Q11, Q10, Q9, Q8}), .dp(1'b0));
  Button #(.activeLow("true")) E (.out(E_out));
  Button #(.activeLow("true")) A (.out(A_out));
  Button #(.activeLow("true")) _6 (.out(_6_out));
  Button #(.activeLow("true")) _2 (.out(_2_out));
  _74173 _74173_3 (
    .pin1(1'b0), .pin2(1'b0), .pin3(A4), .pin4(A5), .pin5(A6), .pin6(A7), .pin7(nLATCH), .pin8(1'b0),
    .pin9(1'b0), .pin10(1'b0), .pin11(A3), .pin12(A2), .pin13(A1), .pin14(A0), .pin15(1'b0), .pin16(1'b1));
  Seven_Seg_Hex seven_seg_hex_7 (.d({Q7, Q6, Q5, Q4}), .dp(1'b0));
  Seven_Seg_Hex seven_seg_hex_8 (.d({Q3, Q2, Q1, Q0}), .dp(1'b0));
  Button #(.activeLow("true")) u_F (.out(F_out));
  Button #(.activeLow("true")) B (.out(B_out));
  Button #(.activeLow("true")) _7 (.out(_7_out));
  Button #(.activeLow("true")) _3 (.out(_3_out));
  _74173 _74173_4 (
    .pin1(1'b0), .pin2(1'b0), .pin3(A0), .pin4(A1), .pin5(A2), .pin6(A3), .pin7(nLATCH), .pin8(1'b0),
    .pin9(1'b0), .pin10(1'b0), .pin11(_74173_4_pin11), .pin12(_74173_4_pin12), .pin13(_74173_4_pin13),
    .pin14(_74173_4_pin14), .pin15(1'b0), .pin16(1'b1));
  Seven_Seg_Hex seven_seg_hex_9 (.d({BUS15, BUS14, BUS13, BUS12}), .dp(1'b0));
  DiodeBackward diodebackward_14 (.in(F_out), .out(diodebackward_14_out));
  DiodeBackward diodebackward_15 (.in(E_out), .out(diodebackward_14_out));
  DiodeBackward diodebackward_16 (.in(D_out), .out(diodebackward_14_out));
  DiodeBackward diodebackward_17 (.in(C_out), .out(diodebackward_14_out));
  DiodeBackward diodebackward_18 (.in(B_out), .out(diodebackward_14_out));
  DiodeBackward diodebackward_19 (.in(A_out), .out(diodebackward_14_out));
  DiodeBackward diodebackward_20 (.in(_9_out), .out(diodebackward_14_out));
  DiodeBackward diodebackward_21 (.in(_8_out), .out(diodebackward_14_out));
  Seven_Seg_Hex seven_seg_hex_10 (.d({BUS11, BUS10, BUS9, BUS8}), .dp(1'b0));
  PullUp pullup_9 (.out(diodebackward_14_out));
  PullUp pullup_10 (.out(pullup_10_out));
  DiodeBackward diodebackward_22 (.in(F_out), .out(pullup_10_out));
  DiodeBackward diodebackward_23 (.in(E_out), .out(pullup_10_out));
  DiodeBackward diodebackward_24 (.in(D_out), .out(pullup_10_out));
  DiodeBackward diodebackward_25 (.in(C_out), .out(pullup_10_out));
  DiodeBackward diodebackward_26 (.in(_7_out), .out(pullup_10_out));
  DiodeBackward diodebackward_27 (.in(_6_out), .out(pullup_10_out));
  DiodeBackward diodebackward_28 (.in(_5_out), .out(pullup_10_out));
  DiodeBackward diodebackward_29 (.in(_4_out), .out(pullup_10_out));
  not not_5 (_74173_4_pin12, pullup_10_out);
  not not_6 (_74173_4_pin11, diodebackward_14_out);
  Seven_Seg_Hex seven_seg_hex_11 (.d({BUS7, BUS6, BUS5, BUS4}), .dp(1'b0));
  PullUp pullup_11 (.out(pullup_11_out));
  DiodeBackward diodebackward_30 (.in(F_out), .out(pullup_11_out));
  DiodeBackward diodebackward_31 (.in(F_out), .out(diodebackward_31_out));
  DiodeBackward diodebackward_32 (.in(E_out), .out(pullup_11_out));
  DiodeBackward diodebackward_33 (.in(D_out), .out(diodebackward_31_out));
  DiodeBackward diodebackward_34 (.in(B_out), .out(pullup_11_out));
  DiodeBackward diodebackward_35 (.in(B_out), .out(diodebackward_31_out));
  DiodeBackward diodebackward_36 (.in(A_out), .out(pullup_11_out));
  DiodeBackward diodebackward_37 (.in(_9_out), .out(diodebackward_31_out));
  DiodeBackward diodebackward_38 (.in(_7_out), .out(pullup_11_out));
  DiodeBackward diodebackward_39 (.in(_7_out), .out(diodebackward_31_out));
  DiodeBackward diodebackward_40 (.in(_6_out), .out(pullup_11_out));
  DiodeBackward diodebackward_41 (.in(_5_out), .out(diodebackward_31_out));
  DiodeBackward diodebackward_42 (.in(_3_out), .out(pullup_11_out));
  DiodeBackward diodebackward_43 (.in(_3_out), .out(diodebackward_31_out));
  DiodeBackward diodebackward_44 (.in(_2_out), .out(pullup_11_out));
  DiodeBackward diodebackward_45 (.in(_1_out), .out(diodebackward_31_out));
  not not_7 (_74173_4_pin13, pullup_11_out);
  Seven_Seg_Hex seven_seg_hex_12 (.d({BUS3, BUS2, BUS1, BUS0}), .dp(1'b0));
  PullUp pullup_12 (.out(diodebackward_31_out));
  DiodeBackward diodebackward_46 (.in(F_out), .out(diodebackward_46_out));
  DiodeBackward diodebackward_47 (.in(E_out), .out(diodebackward_46_out));
  DiodeBackward diodebackward_48 (.in(D_out), .out(diodebackward_46_out));
  DiodeBackward diodebackward_49 (.in(C_out), .out(diodebackward_46_out));
  DiodeBackward diodebackward_50 (.in(B_out), .out(diodebackward_46_out));
  DiodeBackward diodebackward_51 (.in(A_out), .out(diodebackward_46_out));
  DiodeBackward diodebackward_52 (.in(_9_out), .out(diodebackward_46_out));
  DiodeBackward diodebackward_53 (.in(_8_out), .out(diodebackward_46_out));
  DiodeBackward diodebackward_54 (.in(_7_out), .out(diodebackward_46_out));
  DiodeBackward diodebackward_55 (.in(_6_out), .out(diodebackward_46_out));
  DiodeBackward diodebackward_56 (.in(_5_out), .out(diodebackward_46_out));
  DiodeBackward diodebackward_57 (.in(_4_out), .out(diodebackward_46_out));
  DiodeBackward diodebackward_58 (.in(_3_out), .out(diodebackward_46_out));
  DiodeBackward diodebackward_59 (.in(_2_out), .out(diodebackward_46_out));
  DiodeBackward diodebackward_60 (.in(_1_out), .out(diodebackward_46_out));
  DiodeBackward diodebackward_61 (.in(_0_out), .out(diodebackward_46_out));
  not not_8 (_74173_4_pin14, diodebackward_31_out);
  PullUp pullup_13 (.out(diodebackward_46_out));
  not not_9 (not_9_out, diodebackward_46_out);
  Monoflop monoflop_1 (.C(not_9_out), .R(1'b0), .nQ(nLATCH));  // open: Q
  LED led_1 (.in(nLATCH));
  _74193 _74193_1 (
    .pin1(A1), .pin2(Q1), .pin3(Q0), .pin4(DN), .pin5(UP), .pin6(Q2), .pin7(Q3), .pin8(1'b0), .pin9(A3),
    .pin10(A2), .pin11(nLD), .pin12(_74193_1_pin12), .pin13(_74193_1_pin13), .pin14(RESET), .pin15(A0),
    .pin16(1'b1));
  _74193 _74193_2 (
    .pin1(A5), .pin2(Q5), .pin3(Q4), .pin4(_74193_1_pin13), .pin5(_74193_1_pin12), .pin6(Q6), .pin7(Q7),
    .pin8(1'b0), .pin9(A7), .pin10(A6), .pin11(nLD), .pin12(_74193_2_pin12), .pin13(_74193_2_pin13),
    .pin14(RESET), .pin15(A4), .pin16(1'b1));
  _74193 _74193_3 (
    .pin1(A9), .pin2(Q9), .pin3(Q8), .pin4(_74193_2_pin13), .pin5(_74193_2_pin12), .pin6(Q10), .pin7(Q11),
    .pin8(1'b0), .pin9(A11), .pin10(A10), .pin11(nLD), .pin12(_74193_3_pin12), .pin13(_74193_3_pin13),
    .pin14(RESET), .pin15(A8), .pin16(1'b1));
  _74193 _74193_4 (
    .pin1(A13), .pin2(Q13), .pin3(Q12), .pin4(_74193_3_pin13), .pin5(_74193_3_pin12), .pin6(Q14), .pin7(Q15),
    .pin8(1'b0), .pin9(A15), .pin10(A14), .pin11(nLD), .pin14(RESET), .pin15(A12), .pin16(1'b1));  // open: pin12, pin13
  // _62256 _62256_1: pin names not known; wires that end beside it: Q14, Q12, Q7, Q6, Q5, Q4, Q3, Q2, Q1, Q0, BUS8, BUS9, BUS10, 1'b0, 1'b1, nWE, Q13, Q8, Q9, Q11, nOE, Q10, 1'b0, BUS15
  _74541 _74541_1 (
    .pin1(nDE), .pin2(A15), .pin3(A14), .pin4(A13), .pin5(A12), .pin6(A11), .pin7(A10), .pin8(A9), .pin9(A8),
    .pin10(1'b0), .pin11(BUS8), .pin12(BUS9), .pin13(BUS10), .pin14(BUS11), .pin15(BUS12), .pin16(BUS13),
    .pin17(BUS14), .pin18(BUS15), .pin19(nDE), .pin20(1'b1));
  // _62256 _62256_2: pin names not known; wires that end beside it: Q14, Q12, Q7, Q6, Q5, Q4, Q3, Q2, Q1, Q0, BUS0, BUS1, BUS2, 1'b0, 1'b1, nWE, Q13, Q8, Q9, Q11, nOE, Q10, 1'b0, BUS7
  _74541 _74541_2 (
    .pin1(nDE), .pin2(A7), .pin3(A6), .pin4(A5), .pin5(A4), .pin6(A3), .pin7(A2), .pin8(A1), .pin9(A0),
    .pin10(1'b0), .pin11(BUS0), .pin12(BUS1), .pin13(BUS2), .pin14(BUS3), .pin15(BUS4), .pin16(BUS5),
    .pin17(BUS6), .pin18(BUS7), .pin19(nDE), .pin20(1'b1));
  and and_1 (nWE, nRAMWE, TP20);
  and and_2 (nOE, nRAMOE, TP0);
  _74574 U8 (
    .pin1(1'b0), .pin2(BUS8), .pin3(BUS9), .pin4(BUS10), .pin5(BUS11), .pin6(BUS12), .pin7(BUS13),
    .pin8(BUS14), .pin9(BUS15), .pin10(1'b0), .pin11(CLKIR), .pin12(IR7), .pin13(IR6), .pin14(IR5),
    .pin15(IR4), .pin16(IR3), .pin17(IR2), .pin18(IR1), .pin19(IR0), .pin20(1'b1));
  _74574 U9 (
    .pin1(1'b0), .pin2(BUS0), .pin3(BUS1), .pin4(BUS2), .pin5(BUS3), .pin6(BUS4), .pin7(BUS5), .pin8(BUS6),
    .pin9(BUS7), .pin10(1'b0), .pin11(CLKIR), .pin12(U9_pin12), .pin13(U9_pin13), .pin14(U9_pin14),
    .pin15(U9_pin15), .pin16(U9_pin16), .pin17(U9_pin17), .pin18(U9_pin18), .pin19(U9_pin19), .pin20(1'b1));
  _74541 U10 (
    .pin1(nDE), .pin2(U9_pin19), .pin3(U9_pin18), .pin4(U9_pin17), .pin5(U9_pin16), .pin6(U9_pin15),
    .pin7(U9_pin14), .pin8(U9_pin13), .pin9(U9_pin12), .pin10(1'b0), .pin11(BUS7), .pin12(BUS6),
    .pin13(BUS5), .pin14(BUS4), .pin15(BUS3), .pin16(BUS2), .pin17(BUS1), .pin18(BUS0), .pin19(nDE),
    .pin20(1'b1));
  not not_10 (not_10_out, nOE);
  not not_11 (not_11_out, CLKIR);
  not not_12 (not_12_out, LOAD);
  not not_13 (not_13_out, AND);
  not not_14 (not_14_out, OR);
  not not_15 (not_15_out, XOR);
  not not_16 (not_16_out, ADD);
  not not_17 (not_17_out, SUB);
  not not_18 (not_18_out, ST);
  not not_19 (not_19_out, nJMP);
  not not_20 (not_20_out, nWE);
  not not_21 (not_21_out, UP);
  LED RAM_RD (.in(not_10_out));
  LED CLK_IR (.in(not_11_out));
  LED u_LOAD (.in(not_12_out));
  LED AND_3 (.in(not_13_out));
  LED u_OR (.in(not_14_out));
  LED u_XOR (.in(not_15_out));
  LED u_ADD (.in(not_16_out));
  LED u_SUB (.in(not_17_out));
  LED STORE (.in(not_18_out));
  LED JUMP (.in(not_19_out));
  LED RAM_WR (.in(not_20_out));
  LED INC_PC (.in(not_21_out));
  _74163 U7 (
    .pin1(U7_pin1), .pin2(clk), .pin3(1'b0), .pin4(1'b0), .pin5(1'b0), .pin6(1'b0), .pin7(1'b1), .pin8(1'b0),
    .pin9(1'b1), .pin10(1'b1), .pin11(U7_pin11), .pin12(U7_pin12), .pin13(U7_pin13), .pin14(U7_pin14),
    .pin15(U7_pin15), .pin16(1'b1));
  _74163 _74163_1 (
    .pin1(U7_pin1), .pin2(clk), .pin3(1'b0), .pin4(1'b0), .pin5(1'b0), .pin6(1'b0), .pin7(1'b1), .pin8(1'b0),
    .pin9(1'b1), .pin10(U7_pin15), .pin14(_74163_1_pin14), .pin16(1'b1));  // open: pin11, pin12, pin13, pin15
  LED led_2 (.in(U7_pin11));
  LED led_3 (.in(_74163_1_pin14));
  LED led_4 (.in(U7_pin13));
  LED led_5 (.in(U7_pin12));
  LED led_6 (.in(U7_pin14));
  _74138 U1 (
    .pin1(in_3), .pin2(in_4), .pin3(in_5), .pin4(1'b0), .pin5(1'b0), .pin6(1'b1), .pin7(nJMP), .pin8(1'b0),
    .pin9(ST), .pin10(SUB), .pin11(ADD), .pin12(XOR), .pin13(OR), .pin14(AND), .pin15(LOAD), .pin16(1'b1));
  nand nand_3 (nand_3_out, _74163_1_pin14, U7_pin12);
  DiodeForward diodeforward_1 (.in(U7_pin12), .out(diodeforward_1_out));
  DiodeForward diodeforward_2 (.in(U7_pin11), .out(diodeforward_1_out));
  DiodeForward diodeforward_3 (.in(_74163_1_pin14), .out(diodeforward_1_out));
  PullUp pullup_14 (.out(pullup_14_out));
  DiodeBackward diodebackward_62 (.in(LOAD), .out(pullup_14_out));
  DiodeBackward diodebackward_63 (.in(LOAD), .out(diodebackward_63_out));
  DiodeBackward diodebackward_64 (.in(ADD), .out(diodebackward_63_out));
  DiodeBackward diodebackward_65 (.in(SUB), .out(diodebackward_63_out));
  DiodeBackward diodebackward_66 (.in(nJMP), .out(diodebackward_63_out));
  nand nand_4 (nand_4_out, diodeforward_1_out, diodeforward_1_out);
  PullDown pulldown_1 (.out(diodeforward_1_out));
  PullUp pullup_15 (.out(diodebackward_63_out));
  DiodeBackward diodebackward_67 (.in(SUB), .out(diodebackward_67_out));
  PullUp pullup_16 (.out(diodebackward_67_out));
  PullUp pullup_17 (.out(pullup_17_out));
  DiodeBackward diodebackward_68 (.in(SUB), .out(pullup_17_out));
  nand nand_5 (nand_5_out, nand_4_out, nand_4_out);
  _74139 _74139_2 (
    .pin1(nand_3_out), .pin2(U7_pin14), .pin3(U7_pin13), .pin4(TP20), .pin5(_74139_2_pin5),
    .pin6(_74139_2_pin6), .pin7(U7_pin1), .pin8(1'b0), .pin9(TP3), .pin10(TP2), .pin11(CLKIR), .pin12(TP0),
    .pin13(U7_pin13), .pin14(U7_pin14), .pin15(nand_5_out), .pin16(1'b1));
  PullUp pullup_18 (.out(pullup_18_out));
  DiodeBackward diodebackward_69 (.in(AND), .out(diodebackward_69_out));
  DiodeBackward diodebackward_70 (.in(OR), .out(diodebackward_69_out));
  PullUp pullup_19 (.out(diodebackward_69_out));
  DiodeBackward diodebackward_71 (.in(LOAD), .out(diodebackward_71_out));
  DiodeBackward diodebackward_72 (.in(OR), .out(diodebackward_71_out));
  DiodeBackward diodebackward_73 (.in(XOR), .out(diodebackward_71_out));
  DiodeBackward diodebackward_74 (.in(ADD), .out(diodebackward_71_out));
  DiodeBackward diodebackward_75 (.in(SUB), .out(diodebackward_71_out));
  DiodeBackward diodebackward_76 (.in(ST), .out(diodebackward_71_out));
  PullUp pullup_20 (.out(diodebackward_71_out));
  _74540 U2 (
    .pin1(1'b0), .pin2(diodebackward_71_out), .pin3(diodebackward_69_out), .pin4(pullup_18_out),
    .pin5(pullup_17_out), .pin6(diodebackward_67_out), .pin7(diodebackward_63_out), .pin8(pullup_14_out),
    .pin9(1'b0), .pin10(1'b0), .pin12(CLA), .pin13(F), .pin14(C), .pin15(nB), .pin16(nA), .pin17(I1),
    .pin18(I0), .pin19(1'b0), .pin20(1'b1));  // open: pin11
  LED led_7 (.in(TP0));
  LED led_8 (.in(CLKIR));
  LED led_9 (.in(TP2));
  LED led_10 (.in(TP3));
  LED led_11 (.in(TP20));
  LED led_12 (.in(_74139_2_pin5));
  LED led_13 (.in(_74139_2_pin6));
  LED led_14 (.in(U7_pin1));
  LED led_15 (.in(D15));
  D_FF IC17 (.D(IC17_nq), .C(button_1_out), .Q(D15), .nQ(IC17_nq));
  Button button_1 (.out(button_1_out));
  _74165 U3 (
    .pin1(nLDB), .pin2(GCLK), .pin3(D11), .pin4(D10), .pin5(D9), .pin6(D8), .pin8(1'b0), .pin9(U3_pin9),
    .pin10(1'b0), .pin11(D15), .pin12(D14), .pin13(D13), .pin14(D12), .pin15(1'b0), .pin16(1'b1));  // open: pin7
  LED led_16 (.in(D14));
  D_FF d_ff_1 (.D(d_ff_1_nq), .C(button_2_out), .Q(D14), .nQ(d_ff_1_nq));
  Button button_2 (.out(button_2_out));
  LED led_17 (.in(D13));
  D_FF d_ff_2 (.D(d_ff_2_nq), .C(button_3_out), .Q(D13), .nQ(d_ff_2_nq));
  Button button_3 (.out(button_3_out));
  _74595 U8_2 (
    .pin1(ACC14), .pin2(ACC13), .pin3(ACC12), .pin4(ACC11), .pin5(ACC10), .pin6(ACC9), .pin7(ACC8),
    .pin8(1'b0), .pin9(U8_2_pin9), .pin10(RES), .pin11(GCLK), .pin12(T0), .pin13(1'b0), .pin14(Fout),
    .pin15(ACC15), .pin16(1'b1));
  LED led_18 (.in(D12));
  D_FF d_ff_3 (.D(d_ff_3_nq), .C(button_4_out), .Q(D12), .nQ(d_ff_3_nq));
  Button button_4 (.out(button_4_out));
  LED led_19 (.in(D11));
  D_FF d_ff_4 (.D(d_ff_4_nq), .C(button_5_out), .Q(D11), .nQ(d_ff_4_nq));
  Button button_5 (.out(button_5_out));
  LED led_20 (.in(D10));
  D_FF d_ff_5 (.D(d_ff_5_nq), .C(button_6_out), .Q(D10), .nQ(d_ff_5_nq));
  Button button_6 (.out(button_6_out));
  _74165 U4 (
    .pin1(nLDB), .pin2(GCLK), .pin3(D3), .pin4(D2), .pin5(D1), .pin6(D0), .pin8(1'b0), .pin9(Bout),
    .pin10(U3_pin9), .pin11(D7), .pin12(D6), .pin13(D5), .pin14(D4), .pin15(1'b0), .pin16(1'b1));  // open: pin7
  LED led_21 (.in(D9));
  D_FF d_ff_6 (.D(d_ff_6_nq), .C(button_7_out), .Q(D9), .nQ(d_ff_6_nq));
  Button button_7 (.out(button_7_out));
  LED led_22 (.in(D8));
  D_FF IC17_2 (.D(IC17_2_nq), .C(button_8_out), .Q(D8), .nQ(IC17_2_nq));
  Button button_8 (.out(button_8_out));
  _74595 U9_2 (
    .pin1(ACC6), .pin2(ACC5), .pin3(ACC4), .pin4(ACC3), .pin5(ACC2), .pin6(ACC1), .pin7(ACC0), .pin8(1'b0),
    .pin9(U9_2_pin9), .pin10(RES), .pin11(GCLK), .pin12(T0), .pin13(1'b0), .pin14(U8_2_pin9), .pin15(ACC7),
    .pin16(1'b1));
  Seven_Seg_Hex seven_seg_hex_13 (.d({D15, D14, D13, D12}), .dp(1'b0));
  Seven_Seg_Hex seven_seg_hex_14 (.d({D11, D10, D9, D8}), .dp(1'b0));
  LED led_23 (.in(D7));
  D_FF IC16 (.D(IC16_nq), .C(button_9_out), .Q(D7), .nQ(IC16_nq));
  DiodeForward diodeforward_4 (.in(ACC15), .out(diodeforward_4_out));
  DiodeForward diodeforward_5 (.in(ACC14), .out(diodeforward_4_out));
  DiodeForward diodeforward_6 (.in(ACC13), .out(diodeforward_4_out));
  DiodeForward diodeforward_7 (.in(ACC12), .out(diodeforward_4_out));
  DiodeForward diodeforward_8 (.in(ACC11), .out(diodeforward_4_out));
  DiodeForward diodeforward_9 (.in(ACC10), .out(diodeforward_4_out));
  DiodeForward diodeforward_10 (.in(ACC9), .out(diodeforward_4_out));
  DiodeForward diodeforward_11 (.in(ACC8), .out(diodeforward_4_out));
  DiodeForward diodeforward_12 (.in(ACC7), .out(diodeforward_4_out));
  DiodeForward diodeforward_13 (.in(ACC6), .out(diodeforward_4_out));
  DiodeForward diodeforward_14 (.in(ACC5), .out(diodeforward_4_out));
  DiodeForward diodeforward_15 (.in(ACC4), .out(diodeforward_4_out));
  DiodeForward diodeforward_16 (.in(ACC3), .out(diodeforward_4_out));
  DiodeForward diodeforward_17 (.in(ACC2), .out(diodeforward_4_out));
  DiodeForward diodeforward_18 (.in(ACC1), .out(diodeforward_4_out));
  DiodeForward diodeforward_19 (.in(ACC0), .out(diodeforward_4_out));
  LED led_24 (.in(D6));
  D_FF d_ff_7 (.D(d_ff_7_nq), .C(button_10_out), .Q(D6), .nQ(d_ff_7_nq));
  Button button_9 (.out(button_9_out));
  Seven_Seg_Hex seven_seg_hex_15 (.d({ACC15, ACC14, ACC13, ACC12}), .dp(1'b0));
  LED led_25 (.in(diodeforward_4_out));
  PullDown pulldown_2 (.out(diodeforward_4_out));
  LED led_26 (.in(D5));
  D_FF d_ff_8 (.D(d_ff_8_nq), .C(button_11_out), .Q(D5), .nQ(d_ff_8_nq));
  Button button_10 (.out(button_10_out));
  Seven_Seg_Hex seven_seg_hex_16 (.d({ACC11, ACC10, ACC9, ACC8}), .dp(1'b0));
  LED led_27 (.in(D4));
  D_FF d_ff_9 (.D(d_ff_9_nq), .C(button_12_out), .Q(D4), .nQ(d_ff_9_nq));
  Button button_11 (.out(button_11_out));
  Seven_Seg_Hex seven_seg_hex_17 (.d({ACC7, ACC6, ACC5, ACC4}), .dp(1'b0));
  nand nand_6 (nZERO, diodeforward_4_out, diodeforward_4_out);
  _74164 U5 (
    .pin1(1'b1), .pin2(Fout), .pin3(U5_pin6[3]), .pin4(U5_pin6[2]), .pin5(U5_pin6[1]), .pin6(U5_pin6[0]),
    .pin7(1'b0), .pin8(GCLK), .pin9(CLR), .pin10(U5_pin13[3]), .pin11(U5_pin13[2]), .pin12(U5_pin13[1]),
    .pin13(U5_pin13[0]), .pin14(1'b1));
  LED led_28 (.in(D3));
  D_FF d_ff_10 (.D(d_ff_10_nq), .C(button_13_out), .Q(D3), .nQ(d_ff_10_nq));
  Button button_12 (.out(button_12_out));
  Seven_Seg_Hex seven_seg_hex_18 (.d({ACC3, ACC2, ACC1, ACC0}), .dp(1'b0));
  LED led_29 (.in(D2));
  D_FF d_ff_11 (.D(d_ff_11_nq), .C(button_14_out), .Q(D2), .nQ(d_ff_11_nq));
  Button button_13 (.out(button_13_out));
  LED led_30 (.in(D1));
  D_FF d_ff_12 (.D(d_ff_12_nq), .C(button_15_out), .Q(D1), .nQ(d_ff_12_nq));
  Button button_14 (.out(button_14_out));
  Seven_Seg_Hex seven_seg_hex_19 (.d(U5_pin6), .dp(1'b0));
  LED led_31 (.in(D0));
  D_FF IC16_2 (.D(IC16_2_nq), .C(button_16_out), .Q(D0), .nQ(IC16_2_nq));
  Button button_15 (.out(button_15_out));
  _74541 _74541_3 (
    .pin1(1'b1), .pin2(ACC8), .pin3(ACC9), .pin4(ACC10), .pin5(ACC11), .pin6(ACC12), .pin7(ACC13),
    .pin8(ACC14), .pin9(ACC15), .pin10(1'b0), .pin11(BUS15), .pin12(BUS14), .pin13(BUS13), .pin14(BUS12),
    .pin15(BUS11), .pin16(BUS10), .pin17(BUS9), .pin18(BUS8), .pin19(1'b1), .pin20(1'b1));
  _74541 _74541_4 (
    .pin1(1'b1), .pin2(ACC0), .pin3(ACC1), .pin4(ACC2), .pin5(ACC3), .pin6(ACC4), .pin7(ACC5), .pin8(ACC6),
    .pin9(ACC7), .pin10(1'b0), .pin11(BUS7), .pin12(BUS6), .pin13(BUS5), .pin14(BUS4), .pin15(BUS3),
    .pin16(BUS2), .pin17(BUS1), .pin18(BUS0), .pin19(1'b1), .pin20(1'b1));
  Seven_Seg_Hex seven_seg_hex_20 (.d(U5_pin13), .dp(1'b0));
  Button button_16 (.out(button_16_out));
  Seven_Seg_Hex seven_seg_hex_21 (.d(U6_pin6), .dp(1'b0));
  Seven_Seg_Hex seven_seg_hex_22 (.d({D7, D6, D5, D4}), .dp(1'b0));
  Button button_17 (.out(button_17_out));
  Seven_Seg_Hex seven_seg_hex_23 (.d({U6_pin10, Aout}), .dp(1'b0));
  _74164 U6 (
    .pin1(1'b1), .pin2(U5_pin13[0]), .pin3(U6_pin6[3]), .pin4(U6_pin6[2]), .pin5(U6_pin6[1]),
    .pin6(U6_pin6[0]), .pin7(1'b0), .pin8(GCLK), .pin9(CLR), .pin10(U6_pin10[3]), .pin11(U6_pin10[2]),
    .pin12(U6_pin10[1]), .pin13(Aout), .pin14(1'b1));
  Seven_Seg_Hex seven_seg_hex_24 (.d({D3, D2, D1, D0}), .dp(1'b0));
  not not_22 (not_22_out, TP3);
  Monoflop monoflop_2 (.C(button_17_out), .R(1'b0), .Q(nLDA), .nQ(nLDB));
  Monoflop monoflop_3 (.C(nLDB), .R(1'b0), .Q(SETC), .nQ(RES));
  _74161 U7_2 (
    .pin1(RST), .pin2(clk), .pin3(1'b0), .pin4(1'b0), .pin5(1'b0), .pin6(1'b0), .pin7(1'b1), .pin8(1'b0),
    .pin9(1'b1), .pin10(1'b1), .pin11(U7_2_pin11[3]), .pin12(U7_2_pin11[2]), .pin13(U7_2_pin11[1]),
    .pin14(U7_2_pin11[0]), .pin15(U7_2_pin15), .pin16(1'b1));
  Monoflop monoflop_4 (.C(button_18_out), .R(1'b0), .Q(CLR4017), .nQ(nCLRPC));
  Button button_18 (.out(button_18_out));
  nand nand_7 (nand_7_out, SETC, C);
  nand nand_8 (nand_8_out, C, C);
  nand nand_9 (CLR, CLA, nLDA);
  Seven_Seg_Hex seven_seg_hex_25 (.d(U7_2_pin11), .dp(1'b0));
  xor xor_2 (xor_2_out, Aout, nA);
  xor xor_3 (xor_3_out, nB, Bout);
  nand nand_10 (nand_10_out, nand_8_out, nLDA);
  xor xor_4 (xor_4_out, xor_2_out, xor_3_out);
  nand nand_11 (nand_11_out, clk, clk);
  xor xor_5 (xor_5_out, xor_4_out, Cin);
  nand nand_12 (nand_12_out, xor_4_out, Cin);
  nand nand_13 (nand_13_out, xor_2_out, xor_3_out);
  nand nand_14 (GCLK, nand_11_out, RST);
  nand nand_15 (RST, RES, nand_16_out);
  nand nand_16 (nand_16_out, RST, T0);
  nand nand_17 (nand_17_out, nand_12_out, nand_13_out);
  nand nand_18 (nand_18_out, xor_5_out, I0);
  nand nand_19 (nand_19_out, I1, nand_17_out);
  nand nand_20 (nand_20_out, nand_17_out, F);
  _7474 _7474_1 (
    .pin1(1'b1), .pin2(U7_2_pin15), .pin3(clk), .pin4(1'b1), .pin5(IX), .pin6(T0), .pin7(1'b0), .pin9(Cin),
    .pin10(nand_7_out), .pin11(GCLK), .pin12(Cout), .pin13(nand_10_out), .pin14(1'b1));  // open: pin8
  nand nand_21 (Fout, nand_18_out, nand_19_out);
  nand nand_22 (Cout, nand_20_out, nand_20_out);

  // Other names for the same wires on the sheet: TP1 = CLKIR

  // Notes on the sheet:
  //   Front Panel (8 ICs)
  //   UP
  //   LOAD
  //   DOWN
  //   COUNT
  //   WRITE
  //   ~DE
  //   READ
  //   RESET
  //   KEY DATA
  //   Hex Keypad
  //   KEYSWITCH REGISTER
  //   RAM ADDRESS
  //   RAM DATA
  //   PC and RAM (8 ICs)
  //   PROGRAM COUNTER
  //   DATA BUFFER HI
  //   RAM HI
  //   DATA BUFFER LO
  //   RAM LO
  //   Instruction
  //    Register
  //   SPIDER - Bit Serial CPU Testbed  (21 ICs)
  //   Instruction Input
  //   Instruction Decode
  //   CLA
  //   F
  //   ~B
  //   C
  //   ~A
  //   I1
  //   I0
  //   AND
  //   OR
  //   XOR
  //   ADD
  //   SUB
  //   STORE
  //   JMP
  //   TP0
  //   TP1
  //   TP2
  //   TP3
  //   TP20
  //   TP21
  //   TP22
  //   TP23
  //   16 bit Shift Register B
  //   Output Display Registers
  //   ENTER H
  //   Data Input
  //   OUTPUT REGISTER
  //   ENTER L
  //   16 bit Shift Register A
  //   AC TO BUS
  //   ACCUMULATOR
  //   STEP/RUN
  //   CLR PC
  //   Bit Serial ALU
  //   Clock Sequencer
  //   CLR ACC
  //   # Clock
  //   Carry is only set before Bit 0 of an operation
  //   Any residual carry is cleared before an operation
  //   Suppress Carry
  //   Carry FF
endmodule
