// Digital circuit spider_11.dig as structural Verilog
module spider_11 (
  input  clk,
  input  in_3,
  input  in_4,
  input  in_5,
  output Fout
);

  wire ADD, AND, Aout, Bout, BUS0, BUS1, BUS2, BUS3, BUS4, BUS5, BUS6, BUS7, BUS8, BUS9, BUS10, BUS11, BUS12,
       BUS13, BUS14, BUS15, button_1_out, button_2_out, button_3_out, button_4_out, button_5_out,
       button_6_out, button_7_out, button_8_out, button_9_out, button_10_out, button_11_out, button_12_out,
       button_13_out, button_14_out, button_15_out, button_16_out, button_18_out, C, Cin, CLA, CLKB, CLKM,
       CLR, Cout, d_ff_1_nq, d_ff_2_nq, d_ff_3_nq, d_ff_4_nq, d_ff_5_nq, d_ff_6_nq, d_ff_7_nq, d_ff_8_nq,
       d_ff_9_nq, d_ff_10_nq, d_ff_11_nq, d_ff_12_nq, diodebackward_2_out, diodebackward_6_out,
       diodebackward_8_out, diodebackward_10_out, diodeforward_1_out, F, GCLK, I0, I1, IC16_2_nq, IC16_nq,
       IC17_2_nq, IC17_nq, IX, LD, LOAD, MRout, MWin, MWout, nA, nand_2_out, nand_3_out, nand_5_out,
       nand_6_out, nand_9_out, nand_10_out, nand_11_out, nand_12_out, nand_13_out, nand_14_out, nand_15_out,
       nB, nCLRPC, nJMP, nLD, nOE, nRRES, nWE, nZERO, OR, pullup_1_out, pullup_4_out, pullup_5_out, RAM0,
       RAM1, RAM2, RAM3, RAM4, RAM5, RAM6, RAM7, RAM8, RAM9, RAM10, RAM11, RAM12, RAM13, RAM14, RES, RST,
       SELS, SETC, ST, SUB, T0, U3_pin9, U7_pin15, U8_pin9, U9_pin9, U11_pin9, U18_pin9, XOR, xor_1_out,
       xor_2_out, xor_3_out, xor_4_out;
  wire [3:0] _74541_1_pin5, _74541_1_pin9, _74541_2_pin5, _74541_2_pin9, U5_pin6, U5_pin13, U6_pin6, U7_pin11;
  wire [3:1] U6_pin10;

  LED led_1 (.in(_74541_1_pin5[3]));
  LED led_2 (.in(_74541_1_pin5[2]));
  D_FF IC17 (.D(IC17_nq), .C(button_1_out), .Q(_74541_1_pin5[3]), .nQ(IC17_nq));
  Button button_1 (.out(button_1_out));
  _74541 _74541_1 (
    .pin1(1'b0), .pin2(_74541_1_pin5[3]), .pin3(_74541_1_pin5[2]), .pin4(_74541_1_pin5[1]),
    .pin5(_74541_1_pin5[0]), .pin6(_74541_1_pin9[3]), .pin7(_74541_1_pin9[2]), .pin8(_74541_1_pin9[1]),
    .pin9(_74541_1_pin9[0]), .pin10(1'b0), .pin11(BUS8), .pin12(BUS9), .pin13(BUS10), .pin14(BUS11),
    .pin15(BUS12), .pin16(BUS13), .pin17(BUS14), .pin18(BUS15), .pin19(SELS), .pin20(1'b1));
  LED led_3 (.in(_74541_1_pin5[1]));
  D_FF d_ff_1 (.D(d_ff_1_nq), .C(button_2_out), .Q(_74541_1_pin5[2]), .nQ(d_ff_1_nq));
  Button button_2 (.out(button_2_out));
  LED led_4 (.in(_74541_1_pin5[0]));
  D_FF d_ff_2 (.D(d_ff_2_nq), .C(button_3_out), .Q(_74541_1_pin5[1]), .nQ(d_ff_2_nq));
  Button button_3 (.out(button_3_out));
  LED led_5 (.in(_74541_1_pin9[3]));
  D_FF d_ff_3 (.D(d_ff_3_nq), .C(button_4_out), .Q(_74541_1_pin5[0]), .nQ(d_ff_3_nq));
  Button button_4 (.out(button_4_out));
  LED led_6 (.in(_74541_1_pin9[2]));
  D_FF d_ff_4 (.D(d_ff_4_nq), .C(button_5_out), .Q(_74541_1_pin9[3]), .nQ(d_ff_4_nq));
  Button button_5 (.out(button_5_out));
  LED led_7 (.in(_74541_1_pin9[1]));
  D_FF d_ff_5 (.D(d_ff_5_nq), .C(button_6_out), .Q(_74541_1_pin9[2]), .nQ(d_ff_5_nq));
  Button button_6 (.out(button_6_out));
  _74138 U1 (
    .pin1(in_3), .pin2(in_4), .pin3(in_5), .pin4(1'b0), .pin5(1'b0), .pin6(1'b1), .pin7(nJMP), .pin8(1'b0),
    .pin9(ST), .pin10(SUB), .pin11(ADD), .pin12(XOR), .pin13(OR), .pin14(AND), .pin15(LOAD), .pin16(1'b1));
  LED led_8 (.in(_74541_1_pin9[0]));
  D_FF d_ff_6 (.D(d_ff_6_nq), .C(button_7_out), .Q(_74541_1_pin9[1]), .nQ(d_ff_6_nq));
  Button button_7 (.out(button_7_out));
  Seven_Seg_Hex seven_seg_hex_1 (.d(_74541_1_pin5), .dp(1'b0));
  D_FF IC17_2 (.D(IC17_2_nq), .C(button_8_out), .Q(_74541_1_pin9[0]), .nQ(IC17_2_nq));
  Button button_8 (.out(button_8_out));
  Seven_Seg_Hex seven_seg_hex_2 (.d(_74541_1_pin9), .dp(1'b0));
  PullUp pullup_1 (.out(pullup_1_out));
  DiodeBackward diodebackward_1 (.in(LOAD), .out(pullup_1_out));
  DiodeBackward diodebackward_2 (.in(LOAD), .out(diodebackward_2_out));
  DiodeBackward diodebackward_3 (.in(ADD), .out(diodebackward_2_out));
  DiodeBackward diodebackward_4 (.in(SUB), .out(diodebackward_2_out));
  DiodeBackward diodebackward_5 (.in(nJMP), .out(diodebackward_2_out));
  Seven_Seg_Hex seven_seg_hex_3 (.d(_74541_2_pin5), .dp(1'b0));
  PullUp pullup_2 (.out(diodebackward_2_out));
  DiodeBackward diodebackward_6 (.in(SUB), .out(diodebackward_6_out));
  Seven_Seg_Hex seven_seg_hex_4 (.d(_74541_2_pin9), .dp(1'b0));
  PullUp pullup_3 (.out(diodebackward_6_out));
  PullUp pullup_4 (.out(pullup_4_out));
  DiodeBackward diodebackward_7 (.in(SUB), .out(pullup_4_out));
  LED led_9 (.in(_74541_2_pin5[3]));
  D_FF IC16 (.D(IC16_nq), .C(button_9_out), .Q(_74541_2_pin5[3]), .nQ(IC16_nq));
  Button button_9 (.out(button_9_out));
  PullUp pullup_5 (.out(pullup_5_out));
  DiodeBackward diodebackward_8 (.in(AND), .out(diodebackward_8_out));
  DiodeBackward diodebackward_9 (.in(OR), .out(diodebackward_8_out));
  LED led_10 (.in(_74541_2_pin5[2]));
  D_FF d_ff_7 (.D(d_ff_7_nq), .C(button_10_out), .Q(_74541_2_pin5[2]), .nQ(d_ff_7_nq));
  Button button_10 (.out(button_10_out));
  PullUp pullup_6 (.out(diodebackward_8_out));
  DiodeBackward diodebackward_10 (.in(LOAD), .out(diodebackward_10_out));
  DiodeBackward diodebackward_11 (.in(OR), .out(diodebackward_10_out));
  DiodeBackward diodebackward_12 (.in(XOR), .out(diodebackward_10_out));
  DiodeBackward diodebackward_13 (.in(ADD), .out(diodebackward_10_out));
  DiodeBackward diodebackward_14 (.in(SUB), .out(diodebackward_10_out));
  DiodeBackward diodebackward_15 (.in(ST), .out(diodebackward_10_out));
  _74541 _74541_2 (
    .pin1(1'b0), .pin2(_74541_2_pin5[3]), .pin3(_74541_2_pin5[2]), .pin4(_74541_2_pin5[1]),
    .pin5(_74541_2_pin5[0]), .pin6(_74541_2_pin9[3]), .pin7(_74541_2_pin9[2]), .pin8(_74541_2_pin9[1]),
    .pin9(_74541_2_pin9[0]), .pin10(1'b0), .pin11(BUS0), .pin12(BUS1), .pin13(BUS2), .pin14(BUS3),
    .pin15(BUS4), .pin16(BUS5), .pin17(BUS6), .pin18(BUS7), .pin19(SELS), .pin20(1'b1));
  LED led_11 (.in(_74541_2_pin5[1]));
  D_FF d_ff_8 (.D(d_ff_8_nq), .C(button_11_out), .Q(_74541_2_pin5[1]), .nQ(d_ff_8_nq));
  Button button_11 (.out(button_11_out));
  PullUp pullup_7 (.out(diodebackward_10_out));
  _74540 U2 (
    .pin1(1'b0), .pin2(diodebackward_10_out), .pin3(diodebackward_8_out), .pin4(pullup_5_out),
    .pin5(pullup_4_out), .pin6(diodebackward_6_out), .pin7(diodebackward_2_out), .pin8(pullup_1_out),
    .pin9(1'b0), .pin10(1'b0), .pin12(CLA), .pin13(F), .pin14(C), .pin15(nB), .pin16(nA), .pin17(I1),
    .pin18(I0), .pin19(1'b0), .pin20(1'b1));  // open: pin11
  LED led_12 (.in(_74541_2_pin5[0]));
  D_FF d_ff_9 (.D(d_ff_9_nq), .C(button_12_out), .Q(_74541_2_pin5[0]), .nQ(d_ff_9_nq));
  Button button_12 (.out(button_12_out));
  LED led_13 (.in(_74541_2_pin9[3]));
  D_FF d_ff_10 (.D(d_ff_10_nq), .C(button_13_out), .Q(_74541_2_pin9[3]), .nQ(d_ff_10_nq));
  Button button_13 (.out(button_13_out));
  LED led_14 (.in(_74541_2_pin9[2]));
  D_FF d_ff_11 (.D(d_ff_11_nq), .C(button_14_out), .Q(_74541_2_pin9[2]), .nQ(d_ff_11_nq));
  Button button_14 (.out(button_14_out));
  LED led_15 (.in(_74541_2_pin9[1]));
  D_FF d_ff_12 (.D(d_ff_12_nq), .C(button_15_out), .Q(_74541_2_pin9[1]), .nQ(d_ff_12_nq));
  Button button_15 (.out(button_15_out));
  LED led_16 (.in(_74541_2_pin9[0]));
  D_FF IC16_2 (.D(IC16_2_nq), .C(button_16_out), .Q(_74541_2_pin9[0]), .nQ(IC16_2_nq));
  Button button_16 (.out(button_16_out));
  _74165 U3 (
    .pin1(LD), .pin2(GCLK), .pin3(BUS11), .pin4(BUS10), .pin5(BUS9), .pin6(BUS8), .pin8(1'b0),
    .pin9(U3_pin9), .pin10(1'b0), .pin11(BUS15), .pin12(BUS14), .pin13(BUS13), .pin14(BUS12), .pin15(1'b0),
    .pin16(1'b1));  // open: pin7
  _74595 U8 (
    .pin1(BUS14), .pin2(BUS13), .pin3(BUS12), .pin4(BUS11), .pin5(BUS10), .pin6(BUS9), .pin7(BUS8),
    .pin8(1'b0), .pin9(U8_pin9), .pin10(RES), .pin11(GCLK), .pin12(T0), .pin13(1'b0), .pin14(Fout),
    .pin15(BUS15), .pin16(1'b1));
  _74165 U4 (
    .pin1(LD), .pin2(GCLK), .pin3(BUS3), .pin4(BUS2), .pin5(BUS1), .pin6(BUS0), .pin8(1'b0), .pin9(Bout),
    .pin10(U3_pin9), .pin11(BUS7), .pin12(BUS6), .pin13(BUS5), .pin14(BUS4), .pin15(1'b0), .pin16(1'b1));  // open: pin7
  _74595 U9 (
    .pin1(BUS6), .pin2(BUS5), .pin3(BUS4), .pin4(BUS3), .pin5(BUS2), .pin6(BUS1), .pin7(BUS0), .pin8(1'b0),
    .pin9(U9_pin9), .pin10(RES), .pin11(GCLK), .pin12(T0), .pin13(1'b0), .pin14(U8_pin9), .pin15(BUS7),
    .pin16(1'b1));
  _74165 U11 (
    .pin1(LD), .pin2(CLKM), .pin3(BUS11), .pin4(BUS10), .pin5(BUS9), .pin6(BUS8), .pin8(1'b0),
    .pin9(U11_pin9), .pin10(1'b0), .pin11(BUS15), .pin12(BUS14), .pin13(BUS13), .pin14(BUS12), .pin15(1'b0),
    .pin16(1'b1));  // open: pin7
  DiodeForward diodeforward_1 (.in(BUS15), .out(diodeforward_1_out));
  DiodeForward diodeforward_2 (.in(BUS14), .out(diodeforward_1_out));
  DiodeForward diodeforward_3 (.in(BUS13), .out(diodeforward_1_out));
  DiodeForward diodeforward_4 (.in(BUS12), .out(diodeforward_1_out));
  DiodeForward diodeforward_5 (.in(BUS11), .out(diodeforward_1_out));
  DiodeForward diodeforward_6 (.in(BUS10), .out(diodeforward_1_out));
  DiodeForward diodeforward_7 (.in(BUS9), .out(diodeforward_1_out));
  DiodeForward diodeforward_8 (.in(BUS8), .out(diodeforward_1_out));
  DiodeForward diodeforward_9 (.in(BUS7), .out(diodeforward_1_out));
  DiodeForward diodeforward_10 (.in(BUS6), .out(diodeforward_1_out));
  DiodeForward diodeforward_11 (.in(BUS5), .out(diodeforward_1_out));
  DiodeForward diodeforward_12 (.in(BUS4), .out(diodeforward_1_out));
  DiodeForward diodeforward_13 (.in(BUS3), .out(diodeforward_1_out));
  DiodeForward diodeforward_14 (.in(BUS2), .out(diodeforward_1_out));
  DiodeForward diodeforward_15 (.in(BUS1), .out(diodeforward_1_out));
  DiodeForward diodeforward_16 (.in(BUS0), .out(diodeforward_1_out));
  Seven_Seg_Hex seven_seg_hex_5 (.d({BUS15, BUS14, BUS13, BUS12}), .dp(1'b0));
  Seven_Seg_Hex seven_seg_hex_6 (.d({BUS11, BUS10, BUS9, BUS8}), .dp(1'b0));
  nand nand_1 (nZERO, diodeforward_1_out, diodeforward_1_out);
  PullDown pulldown_1 (.out(diodeforward_1_out));
  Seven_Seg_Hex seven_seg_hex_7 (.d({BUS7, BUS6, BUS5, BUS4}), .dp(1'b0));
  _74164 U5 (
    .pin1(1'b1), .pin2(Fout), .pin3(U5_pin6[3]), .pin4(U5_pin6[2]), .pin5(U5_pin6[1]), .pin6(U5_pin6[0]),
    .pin7(1'b0), .pin8(GCLK), .pin9(CLR), .pin10(U5_pin13[3]), .pin11(U5_pin13[2]), .pin12(U5_pin13[1]),
    .pin13(U5_pin13[0]), .pin14(1'b1));
  _74165 U12 (
    .pin1(LD), .pin2(CLKM), .pin3(BUS3), .pin4(BUS2), .pin5(BUS1), .pin6(BUS0), .pin8(1'b0), .pin9(MRout),
    .pin10(U11_pin9), .pin11(BUS7), .pin12(BUS6), .pin13(BUS5), .pin14(BUS4), .pin15(1'b0), .pin16(1'b1));  // open: pin7
  Seven_Seg_Hex seven_seg_hex_8 (.d({BUS3, BUS2, BUS1, BUS0}), .dp(1'b0));
  LED led_17 (.in(nZERO));
  Seven_Seg_Hex seven_seg_hex_9 (.d(U5_pin6), .dp(1'b0));
  Seven_Seg_Hex seven_seg_hex_10 (.d(U5_pin13), .dp(1'b0));
  Seven_Seg_Hex seven_seg_hex_11 (.d(U6_pin6), .dp(1'b0));
  Seven_Seg_Hex seven_seg_hex_12 (.d({U6_pin10, Aout}), .dp(1'b0));
  _74164 U6 (
    .pin1(1'b1), .pin2(U5_pin13[0]), .pin3(U6_pin6[3]), .pin4(U6_pin6[2]), .pin5(U6_pin6[1]),
    .pin6(U6_pin6[0]), .pin7(1'b0), .pin8(GCLK), .pin9(CLR), .pin10(U6_pin10[3]), .pin11(U6_pin10[2]),
    .pin12(U6_pin10[1]), .pin13(Aout), .pin14(1'b1));
  _74595 U18 (
    .pin1(BUS14), .pin2(BUS13), .pin3(BUS12), .pin4(BUS11), .pin5(BUS10), .pin6(BUS9), .pin7(BUS8),
    .pin8(1'b0), .pin9(U18_pin9), .pin10(nRRES), .pin11(CLKB), .pin12(T0), .pin13(nWE), .pin14(MWin),
    .pin15(BUS15), .pin16(1'b1));
  Monoflop monoflop_1 (.C(IX), .R(1'b0), .Q(nLD), .nQ(LD));
  Button button_17 ();  // open: out
  Monoflop monoflop_2 (.C(LD), .R(1'b0), .Q(SETC), .nQ(RES));
  _74161 U7 (
    .pin1(RST), .pin2(clk), .pin3(1'b0), .pin4(1'b0), .pin5(1'b0), .pin6(1'b0), .pin7(1'b1), .pin8(1'b0),
    .pin9(1'b1), .pin10(1'b1), .pin11(U7_pin11[3]), .pin12(U7_pin11[2]), .pin13(U7_pin11[1]),
    .pin14(U7_pin11[0]), .pin15(U7_pin15), .pin16(1'b1));
  Monoflop monoflop_3 (.C(button_18_out), .R(1'b0), .nQ(nCLRPC));  // open: Q
  Button button_18 (.out(button_18_out));
  _74595 U19 (
    .pin1(BUS6), .pin2(BUS5), .pin3(BUS4), .pin4(BUS3), .pin5(BUS2), .pin6(BUS1), .pin7(BUS0), .pin8(1'b0),
    .pin9(MWout), .pin10(nRRES), .pin11(CLKB), .pin12(T0), .pin13(nWE), .pin14(U18_pin9), .pin15(BUS7),
    .pin16(1'b1));
  nand nand_2 (nand_2_out, SETC, C);
  nand nand_3 (nand_3_out, C, C);
  nand nand_4 (CLR, CLA, nLD);
  Seven_Seg_Hex seven_seg_hex_13 (.d(U7_pin11), .dp(1'b0));
  xor xor_1 (xor_1_out, Aout, nA);
  xor xor_2 (xor_2_out, nB, Bout);
  nand nand_5 (nand_5_out, nand_3_out, nLD);
  Seven_Seg_Hex seven_seg_hex_14 (.d({BUS15, BUS14, BUS13, BUS12}), .dp(1'b0));
  Seven_Seg_Hex seven_seg_hex_15 (.d({BUS11, BUS10, BUS9, BUS8}), .dp(1'b0));
  D_FF d_ff_13 (.D(U7_pin15), .C(clk), .Q(IX), .nQ(T0));
  nand nand_6 (nand_6_out, clk, clk);
  xor xor_3 (xor_3_out, xor_1_out, xor_2_out);
  Seven_Seg_Hex seven_seg_hex_16 (.d({BUS7, BUS6, BUS5, BUS4}), .dp(1'b0));
  Seven_Seg_Hex seven_seg_hex_17 (.d({BUS3, BUS2, BUS1, BUS0}), .dp(1'b0));
  nand nand_7 (GCLK, nand_6_out, RST);
  nand nand_8 (RST, RES, nand_9_out);
  nand nand_9 (nand_9_out, RST, T0);
  xor xor_4 (xor_4_out, xor_3_out, Cin);
  nand nand_10 (nand_10_out, xor_3_out, Cin);
  nand nand_11 (nand_11_out, xor_1_out, xor_2_out);
  nand nand_12 (nand_12_out, nand_10_out, nand_11_out);
  // _62256 U35: pin names not known; wires that end beside it: RAM14, RAM12, RAM7, RAM6, RAM5, RAM4, RAM3, RAM2, RAM1, RAM0, BUS8, BUS9, BUS10, 1'b0, 1'b1, nWE, RAM13, RAM8, RAM9, RAM11, nOE, RAM10, 1'b0, BUS15
  nand nand_13 (nand_13_out, xor_4_out, I0);
  nand nand_14 (nand_14_out, I1, nand_12_out);
  nand nand_15 (nand_15_out, nand_12_out, F);
  nand nand_16 (Fout, nand_13_out, nand_14_out);
  nand nand_17 (Cout, nand_15_out, nand_15_out);
  // _62256 U34: pin names not known; wires that end beside it: RAM14, RAM12, RAM7, RAM6, RAM5, RAM4, RAM3, RAM2, RAM1, RAM0, BUS0, BUS1, BUS2, 1'b0, 1'b1, nWE, RAM13, RAM8, RAM9, RAM11, nOE, RAM10, 1'b0, BUS7
  D_FF_AS d_ff_as_1 (.Set(~nand_2_out), .D(Cout), .C(GCLK), .Clr(~nand_5_out), .Q(Cin));  // open: nQ

  // Notes on the sheet:
  //   clk: Hz: 2147483647
  //   spider-0
  //   Front Panel Switches
  //   Instruction Input
  //   ENTER H
  //   Data Input
  //   Instruction Decode
  //   CLA
  //   F
  //   ~B
  //   C
  //   ~A
  //   I1
  //   I0
  //   LOAD
  //   AND
  //   OR
  //   XOR
  //   ADD
  //   SUB
  //   STORE
  //   JMP
  //   ENTER L
  //   Output Display Registers
  //   16 bit Shift Register B
  //   RAM Subsection
  //   Memory Read Register 2 packages
  //   Memory Read Register
  //   OUTPUT REGISTER
  //   16 bit Shift Register A
  //   ACCUMULATOR
  //   Y REGISTER
  //   STEP/RUN
  //   Memory Write Register
  //   CLR PC
  //   Clock Sequencer
  //   CLR ACC
  //   # Clock
  //   BUS DATA
  //   Carry is only set before Bit 0 of an operation
  //   Any residual carry is cleared before an operation
  //   Spider_0 Bit serial CPU Testbed
  //   RAM HI
  //   Suppress Carry
  //   RAM LO
  //   Carry FF
endmodule
