// Digital circuit spider_4A.dig as structural Verilog
module spider_4A (
  input  clk,
  input  in_4,
  input  in_5,
  input  in_6,
  input  in_7,
  input  in_8,
  input  in_9,
  input  in_10,
  output GCLK,
  output Fout
);

  wire _8_n16, A0, A1, A2, A3, A4, A5, A6, A7, A8, A9, A10, A11, A12, A13, A14, A15, ADD, AND, and_1_out,
       Aout, BUS0, BUS1, BUS2, BUS3, BUS4, BUS5, BUS6, BUS7, button_1_out, button_2_out, button_3_out,
       button_4_out, button_5_out, button_6_out, button_7_out, button_8_out, button_9_out, button_10_out,
       button_11_out, button_12_out, button_13_out, button_14_out, button_15_out, button_16_out,
       button_17_out, button_18_out, C, Cin, CLA, CLKB, CLKC, CLKD, CLKE, CLKX, CLKY, CLR, Cout, D0, D1, D2,
       D3, D4, D5, D6, D7, D8, D9, D10, D11, D12, D13, D14, D15, d_ff_1_nq, d_ff_2_nq, d_ff_3_nq, d_ff_4_nq,
       d_ff_5_nq, d_ff_6_nq, d_ff_7_nq, d_ff_8_nq, d_ff_9_nq, d_ff_10_nq, d_ff_11_nq, d_ff_12_nq,
       diodebackward_1_out, diodebackward_4_out, diodebackward_11_out, diodeforward_1_out, F, I0, I1,
       IC13_pin9, IC14_pin9, IC15_pin9, IC16_2_nq, IC16_3_pin9, IC16_nq, IC17_2_nq, IC17_3_pin9, IC17_nq,
       IC18_pin9, IC19_pin9, IC20_pin9, IC21_pin9, IC22_pin9, IC23_pin9, IX, LD, LDH, LDL, nA, nand_1_out,
       nand_2_out, nand_3_out, nand_4_out, nand_5_out, nand_6_out, nand_7_out, nand_8_out, nand_9_out,
       nand_12_out, nand_13_out, nand_14_out, nand_15_out, nand_16_out, nand_19_out, nand_20_out,
       nand_21_out, nand_22_out, nand_23_out, nand_24_out, nand_25_out, nand_26_out, nand_27_out,
       nand_28_out, nand_29_out, nand_30_out, nand_31_out, nB, nClr, nCLRPC, nJMP, nLD, nSet, nZERO, OR,
       or_2_out, PC_Cin, PCin, PCLD, PCout, pullup_1_out, pullup_3_out, pullup_5_out, pullup_6_out,
       pullup_8_out, Q0, Q1, Q2, Q3, Q4, Q5, Q6, Q7, RES, Rout, RST, SELX, SELY, SETC, Sout, SUB, SW, T0,
       U2_pin9, U2_pin10, U2_pin11, U2_pin12, U2_pin13, U2_pin14, U2_pin15, U3_pin9, U7_pin15, U16_pin18,
       U17_pin15, U19_pin10, U19_pin15, XOR, xor_1_out, xor_2_out, xor_3_out, xor_4_out, xor_5_out,
       xor_6_out, Xout, Yout;
  wire [3:0] IC13_pin4, IC13_pin15, IC15_pin4, IC15_pin15, IC16_3_pin4, IC16_3_pin15, IC17_3_pin4,
       IC17_3_pin15, IC18_pin4, IC18_pin15, IC19_pin4, IC19_pin15, IC20_pin4, IC20_pin15, IC21_pin4,
       IC21_pin15, IC22_pin4, IC22_pin15, IC23_pin4, IC23_pin15, IC24_pin4, IC24_pin15, U5_pin6, U5_pin13,
       U6_pin6, U7_2_pin6, U7_2_pin13, U7_pin11, U8_pin6, U9_pin6, U9_pin13, U10_pin6;
  wire [3:1] U6_pin10, U8_pin10, U10_pin10;

  _74541 U15 (
    .pin1(1'b1), .pin2(1'b0), .pin3(1'b0), .pin4(1'b0), .pin5(1'b0), .pin6(1'b0), .pin7(1'b0), .pin8(1'b0),
    .pin9(1'b0), .pin10(1'b0), .pin11(BUS0), .pin12(BUS1), .pin13(BUS2), .pin14(BUS3), .pin15(BUS4),
    .pin16(BUS5), .pin17(BUS6), .pin18(BUS7), .pin19(1'b1), .pin20(1'b1));
  _74541 U16 (
    .pin1(1'b0), .pin2(1'b0), .pin3(1'b0), .pin4(1'b0), .pin5(1'b0), .pin6(1'b0), .pin7(1'b0), .pin8(1'b0),
    .pin9(1'b0), .pin10(1'b0), .pin11(A8), .pin12(A9), .pin13(A10), .pin14(A11), .pin15(A12), .pin16(A13),
    .pin17(A14), .pin18(U16_pin18), .pin19(1'b0), .pin20(1'b1));
  _74138 U1 (
    .pin1(in_4), .pin2(in_5), .pin3(in_6), .pin4(in_7), .pin5(1'b0), .pin6(1'b1), .pin7(SW), .pin8(1'b0),
    .pin9(SUB), .pin10(ADD), .pin11(XOR), .pin12(OR), .pin13(AND), .pin14(LDH), .pin15(LDL), .pin16(1'b1));
  _74138 U2 (
    .pin1(in_4), .pin2(in_5), .pin3(in_6), .pin4(1'b0), .pin5(1'b0), .pin6(in_7), .pin7(nJMP), .pin8(1'b0),
    .pin9(U2_pin9), .pin10(U2_pin10), .pin11(U2_pin11), .pin12(U2_pin12), .pin13(U2_pin13), .pin14(U2_pin14),
    .pin15(U2_pin15), .pin16(1'b1));
  _74163 U19 (
    .pin1(nCLRPC), .pin2(clk), .pin3(BUS0), .pin4(BUS1), .pin5(BUS2), .pin6(BUS3), .pin7(IX), .pin8(1'b0),
    .pin9(nJMP), .pin10(U19_pin10), .pin11(A11), .pin12(A10), .pin13(A9), .pin14(A8), .pin15(U19_pin15),
    .pin16(1'b1));
  _74163 U18 (
    .pin1(nCLRPC), .pin2(clk), .pin3(BUS4), .pin4(BUS5), .pin5(BUS6), .pin6(BUS7), .pin7(IX), .pin8(1'b0),
    .pin9(nJMP), .pin10(U19_pin15), .pin11(A15), .pin12(A14), .pin13(A13), .pin14(A12), .pin16(1'b1));  // open: pin15
  _74163 U17 (
    .pin1(nCLRPC), .pin2(clk), .pin3(BUS0), .pin4(BUS1), .pin5(BUS2), .pin6(BUS3), .pin7(IX), .pin8(1'b0),
    .pin9(nJMP), .pin10(1'b1), .pin11(A3), .pin12(A2), .pin13(A1), .pin14(A0), .pin15(U17_pin15), .pin16(1'b1));
  _74163 U16_2 (
    .pin1(nCLRPC), .pin2(clk), .pin3(BUS4), .pin4(BUS5), .pin5(BUS6), .pin6(BUS7), .pin7(IX), .pin8(1'b0),
    .pin9(nJMP), .pin10(U17_pin15), .pin11(A7), .pin12(A6), .pin13(A5), .pin14(A4), .pin15(U19_pin10),
    .pin16(1'b1));
  PullUp pullup_1 (.out(pullup_1_out));
  DiodeBackward diodebackward_1 (.in(LDL), .out(diodebackward_1_out));
  DiodeBackward diodebackward_2 (.in(LDL), .out(pullup_1_out));
  DiodeBackward diodebackward_3 (.in(SW), .out(pullup_1_out));
  PullUp pullup_2 (.out(diodebackward_1_out));
  DiodeBackward diodebackward_4 (.in(LDL), .out(diodebackward_4_out));
  DiodeBackward diodebackward_5 (.in(ADD), .out(diodebackward_4_out));
  DiodeBackward diodebackward_6 (.in(SUB), .out(diodebackward_4_out));
  DiodeBackward diodebackward_7 (.in(SW), .out(diodebackward_4_out));
  DiodeBackward diodebackward_8 (.in(nJMP), .out(diodebackward_4_out));
  PullUp pullup_3 (.out(pullup_3_out));
  PullUp pullup_4 (.out(diodebackward_4_out));
  DiodeBackward diodebackward_9 (.in(SUB), .out(pullup_3_out));
  PullUp pullup_5 (.out(pullup_5_out));
  DiodeBackward diodebackward_10 (.in(SUB), .out(pullup_5_out));
  PullUp pullup_6 (.out(pullup_6_out));
  DiodeBackward diodebackward_11 (.in(AND), .out(diodebackward_11_out));
  DiodeBackward diodebackward_12 (.in(OR), .out(diodebackward_11_out));
  PullUp pullup_7 (.out(diodebackward_11_out));
  PullUp pullup_8 (.out(pullup_8_out));
  DiodeBackward diodebackward_13 (.in(LDL), .out(pullup_8_out));
  DiodeBackward diodebackward_14 (.in(LDH), .out(pullup_8_out));
  DiodeBackward diodebackward_15 (.in(OR), .out(pullup_8_out));
  DiodeBackward diodebackward_16 (.in(XOR), .out(pullup_8_out));
  DiodeBackward diodebackward_17 (.in(ADD), .out(pullup_8_out));
  DiodeBackward diodebackward_18 (.in(SUB), .out(pullup_8_out));
  DiodeBackward diodebackward_19 (.in(SW), .out(pullup_8_out));
  Seven_Seg_Hex seven_seg_hex_1 (.d({A15, A14, A13, A12}), .dp(1'b0));
  _74540 U2_2 (
    .pin1(1'b0), .pin2(pullup_8_out), .pin3(diodebackward_11_out), .pin4(pullup_6_out), .pin5(pullup_5_out),
    .pin6(pullup_3_out), .pin7(diodebackward_4_out), .pin8(diodebackward_1_out), .pin9(pullup_1_out),
    .pin10(1'b0), .pin11(_8_n16), .pin12(CLA), .pin13(F), .pin14(C), .pin15(nB), .pin16(nA), .pin17(I1),
    .pin18(I0), .pin19(1'b0), .pin20(1'b1));
  Seven_Seg_Hex seven_seg_hex_2 (.d({A11, A10, A9, A8}), .dp(1'b0));
  // _62256 U36: pin names not known; wires that end beside it: A14, A12, A7, A6, A5, A4, A3, A2, A1, A0, BUS0, BUS1, BUS2, 1'b0, 1'b1, 1'b1, A13, A8, A9, A11, 1'b1, A10, 1'b0, BUS7
  Seven_Seg_Hex seven_seg_hex_3 (.d({A7, A6, A5, A4}), .dp(1'b0));
  Seven_Seg_Hex seven_seg_hex_4 (.d({A3, A2, A1, A0}), .dp(1'b0));
  LED led_1 (.in(D15));
  D_FF IC17 (.D(IC17_nq), .C(button_1_out), .Q(D15), .nQ(IC17_nq));
  Button button_1 (.out(button_1_out));
  _74165 U3 (
    .pin1(LD), .pin2(GCLK), .pin3(D11), .pin4(D10), .pin5(D9), .pin6(D8), .pin8(1'b0), .pin9(U3_pin9),
    .pin10(1'b0), .pin11(D15), .pin12(D14), .pin13(D13), .pin14(D12), .pin15(1'b0), .pin16(1'b1));  // open: pin7
  LED led_2 (.in(D14));
  D_FF d_ff_1 (.D(d_ff_1_nq), .C(button_2_out), .Q(D14), .nQ(d_ff_1_nq));
  Button button_2 (.out(button_2_out));
  LED led_3 (.in(D13));
  D_FF d_ff_2 (.D(d_ff_2_nq), .C(button_3_out), .Q(D13), .nQ(d_ff_2_nq));
  Button button_3 (.out(button_3_out));
  _74541 U17_2 (
    .pin1(1'b1), .pin2(BUS7), .pin3(BUS6), .pin4(BUS5), .pin5(BUS4), .pin6(BUS3), .pin7(BUS2), .pin8(BUS1),
    .pin9(BUS0), .pin10(1'b0), .pin11(D0), .pin12(D1), .pin13(D2), .pin14(D3), .pin15(D4), .pin16(D5),
    .pin17(D6), .pin18(D7), .pin19(1'b1), .pin20(1'b1));
  _74574 _74574_1 (
    .pin1(1'b1), .pin2(BUS7), .pin3(BUS6), .pin4(BUS5), .pin5(BUS4), .pin6(BUS3), .pin7(BUS2), .pin8(BUS1),
    .pin9(BUS0), .pin10(1'b0), .pin11(clk), .pin12(D8), .pin13(D9), .pin14(D10), .pin15(D11), .pin16(D12),
    .pin17(D13), .pin18(D14), .pin19(D15), .pin20(1'b1));
  LED led_4 (.in(D12));
  D_FF d_ff_3 (.D(d_ff_3_nq), .C(button_4_out), .Q(D12), .nQ(d_ff_3_nq));
  Button button_4 (.out(button_4_out));
  LED led_5 (.in(D11));
  D_FF d_ff_4 (.D(d_ff_4_nq), .C(button_5_out), .Q(D11), .nQ(d_ff_4_nq));
  Button button_5 (.out(button_5_out));
  LED led_6 (.in(D10));
  D_FF d_ff_5 (.D(d_ff_5_nq), .C(button_6_out), .Q(D10), .nQ(d_ff_5_nq));
  Button button_6 (.out(button_6_out));
  _74165 U4 (
    .pin1(LD), .pin2(GCLK), .pin3(D3), .pin4(D2), .pin5(D1), .pin6(D0), .pin8(1'b0), .pin9(Sout),
    .pin10(U3_pin9), .pin11(D7), .pin12(D6), .pin13(D5), .pin14(D4), .pin15(1'b0), .pin16(1'b1));  // open: pin7
  LED led_7 (.in(D9));
  D_FF d_ff_6 (.D(d_ff_6_nq), .C(button_7_out), .Q(D9), .nQ(d_ff_6_nq));
  Button button_7 (.out(button_7_out));
  LED led_8 (.in(D8));
  D_FF IC17_2 (.D(IC17_2_nq), .C(button_8_out), .Q(D8), .nQ(IC17_2_nq));
  Button button_8 (.out(button_8_out));
  Seven_Seg_Hex seven_seg_hex_5 (.d({D15, D14, D13, D12}), .dp(1'b0));
  Seven_Seg_Hex seven_seg_hex_6 (.d({D11, D10, D9, D8}), .dp(1'b0));
  LED led_9 (.in(D7));
  D_FF IC16 (.D(IC16_nq), .C(button_9_out), .Q(D7), .nQ(IC16_nq));
  LED led_10 (.in(D6));
  D_FF d_ff_7 (.D(d_ff_7_nq), .C(button_10_out), .Q(D6), .nQ(d_ff_7_nq));
  Button button_9 (.out(button_9_out));
  LED led_11 (.in(D5));
  D_FF d_ff_8 (.D(d_ff_8_nq), .C(button_11_out), .Q(D5), .nQ(d_ff_8_nq));
  Button button_10 (.out(button_10_out));
  LED led_12 (.in(D4));
  D_FF d_ff_9 (.D(d_ff_9_nq), .C(button_12_out), .Q(D4), .nQ(d_ff_9_nq));
  Button button_11 (.out(button_11_out));
  _74164 U5 (
    .pin1(1'b1), .pin2(Fout), .pin3(U5_pin6[3]), .pin4(U5_pin6[2]), .pin5(U5_pin6[1]), .pin6(U5_pin6[0]),
    .pin7(1'b0), .pin8(GCLK), .pin9(CLR), .pin10(U5_pin13[3]), .pin11(U5_pin13[2]), .pin12(U5_pin13[1]),
    .pin13(U5_pin13[0]), .pin14(1'b1));
  LED led_13 (.in(D3));
  D_FF d_ff_10 (.D(d_ff_10_nq), .C(button_13_out), .Q(D3), .nQ(d_ff_10_nq));
  Button button_12 (.out(button_12_out));
  LED led_14 (.in(D2));
  D_FF d_ff_11 (.D(d_ff_11_nq), .C(button_14_out), .Q(D2), .nQ(d_ff_11_nq));
  Button button_13 (.out(button_13_out));
  LED led_15 (.in(D1));
  D_FF d_ff_12 (.D(d_ff_12_nq), .C(button_15_out), .Q(D1), .nQ(d_ff_12_nq));
  Button button_14 (.out(button_14_out));
  Seven_Seg_Hex seven_seg_hex_7 (.d(U5_pin6), .dp(1'b0));
  LED led_16 (.in(D0));
  D_FF IC16_2 (.D(IC16_2_nq), .C(button_16_out), .Q(D0), .nQ(IC16_2_nq));
  Button button_15 (.out(button_15_out));
  Seven_Seg_Hex seven_seg_hex_8 (.d(U5_pin13), .dp(1'b0));
  Button button_16 (.out(button_16_out));
  Seven_Seg_Hex seven_seg_hex_9 (.d(U6_pin6), .dp(1'b0));
  Seven_Seg_Hex seven_seg_hex_10 (.d({D7, D6, D5, D4}), .dp(1'b0));
  Seven_Seg_Hex seven_seg_hex_11 (.d({U6_pin10, Aout}), .dp(1'b0));
  _74164 U6 (
    .pin1(1'b1), .pin2(U5_pin13[0]), .pin3(U6_pin6[3]), .pin4(U6_pin6[2]), .pin5(U6_pin6[1]),
    .pin6(U6_pin6[0]), .pin7(1'b0), .pin8(GCLK), .pin9(CLR), .pin10(U6_pin10[3]), .pin11(U6_pin10[2]),
    .pin12(U6_pin10[1]), .pin13(Aout), .pin14(1'b1));
  Seven_Seg_Hex seven_seg_hex_12 (.d({D3, D2, D1, D0}), .dp(1'b0));
  nand nand_1 (nand_1_out, SELX, SELX);
  nand nand_2 (nand_2_out, SELY, SELY);
  Monoflop monoflop_1 (.C(button_17_out), .R(1'b0), .Q(nLD), .nQ(LD));
  Button button_17 (.out(button_17_out));
  nand nand_3 (nand_3_out, Xout, SELX);
  nand nand_4 (nand_4_out, nand_1_out, Fout);
  nand nand_5 (nand_5_out, Yout, SELY);
  nand nand_6 (nand_6_out, nand_2_out, Fout);
  Monoflop monoflop_2 (.C(LD), .R(1'b0), .Q(SETC), .nQ(RES));
  nand nand_7 (nand_7_out, nand_3_out, nand_4_out);
  nand nand_8 (nand_8_out, nand_5_out, nand_6_out);
  _74161 U7 (
    .pin1(RST), .pin2(clk), .pin3(1'b0), .pin4(1'b0), .pin5(1'b0), .pin6(1'b0), .pin7(1'b1), .pin8(1'b0),
    .pin9(1'b1), .pin10(1'b1), .pin11(U7_pin11[3]), .pin12(U7_pin11[2]), .pin13(U7_pin11[1]),
    .pin14(U7_pin11[0]), .pin15(U7_pin15), .pin16(1'b1));
  Monoflop monoflop_3 (.C(button_18_out), .R(1'b0), .nQ(nCLRPC));  // open: Q
  Button button_18 (.out(button_18_out));
  _74164 U7_2 (
    .pin1(1'b1), .pin2(nand_7_out), .pin3(U7_2_pin6[3]), .pin4(U7_2_pin6[2]), .pin5(U7_2_pin6[1]),
    .pin6(U7_2_pin6[0]), .pin7(1'b0), .pin8(CLKX), .pin9(nCLRPC), .pin10(U7_2_pin13[3]),
    .pin11(U7_2_pin13[2]), .pin12(U7_2_pin13[1]), .pin13(U7_2_pin13[0]), .pin14(1'b1));
  _74164 U9 (
    .pin1(1'b1), .pin2(nand_8_out), .pin3(U9_pin6[3]), .pin4(U9_pin6[2]), .pin5(U9_pin6[1]),
    .pin6(U9_pin6[0]), .pin7(1'b0), .pin8(CLKY), .pin9(nCLRPC), .pin10(U9_pin13[3]), .pin11(U9_pin13[2]),
    .pin12(U9_pin13[1]), .pin13(U9_pin13[0]), .pin14(1'b1));
  nand nand_9 (nand_9_out, _8_n16, _8_n16);
  nand nand_10 (nSet, SETC, C);
  or or_1 (nClr, C, LD);
  nand nand_11 (CLR, CLA, nLD);
  nand nand_12 (nand_12_out, SETC, C);
  or or_2 (or_2_out, C, LD);
  and and_1 (and_1_out, U7_pin11[0], U7_pin11[1], U7_pin11[2]);
  Seven_Seg_Hex seven_seg_hex_13 (.d(U7_pin11), .dp(1'b0));
  _74595 IC23 (
    .pin1(IC23_pin15[2]), .pin2(IC23_pin15[1]), .pin3(IC23_pin15[0]), .pin4(IC23_pin4[3]),
    .pin5(IC23_pin4[2]), .pin6(IC23_pin4[1]), .pin7(IC23_pin4[0]), .pin8(1'b0), .pin9(IC23_pin9),
    .pin10(nCLRPC), .pin11(GCLK), .pin12(T0), .pin13(1'b0), .pin14(PCin), .pin15(IC23_pin15[3]), .pin16(1'b1));
  Seven_Seg_Hex seven_seg_hex_14 (.d(U7_2_pin6), .dp(1'b0));
  Seven_Seg_Hex seven_seg_hex_15 (.d(U9_pin6), .dp(1'b0));
  xor xor_1 (xor_1_out, Aout, nA);
  xor xor_2 (xor_2_out, nB, Rout);
  Seven_Seg_Hex seven_seg_hex_16 (.d(U7_2_pin13), .dp(1'b0));
  Seven_Seg_Hex seven_seg_hex_17 (.d(U9_pin13), .dp(1'b0));
  nand nand_13 (nand_13_out, U7_pin15, nand_9_out);
  nand nand_14 (nand_14_out, _8_n16, and_1_out);
  Seven_Seg_Hex seven_seg_hex_18 (.d(U8_pin6), .dp(1'b0));
  Seven_Seg_Hex seven_seg_hex_19 (.d(U10_pin6), .dp(1'b0));
  D_FF d_ff_13 (.D(nand_16_out), .C(clk), .Q(IX), .nQ(T0));
  nand nand_15 (nand_15_out, clk, clk);
  xor xor_3 (xor_3_out, xor_1_out, xor_2_out);
  xor xor_4 (xor_4_out, PCout, Rout);
  Seven_Seg_Hex seven_seg_hex_20 (.d({U8_pin10, Xout}), .dp(1'b0));
  Seven_Seg_Hex seven_seg_hex_21 (.d({U10_pin10, Yout}), .dp(1'b0));
  nand nand_16 (nand_16_out, nand_13_out, nand_14_out);
  _74164 U8 (
    .pin1(1'b1), .pin2(U7_2_pin13[0]), .pin3(U8_pin6[3]), .pin4(U8_pin6[2]), .pin5(U8_pin6[1]),
    .pin6(U8_pin6[0]), .pin7(1'b0), .pin8(CLKX), .pin9(nCLRPC), .pin10(U8_pin10[3]), .pin11(U8_pin10[2]),
    .pin12(U8_pin10[1]), .pin13(Xout), .pin14(1'b1));
  _74164 U10 (
    .pin1(1'b1), .pin2(U9_pin13[0]), .pin3(U10_pin6[3]), .pin4(U10_pin6[2]), .pin5(U10_pin6[1]),
    .pin6(U10_pin6[0]), .pin7(1'b0), .pin8(CLKY), .pin9(nCLRPC), .pin10(U10_pin10[3]), .pin11(U10_pin10[2]),
    .pin12(U10_pin10[1]), .pin13(Yout), .pin14(1'b1));
  nand nand_17 (GCLK, nand_15_out, RST);
  nand nand_18 (RST, RES, nand_19_out);
  nand nand_19 (nand_19_out, RST, T0);
  xor xor_5 (xor_5_out, xor_3_out, Cin);
  nand nand_20 (nand_20_out, xor_3_out, Cin);
  nand nand_21 (nand_21_out, xor_1_out, xor_2_out);
  xor xor_6 (xor_6_out, xor_4_out, PC_Cin);
  nand nand_22 (nand_22_out, xor_4_out, PC_Cin);
  nand nand_23 (nand_23_out, PCout, Rout);
  _74595 IC24 (
    .pin1(IC24_pin15[2]), .pin2(IC24_pin15[1]), .pin3(IC24_pin15[0]), .pin4(IC24_pin4[3]),
    .pin5(IC24_pin4[2]), .pin6(IC24_pin4[1]), .pin7(IC24_pin4[0]), .pin8(1'b0), .pin9(PCout), .pin10(nCLRPC),
    .pin11(GCLK), .pin12(T0), .pin13(1'b0), .pin14(IC23_pin9), .pin15(IC24_pin15[3]), .pin16(1'b1));
  nand nand_24 (nand_24_out, nand_20_out, nand_21_out);
  nand nand_25 (nand_25_out, nand_22_out, nand_23_out);
  nand nand_26 (nand_26_out, PCLD, PCLD);
  nand nand_27 (nand_27_out, xor_5_out, I0);
  nand nand_28 (nand_28_out, I1, nand_24_out);
  nand nand_29 (nand_29_out, nand_24_out, F);
  nand nand_30 (nand_30_out, xor_6_out, nand_26_out);
  nand nand_31 (nand_31_out, PCLD, nand_25_out);
  Seven_Seg_Hex seven_seg_hex_22 (.d(IC23_pin15), .dp(1'b0));
  Seven_Seg_Hex seven_seg_hex_23 (.d(IC23_pin4), .dp(1'b0));
  nand nand_32 (Fout, nand_27_out, nand_28_out);
  nand nand_33 (Cout, nand_29_out, nand_29_out);
  nand nand_34 (PCin, nand_30_out, nand_31_out);
  Seven_Seg_Hex seven_seg_hex_24 (.d(IC24_pin15), .dp(1'b0));
  Seven_Seg_Hex seven_seg_hex_25 (.d(IC24_pin4), .dp(1'b0));
  _74138 _74138_1 (
    .pin1(in_8), .pin2(in_9), .pin3(in_10), .pin4(GCLK), .pin5(1'b0), .pin6(1'b1), .pin8(1'b0), .pin9(CLKE),
    .pin10(CLKD), .pin11(CLKC), .pin12(CLKB), .pin13(CLKY), .pin14(CLKX), .pin16(1'b1));  // open: pin7, pin15
  _74138 _74138_2 (
    .pin1(in_8), .pin2(in_9), .pin3(in_10), .pin4(1'b0), .pin5(1'b0), .pin6(1'b1), .pin8(1'b0), .pin13(SELY),
    .pin14(SELX), .pin16(1'b1));  // open: pin7, pin9, pin10, pin11, pin12, pin15
  _74151 _74151_1 (
    .pin1(1'b0), .pin2(Yout), .pin3(Xout), .pin4(Sout), .pin5(Rout), .pin7(1'b0), .pin8(1'b0), .pin9(in_10),
    .pin10(in_9), .pin11(in_8), .pin12(1'b0), .pin13(1'b0), .pin14(1'b0), .pin15(1'b0), .pin16(1'b1));  // open: pin6
  D_FF_AS d_ff_as_1 (.Set(~nSet), .D(Cout), .C(GCLK), .Clr(~nClr), .Q(Cin));  // open: nQ
  D_FF_AS d_ff_as_2 (.Set(~nand_12_out), .D(nand_25_out), .C(GCLK), .Clr(~or_2_out), .Q(PC_Cin));  // open: nQ
  _74595 IC13 (
    .pin1(IC13_pin15[2]), .pin2(IC13_pin15[1]), .pin3(IC13_pin15[0]), .pin4(IC13_pin4[3]),
    .pin5(IC13_pin4[2]), .pin6(IC13_pin4[1]), .pin7(IC13_pin4[0]), .pin8(1'b0), .pin9(IC13_pin9),
    .pin10(RES), .pin11(GCLK), .pin12(T0), .pin13(1'b0), .pin14(Fout), .pin15(IC13_pin15[3]), .pin16(1'b1));
  _74595 IC15 (
    .pin1(IC15_pin15[2]), .pin2(IC15_pin15[1]), .pin3(IC15_pin15[0]), .pin4(IC15_pin4[3]),
    .pin5(IC15_pin4[2]), .pin6(IC15_pin4[1]), .pin7(IC15_pin4[0]), .pin8(1'b0), .pin9(IC15_pin9),
    .pin10(nCLRPC), .pin11(CLKB), .pin12(T0), .pin13(1'b0), .pin14(Fout), .pin15(IC15_pin15[3]), .pin16(1'b1));
  _74595 IC17_3 (
    .pin1(IC17_3_pin15[2]), .pin2(IC17_3_pin15[1]), .pin3(IC17_3_pin15[0]), .pin4(IC17_3_pin4[3]),
    .pin5(IC17_3_pin4[2]), .pin6(IC17_3_pin4[1]), .pin7(IC17_3_pin4[0]), .pin8(1'b0), .pin9(IC17_3_pin9),
    .pin10(nCLRPC), .pin11(CLKC), .pin12(T0), .pin13(1'b0), .pin14(Fout), .pin15(IC17_3_pin15[3]),
    .pin16(1'b1));
  _74595 IC19 (
    .pin1(IC19_pin15[2]), .pin2(IC19_pin15[1]), .pin3(IC19_pin15[0]), .pin4(IC19_pin4[3]),
    .pin5(IC19_pin4[2]), .pin6(IC19_pin4[1]), .pin7(IC19_pin4[0]), .pin8(1'b0), .pin9(IC19_pin9),
    .pin10(nCLRPC), .pin11(CLKD), .pin12(T0), .pin13(1'b0), .pin14(Fout), .pin15(IC19_pin15[3]), .pin16(1'b1));
  _74595 IC21 (
    .pin1(IC21_pin15[2]), .pin2(IC21_pin15[1]), .pin3(IC21_pin15[0]), .pin4(IC21_pin4[3]),
    .pin5(IC21_pin4[2]), .pin6(IC21_pin4[1]), .pin7(IC21_pin4[0]), .pin8(1'b0), .pin9(IC21_pin9),
    .pin10(nCLRPC), .pin11(CLKE), .pin12(T0), .pin13(1'b0), .pin14(Fout), .pin15(IC21_pin15[3]), .pin16(1'b1));
  _74595 IC16_3 (
    .pin1(IC16_3_pin15[2]), .pin2(IC16_3_pin15[1]), .pin3(IC16_3_pin15[0]), .pin4(IC16_3_pin4[3]),
    .pin5(IC16_3_pin4[2]), .pin6(IC16_3_pin4[1]), .pin7(IC16_3_pin4[0]), .pin8(1'b0), .pin9(IC16_3_pin9),
    .pin10(nCLRPC), .pin11(CLKB), .pin12(T0), .pin13(1'b0), .pin14(IC15_pin9), .pin15(IC16_3_pin15[3]),
    .pin16(1'b1));
  _74595 IC18 (
    .pin1(IC18_pin15[2]), .pin2(IC18_pin15[1]), .pin3(IC18_pin15[0]), .pin4(IC18_pin4[3]),
    .pin5(IC18_pin4[2]), .pin6(IC18_pin4[1]), .pin7(IC18_pin4[0]), .pin8(1'b0), .pin9(IC18_pin9),
    .pin10(nCLRPC), .pin11(CLKC), .pin12(T0), .pin13(1'b0), .pin14(IC17_3_pin9), .pin15(IC18_pin15[3]),
    .pin16(1'b1));
  _74595 IC20 (
    .pin1(IC20_pin15[2]), .pin2(IC20_pin15[1]), .pin3(IC20_pin15[0]), .pin4(IC20_pin4[3]),
    .pin5(IC20_pin4[2]), .pin6(IC20_pin4[1]), .pin7(IC20_pin4[0]), .pin8(1'b0), .pin9(IC20_pin9),
    .pin10(nCLRPC), .pin11(CLKD), .pin12(T0), .pin13(1'b0), .pin14(IC19_pin9), .pin15(IC20_pin15[3]),
    .pin16(1'b1));
  _74595 IC22 (
    .pin1(IC22_pin15[2]), .pin2(IC22_pin15[1]), .pin3(IC22_pin15[0]), .pin4(IC22_pin4[3]),
    .pin5(IC22_pin4[2]), .pin6(IC22_pin4[1]), .pin7(IC22_pin4[0]), .pin8(1'b0), .pin9(IC22_pin9),
    .pin10(nCLRPC), .pin11(CLKE), .pin12(T0), .pin13(1'b0), .pin14(IC21_pin9), .pin15(IC22_pin15[3]),
    .pin16(1'b1));
  _74595 IC14 (
    .pin1(BUS6), .pin2(BUS5), .pin3(BUS4), .pin4(BUS3), .pin5(BUS2), .pin6(BUS1), .pin7(BUS0), .pin8(1'b0),
    .pin9(IC14_pin9), .pin10(RES), .pin11(GCLK), .pin12(T0), .pin13(1'b0), .pin14(IC13_pin9), .pin15(BUS7),
    .pin16(1'b1));
  Seven_Seg_Hex seven_seg_hex_26 (.d(IC13_pin15), .dp(1'b0));
  DiodeForward diodeforward_1 (.in(IC13_pin15[3]), .out(diodeforward_1_out));
  DiodeForward diodeforward_2 (.in(IC13_pin15[2]), .out(diodeforward_1_out));
  DiodeForward diodeforward_3 (.in(IC13_pin15[1]), .out(diodeforward_1_out));
  DiodeForward diodeforward_4 (.in(IC13_pin15[0]), .out(diodeforward_1_out));
  DiodeForward diodeforward_5 (.in(IC13_pin4[3]), .out(diodeforward_1_out));
  DiodeForward diodeforward_6 (.in(IC13_pin4[2]), .out(diodeforward_1_out));
  DiodeForward diodeforward_7 (.in(IC13_pin4[1]), .out(diodeforward_1_out));
  DiodeForward diodeforward_8 (.in(IC13_pin4[0]), .out(diodeforward_1_out));
  DiodeForward diodeforward_9 (.in(BUS7), .out(diodeforward_1_out));
  DiodeForward diodeforward_10 (.in(BUS6), .out(diodeforward_1_out));
  DiodeForward diodeforward_11 (.in(BUS5), .out(diodeforward_1_out));
  DiodeForward diodeforward_12 (.in(BUS4), .out(diodeforward_1_out));
  DiodeForward diodeforward_13 (.in(BUS3), .out(diodeforward_1_out));
  DiodeForward diodeforward_14 (.in(BUS2), .out(diodeforward_1_out));
  DiodeForward diodeforward_15 (.in(BUS1), .out(diodeforward_1_out));
  DiodeForward diodeforward_16 (.in(BUS0), .out(diodeforward_1_out));
  Seven_Seg_Hex seven_seg_hex_27 (.d(IC15_pin15), .dp(1'b0));
  Seven_Seg_Hex seven_seg_hex_28 (.d(IC17_3_pin15), .dp(1'b0));
  Seven_Seg_Hex seven_seg_hex_29 (.d(IC19_pin15), .dp(1'b0));
  Seven_Seg_Hex seven_seg_hex_30 (.d(IC21_pin15), .dp(1'b0));
  _74574 _74574_2 (
    .pin1(1'b0), .pin2(Fout), .pin3(Q0), .pin4(Q1), .pin5(Q2), .pin6(Q3), .pin7(Q4), .pin8(Q5), .pin9(Q6),
    .pin10(1'b0), .pin11(GCLK), .pin12(Q7), .pin13(Q6), .pin14(Q5), .pin15(Q4), .pin16(Q3), .pin17(Q2),
    .pin18(Q1), .pin19(Q0), .pin20(1'b1));
  Seven_Seg_Hex seven_seg_hex_31 (.d(IC13_pin4), .dp(1'b0));
  LED led_17 (.in(diodeforward_1_out));
  PullDown pulldown_1 (.out(diodeforward_1_out));
  Seven_Seg_Hex seven_seg_hex_32 (.d(IC15_pin4), .dp(1'b0));
  Seven_Seg_Hex seven_seg_hex_33 (.d(IC17_3_pin4), .dp(1'b0));
  Seven_Seg_Hex seven_seg_hex_34 (.d(IC19_pin4), .dp(1'b0));
  Seven_Seg_Hex seven_seg_hex_35 (.d(IC21_pin4), .dp(1'b0));
  Seven_Seg_Hex seven_seg_hex_36 (.d({BUS7, BUS6, BUS5, BUS4}), .dp(1'b0));
  nand nand_35 (nZERO, diodeforward_1_out, diodeforward_1_out);
  Seven_Seg_Hex seven_seg_hex_37 (.d(IC16_3_pin15), .dp(1'b0));
  Seven_Seg_Hex seven_seg_hex_38 (.d(IC18_pin15), .dp(1'b0));
  Seven_Seg_Hex seven_seg_hex_39 (.d(IC20_pin15), .dp(1'b0));
  Seven_Seg_Hex seven_seg_hex_40 (.d(IC22_pin15), .dp(1'b0));
  Seven_Seg_Hex seven_seg_hex_41 (.d({Q0, Q1, Q2, Q3}), .dp(1'b0));
  Seven_Seg_Hex seven_seg_hex_42 (.d({BUS3, BUS2, BUS1, BUS0}), .dp(1'b0));
  Seven_Seg_Hex seven_seg_hex_43 (.d(IC16_3_pin4), .dp(1'b0));
  Seven_Seg_Hex seven_seg_hex_44 (.d(IC18_pin4), .dp(1'b0));
  Seven_Seg_Hex seven_seg_hex_45 (.d(IC20_pin4), .dp(1'b0));
  Seven_Seg_Hex seven_seg_hex_46 (.d(IC22_pin4), .dp(1'b0));
  Seven_Seg_Hex seven_seg_hex_47 (.d({Q4, Q5, Q6, Q7}), .dp(1'b0));

  // Other names for the same wires on the sheet: nRRES = nCLRPC

  // Notes on the sheet:
  //   clk: Hz: 16
  //   SPIder Bit Serial CPU
  //   Acc to Bus
  //   Instruction Input
  //   High Address
  //   PC LOW
  //   8/~16
  //   Instruction Decode
  //   CLA
  //   C
  //   F
  //   ~B
  //   ~A
  //   I0
  //   I1
  //   LD-H
  //   LD-L
  //   AND
  //   OR
  //   XOR
  //   ADD
  //   SUB
  //   SWAP
  //   JMP
  //   PC HI
  //   32K RAM
  //   16 bit Switch Register S
  //   ENTER H
  //   Data Input
  //   ENTER L
  //   16 bit Shift Register A
  //   ACCUMULATOR
  //   LOAD
  //   8 or 16-bit sequence
  //   CLR PC
  //   Clock Sequencer
  //   CLR ACC
  //   # Clock
  //   REGISTER X
  //   REGISTER Y
  //   Carry is only set before Bit 0 of an operation
  //   Any residual carry is cleared before an operation
  //   Program Counter
  //   Suppress Carry
  //   Register Select
  //   Carry FF
  //   Output Display Registers
  //   REGISTER B
  //   REGISTER C
  //   REGISTER D
  //   REGISTER E
  //   OUTPUT
endmodule
