// Digital circuit spider_no_monoflops_2.dig as structural Verilog
module spider_no_monoflops_2 (
  input  clk,
  input  in_2,
  input  in_3,
  input  in_4,
  output LD,
  output SETC,
  output GCLK,
  output T0,
  output T1
);

  wire _74173_1_pin4, _74173_1_pin5, _74173_1_pin6, ADD, AND, Aout, Bout, BUS0, BUS1, BUS2, BUS3, BUS4, BUS5,
       BUS6, BUS7, button_2_out, button_3_out, button_4_out, button_5_out, button_6_out, button_7_out,
       button_8_out, button_9_out, button_10_out, button_11_out, button_12_out, button_13_out, button_14_out,
       button_15_out, button_16_out, button_17_out, C, Cin, CLA, CLR, Cout, D0, D1, D2, D3, D4, D5, D6, D7,
       D8, D9, D10, D11, D12, D13, D14, D15, d_ff_1_nq, d_ff_2_nq, d_ff_3_nq, d_ff_4_nq, d_ff_5_nq,
       d_ff_6_nq, d_ff_7_nq, d_ff_8_nq, d_ff_9_nq, d_ff_10_nq, d_ff_11_nq, d_ff_12_nq, diodebackward_1_out,
       diodebackward_6_out, diodeforward_1_out, F, Fout, I0, I1, IC16_2_nq, IC16_nq, IC17_2_nq, IC17_nq, IX,
       LD_t, LOAD, nA, nand_2_out, nand_6_out, nand_7_out, nand_9_out, nand_10_out, nand_11_out, nand_12_out,
       nand_13_out, nand_14_out, nand_15_out, nB, nJMP, nRES, OR, pullup_1_out, pullup_3_out, pullup_5_out,
       pullup_6_out, pullup_7_out, RCO, RST, ST, SUB, U3_pin9, U8_pin9, U9_pin9, XOR, xor_1_out, xor_2_out,
       xor_3_out, xor_4_out, ZERO;
  wire [3:0] U5_pin6, U5_pin13, U6_pin6, U7_pin12, U8_pin4, U8_pin15;
  wire [3:1] U6_pin12;

  _74173 _74173_1 (
    .pin1(1'b0), .pin2(1'b0), .pin4(_74173_1_pin4), .pin5(_74173_1_pin5), .pin6(_74173_1_pin6), .pin7(LD_t),
    .pin8(1'b0), .pin9(1'b0), .pin10(1'b0), .pin11(in_2), .pin12(in_3), .pin13(in_4), .pin14(1'b0),
    .pin15(1'b0), .pin16(1'b1));  // open: pin3
  _74165 U3 (
    .pin1(LD), .pin2(GCLK), .pin3(D11), .pin4(D10), .pin5(D9), .pin6(D8), .pin8(1'b0), .pin9(U3_pin9),
    .pin10(1'b0), .pin11(D15), .pin12(D14), .pin13(D13), .pin14(D12), .pin15(1'b0), .pin16(1'b1));  // open: pin7
  _74138 U1 (
    .pin1(_74173_1_pin6), .pin2(_74173_1_pin5), .pin3(_74173_1_pin4), .pin4(1'b0), .pin5(1'b0), .pin6(1'b1),
    .pin7(nJMP), .pin8(1'b0), .pin9(ST), .pin10(SUB), .pin11(ADD), .pin12(XOR), .pin13(OR), .pin14(AND),
    .pin15(LOAD), .pin16(1'b1));
  Button button_1 ();  // open: out
  DiodeBackward diodebackward_1 (.in(LOAD), .out(diodebackward_1_out));
  PullUp pullup_1 (.out(pullup_1_out));
  PullUp pullup_2 (.out(diodebackward_1_out));
  DiodeBackward diodebackward_2 (.in(LOAD), .out(pullup_1_out));
  DiodeBackward diodebackward_3 (.in(ADD), .out(pullup_1_out));
  DiodeBackward diodebackward_4 (.in(SUB), .out(pullup_1_out));
  DiodeBackward diodebackward_5 (.in(nJMP), .out(pullup_1_out));
  _74165 U4 (
    .pin1(LD), .pin2(GCLK), .pin3(D3), .pin4(D2), .pin5(D1), .pin6(D0), .pin8(1'b0), .pin9(Bout),
    .pin10(U3_pin9), .pin11(D7), .pin12(D6), .pin13(D5), .pin14(D4), .pin15(1'b0), .pin16(1'b1));  // open: pin7
  PullUp pullup_3 (.out(pullup_3_out));
  DiodeBackward diodebackward_6 (.in(SUB), .out(diodebackward_6_out));
  DiodeBackward diodebackward_7 (.in(SUB), .out(pullup_3_out));
  PullUp pullup_4 (.out(diodebackward_6_out));
  PullUp pullup_5 (.out(pullup_5_out));
  PullUp pullup_6 (.out(pullup_6_out));
  DiodeBackward diodebackward_8 (.in(AND), .out(pullup_6_out));
  DiodeBackward diodebackward_9 (.in(OR), .out(pullup_6_out));
  PullUp pullup_7 (.out(pullup_7_out));
  DiodeBackward diodebackward_10 (.in(LOAD), .out(pullup_7_out));
  DiodeBackward diodebackward_11 (.in(OR), .out(pullup_7_out));
  DiodeBackward diodebackward_12 (.in(XOR), .out(pullup_7_out));
  DiodeBackward diodebackward_13 (.in(ADD), .out(pullup_7_out));
  DiodeBackward diodebackward_14 (.in(SUB), .out(pullup_7_out));
  DiodeBackward diodebackward_15 (.in(ST), .out(pullup_7_out));
  _74540 U2 (
    .pin1(1'b0), .pin2(pullup_7_out), .pin3(pullup_6_out), .pin4(pullup_5_out), .pin5(diodebackward_6_out),
    .pin6(pullup_3_out), .pin7(pullup_1_out), .pin8(diodebackward_1_out), .pin9(1'b0), .pin10(1'b0),
    .pin12(CLA), .pin13(F), .pin14(C), .pin15(nB), .pin16(nA), .pin17(I1), .pin18(I0), .pin19(1'b0),
    .pin20(1'b1));  // open: pin11
  _74595 U8 (
    .pin1(U8_pin15[2]), .pin2(U8_pin15[1]), .pin3(U8_pin15[0]), .pin4(U8_pin4[3]), .pin5(U8_pin4[2]),
    .pin6(U8_pin4[1]), .pin7(U8_pin4[0]), .pin8(1'b0), .pin9(U8_pin9), .pin10(nRES), .pin11(GCLK),
    .pin12(T0), .pin13(1'b0), .pin14(Fout), .pin15(U8_pin15[3]), .pin16(1'b1));
  LED led_1 (.in(D15));
  D_FF IC17 (.D(IC17_nq), .C(button_2_out), .Q(D15), .nQ(IC17_nq));
  Button button_2 (.out(button_2_out));
  LED led_2 (.in(D14));
  D_FF d_ff_1 (.D(d_ff_1_nq), .C(button_3_out), .Q(D14), .nQ(d_ff_1_nq));
  Button button_3 (.out(button_3_out));
  LED led_3 (.in(D13));
  D_FF d_ff_2 (.D(d_ff_2_nq), .C(button_4_out), .Q(D13), .nQ(d_ff_2_nq));
  Button button_4 (.out(button_4_out));
  LED led_4 (.in(D12));
  D_FF d_ff_3 (.D(d_ff_3_nq), .C(button_5_out), .Q(D12), .nQ(d_ff_3_nq));
  Button button_5 (.out(button_5_out));
  _74595 U9 (
    .pin1(BUS6), .pin2(BUS5), .pin3(BUS4), .pin4(BUS3), .pin5(BUS2), .pin6(BUS1), .pin7(BUS0), .pin8(1'b0),
    .pin9(U9_pin9), .pin10(nRES), .pin11(GCLK), .pin12(T0), .pin13(1'b0), .pin14(U8_pin9), .pin15(BUS7),
    .pin16(1'b1));
  LED led_5 (.in(D11));
  D_FF d_ff_4 (.D(d_ff_4_nq), .C(button_6_out), .Q(D11), .nQ(d_ff_4_nq));
  Button button_6 (.out(button_6_out));
  LED led_6 (.in(D10));
  D_FF d_ff_5 (.D(d_ff_5_nq), .C(button_7_out), .Q(D10), .nQ(d_ff_5_nq));
  Button button_7 (.out(button_7_out));
  LED led_7 (.in(D9));
  D_FF d_ff_6 (.D(d_ff_6_nq), .C(button_8_out), .Q(D9), .nQ(d_ff_6_nq));
  Button button_8 (.out(button_8_out));
  LED led_8 (.in(D8));
  D_FF IC17_2 (.D(IC17_2_nq), .C(button_9_out), .Q(D8), .nQ(IC17_2_nq));
  Button button_9 (.out(button_9_out));
  DiodeForward diodeforward_1 (.in(U8_pin15[3]), .out(diodeforward_1_out));
  DiodeForward diodeforward_2 (.in(U8_pin15[2]), .out(diodeforward_1_out));
  DiodeForward diodeforward_3 (.in(U8_pin15[1]), .out(diodeforward_1_out));
  DiodeForward diodeforward_4 (.in(U8_pin15[0]), .out(diodeforward_1_out));
  DiodeForward diodeforward_5 (.in(U8_pin4[3]), .out(diodeforward_1_out));
  DiodeForward diodeforward_6 (.in(U8_pin4[2]), .out(diodeforward_1_out));
  DiodeForward diodeforward_7 (.in(U8_pin4[1]), .out(diodeforward_1_out));
  DiodeForward diodeforward_8 (.in(U8_pin4[0]), .out(diodeforward_1_out));
  DiodeForward diodeforward_9 (.in(BUS7), .out(diodeforward_1_out));
  DiodeForward diodeforward_10 (.in(BUS6), .out(diodeforward_1_out));
  DiodeForward diodeforward_11 (.in(BUS5), .out(diodeforward_1_out));
  DiodeForward diodeforward_12 (.in(BUS4), .out(diodeforward_1_out));
  DiodeForward diodeforward_13 (.in(BUS3), .out(diodeforward_1_out));
  DiodeForward diodeforward_14 (.in(BUS2), .out(diodeforward_1_out));
  DiodeForward diodeforward_15 (.in(BUS1), .out(diodeforward_1_out));
  DiodeForward diodeforward_16 (.in(BUS0), .out(diodeforward_1_out));
  Seven_Seg_Hex seven_seg_hex_1 (.d({D15, D14, D13, D12}), .dp(1'b0));
  Seven_Seg_Hex seven_seg_hex_2 (.d(U8_pin15), .dp(1'b0));
  Seven_Seg_Hex seven_seg_hex_3 (.d({D11, D10, D9, D8}), .dp(1'b0));
  Seven_Seg_Hex seven_seg_hex_4 (.d(U8_pin4), .dp(1'b0));
  PullDown pulldown_1 (.out(diodeforward_1_out));
  Seven_Seg_Hex seven_seg_hex_5 (.d({BUS7, BUS6, BUS5, BUS4}), .dp(1'b0));
  nand nand_1 (ZERO, diodeforward_1_out, diodeforward_1_out);
  LED led_9 (.in(D7));
  D_FF IC16 (.D(IC16_nq), .C(button_10_out), .Q(D7), .nQ(IC16_nq));
  Button button_10 (.out(button_10_out));
  Seven_Seg_Hex seven_seg_hex_6 (.d({BUS3, BUS2, BUS1, BUS0}), .dp(1'b0));
  LED led_10 (.in(ZERO));
  LED led_11 (.in(D6));
  D_FF d_ff_7 (.D(d_ff_7_nq), .C(button_11_out), .Q(D6), .nQ(d_ff_7_nq));
  Button button_11 (.out(button_11_out));
  LED led_12 (.in(D5));
  D_FF d_ff_8 (.D(d_ff_8_nq), .C(button_12_out), .Q(D5), .nQ(d_ff_8_nq));
  Button button_12 (.out(button_12_out));
  LED led_13 (.in(D4));
  D_FF d_ff_9 (.D(d_ff_9_nq), .C(button_13_out), .Q(D4), .nQ(d_ff_9_nq));
  Button button_13 (.out(button_13_out));
  LED led_14 (.in(D3));
  D_FF d_ff_10 (.D(d_ff_10_nq), .C(button_14_out), .Q(D3), .nQ(d_ff_10_nq));
  Button button_14 (.out(button_14_out));
  LED led_15 (.in(D2));
  D_FF d_ff_11 (.D(d_ff_11_nq), .C(button_15_out), .Q(D2), .nQ(d_ff_11_nq));
  Button button_15 (.out(button_15_out));
  LED led_16 (.in(D1));
  D_FF d_ff_12 (.D(d_ff_12_nq), .C(button_16_out), .Q(D1), .nQ(d_ff_12_nq));
  Button button_16 (.out(button_16_out));
  _74164 U5 (
    .pin1(1'b1), .pin2(Fout), .pin3(U5_pin6[3]), .pin4(U5_pin6[2]), .pin5(U5_pin6[1]), .pin6(U5_pin6[0]),
    .pin7(1'b0), .pin8(GCLK), .pin9(CLR), .pin10(U5_pin13[3]), .pin11(U5_pin13[2]), .pin12(U5_pin13[1]),
    .pin13(U5_pin13[0]), .pin14(1'b1));
  LED led_17 (.in(D0));
  D_FF IC16_2 (.D(IC16_2_nq), .C(button_17_out), .Q(D0), .nQ(IC16_2_nq));
  Button button_17 (.out(button_17_out));
  Seven_Seg_Hex seven_seg_hex_7 (.d({D7, D6, D5, D4}), .dp(1'b0));
  nand nand_2 (nand_2_out, clk, clk);
  nand nand_3 (RST, nRES, SETC);
  nand nand_4 (SETC, RST, T0);
  Seven_Seg_Hex seven_seg_hex_8 (.d({D3, D2, D1, D0}), .dp(1'b0));
  Seven_Seg_Hex seven_seg_hex_9 (.d(U5_pin6), .dp(1'b0));
  nand nand_5 (GCLK, nand_2_out, RST);
  Seven_Seg_Hex seven_seg_hex_10 (.d(U5_pin13), .dp(1'b0));
  Seven_Seg_Hex seven_seg_hex_11 (.d(U6_pin6), .dp(1'b0));
  Seven_Seg_Hex seven_seg_hex_12 (.d({U6_pin12, Aout}), .dp(1'b0));
  _74164 U6 (
    .pin1(1'b1), .pin2(U5_pin13[0]), .pin3(U6_pin6[3]), .pin4(U6_pin6[2]), .pin5(U6_pin6[1]),
    .pin6(U6_pin6[0]), .pin7(1'b0), .pin8(GCLK), .pin9(CLR), .pin10(U6_pin12[3]), .pin11(U6_pin12[2]),
    .pin12(U6_pin12[1]), .pin13(Aout), .pin14(1'b1));
  xor xor_1 (xor_1_out, Aout, nA);
  xor xor_2 (xor_2_out, nB, Bout);
  nand nand_6 (nand_6_out, SETC, C);
  nand nand_7 (nand_7_out, C, C);
  nand nand_8 (CLR, CLA, LD_t);
  _74161 U7 (
    .pin1(RST), .pin2(clk), .pin3(1'b0), .pin4(1'b0), .pin5(1'b0), .pin6(1'b0), .pin7(1'b1), .pin8(1'b0),
    .pin9(1'b1), .pin10(1'b1), .pin11(U7_pin12[3]), .pin12(U7_pin12[2]), .pin13(U7_pin12[1]),
    .pin14(U7_pin12[0]), .pin15(RCO), .pin16(1'b1));
  xor xor_3 (xor_3_out, xor_1_out, xor_2_out);
  nand nand_9 (nand_9_out, nand_7_out, LD_t);
  xor xor_4 (xor_4_out, xor_3_out, Cin);
  nand nand_10 (nand_10_out, xor_3_out, Cin);
  nand nand_11 (nand_11_out, xor_1_out, xor_2_out);
  Seven_Seg_Hex seven_seg_hex_13 (.d(U7_pin12), .dp(1'b0));
  nand nand_12 (nand_12_out, nand_10_out, nand_11_out);
  nand nand_13 (nand_13_out, xor_4_out, I0);
  nand nand_14 (nand_14_out, I1, nand_12_out);
  nand nand_15 (nand_15_out, nand_12_out, F);
  _7474 _7474_1 (
    .pin1(1'b1), .pin2(LD_t), .pin3(clk), .pin4(1'b1), .pin6(T1), .pin7(1'b0), .pin8(T0), .pin9(LD_t),
    .pin10(1'b1), .pin11(clk), .pin12(RCO), .pin13(1'b1), .pin14(1'b1));  // open: pin5
  nand nand_16 (Fout, nand_13_out, nand_14_out);
  nand nand_17 (Cout, nand_15_out, nand_15_out);
  _74139 _74139_1 (
    .pin1(1'b0), .pin2(1'b0), .pin3(1'b0), .pin8(1'b0), .pin10(nRES), .pin11(LD), .pin13(T0), .pin14(LD_t),
    .pin15(RST), .pin16(1'b1));  // open: pin4, pin5, pin6, pin7, pin9, pin12
  _7474 _7474_2 (
    .pin1(nand_9_out), .pin2(Cout), .pin3(GCLK), .pin4(nand_6_out), .pin5(Cin), .pin7(1'b0), .pin9(IX),
    .pin10(1'b1), .pin11(clk), .pin12(RCO), .pin13(1'b1), .pin14(1'b1));  // open: pin6, pin8
  LED led_18 (.in(Cin));

  // Other names for the same wires on the sheet: nLD = LD; nRST = SETC

  // Notes on the sheet:
  //   clk: Hz: 2
  //   Instruction Register
  //   spider 0
  //   STEP/RUN
  //   16 bit Shift Register B
  //   Instruction Decode
  //   F
  //   CLA
  //   C
  //   ~B
  //   I1
  //   ~A
  //   I0
  //   LOAD
  //   AND
  //   OR
  //   XOR
  //   ADD
  //   SUB
  //   STORE
  //   JMP
  //   Output Display Registers
  //   ENTER H
  //   Data Input
  //   OUTPUT REGISTER
  //   ZERO
  //   ENTER L
  //   16 bit Shift Register A
  //   ACCUMULATOR
  //   ALU
  //   CLR ACC
  //   Clock Sequencer
  //   Spider 0 Bit serial CPU Testbed
  //   Any residual carry is cleared before an operation
  //   # Clock
  //   Carry is only set before Bit 0 of an operation
  //   Suppress Carry
  //   T0 Gen
  //   Carry FF
  //   CARRY
endmodule
