// Digital circuit sync_1.dig as structural Verilog
module sync_1 (
  input  clk,
  output nLOAD,
  output GCLK,
  output nRCLK,
  output RCO,
  output TC,
  output nCE
);

  wire button_1_out, LD, n2SD, nand_2_out, nand_3_out, nand_5_out, nRES, nT0, RCLK, RST, SETC, U30_pin6;
  wire [3:0] U7_pin11, U8_pin11;

  Reset reset_1 (.out(n2SD));
  nand nand_1 (RST, nRES, nand_2_out);
  nand nand_2 (nand_2_out, RST, nT0);
  nand nand_3 (nand_3_out, clk, clk);
  nand nand_4 (GCLK, RST, nand_3_out);
  _74161 U7 (
    .pin1(RST), .pin2(clk), .pin3(1'b0), .pin4(1'b0), .pin5(1'b0), .pin6(1'b0), .pin7(1'b1), .pin8(1'b0),
    .pin9(1'b1), .pin10(1'b1), .pin11(U7_pin11[3]), .pin12(U7_pin11[2]), .pin13(U7_pin11[1]),
    .pin14(U7_pin11[0]), .pin15(RCO), .pin16(1'b1));
  _7474 U31 (
    .pin1(1'b1), .pin2(1'b1), .pin3(1'b1), .pin4(1'b1), .pin7(1'b0), .pin8(nT0), .pin10(1'b1), .pin11(clk),
    .pin12(RCO), .pin13(1'b1), .pin14(1'b1));  // open: pin5, pin6, pin9
  Seven_Seg_Hex seven_seg_hex_1 (.d(U7_pin11), .dp(1'b0));
  Monoflop monoflop_1 (.C(nLOAD), .R(1'b0), .Q(SETC), .nQ(nRES));
  Monoflop monoflop_2 (.C(button_1_out), .R(1'b0), .Q(LD), .nQ(nLOAD));
  Button button_1 (.out(button_1_out));
  nand nand_5 (nand_5_out, GCLK, GCLK);
  _74161 U8 (
    .pin1(nLOAD), .pin2(nand_5_out), .pin3(1'b0), .pin4(1'b0), .pin5(1'b0), .pin6(1'b0), .pin7(1'b1),
    .pin8(1'b0), .pin9(1'b1), .pin10(1'b1), .pin11(U8_pin11[3]), .pin12(U8_pin11[2]), .pin13(U8_pin11[1]),
    .pin14(U8_pin11[0]), .pin15(TC), .pin16(1'b1));
  _7474 U30 (
    .pin1(nRCLK), .pin2(1'b1), .pin3(1'b1), .pin4(nLOAD), .pin6(U30_pin6), .pin7(1'b0), .pin8(nRCLK),
    .pin9(RCLK), .pin10(1'b1), .pin11(GCLK), .pin12(TC), .pin13(1'b1), .pin14(1'b1));  // open: pin5
  or or_1 (nCE, U30_pin6, RCLK);
  Seven_Seg_Hex seven_seg_hex_2 (.d(U8_pin11), .dp(1'b0));

  // Other names for the same wires on the sheet: nLD = nLOAD

  // Notes on the sheet:
  //   clk: Hz: 2
  //   Input & Clock
  //   Clock Sequencer
  //   # Clock
  //   Slave Sequencer
endmodule
