// Digital circuit timing_generator_1.dig as structural Verilog
module timing_generator_1 (
  input  clk,
  output RST,
  output GATED_CLK,
  output T0,
  output T1
);

  wire _74139_1_pin9, _74139_1_pin11, _74139_1_pin12, LD, nand_1_out, nRES, nRST, RCO;
  wire [3:0] U7_pin11;

  _74139 _74139_1 (
    .pin1(1'b0), .pin2(1'b0), .pin3(1'b0), .pin8(1'b0), .pin9(_74139_1_pin9), .pin10(nRES),
    .pin11(_74139_1_pin11), .pin12(_74139_1_pin12), .pin13(T0), .pin14(LD), .pin15(RST), .pin16(1'b1));  // open: pin4, pin5, pin6, pin7
  LED nLD (.in(_74139_1_pin11));
  LED u_nRES (.in(nRES));
  nand nand_1 (nand_1_out, clk, clk);
  nand nand_2 (RST, nRES, nRST);
  nand nand_3 (nRST, RST, T0);
  nand nand_4 (GATED_CLK, nand_1_out, RST);
  _74161 U7 (
    .pin1(RST), .pin2(clk), .pin3(1'b0), .pin4(1'b0), .pin5(1'b0), .pin6(1'b0), .pin7(1'b1), .pin8(1'b0),
    .pin9(1'b1), .pin10(1'b1), .pin11(U7_pin11[3]), .pin12(U7_pin11[2]), .pin13(U7_pin11[1]),
    .pin14(U7_pin11[0]), .pin15(RCO), .pin16(1'b1));
  LED led_1 (.in(GATED_CLK));
  Seven_Seg_Hex seven_seg_hex_1 (.d(U7_pin11), .dp(1'b0));
  _7474 _7474_1 (
    .pin1(1'b1), .pin2(LD), .pin3(clk), .pin4(1'b1), .pin6(T1), .pin7(1'b0), .pin8(T0), .pin9(LD),
    .pin10(1'b1), .pin11(clk), .pin12(RCO), .pin13(1'b1), .pin14(1'b1));  // open: pin5
  LED u_LD (.in(LD));

  // Other names for the same wires on the sheet: GCLK = GATED_CLK

  // Notes on the sheet:
  //   clk: Hz: 2
  //   Clock Sequencer
  //   # Clock
  //   T0 Gen
endmodule
