// Digital circuit universal_gate.dig as structural Verilog
module universal_gate (
  input  I1,
  input  I0,
  input  A,
  input  B,
  input  Din,
  input  CLK,
  input  in_10,
  input  in_11,
  input  in_12,
  input  in_13,
  input  CLK_2,
  input  in_16,
  input  in_17,
  input  I3,
  input  I2,
  input  B_2,
  input  A_2,
  input  B_3,
  input  C,
  input  N,
  input  INC,
  input  LD,
  input  INC_IN,
  input  D0,
  input  CLK_3,
  input  in_33,
  input  in_34,
  output Fout,
  output Q0,
  output out_9,
  output Q1,
  output out_25,
  output INC_OUT,
  output Q0_2
);

  wire nand_1_out, nand_2_out, nand_3_out, nand_4_out, nand_5_out, nand_6_out, nand_7_out, nand_8_out,
       nand_9_out, nand_10_out, nand_11_out, nand_12_out, nand_13_out, nand_14_out, nand_15_out, nand_16_out,
       nand_17_out, nand_18_out, nand_19_out, nand_21_out, nand_22_out, nand_23_out, nand_24_out,
       nand_25_out, nand_26_out, nand_27_out, nand_28_out, nand_29_out, nand_30_out, nand_31_out,
       nand_32_out, nand_33_out, nand_34_out, nand_35_out, nand_36_out, nand_37_out, nand_38_out,
       nand_39_out, nand_41_out, nand_43_out, nand_44_out, nand_45_out, nand_46_out, nand_47_out,
       nand_48_out, nand_49_out, nand_50_out, nand_51_out, nand_52_out, nand_53_out, nand_54_out,
       nand_56_out, nand_57_out, nand_58_out, nand_59_out, nand_60_out, nand_61_out, nand_62_out,
       nand_63_out, nand_65_out, nand_66_out, nand_67_out, nand_68_out, nand_70_out, nand_71_out,
       nand_72_out, nand_73_out, nand_74_out, nand_75_out, nand_76_out;

  nand nand_1 (nand_1_out, Q1, B_2);
  nand nand_2 (nand_2_out, Q1, nand_1_out);
  nand nand_3 (nand_3_out, nand_1_out, nand_1_out);
  nand nand_4 (nand_4_out, nand_1_out, B_2);
  nand nand_5 (nand_5_out, in_10, in_10);
  nand nand_6 (nand_6_out, CLK, CLK);
  nand nand_7 (nand_7_out, A, B);
  nand nand_8 (nand_8_out, nand_2_out, nand_4_out);
  nand nand_9 (nand_9_out, Q0_2, INC_IN);
  nand nand_10 (nand_10_out, in_11, nand_5_out);
  nand nand_11 (nand_11_out, nand_10_out, nand_5_out);
  nand nand_12 (nand_12_out, Din, nand_6_out);
  nand nand_13 (nand_13_out, nand_12_out, nand_6_out);
  nand nand_14 (nand_14_out, A, nand_7_out);
  nand nand_15 (nand_15_out, nand_7_out, nand_7_out);
  nand nand_16 (nand_16_out, nand_7_out, B);
  nand nand_17 (nand_17_out, I2, nand_8_out);
  nand nand_18 (nand_18_out, nand_3_out, I3);
  nand nand_19 (nand_19_out, Q0_2, nand_9_out);
  nand nand_20 (INC_OUT, nand_9_out, nand_9_out);
  nand nand_21 (nand_21_out, nand_9_out, INC_IN);
  nand nand_22 (nand_22_out, nand_10_out, nand_23_out);
  nand nand_23 (nand_23_out, nand_22_out, nand_11_out);
  nand nand_24 (nand_24_out, nand_12_out, nand_25_out);
  nand nand_25 (nand_25_out, nand_24_out, nand_13_out);
  nand nand_26 (nand_26_out, nand_14_out, nand_16_out);
  nand nand_27 (nand_27_out, nand_17_out, nand_18_out);
  nand nand_28 (nand_28_out, CLK_2, CLK_2);
  nand nand_29 (nand_29_out, nand_19_out, nand_21_out);
  nand nand_30 (nand_30_out, nand_22_out, in_10);
  nand nand_31 (nand_31_out, nand_30_out, in_10);
  nand nand_32 (nand_32_out, I0, nand_26_out);
  nand nand_33 (nand_33_out, nand_15_out, I1);
  nand nand_34 (nand_34_out, nand_24_out, CLK);
  nand nand_35 (nand_35_out, nand_34_out, CLK);
  nand nand_36 (nand_36_out, nand_27_out, nand_28_out);
  nand nand_37 (nand_37_out, nand_36_out, nand_28_out);
  nand nand_38 (nand_38_out, LD, nand_29_out);
  nand nand_39 (nand_39_out, INC, D0);
  nand nand_40 (out_9, nand_30_out, nand_41_out);
  nand nand_41 (nand_41_out, out_9, nand_31_out);
  nand nand_42 (Fout, nand_32_out, nand_33_out);
  nand nand_43 (nand_43_out, nand_34_out, nand_44_out);
  nand nand_44 (nand_44_out, nand_43_out, nand_35_out);
  nand nand_45 (nand_45_out, nand_36_out, nand_46_out);
  nand nand_46 (nand_46_out, nand_45_out, nand_37_out);
  nand nand_47 (nand_47_out, nand_38_out, nand_39_out);
  nand nand_48 (nand_48_out, CLK_3, CLK_3);
  nand nand_49 (nand_49_out, nand_43_out, in_12);
  nand nand_50 (nand_50_out, in_13, nand_44_out);
  nand nand_51 (nand_51_out, nand_45_out, CLK_2);
  nand nand_52 (nand_52_out, nand_51_out, CLK_2);
  nand nand_53 (nand_53_out, nand_47_out, nand_48_out);
  nand nand_54 (nand_54_out, nand_53_out, nand_48_out);
  nand nand_55 (Q0, nand_49_out, nand_50_out);
  nand nand_56 (nand_56_out, nand_51_out, nand_57_out);
  nand nand_57 (nand_57_out, nand_56_out, nand_52_out);
  nand nand_58 (nand_58_out, nand_53_out, nand_59_out);
  nand nand_59 (nand_59_out, nand_58_out, nand_54_out);
  nand nand_60 (nand_60_out, nand_56_out, in_16);
  nand nand_61 (nand_61_out, in_17, nand_57_out);
  nand nand_62 (nand_62_out, nand_58_out, CLK_3);
  nand nand_63 (nand_63_out, nand_62_out, CLK_3);
  nand nand_64 (Q1, nand_60_out, nand_61_out);
  nand nand_65 (nand_65_out, nand_62_out, nand_66_out);
  nand nand_66 (nand_66_out, nand_65_out, nand_63_out);
  nand nand_67 (nand_67_out, nand_65_out, in_33);
  nand nand_68 (nand_68_out, in_34, nand_66_out);
  nand nand_69 (Q0_2, nand_67_out, nand_68_out);
  nand nand_70 (nand_70_out, C, C);
  nand nand_71 (nand_71_out, A_2, nand_70_out);
  nand nand_72 (nand_72_out, C, B_3);
  nand nand_73 (nand_73_out, nand_71_out, nand_72_out);
  nand nand_74 (nand_74_out, nand_73_out, N);
  nand nand_75 (nand_75_out, nand_73_out, nand_74_out);
  nand nand_76 (nand_76_out, nand_74_out, N);
  nand nand_77 (out_25, nand_75_out, nand_76_out);

  // Notes on the sheet:
  //   Master-Slave D-Type Flipflop
  //   ZERO, XOR, AND, OR Network.
  //   Program Counter Slice
  //   Universal gate
endmodule
